// Logisim project 8 er.circ as structural Verilog: 2 circuits, main circuit main
module main (
  input  _8,
  input  _4,
  input  _2,
  input  _1,
  input  in_5,
  input  in_6,
  input  in_7,
  input  B2,
  input  B3,
  input  S1,
  input  A0,
  input  C0
);

  wire _2_0, _2_1, _2_2, _2_3, A0_t, A1, A2, A3, \n74573_καταχοριτες_1_p4 , \n74573_καταχοριτες_1_p6 ,
       \n74573_καταχοριτες_1_p8 , \n74573_καταχοριτες_1_p10 , \μνημη_Α0 , \μνημη_Α1 , \μνημη_Α2 , \μνημη_Α3 ,
       \νεο_τσιπ_1_out_13 ;

  // _74257 74257_1: pin names not known; wires that end beside it: 1'b1, in_6, 1'b0, \μνημη_Α2 , _2, _4, \μνημη_Α1 , A2, A1, \μνημη_Α3 , _1, _8, \μνημη_Α0 , A3, A0_t, 1'b0
  \νεο_τσιπ  \u_νεο_τσιπ_1  (
    .B3(B3), .S3(_2_3), .out_13(\νεο_τσιπ_1_out_13 ), .C0(C0), .B0(A0), .A0(A0_t), .out_14(_2_0), .in_7(A3),
    .out_16(_2_2), .in_8(A2), .in_5(B2), .in_10(1'b1), .in_11(1'b0), .S1(_2_1), .B1(S1), .in_9(A1));
  LED _16 (.in(\νεο_τσιπ_1_out_13 ));
  LED u__1 (.in(\n74573_καταχοριτες_1_p4 ));
  LED u__2 (.in(\n74573_καταχοριτες_1_p6 ));
  LED u__4 (.in(\n74573_καταχοριτες_1_p8 ));
  LED u__8 (.in(\n74573_καταχοριτες_1_p10 ));
  // _74573_καταχοριτες 74573_καταχοριτες_1: pin names not known; wires that end beside it: 1'b1, 1'b0, \μνημη_Α0 , \n74573_καταχοριτες_1_p4 , \μνημη_Α1 , \n74573_καταχοριτες_1_p6 , \μνημη_Α2 , \n74573_καταχοριτες_1_p8 , \μνημη_Α3 , \n74573_καταχοριτες_1_p10 , in_5, 1'b0
  // _74573_καταχοριτες 74573_καταχοριτες_2: pin names not known; wires that end beside it: C0, 1'b1, 1'b0, \n74573_καταχοριτες_1_p4 , _2_0, \n74573_καταχοριτες_1_p6 , _2_1, \n74573_καταχοριτες_1_p8 , _2_2, \n74573_καταχοριτες_1_p10 , _2_3, in_7, 1'b0

  // Notes on the sheet:
  //   B1
  //   S2
  //   A2
  //   A3
  //   A1
  //   S0
  //   S3
  //   B0
  //   C4
endmodule

module \νεο_τσιπ  (
  input  B3,
  input  C0,
  input  B0,
  input  A0,
  input  in_5,
  input  B1,
  input  in_7,
  input  in_8,
  input  in_9,
  input  in_10,
  input  in_11,
  output S3,
  output out_13,
  output out_14,
  output S1,
  output out_16
);

  wire and_1_out, and_2_out, and_3_out, and_4_out, and_5_out, and_6_out, and_7_out, and_8_out, and_9_out,
       and_10_out, and_11_out, and_12_out, and_13_out, and_14_out, and_15_out, controlled_buffer_3_out,
       controlled_buffer_5_out, controlled_buffer_6_out, controlled_buffer_8_out, nand_1_out, nand_2_out,
       nand_3_out, nand_4_out, nor_1_out, nor_2_out, nor_3_out, nor_4_out, nor_5_out, nor_6_out, nor_7_out,
       nor_8_out, not_1_out, not_2_out, not_3_out, not_4_out, not_5_out, not_6_out, not_7_out, xor_1_out,
       xor_2_out, xor_3_out, xor_4_out;

  not not_1 (not_1_out, C0);
  not not_2 (not_2_out, not_1_out);
  nor nor_1 (nor_1_out, A0, B0);
  xor xor_1 (xor_1_out, not_2_out, and_1_out);
  nand nand_1 (nand_1_out, A0, B0);
  not not_3 (not_3_out, nor_1_out);
  and and_1 (and_1_out, not_3_out, nand_1_out);
  assign S3 = and_11_out ? xor_4_out : 1'bz;  // Controlled_Buffer controlled_buffer_1
  and and_2 (and_2_out, not_1_out, nand_1_out);
  nor nor_2 (nor_2_out, and_2_out, controlled_buffer_3_out);
  assign out_16 = and_11_out ? xor_3_out : 1'bz;  // Controlled_Buffer controlled_buffer_2
  nor nor_3 (nor_3_out, in_9, B1);
  nand nand_2 (nand_2_out, in_9, B1);
  assign controlled_buffer_3_out = in_10 ? nor_1_out : 1'bz;  // Controlled_Buffer controlled_buffer_3
  not not_4 (not_4_out, nor_3_out);
  and and_3 (and_3_out, not_4_out, nand_2_out);
  xor xor_2 (xor_2_out, nor_2_out, and_3_out);
  assign out_13 = and_11_out ? nor_8_out : 1'bz;  // Controlled_Buffer controlled_buffer_4
  and and_4 (and_4_out, not_1_out, nand_1_out, nand_2_out);
  and and_5 (and_5_out, nand_2_out, nor_1_out);
  nor nor_4 (nor_4_out, and_4_out, and_5_out, controlled_buffer_5_out);
  nor nor_5 (nor_5_out, in_8, in_5);
  assign controlled_buffer_5_out = in_10 ? nor_3_out : 1'bz;  // Controlled_Buffer controlled_buffer_5
  not not_5 (not_5_out, nor_5_out);
  xor xor_3 (xor_3_out, nor_4_out, and_7_out);
  nand nand_3 (nand_3_out, in_8, in_5);
  and and_6 (and_6_out, not_1_out, nand_1_out, nand_2_out, nand_3_out);
  and and_7 (and_7_out, not_5_out, nand_3_out);
  and and_8 (and_8_out, nand_2_out, nand_3_out, nor_1_out);
  assign controlled_buffer_6_out = in_10 ? nor_5_out : 1'bz;  // Controlled_Buffer controlled_buffer_6
  and and_9 (and_9_out, nand_3_out, nor_3_out);
  nor nor_6 (nor_6_out, and_6_out, and_8_out, and_9_out, controlled_buffer_6_out);
  nor nor_7 (nor_7_out, in_7, B3);
  not not_6 (not_6_out, nor_7_out);
  and and_10 (and_10_out, not_6_out, nand_4_out);
  xor xor_4 (xor_4_out, nor_6_out, and_10_out);
  and and_11 (and_11_out, in_10, not_7_out);
  not not_7 (not_7_out, in_11);
  nand nand_4 (nand_4_out, in_7, B3);
  and and_12 (and_12_out, not_1_out, nand_1_out, nand_2_out, nand_3_out, nand_4_out);
  assign S1 = and_11_out ? xor_2_out : 1'bz;  // Controlled_Buffer controlled_buffer_7
  and and_13 (and_13_out, nand_2_out, nand_3_out, nand_4_out, nor_1_out);
  and and_14 (and_14_out, nand_4_out, nor_5_out);
  and and_15 (and_15_out, nand_3_out, nand_4_out, nor_3_out);
  nor nor_8 (nor_8_out, and_12_out, and_13_out, and_15_out, and_14_out, controlled_buffer_8_out);
  assign controlled_buffer_8_out = in_10 ? nor_7_out : 1'bz;  // Controlled_Buffer controlled_buffer_8
  assign out_14 = and_11_out ? xor_1_out : 1'bz;  // Controlled_Buffer controlled_buffer_9

  // Notes on the sheet:
  //   A3
  //   S2
  //   C4
  //   A2
  //   B2
  //   S0
  //   A1
endmodule
