// Logisim project a.circ as structural Verilog
module A (
  input  in_1,
  output [4:0] out_2,
  output [4:0] out_3,
  output [4:0] out_4
);

  assign out_2 = {5{in_1}} & 5'b01111;  // AND_Gate and_1, 5 bits wide
  assign out_3 = {5{in_1}} & 5'b10100;  // AND_Gate and_2, 5 bits wide
  assign out_4 = {5{in_1}} & 5'b01111;  // AND_Gate and_3, 5 bits wide
  DotMatrix #(.matrixcols(4), .matrixrows(5)) dotmatrix_1 (.col0(out_2), .col1(out_3), .col2(out_4));  // open: col3
endmodule

module B (
  input  in_1,
  output [4:0] out_2,
  output [4:0] out_3,
  output [4:0] out_4,
  output [4:0] out_5
);

  wire [4:0] register_1_q, register_2_q, register_3_q;
  wire [7:4] register_4_q;

  Register #(.width(5)) register_1 (.Q(register_1_q));  // open: D, en, clk, clr
  Register #(.width(5)) register_2 (.Q(register_2_q));  // open: D, en, clk, clr
  Register #(.width(5)) register_3 (.Q(register_3_q));  // open: D, en, clk, clr
  assign out_2 = {5{in_1}} & register_1_q;  // AND_Gate and_1, 5 bits wide
  assign out_3 = {5{in_1}} & register_2_q;  // AND_Gate and_2, 5 bits wide
  assign out_5 = {5{in_1}} & register_3_q;  // AND_Gate and_3, 5 bits wide
  DotMatrix #(.matrixcols(4), .matrixrows(5)) dotmatrix_1 (.col0(out_2), .col1(out_3), .col2(out_3), .col3(out_5));
  Register register_4 (.Q({{3{register_4_q[7]}}, register_4_q[4], register_4_q[7], register_4_q[4], {2{register_4_q[7]}}}));  // open: D, en, clk, clr

  assign out_4 = out_3;
  // also tied to GND on the sheet: register_4_q[7]
  // also tied to VCC on the sheet: register_4_q[4]
endmodule

module D (
  input  in_1,
  input  in_2,
  input  in_3,
  input  in_4,
  output [4:0] out_5,
  output [4:0] out_6,
  output [4:0] out_7,
  output [4:0] out_8
);

  wire [4:0] register_1_q, register_2_q, register_3_q, register_4_q, register_5_q, register_6_q,
       register_7_q, register_8_q, register_9_q, register_10_q, register_11_q, register_12_q, register_13_q,
       register_14_q, register_15_q, register_16_q, register_17_q, register_18_q, register_19_q,
       register_20_q, register_21_q, register_22_q, register_23_q, register_24_q, register_25_q,
       register_26_q, register_27_q, register_28_q, register_29_q, register_30_q, register_31_q,
       register_32_q, register_33_q, register_34_q, register_35_q, undriven;

  Register #(.width(5)) register_1 (.Q(register_1_q));  // open: D, en, clk, clr
  Register #(.width(5)) register_2 (.Q(register_2_q));  // open: D, en, clk, clr
  Register #(.width(5)) register_3 (.Q(register_3_q));  // open: D, en, clk, clr
  Register #(.width(5)) register_4 (.Q(register_4_q));  // open: D, en, clk, clr
  assign out_5 = {5{in_1}} & register_1_q;  // AND_Gate and_1, 5 bits wide
  assign out_6 = {5{in_1}} & register_2_q;  // AND_Gate and_2, 5 bits wide
  assign out_7 = {5{in_1}} & register_3_q;  // AND_Gate and_3, 5 bits wide
  assign out_8 = {5{in_1}} & register_4_q;  // AND_Gate and_4, 5 bits wide
  DotMatrix #(.matrixcols(4), .matrixrows(5)) dotmatrix_1 (.col0(out_5), .col1(out_6), .col2(out_7), .col3(out_8));
  DotMatrix #(.matrixcols(32), .matrixrows(5)) dotmatrix_2 (
    .col0(register_5_q), .col1(undriven), .col2(register_6_q), .col3(undriven), .col4(register_7_q),
    .col5(undriven), .col6(register_8_q), .col7(undriven), .col8(register_9_q), .col9(undriven),
    .col10(register_10_q), .col11(undriven), .col12(register_11_q), .col13(undriven), .col14(register_12_q),
    .col15(undriven), .col16(register_13_q), .col17(undriven), .col18(register_14_q), .col19(undriven),
    .col20(register_15_q), .col21(undriven), .col22(register_16_q), .col23(undriven), .col24(register_17_q),
    .col25(undriven), .col26(register_18_q), .col27(undriven), .col28(register_19_q), .col29(undriven),
    .col30(register_20_q), .col31(undriven));
  Register #(.width(5)) register_5 (.D({{2{in_4}}, in_3, {2{in_4}}}), .Q(register_5_q), .clk(in_2));  // open: en, clr
  Register #(.width(5)) register_6 (.Q(register_6_q));  // open: D, en, clk, clr
  Register #(.width(5)) register_7 (.Q(register_7_q));  // open: D, en, clk, clr
  Register #(.width(5)) register_8 (.Q(register_8_q));  // open: D, en, clk, clr
  Register #(.width(5)) register_9 (.Q(register_9_q));  // open: D, en, clk, clr
  Register #(.width(5)) register_10 (.Q(register_10_q));  // open: D, en, clk, clr
  Register #(.width(5)) register_11 (.Q(register_11_q));  // open: D, en, clk, clr
  Register #(.width(5)) register_12 (.Q(register_12_q));  // open: D, en, clk, clr
  Register #(.width(5)) register_13 (.Q(register_13_q));  // open: D, en, clk, clr
  Register #(.width(5)) register_14 (.Q(register_14_q));  // open: D, en, clk, clr
  Register #(.width(5)) register_15 (.Q(register_15_q));  // open: D, en, clk, clr
  Register #(.width(5)) register_16 (.Q(register_16_q));  // open: D, en, clk, clr
  Register #(.width(5)) register_17 (.Q(register_17_q));  // open: D, en, clk, clr
  Register #(.width(5)) register_18 (.Q(register_18_q));  // open: D, en, clk, clr
  Register #(.width(5)) register_19 (.Q(register_19_q));  // open: D, en, clk, clr
  Register #(.width(5)) register_20 (.Q(register_20_q));  // open: D, en, clk, clr
  Register #(.width(5)) register_21 (.Q(register_21_q));  // open: D, en, clk, clr
  Register #(.width(5)) register_22 (.Q(register_22_q));  // open: D, en, clk, clr
  Register #(.width(5)) register_23 (.Q(register_23_q));  // open: D, en, clk, clr
  Register #(.width(5)) register_24 (.Q(register_24_q));  // open: D, en, clk, clr
  Register #(.width(5)) register_25 (.Q(register_25_q));  // open: D, en, clk, clr
  Register #(.width(5)) register_26 (.Q(register_26_q));  // open: D, en, clk, clr
  Register #(.width(5)) register_27 (.Q(register_27_q));  // open: D, en, clk, clr
  Register #(.width(5)) register_28 (.Q(register_28_q));  // open: D, en, clk, clr
  Register #(.width(5)) register_29 (.Q(register_29_q));  // open: D, en, clk, clr
  Register #(.width(5)) register_30 (.Q(register_30_q));  // open: D, en, clk, clr
  Register #(.width(5)) register_31 (.Q(register_31_q));  // open: D, en, clk, clr
  Register #(.width(5)) register_32 (.Q(register_32_q));  // open: D, en, clk, clr
  Register #(.width(5)) register_33 (.Q(register_33_q));  // open: D, en, clk, clr
  Register #(.width(5)) register_34 (.Q(register_34_q));  // open: D, en, clk, clr
  Register #(.width(5)) register_35 (.Q(register_35_q));  // open: D, en, clk, clr
  DotMatrix #(.matrixcols(32), .matrixrows(5)) dotmatrix_3 (
    .col0(register_21_q), .col1(undriven), .col2(register_22_q), .col3(undriven), .col4(register_23_q),
    .col5(undriven), .col6(register_24_q), .col7(undriven), .col8(register_25_q), .col9(undriven),
    .col10(register_26_q), .col11(undriven), .col12(register_27_q), .col13(undriven), .col14(register_28_q),
    .col15(undriven), .col16(register_29_q), .col17(undriven), .col18(register_30_q), .col19(undriven),
    .col20(register_31_q), .col21(undriven), .col22(register_32_q), .col23(undriven), .col24(register_33_q),
    .col25(undriven), .col26(register_34_q), .col27(undriven), .col28(register_35_q), .col29(undriven),
    .col30(undriven), .col31(undriven));
endmodule

module C (
  input  in_1,
  output [4:0] out_2,
  output [4:0] out_3,
  output [4:0] out_4,
  output [4:0] out_5
);

  wire [4:0] register_1_q, register_2_q, register_3_q, register_4_q;

  Register #(.width(5)) register_1 (.Q(register_1_q));  // open: D, en, clk, clr
  Register #(.width(5)) register_2 (.Q(register_2_q));  // open: D, en, clk, clr
  Register #(.width(5)) register_3 (.Q(register_3_q));  // open: D, en, clk, clr
  Register #(.width(5)) register_4 (.Q(register_4_q));  // open: D, en, clk, clr
  assign out_2 = {5{in_1}} & register_1_q;  // AND_Gate and_1, 5 bits wide
  assign out_3 = {5{in_1}} & register_2_q;  // AND_Gate and_2, 5 bits wide
  assign out_4 = {5{in_1}} & register_3_q;  // AND_Gate and_3, 5 bits wide
  assign out_5 = {5{in_1}} & register_4_q;  // AND_Gate and_4, 5 bits wide
  DotMatrix #(.matrixcols(4), .matrixrows(5)) dotmatrix_1 (.col0(out_2), .col1(out_3), .col2(out_4), .col3(out_5));
endmodule

module E (
  input  in_1,
  output [4:0] out_2,
  output [4:0] out_3,
  output [4:0] out_4
);

  wire [4:0] register_1_q, register_2_q, register_3_q;

  Register #(.width(5)) register_1 (.Q(register_1_q));  // open: D, en, clk, clr
  Register #(.width(5)) register_2 (.Q(register_2_q));  // open: D, en, clk, clr
  Register #(.width(5)) register_3 (.Q(register_3_q));  // open: D, en, clk, clr
  assign out_2 = {5{in_1}} & register_1_q;  // AND_Gate and_1, 5 bits wide
  assign out_3 = {5{in_1}} & register_2_q;  // AND_Gate and_2, 5 bits wide
  assign out_4 = {5{in_1}} & register_3_q;  // AND_Gate and_3, 5 bits wide
  DotMatrix #(.matrixcols(4), .matrixrows(5)) dotmatrix_1 (.col0(out_2), .col1(out_3), .col2(out_4));  // open: col3
endmodule

module F (
  input  in_1,
  output [4:0] out_2,
  output [4:0] out_3,
  output [4:0] out_4
);

  wire [4:0] register_1_q, register_2_q, register_3_q;

  Register #(.width(5)) register_1 (.Q(register_1_q));  // open: D, en, clk, clr
  Register #(.width(5)) register_2 (.Q(register_2_q));  // open: D, en, clk, clr
  Register #(.width(5)) register_3 (.Q(register_3_q));  // open: D, en, clk, clr
  assign out_2 = {5{in_1}} & register_1_q;  // AND_Gate and_1, 5 bits wide
  assign out_3 = {5{in_1}} & register_2_q;  // AND_Gate and_2, 5 bits wide
  assign out_4 = {5{in_1}} & register_3_q;  // AND_Gate and_3, 5 bits wide
  DotMatrix #(.matrixcols(4), .matrixrows(5)) dotmatrix_1 (.col0(out_2), .col1(out_3), .col2(out_4));  // open: col3
endmodule

module shn (
  input  in_1,
  input  in_2,
  input  in_3,
  input  in_4,
  input  in_5,
  input  in_6,
  output [4:0] out_7,
  output [4:0] out_8,
  output [4:0] out_9,
  output [4:0] out_10
);

  wire [4:0] a_1_out_2, a_1_out_3, a_1_out_4, b_1_out_2, b_1_out_3, b_1_out_4, b_1_out_5, c_1_out_2,
       c_1_out_3, c_1_out_4, c_1_out_5, d_1_out_5, d_1_out_6, d_1_out_7, d_1_out_8, e_1_out_2, e_1_out_3,
       e_1_out_4, f_1_out_2, f_1_out_3, f_1_out_4;

  A a_1 (.in_1(in_1), .out_2(a_1_out_2), .out_3(a_1_out_3), .out_4(a_1_out_4));
  E e_1 (.in_1(in_2), .out_2(e_1_out_2), .out_3(e_1_out_3), .out_4(e_1_out_4));
  F f_1 (.in_1(in_3), .out_2(f_1_out_2), .out_3(f_1_out_3), .out_4(f_1_out_4));
  C c_1 (.in_1(in_4), .out_2(c_1_out_2), .out_3(c_1_out_3), .out_4(c_1_out_4), .out_5(c_1_out_5));
  B b_1 (.in_1(in_5), .out_3(b_1_out_3), .out_2(b_1_out_2), .out_5(b_1_out_5), .out_4(b_1_out_4));
  D d_1 (
    .in_1(in_6), .out_5(d_1_out_5), .out_6(d_1_out_6), .out_7(d_1_out_7), .out_8(d_1_out_8));  // open: in_2, in_4, in_3
  assign out_7 = a_1_out_2 | e_1_out_2 | f_1_out_2 | c_1_out_2 | b_1_out_3 | d_1_out_5;  // OR_Gate or_1, 5 bits wide
  assign out_8 = a_1_out_3 | e_1_out_3 | f_1_out_3 | c_1_out_3 | b_1_out_2 | d_1_out_6;  // OR_Gate or_2, 5 bits wide
  assign out_9 = e_1_out_4 | a_1_out_4 | f_1_out_4 | c_1_out_4 | b_1_out_5 | d_1_out_7;  // OR_Gate or_3, 5 bits wide
  assign out_10 = c_1_out_5 | b_1_out_4;  // OR_Gate or_4, 5 bits wide
endmodule
