// Logisim project neo.circ as structural Verilog: 33 circuits, main circuit main
module main (
  input  in_1,
  input  in_2
);

  wire _1, _2, _3, _4, button_1_out, button_2_out, button_3_out, button_4_out, clock_2_out, keyboard_1_p1,
       keyboard_2_avail, klok, or_3_out, or_4_out, plus_or_minus, s1, s2, s3, s4;
  wire [1:0] joystick_1_x, joystick_1_y;
  wire [2:0] n2_1_out_4, n2_1_out_5, n2_2_out_4, n2_2_out_5;
  wire [3:0] ss_1_out_3;
  wire [6:0] keyboard_2_data;
  wire [7:0] _11, _12, _13, _14, _15, _21, _22, _23, _24, _25, _31, _32, _33, _34, _35, ss_1_out_4,
       ss_1_out_5, ss_1_out_6, ss_1_out_7, ss_1_out_8, ss_1_out_9, ss_1_out_10, ss_1_out_11, ss_1_out_12,
       ss_1_out_13, ss_1_out_14, ss_1_out_15, ss_1_out_16, ss_1_out_17, ss_1_out_18, ss_1_out_19,
       ss_1_out_20, ss_1_out_21, ss_1_out_22, ss_1_out_23, ss_1_out_24, ss_1_out_25, ss_1_out_26,
       ss_1_out_27, ss_1_out_28, ss_1_out_29, ss_1_out_30, ss_1_out_31, ss_1_out_32, ss_1_out_33,
       ss_1_out_34, ss_1_out_35, x, x11, x12, x13, x14, x15, x21, x22, x23, x24, x25, x31, x32, x33, x34, x35;

  or or_1 (plus_or_minus, s4, _3);
  or or_2 (klok, s3, _4);
  // Keyboard keyboard_1: pin names not known; wires that end beside it: keyboard_1_p1, _2, _1
  Clock clock_1 (.out(keyboard_1_p1));
  or or_3 (or_3_out, _2, s2);
  or or_4 (or_4_out, s1, _1);
  Joystick #(.bits(2)) joystick_1 (.x(joystick_1_x), .y(joystick_1_y));
  Clock clock_2 (.out(clock_2_out));
  Keyboard keyboard_2 (.clk(clock_2_out), .avail(keyboard_2_avail), .data(keyboard_2_data));  // open: re, clr
  DotMatrix #(.matrixcols(7), .matrixrows(8)) dotmatrix_1 (
    .col0(x), .col1(_11), .col2(_12), .col3(_13), .col4(_14), .col5(_15), .col6(x));
  DotMatrix #(.matrixcols(7), .matrixrows(8)) dotmatrix_2 (
    .col0(x), .col1(_21), .col2(_22), .col3(_23), .col4(_24), .col5(_25), .col6(x));
  Hex_Digit_Display hex_digit_display_1 (.value(ss_1_out_3));  // open: dp
  DotMatrix #(.matrixcols(32), .matrixrows(8)) dotmatrix_3 (
    .col0(ss_1_out_4), .col1(ss_1_out_5), .col2(ss_1_out_6), .col3(ss_1_out_7), .col4(ss_1_out_8),
    .col5(ss_1_out_9), .col6(ss_1_out_10), .col7(ss_1_out_11), .col8(ss_1_out_12), .col9(ss_1_out_13),
    .col10(ss_1_out_14), .col11(ss_1_out_15), .col12(ss_1_out_16), .col13(ss_1_out_17), .col14(ss_1_out_18),
    .col15(ss_1_out_19), .col16(ss_1_out_20), .col17(ss_1_out_21), .col18(ss_1_out_22), .col19(ss_1_out_23),
    .col20(ss_1_out_24), .col21(ss_1_out_25), .col22(ss_1_out_26), .col23(ss_1_out_27), .col24(ss_1_out_28),
    .col25(ss_1_out_29), .col26(ss_1_out_30), .col27(ss_1_out_31), .col28(ss_1_out_32), .col29(ss_1_out_33),
    .col30(ss_1_out_34), .col31(ss_1_out_35));
  ss ss_1 (
    .out_5(ss_1_out_5), .out_6(ss_1_out_6), .out_7(ss_1_out_7), .out_8(ss_1_out_8), .out_9(ss_1_out_9),
    .out_10(ss_1_out_10), .out_11(ss_1_out_11), .out_12(ss_1_out_12), .out_13(ss_1_out_13),
    .out_14(ss_1_out_14), .out_15(ss_1_out_15), .out_16(ss_1_out_16), .out_17(ss_1_out_17),
    .out_18(ss_1_out_18), .out_19(ss_1_out_19), .out_20(ss_1_out_20), .out_21(ss_1_out_21),
    .out_22(ss_1_out_22), .out_23(ss_1_out_23), .out_24(ss_1_out_24), .out_25(ss_1_out_25),
    .out_26(ss_1_out_26), .out_27(ss_1_out_27), .out_28(ss_1_out_28), .out_29(ss_1_out_29),
    .out_30(ss_1_out_30), .out_31(ss_1_out_31), .out_32(ss_1_out_32), .out_33(ss_1_out_33),
    .out_34(ss_1_out_34), .out_35(ss_1_out_35), .in_2(keyboard_2_avail), .in_1(keyboard_2_data),
    .out_3(ss_1_out_3), .out_4(ss_1_out_4));
  DotMatrix #(.matrixcols(7), .matrixrows(8)) dotmatrix_4 (
    .col0(x), .col1(_31), .col2(_32), .col3(_33), .col4(_34), .col5(_35), .col6(x));
  Button button_1 (.out(button_1_out));
  Button button_2 (.out(button_2_out));
  b b_1 (
    .in_1(n2_1_out_4), .in_2(n2_1_out_5), .out_4({x, _11, _12, _13}), .out_5({_14, _15, _21, _22}),
    .out_6({_23, _24, _25, _31}), .out_7({_32, _33, _34, _35}), .in_3(in_2));
  _2 u_2_1 (
    .out_4(n2_1_out_4), .out_5(n2_1_out_5), .in_1(button_1_out), .in_2(button_2_out), .in_3(in_2));  // open: out_6
  Button button_3 (.out(button_3_out));
  Button button_4 (.out(button_4_out));
  b b_2 (
    .in_1(n2_2_out_4), .in_2(n2_2_out_5), .out_4({x, x11, x12, x13}), .out_5({x14, x15, x21, x22}),
    .out_6({x23, x24, x25, x31}), .out_7({x32, x33, x34, x35}), .in_3(in_2));
  _2 u_2_2 (
    .out_4(n2_2_out_4), .out_5(n2_2_out_5), .in_1(button_3_out), .in_2(button_4_out), .in_3(in_2));  // open: out_6

  // Other names for the same wires on the sheet: res = in_1; reset = in_2
endmodule

module zoes (
  input  in_1,
  input  in_2,
  input  in_3,
  output [7:0] out_4,
  output [7:0] out_5,
  output [7:0] out_6,
  output [7:0] out_7,
  output [7:0] out_8,
  output [7:0] out_9,
  output [7:0] out_10
);

  wire clock_1_out, not_1_out, not_2_out, not_3_out, not_4_out, not_5_out, or_1_out, or_2_out, or_3_out,
       or_4_out, or_5_out, register_1_q, register_2_q, register_3_q, register_4_q, register_5_q,
       register_6_q, register_7_q, register_8_q, register_9_q, register_10_q;

  Register #(.width(1)) register_1 (.D(in_1), .Q(register_1_q), .clk(in_1), .clr(or_1_out));  // open: en
  or or_1 (or_1_out, register_2_q, in_2);
  Register #(.width(1)) register_2 (.D(1'b1), .Q(register_2_q), .clk(in_3), .clr(clock_1_out));  // open: en
  Register #(.width(1)) register_3 (.D(register_1_q), .Q(register_3_q), .clk(in_1), .clr(or_2_out));  // open: en
  or or_2 (or_2_out, register_4_q, in_2);
  Register #(.width(1)) register_4 (.D(register_1_q), .Q(register_4_q), .clk(in_3), .clr(clock_1_out));  // open: en
  Register #(.width(1)) register_5 (.D(register_3_q), .Q(register_5_q), .clk(in_3), .clr(clock_1_out));  // open: en
  Clock #(.lowDuration(10)) clock_1 (.out(clock_1_out));
  Register #(.width(1)) register_6 (.D(register_3_q), .Q(register_6_q), .clk(in_1), .clr(or_3_out));  // open: en
  or or_3 (or_3_out, register_5_q, in_2);
  Register #(.width(1)) register_7 (.D(register_6_q), .Q(register_7_q), .clk(in_3), .clr(clock_1_out));  // open: en
  Register #(.width(1)) register_8 (.D(register_6_q), .Q(register_8_q), .clk(in_1), .clr(or_4_out));  // open: en
  or or_4 (or_4_out, register_7_q, in_2);
  not not_1 (not_1_out, register_1_q);
  not not_2 (not_2_out, register_3_q);
  not not_3 (not_3_out, register_6_q);
  not not_4 (not_4_out, register_8_q);
  not not_5 (not_5_out, register_9_q);
  Register #(.width(1)) register_9 (.D(register_8_q), .Q(register_9_q), .clk(in_1), .clr(or_5_out));  // open: en
  or or_5 (or_5_out, in_2, register_10_q);
  Register #(.width(1)) register_10 (.D(register_8_q), .Q(register_10_q), .clk(in_3), .clr(clock_1_out));  // open: en
  assign out_5 = not_1_out ? 8'hfc : 8'bz;  // Controlled_Buffer controlled_buffer_1
  assign out_6 = not_2_out ? 8'hfe : 8'bz;  // Controlled_Buffer controlled_buffer_2
  assign out_7 = not_3_out ? 8'h7f : 8'bz;  // Controlled_Buffer controlled_buffer_3
  assign out_8 = not_4_out ? 8'hfe : 8'bz;  // Controlled_Buffer controlled_buffer_4
  assign out_9 = not_5_out ? 8'hfc : 8'bz;  // Controlled_Buffer controlled_buffer_5
  DotMatrix #(.matrixcols(7), .matrixrows(8)) dotmatrix_1 (
    .col0(8'h70), .col1(out_5), .col2(out_6), .col3(out_7), .col4(out_8), .col5(out_9), .col6(8'h70));

  assign out_4 = 8'h70;
  assign out_10 = 8'h70;
  // also tied to GND on the sheet: {out_5[0], out_5[1], out_5[4], out_5[5], out_5[6], out_6[0], out_6[2], out_6[3], out_6[4], out_6[5], out_6[6], out_7[1], out_7[2], out_7[3], out_7[4], out_7[5], out_7[7], out_8[0], out_8[2], out_8[3], out_8[4], out_8[5], out_8[6], out_9[0], out_9[1], out_9[4], out_9[5], out_9[6]}
  // also tied to VCC on the sheet: {out_5[2], out_5[3], out_5[7], out_6[1], out_6[7], out_7[0], out_7[6], out_8[1], out_8[7], out_9[2], out_9[3], out_9[7]}
endmodule

module _2 (
  input  in_1,
  input  in_2,
  input  in_3,
  output [2:0] out_4,
  output [2:0] out_5,
  output out_6
);

  wire and_1_out, and_9_out, and_10_out, comparator_1_eq, comparator_2_eq, comparator_2_gt, comparator_2_lt,
       comparator_3_eq, comparator_3_gt, comparator_3_lt, comparator_4_gt, comparator_5_eq, comparator_5_gt,
       comparator_5_lt, comparator_6_eq, comparator_6_gt, comparator_6_lt, comparator_7_gt, not_1_out,
       or_1_out, or_2_out, or_3_out, or_4_out, or_5_out, xor_1_out;
  wire [0:0] and_2_out;
  wire [1:1] and_3_out, and_5_out;
  wire [2:0] and_11_out, and_12_out;
  wire [2:2] and_6_out, and_7_out;
  wire [7:0] adder_1_out, controlled_buffer_1_out, multiplexer_1_out, s;

  ExactlyOne xor_1 (.out(xor_1_out), .in0(1'b1), .in1(out_4[1]), .in2(out_4[2]));
  assign controlled_buffer_1_out = xor_1_out ? {8{1'b0}} : 8'bz;  // Controlled_Buffer controlled_buffer_1
  assign controlled_buffer_1_out = out_4[1] ? 8'h5 : 8'bz;  // Controlled_Buffer controlled_buffer_2
  assign controlled_buffer_1_out = out_4[2] ? 8'ha : 8'bz;  // Controlled_Buffer controlled_buffer_3
  Adder adder_1 (.a(s), .b({8{1'b0}}), .out(adder_1_out), .cin(1'b1));  // open: cout
  not not_1 (not_1_out, comparator_1_eq);
  Comparator comparator_1 (.a(8'hf), .b(s), .eq(comparator_1_eq));  // open: gt, lt
  Register #(.trigger("falling")) register_1 (.D(multiplexer_1_out), .Q(s), .clk(and_1_out), .clr(in_3));  // open: en
  Multiplexer #(.width(8), .enable("false")) multiplexer_1 (
    .in0(adder_1_out), .in1(controlled_buffer_1_out), .out(multiplexer_1_out), .sel(in_1));
  and and_1 (and_1_out, not_1_out, or_1_out);
  or or_1 (or_1_out, in_1, in_2);
  and and_2 (and_2_out[0], comparator_2_gt, in_2);
  Comparator comparator_2 (.a(8'h5), .b(s), .gt(comparator_2_gt), .eq(comparator_2_eq), .lt(comparator_2_lt));
  Comparator comparator_3 (.a(8'ha), .b(s), .gt(comparator_3_gt), .eq(comparator_3_eq), .lt(comparator_3_lt));
  and and_3 (and_3_out[1], comparator_3_gt, in_2);
  Comparator comparator_4 (.a(8'hf), .b(s), .gt(comparator_4_gt), .eq(out_6));  // open: lt
  and and_4 (out_4[0], comparator_5_gt, in_1);
  Comparator comparator_5 (.a(8'h6), .b(s), .gt(comparator_5_gt), .eq(comparator_5_eq), .lt(comparator_5_lt));
  or or_2 (or_2_out, comparator_5_eq, comparator_5_lt);
  Comparator comparator_6 (.a(8'hb), .b(s), .gt(comparator_6_gt), .eq(comparator_6_eq), .lt(comparator_6_lt));
  or or_3 (or_3_out, comparator_6_eq, comparator_6_lt);
  Comparator comparator_7 (.a(8'h10), .b(s), .gt(comparator_7_gt));  // open: eq, lt
  or or_4 (or_4_out, comparator_2_eq, comparator_2_lt);
  and and_5 (and_5_out[1], or_4_out, and_3_out[1]);
  or or_5 (or_5_out, comparator_3_eq, comparator_3_lt);
  and and_6 (and_6_out[2], or_5_out, and_7_out[2]);
  and and_7 (and_7_out[2], comparator_4_gt, in_2);
  and and_8 (out_4[1], and_9_out, in_1);
  and and_9 (and_9_out, or_2_out, comparator_6_gt);
  and and_10 (and_10_out, or_3_out, comparator_7_gt);
  assign and_11_out = {1'b0, and_5_out[1], 1'b0} & {1'b0, and_3_out[1], 1'b0};  // AND_Gate and_11, 3 bits wide
  assign and_12_out = {and_6_out[2], 2'b00} & {and_7_out[2], 2'b00};  // AND_Gate and_12, 3 bits wide
  and and_13 (out_4[2], and_10_out, in_1);
  assign out_5 = {2'b00, and_2_out[0]} | and_11_out | and_12_out;  // OR_Gate or_6, 3 bits wide

  // Other names for the same wires on the sheet: _1 = out_4[0]; _2 = out_4[1]; _3 = out_4[2]; r = in_3; s1[7:0] = s;
  //   tunnel = in_1; tunnel_t = in_2
endmodule

module b (
  input  [2:0] in_1,
  input  [2:0] in_2,
  input  in_3,
  output [31:0] out_4,
  output [31:0] out_5,
  output [31:0] out_6,
  output [31:0] out_7
);

  zoes zoes_1 (
    .in_2(in_3), .in_3(in_1[0]), .out_4(out_4[31:24]), .out_5(out_4[23:16]), .out_6(out_4[15:8]),
    .out_7(out_4[7:0]), .out_8(out_5[31:24]), .out_9(out_5[23:16]), .in_1(in_2[0]));  // open: out_10
  zoes zoes_2 (
    .in_2(in_3), .in_3(in_1[1]), .out_5(out_5[15:8]), .out_6(out_5[7:0]), .out_7(out_6[31:24]),
    .out_8(out_6[23:16]), .out_9(out_6[15:8]), .in_1(in_2[1]));  // open: out_4, out_10
  zoes zoes_3 (
    .in_2(in_3), .in_3(in_1[2]), .out_5(out_6[7:0]), .out_6(out_7[31:24]), .out_7(out_7[23:16]),
    .out_8(out_7[15:8]), .out_9(out_7[7:0]), .in_1(in_2[2]));  // open: out_4, out_10
endmodule

module ss (
  input  [6:0] in_1,
  input  in_2,
  output [3:0] out_3,
  output [7:0] out_4,
  output [7:0] out_5,
  output [7:0] out_6,
  output [7:0] out_7,
  output [7:0] out_8,
  output [7:0] out_9,
  output [7:0] out_10,
  output [7:0] out_11,
  output [7:0] out_12,
  output [7:0] out_13,
  output [7:0] out_14,
  output [7:0] out_15,
  output [7:0] out_16,
  output [7:0] out_17,
  output [7:0] out_18,
  output [7:0] out_19,
  output [7:0] out_20,
  output [7:0] out_21,
  output [7:0] out_22,
  output [7:0] out_23,
  output [7:0] out_24,
  output [7:0] out_25,
  output [7:0] out_26,
  output [7:0] out_27,
  output [7:0] out_28,
  output [7:0] out_29,
  output [7:0] out_30,
  output [7:0] out_31,
  output [7:0] out_32,
  output [7:0] out_33,
  output [7:0] out_34,
  output [7:0] out_35
);

  wire and_1_out, and_2_out, and_3_out, and_4_out, comparator_1_eq, comparator_1_gt, comparator_2_lt,
       demultiplexer_1_out0, demultiplexer_1_out1, demultiplexer_1_out2, demultiplexer_1_out3,
       demultiplexer_1_out4, not_1_out, not_2_out, not_3_out, not_5_out, or_1_out, or_2_out, or_3_out, sos;
  wire [2:0] niiio101;
  wire [6:0] demultiplexer_2_out0, demultiplexer_2_out1, demultiplexer_2_out2, demultiplexer_2_out3,
       demultiplexer_2_out4;

  and and_1 (and_1_out, not_1_out, in_1[1], in_1[2], in_1[3], in_1[4], in_1[5], not_2_out);
  and and_2 (and_2_out, not_3_out, sos, in_1[2], in_1[3], in_1[4], in_1[5], not_5_out);
  not not_1 (not_1_out, in_1[0]);
  not not_2 (not_2_out, in_1[6]);
  not not_3 (not_3_out, in_1[0]);
  not not_4 (sos, in_1[1]);
  not not_5 (not_5_out, in_1[6]);
  and and_3 (and_3_out, or_3_out, and_2_out);
  Counter #(.width(4), .max('hf)) counter_1 (
    .load(and_3_out), .D(4'b0001), .count(1'b1), .Q(out_3), .clk(and_4_out));  // open: carry, clr
  and and_4 (and_4_out, or_1_out, or_2_out);
  or or_1 (or_1_out, and_1_out, and_2_out);
  or or_2 (or_2_out, comparator_2_lt, sos);
  Comparator #(.width(4)) comparator_1 (
    .a(out_3), .b(4'b0001), .gt(comparator_1_gt), .eq(comparator_1_eq));  // open: lt
  Bit_Extender #(.in_width(4), .out_width(3)) bit_extender_1 (.in(out_3), .out(niiio101));
  Comparator #(.width(4)) comparator_2 (.a(out_3), .b(4'b0101), .lt(comparator_2_lt));  // open: gt, eq
  or or_3 (or_3_out, comparator_1_gt, comparator_1_eq);
  ola ola_1 (
    .out_3(out_10), .out_4(out_6), .out_5(out_7), .out_6(out_8), .out_7(out_9), .in_2(demultiplexer_1_out0),
    .in_1(demultiplexer_2_out0));
  ola ola_2 (
    .out_3(out_22), .out_4(out_18), .out_5(out_19), .out_6(out_20), .out_7(out_21),
    .in_2(demultiplexer_1_out2), .in_1(demultiplexer_2_out2));
  ola ola_3 (
    .out_3(out_16), .out_4(out_12), .out_5(out_13), .out_6(out_14), .out_7(out_15),
    .in_2(demultiplexer_1_out1), .in_1(demultiplexer_2_out1));
  Demultiplexer #(.select(3), .enable("false")) demultiplexer_1 (
    .out0(demultiplexer_1_out0), .out1(demultiplexer_1_out1), .out2(demultiplexer_1_out2),
    .out3(demultiplexer_1_out3), .out4(demultiplexer_1_out4), .in(in_2), .sel(niiio101));  // open: out5, out6, out7
  ola ola_4 (
    .out_3(out_28), .out_4(out_24), .out_5(out_25), .out_6(out_26), .out_7(out_27),
    .in_2(demultiplexer_1_out3), .in_1(demultiplexer_2_out3));
  ola ola_5 (
    .out_3(out_34), .out_4(out_30), .out_5(out_31), .out_6(out_32), .out_7(out_33),
    .in_2(demultiplexer_1_out4), .in_1(demultiplexer_2_out4));
  Demultiplexer #(.select(3), .width(7), .enable("false")) demultiplexer_2 (
    .out0(demultiplexer_2_out0), .out1(demultiplexer_2_out1), .out2(demultiplexer_2_out2),
    .out3(demultiplexer_2_out3), .out4(demultiplexer_2_out4), .in(in_1), .sel(niiio101));  // open: out5, out6, out7

  assign out_4 = {8{1'b0}};
  assign out_5 = {8{1'b0}};
  assign out_11 = {8{1'b0}};
  assign out_17 = {8{1'b0}};
  assign out_23 = {8{1'b0}};
  assign out_29 = {8{1'b0}};
  assign out_35 = {8{1'b0}};

  // Other names for the same wires on the sheet: niiio[6:0] = in_1
endmodule

module ola (
  input  [6:0] in_1,
  input  in_2,
  output [7:0] out_3,
  output [7:0] out_4,
  output [7:0] out_5,
  output [7:0] out_6,
  output [7:0] out_7
);

  wire and_1_out, and_2_out, clock_1_out, clock_2_out, decoder_1_out1, decoder_1_out2, decoder_1_out3,
       decoder_1_out4, decoder_1_out5, decoder_1_out6, decoder_1_out7, decoder_1_out8, decoder_1_out9,
       decoder_1_out10, decoder_1_out11, decoder_1_out12, decoder_1_out13, decoder_1_out14, decoder_1_out15,
       decoder_1_out16, decoder_1_out17, decoder_1_out18, decoder_1_out19, decoder_1_out20, decoder_1_out21,
       decoder_1_out22, decoder_1_out23, decoder_1_out24, decoder_1_out25, decoder_1_out26, neo_ko_1_out_5,
       not_1_out, not_2_out, not_3_out, not_4_out, not_5_out, not_6_out, not_7_out, not_8_out, not_9_out,
       not_10_out, not_11_out, not_12_out, not_13_out, not_14_out, not_15_out, not_16_out, not_17_out,
       not_18_out, not_19_out, not_20_out, not_21_out, not_22_out, not_23_out, not_24_out, not_25_out,
       not_26_out, not_27_out, not_28_out, not_29_out, not_30_out, not_31_out, not_32_out, not_33_out,
       or_5_out, r, r1, undriven;
  wire [4:0] bit_extender_2_out;
  wire [5:0] bit_extender_1_out;
  wire [7:0] a_1_out_2, a_1_out_3, a_1_out_4, a_1_out_5, a_1_out_6, adder_1_out, adder_2_out, adder_3_out,
       adder_4_out, adder_5_out, b_1_out_2, b_1_out_3, b_1_out_4, b_1_out_5, b_1_out_6, c_1_out_2, c_1_out_3,
       c_1_out_4, c_1_out_5, c_1_out_6, d_1_out_2, d_1_out_3, d_1_out_4, d_1_out_5, d_1_out_6, e, e_1_out_2,
       e_1_out_3, e_1_out_4, e_1_out_5, e_1_out_6, f_1_out_2, f_1_out_3, f_1_out_4, f_1_out_5, f_1_out_6,
       g_1_out_2, g_1_out_3, g_1_out_4, g_1_out_5, g_1_out_6, h_1_out_2, h_1_out_3, h_1_out_4, h_1_out_5,
       h_1_out_6, i_1_out_2, i_1_out_3, i_1_out_4, i_1_out_5, i_1_out_6, j_1_out_2, j_1_out_3, j_1_out_4,
       j_1_out_5, j_1_out_6, k_1_out_2, k_1_out_3, k_1_out_4, k_1_out_5, k_1_out_6, l_1_out_2, l_1_out_3,
       l_1_out_4, l_1_out_5, l_1_out_6, m_1_out_2, m_1_out_3, m_1_out_4, m_1_out_5, m_1_out_6, n_1_out_2,
       n_1_out_3, n_1_out_4, n_1_out_5, n_1_out_6, neo_ko_1_out_4, o_1_out_2, o_1_out_3, o_1_out_4,
       o_1_out_5, o_1_out_6, or_1_out, p_1_out_2, p_1_out_3, p_1_out_4, p_1_out_5, p_1_out_6, q_1_out_2,
       q_1_out_3, q_1_out_4, q_1_out_5, q_1_out_6, r_1_out_2, r_1_out_3, r_1_out_4, r_1_out_5, r_1_out_6,
       register_2_q, register_3_q, register_5_q, register_7_q, register_9_q, register_11_q, s, s_1_out_2,
       s_1_out_3, s_1_out_4, s_1_out_5, s_1_out_6, t_1_out_2, t_1_out_3, t_1_out_4, t_1_out_5, t_1_out_6,
       u_1_out_2, u_1_out_3, u_1_out_4, u_1_out_5, u_1_out_6, v_1_out_2, v_1_out_3, v_1_out_4, v_1_out_5,
       v_1_out_6, w_1_out_2, w_1_out_3, w_1_out_4, w_1_out_5, w_1_out_6, x_1_out_2, x_1_out_3, x_1_out_4,
       x_1_out_5, x_1_out_6, y_1_out_2, y_1_out_3, y_1_out_4, y_1_out_5, y_1_out_6, z_1_out_2, z_1_out_3,
       z_1_out_4, z_1_out_5, z_1_out_6;
  wire [31:0] or_3_out, register_1_q, s2;

  Decoder #(.select(5), .enable("false")) decoder_1 (
    .out1(decoder_1_out1), .out2(decoder_1_out2), .out3(decoder_1_out3), .out4(decoder_1_out4),
    .out5(decoder_1_out5), .out6(decoder_1_out6), .out7(decoder_1_out7), .out8(decoder_1_out8),
    .out9(decoder_1_out9), .out10(decoder_1_out10), .out11(decoder_1_out11), .out12(decoder_1_out12),
    .out13(decoder_1_out13), .out14(decoder_1_out14), .out15(decoder_1_out15), .out16(decoder_1_out16),
    .out17(decoder_1_out17), .out18(decoder_1_out18), .out19(decoder_1_out19), .out20(decoder_1_out20),
    .out21(decoder_1_out21), .out22(decoder_1_out22), .out23(decoder_1_out23), .out24(decoder_1_out24),
    .out25(decoder_1_out25), .out26(decoder_1_out26), .out27(r), .sel(bit_extender_2_out));  // open: out0, out28, out29, out30, out31
  assign e = undriven ? 8'h2 : 8'bz;  // Controlled_Buffer controlled_buffer_1
  A a_1 (
    .in_1(decoder_1_out1), .out_2(a_1_out_2), .out_3(a_1_out_3), .out_4(a_1_out_4), .out_5(a_1_out_5),
    .out_6(a_1_out_6));
  M m_1 (
    .in_1(decoder_1_out2), .out_2(m_1_out_2), .out_3(m_1_out_3), .out_4(m_1_out_4), .out_5(m_1_out_5),
    .out_6(m_1_out_6));
  B b_1 (
    .in_1(decoder_1_out3), .out_2(b_1_out_2), .out_3(b_1_out_3), .out_4(b_1_out_4), .out_5(b_1_out_5),
    .out_6(b_1_out_6));
  Y y_1 (
    .in_1(decoder_1_out4), .out_2(y_1_out_2), .out_3(y_1_out_3), .out_4(y_1_out_4), .out_5(y_1_out_5),
    .out_6(y_1_out_6));
  G g_1 (
    .in_1(decoder_1_out5), .out_2(g_1_out_2), .out_3(g_1_out_3), .out_4(g_1_out_4), .out_5(g_1_out_5),
    .out_6(g_1_out_6));
  F f_1 (
    .in_1(decoder_1_out6), .out_2(f_1_out_2), .out_3(f_1_out_3), .out_4(f_1_out_4), .out_5(f_1_out_5),
    .out_6(f_1_out_6));
  H h_1 (
    .in_1(decoder_1_out7), .out_2(h_1_out_2), .out_3(h_1_out_3), .out_4(h_1_out_4), .out_5(h_1_out_5),
    .out_6(h_1_out_6));
  C c_1 (
    .in_1(decoder_1_out8), .out_2(c_1_out_2), .out_3(c_1_out_3), .out_4(c_1_out_4), .out_5(c_1_out_5),
    .out_6(c_1_out_6));
  D d_1 (
    .in_1(decoder_1_out9), .out_2(d_1_out_2), .out_3(d_1_out_3), .out_4(d_1_out_4), .out_5(d_1_out_5),
    .out_6(d_1_out_6));
  L l_1 (
    .in_1(decoder_1_out10), .out_2(l_1_out_2), .out_3(l_1_out_3), .out_4(l_1_out_4), .out_5(l_1_out_5),
    .out_6(l_1_out_6));
  X x_1 (
    .in_1(decoder_1_out11), .out_2(x_1_out_2), .out_3(x_1_out_3), .out_4(x_1_out_4), .out_5(x_1_out_5),
    .out_6(x_1_out_6));
  Z z_1 (
    .in_1(decoder_1_out12), .out_2(z_1_out_2), .out_3(z_1_out_3), .out_4(z_1_out_4), .out_5(z_1_out_5),
    .out_6(z_1_out_6));
  S s_1 (
    .in_1(decoder_1_out13), .out_2(s_1_out_2), .out_3(s_1_out_3), .out_4(s_1_out_4), .out_5(s_1_out_5),
    .out_6(s_1_out_6));
  Q q_1 (
    .in_1(decoder_1_out14), .out_2(q_1_out_2), .out_3(q_1_out_3), .out_4(q_1_out_4), .out_5(q_1_out_5),
    .out_6(q_1_out_6));
  W w_1 (
    .in_1(decoder_1_out15), .out_2(w_1_out_2), .out_3(w_1_out_3), .out_4(w_1_out_4), .out_5(w_1_out_5),
    .out_6(w_1_out_6));
  E e_1 (
    .in_1(decoder_1_out16), .out_2(e_1_out_2), .out_3(e_1_out_3), .out_4(e_1_out_4), .out_5(e_1_out_5),
    .out_6(e_1_out_6));
  R r_1 (
    .in_1(decoder_1_out17), .out_2(r_1_out_2), .out_3(r_1_out_3), .out_4(r_1_out_4), .out_5(r_1_out_5),
    .out_6(r_1_out_6));
  T t_1 (
    .in_1(decoder_1_out18), .out_2(t_1_out_2), .out_3(t_1_out_3), .out_4(t_1_out_4), .out_5(t_1_out_5),
    .out_6(t_1_out_6));
  U u_1 (
    .in_1(decoder_1_out19), .out_2(u_1_out_2), .out_3(u_1_out_3), .out_4(u_1_out_4), .out_5(u_1_out_5),
    .out_6(u_1_out_6));
  I i_1 (
    .in_1(decoder_1_out20), .out_2(i_1_out_2), .out_3(i_1_out_3), .out_4(i_1_out_4), .out_5(i_1_out_5),
    .out_6(i_1_out_6));
  O o_1 (
    .in_1(decoder_1_out21), .out_2(o_1_out_2), .out_3(o_1_out_3), .out_4(o_1_out_4), .out_5(o_1_out_5),
    .out_6(o_1_out_6));
  P p_1 (
    .in_1(decoder_1_out22), .out_2(p_1_out_2), .out_3(p_1_out_3), .out_4(p_1_out_4), .out_5(p_1_out_5),
    .out_6(p_1_out_6));
  V v_1 (
    .in_1(decoder_1_out23), .out_2(v_1_out_2), .out_3(v_1_out_3), .out_4(v_1_out_4), .out_5(v_1_out_5),
    .out_6(v_1_out_6));
  J j_1 (
    .in_1(decoder_1_out24), .out_2(j_1_out_2), .out_3(j_1_out_3), .out_4(j_1_out_4), .out_5(j_1_out_5),
    .out_6(j_1_out_6));
  N n_1 (
    .in_1(decoder_1_out25), .out_2(n_1_out_2), .out_3(n_1_out_3), .out_4(n_1_out_4), .out_5(n_1_out_5),
    .out_6(n_1_out_6));
  K k_1 (
    .in_1(decoder_1_out26), .out_2(k_1_out_2), .out_3(k_1_out_3), .out_4(k_1_out_4), .out_5(k_1_out_5),
    .out_6(k_1_out_6));
  LED led_1 (.in(neo_ko_1_out_5));
  neo_ko neo_ko_1 (.out_4(neo_ko_1_out_4), .in_2(in_2), .in_1(in_1), .out_5(neo_ko_1_out_5), .in_3(r));
  Bit_Extender #(.out_width(6)) bit_extender_1 (.in(neo_ko_1_out_4), .out(bit_extender_1_out));
  Bit_Extender #(.in_width(6), .out_width(5)) bit_extender_2 (.in(bit_extender_1_out), .out(bit_extender_2_out));
  not not_1 (not_1_out, and_1_out);
  and and_1 (and_1_out, not_2_out, not_3_out, not_4_out, not_5_out, not_6_out, not_7_out, not_8_out, not_9_out, not_10_out, not_11_out, not_12_out, not_13_out, not_14_out, not_15_out, not_16_out, not_17_out, not_18_out, not_19_out, not_20_out, not_21_out, not_22_out, not_23_out, not_24_out, not_25_out, not_26_out, not_27_out, not_28_out, not_29_out, not_30_out, not_31_out, not_32_out, not_33_out);
  assign or_1_out = n_1_out_6 | j_1_out_6 | v_1_out_6 | p_1_out_6 | o_1_out_6 | i_1_out_6 | u_1_out_6 | t_1_out_6 | r_1_out_6 | e_1_out_6 | w_1_out_6 | q_1_out_6 | s_1_out_6 | z_1_out_6 | x_1_out_6 | l_1_out_6 | d_1_out_6 | c_1_out_6 | h_1_out_6 | f_1_out_6 | g_1_out_6 | y_1_out_6 | b_1_out_6 | m_1_out_6 | a_1_out_6;  // OR_Gate or_1, 8 bits wide
  assign s = k_1_out_6 | or_1_out;  // OR_Gate or_2, 8 bits wide
  not not_2 (not_2_out, s2[0]);
  not not_3 (not_3_out, s2[1]);
  not not_4 (not_4_out, s2[2]);
  not not_5 (not_5_out, s2[3]);
  not not_6 (not_6_out, s2[4]);
  not not_7 (not_7_out, s2[5]);
  not not_8 (not_8_out, s2[6]);
  not not_9 (not_9_out, s2[7]);
  not not_10 (not_10_out, s2[8]);
  not not_11 (not_11_out, s2[9]);
  not not_12 (not_12_out, s2[10]);
  not not_13 (not_13_out, s2[11]);
  not not_14 (not_14_out, s2[12]);
  not not_15 (not_15_out, s2[13]);
  not not_16 (not_16_out, s2[14]);
  not not_17 (not_17_out, s2[15]);
  not not_18 (not_18_out, s2[16]);
  not not_19 (not_19_out, s2[17]);
  not not_20 (not_20_out, s2[18]);
  not not_21 (not_21_out, s2[19]);
  not not_22 (not_22_out, s2[20]);
  not not_23 (not_23_out, s2[21]);
  not not_24 (not_24_out, s2[22]);
  not not_25 (not_25_out, s2[23]);
  not not_26 (not_26_out, s2[24]);
  not not_27 (not_27_out, s2[25]);
  not not_28 (not_28_out, s2[26]);
  not not_29 (not_29_out, s2[27]);
  not not_30 (not_30_out, s2[28]);
  not not_31 (not_31_out, s2[29]);
  not not_32 (not_32_out, s2[30]);
  not not_33 (not_33_out, s2[31]);
  DotMatrix #(.matrixrows(8)) dotmatrix_1 (
    .col0(s2[7:0]), .col1(s2[15:8]), .col2(s2[23:16]), .col3(s2[31:24]), .col4(s));
  assign or_3_out = {a_1_out_5, a_1_out_4, a_1_out_3, a_1_out_2} | {m_1_out_5, m_1_out_4, m_1_out_3, m_1_out_2} | {b_1_out_5, b_1_out_4, b_1_out_3, b_1_out_2} | {y_1_out_5, y_1_out_4, y_1_out_3, y_1_out_2} | {g_1_out_5, g_1_out_4, g_1_out_3, g_1_out_2} | {f_1_out_5, f_1_out_4, f_1_out_3, f_1_out_2} | {h_1_out_5, h_1_out_4, h_1_out_3, h_1_out_2} | {c_1_out_5, c_1_out_4, c_1_out_3, c_1_out_2} | {d_1_out_5, d_1_out_4, d_1_out_3, d_1_out_2} | {l_1_out_5, l_1_out_4, l_1_out_3, l_1_out_2} | {x_1_out_5, x_1_out_4, x_1_out_3, x_1_out_2} | {z_1_out_5, z_1_out_4, z_1_out_3, z_1_out_2} | {s_1_out_5, s_1_out_4, s_1_out_3, s_1_out_2} | {q_1_out_5, q_1_out_4, q_1_out_3, q_1_out_2} | {w_1_out_5, w_1_out_4, w_1_out_3, w_1_out_2} | {e_1_out_5, e_1_out_4, e_1_out_3, e_1_out_2} | {r_1_out_5, r_1_out_4, r_1_out_3, r_1_out_2} | {t_1_out_5, t_1_out_4, t_1_out_3, t_1_out_2} | {u_1_out_5, u_1_out_4, u_1_out_3, u_1_out_2} | {i_1_out_5, i_1_out_4, i_1_out_3, i_1_out_2} | {o_1_out_5, o_1_out_4, o_1_out_3, o_1_out_2} | {p_1_out_5, p_1_out_4, p_1_out_3, p_1_out_2} | {v_1_out_5, v_1_out_4, v_1_out_3, v_1_out_2} | {j_1_out_5, j_1_out_4, j_1_out_3, j_1_out_2} | {n_1_out_5, n_1_out_4, n_1_out_3, n_1_out_2};  // OR_Gate or_3, 32 bits wide
  assign s2 = or_3_out | {k_1_out_5, k_1_out_4, k_1_out_3, k_1_out_2};  // OR_Gate or_4, 32 bits wide
  Register #(.width(32), .trigger("high")) register_1 (.D(s2), .Q(register_1_q), .clk(not_1_out));  // open: en, clr
  Register #(.trigger("high")) register_2 (.D(s), .Q(register_2_q), .clk(not_1_out));  // open: en, clr
  and and_2 (and_2_out, not_1_out, clock_1_out);
  Clock clock_1 (.out(clock_1_out));
  assign out_3 = 1'b1 ? register_3_q : 8'bz;  // Controlled_Buffer controlled_buffer_2
  Register register_3 (.D(register_2_q), .Q(register_3_q), .clk(and_2_out), .clr(r));  // open: en
  Register register_4 (.D(adder_1_out), .Q(out_3), .clk(and_2_out), .clr(r));  // open: en
  Adder adder_1 (.a(register_3_q), .b({8{1'b0}}), .out(adder_1_out), .cin(1'b1));  // open: cout
  Register register_5 (.D(register_1_q[7:0]), .Q(register_5_q), .clk(and_2_out), .clr(r));  // open: en
  assign out_4 = 1'b1 ? register_5_q : 8'bz;  // Controlled_Buffer controlled_buffer_3
  Adder adder_2 (.a(register_5_q), .b({8{1'b0}}), .out(adder_2_out), .cin(1'b1));  // open: cout
  Register register_6 (.D(adder_2_out), .Q(out_4), .clk(and_2_out), .clr(r));  // open: en
  Register register_7 (.D(register_1_q[15:8]), .Q(register_7_q), .clk(and_2_out), .clr(r));  // open: en
  assign out_5 = 1'b1 ? register_7_q : 8'bz;  // Controlled_Buffer controlled_buffer_4
  DotMatrix #(.matrixrows(8)) dotmatrix_2 (.col0(out_4), .col1(out_5), .col2(out_6), .col3(out_7), .col4(out_3));
  Register register_8 (.D(adder_3_out), .Q(out_5), .clk(and_2_out), .clr(r));  // open: en
  Adder adder_3 (.a(register_7_q), .b({8{1'b0}}), .out(adder_3_out), .cin(1'b1));  // open: cout
  Register register_9 (.D(register_1_q[23:16]), .Q(register_9_q), .clk(and_2_out), .clr(r));  // open: en
  assign out_6 = 1'b1 ? register_9_q : 8'bz;  // Controlled_Buffer controlled_buffer_5
  Register register_10 (.D(adder_4_out), .Q(out_6), .clk(and_2_out), .clr(r));  // open: en
  Adder adder_4 (.a(register_9_q), .b({8{1'b0}}), .out(adder_4_out), .cin(1'b1));  // open: cout
  Register register_11 (.D(register_1_q[31:24]), .Q(register_11_q), .clk(and_2_out), .clr(r));  // open: en
  assign out_7 = 1'b1 ? register_11_q : 8'bz;  // Controlled_Buffer controlled_buffer_6
  Adder adder_5 (.a(register_11_q), .b({8{1'b0}}), .out(adder_5_out), .cin(1'b1));  // open: cout
  Register register_12 (.D(adder_5_out), .Q(out_7), .clk(and_2_out), .clr(r));  // open: en
  or or_5 (or_5_out, out_4[7], out_4[6], out_4[5], out_4[4], out_4[3], out_4[2], out_4[1], out_4[0], out_5[7], out_5[6], out_5[5], out_5[4], out_5[3], out_5[2], out_5[1], out_5[0], out_6[6], out_6[5], out_6[4], out_6[3], out_6[2], out_6[1], out_6[0], out_7[7], out_7[6], out_7[5], out_7[4], out_7[3], out_7[2], out_7[1], out_7[0], out_6[7]);
  and and_3 (r1, or_5_out, clock_2_out);
  Clock #(.highDuration(100), .lowDuration(100)) clock_2 (.out(clock_2_out));
endmodule

module neo_ko (
  input  [6:0] in_1,
  input  in_2,
  input  in_3,
  output [7:0] out_4,
  output out_5
);

  wire a_out, and_1_out, and_2_out, and_3_out, and_4_out, and_5_out, and_6_out, and_7_out, and_8_out,
       and_9_out, and_10_out, and_11_out, and_12_out, and_13_out, and_14_out, and_15_out, and_16_out,
       and_17_out, and_18_out, and_19_out, and_20_out, and_21_out, and_22_out, and_23_out, and_24_out,
       and_25_out, and_26_out, and_27_out, and_28_out, and_29_out, and_30_out, and_31_out, and_32_out,
       and_33_out, and_34_out, and_35_out, and_36_out, and_37_out, and_38_out, and_39_out, and_40_out,
       and_41_out, and_42_out, and_43_out, and_44_out, and_45_out, and_46_out, and_47_out, and_48_out,
       and_49_out, and_50_out, and_51_out, and_53_out, b_out, c_out, d_out, e_out, f_out, g_out, h_out,
       i_out, j_out, k_2_out, k_3_out, k_out, l_out, m_2_out, m_out, n_out, not_1_out, not_2_out, not_3_out,
       not_4_out, not_5_out, not_6_out, not_7_out, not_8_out, not_9_out, not_10_out, not_11_out, not_12_out,
       not_13_out, not_14_out, not_15_out, not_16_out, not_17_out, not_18_out, not_19_out, not_20_out,
       not_21_out, not_22_out, not_23_out, not_24_out, not_25_out, not_26_out, not_27_out, not_28_out,
       not_29_out, not_30_out, not_31_out, not_32_out, not_33_out, not_34_out, not_35_out, not_36_out,
       not_37_out, not_38_out, not_39_out, not_40_out, not_41_out, not_42_out, not_43_out, not_44_out,
       not_45_out, not_46_out, not_47_out, not_48_out, not_49_out, not_50_out, not_51_out, not_52_out,
       not_53_out, not_54_out, not_55_out, not_56_out, not_57_out, not_58_out, not_59_out, not_60_out,
       not_61_out, not_62_out, not_63_out, not_64_out, not_65_out, not_66_out, not_67_out, not_68_out,
       not_69_out, not_70_out, not_71_out, not_72_out, not_73_out, not_74_out, not_75_out, not_76_out,
       not_77_out, not_78_out, not_79_out, not_80_out, not_81_out, not_82_out, not_83_out, not_84_out,
       not_85_out, not_86_out, not_87_out, not_88_out, not_89_out, not_90_out, not_91_out, not_92_out,
       not_93_out, not_94_out, not_95_out, not_96_out, not_97_out, not_98_out, not_99_out, not_100_out,
       not_101_out, not_102_out, not_103_out, not_104_out, not_105_out, not_106_out, not_107_out,
       not_108_out, not_109_out, not_110_out, not_111_out, not_112_out, not_113_out, not_114_out,
       not_115_out, not_116_out, not_117_out, not_118_out, not_119_out, not_120_out, not_121_out,
       not_122_out, not_123_out, not_124_out, not_125_out, not_126_out, not_127_out, not_128_out,
       not_129_out, not_130_out, not_131_out, not_132_out, not_133_out, not_134_out, not_135_out,
       not_136_out, not_137_out, not_138_out, not_139_out, not_140_out, not_141_out, not_142_out,
       not_143_out, not_144_out, not_145_out, not_146_out, not_147_out, not_148_out, not_149_out,
       not_150_out, not_151_out, not_152_out, not_153_out, not_154_out, not_155_out, not_156_out,
       not_157_out, not_158_out, not_159_out, not_160_out, not_161_out, not_162_out, not_163_out,
       not_164_out, not_165_out, not_166_out, not_167_out, not_168_out, not_169_out, not_170_out,
       not_171_out, not_172_out, not_173_out, not_174_out, o_out, p_out, q_out, r_out, s_out, t_out, u_out,
       v_out, w_out, x_out, y_out, z_out;
  wire [6:0] niiio;

  or m (m_out, niiio[0], niiio[1], niiio[2], niiio[3], niiio[4], niiio[5], niiio[6]);
  Register #(.width(7)) register_1 (.D(in_1), .Q(niiio), .clk(in_2), .clr(and_1_out));  // open: en
  and and_1 (and_1_out, m_out, in_3);
  not not_1 (not_1_out, niiio[2]);
  and k (k_out, niiio[0], niiio[1], not_1_out, niiio[3], not_2_out, niiio[5], niiio[6]);
  not not_2 (not_2_out, niiio[4]);
  not not_3 (not_3_out, niiio[2]);
  and k_2 (k_2_out, niiio[0], niiio[1], not_3_out, niiio[3], not_4_out, not_5_out, niiio[6]);
  not not_4 (not_4_out, niiio[4]);
  not not_5 (not_5_out, niiio[5]);
  not not_6 (not_6_out, niiio[1]);
  not not_7 (not_7_out, niiio[2]);
  not not_8 (not_8_out, niiio[3]);
  and and_2 (and_2_out, niiio[0], not_6_out, not_7_out, not_8_out, not_9_out, niiio[5], niiio[6]);
  not not_9 (not_9_out, niiio[4]);
  not not_10 (not_10_out, niiio[1]);
  not not_11 (not_11_out, niiio[2]);
  not not_12 (not_12_out, niiio[3]);
  and and_3 (and_3_out, niiio[0], not_10_out, not_11_out, not_12_out, not_13_out, not_14_out, niiio[6]);
  not not_13 (not_13_out, niiio[4]);
  not not_14 (not_14_out, niiio[5]);
  not not_15 (not_15_out, niiio[1]);
  not not_16 (not_16_out, niiio[2]);
  not not_17 (not_17_out, niiio[3]);
  and and_4 (and_4_out, niiio[0], not_15_out, not_16_out, not_17_out, niiio[4], niiio[5], niiio[6]);
  not not_18 (not_18_out, niiio[1]);
  not not_19 (not_19_out, niiio[2]);
  and and_5 (and_5_out, niiio[0], not_18_out, not_19_out, not_20_out, niiio[4], not_21_out, niiio[6]);
  not not_20 (not_20_out, niiio[3]);
  not not_21 (not_21_out, niiio[5]);
  not not_22 (not_22_out, niiio[3]);
  and and_6 (and_6_out, niiio[0], niiio[1], niiio[2], not_22_out, niiio[4], niiio[5], niiio[6]);
  not not_23 (not_23_out, niiio[3]);
  and and_7 (and_7_out, niiio[0], niiio[1], niiio[2], not_23_out, niiio[4], not_24_out, niiio[6]);
  not not_24 (not_24_out, niiio[5]);
  not not_25 (not_25_out, niiio[1]);
  not not_26 (not_26_out, niiio[3]);
  and and_8 (and_8_out, niiio[0], not_25_out, niiio[2], not_26_out, not_27_out, niiio[5], niiio[6]);
  not not_27 (not_27_out, niiio[4]);
  not not_28 (not_28_out, niiio[1]);
  not not_29 (not_29_out, niiio[3]);
  and and_9 (and_9_out, niiio[0], not_28_out, niiio[2], not_29_out, not_30_out, not_31_out, niiio[6]);
  not not_30 (not_30_out, niiio[4]);
  not not_31 (not_31_out, niiio[5]);
  not not_32 (not_32_out, niiio[0]);
  not not_33 (not_33_out, niiio[2]);
  not not_34 (not_34_out, niiio[3]);
  and and_10 (and_10_out, not_32_out, niiio[1], not_33_out, not_34_out, niiio[4], niiio[5], niiio[6]);
  not not_35 (not_35_out, niiio[0]);
  not not_36 (not_36_out, niiio[2]);
  not not_37 (not_37_out, niiio[3]);
  and and_11 (and_11_out, not_35_out, niiio[1], not_36_out, not_37_out, niiio[4], not_38_out, niiio[6]);
  not not_38 (not_38_out, niiio[5]);
  not not_39 (not_39_out, niiio[0]);
  not not_40 (not_40_out, niiio[1]);
  and and_12 (and_12_out, not_39_out, not_40_out, niiio[2], not_41_out, niiio[4], niiio[5], niiio[6]);
  not not_41 (not_41_out, niiio[3]);
  not not_42 (not_42_out, niiio[0]);
  not not_43 (not_43_out, niiio[1]);
  and and_13 (and_13_out, not_42_out, not_43_out, niiio[2], not_44_out, niiio[4], not_45_out, niiio[6]);
  not not_44 (not_44_out, niiio[3]);
  not not_45 (not_45_out, niiio[5]);
  not not_46 (not_46_out, niiio[1]);
  not not_47 (not_47_out, niiio[2]);
  and and_14 (and_14_out, niiio[0], not_46_out, not_47_out, niiio[3], niiio[4], niiio[5], niiio[6]);
  not not_48 (not_48_out, niiio[1]);
  not not_49 (not_49_out, niiio[2]);
  and and_15 (and_15_out, niiio[0], not_48_out, not_49_out, niiio[3], niiio[4], not_50_out, niiio[6]);
  not not_50 (not_50_out, niiio[5]);
  not not_51 (not_51_out, niiio[1]);
  not not_52 (not_52_out, niiio[3]);
  and and_16 (and_16_out, niiio[0], not_51_out, niiio[2], not_52_out, niiio[4], niiio[5], niiio[6]);
  not not_53 (not_53_out, niiio[1]);
  and and_17 (and_17_out, niiio[0], not_53_out, niiio[2], not_54_out, niiio[4], not_55_out, niiio[6]);
  not not_54 (not_54_out, niiio[3]);
  not not_55 (not_55_out, niiio[5]);
  not not_56 (not_56_out, niiio[1]);
  not not_57 (not_57_out, niiio[2]);
  and and_18 (and_18_out, niiio[0], not_56_out, not_57_out, niiio[3], not_58_out, niiio[5], niiio[6]);
  not not_58 (not_58_out, niiio[4]);
  not not_59 (not_59_out, niiio[1]);
  not not_60 (not_60_out, niiio[2]);
  and and_19 (and_19_out, niiio[0], not_59_out, not_60_out, niiio[3], not_61_out, not_62_out, niiio[6]);
  not not_61 (not_61_out, niiio[4]);
  not not_62 (not_62_out, niiio[5]);
  and and_20 (and_20_out, niiio[0], niiio[1], niiio[2], niiio[3], not_63_out, niiio[5], niiio[6]);
  not not_63 (not_63_out, niiio[4]);
  and and_21 (and_21_out, niiio[0], niiio[1], niiio[2], niiio[3], not_64_out, not_65_out, niiio[6]);
  not not_64 (not_64_out, niiio[4]);
  not not_65 (not_65_out, niiio[5]);
  and and_22 (and_22_out, niiio[0], niiio[1], niiio[2], niiio[3], niiio[4], niiio[5], niiio[6]);
  not not_66 (not_66_out, niiio[0]);
  not not_67 (not_67_out, niiio[1]);
  not not_68 (not_68_out, niiio[2]);
  not not_69 (not_69_out, niiio[3]);
  and and_23 (and_23_out, not_66_out, not_67_out, not_68_out, not_69_out, niiio[4], niiio[5], niiio[6]);
  not not_70 (not_70_out, niiio[2]);
  and and_24 (and_24_out, niiio[0], niiio[1], not_70_out, not_71_out, niiio[4], niiio[5], niiio[6]);
  not not_71 (not_71_out, niiio[3]);
  not not_72 (not_72_out, niiio[2]);
  and and_25 (and_25_out, niiio[0], niiio[1], not_72_out, not_73_out, niiio[4], not_74_out, niiio[6]);
  not not_73 (not_73_out, niiio[3]);
  not not_74 (not_74_out, niiio[5]);
  not not_75 (not_75_out, niiio[0]);
  not not_76 (not_76_out, niiio[1]);
  not not_77 (not_77_out, niiio[3]);
  and and_26 (and_26_out, not_75_out, not_76_out, niiio[2], not_77_out, not_78_out, niiio[5], niiio[6]);
  not not_78 (not_78_out, niiio[4]);
  not not_79 (not_79_out, niiio[0]);
  not not_80 (not_80_out, niiio[1]);
  and and_27 (and_27_out, not_79_out, not_80_out, niiio[2], not_81_out, not_82_out, not_83_out, niiio[6]);
  not not_81 (not_81_out, niiio[3]);
  not not_82 (not_82_out, niiio[4]);
  not not_83 (not_83_out, niiio[5]);
  not not_84 (not_84_out, niiio[0]);
  not not_85 (not_85_out, niiio[3]);
  and and_28 (and_28_out, not_84_out, niiio[1], niiio[2], not_85_out, not_86_out, niiio[5], niiio[6]);
  not not_86 (not_86_out, niiio[4]);
  not not_87 (not_87_out, niiio[0]);
  not not_88 (not_88_out, niiio[3]);
  and and_29 (and_29_out, not_87_out, niiio[1], niiio[2], not_88_out, not_89_out, not_90_out, niiio[6]);
  not not_89 (not_89_out, niiio[4]);
  not not_90 (not_90_out, niiio[5]);
  not not_91 (not_91_out, niiio[3]);
  and and_30 (and_30_out, niiio[0], niiio[1], niiio[2], not_91_out, not_92_out, niiio[5], niiio[6]);
  not not_92 (not_92_out, niiio[4]);
  and and_31 (and_31_out, niiio[0], niiio[1], niiio[2], not_93_out, not_94_out, not_95_out, niiio[6]);
  not not_93 (not_93_out, niiio[3]);
  not not_94 (not_94_out, niiio[4]);
  not not_95 (not_95_out, niiio[5]);
  not not_96 (not_96_out, niiio[0]);
  not not_97 (not_97_out, niiio[1]);
  not not_98 (not_98_out, niiio[2]);
  and and_32 (and_32_out, not_96_out, not_97_out, not_98_out, niiio[3], not_99_out, niiio[5], niiio[6]);
  not not_99 (not_99_out, niiio[4]);
  not not_100 (not_100_out, niiio[0]);
  not not_101 (not_101_out, niiio[1]);
  not not_102 (not_102_out, niiio[2]);
  and and_33 (and_33_out, not_100_out, not_101_out, not_102_out, niiio[3], not_103_out, not_104_out, niiio[6]);
  not not_103 (not_103_out, niiio[4]);
  not not_104 (not_104_out, niiio[5]);
  not not_105 (not_105_out, niiio[0]);
  not not_106 (not_106_out, niiio[2]);
  and and_34 (and_34_out, not_105_out, niiio[1], not_106_out, niiio[3], not_107_out, niiio[5], niiio[6]);
  not not_107 (not_107_out, niiio[4]);
  not not_108 (not_108_out, niiio[0]);
  not not_109 (not_109_out, niiio[2]);
  and and_35 (and_35_out, not_108_out, niiio[1], not_109_out, niiio[3], not_110_out, not_111_out, niiio[6]);
  not not_110 (not_110_out, niiio[4]);
  not not_111 (not_111_out, niiio[5]);
  not not_112 (not_112_out, niiio[0]);
  not not_113 (not_113_out, niiio[1]);
  and and_36 (and_36_out, not_112_out, not_113_out, niiio[2], niiio[3], not_114_out, niiio[5], niiio[6]);
  not not_114 (not_114_out, niiio[4]);
  not not_115 (not_115_out, niiio[0]);
  not not_116 (not_116_out, niiio[1]);
  and and_37 (and_37_out, not_115_out, not_116_out, niiio[2], niiio[3], not_117_out, not_118_out, niiio[6]);
  not not_117 (not_117_out, niiio[4]);
  not not_118 (not_118_out, niiio[5]);
  not not_119 (not_119_out, niiio[0]);
  not not_120 (not_120_out, niiio[2]);
  and and_38 (and_38_out, not_119_out, niiio[1], not_120_out, niiio[3], niiio[4], niiio[5], niiio[6]);
  not not_121 (not_121_out, niiio[0]);
  not not_122 (not_122_out, niiio[2]);
  and and_39 (and_39_out, not_121_out, niiio[1], not_122_out, niiio[3], niiio[4], not_123_out, niiio[6]);
  not not_123 (not_123_out, niiio[5]);
  not not_124 (not_124_out, niiio[0]);
  not not_125 (not_125_out, niiio[1]);
  not not_126 (not_126_out, niiio[2]);
  and and_40 (and_40_out, not_124_out, not_125_out, not_126_out, niiio[3], niiio[4], niiio[5], niiio[6]);
  not not_127 (not_127_out, niiio[0]);
  not not_128 (not_128_out, niiio[1]);
  not not_129 (not_129_out, niiio[2]);
  and and_41 (and_41_out, not_127_out, not_128_out, not_129_out, niiio[3], niiio[4], not_130_out, niiio[6]);
  not not_130 (not_130_out, niiio[5]);
  not not_131 (not_131_out, niiio[2]);
  and and_42 (and_42_out, niiio[0], niiio[1], not_131_out, not_132_out, not_133_out, niiio[5], niiio[6]);
  not not_132 (not_132_out, niiio[3]);
  not not_133 (not_133_out, niiio[4]);
  not not_134 (not_134_out, niiio[2]);
  not not_135 (not_135_out, niiio[3]);
  and and_43 (and_43_out, niiio[0], niiio[1], not_134_out, not_135_out, not_136_out, not_137_out, niiio[6]);
  not not_136 (not_136_out, niiio[4]);
  not not_137 (not_137_out, niiio[5]);
  not not_138 (not_138_out, niiio[0]);
  not not_139 (not_139_out, niiio[3]);
  and and_44 (and_44_out, not_138_out, niiio[1], niiio[2], not_139_out, niiio[4], niiio[5], niiio[6]);
  not not_140 (not_140_out, niiio[0]);
  and and_45 (and_45_out, not_140_out, niiio[1], niiio[2], not_141_out, niiio[4], not_142_out, niiio[6]);
  not not_141 (not_141_out, niiio[3]);
  not not_142 (not_142_out, niiio[5]);
  not not_143 (not_143_out, niiio[0]);
  not not_144 (not_144_out, niiio[2]);
  and and_46 (and_46_out, not_143_out, niiio[1], not_144_out, not_145_out, not_146_out, niiio[5], niiio[6]);
  not not_145 (not_145_out, niiio[3]);
  not not_146 (not_146_out, niiio[4]);
  not not_147 (not_147_out, niiio[0]);
  not not_148 (not_148_out, niiio[2]);
  and and_47 (and_47_out, not_147_out, niiio[1], not_148_out, not_149_out, not_150_out, not_151_out, niiio[6]);
  not not_149 (not_149_out, niiio[3]);
  not not_150 (not_150_out, niiio[4]);
  not not_151 (not_151_out, niiio[5]);
  not not_152 (not_152_out, niiio[0]);
  and and_48 (and_48_out, not_152_out, niiio[1], niiio[2], niiio[3], not_153_out, niiio[5], niiio[6]);
  not not_153 (not_153_out, niiio[4]);
  not not_154 (not_154_out, niiio[0]);
  and and_49 (and_49_out, not_154_out, niiio[1], niiio[2], niiio[3], not_155_out, not_156_out, niiio[6]);
  not not_155 (not_155_out, niiio[4]);
  not not_156 (not_156_out, niiio[5]);
  not not_157 (not_157_out, niiio[1]);
  and and_50 (and_50_out, niiio[0], not_157_out, niiio[2], niiio[3], not_158_out, niiio[5], niiio[6]);
  not not_158 (not_158_out, niiio[4]);
  not not_159 (not_159_out, niiio[1]);
  and and_51 (and_51_out, niiio[0], not_159_out, niiio[2], niiio[3], not_160_out, not_161_out, niiio[6]);
  not not_160 (not_160_out, niiio[4]);
  not not_161 (not_161_out, niiio[5]);
  not not_162 (not_162_out, niiio[0]);
  not not_163 (not_163_out, niiio[1]);
  not not_164 (not_164_out, niiio[2]);
  and and_52 (out_5, not_162_out, not_163_out, not_164_out, not_165_out, not_166_out, not_167_out, not_168_out);
  not not_165 (not_165_out, niiio[3]);
  not not_166 (not_166_out, niiio[4]);
  not not_167 (not_167_out, niiio[5]);
  not not_168 (not_168_out, niiio[6]);
  not not_169 (not_169_out, niiio[0]);
  not not_170 (not_170_out, niiio[1]);
  not not_171 (not_171_out, niiio[2]);
  not not_172 (not_172_out, niiio[4]);
  not not_173 (not_173_out, niiio[5]);
  not not_174 (not_174_out, niiio[6]);
  or k_3 (k_3_out, k_out, k_2_out);
  or a (a_out, and_2_out, and_3_out);
  or q (q_out, and_4_out, and_5_out);
  or w (w_out, and_6_out, and_7_out);
  or e (e_out, and_8_out, and_9_out);
  or r (r_out, and_10_out, and_11_out);
  or t (t_out, and_12_out, and_13_out);
  or y (y_out, and_14_out, and_15_out);
  or u (u_out, and_16_out, and_17_out);
  or i (i_out, and_18_out, and_19_out);
  or o (o_out, and_20_out, and_21_out);
  or p (p_out, and_22_out, and_23_out);
  or s (s_out, and_24_out, and_25_out);
  or d (d_out, and_26_out, and_27_out);
  or f (f_out, and_28_out, and_29_out);
  or g (g_out, and_30_out, and_31_out);
  or h (h_out, and_32_out, and_33_out);
  or j (j_out, and_34_out, and_35_out);
  or l (l_out, and_36_out, and_37_out);
  or z (z_out, and_38_out, and_39_out);
  or x (x_out, and_40_out, and_41_out);
  or c (c_out, and_42_out, and_43_out);
  or v (v_out, and_44_out, and_45_out);
  or b (b_out, and_46_out, and_47_out);
  or n (n_out, and_48_out, and_49_out);
  or m_2 (m_2_out, and_50_out, and_51_out);
  and and_53 (and_53_out, not_169_out, not_170_out, not_171_out, niiio[3], not_172_out, not_173_out, not_174_out);
  assign out_4 = and_53_out ? 8'h1b : 8'bz;  // Controlled_Buffer controlled_buffer_1
  assign out_4 = k_3_out ? 8'h1a : 8'bz;  // Controlled_Buffer controlled_buffer_2
  assign out_4 = a_out ? 8'h1 : 8'bz;  // Controlled_Buffer controlled_buffer_3
  assign out_4 = q_out ? 8'he : 8'bz;  // Controlled_Buffer controlled_buffer_4
  assign out_4 = w_out ? 8'hf : 8'bz;  // Controlled_Buffer controlled_buffer_5
  assign out_4 = e_out ? 8'h10 : 8'bz;  // Controlled_Buffer controlled_buffer_6
  assign out_4 = r_out ? 8'h11 : 8'bz;  // Controlled_Buffer controlled_buffer_7
  assign out_4 = t_out ? 8'h12 : 8'bz;  // Controlled_Buffer controlled_buffer_8
  assign out_4 = y_out ? 8'h4 : 8'bz;  // Controlled_Buffer controlled_buffer_9
  assign out_4 = u_out ? 8'h13 : 8'bz;  // Controlled_Buffer controlled_buffer_10
  assign out_4 = i_out ? 8'h14 : 8'bz;  // Controlled_Buffer controlled_buffer_11
  assign out_4 = o_out ? 8'h15 : 8'bz;  // Controlled_Buffer controlled_buffer_12
  assign out_4 = p_out ? 8'h16 : 8'bz;  // Controlled_Buffer controlled_buffer_13
  assign out_4 = s_out ? 8'hd : 8'bz;  // Controlled_Buffer controlled_buffer_14
  assign out_4 = d_out ? 8'h9 : 8'bz;  // Controlled_Buffer controlled_buffer_15
  assign out_4 = f_out ? 8'h6 : 8'bz;  // Controlled_Buffer controlled_buffer_16
  assign out_4 = g_out ? 8'h5 : 8'bz;  // Controlled_Buffer controlled_buffer_17
  assign out_4 = h_out ? 8'h7 : 8'bz;  // Controlled_Buffer controlled_buffer_18
  assign out_4 = j_out ? 8'h18 : 8'bz;  // Controlled_Buffer controlled_buffer_19
  assign out_4 = l_out ? 8'ha : 8'bz;  // Controlled_Buffer controlled_buffer_20
  assign out_4 = z_out ? 8'hc : 8'bz;  // Controlled_Buffer controlled_buffer_21
  assign out_4 = x_out ? 8'hb : 8'bz;  // Controlled_Buffer controlled_buffer_22
  assign out_4 = c_out ? 8'h8 : 8'bz;  // Controlled_Buffer controlled_buffer_23
  assign out_4 = v_out ? 8'h17 : 8'bz;  // Controlled_Buffer controlled_buffer_24
  assign out_4 = b_out ? 8'h3 : 8'bz;  // Controlled_Buffer controlled_buffer_25
  assign out_4 = n_out ? 8'h19 : 8'bz;  // Controlled_Buffer controlled_buffer_26
  assign out_4 = m_2_out ? 8'h2 : 8'bz;  // Controlled_Buffer controlled_buffer_27
  assign out_4 = out_5 ? {8{1'b0}} : 8'bz;  // Controlled_Buffer controlled_buffer_28

  // Other names for the same wires on the sheet: e[7:0] = out_4
endmodule

module K (
  input  in_1,
  output [7:0] out_2,
  output [7:0] out_3,
  output [7:0] out_4,
  output [7:0] out_5,
  output [7:0] out_6
);

  wire not_1_out, not_2_out, not_3_out, not_4_out, not_5_out;

  assign out_2 = in_1 ? 8'h7c : 8'bz;  // Controlled_Buffer controlled_buffer_1
  assign out_3 = in_1 ? 8'h10 : 8'bz;  // Controlled_Buffer controlled_buffer_2
  assign out_2 = not_1_out ? {8{1'b0}} : 8'bz;  // Controlled_Buffer controlled_buffer_3
  not not_1 (not_1_out, in_1);
  assign out_3 = not_2_out ? {8{1'b0}} : 8'bz;  // Controlled_Buffer controlled_buffer_4
  assign out_4 = in_1 ? 8'h28 : 8'bz;  // Controlled_Buffer controlled_buffer_5
  not not_2 (not_2_out, in_1);
  assign out_4 = not_3_out ? {8{1'b0}} : 8'bz;  // Controlled_Buffer controlled_buffer_6
  assign out_5 = in_1 ? 8'h44 : 8'bz;  // Controlled_Buffer controlled_buffer_7
  not not_3 (not_3_out, in_1);
  assign out_5 = not_4_out ? {8{1'b0}} : 8'bz;  // Controlled_Buffer controlled_buffer_8
  assign out_6 = in_1 ? {8{1'b0}} : 8'bz;  // Controlled_Buffer controlled_buffer_9
  not not_4 (not_4_out, in_1);
  assign out_6 = not_5_out ? {8{1'b0}} : 8'bz;  // Controlled_Buffer controlled_buffer_10
  not not_5 (not_5_out, in_1);
endmodule

module A (
  input  in_1,
  output [7:0] out_2,
  output [7:0] out_3,
  output [7:0] out_4,
  output [7:0] out_5,
  output [7:0] out_6
);

  wire not_1_out, not_2_out, not_3_out, not_4_out, not_5_out;

  assign out_2 = in_1 ? {8{1'b0}} : 8'bz;  // Controlled_Buffer controlled_buffer_1
  assign out_2 = not_1_out ? {8{1'b0}} : 8'bz;  // Controlled_Buffer controlled_buffer_2
  assign out_3 = in_1 ? 8'h3e : 8'bz;  // Controlled_Buffer controlled_buffer_3
  not not_1 (not_1_out, in_1);
  assign out_3 = not_2_out ? {8{1'b0}} : 8'bz;  // Controlled_Buffer controlled_buffer_4
  assign out_4 = in_1 ? 8'h50 : 8'bz;  // Controlled_Buffer controlled_buffer_5
  not not_2 (not_2_out, in_1);
  assign out_5 = in_1 ? 8'h3e : 8'bz;  // Controlled_Buffer controlled_buffer_6
  assign out_4 = not_3_out ? {8{1'b0}} : 8'bz;  // Controlled_Buffer controlled_buffer_7
  not not_3 (not_3_out, in_1);
  assign out_5 = not_4_out ? {8{1'b0}} : 8'bz;  // Controlled_Buffer controlled_buffer_8
  assign out_6 = in_1 ? {8{1'b0}} : 8'bz;  // Controlled_Buffer controlled_buffer_9
  not not_4 (not_4_out, in_1);
  assign out_6 = not_5_out ? {8{1'b0}} : 8'bz;  // Controlled_Buffer controlled_buffer_10
  not not_5 (not_5_out, in_1);
endmodule

module M (
  input  in_1,
  output [7:0] out_2,
  output [7:0] out_3,
  output [7:0] out_4,
  output [7:0] out_5,
  output [7:0] out_6
);

  wire not_1_out, not_2_out, not_3_out, not_4_out, not_5_out;

  assign out_2 = in_1 ? 8'h7e : 8'bz;  // Controlled_Buffer controlled_buffer_1
  assign out_3 = in_1 ? 8'h20 : 8'bz;  // Controlled_Buffer controlled_buffer_2
  assign out_2 = not_1_out ? {8{1'b0}} : 8'bz;  // Controlled_Buffer controlled_buffer_3
  not not_1 (not_1_out, in_1);
  assign out_4 = in_1 ? 8'h10 : 8'bz;  // Controlled_Buffer controlled_buffer_4
  assign out_3 = not_2_out ? {8{1'b0}} : 8'bz;  // Controlled_Buffer controlled_buffer_5
  not not_2 (not_2_out, in_1);
  assign out_5 = in_1 ? 8'h20 : 8'bz;  // Controlled_Buffer controlled_buffer_6
  assign out_4 = not_3_out ? {8{1'b0}} : 8'bz;  // Controlled_Buffer controlled_buffer_7
  not not_3 (not_3_out, in_1);
  assign out_5 = not_4_out ? {8{1'b0}} : 8'bz;  // Controlled_Buffer controlled_buffer_8
  assign out_6 = in_1 ? 8'h7e : 8'bz;  // Controlled_Buffer controlled_buffer_9
  not not_4 (not_4_out, in_1);
  assign out_6 = not_5_out ? {8{1'b0}} : 8'bz;  // Controlled_Buffer controlled_buffer_10
  not not_5 (not_5_out, in_1);
endmodule

module B (
  input  in_1,
  output [7:0] out_2,
  output [7:0] out_3,
  output [7:0] out_4,
  output [7:0] out_5,
  output [7:0] out_6
);

  wire not_1_out, not_2_out, not_3_out, not_4_out, not_5_out;

  assign out_2 = in_1 ? 8'h7e : 8'bz;  // Controlled_Buffer controlled_buffer_1
  assign out_2 = not_1_out ? {8{1'b0}} : 8'bz;  // Controlled_Buffer controlled_buffer_2
  assign out_3 = in_1 ? 8'h52 : 8'bz;  // Controlled_Buffer controlled_buffer_3
  not not_1 (not_1_out, in_1);
  assign out_3 = not_2_out ? {8{1'b0}} : 8'bz;  // Controlled_Buffer controlled_buffer_4
  assign out_4 = in_1 ? 8'h52 : 8'bz;  // Controlled_Buffer controlled_buffer_5
  not not_2 (not_2_out, in_1);
  assign out_4 = not_3_out ? {8{1'b0}} : 8'bz;  // Controlled_Buffer controlled_buffer_6
  assign out_5 = in_1 ? 8'h52 : 8'bz;  // Controlled_Buffer controlled_buffer_7
  not not_3 (not_3_out, in_1);
  assign out_5 = not_4_out ? {8{1'b0}} : 8'bz;  // Controlled_Buffer controlled_buffer_8
  assign out_6 = in_1 ? 8'h2c : 8'bz;  // Controlled_Buffer controlled_buffer_9
  not not_4 (not_4_out, in_1);
  assign out_6 = not_5_out ? {8{1'b0}} : 8'bz;  // Controlled_Buffer controlled_buffer_10
  not not_5 (not_5_out, in_1);
endmodule

module Y (
  input  in_1,
  output [7:0] out_2,
  output [7:0] out_3,
  output [7:0] out_4,
  output [7:0] out_5,
  output [7:0] out_6
);

  wire not_1_out, not_2_out, not_3_out, not_4_out, not_5_out;

  assign out_2 = in_1 ? 8'h60 : 8'bz;  // Controlled_Buffer controlled_buffer_1
  assign out_3 = in_1 ? 8'h30 : 8'bz;  // Controlled_Buffer controlled_buffer_2
  assign out_2 = not_1_out ? {8{1'b0}} : 8'bz;  // Controlled_Buffer controlled_buffer_3
  not not_1 (not_1_out, in_1);
  assign out_4 = in_1 ? 8'h1e : 8'bz;  // Controlled_Buffer controlled_buffer_4
  assign out_3 = not_2_out ? {8{1'b0}} : 8'bz;  // Controlled_Buffer controlled_buffer_5
  not not_2 (not_2_out, in_1);
  assign out_5 = in_1 ? 8'h30 : 8'bz;  // Controlled_Buffer controlled_buffer_6
  assign out_4 = not_3_out ? {8{1'b0}} : 8'bz;  // Controlled_Buffer controlled_buffer_7
  not not_3 (not_3_out, in_1);
  assign out_6 = in_1 ? 8'h60 : 8'bz;  // Controlled_Buffer controlled_buffer_8
  assign out_5 = not_4_out ? {8{1'b0}} : 8'bz;  // Controlled_Buffer controlled_buffer_9
  not not_4 (not_4_out, in_1);
  assign out_6 = not_5_out ? {8{1'b0}} : 8'bz;  // Controlled_Buffer controlled_buffer_10
  not not_5 (not_5_out, in_1);
endmodule

module C (
  input  in_1,
  output [7:0] out_2,
  output [7:0] out_3,
  output [7:0] out_4,
  output [7:0] out_5,
  output [7:0] out_6
);

  wire not_1_out, not_2_out, not_3_out, not_4_out, not_5_out;

  assign out_2 = in_1 ? 8'h3c : 8'bz;  // Controlled_Buffer controlled_buffer_1
  assign out_2 = not_1_out ? {8{1'b0}} : 8'bz;  // Controlled_Buffer controlled_buffer_2
  assign out_3 = in_1 ? 8'h66 : 8'bz;  // Controlled_Buffer controlled_buffer_3
  not not_1 (not_1_out, in_1);
  assign out_3 = not_2_out ? {8{1'b0}} : 8'bz;  // Controlled_Buffer controlled_buffer_4
  assign out_4 = in_1 ? 8'h42 : 8'bz;  // Controlled_Buffer controlled_buffer_5
  not not_2 (not_2_out, in_1);
  assign out_4 = not_3_out ? {8{1'b0}} : 8'bz;  // Controlled_Buffer controlled_buffer_6
  assign out_5 = in_1 ? 8'h42 : 8'bz;  // Controlled_Buffer controlled_buffer_7
  not not_3 (not_3_out, in_1);
  assign out_6 = in_1 ? 8'h24 : 8'bz;  // Controlled_Buffer controlled_buffer_8
  assign out_5 = not_4_out ? {8{1'b0}} : 8'bz;  // Controlled_Buffer controlled_buffer_9
  not not_4 (not_4_out, in_1);
  assign out_6 = not_5_out ? {8{1'b0}} : 8'bz;  // Controlled_Buffer controlled_buffer_10
  not not_5 (not_5_out, in_1);
endmodule

module X (
  input  in_1,
  output [7:0] out_2,
  output [7:0] out_3,
  output [7:0] out_4,
  output [7:0] out_5,
  output [7:0] out_6
);

  wire not_1_out, not_2_out, not_3_out, not_4_out, not_5_out;

  assign out_2 = in_1 ? 8'h44 : 8'bz;  // Controlled_Buffer controlled_buffer_1
  assign out_3 = in_1 ? 8'h28 : 8'bz;  // Controlled_Buffer controlled_buffer_2
  assign out_2 = not_1_out ? {8{1'b0}} : 8'bz;  // Controlled_Buffer controlled_buffer_3
  not not_1 (not_1_out, in_1);
  assign out_4 = in_1 ? 8'h10 : 8'bz;  // Controlled_Buffer controlled_buffer_4
  assign out_3 = not_2_out ? {8{1'b0}} : 8'bz;  // Controlled_Buffer controlled_buffer_5
  not not_2 (not_2_out, in_1);
  assign out_4 = not_3_out ? {8{1'b0}} : 8'bz;  // Controlled_Buffer controlled_buffer_6
  assign out_5 = in_1 ? 8'h28 : 8'bz;  // Controlled_Buffer controlled_buffer_7
  not not_3 (not_3_out, in_1);
  assign out_5 = not_4_out ? {8{1'b0}} : 8'bz;  // Controlled_Buffer controlled_buffer_8
  assign out_6 = in_1 ? 8'h44 : 8'bz;  // Controlled_Buffer controlled_buffer_9
  not not_4 (not_4_out, in_1);
  assign out_6 = not_5_out ? {8{1'b0}} : 8'bz;  // Controlled_Buffer controlled_buffer_10
  not not_5 (not_5_out, in_1);
endmodule

module Z (
  input  in_1,
  output [7:0] out_2,
  output [7:0] out_3,
  output [7:0] out_4,
  output [7:0] out_5,
  output [7:0] out_6
);

  wire not_1_out, not_2_out, not_3_out, not_4_out, not_5_out;

  assign out_2 = in_1 ? 8'h46 : 8'bz;  // Controlled_Buffer controlled_buffer_1
  assign out_2 = not_1_out ? {8{1'b0}} : 8'bz;  // Controlled_Buffer controlled_buffer_2
  assign out_3 = in_1 ? 8'h4e : 8'bz;  // Controlled_Buffer controlled_buffer_3
  not not_1 (not_1_out, in_1);
  assign out_3 = not_2_out ? {8{1'b0}} : 8'bz;  // Controlled_Buffer controlled_buffer_4
  assign out_4 = in_1 ? 8'h5a : 8'bz;  // Controlled_Buffer controlled_buffer_5
  not not_2 (not_2_out, in_1);
  assign out_5 = in_1 ? 8'h72 : 8'bz;  // Controlled_Buffer controlled_buffer_6
  assign out_4 = not_3_out ? {8{1'b0}} : 8'bz;  // Controlled_Buffer controlled_buffer_7
  not not_3 (not_3_out, in_1);
  assign out_5 = not_4_out ? {8{1'b0}} : 8'bz;  // Controlled_Buffer controlled_buffer_8
  assign out_6 = in_1 ? 8'h62 : 8'bz;  // Controlled_Buffer controlled_buffer_9
  not not_4 (not_4_out, in_1);
  assign out_6 = not_5_out ? {8{1'b0}} : 8'bz;  // Controlled_Buffer controlled_buffer_10
  not not_5 (not_5_out, in_1);
endmodule

module L (
  input  in_1,
  output [7:0] out_2,
  output [7:0] out_3,
  output [7:0] out_4,
  output [7:0] out_5,
  output [7:0] out_6
);

  wire not_1_out, not_2_out, not_3_out, not_4_out, not_5_out;

  assign out_2 = in_1 ? 8'h7e : 8'bz;  // Controlled_Buffer controlled_buffer_1
  assign out_3 = in_1 ? 8'h2 : 8'bz;  // Controlled_Buffer controlled_buffer_2
  assign out_2 = not_1_out ? {8{1'b0}} : 8'bz;  // Controlled_Buffer controlled_buffer_3
  not not_1 (not_1_out, in_1);
  assign out_4 = in_1 ? 8'h2 : 8'bz;  // Controlled_Buffer controlled_buffer_4
  assign out_3 = not_2_out ? {8{1'b0}} : 8'bz;  // Controlled_Buffer controlled_buffer_5
  not not_2 (not_2_out, in_1);
  assign out_5 = in_1 ? 8'h2 : 8'bz;  // Controlled_Buffer controlled_buffer_6
  assign out_4 = not_3_out ? {8{1'b0}} : 8'bz;  // Controlled_Buffer controlled_buffer_7
  not not_3 (not_3_out, in_1);
  assign out_5 = not_4_out ? {8{1'b0}} : 8'bz;  // Controlled_Buffer controlled_buffer_8
  assign out_6 = in_1 ? {8{1'b0}} : 8'bz;  // Controlled_Buffer controlled_buffer_9
  not not_4 (not_4_out, in_1);
  assign out_6 = not_5_out ? {8{1'b0}} : 8'bz;  // Controlled_Buffer controlled_buffer_10
  not not_5 (not_5_out, in_1);
endmodule

module H (
  input  in_1,
  output [7:0] out_2,
  output [7:0] out_3,
  output [7:0] out_4,
  output [7:0] out_5,
  output [7:0] out_6
);

  wire not_1_out, not_2_out, not_3_out, not_4_out, not_5_out;

  assign out_2 = in_1 ? {8{1'b0}} : 8'bz;  // Controlled_Buffer controlled_buffer_1
  assign out_2 = not_1_out ? {8{1'b0}} : 8'bz;  // Controlled_Buffer controlled_buffer_2
  assign out_3 = in_1 ? 8'h7c : 8'bz;  // Controlled_Buffer controlled_buffer_3
  not not_1 (not_1_out, in_1);
  assign out_4 = in_1 ? 8'h10 : 8'bz;  // Controlled_Buffer controlled_buffer_4
  assign out_3 = not_2_out ? {8{1'b0}} : 8'bz;  // Controlled_Buffer controlled_buffer_5
  not not_2 (not_2_out, in_1);
  assign out_4 = not_3_out ? {8{1'b0}} : 8'bz;  // Controlled_Buffer controlled_buffer_6
  assign out_5 = in_1 ? 8'h7c : 8'bz;  // Controlled_Buffer controlled_buffer_7
  not not_3 (not_3_out, in_1);
  assign out_5 = not_4_out ? {8{1'b0}} : 8'bz;  // Controlled_Buffer controlled_buffer_8
  assign out_6 = in_1 ? {8{1'b0}} : 8'bz;  // Controlled_Buffer controlled_buffer_9
  not not_4 (not_4_out, in_1);
  assign out_6 = not_5_out ? {8{1'b0}} : 8'bz;  // Controlled_Buffer controlled_buffer_10
  not not_5 (not_5_out, in_1);
endmodule

module R (
  input  in_1,
  output [7:0] out_2,
  output [7:0] out_3,
  output [7:0] out_4,
  output [7:0] out_5,
  output [7:0] out_6
);

  wire not_1_out, not_2_out, not_3_out, not_4_out, not_5_out;

  assign out_2 = in_1 ? 8'hfe : 8'bz;  // Controlled_Buffer controlled_buffer_1
  assign out_2 = not_1_out ? {8{1'b0}} : 8'bz;  // Controlled_Buffer controlled_buffer_2
  assign out_3 = in_1 ? 8'h98 : 8'bz;  // Controlled_Buffer controlled_buffer_3
  not not_1 (not_1_out, in_1);
  assign out_4 = in_1 ? 8'h9c : 8'bz;  // Controlled_Buffer controlled_buffer_4
  assign out_3 = not_2_out ? {8{1'b0}} : 8'bz;  // Controlled_Buffer controlled_buffer_5
  not not_2 (not_2_out, in_1);
  assign out_5 = in_1 ? 8'hf6 : 8'bz;  // Controlled_Buffer controlled_buffer_6
  assign out_4 = not_3_out ? {8{1'b0}} : 8'bz;  // Controlled_Buffer controlled_buffer_7
  not not_3 (not_3_out, in_1);
  assign out_5 = not_4_out ? {8{1'b0}} : 8'bz;  // Controlled_Buffer controlled_buffer_8
  assign out_6 = in_1 ? {8{1'b0}} : 8'bz;  // Controlled_Buffer controlled_buffer_9
  not not_4 (not_4_out, in_1);
  assign out_6 = not_5_out ? {8{1'b0}} : 8'bz;  // Controlled_Buffer controlled_buffer_10
  not not_5 (not_5_out, in_1);
endmodule

module G (
  input  in_1,
  output [7:0] out_2,
  output [7:0] out_3,
  output [7:0] out_4,
  output [7:0] out_5,
  output [7:0] out_6
);

  wire not_1_out, not_2_out, not_3_out, not_4_out, not_5_out;

  assign out_2 = in_1 ? 8'h3c : 8'bz;  // Controlled_Buffer controlled_buffer_1
  assign out_2 = not_1_out ? {8{1'b0}} : 8'bz;  // Controlled_Buffer controlled_buffer_2
  assign out_3 = in_1 ? 8'h42 : 8'bz;  // Controlled_Buffer controlled_buffer_3
  not not_1 (not_1_out, in_1);
  assign out_4 = in_1 ? 8'h42 : 8'bz;  // Controlled_Buffer controlled_buffer_4
  assign out_3 = not_2_out ? {8{1'b0}} : 8'bz;  // Controlled_Buffer controlled_buffer_5
  not not_2 (not_2_out, in_1);
  assign out_5 = in_1 ? 8'h4a : 8'bz;  // Controlled_Buffer controlled_buffer_6
  assign out_4 = not_3_out ? {8{1'b0}} : 8'bz;  // Controlled_Buffer controlled_buffer_7
  not not_3 (not_3_out, in_1);
  assign out_6 = in_1 ? 8'h2e : 8'bz;  // Controlled_Buffer controlled_buffer_8
  assign out_5 = not_4_out ? {8{1'b0}} : 8'bz;  // Controlled_Buffer controlled_buffer_9
  not not_4 (not_4_out, in_1);
  assign out_6 = not_5_out ? {8{1'b0}} : 8'bz;  // Controlled_Buffer controlled_buffer_10
  not not_5 (not_5_out, in_1);
endmodule

module F (
  input  in_1,
  output [7:0] out_2,
  output [7:0] out_3,
  output [7:0] out_4,
  output [7:0] out_5,
  output [7:0] out_6
);

  wire not_1_out, not_2_out, not_3_out, not_4_out, not_5_out;

  assign out_2 = in_1 ? 8'h7e : 8'bz;  // Controlled_Buffer controlled_buffer_1
  assign out_2 = not_1_out ? {8{1'b0}} : 8'bz;  // Controlled_Buffer controlled_buffer_2
  assign out_3 = in_1 ? 8'h50 : 8'bz;  // Controlled_Buffer controlled_buffer_3
  not not_1 (not_1_out, in_1);
  assign out_3 = not_2_out ? {8{1'b0}} : 8'bz;  // Controlled_Buffer controlled_buffer_4
  assign out_4 = in_1 ? 8'h50 : 8'bz;  // Controlled_Buffer controlled_buffer_5
  not not_2 (not_2_out, in_1);
  assign out_4 = not_3_out ? {8{1'b0}} : 8'bz;  // Controlled_Buffer controlled_buffer_6
  assign out_5 = in_1 ? 8'h40 : 8'bz;  // Controlled_Buffer controlled_buffer_7
  not not_3 (not_3_out, in_1);
  assign out_6 = in_1 ? {8{1'b0}} : 8'bz;  // Controlled_Buffer controlled_buffer_8
  assign out_5 = not_4_out ? {8{1'b0}} : 8'bz;  // Controlled_Buffer controlled_buffer_9
  not not_4 (not_4_out, in_1);
  assign out_6 = not_5_out ? {8{1'b0}} : 8'bz;  // Controlled_Buffer controlled_buffer_10
  not not_5 (not_5_out, in_1);
endmodule

module D (
  input  in_1,
  output [7:0] out_2,
  output [7:0] out_3,
  output [7:0] out_4,
  output [7:0] out_5,
  output [7:0] out_6
);

  wire not_1_out, not_2_out, not_3_out, not_4_out, not_5_out;

  assign out_2 = in_1 ? 8'h7e : 8'bz;  // Controlled_Buffer controlled_buffer_1
  assign out_2 = not_1_out ? {8{1'b0}} : 8'bz;  // Controlled_Buffer controlled_buffer_2
  assign out_3 = in_1 ? 8'h42 : 8'bz;  // Controlled_Buffer controlled_buffer_3
  not not_1 (not_1_out, in_1);
  assign out_3 = not_2_out ? {8{1'b0}} : 8'bz;  // Controlled_Buffer controlled_buffer_4
  assign out_4 = in_1 ? 8'h42 : 8'bz;  // Controlled_Buffer controlled_buffer_5
  not not_2 (not_2_out, in_1);
  assign out_4 = not_3_out ? {8{1'b0}} : 8'bz;  // Controlled_Buffer controlled_buffer_6
  assign out_5 = in_1 ? 8'h3c : 8'bz;  // Controlled_Buffer controlled_buffer_7
  not not_3 (not_3_out, in_1);
  assign out_5 = not_4_out ? {8{1'b0}} : 8'bz;  // Controlled_Buffer controlled_buffer_8
  assign out_6 = in_1 ? {8{1'b0}} : 8'bz;  // Controlled_Buffer controlled_buffer_9
  not not_4 (not_4_out, in_1);
  assign out_6 = not_5_out ? {8{1'b0}} : 8'bz;  // Controlled_Buffer controlled_buffer_10
  not not_5 (not_5_out, in_1);
endmodule

module W (
  input  in_1,
  output [7:0] out_2,
  output [7:0] out_3,
  output [7:0] out_4,
  output [7:0] out_5,
  output [7:0] out_6
);

  wire not_1_out, not_2_out, not_3_out, not_4_out, not_5_out;

  assign out_2 = in_1 ? 8'h10 : 8'bz;  // Controlled_Buffer controlled_buffer_1
  assign out_2 = not_1_out ? {8{1'b0}} : 8'bz;  // Controlled_Buffer controlled_buffer_2
  assign out_3 = in_1 ? 8'h4 : 8'bz;  // Controlled_Buffer controlled_buffer_3
  not not_1 (not_1_out, in_1);
  assign out_4 = in_1 ? 8'h10 : 8'bz;  // Controlled_Buffer controlled_buffer_4
  assign out_3 = not_2_out ? {8{1'b0}} : 8'bz;  // Controlled_Buffer controlled_buffer_5
  not not_2 (not_2_out, in_1);
  assign out_5 = in_1 ? 8'h4 : 8'bz;  // Controlled_Buffer controlled_buffer_6
  assign out_4 = not_3_out ? {8{1'b0}} : 8'bz;  // Controlled_Buffer controlled_buffer_7
  not not_3 (not_3_out, in_1);
  assign out_5 = not_4_out ? {8{1'b0}} : 8'bz;  // Controlled_Buffer controlled_buffer_8
  assign out_6 = in_1 ? 8'h10 : 8'bz;  // Controlled_Buffer controlled_buffer_9
  not not_4 (not_4_out, in_1);
  assign out_6 = not_5_out ? {8{1'b0}} : 8'bz;  // Controlled_Buffer controlled_buffer_10
  not not_5 (not_5_out, in_1);
endmodule

module E (
  input  in_1,
  output [7:0] out_2,
  output [7:0] out_3,
  output [7:0] out_4,
  output [7:0] out_5,
  output [7:0] out_6
);

  wire not_1_out, not_2_out, not_3_out, not_4_out, not_5_out;

  assign out_2 = in_1 ? 8'h7e : 8'bz;  // Controlled_Buffer controlled_buffer_1
  assign out_2 = not_1_out ? {8{1'b0}} : 8'bz;  // Controlled_Buffer controlled_buffer_2
  assign out_3 = in_1 ? 8'h52 : 8'bz;  // Controlled_Buffer controlled_buffer_3
  not not_1 (not_1_out, in_1);
  assign out_4 = in_1 ? 8'h52 : 8'bz;  // Controlled_Buffer controlled_buffer_4
  assign out_3 = not_2_out ? {8{1'b0}} : 8'bz;  // Controlled_Buffer controlled_buffer_5
  not not_2 (not_2_out, in_1);
  assign out_5 = in_1 ? 8'h52 : 8'bz;  // Controlled_Buffer controlled_buffer_6
  assign out_4 = not_3_out ? {8{1'b0}} : 8'bz;  // Controlled_Buffer controlled_buffer_7
  not not_3 (not_3_out, in_1);
  assign out_6 = in_1 ? {8{1'b0}} : 8'bz;  // Controlled_Buffer controlled_buffer_8
  assign out_5 = not_4_out ? {8{1'b0}} : 8'bz;  // Controlled_Buffer controlled_buffer_9
  not not_4 (not_4_out, in_1);
  assign out_6 = not_5_out ? {8{1'b0}} : 8'bz;  // Controlled_Buffer controlled_buffer_10
  not not_5 (not_5_out, in_1);
endmodule

module T (
  input  in_1,
  output [7:0] out_2,
  output [7:0] out_3,
  output [7:0] out_4,
  output [7:0] out_5,
  output [7:0] out_6
);

  wire not_1_out, not_2_out, not_3_out, not_4_out, not_5_out;

  assign out_2 = in_1 ? 8'h40 : 8'bz;  // Controlled_Buffer controlled_buffer_1
  assign out_3 = in_1 ? 8'h40 : 8'bz;  // Controlled_Buffer controlled_buffer_2
  assign out_2 = not_1_out ? {8{1'b0}} : 8'bz;  // Controlled_Buffer controlled_buffer_3
  not not_1 (not_1_out, in_1);
  assign out_3 = not_2_out ? {8{1'b0}} : 8'bz;  // Controlled_Buffer controlled_buffer_4
  assign out_4 = in_1 ? 8'h7e : 8'bz;  // Controlled_Buffer controlled_buffer_5
  not not_2 (not_2_out, in_1);
  assign out_5 = in_1 ? 8'h40 : 8'bz;  // Controlled_Buffer controlled_buffer_6
  assign out_4 = not_3_out ? {8{1'b0}} : 8'bz;  // Controlled_Buffer controlled_buffer_7
  not not_3 (not_3_out, in_1);
  assign out_6 = in_1 ? 8'h40 : 8'bz;  // Controlled_Buffer controlled_buffer_8
  assign out_5 = not_4_out ? {8{1'b0}} : 8'bz;  // Controlled_Buffer controlled_buffer_9
  not not_4 (not_4_out, in_1);
  assign out_6 = not_5_out ? {8{1'b0}} : 8'bz;  // Controlled_Buffer controlled_buffer_10
  not not_5 (not_5_out, in_1);
endmodule

module O (
  input  in_1,
  output [7:0] out_2,
  output [7:0] out_3,
  output [7:0] out_4,
  output [7:0] out_5,
  output [7:0] out_6
);

  wire not_1_out, not_2_out, not_3_out, not_4_out, not_5_out;

  assign out_2 = in_1 ? 8'h3c : 8'bz;  // Controlled_Buffer controlled_buffer_1
  assign out_3 = in_1 ? 8'h42 : 8'bz;  // Controlled_Buffer controlled_buffer_2
  assign out_2 = not_1_out ? {8{1'b0}} : 8'bz;  // Controlled_Buffer controlled_buffer_3
  not not_1 (not_1_out, in_1);
  assign out_4 = in_1 ? 8'h42 : 8'bz;  // Controlled_Buffer controlled_buffer_4
  assign out_3 = not_2_out ? {8{1'b0}} : 8'bz;  // Controlled_Buffer controlled_buffer_5
  not not_2 (not_2_out, in_1);
  assign out_4 = not_3_out ? {8{1'b0}} : 8'bz;  // Controlled_Buffer controlled_buffer_6
  assign out_5 = in_1 ? 8'h42 : 8'bz;  // Controlled_Buffer controlled_buffer_7
  not not_3 (not_3_out, in_1);
  assign out_5 = not_4_out ? {8{1'b0}} : 8'bz;  // Controlled_Buffer controlled_buffer_8
  assign out_6 = in_1 ? 8'h3c : 8'bz;  // Controlled_Buffer controlled_buffer_9
  not not_4 (not_4_out, in_1);
  assign out_6 = not_5_out ? {8{1'b0}} : 8'bz;  // Controlled_Buffer controlled_buffer_10
  not not_5 (not_5_out, in_1);
endmodule

module U (
  input  in_1,
  output [7:0] out_2,
  output [7:0] out_3,
  output [7:0] out_4,
  output [7:0] out_5,
  output [7:0] out_6
);

  wire not_1_out, not_2_out, not_3_out, not_4_out, not_5_out;

  assign out_2 = in_1 ? 8'h7c : 8'bz;  // Controlled_Buffer controlled_buffer_1
  assign out_3 = in_1 ? 8'h2 : 8'bz;  // Controlled_Buffer controlled_buffer_2
  assign out_2 = not_1_out ? {8{1'b0}} : 8'bz;  // Controlled_Buffer controlled_buffer_3
  not not_1 (not_1_out, in_1);
  assign out_4 = in_1 ? 8'h2 : 8'bz;  // Controlled_Buffer controlled_buffer_4
  assign out_3 = not_2_out ? {8{1'b0}} : 8'bz;  // Controlled_Buffer controlled_buffer_5
  not not_2 (not_2_out, in_1);
  assign out_4 = not_3_out ? {8{1'b0}} : 8'bz;  // Controlled_Buffer controlled_buffer_6
  assign out_5 = in_1 ? 8'h2 : 8'bz;  // Controlled_Buffer controlled_buffer_7
  not not_3 (not_3_out, in_1);
  assign out_6 = in_1 ? 8'h7c : 8'bz;  // Controlled_Buffer controlled_buffer_8
  assign out_5 = not_4_out ? {8{1'b0}} : 8'bz;  // Controlled_Buffer controlled_buffer_9
  not not_4 (not_4_out, in_1);
  assign out_6 = not_5_out ? {8{1'b0}} : 8'bz;  // Controlled_Buffer controlled_buffer_10
  not not_5 (not_5_out, in_1);
endmodule

module I (
  input  in_1,
  output [7:0] out_2,
  output [7:0] out_3,
  output [7:0] out_4,
  output [7:0] out_5,
  output [7:0] out_6
);

  wire not_1_out, not_2_out, not_3_out, not_4_out, not_5_out;

  assign out_2 = in_1 ? {8{1'b0}} : 8'bz;  // Controlled_Buffer controlled_buffer_1
  assign out_2 = not_1_out ? {8{1'b0}} : 8'bz;  // Controlled_Buffer controlled_buffer_2
  assign out_3 = in_1 ? 8'h42 : 8'bz;  // Controlled_Buffer controlled_buffer_3
  not not_1 (not_1_out, in_1);
  assign out_4 = in_1 ? 8'h7e : 8'bz;  // Controlled_Buffer controlled_buffer_4
  assign out_3 = not_2_out ? {8{1'b0}} : 8'bz;  // Controlled_Buffer controlled_buffer_5
  not not_2 (not_2_out, in_1);
  assign out_4 = not_3_out ? {8{1'b0}} : 8'bz;  // Controlled_Buffer controlled_buffer_6
  assign out_5 = in_1 ? 8'h42 : 8'bz;  // Controlled_Buffer controlled_buffer_7
  not not_3 (not_3_out, in_1);
  assign out_5 = not_4_out ? {8{1'b0}} : 8'bz;  // Controlled_Buffer controlled_buffer_8
  assign out_6 = in_1 ? {8{1'b0}} : 8'bz;  // Controlled_Buffer controlled_buffer_9
  not not_4 (not_4_out, in_1);
  assign out_6 = not_5_out ? {8{1'b0}} : 8'bz;  // Controlled_Buffer controlled_buffer_10
  not not_5 (not_5_out, in_1);
endmodule

module P (
  input  in_1,
  output [7:0] out_2,
  output [7:0] out_3,
  output [7:0] out_4,
  output [7:0] out_5,
  output [7:0] out_6
);

  wire not_1_out, not_2_out, not_3_out, not_4_out, not_5_out;

  assign out_2 = in_1 ? 8'h7e : 8'bz;  // Controlled_Buffer controlled_buffer_1
  assign out_2 = not_1_out ? {8{1'b0}} : 8'bz;  // Controlled_Buffer controlled_buffer_2
  assign out_3 = in_1 ? 8'h48 : 8'bz;  // Controlled_Buffer controlled_buffer_3
  not not_1 (not_1_out, in_1);
  assign out_4 = in_1 ? 8'h48 : 8'bz;  // Controlled_Buffer controlled_buffer_4
  assign out_3 = not_2_out ? {8{1'b0}} : 8'bz;  // Controlled_Buffer controlled_buffer_5
  not not_2 (not_2_out, in_1);
  assign out_4 = not_3_out ? {8{1'b0}} : 8'bz;  // Controlled_Buffer controlled_buffer_6
  assign out_5 = in_1 ? 8'h78 : 8'bz;  // Controlled_Buffer controlled_buffer_7
  not not_3 (not_3_out, in_1);
  assign out_5 = not_4_out ? {8{1'b0}} : 8'bz;  // Controlled_Buffer controlled_buffer_8
  assign out_6 = in_1 ? {8{1'b0}} : 8'bz;  // Controlled_Buffer controlled_buffer_9
  not not_4 (not_4_out, in_1);
  assign out_6 = not_5_out ? {8{1'b0}} : 8'bz;  // Controlled_Buffer controlled_buffer_10
  not not_5 (not_5_out, in_1);
endmodule

module S (
  input  in_1,
  output [7:0] out_2,
  output [7:0] out_3,
  output [7:0] out_4,
  output [7:0] out_5,
  output [7:0] out_6
);

  wire not_1_out, not_2_out, not_3_out, not_4_out, not_5_out;

  assign out_2 = in_1 ? 8'h66 : 8'bz;  // Controlled_Buffer controlled_buffer_1
  assign out_2 = not_1_out ? {8{1'b0}} : 8'bz;  // Controlled_Buffer controlled_buffer_2
  assign out_3 = in_1 ? 8'h72 : 8'bz;  // Controlled_Buffer controlled_buffer_3
  not not_1 (not_1_out, in_1);
  assign out_3 = not_2_out ? {8{1'b0}} : 8'bz;  // Controlled_Buffer controlled_buffer_4
  assign out_4 = in_1 ? 8'h5a : 8'bz;  // Controlled_Buffer controlled_buffer_5
  not not_2 (not_2_out, in_1);
  assign out_4 = not_3_out ? {8{1'b0}} : 8'bz;  // Controlled_Buffer controlled_buffer_6
  assign out_5 = in_1 ? 8'h4e : 8'bz;  // Controlled_Buffer controlled_buffer_7
  not not_3 (not_3_out, in_1);
  assign out_5 = not_4_out ? {8{1'b0}} : 8'bz;  // Controlled_Buffer controlled_buffer_8
  assign out_6 = in_1 ? 8'h66 : 8'bz;  // Controlled_Buffer controlled_buffer_9
  not not_4 (not_4_out, in_1);
  assign out_6 = not_5_out ? {8{1'b0}} : 8'bz;  // Controlled_Buffer controlled_buffer_10
  not not_5 (not_5_out, in_1);
endmodule

module V (
  input  in_1,
  output [7:0] out_2,
  output [7:0] out_3,
  output [7:0] out_4,
  output [7:0] out_5,
  output [7:0] out_6
);

  wire not_1_out, not_2_out, not_3_out, not_4_out, not_5_out;

  assign out_2 = in_1 ? 8'h18 : 8'bz;  // Controlled_Buffer controlled_buffer_1
  assign out_3 = in_1 ? 8'hc : 8'bz;  // Controlled_Buffer controlled_buffer_2
  assign out_2 = not_1_out ? {8{1'b0}} : 8'bz;  // Controlled_Buffer controlled_buffer_3
  not not_1 (not_1_out, in_1);
  assign out_4 = in_1 ? 8'h6 : 8'bz;  // Controlled_Buffer controlled_buffer_4
  assign out_3 = not_2_out ? {8{1'b0}} : 8'bz;  // Controlled_Buffer controlled_buffer_5
  not not_2 (not_2_out, in_1);
  assign out_5 = in_1 ? 8'hc : 8'bz;  // Controlled_Buffer controlled_buffer_6
  assign out_4 = not_3_out ? {8{1'b0}} : 8'bz;  // Controlled_Buffer controlled_buffer_7
  not not_3 (not_3_out, in_1);
  assign out_5 = not_4_out ? {8{1'b0}} : 8'bz;  // Controlled_Buffer controlled_buffer_8
  assign out_6 = in_1 ? 8'h18 : 8'bz;  // Controlled_Buffer controlled_buffer_9
  not not_4 (not_4_out, in_1);
  assign out_6 = not_5_out ? {8{1'b0}} : 8'bz;  // Controlled_Buffer controlled_buffer_10
  not not_5 (not_5_out, in_1);
endmodule

module J (
  input  in_1,
  output [7:0] out_2,
  output [7:0] out_3,
  output [7:0] out_4,
  output [7:0] out_5,
  output [7:0] out_6
);

  wire not_1_out, not_2_out, not_3_out, not_4_out, not_5_out;

  assign out_2 = in_1 ? 8'h6 : 8'bz;  // Controlled_Buffer controlled_buffer_1
  assign out_2 = not_1_out ? {8{1'b0}} : 8'bz;  // Controlled_Buffer controlled_buffer_2
  assign out_3 = in_1 ? 8'h2 : 8'bz;  // Controlled_Buffer controlled_buffer_3
  not not_1 (not_1_out, in_1);
  assign out_4 = in_1 ? 8'h7e : 8'bz;  // Controlled_Buffer controlled_buffer_4
  assign out_3 = not_2_out ? {8{1'b0}} : 8'bz;  // Controlled_Buffer controlled_buffer_5
  not not_2 (not_2_out, in_1);
  assign out_4 = not_3_out ? {8{1'b0}} : 8'bz;  // Controlled_Buffer controlled_buffer_6
  assign out_5 = in_1 ? {8{1'b0}} : 8'bz;  // Controlled_Buffer controlled_buffer_7
  not not_3 (not_3_out, in_1);
  assign out_6 = in_1 ? {8{1'b0}} : 8'bz;  // Controlled_Buffer controlled_buffer_8
  assign out_5 = not_4_out ? {8{1'b0}} : 8'bz;  // Controlled_Buffer controlled_buffer_9
  not not_4 (not_4_out, in_1);
  assign out_6 = not_5_out ? {8{1'b0}} : 8'bz;  // Controlled_Buffer controlled_buffer_10
  not not_5 (not_5_out, in_1);
endmodule

module Q (
  input  in_1,
  output [7:0] out_2,
  output [7:0] out_3,
  output [7:0] out_4,
  output [7:0] out_5,
  output [7:0] out_6
);

  wire not_1_out, not_2_out, not_3_out, not_4_out, not_5_out;

  assign out_2 = in_1 ? {8{1'b0}} : 8'bz;  // Controlled_Buffer controlled_buffer_1
  assign out_2 = not_1_out ? {8{1'b0}} : 8'bz;  // Controlled_Buffer controlled_buffer_2
  assign out_3 = in_1 ? {8{1'b0}} : 8'bz;  // Controlled_Buffer controlled_buffer_3
  not not_1 (not_1_out, in_1);
  assign out_3 = not_2_out ? {8{1'b0}} : 8'bz;  // Controlled_Buffer controlled_buffer_4
  assign out_4 = in_1 ? 8'h70 : 8'bz;  // Controlled_Buffer controlled_buffer_5
  not not_2 (not_2_out, in_1);
  assign out_5 = in_1 ? 8'h50 : 8'bz;  // Controlled_Buffer controlled_buffer_6
  assign out_4 = not_3_out ? {8{1'b0}} : 8'bz;  // Controlled_Buffer controlled_buffer_7
  not not_3 (not_3_out, in_1);
  assign out_6 = in_1 ? 8'h7e : 8'bz;  // Controlled_Buffer controlled_buffer_8
  assign out_5 = not_4_out ? {8{1'b0}} : 8'bz;  // Controlled_Buffer controlled_buffer_9
  not not_4 (not_4_out, in_1);
  assign out_6 = not_5_out ? {8{1'b0}} : 8'bz;  // Controlled_Buffer controlled_buffer_10
  not not_5 (not_5_out, in_1);
endmodule

module N (
  input  in_1,
  output [7:0] out_2,
  output [7:0] out_3,
  output [7:0] out_4,
  output [7:0] out_5,
  output [7:0] out_6
);

  wire not_1_out, not_2_out, not_3_out, not_4_out, not_5_out;

  assign out_2 = in_1 ? 8'h3e : 8'bz;  // Controlled_Buffer controlled_buffer_1
  assign out_2 = not_1_out ? {8{1'b0}} : 8'bz;  // Controlled_Buffer controlled_buffer_2
  not not_1 (not_1_out, in_1);
  assign out_3 = not_2_out ? {8{1'b0}} : 8'bz;  // Controlled_Buffer controlled_buffer_3
  assign out_3 = in_1 ? 8'h10 : 8'bz;  // Controlled_Buffer controlled_buffer_4
  not not_2 (not_2_out, in_1);
  assign out_4 = not_3_out ? {8{1'b0}} : 8'bz;  // Controlled_Buffer controlled_buffer_5
  assign out_4 = in_1 ? 8'h8 : 8'bz;  // Controlled_Buffer controlled_buffer_6
  not not_3 (not_3_out, in_1);
  assign out_5 = in_1 ? 8'h4 : 8'bz;  // Controlled_Buffer controlled_buffer_7
  assign out_5 = not_4_out ? {8{1'b0}} : 8'bz;  // Controlled_Buffer controlled_buffer_8
  not not_4 (not_4_out, in_1);
  assign out_6 = not_5_out ? {8{1'b0}} : 8'bz;  // Controlled_Buffer controlled_buffer_9
  assign out_6 = in_1 ? 8'h3e : 8'bz;  // Controlled_Buffer controlled_buffer_10
  not not_5 (not_5_out, in_1);
endmodule
