// Logisim project niiio.circ as structural Verilog: 22 circuits, main circuit main
module main (
  input  in_1
);

  wire bol, clock_1_out, keyboard_1_avail, \reset_ή_παραδοση , start;
  wire [1:0] _1, _2, le_1_out_21, le_1_out_23, le_1_out_25, le_1_out_27;
  wire [3:0] teliko_1_out_47, teliko_1_out_48, teliko_1_out_49, teliko_1_out_50, teliko_1_out_92;
  wire [6:0] keyboard_1_data;
  wire [7:0] le_1_out_2, le_1_out_3, le_1_out_4, le_1_out_5, le_1_out_6, le_1_out_7, le_1_out_8, le_1_out_9,
       le_1_out_10, le_1_out_11, le_1_out_12, le_1_out_13, le_1_out_14, le_1_out_15, le_1_out_16,
       le_1_out_17, le_1_out_18, le_1_out_19, le_1_out_20, le_1_out_22, le_1_out_24, le_1_out_26,
       le_1_out_28, le_1_out_29, le_1_out_30, le_1_out_31, le_1_out_32, onoma_1_out_3, onoma_1_out_4,
       onoma_1_out_5, onoma_1_out_6, onoma_1_out_7, onoma_1_out_8, onoma_1_out_9, onoma_1_out_10,
       onoma_1_out_11, onoma_1_out_12, onoma_1_out_13, onoma_1_out_14, onoma_1_out_15, onoma_1_out_16,
       onoma_1_out_17, onoma_1_out_18, onoma_1_out_19, onoma_1_out_20, onoma_1_out_21, onoma_1_out_22,
       onoma_1_out_23, onoma_1_out_24, onoma_1_out_25, onoma_1_out_26, onoma_1_out_27, onoma_1_out_28,
       onoma_1_out_29, onoma_1_out_30, onoma_1_out_31, onoma_1_out_32, onoma_1_out_33, teliko_1_out_7,
       teliko_1_out_8, teliko_1_out_9, teliko_1_out_10, teliko_1_out_11, teliko_1_out_12, teliko_1_out_13,
       teliko_1_out_14, teliko_1_out_15, teliko_1_out_16, teliko_1_out_17, teliko_1_out_18, teliko_1_out_19,
       teliko_1_out_24, teliko_1_out_25, teliko_1_out_26, teliko_1_out_27, teliko_1_out_28, teliko_1_out_29,
       teliko_1_out_30, teliko_1_out_31, teliko_1_out_32, teliko_1_out_33, teliko_1_out_34, teliko_1_out_35,
       teliko_1_out_36, teliko_1_out_41, teliko_1_out_42, teliko_1_out_43, teliko_1_out_44, teliko_1_out_45,
       teliko_1_out_46, teliko_1_out_51, teliko_1_out_52, teliko_1_out_53, teliko_1_out_54, teliko_1_out_55,
       teliko_1_out_60, teliko_1_out_61, teliko_1_out_62, teliko_1_out_63, teliko_1_out_64, teliko_1_out_65,
       teliko_1_out_66, teliko_1_out_67, teliko_1_out_68, teliko_1_out_69, teliko_1_out_70, teliko_1_out_71,
       teliko_1_out_72, teliko_1_out_73, teliko_1_out_74, teliko_1_out_75, teliko_1_out_76, teliko_1_out_81,
       teliko_1_out_82, teliko_1_out_83, teliko_1_out_84, teliko_1_out_89, teliko_1_out_90, teliko_1_out_91,
       teliko_1_out_93, teliko_1_out_98, teliko_1_out_99, teliko_1_out_100, teliko_1_out_101,
       teliko_1_out_106, teliko_1_out_107, teliko_1_out_108, teliko_1_out_109, teliko_1_out_114,
       teliko_1_out_115, teliko_1_out_116, teliko_1_out_117, teliko_1_out_122, teliko_1_out_123,
       teliko_1_out_124, teliko_1_out_125, teliko_1_out_130, teliko_1_out_131, teliko_1_out_132,
       teliko_1_out_133, teliko_1_out_138;
  wire [31:0] teliko_1_out_20, teliko_1_out_21, teliko_1_out_22, teliko_1_out_23, teliko_1_out_37,
       teliko_1_out_38, teliko_1_out_39, teliko_1_out_40, teliko_1_out_56, teliko_1_out_57, teliko_1_out_58,
       teliko_1_out_59, teliko_1_out_77, teliko_1_out_78, teliko_1_out_79, teliko_1_out_80, teliko_1_out_85,
       teliko_1_out_86, teliko_1_out_87, teliko_1_out_88, teliko_1_out_94, teliko_1_out_95, teliko_1_out_96,
       teliko_1_out_97, teliko_1_out_102, teliko_1_out_103, teliko_1_out_104, teliko_1_out_105,
       teliko_1_out_110, teliko_1_out_111, teliko_1_out_112, teliko_1_out_113, teliko_1_out_118,
       teliko_1_out_119, teliko_1_out_120, teliko_1_out_121, teliko_1_out_126, teliko_1_out_127,
       teliko_1_out_128, teliko_1_out_129, teliko_1_out_134, teliko_1_out_135, teliko_1_out_136,
       teliko_1_out_137, teliko_1_out_139, teliko_1_out_140, teliko_1_out_141, teliko_1_out_142,
       teliko_1_out_143, teliko_1_out_144, teliko_1_out_145, teliko_1_out_146, teliko_1_out_147,
       teliko_1_out_148, teliko_1_out_149, teliko_1_out_150, teliko_1_out_151, teliko_1_out_152,
       teliko_1_out_153, teliko_1_out_154, teliko_1_out_155, teliko_1_out_156;

  Keyboard keyboard_1 (.clk(clock_1_out), .avail(keyboard_1_avail), .data(keyboard_1_data));  // open: re, clr
  Clock clock_1 (.out(clock_1_out));
  Button button_1 (.out(start));
  Button button_2 (.out(\reset_ή_παραδοση ));
  Joystick #(.bits(2)) joystick_1 (.x(_2), .y(_1));
  Button button_3 (.out(bol));
  onoma onoma_1 (
    .in_2(keyboard_1_avail), .in_1(keyboard_1_data), .out_28(onoma_1_out_28), .out_23(onoma_1_out_23),
    .out_18(onoma_1_out_18), .out_13(onoma_1_out_13), .out_8(onoma_1_out_8), .out_3(onoma_1_out_3),
    .out_29(onoma_1_out_29), .out_24(onoma_1_out_24), .out_19(onoma_1_out_19), .out_14(onoma_1_out_14),
    .out_9(onoma_1_out_9), .out_4(onoma_1_out_4), .out_30(onoma_1_out_30), .out_25(onoma_1_out_25),
    .out_20(onoma_1_out_20), .out_15(onoma_1_out_15), .out_10(onoma_1_out_10), .out_5(onoma_1_out_5),
    .out_31(onoma_1_out_31), .out_26(onoma_1_out_26), .out_21(onoma_1_out_21), .out_16(onoma_1_out_16),
    .out_11(onoma_1_out_11), .out_6(onoma_1_out_6), .out_32(onoma_1_out_32), .out_27(onoma_1_out_27),
    .out_22(onoma_1_out_22), .out_17(onoma_1_out_17), .out_12(onoma_1_out_12), .out_7(onoma_1_out_7),
    .out_33(onoma_1_out_33));
  DotMatrix #(.matrixcols(6), .matrixrows(17)) dotmatrix_1 (
    .col0({17{1'b0}}), .col1({17{1'b0}}), .col2({17{1'b0}}), .col3({17{1'b0}}), .col4({17{1'b0}}),
    .col5({17{1'b0}}));
  DotMatrix #(.matrixcols(13), .matrixrows(6)) dotmatrix_2 (
    .col0({6{1'b0}}), .col1({6{1'b0}}), .col2({6{1'b0}}), .col3({6{1'b0}}), .col4({6{1'b0}}),
    .col5({6{1'b0}}), .col6({6{1'b0}}), .col7({6{1'b0}}), .col8({6{1'b0}}), .col9({6{1'b0}}),
    .col10({6{1'b0}}), .col11({6{1'b0}}), .col12({6{1'b0}}));
  DotMatrix #(.matrixcols(13), .matrixrows(32)) dotmatrix_3 (
    .col0({32{1'b0}}), .col1({32{1'b0}}), .col2({32{1'b0}}), .col3({32{1'b0}}), .col4({32{1'b0}}),
    .col5({32{1'b0}}), .col6({32{1'b0}}), .col7({32{1'b0}}), .col8({32{1'b0}}), .col9({32{1'b0}}),
    .col10({32{1'b0}}), .col11({32{1'b0}}), .col12({32{1'b0}}));
  DotMatrix #(.matrixcols(13), .matrixrows(32)) dotmatrix_4 (
    .col0({32{1'b0}}), .col1({32{1'b0}}), .col2({32{1'b0}}), .col3({32{1'b0}}), .col4({32{1'b0}}),
    .col5({32{1'b0}}), .col6({32{1'b0}}), .col7({32{1'b0}}), .col8({32{1'b0}}), .col9({32{1'b0}}),
    .col10({32{1'b0}}), .col11({32{1'b0}}), .col12({32{1'b0}}));
  DotMatrix #(.matrixcols(13), .matrixrows(32)) dotmatrix_5 (
    .col0({32{1'b0}}), .col1({32{1'b0}}), .col2({32{1'b0}}), .col3({32{1'b0}}), .col4({32{1'b0}}),
    .col5({32{1'b0}}), .col6({32{1'b0}}), .col7({32{1'b0}}), .col8({32{1'b0}}), .col9({32{1'b0}}),
    .col10({32{1'b0}}), .col11({32{1'b0}}), .col12({32{1'b0}}));
  DotMatrix #(.matrixcols(28), .matrixrows(15)) dotmatrix_6 (
    .col0({15{1'b0}}), .col1({15{1'b0}}), .col2({15{1'b0}}), .col3({15{1'b0}}), .col4({15{1'b0}}),
    .col5({15{1'b0}}), .col6({15{1'b0}}), .col7({15{1'b0}}), .col8({15{1'b0}}), .col9({15{1'b0}}),
    .col10({15{1'b0}}), .col11({15{1'b0}}), .col12({15{1'b0}}), .col13({15{1'b0}}), .col14({15{1'b0}}),
    .col15({15{1'b0}}), .col16({15{1'b0}}), .col17({15{1'b0}}), .col18({15{1'b0}}), .col19({15{1'b0}}),
    .col20({15{1'b0}}), .col21({15{1'b0}}), .col22({15{1'b0}}), .col23({15{1'b0}}), .col24({15{1'b0}}),
    .col25({15{1'b0}}), .col26({15{1'b0}}), .col27({15{1'b0}}));
  DotMatrix #(.matrixcols(22), .matrixrows(9)) dotmatrix_7 (
    .col0({9{1'b0}}), .col1({9{1'b0}}), .col2({9{1'b0}}), .col3({9{1'b0}}), .col4({9{1'b0}}),
    .col5({9{1'b0}}), .col6({9{1'b0}}), .col7({9{1'b0}}), .col8({9{1'b0}}), .col9({9{1'b0}}),
    .col10({9{1'b0}}), .col11({9{1'b0}}), .col12({9{1'b0}}), .col13({9{1'b0}}), .col14({9{1'b0}}),
    .col15({9{1'b0}}), .col16({9{1'b0}}), .col17({9{1'b0}}), .col18({9{1'b0}}), .col19({9{1'b0}}),
    .col20({9{1'b0}}), .col21({9{1'b0}}));
  DotMatrix #(.matrixcols(32), .matrixrows(8)) dotmatrix_8 (
    .col0(teliko_1_out_138), .col1(teliko_1_out_133), .col2(teliko_1_out_132), .col3(teliko_1_out_131),
    .col4(teliko_1_out_130), .col5(teliko_1_out_125), .col6(teliko_1_out_124), .col7(teliko_1_out_123),
    .col8(teliko_1_out_122), .col9(teliko_1_out_117), .col10(teliko_1_out_116), .col11(teliko_1_out_115),
    .col12(teliko_1_out_114), .col13(teliko_1_out_109), .col14(teliko_1_out_108), .col15(teliko_1_out_107),
    .col16(teliko_1_out_106), .col17(teliko_1_out_101), .col18(teliko_1_out_100), .col19(teliko_1_out_99),
    .col20(teliko_1_out_98), .col21(teliko_1_out_93), .col22(teliko_1_out_91), .col23(teliko_1_out_90),
    .col24(teliko_1_out_89), .col25(teliko_1_out_84), .col26(teliko_1_out_83), .col27(teliko_1_out_82),
    .col28(teliko_1_out_81), .col29(teliko_1_out_76), .col30(teliko_1_out_71), .col31(teliko_1_out_66));
  teliko teliko_1 (
    .in_2(_2), .in_4(_1), .in_3(start), .in_5(\reset_ή_παραδοση ), .in_6(bol), .out_155(teliko_1_out_155),
    .out_151(teliko_1_out_151), .out_143(teliko_1_out_143), .out_147(teliko_1_out_147),
    .out_118(teliko_1_out_118), .out_126(teliko_1_out_126), .out_134(teliko_1_out_134),
    .out_139(teliko_1_out_139), .out_20(teliko_1_out_20), .out_37(teliko_1_out_37), .out_56(teliko_1_out_56),
    .out_77(teliko_1_out_77), .out_85(teliko_1_out_85), .out_94(teliko_1_out_94), .out_102(teliko_1_out_102),
    .out_110(teliko_1_out_110), .out_152(teliko_1_out_152), .out_148(teliko_1_out_148),
    .out_144(teliko_1_out_144), .out_140(teliko_1_out_140), .out_135(teliko_1_out_135),
    .out_127(teliko_1_out_127), .out_119(teliko_1_out_119), .out_111(teliko_1_out_111),
    .out_103(teliko_1_out_103), .out_95(teliko_1_out_95), .out_86(teliko_1_out_86), .out_78(teliko_1_out_78),
    .out_57(teliko_1_out_57), .out_38(teliko_1_out_38), .out_21(teliko_1_out_21), .out_22(teliko_1_out_22),
    .out_23(teliko_1_out_23), .out_39(teliko_1_out_39), .out_40(teliko_1_out_40), .out_58(teliko_1_out_58),
    .out_59(teliko_1_out_59), .out_79(teliko_1_out_79), .out_80(teliko_1_out_80), .out_87(teliko_1_out_87),
    .out_88(teliko_1_out_88), .out_96(teliko_1_out_96), .out_97(teliko_1_out_97), .out_104(teliko_1_out_104),
    .out_105(teliko_1_out_105), .out_112(teliko_1_out_112), .out_113(teliko_1_out_113),
    .out_120(teliko_1_out_120), .out_121(teliko_1_out_121), .out_128(teliko_1_out_128),
    .out_129(teliko_1_out_129), .out_136(teliko_1_out_136), .out_137(teliko_1_out_137),
    .out_141(teliko_1_out_141), .out_142(teliko_1_out_142), .out_145(teliko_1_out_145),
    .out_146(teliko_1_out_146), .out_149(teliko_1_out_149), .out_150(teliko_1_out_150),
    .out_153(teliko_1_out_153), .out_154(teliko_1_out_154), .out_156(teliko_1_out_156),
    .out_10(teliko_1_out_10), .out_12(teliko_1_out_12), .out_17(teliko_1_out_17), .out_19(teliko_1_out_19),
    .out_25(teliko_1_out_25), .out_30(teliko_1_out_30), .out_32(teliko_1_out_32), .out_36(teliko_1_out_36),
    .out_45(teliko_1_out_45), .out_51(teliko_1_out_51), .out_53(teliko_1_out_53), .out_55(teliko_1_out_55),
    .out_64(teliko_1_out_64), .out_66(teliko_1_out_66), .out_71(teliko_1_out_71), .out_76(teliko_1_out_76),
    .out_81(teliko_1_out_81), .out_82(teliko_1_out_82), .out_83(teliko_1_out_83), .out_84(teliko_1_out_84),
    .out_89(teliko_1_out_89), .out_90(teliko_1_out_90), .out_91(teliko_1_out_91), .out_93(teliko_1_out_93),
    .out_98(teliko_1_out_98), .out_99(teliko_1_out_99), .out_100(teliko_1_out_100),
    .out_101(teliko_1_out_101), .out_106(teliko_1_out_106), .out_107(teliko_1_out_107),
    .out_108(teliko_1_out_108), .out_109(teliko_1_out_109), .out_114(teliko_1_out_114),
    .out_115(teliko_1_out_115), .out_116(teliko_1_out_116), .out_117(teliko_1_out_117),
    .out_122(teliko_1_out_122), .out_123(teliko_1_out_123), .out_124(teliko_1_out_124),
    .out_125(teliko_1_out_125), .out_130(teliko_1_out_130), .out_131(teliko_1_out_131),
    .out_132(teliko_1_out_132), .out_133(teliko_1_out_133), .out_138(teliko_1_out_138),
    .out_11(teliko_1_out_11), .out_13(teliko_1_out_13), .out_18(teliko_1_out_18), .out_24(teliko_1_out_24),
    .out_26(teliko_1_out_26), .out_31(teliko_1_out_31), .out_33(teliko_1_out_33), .out_34(teliko_1_out_34),
    .out_35(teliko_1_out_35), .out_41(teliko_1_out_41), .out_46(teliko_1_out_46), .out_52(teliko_1_out_52),
    .out_54(teliko_1_out_54), .out_60(teliko_1_out_60), .out_65(teliko_1_out_65), .out_67(teliko_1_out_67),
    .out_72(teliko_1_out_72), .out_92(teliko_1_out_92), .out_73(teliko_1_out_73), .out_68(teliko_1_out_68),
    .out_42(teliko_1_out_42), .out_61(teliko_1_out_61), .out_7(teliko_1_out_7), .out_14(teliko_1_out_14),
    .out_27(teliko_1_out_27), .out_8(teliko_1_out_8), .out_15(teliko_1_out_15), .out_28(teliko_1_out_28),
    .out_43(teliko_1_out_43), .out_62(teliko_1_out_62), .out_69(teliko_1_out_69), .out_74(teliko_1_out_74),
    .out_9(teliko_1_out_9), .out_16(teliko_1_out_16), .out_29(teliko_1_out_29), .out_44(teliko_1_out_44),
    .out_63(teliko_1_out_63), .out_70(teliko_1_out_70), .out_75(teliko_1_out_75), .out_47(teliko_1_out_47),
    .out_48(teliko_1_out_48), .out_49(teliko_1_out_49), .out_50(teliko_1_out_50), .in_1(in_1));
  le le_1 (
    .out_2(le_1_out_2), .out_4(le_1_out_4), .out_6(le_1_out_6), .out_8(le_1_out_8), .out_10(le_1_out_10),
    .out_12(le_1_out_12), .out_14(le_1_out_14), .out_16(le_1_out_16), .out_18(le_1_out_18),
    .out_20(le_1_out_20), .out_22(le_1_out_22), .out_24(le_1_out_24), .out_26(le_1_out_26),
    .out_28(le_1_out_28), .out_29(le_1_out_29), .out_30(le_1_out_30), .out_31(le_1_out_31),
    .out_32(le_1_out_32), .out_3(le_1_out_3), .out_5(le_1_out_5), .out_7(le_1_out_7), .out_9(le_1_out_9),
    .out_11(le_1_out_11), .out_13(le_1_out_13), .out_15(le_1_out_15), .out_17(le_1_out_17),
    .out_19(le_1_out_19), .out_21(le_1_out_21), .out_23(le_1_out_23), .out_25(le_1_out_25),
    .out_27(le_1_out_27), .in_1(in_1));
  DotMatrix #(.matrixcols(27), .matrixrows(8)) dotmatrix_9 (
    .col0(le_1_out_2), .col1(le_1_out_4), .col2(le_1_out_6), .col3(le_1_out_8), .col4(le_1_out_10),
    .col5(le_1_out_12), .col6(le_1_out_14), .col7(le_1_out_16), .col8(le_1_out_18), .col9(le_1_out_20),
    .col10(le_1_out_22), .col11(le_1_out_24), .col12(le_1_out_26), .col13(le_1_out_28), .col14(le_1_out_29),
    .col15(le_1_out_30), .col16(le_1_out_31), .col17(le_1_out_32), .col18(le_1_out_3), .col19(le_1_out_5),
    .col20(le_1_out_7), .col21(le_1_out_9), .col22(le_1_out_11), .col23(le_1_out_13), .col24(le_1_out_15),
    .col25(le_1_out_17), .col26(le_1_out_19));
  DotMatrix #(.matrixcols(31), .matrixrows(8)) dotmatrix_10 (
    .col0(onoma_1_out_28), .col1(onoma_1_out_23), .col2(onoma_1_out_18), .col3(onoma_1_out_13),
    .col4(onoma_1_out_8), .col5(onoma_1_out_3), .col6(onoma_1_out_29), .col7(onoma_1_out_24),
    .col8(onoma_1_out_19), .col9(onoma_1_out_14), .col10(onoma_1_out_9), .col11(onoma_1_out_4),
    .col12(onoma_1_out_30), .col13(onoma_1_out_25), .col14(onoma_1_out_20), .col15(onoma_1_out_15),
    .col16(onoma_1_out_10), .col17(onoma_1_out_5), .col18(onoma_1_out_31), .col19(onoma_1_out_26),
    .col20(onoma_1_out_21), .col21(onoma_1_out_16), .col22(onoma_1_out_11), .col23(onoma_1_out_6),
    .col24(onoma_1_out_32), .col25(onoma_1_out_27), .col26(onoma_1_out_22), .col27(onoma_1_out_17),
    .col28(onoma_1_out_12), .col29(onoma_1_out_7), .col30(onoma_1_out_33));
  DotMatrix #(.matrixrows(22)) dotmatrix_11 (
    .col0({22{1'b0}}), .col1({22{1'b0}}), .col2({22{1'b0}}), .col3({22{1'b0}}), .col4({22{1'b0}}));
  DotMatrix #(.matrixcols(31), .matrixrows(32)) dotmatrix_12 (
    .col0(teliko_1_out_155), .col1(teliko_1_out_151), .col2(teliko_1_out_147), .col3(teliko_1_out_143),
    .col4(teliko_1_out_139), .col5(teliko_1_out_134), .col6(teliko_1_out_126), .col7(teliko_1_out_118),
    .col8(teliko_1_out_110), .col9(teliko_1_out_102), .col10(teliko_1_out_94), .col11(teliko_1_out_85),
    .col12(teliko_1_out_77), .col13(teliko_1_out_56), .col14(teliko_1_out_37), .col15(teliko_1_out_20),
    .col16(teliko_1_out_21), .col17(teliko_1_out_38), .col18(teliko_1_out_57), .col19(teliko_1_out_78),
    .col20(teliko_1_out_86), .col21(teliko_1_out_95), .col22(teliko_1_out_103), .col23(teliko_1_out_111),
    .col24(teliko_1_out_119), .col25(teliko_1_out_127), .col26(teliko_1_out_135), .col27(teliko_1_out_140),
    .col28(teliko_1_out_144), .col29(teliko_1_out_148), .col30(teliko_1_out_152));
  DotMatrix #(.matrixcols(31), .matrixrows(32)) dotmatrix_13 (
    .col0(teliko_1_out_156), .col1(teliko_1_out_153), .col2(teliko_1_out_149), .col3(teliko_1_out_145),
    .col4(teliko_1_out_141), .col5(teliko_1_out_136), .col6(teliko_1_out_128), .col7(teliko_1_out_120),
    .col8(teliko_1_out_112), .col9(teliko_1_out_104), .col10(teliko_1_out_96), .col11(teliko_1_out_87),
    .col12(teliko_1_out_79), .col13(teliko_1_out_58), .col14(teliko_1_out_39), .col15(teliko_1_out_22),
    .col16(teliko_1_out_23), .col17(teliko_1_out_40), .col18(teliko_1_out_59), .col19(teliko_1_out_80),
    .col20(teliko_1_out_88), .col21(teliko_1_out_97), .col22(teliko_1_out_105), .col23(teliko_1_out_113),
    .col24(teliko_1_out_121), .col25(teliko_1_out_129), .col26(teliko_1_out_137), .col27(teliko_1_out_142),
    .col28(teliko_1_out_146), .col29(teliko_1_out_150), .col30(teliko_1_out_154));
  Hex_Digit_Display hex_digit_display_1 (.value(teliko_1_out_48));  // open: dp
  Hex_Digit_Display hex_digit_display_2 (.value(teliko_1_out_47));  // open: dp
  DotMatrix #(.matrixcols(21), .matrixrows(8)) dotmatrix_14 (
    .col0({8{1'b0}}), .col1({8{1'b0}}), .col2(teliko_1_out_72), .col3(teliko_1_out_67),
    .col4(teliko_1_out_65), .col5(teliko_1_out_60), .col6(teliko_1_out_54), .col7(teliko_1_out_52),
    .col8(teliko_1_out_46), .col9(teliko_1_out_41), .col10(teliko_1_out_33), .col11(teliko_1_out_34),
    .col12(teliko_1_out_35), .col13(teliko_1_out_31), .col14(teliko_1_out_26), .col15(teliko_1_out_24),
    .col16(teliko_1_out_18), .col17(teliko_1_out_13), .col18(teliko_1_out_11), .col19({8{1'b0}}),
    .col20({8{1'b0}}));
  DotMatrix #(.matrixcols(7), .matrixrows(8)) dotmatrix_15 (
    .col0(teliko_1_out_73), .col1(teliko_1_out_68), .col2(teliko_1_out_61), .col3(teliko_1_out_42),
    .col4(teliko_1_out_27), .col5(teliko_1_out_14), .col6(teliko_1_out_7));
  DotMatrix #(.matrixcols(7), .matrixrows(8)) dotmatrix_16 (
    .col0(teliko_1_out_74), .col1(teliko_1_out_69), .col2(teliko_1_out_62), .col3(teliko_1_out_43),
    .col4(teliko_1_out_28), .col5(teliko_1_out_15), .col6(teliko_1_out_8));
  DotMatrix #(.matrixcols(23), .matrixrows(9)) dotmatrix_17 (
    .col0({9{1'b0}}), .col1({9{1'b0}}), .col2({9{1'b0}}), .col3({9{1'b0}}), .col4({9{1'b0}}),
    .col5({9{1'b0}}), .col6({9{1'b0}}), .col7({9{1'b0}}), .col8({9{1'b0}}), .col9({9{1'b0}}),
    .col10({9{1'b0}}), .col11({9{1'b0}}), .col12({9{1'b0}}), .col13({9{1'b0}}), .col14({9{1'b0}}),
    .col15({9{1'b0}}), .col16({9{1'b0}}), .col17({9{1'b0}}), .col18({9{1'b0}}), .col19({9{1'b0}}),
    .col20({9{1'b0}}), .col21({9{1'b0}}), .col22({9{1'b0}}));
  DotMatrix #(.matrixrows(6)) dotmatrix_18 (
    .col0({6{1'b0}}), .col1({6{1'b0}}), .col2(6'b010010), .col3({6{1'b0}}), .col4({6{1'b0}}));
  Hex_Digit_Display hex_digit_display_3 (.value(teliko_1_out_49));  // open: dp
  DotMatrix #(.matrixcols(7), .matrixrows(8)) dotmatrix_19 (
    .col0(teliko_1_out_75), .col1(teliko_1_out_70), .col2(teliko_1_out_63), .col3(teliko_1_out_44),
    .col4(teliko_1_out_29), .col5(teliko_1_out_16), .col6(teliko_1_out_9));
  DotMatrix #(.matrixcols(29), .matrixrows(15)) dotmatrix_20 (
    .col0({15{1'b0}}), .col1({15{1'b0}}), .col2({15{1'b0}}), .col3({15{1'b0}}), .col4({15{1'b0}}),
    .col5({15{1'b0}}), .col6({15{1'b0}}), .col7({15{1'b0}}), .col8({15{1'b0}}), .col9({15{1'b0}}),
    .col10({15{1'b0}}), .col11({15{1'b0}}), .col12({15{1'b0}}), .col13({15{1'b0}}), .col14({15{1'b0}}),
    .col15({15{1'b0}}), .col16({15{1'b0}}), .col17({15{1'b0}}), .col18({15{1'b0}}), .col19({15{1'b0}}),
    .col20({15{1'b0}}), .col21({15{1'b0}}), .col22({15{1'b0}}), .col23({15{1'b0}}), .col24({15{1'b0}}),
    .col25({15{1'b0}}), .col26({15{1'b0}}), .col27({15{1'b0}}), .col28({15{1'b0}}));
  DotMatrix #(.matrixcols(13), .matrixrows(8)) dotmatrix_21 (
    .col0(teliko_1_out_64), .col1(teliko_1_out_55), .col2(teliko_1_out_53), .col3(teliko_1_out_51),
    .col4(teliko_1_out_45), .col5(teliko_1_out_36), .col6(teliko_1_out_32), .col7(teliko_1_out_30),
    .col8(teliko_1_out_25), .col9(teliko_1_out_19), .col10(teliko_1_out_17), .col11(teliko_1_out_12),
    .col12(teliko_1_out_10));
  Hex_Digit_Display hex_digit_display_4 (.value(teliko_1_out_92));  // open: dp
  DotMatrix #(.matrixcols(4), .matrixrows(2)) dotmatrix_22 (
    .col0(le_1_out_21), .col1(le_1_out_23), .col2(le_1_out_25), .col3(le_1_out_27));
  Hex_Digit_Display hex_digit_display_5 (.value(teliko_1_out_50));  // open: dp
  DotMatrix #(.matrixrows(22)) dotmatrix_23 (
    .col0({22{1'b0}}), .col1({22{1'b0}}), .col2({22{1'b0}}), .col3({22{1'b0}}), .col4({22{1'b0}}));
  DotMatrix #(.matrixcols(13), .matrixrows(6)) dotmatrix_24 (
    .col0({6{1'b0}}), .col1({6{1'b0}}), .col2({6{1'b0}}), .col3({6{1'b0}}), .col4({6{1'b0}}),
    .col5({6{1'b0}}), .col6({6{1'b0}}), .col7({6{1'b0}}), .col8({6{1'b0}}), .col9({6{1'b0}}),
    .col10({6{1'b0}}), .col11({6{1'b0}}), .col12({6{1'b0}}));
  DotMatrix #(.matrixcols(13), .matrixrows(32)) dotmatrix_25 (
    .col0({32{1'b0}}), .col1({32{1'b0}}), .col2({32{1'b0}}), .col3({32{1'b0}}), .col4({32{1'b0}}),
    .col5({32{1'b0}}), .col6({32{1'b0}}), .col7({32{1'b0}}), .col8({32{1'b0}}), .col9({32{1'b0}}),
    .col10({32{1'b0}}), .col11({32{1'b0}}), .col12({32{1'b0}}));
  DotMatrix #(.matrixcols(13), .matrixrows(32)) dotmatrix_26 (
    .col0({32{1'b0}}), .col1({32{1'b0}}), .col2({32{1'b0}}), .col3({32{1'b0}}), .col4({32{1'b0}}),
    .col5({32{1'b0}}), .col6({32{1'b0}}), .col7({32{1'b0}}), .col8({32{1'b0}}), .col9({32{1'b0}}),
    .col10({32{1'b0}}), .col11({32{1'b0}}), .col12({32{1'b0}}));
  DotMatrix #(.matrixcols(13), .matrixrows(32)) dotmatrix_27 (
    .col0({32{1'b0}}), .col1({32{1'b0}}), .col2({32{1'b0}}), .col3({32{1'b0}}), .col4({32{1'b0}}),
    .col5({32{1'b0}}), .col6({32{1'b0}}), .col7({32{1'b0}}), .col8({32{1'b0}}), .col9({32{1'b0}}),
    .col10({32{1'b0}}), .col11({32{1'b0}}), .col12({32{1'b0}}));
  DotMatrix #(.matrixcols(6), .matrixrows(17)) dotmatrix_28 (
    .col0({17{1'b0}}), .col1({17{1'b0}}), .col2({17{1'b0}}), .col3({17{1'b0}}), .col4({17{1'b0}}),
    .col5({17{1'b0}}));

  // Other names for the same wires on the sheet: on_or_off = in_1
endmodule

module teliko (
  input  in_1,
  input  [1:0] in_2,
  input  in_3,
  input  [1:0] in_4,
  input  in_5,
  input  in_6,
  output [7:0] out_7,
  output [7:0] out_8,
  output [7:0] out_9,
  output [7:0] out_10,
  output [7:0] out_11,
  output [7:0] out_12,
  output [7:0] out_13,
  output [7:0] out_14,
  output [7:0] out_15,
  output [7:0] out_16,
  output [7:0] out_17,
  output [7:0] out_18,
  output [7:0] out_19,
  output [31:0] out_20,
  output [31:0] out_21,
  output [31:0] out_22,
  output [31:0] out_23,
  output [7:0] out_24,
  output [7:0] out_25,
  output [7:0] out_26,
  output [7:0] out_27,
  output [7:0] out_28,
  output [7:0] out_29,
  output [7:0] out_30,
  output [7:0] out_31,
  output [7:0] out_32,
  output [7:0] out_33,
  output [7:0] out_34,
  output [7:0] out_35,
  output [7:0] out_36,
  output [31:0] out_37,
  output [31:0] out_38,
  output [31:0] out_39,
  output [31:0] out_40,
  output [7:0] out_41,
  output [7:0] out_42,
  output [7:0] out_43,
  output [7:0] out_44,
  output [7:0] out_45,
  output [7:0] out_46,
  output [3:0] out_47,
  output [3:0] out_48,
  output [3:0] out_49,
  output [3:0] out_50,
  output [7:0] out_51,
  output [7:0] out_52,
  output [7:0] out_53,
  output [7:0] out_54,
  output [7:0] out_55,
  output [31:0] out_56,
  output [31:0] out_57,
  output [31:0] out_58,
  output [31:0] out_59,
  output [7:0] out_60,
  output [7:0] out_61,
  output [7:0] out_62,
  output [7:0] out_63,
  output [7:0] out_64,
  output [7:0] out_65,
  output [7:0] out_66,
  output [7:0] out_67,
  output [7:0] out_68,
  output [7:0] out_69,
  output [7:0] out_70,
  output [7:0] out_71,
  output [7:0] out_72,
  output [7:0] out_73,
  output [7:0] out_74,
  output [7:0] out_75,
  output [7:0] out_76,
  output [31:0] out_77,
  output [31:0] out_78,
  output [31:0] out_79,
  output [31:0] out_80,
  output [7:0] out_81,
  output [7:0] out_82,
  output [7:0] out_83,
  output [7:0] out_84,
  output [31:0] out_85,
  output [31:0] out_86,
  output [31:0] out_87,
  output [31:0] out_88,
  output [7:0] out_89,
  output [7:0] out_90,
  output [7:0] out_91,
  output [3:0] out_92,
  output [7:0] out_93,
  output [31:0] out_94,
  output [31:0] out_95,
  output [31:0] out_96,
  output [31:0] out_97,
  output [7:0] out_98,
  output [7:0] out_99,
  output [7:0] out_100,
  output [7:0] out_101,
  output [31:0] out_102,
  output [31:0] out_103,
  output [31:0] out_104,
  output [31:0] out_105,
  output [7:0] out_106,
  output [7:0] out_107,
  output [7:0] out_108,
  output [7:0] out_109,
  output [31:0] out_110,
  output [31:0] out_111,
  output [31:0] out_112,
  output [31:0] out_113,
  output [7:0] out_114,
  output [7:0] out_115,
  output [7:0] out_116,
  output [7:0] out_117,
  output [31:0] out_118,
  output [31:0] out_119,
  output [31:0] out_120,
  output [31:0] out_121,
  output [7:0] out_122,
  output [7:0] out_123,
  output [7:0] out_124,
  output [7:0] out_125,
  output [31:0] out_126,
  output [31:0] out_127,
  output [31:0] out_128,
  output [31:0] out_129,
  output [7:0] out_130,
  output [7:0] out_131,
  output [7:0] out_132,
  output [7:0] out_133,
  output [31:0] out_134,
  output [31:0] out_135,
  output [31:0] out_136,
  output [31:0] out_137,
  output [7:0] out_138,
  output [31:0] out_139,
  output [31:0] out_140,
  output [31:0] out_141,
  output [31:0] out_142,
  output [31:0] out_143,
  output [31:0] out_144,
  output [31:0] out_145,
  output [31:0] out_146,
  output [31:0] out_147,
  output [31:0] out_148,
  output [31:0] out_149,
  output [31:0] out_150,
  output [31:0] out_151,
  output [31:0] out_152,
  output [31:0] out_153,
  output [31:0] out_154,
  output [31:0] out_155,
  output [31:0] out_156
);

  wire _0, _01, and_1_out, and_2_out, and_3_out, and_4_out, and_5_out, and_7_out, and_8_out, comparator_1_lt,
       multiplexer_28_out, multiplexer_29_out, n2_1_out_6, nhkh_or_hta, not_1_out, not_2_out, not_3_out,
       not_4_out, not_5_out, not_6_out, not_7_out, or_1_out, or_3_out, register_1_q, register_2_q,
       reset_or_sos, rest, sos, sp, start, \βολη , \ρο ;
  wire [1:0] _1, _2;
  wire [2:0] n2_1_out_4, n2_1_out_5;
  wire [3:0] niiio, roloh_1_out_4, roloh_1_out_5, roloh_1_out_6, roloh_1_out_7;
  wire [7:0] b_2_out_2, b_2_out_3, b_2_out_4, b_2_out_5, b_2_out_6, counter_2_q, counter_3_q, o_1_out_2,
       o_1_out_3, o_1_out_4, o_1_out_5, o_1_out_6, register_3_q, s_1_out_2, s_1_out_3, s_1_out_4, s_1_out_5,
       s_1_out_6, sos_1_out_38;
  wire [31:0] b_1_out_4, b_1_out_5, b_1_out_6, b_1_out_7, bol2_1_out_5, bol2_1_out_6, bol2_1_out_7,
       bol2_1_out_8, bol2_1_out_9, bol2_1_out_10, bol2_1_out_11, bol2_1_out_12, bol2_1_out_13, bol2_1_out_14,
       bol2_1_out_15, bol2_1_out_16, bol2_1_out_17, bol2_1_out_18, bol2_1_out_19, bol2_1_out_20,
       bol2_1_out_21, bol2_1_out_22, bol2_1_out_23, bol2_1_out_24, bol2_1_out_25, bol2_1_out_26,
       bol2_1_out_27, bol2_1_out_28, bol2_1_out_29, bol2_1_out_30, bol2_1_out_31, bol2_1_out_32,
       bol2_1_out_33, bol2_1_out_34, bol2_1_out_35, sos_1_out_7, sos_1_out_8, sos_1_out_9, sos_1_out_10,
       sos_1_out_11, sos_1_out_12, sos_1_out_13, sos_1_out_14, sos_1_out_15, sos_1_out_16, sos_1_out_17,
       sos_1_out_18, sos_1_out_19, sos_1_out_20, sos_1_out_21, sos_1_out_22, sos_1_out_23, sos_1_out_24,
       sos_1_out_25, sos_1_out_26, sos_1_out_27, sos_1_out_28, sos_1_out_29, sos_1_out_30, sos_1_out_31,
       sos_1_out_32, sos_1_out_33, sos_1_out_34, sos_1_out_35, sos_1_out_36, sos_1_out_37;

  Hex_Digit_Display hex_digit_display_1 (.value(out_47));  // open: dp
  Multiplexer #(.width(4), .enable("false")) multiplexer_1 (
    .in0(4'b0000), .in1(roloh_1_out_4), .out(out_47), .sel(in_1));
  Multiplexer #(.width(32), .enable("false")) multiplexer_2 (
    .in0({32{1'b0}}), .in1(b_1_out_4), .out({out_7, out_68, out_61, out_42}), .sel(in_1));
  b b_1 (
    .in_1(n2_1_out_4), .in_2(n2_1_out_5), .out_4(b_1_out_4), .out_5(b_1_out_5), .out_6(b_1_out_6),
    .out_7(b_1_out_7), .in_3(or_1_out));
  neo_2 u_2_1 (.out_4(n2_1_out_4), .out_5(n2_1_out_5), .out_6(n2_1_out_6), .in_1(1'b0), .in_2(\βολη ), .in_3(or_1_out));
  or or_1 (or_1_out, start, and_1_out, rest);
  and and_1 (and_1_out, n2_1_out_6, not_1_out);
  not not_1 (not_1_out, and_2_out);
  not not_2 (not_2_out, niiio[1]);
  and and_2 (and_2_out, niiio[0], not_2_out, not_3_out, niiio[3]);
  not not_3 (not_3_out, niiio[2]);
  Register #(.width(1), .trigger("high")) register_1 (
    .D(sos), .Q(register_1_q), .clk(sos), .clr(or_3_out));  // open: en
  Multiplexer #(.width(4), .enable("false")) multiplexer_3 (
    .in0(4'b0000), .in1(roloh_1_out_5), .out(out_48), .sel(in_1));
  Hex_Digit_Display hex_digit_display_2 (.value(out_48));  // open: dp
  Hex_Digit_Display hex_digit_display_3 (.value(out_49));  // open: dp
  Multiplexer #(.width(4), .enable("false")) multiplexer_4 (
    .in0(4'b0000), .in1(roloh_1_out_6), .out(out_49), .sel(in_1));
  roloh roloh_1 (
    .in_1(rest), .star(start), .out_8(nhkh_or_hta), .out_4(roloh_1_out_4), .out_5(roloh_1_out_5),
    .out_6(roloh_1_out_6), .out_7(roloh_1_out_7), .in_3(and_5_out));
  Multiplexer #(.width(32), .enable("false")) multiplexer_5 (
    .in0({32{1'b0}}), .in1(b_1_out_6), .out({out_43, out_28, out_15, out_70}), .sel(in_1));
  Multiplexer #(.width(32), .enable("false")) multiplexer_6 (
    .in0({32{1'b0}}), .in1(b_1_out_5), .out({out_27, out_14, out_69, out_62}), .sel(in_1));
  Counter #(.width(4), .max('hf)) counter_1 (
    .Q(niiio), .clk(and_3_out), .clr(reset_or_sos));  // open: load, D, count, carry
  and and_3 (and_3_out, n2_1_out_6, not_4_out);
  not not_4 (not_4_out, and_4_out);
  and and_4 (and_4_out, niiio[0], not_6_out, not_5_out, niiio[3]);
  Register #(.width(1)) register_2 (
    .D(n2_1_out_6), .Q(register_2_q), .clk(n2_1_out_6), .clr(reset_or_sos));  // open: en
  or or_2 (reset_or_sos, rest, start);
  Counter counter_2 (
    .load(register_1_q), .D(8'h3), .count(1'b0), .Q(counter_2_q), .clk(register_1_q), .clr(or_3_out));  // open: carry
  Counter counter_3 (.Q(counter_3_q), .clk(\ρο ), .clr(or_3_out));  // open: load, D, count, carry
  Clock clock_1 (.out(\ρο ));
  Multiplexer #(.width(4), .enable("false")) multiplexer_7 (
    .in0(4'b0000), .in1(roloh_1_out_7), .out(out_50), .sel(in_1));
  Hex_Digit_Display hex_digit_display_4 (.value(out_50));  // open: dp
  Multiplexer #(.width(32), .enable("false")) multiplexer_8 (
    .in0({32{1'b0}}), .in1(b_1_out_7), .out({out_63, out_44, out_29, out_16}), .sel(in_1));
  not not_5 (not_5_out, niiio[2]);
  not not_6 (not_6_out, niiio[1]);
  and and_5 (and_5_out, register_2_q, niiio[3], not_5_out, not_6_out, niiio[0]);
  Comparator comparator_1 (.a(counter_2_q), .b(counter_3_q), .lt(comparator_1_lt));  // open: gt, eq
  or or_3 (or_3_out, comparator_1_lt, rest);
  and and_6 (\βολη , register_1_q, \ρο );
  Multiplexer #(.width(8), .enable("false")) multiplexer_9 (.in0({8{1'b0}}), .in1(s_1_out_6), .out(out_11), .sel(in_1));
  Multiplexer #(.width(8), .enable("false")) multiplexer_10 (
    .in0({8{1'b0}}), .in1(s_1_out_5), .out(out_13), .sel(in_1));
  Multiplexer #(.width(8), .enable("false")) multiplexer_11 (
    .in0({8{1'b0}}), .in1(s_1_out_4), .out(out_18), .sel(in_1));
  Multiplexer #(.width(8), .enable("false")) multiplexer_12 (
    .in0({8{1'b0}}), .in1(s_1_out_3), .out(out_24), .sel(in_1));
  Multiplexer #(.width(8), .enable("false")) multiplexer_13 (
    .in0({8{1'b0}}), .in1(s_1_out_2), .out(out_26), .sel(in_1));
  Multiplexer #(.width(8), .enable("false")) multiplexer_14 (
    .in0({8{1'b0}}), .in1({8{1'b0}}), .out(out_31), .sel(in_1));
  Multiplexer #(.width(8), .enable("false")) multiplexer_15 (
    .in0({8{1'b0}}), .in1(o_1_out_6), .out(out_35), .sel(in_1));
  Multiplexer #(.width(8), .enable("false")) multiplexer_16 (
    .in0({8{1'b0}}), .in1(o_1_out_5), .out(out_34), .sel(in_1));
  Multiplexer #(.width(8), .enable("false")) multiplexer_17 (
    .in0({8{1'b0}}), .in1(o_1_out_4), .out(out_33), .sel(in_1));
  Multiplexer #(.width(8), .enable("false")) multiplexer_18 (
    .in0({8{1'b0}}), .in1(o_1_out_3), .out(out_41), .sel(in_1));
  Multiplexer #(.width(8), .enable("false")) multiplexer_19 (
    .in0({8{1'b0}}), .in1(o_1_out_2), .out(out_46), .sel(in_1));
  Multiplexer #(.width(8), .enable("false")) multiplexer_20 (
    .in0({8{1'b0}}), .in1({8{1'b0}}), .out(out_52), .sel(in_1));
  Multiplexer #(.width(8), .enable("false")) multiplexer_21 (
    .in0({8{1'b0}}), .in1(b_2_out_6), .out(out_54), .sel(in_1));
  Multiplexer #(.width(8), .enable("false")) multiplexer_22 (
    .in0({8{1'b0}}), .in1(b_2_out_5), .out(out_60), .sel(in_1));
  Multiplexer #(.width(8), .enable("false")) multiplexer_23 (
    .in0({8{1'b0}}), .in1(b_2_out_4), .out(out_65), .sel(in_1));
  Multiplexer #(.width(8), .enable("false")) multiplexer_24 (
    .in0({8{1'b0}}), .in1(b_2_out_3), .out(out_67), .sel(in_1));
  Multiplexer #(.width(8), .enable("false")) multiplexer_25 (
    .in0({8{1'b0}}), .in1(b_2_out_2), .out(out_72), .sel(in_1));
  DotMatrix #(.matrixcols(17), .matrixrows(8)) dotmatrix_1 (
    .col0(b_2_out_2), .col1(b_2_out_3), .col2(b_2_out_4), .col3(b_2_out_5), .col4(b_2_out_6),
    .col5({8{1'b0}}), .col6(o_1_out_2), .col7(o_1_out_3), .col8(o_1_out_4), .col9(o_1_out_5),
    .col10(o_1_out_6), .col11({8{1'b0}}), .col12(s_1_out_2), .col13(s_1_out_3), .col14(s_1_out_4),
    .col15(s_1_out_5), .col16(s_1_out_6));
  B b_2 (.in_1(1'b1), .out_2(b_2_out_2), .out_3(b_2_out_3), .out_4(b_2_out_4), .out_5(b_2_out_5), .out_6(b_2_out_6));
  O o_1 (.in_1(1'b1), .out_2(o_1_out_2), .out_3(o_1_out_3), .out_4(o_1_out_4), .out_5(o_1_out_5), .out_6(o_1_out_6));
  sos sos_1 (
    .in_1(sp), .in_2(start), .in_3(rest), .in_4(_01), .out_39(_01), .in_5(_1), .in_6(_2),
    .out_23(sos_1_out_23), .out_24(sos_1_out_24), .out_25(sos_1_out_25), .out_26(sos_1_out_26),
    .out_27(sos_1_out_27), .out_28(sos_1_out_28), .out_29(sos_1_out_29), .out_30(sos_1_out_30),
    .out_31(sos_1_out_31), .out_32(sos_1_out_32), .out_33(sos_1_out_33), .out_34(sos_1_out_34),
    .out_35(sos_1_out_35), .out_36(sos_1_out_36), .out_37(sos_1_out_37), .out_38(sos_1_out_38),
    .out_8(sos_1_out_8), .out_9(sos_1_out_9), .out_10(sos_1_out_10), .out_11(sos_1_out_11),
    .out_12(sos_1_out_12), .out_13(sos_1_out_13), .out_14(sos_1_out_14), .out_15(sos_1_out_15),
    .out_16(sos_1_out_16), .out_17(sos_1_out_17), .out_18(sos_1_out_18), .out_19(sos_1_out_19),
    .out_20(sos_1_out_20), .out_21(sos_1_out_21), .out_22(sos_1_out_22), .out_7(sos_1_out_7));
  S s_1 (.in_1(1'b1), .out_2(s_1_out_2), .out_3(s_1_out_3), .out_4(s_1_out_4), .out_5(s_1_out_5), .out_6(s_1_out_6));
  DotMatrix #(.matrixcols(7), .matrixrows(8)) dotmatrix_2 (
    .col0(out_7), .col1(out_68), .col2(out_61), .col3(out_42), .col4(out_27), .col5(out_14), .col6(out_7));
  Multiplexer #(.width(4), .enable("false")) multiplexer_26 (.in0(4'b0000), .in1(niiio), .out(out_92), .sel(in_1));
  Hex_Digit_Display hex_digit_display_5 (.value(out_92));  // open: dp
  Button button_1 ();  // open: out
  DotMatrix #(.matrixcols(7), .matrixrows(8)) dotmatrix_3 (
    .col0(out_7), .col1(out_69), .col2(out_62), .col3(out_43), .col4(out_28), .col5(out_15), .col6(out_7));
  and and_7 (and_7_out, nhkh_or_hta, in_1);
  and and_8 (and_8_out, in_1, and_5_out);
  Joystick #(.bits(2)) joystick_1 ();  // open: x, y
  DotMatrix #(.matrixcols(7), .matrixrows(8)) dotmatrix_4 (
    .col0(out_7), .col1(out_70), .col2(out_63), .col3(out_44), .col4(out_29), .col5(out_16), .col6(out_7));
  nikh_h_hta nikh_h_hta_1 (
    .in_1(and_7_out), .out_47(out_138), .out_46(out_133), .out_45(out_132), .out_44(out_131),
    .out_43(out_130), .out_42(out_125), .out_41(out_124), .out_40(out_123), .out_39(out_122),
    .out_38(out_117), .out_37(out_116), .out_36(out_115), .out_35(out_114), .out_34(out_109),
    .out_33(out_108), .out_32(out_107), .out_31(out_106), .out_30(out_101), .out_29(out_100),
    .out_28(out_99), .out_27(out_98), .out_26(out_93), .out_25(out_91), .out_24(out_90), .out_23(out_89),
    .out_22(out_84), .out_21(out_83), .out_20(out_82), .out_19(out_81), .out_18(out_76), .out_17(out_71),
    .out_16(out_66), .out_15(out_64), .out_14(out_55), .out_13(out_53), .out_12(out_51), .out_11(out_45),
    .out_10(out_36), .out_9(out_32), .out_8(out_30), .out_7(out_25), .out_6(out_19), .out_5(out_17),
    .out_4(out_12), .out_3(out_10), .in_2(and_8_out));
  DotMatrix #(.matrixcols(32), .matrixrows(8)) dotmatrix_5 (
    .col0(out_138), .col1(out_133), .col2(out_132), .col3(out_131), .col4(out_130), .col5(out_125),
    .col6(out_124), .col7(out_123), .col8(out_122), .col9(out_117), .col10(out_116), .col11(out_115),
    .col12(out_114), .col13(out_109), .col14(out_108), .col15(out_107), .col16(out_106), .col17(out_101),
    .col18(out_100), .col19(out_99), .col20(out_98), .col21(out_93), .col22(out_91), .col23(out_90),
    .col24(out_89), .col25(out_84), .col26(out_83), .col27(out_82), .col28(out_81), .col29(out_76),
    .col30(out_71), .col31(out_66));
  Multiplexer #(.enable("false")) multiplexer_27 (.in0(1'b0), .in1(in_3), .out(start), .sel(in_1));
  Multiplexer #(.enable("false")) multiplexer_28 (.in0(1'b0), .in1(in_5), .out(multiplexer_28_out), .sel(in_1));
  Multiplexer #(.enable("false")) multiplexer_29 (.in0(1'b0), .in1(in_6), .out(multiplexer_29_out), .sel(in_1));
  not not_7 (not_7_out, in_1);
  fortosh_bol fortosh_bol_1 (.in_1(multiplexer_29_out), .in_2(_0), .out_5(sp), .in_4(rest), .in_3(_01));
  or or_4 (rest, multiplexer_28_out, not_7_out);
  DotMatrix #(.matrixcols(13), .matrixrows(8)) dotmatrix_6 (
    .col0(out_64), .col1(out_55), .col2(out_53), .col3(out_51), .col4(out_45), .col5(out_36), .col6(out_32),
    .col7(out_30), .col8(out_25), .col9(out_19), .col10(out_17), .col11(out_12), .col12(out_10));
  sos_sos sos_sos_1 (
    .out_33(out_155), .out_34(out_151), .out_35(out_147), .in_1(in_1), .out_36(out_143), .out_37(out_139),
    .out_38(out_134), .out_39(out_126), .out_40(out_118), .out_41(out_110), .out_42(out_102),
    .out_43(out_94), .out_44(out_85), .out_45(out_77), .out_46(out_56), .out_47(out_37), .out_48(out_20),
    .out_49(out_21), .out_50(out_38), .out_51(out_57), .out_52(out_78), .out_53(out_86), .out_54(out_95),
    .out_55(out_103), .out_56(out_111), .out_57(out_119), .out_58(out_127), .out_59(out_135),
    .out_60(out_140), .out_61(out_144), .out_62(out_148), .out_63(out_152), .in_2(sos_1_out_37),
    .in_3(sos_1_out_36), .in_4(sos_1_out_35), .in_5(sos_1_out_34), .in_6(sos_1_out_33), .in_7(sos_1_out_32),
    .in_8(sos_1_out_31), .in_9(sos_1_out_30), .in_10(sos_1_out_29), .in_11(sos_1_out_28),
    .in_12(sos_1_out_27), .in_13(sos_1_out_26), .in_14(sos_1_out_25), .in_15(sos_1_out_24),
    .in_16(sos_1_out_23), .in_17(sos_1_out_22), .in_18(sos_1_out_21), .in_19(sos_1_out_20),
    .in_20(sos_1_out_19), .in_21(sos_1_out_18), .in_22(sos_1_out_17), .in_23(sos_1_out_16),
    .in_24(sos_1_out_15), .in_25(sos_1_out_14), .in_26(sos_1_out_13), .in_27(sos_1_out_12),
    .in_28(sos_1_out_11), .in_29(sos_1_out_10), .in_30(sos_1_out_9), .in_31(sos_1_out_8), .in_32(sos_1_out_7));
  Multiplexer #(.width(2), .enable("false")) multiplexer_30 (.in0(2'b00), .in1(in_2), .out(_1), .sel(in_1));
  Multiplexer #(.width(2), .enable("false")) multiplexer_31 (.in0(2'b00), .in1(in_4), .out(_2), .sel(in_1));
  Register register_3 (.D(sos_1_out_38), .Q(register_3_q), .clk(_01), .clr(rest));  // open: en
  not not_8 (_0, _01);
  DotMatrix #(.matrixcols(31), .matrixrows(32)) dotmatrix_7 (
    .col0(out_155), .col1(out_151), .col2(out_147), .col3(out_143), .col4(out_139), .col5(out_134),
    .col6(out_126), .col7(out_118), .col8(out_110), .col9(out_102), .col10(out_94), .col11(out_85),
    .col12(out_77), .col13(out_56), .col14(out_37), .col15(out_20), .col16(out_21), .col17(out_38),
    .col18(out_57), .col19(out_78), .col20(out_86), .col21(out_95), .col22(out_103), .col23(out_111),
    .col24(out_119), .col25(out_127), .col26(out_135), .col27(out_140), .col28(out_144), .col29(out_148),
    .col30(out_152));
  bol2 bol2_1 (
    .in_1(register_3_q), .out_33(bol2_1_out_33), .in_2(_01), .out_29(bol2_1_out_29), .out_21(bol2_1_out_21),
    .out_25(bol2_1_out_25), .out_6(bol2_1_out_6), .out_9(bol2_1_out_9), .out_13(bol2_1_out_13),
    .out_17(bol2_1_out_17), .out_10(bol2_1_out_10), .out_14(bol2_1_out_14), .out_18(bol2_1_out_18),
    .out_22(bol2_1_out_22), .out_26(bol2_1_out_26), .out_30(bol2_1_out_30), .out_34(bol2_1_out_34),
    .out_8(bol2_1_out_8), .out_5(bol2_1_out_5), .out_12(bol2_1_out_12), .out_16(bol2_1_out_16),
    .out_20(bol2_1_out_20), .out_24(bol2_1_out_24), .out_28(bol2_1_out_28), .out_32(bol2_1_out_32),
    .out_7(bol2_1_out_7), .out_11(bol2_1_out_11), .out_15(bol2_1_out_15), .out_19(bol2_1_out_19),
    .out_23(bol2_1_out_23), .out_27(bol2_1_out_27), .out_31(bol2_1_out_31), .out_35(bol2_1_out_35),
    .out_36(sos), .in_4(start), .in_3(rest));
  sos_sos sos_sos_2 (
    .out_33(out_156), .out_34(out_153), .out_35(out_149), .in_1(in_1), .out_36(out_145), .out_37(out_141),
    .out_38(out_136), .out_39(out_128), .out_40(out_120), .out_41(out_112), .out_42(out_104),
    .out_43(out_96), .out_44(out_87), .out_45(out_79), .out_46(out_58), .out_47(out_39), .out_48(out_22),
    .out_49(out_23), .out_50(out_40), .out_51(out_59), .out_52(out_80), .out_53(out_88), .out_54(out_97),
    .out_55(out_105), .out_56(out_113), .out_57(out_121), .out_58(out_129), .out_59(out_137),
    .out_60(out_142), .out_61(out_146), .out_62(out_150), .out_63(out_154), .in_2(bol2_1_out_5),
    .in_3(bol2_1_out_8), .in_4(bol2_1_out_12), .in_5(bol2_1_out_16), .in_6(bol2_1_out_20),
    .in_7(bol2_1_out_24), .in_8(bol2_1_out_28), .in_9(bol2_1_out_32), .in_10(bol2_1_out_33),
    .in_11(bol2_1_out_29), .in_12(bol2_1_out_25), .in_13(bol2_1_out_21), .in_14(bol2_1_out_17),
    .in_15(bol2_1_out_13), .in_16(bol2_1_out_9), .in_17(bol2_1_out_6), .in_18(bol2_1_out_10),
    .in_19(bol2_1_out_14), .in_20(bol2_1_out_18), .in_21(bol2_1_out_22), .in_22(bol2_1_out_26),
    .in_23(bol2_1_out_30), .in_24(bol2_1_out_34), .in_25(bol2_1_out_7), .in_26(bol2_1_out_11),
    .in_27(bol2_1_out_15), .in_28(bol2_1_out_19), .in_29(bol2_1_out_23), .in_30(bol2_1_out_27),
    .in_31(bol2_1_out_31), .in_32(bol2_1_out_35));
  DotMatrix #(.matrixcols(31), .matrixrows(32)) dotmatrix_8 (
    .col0(out_156), .col1(out_153), .col2(out_149), .col3(out_145), .col4(out_141), .col5(out_136),
    .col6(out_128), .col7(out_120), .col8(out_112), .col9(out_104), .col10(out_96), .col11(out_87),
    .col12(out_79), .col13(out_58), .col14(out_39), .col15(out_22), .col16(out_23), .col17(out_40),
    .col18(out_59), .col19(out_80), .col20(out_88), .col21(out_97), .col22(out_105), .col23(out_113),
    .col24(out_121), .col25(out_129), .col26(out_137), .col27(out_142), .col28(out_146), .col29(out_150),
    .col30(out_154));

  assign out_8 = out_7;
  assign out_9 = out_7;
  assign out_73 = out_7;
  assign out_74 = out_7;
  assign out_75 = out_7;

  // Other names for the same wires on the sheet: _13[7:0] = out_42; _12[7:0] = out_61; _11[7:0] = out_68;
  //   x[7:0] = out_7; _22[7:0] = out_62; _21[7:0] = out_69; _15[7:0] = out_14; _14[7:0] = out_27; _31[7:0] = out_70;
  //   _25[7:0] = out_15; _24[7:0] = out_28; _23[7:0] = out_43; _35[7:0] = out_16; _34[7:0] = out_29;
  //   _33[7:0] = out_44; _32[7:0] = out_63; on_or_off = in_1
endmodule

module bol2 (
  input  [7:0] in_1,
  input  in_2,
  input  in_3,
  input  in_4,
  output [31:0] out_5,
  output [31:0] out_6,
  output [31:0] out_7,
  output [31:0] out_8,
  output [31:0] out_9,
  output [31:0] out_10,
  output [31:0] out_11,
  output [31:0] out_12,
  output [31:0] out_13,
  output [31:0] out_14,
  output [31:0] out_15,
  output [31:0] out_16,
  output [31:0] out_17,
  output [31:0] out_18,
  output [31:0] out_19,
  output [31:0] out_20,
  output [31:0] out_21,
  output [31:0] out_22,
  output [31:0] out_23,
  output [31:0] out_24,
  output [31:0] out_25,
  output [31:0] out_26,
  output [31:0] out_27,
  output [31:0] out_28,
  output [31:0] out_29,
  output [31:0] out_30,
  output [31:0] out_31,
  output [31:0] out_32,
  output [31:0] out_33,
  output [31:0] out_34,
  output [31:0] out_35,
  output out_36
);

  wire _2, _3, and_1_out, and_2_out, and_3_out, and_4_out, and_5_out, clock_1_out, clock_2_out, not_1_out,
       or_1_out, or_2_out, or_3_out, register_1_q, register_2_q, rest, thxh_1_out_3,
       \επιτρεπτες_τημες_1_out_3 , \επιτρεπτες_τημες_1_out_4 ;
  wire [4:0] ma, xa;
  wire [31:0] adder_1_out, bot_sxedio_1_out_4, bot_sxedio_1_out_5, bot_sxedio_1_out_6, bot_sxedio_1_out_7,
       bot_sxedio_1_out_8, bot_sxedio_1_out_9, bot_sxedio_1_out_10, bot_sxedio_1_out_11, bot_sxedio_1_out_12,
       dejia_aristera_1_out_13, dejia_aristera_1_out_14, dejia_aristera_1_out_15, dejia_aristera_1_out_16,
       dejia_aristera_1_out_17, dejia_aristera_1_out_18, dejia_aristera_1_out_19, dejia_aristera_1_out_20,
       dejia_aristera_1_out_21, dejia_aristera_1_out_22, dejia_aristera_1_out_23, dejia_aristera_1_out_24,
       dejia_aristera_1_out_25, dejia_aristera_1_out_26, dejia_aristera_1_out_27, dejia_aristera_1_out_28,
       dejia_aristera_1_out_29, dejia_aristera_1_out_30, dejia_aristera_1_out_31, dejia_aristera_1_out_32,
       dejia_aristera_1_out_33, dejia_aristera_1_out_34, dejia_aristera_1_out_35, dejia_aristera_1_out_36,
       dejia_aristera_1_out_37, dejia_aristera_1_out_38, dejia_aristera_1_out_39, demultiplexer_1_out0,
       demultiplexer_1_out1, demultiplexer_1_out2, demultiplexer_1_out3, demultiplexer_1_out4,
       demultiplexer_1_out5, demultiplexer_1_out6, demultiplexer_1_out7, demultiplexer_1_out8,
       demultiplexer_1_out9, demultiplexer_1_out10, demultiplexer_1_out11, demultiplexer_1_out12,
       demultiplexer_1_out13, demultiplexer_1_out14, demultiplexer_1_out15, demultiplexer_1_out16,
       demultiplexer_1_out17, demultiplexer_1_out18, demultiplexer_1_out19, demultiplexer_1_out20,
       demultiplexer_1_out21, demultiplexer_1_out22, demultiplexer_1_out23, demultiplexer_1_out24,
       demultiplexer_1_out25, demultiplexer_1_out26, shift_register_1_q31;

  Register #(.width(1)) register_1 (.D(in_2), .Q(register_1_q), .clk(in_2), .clr(rest));  // open: en
  and and_1 (and_1_out, register_1_q, _2, clock_1_out);
  Clock clock_1 (.out(clock_1_out));
  Shift_Register #(.length(32)) shift_register_1 (
    .shift(1'b1), .in(1'b0), .clk(or_1_out), .load(in_2), .clr(rest), .d0(1'b1),
    .q0(shift_register_1_q31[31]), .d1(1'b0), .q1(shift_register_1_q31[30]), .d2(1'b0),
    .q2(shift_register_1_q31[29]), .d3(1'b0), .q3(shift_register_1_q31[28]), .d4(1'b0),
    .q4(shift_register_1_q31[27]), .d5(1'b0), .q5(shift_register_1_q31[26]), .d6(1'b0),
    .q6(shift_register_1_q31[25]), .d7(1'b0), .q7(shift_register_1_q31[24]), .d8(1'b0),
    .q8(shift_register_1_q31[23]), .d9(1'b0), .q9(shift_register_1_q31[22]), .d10(1'b0),
    .q10(shift_register_1_q31[21]), .d11(1'b0), .q11(shift_register_1_q31[20]), .d12(1'b0),
    .q12(shift_register_1_q31[19]), .d13(1'b0), .q13(shift_register_1_q31[18]), .d14(1'b0),
    .q14(shift_register_1_q31[17]), .d15(1'b0), .q15(shift_register_1_q31[16]), .d16(1'b0),
    .q16(shift_register_1_q31[15]), .d17(1'b0), .q17(shift_register_1_q31[14]), .d18(1'b0),
    .q18(shift_register_1_q31[13]), .d19(1'b0), .q19(_3), .d20(1'b0), .q20(shift_register_1_q31[11]),
    .d21(1'b0), .q21(shift_register_1_q31[10]), .d22(1'b0), .q22(shift_register_1_q31[9]), .d23(1'b0),
    .q23(rest), .d24(1'b0), .q24(shift_register_1_q31[7]), .d25(1'b0), .q25(shift_register_1_q31[6]),
    .d26(1'b0), .q26(shift_register_1_q31[5]), .d27(1'b0), .q27(shift_register_1_q31[4]), .d28(1'b0),
    .q28(shift_register_1_q31[3]), .d29(1'b0), .q29(shift_register_1_q31[2]), .d30(1'b0),
    .q30(shift_register_1_q31[1]), .d31(1'b0), .q31(shift_register_1_q31[0]));  // open: out
  or or_1 (or_1_out, and_1_out, in_2);
  Clock #(.highDuration(5), .lowDuration(5)) clock_2 (.out(clock_2_out));
  thxh thxh_1 (.in_1(or_2_out), .out_3(thxh_1_out_3), .in_2(in_3));
  or or_2 (or_2_out, in_4, in_3);
  not not_1 (not_1_out, thxh_1_out_3);
  and and_2 (and_2_out, clock_2_out, thxh_1_out_3);
  and and_3 (and_3_out, clock_2_out, not_1_out);
  not not_2 (_2, rest);
  DotMatrix #(.matrixcols(31), .matrixrows(32)) dotmatrix_1 (
    .col0(out_5), .col1(out_5), .col2(out_12), .col3(out_16), .col4(out_20), .col5(out_24), .col6(out_28),
    .col7(out_32), .col8(out_33), .col9(out_29), .col10(out_25), .col11(out_21), .col12(out_17),
    .col13(out_13), .col14(out_9), .col15(out_6), .col16(out_10), .col17(out_14), .col18(out_18),
    .col19(out_22), .col20(out_26), .col21(out_30), .col22(out_34), .col23(out_7), .col24(out_11),
    .col25(out_15), .col26(out_19), .col27(out_23), .col28(out_27), .col29(out_5), .col30(out_5));
  or or_3 (or_3_out, in_3, in_4);
  h h_1 (
    .in_1(demultiplexer_1_out26), .in_2(demultiplexer_1_out25), .in_3(demultiplexer_1_out24),
    .in_4(demultiplexer_1_out23), .in_5(demultiplexer_1_out22), .in_6(demultiplexer_1_out21),
    .in_7(demultiplexer_1_out20), .in_8(demultiplexer_1_out19), .in_9(demultiplexer_1_out18),
    .out_55(out_12), .out_56(out_16), .out_57(out_20), .out_58(out_24), .out_59(out_28), .out_60(out_32),
    .out_61(out_33), .out_62(out_29), .out_63(out_25), .out_64(out_21), .out_65(out_17), .out_66(out_13),
    .out_67(out_9), .out_68(out_6), .out_69(out_10), .out_70(out_14), .out_71(out_18), .out_72(out_22),
    .out_73(out_26), .out_74(out_30), .out_75(out_34), .out_76(out_7), .out_77(out_11), .out_78(out_15),
    .out_79(out_19), .out_80(out_23), .out_81(out_27), .in_28(dejia_aristera_1_out_13),
    .in_29(dejia_aristera_1_out_14), .in_30(dejia_aristera_1_out_15), .in_31(dejia_aristera_1_out_16),
    .in_32(dejia_aristera_1_out_17), .in_33(dejia_aristera_1_out_18), .in_34(dejia_aristera_1_out_19),
    .in_35(dejia_aristera_1_out_20), .in_36(dejia_aristera_1_out_21), .in_37(dejia_aristera_1_out_22),
    .in_38(dejia_aristera_1_out_23), .in_39(dejia_aristera_1_out_24), .in_40(dejia_aristera_1_out_25),
    .in_41(dejia_aristera_1_out_26), .in_42(dejia_aristera_1_out_27), .in_43(dejia_aristera_1_out_28),
    .in_44(dejia_aristera_1_out_29), .in_45(dejia_aristera_1_out_30), .in_46(dejia_aristera_1_out_31),
    .in_47(dejia_aristera_1_out_32), .in_48(dejia_aristera_1_out_33), .in_49(dejia_aristera_1_out_34),
    .in_50(dejia_aristera_1_out_35), .in_51(dejia_aristera_1_out_36), .in_52(dejia_aristera_1_out_37),
    .in_53(dejia_aristera_1_out_38), .in_54(dejia_aristera_1_out_39), .in_10(demultiplexer_1_out17),
    .in_11(demultiplexer_1_out16), .in_12(demultiplexer_1_out15), .in_13(demultiplexer_1_out14),
    .in_14(demultiplexer_1_out13), .in_15(demultiplexer_1_out12), .in_16(demultiplexer_1_out11),
    .in_17(demultiplexer_1_out10), .in_18(demultiplexer_1_out9), .in_19(demultiplexer_1_out8),
    .in_20(demultiplexer_1_out7), .in_21(demultiplexer_1_out6), .in_22(demultiplexer_1_out5),
    .in_23(demultiplexer_1_out4), .in_24(demultiplexer_1_out3), .in_25(demultiplexer_1_out2),
    .in_26(demultiplexer_1_out1), .in_27(demultiplexer_1_out0));
  dejia_aristera dejia_aristera_1 (
    .in_4(bot_sxedio_1_out_12), .in_5(bot_sxedio_1_out_11), .in_6(bot_sxedio_1_out_10),
    .in_7(bot_sxedio_1_out_9), .in_8(bot_sxedio_1_out_8), .in_9(bot_sxedio_1_out_7),
    .in_10(bot_sxedio_1_out_6), .in_11(bot_sxedio_1_out_5), .in_12(bot_sxedio_1_out_4),
    .out_13(dejia_aristera_1_out_13), .out_14(dejia_aristera_1_out_14), .out_15(dejia_aristera_1_out_15),
    .out_16(dejia_aristera_1_out_16), .out_17(dejia_aristera_1_out_17), .out_18(dejia_aristera_1_out_18),
    .out_19(dejia_aristera_1_out_19), .out_20(dejia_aristera_1_out_20), .out_21(dejia_aristera_1_out_21),
    .out_22(dejia_aristera_1_out_22), .out_23(dejia_aristera_1_out_23), .out_24(dejia_aristera_1_out_24),
    .out_25(dejia_aristera_1_out_25), .out_26(dejia_aristera_1_out_26), .out_27(dejia_aristera_1_out_27),
    .out_28(dejia_aristera_1_out_28), .out_29(dejia_aristera_1_out_29), .out_30(dejia_aristera_1_out_30),
    .out_31(dejia_aristera_1_out_31), .out_32(dejia_aristera_1_out_32), .out_33(dejia_aristera_1_out_33),
    .out_34(dejia_aristera_1_out_34), .out_35(dejia_aristera_1_out_35), .out_36(dejia_aristera_1_out_36),
    .out_37(dejia_aristera_1_out_37), .out_38(dejia_aristera_1_out_38), .out_39(dejia_aristera_1_out_39),
    .in_1(or_3_out), .in_2(and_2_out), .in_3(and_3_out), .out_40(ma));
  bot_sxedio bot_sxedio_1 (
    .out_15(out_5), .out_10(bot_sxedio_1_out_10), .out_11(bot_sxedio_1_out_11), .out_12(bot_sxedio_1_out_12),
    .out_4(bot_sxedio_1_out_4), .out_5(bot_sxedio_1_out_5), .out_6(bot_sxedio_1_out_6),
    .out_7(bot_sxedio_1_out_7), .out_8(bot_sxedio_1_out_8), .out_9(bot_sxedio_1_out_9));  // open: out_13, out_14, out_1, out_2, out_3
  Demultiplexer #(.select(5), .width(32), .enable("false")) demultiplexer_1 (
    .out0(demultiplexer_1_out0), .out1(demultiplexer_1_out1), .out2(demultiplexer_1_out2),
    .out3(demultiplexer_1_out3), .out4(demultiplexer_1_out4), .out5(demultiplexer_1_out5),
    .out6(demultiplexer_1_out6), .out7(demultiplexer_1_out7), .out8(demultiplexer_1_out8),
    .out9(demultiplexer_1_out9), .out10(demultiplexer_1_out10), .out11(demultiplexer_1_out11),
    .out12(demultiplexer_1_out12), .out13(demultiplexer_1_out13), .out14(demultiplexer_1_out14),
    .out15(demultiplexer_1_out15), .out16(demultiplexer_1_out16), .out17(demultiplexer_1_out17),
    .out18(demultiplexer_1_out18), .out19(demultiplexer_1_out19), .out20(demultiplexer_1_out20),
    .out21(demultiplexer_1_out21), .out22(demultiplexer_1_out22), .out23(demultiplexer_1_out23),
    .out24(demultiplexer_1_out24), .out25(demultiplexer_1_out25), .out26(demultiplexer_1_out26),
    .in(adder_1_out), .sel(xa));  // open: out27, out28, out29, out30, out31
  Adder #(.width(32)) adder_1 (
    .a({32{1'b0}}),
    .b({shift_register_1_q31[31:13], _3, shift_register_1_q31[11:9], rest, shift_register_1_q31[7:0]}),
    .out(adder_1_out));  // open: cin, cout
  Bit_Extender #(.out_width(5)) bit_extender_1 (.in(in_1), .out(xa));
  Register #(.width(1)) register_2 (.D(1'b1), .Q(register_2_q), .clk(in_2), .clr(rest));  // open: en
  \επιτρεπτες_τημες  \u_επιτρεπτες_τημες_1  (
    .in_2(xa), .out_3(\επιτρεπτες_τημες_1_out_3 ), .out_4(\επιτρεπτες_τημες_1_out_4 ), .in_1(ma));
  and and_4 (and_4_out, \επιτρεπτες_τημες_1_out_4 , \επιτρεπτες_τημες_1_out_3 );
  and and_5 (and_5_out, and_4_out, register_2_q);
  and and_6 (out_36, _3, and_5_out);

  assign out_8 = out_5;
  assign out_31 = out_5;
  assign out_35 = out_5;

  // Other names for the same wires on the sheet: xth = rest; _1 = in_2; start = in_4; πληρες_rest = in_3
endmodule

module \επιτρεπτες_τημες  (
  input  [4:0] in_1,
  input  [4:0] in_2,
  output out_3,
  output out_4
);

  wire comparator_1_eq, comparator_1_gt, comparator_2_eq, comparator_2_lt;
  wire [5:0] bit_extender_1_out, bit_extender_2_out, multiplexer_1_out, multiplexer_2_out;

  Multiplexer #(.select(5), .width(6), .enable("false")) multiplexer_1 (
    .in0({6{1'b0}}), .in1(6'b000001), .in2(6'b000010), .in3(6'b000011), .in4(6'b000100), .in5(6'b000101),
    .in6(6'b000110), .in7(6'b000111), .in8(6'b001000), .in9(6'b001001), .in10(6'b001010), .in11(6'b001011),
    .in12(6'b001100), .in13(6'b001101), .in14(6'b001110), .in15(6'b001111), .in16(6'b010000),
    .in17(6'b010001), .in18(6'b010010), .in19(6'b010011), .in20(6'b010100), .in21(6'b010101),
    .in22(6'b010110), .in23(6'b010111), .in24(6'b011000), .in25(6'b011001), .in26(6'b011010),
    .out(multiplexer_1_out), .sel(in_1));  // open: in27, in28, in29, in30, in31
  Multiplexer #(.select(5), .width(6), .enable("false")) multiplexer_2 (
    .in0(6'b001010), .in1(6'b001011), .in2(6'b001100), .in3(6'b001101), .in4(6'b001110), .in5(6'b001111),
    .in6(6'b010000), .in7(6'b010001), .in8(6'b010010), .in9(6'b010011), .in10(6'b010100), .in11(6'b010101),
    .in12(6'b010110), .in13(6'b010111), .in14(6'b011000), .in15(6'b011001), .in16(6'b011010),
    .in17(6'b011011), .in18(6'b011100), .in19(6'b011101), .in20(6'b011110), .in21(6'b011111),
    .in22(6'b100000), .in23(6'b100001), .in24(6'b100010), .in25(6'b100011), .in26(6'b100100),
    .out(multiplexer_2_out), .sel(in_1));  // open: in27, in28, in29, in30, in31
  assign bit_extender_1_out = {{1{1'b0}}, in_2};  // Bit_Extender bit_extender_1
  assign bit_extender_2_out = {{1{1'b0}}, in_2};  // Bit_Extender bit_extender_2
  Comparator #(.width(6)) comparator_1 (
    .a(bit_extender_1_out), .b(multiplexer_1_out), .gt(comparator_1_gt), .eq(comparator_1_eq));  // open: lt
  Comparator #(.width(6)) comparator_2 (
    .a(bit_extender_2_out), .b(multiplexer_2_out), .eq(comparator_2_eq), .lt(comparator_2_lt));  // open: gt
  or or_1 (out_3, comparator_1_gt, comparator_1_eq);
  or or_2 (out_4, comparator_2_eq, comparator_2_lt);
endmodule

module ok (
  input  in_1,
  output [7:0] out_2,
  output [7:0] out_3,
  output [7:0] out_4,
  output [7:0] out_5,
  output [7:0] out_6,
  output [7:0] out_7,
  output [7:0] out_8,
  output [7:0] out_9,
  output [7:0] out_10,
  output [7:0] out_11,
  output [7:0] out_12,
  output [7:0] out_13,
  output [7:0] out_14,
  output [7:0] out_15,
  output [7:0] out_16,
  output [7:0] out_17,
  output [7:0] out_18,
  output [7:0] out_19,
  output [7:0] out_20,
  output [7:0] out_21,
  output [7:0] out_22,
  output [7:0] out_23,
  output [7:0] out_24,
  output [7:0] out_25,
  output [7:0] out_26,
  output [7:0] out_27,
  output [7:0] out_28,
  output [7:0] out_29,
  output [7:0] out_30,
  output [7:0] out_31,
  output [7:0] out_32,
  output [7:0] out_33,
  output [7:0] out_34,
  output [7:0] out_35,
  output [7:0] out_36,
  output [7:0] out_37,
  output [7:0] out_38,
  output [7:0] out_39,
  output [7:0] out_40,
  output [7:0] out_41,
  output [7:0] out_42,
  output [7:0] out_43,
  output [7:0] out_44,
  output [7:0] out_45,
  output [7:0] out_46
);

  DotMatrix #(.matrixcols(32), .matrixrows(8)) dotmatrix_1 (
    .col0(out_2), .col1(out_2), .col2(out_2), .col3(out_2), .col4(out_2), .col5(out_2), .col6(out_2),
    .col7(out_2), .col8(out_38), .col9(out_37), .col10(out_36), .col11(out_35), .col12(out_34),
    .col13(out_2), .col14(out_32), .col15(out_31), .col16(out_30), .col17(out_29), .col18(out_2),
    .col19(out_27), .col20(out_26), .col21(out_25), .col22(out_24), .col23(out_23), .col24(out_2),
    .col25(out_2), .col26(out_20), .col27(out_18), .col28(out_18), .col29(out_17), .col30(out_2),
    .col31(out_2));
  F f_1 (.in_1(in_1), .out_2(out_38), .out_3(out_37), .out_4(out_36), .out_5(out_35), .out_6(out_34));
  G g_1 (.in_1(in_1), .out_2(out_27), .out_3(out_26), .out_4(out_25), .out_5(out_24), .out_6(out_23));
  I i_1 (.in_1(in_1), .out_2(out_2), .out_3(out_32), .out_4(out_31), .out_5(out_30), .out_6(out_29));
  H h_1 (.in_1(in_1), .out_2(out_2), .out_3(out_20), .out_4(out_18), .out_5(out_17), .out_6(out_2));
  DotMatrix #(.matrixcols(13), .matrixrows(8)) dotmatrix_2 (
    .col0(out_14), .col1(out_13), .col2(out_12), .col3(out_11), .col4(out_10), .col5(out_2), .col6(out_2),
    .col7(out_2), .col8(out_2), .col9(out_2), .col10(out_2), .col11(out_2), .col12(out_2));
  T t_1 (.in_1(in_1), .out_2(out_14), .out_3(out_13), .out_4(out_12), .out_5(out_11), .out_6(out_10));

  assign out_3 = out_2;
  assign out_4 = out_2;
  assign out_5 = out_2;
  assign out_6 = out_2;
  assign out_7 = out_2;
  assign out_8 = out_2;
  assign out_9 = out_2;
  assign out_15 = out_2;
  assign out_16 = out_2;
  assign out_19 = out_18;
  assign out_21 = out_2;
  assign out_22 = out_2;
  assign out_28 = out_2;
  assign out_33 = out_2;
  assign out_39 = out_2;
  assign out_40 = out_2;
  assign out_41 = out_2;
  assign out_42 = out_2;
  assign out_43 = out_2;
  assign out_44 = out_2;
  assign out_45 = out_2;
  assign out_46 = out_2;
endmodule

module onoma (
  input  [6:0] in_1,
  input  in_2,
  output [7:0] out_3,
  output [7:0] out_4,
  output [7:0] out_5,
  output [7:0] out_6,
  output [7:0] out_7,
  output [7:0] out_8,
  output [7:0] out_9,
  output [7:0] out_10,
  output [7:0] out_11,
  output [7:0] out_12,
  output [7:0] out_13,
  output [7:0] out_14,
  output [7:0] out_15,
  output [7:0] out_16,
  output [7:0] out_17,
  output [7:0] out_18,
  output [7:0] out_19,
  output [7:0] out_20,
  output [7:0] out_21,
  output [7:0] out_22,
  output [7:0] out_23,
  output [7:0] out_24,
  output [7:0] out_25,
  output [7:0] out_26,
  output [7:0] out_27,
  output [7:0] out_28,
  output [7:0] out_29,
  output [7:0] out_30,
  output [7:0] out_31,
  output [7:0] out_32,
  output [7:0] out_33
);

  ss ss_1 (
    .out_5(out_28), .out_6(out_23), .out_7(out_18), .out_8(out_13), .out_9(out_8), .out_10(out_3),
    .out_11(out_29), .out_12(out_24), .out_13(out_19), .out_14(out_14), .out_15(out_9), .out_16(out_4),
    .out_17(out_30), .out_18(out_25), .out_19(out_20), .out_20(out_15), .out_21(out_10), .out_22(out_5),
    .out_23(out_31), .out_24(out_26), .out_25(out_21), .out_26(out_16), .out_27(out_11), .out_28(out_6),
    .out_29(out_32), .out_30(out_27), .out_31(out_22), .out_32(out_17), .out_33(out_12), .out_34(out_7),
    .out_35(out_33), .in_2(in_2), .in_1(in_1));  // open: out_3, out_4
endmodule

module bos_xelu (
  output [7:0] out_1,
  output [7:0] out_2,
  output [7:0] out_3,
  output [7:0] out_4,
  output [7:0] out_5,
  output [7:0] out_6,
  output [7:0] out_7,
  output [7:0] out_8,
  output [7:0] out_9,
  output [7:0] out_10,
  output [7:0] out_11,
  output [7:0] out_12,
  output [7:0] out_13,
  output [7:0] out_14,
  output [7:0] out_15,
  output [7:0] out_16,
  output [7:0] out_17
);

  B b_1 (.in_1(1'b1), .out_2(out_17), .out_3(out_16), .out_4(out_15), .out_5(out_14), .out_6(out_13));
  O o_1 (.in_1(1'b1), .out_2(out_11), .out_3(out_10), .out_4(out_7), .out_5(out_8), .out_6(out_9));
  S s_1 (.in_1(1'b1), .out_2(out_5), .out_3(out_4), .out_4(out_3), .out_5(out_2), .out_6(out_1));

  assign out_6 = {8{1'b0}};
  assign out_12 = {8{1'b0}};
endmodule

module sos (
  input  in_1,
  input  in_2,
  input  in_3,
  input  in_4,
  input  [1:0] in_5,
  input  [1:0] in_6,
  output [31:0] out_7,
  output [31:0] out_8,
  output [31:0] out_9,
  output [31:0] out_10,
  output [31:0] out_11,
  output [31:0] out_12,
  output [31:0] out_13,
  output [31:0] out_14,
  output [31:0] out_15,
  output [31:0] out_16,
  output [31:0] out_17,
  output [31:0] out_18,
  output [31:0] out_19,
  output [31:0] out_20,
  output [31:0] out_21,
  output [31:0] out_22,
  output [31:0] out_23,
  output [31:0] out_24,
  output [31:0] out_25,
  output [31:0] out_26,
  output [31:0] out_27,
  output [31:0] out_28,
  output [31:0] out_29,
  output [31:0] out_30,
  output [31:0] out_31,
  output [31:0] out_32,
  output [31:0] out_33,
  output [31:0] out_34,
  output [31:0] out_35,
  output [31:0] out_36,
  output [31:0] out_37,
  output [7:0] out_38,
  output out_39
);

  wire button_1_out, button_2_out, register_1_q;
  wire [1:0] _1, _1a, _2, _2a;
  wire [7:0] n1_1_out_5, n1_1_out_6;
  wire [31:0] n1_1_out_7, n1_1_out_9, n1_1_out_11, n1_1_out_12, n1_1_out_13, n1_1_out_14, n1_1_out_15,
       n1_1_out_16, n1_1_out_17, n1_1_out_18, n1_1_out_19, n1_1_out_20, n1_1_out_21, n1_1_out_22,
       n1_1_out_23, n1_1_out_24, n1_1_out_25, n1_1_out_26, n1_1_out_27, n1_1_out_28, n1_1_out_29,
       n1_1_out_30, n1_1_out_31, n1_1_out_32, n1_1_out_34, n1_1_out_36, n1_1_out_37;

  Register #(.width(1)) register_1 (
    .D(button_1_out), .Q(register_1_q), .clk(button_1_out), .clr(button_2_out));  // open: en
  Button button_1 (.out(button_1_out));
  Button button_2 (.out(button_2_out));
  Joystick #(.bits(2)) joystick_1 (.x(_1a), .y(_2a));
  Multiplexer #(.width(2), .enable("false")) multiplexer_1 (.in0(in_5), .in1(_1a), .out(_1), .sel(register_1_q));
  Multiplexer #(.width(2), .enable("false")) multiplexer_2 (.in0(in_6), .in1(_2a), .out(_2), .sel(register_1_q));
  bol bol_1 (
    .in_4(n1_1_out_31), .in_6(n1_1_out_29), .in_9(n1_1_out_6), .in_7(n1_1_out_27), .in_8(n1_1_out_25),
    .in_10(n1_1_out_23), .in_11(n1_1_out_21), .in_12(n1_1_out_19), .in_13(n1_1_out_17), .in_14(n1_1_out_15),
    .in_15(n1_1_out_13), .in_16(n1_1_out_11), .out_34(out_35), .out_35(out_34), .out_36(out_33),
    .out_37(out_32), .out_39(out_31), .out_40(out_30), .out_41(out_29), .out_42(out_28), .out_43(out_27),
    .out_44(out_26), .out_45(out_25), ._0(in_3), .start(in_1), .out_33(out_39), .in_5(n1_1_out_5),
    .in_3(in_4), .out_38(out_38), .in_17(n1_1_out_9), .out_46(out_24), .in_18(n1_1_out_7), .out_47(out_23),
    .in_19(n1_1_out_37), .out_48(out_22), .in_20(n1_1_out_36), .out_49(out_21), .in_21(n1_1_out_34),
    .out_50(out_20), .in_22(n1_1_out_32), .out_51(out_19), .in_23(n1_1_out_30), .out_52(out_18),
    .in_24(n1_1_out_28), .out_53(out_17), .in_25(n1_1_out_26), .out_54(out_16), .in_26(n1_1_out_24),
    .out_55(out_15), .in_27(n1_1_out_22), .out_56(out_14), .in_28(n1_1_out_20), .out_57(out_13),
    .in_29(n1_1_out_18), .out_58(out_12), .in_30(n1_1_out_16), .out_59(out_11), .in_31(n1_1_out_14),
    .out_60(out_10), .in_32(n1_1_out_12), .out_61(out_9));
  _1 u_1_1 (
    .in_3(_1), .in_4(_2), .in_1(in_2), .in_2(in_3), .out_35(out_37), .out_33(out_36), .out_31(n1_1_out_31),
    .out_29(n1_1_out_29), .out_27(n1_1_out_27), .out_25(n1_1_out_25), .out_23(n1_1_out_23),
    .out_21(n1_1_out_21), .out_19(n1_1_out_19), .out_17(n1_1_out_17), .out_15(n1_1_out_15),
    .out_13(n1_1_out_13), .out_11(n1_1_out_11), .out_9(n1_1_out_9), .out_7(n1_1_out_7), .out_6(n1_1_out_6),
    .out_5(n1_1_out_5), .out_10(out_8), .out_12(n1_1_out_12), .out_14(n1_1_out_14), .out_16(n1_1_out_16),
    .out_18(n1_1_out_18), .out_20(n1_1_out_20), .out_22(n1_1_out_22), .out_24(n1_1_out_24),
    .out_26(n1_1_out_26), .out_28(n1_1_out_28), .out_30(n1_1_out_30), .out_32(n1_1_out_32),
    .out_34(n1_1_out_34), .out_36(n1_1_out_36), .out_37(n1_1_out_37), .out_8(out_7));

  // Other names for the same wires on the sheet: rest = in_3; sp = in_1; start = in_2
endmodule

module bol (
  input  start,
  input  _0,
  input  in_3,
  input  [31:0] in_4,
  input  [7:0] in_5,
  input  [31:0] in_6,
  input  [31:0] in_7,
  input  [31:0] in_8,
  input  [7:0] in_9,
  input  [31:0] in_10,
  input  [31:0] in_11,
  input  [31:0] in_12,
  input  [31:0] in_13,
  input  [31:0] in_14,
  input  [31:0] in_15,
  input  [31:0] in_16,
  input  [31:0] in_17,
  input  [31:0] in_18,
  input  [31:0] in_19,
  input  [31:0] in_20,
  input  [31:0] in_21,
  input  [31:0] in_22,
  input  [31:0] in_23,
  input  [31:0] in_24,
  input  [31:0] in_25,
  input  [31:0] in_26,
  input  [31:0] in_27,
  input  [31:0] in_28,
  input  [31:0] in_29,
  input  [31:0] in_30,
  input  [31:0] in_31,
  input  [31:0] in_32,
  output out_33,
  output [31:0] out_34,
  output [31:0] out_35,
  output [31:0] out_36,
  output [31:0] out_37,
  output [7:0] out_38,
  output [31:0] out_39,
  output [31:0] out_40,
  output [31:0] out_41,
  output [31:0] out_42,
  output [31:0] out_43,
  output [31:0] out_44,
  output [31:0] out_45,
  output [31:0] out_46,
  output [31:0] out_47,
  output [31:0] out_48,
  output [31:0] out_49,
  output [31:0] out_50,
  output [31:0] out_51,
  output [31:0] out_52,
  output [31:0] out_53,
  output [31:0] out_54,
  output [31:0] out_55,
  output [31:0] out_56,
  output [31:0] out_57,
  output [31:0] out_58,
  output [31:0] out_59,
  output [31:0] out_60,
  output [31:0] out_61
);

  wire _1, clock_1_out, decoder_1_out0, decoder_1_out1, decoder_1_out2, decoder_1_out3, decoder_1_out4,
       decoder_1_out5, decoder_1_out6, decoder_1_out7, decoder_1_out8, decoder_1_out9, decoder_1_out10,
       decoder_1_out11, decoder_1_out12, decoder_1_out13, decoder_1_out14, decoder_1_out15, decoder_1_out16,
       decoder_1_out17, decoder_1_out18, decoder_1_out19, decoder_1_out20, decoder_1_out21, decoder_1_out22,
       decoder_1_out23, decoder_1_out24, decoder_1_out25, decoder_1_out26, or_1_out, or_2_out, or_3_out,
       or_4_out, register_1_q, sos;
  wire [4:0] bit_extender_1_out, bit_extender_2_out;
  wire [31:0] adder_1_out, adder_2_out, adder_3_out, adder_4_out, adder_5_out, adder_6_out, adder_7_out,
       adder_8_out, adder_9_out, adder_10_out, adder_11_out, adder_12_out, adder_13_out, adder_14_out,
       adder_15_out, adder_16_out, adder_17_out, adder_18_out, adder_19_out, adder_20_out, adder_21_out,
       adder_22_out, adder_23_out, adder_24_out, adder_25_out, adder_26_out, adder_27_out, multiplexer_1_out,
       shift_register_1_q31;

  Bit_Extender #(.out_width(5)) bit_extender_1 (.in(in_5), .out(bit_extender_1_out));
  Multiplexer #(.select(5), .width(32), .enable("false")) multiplexer_1 (
    .in4(32'h8000000), .in5(32'h4000000), .in6(32'h2000000), .in7(32'h1000000), .in8(32'h800000),
    .in9(32'h400000), .in10(32'h200000), .in11(32'h100000), .in12(32'h80000), .in13(32'h40000),
    .in14(32'h20000), .in15(32'h10000), .in16(32'h8000), .in17(32'h4000), .in18(32'h2000), .in19(32'h1000),
    .out(multiplexer_1_out), .sel(bit_extender_1_out));  // open: in0, in1, in2, in3, in20, in21, in22, in23, in24, in25, in26, in27, in28, in29, in30, in31
  Button button_1 ();  // open: out
  or or_1 (or_1_out, sos, start);
  Shift_Register #(.length(32)) shift_register_1 (
    .shift(1'b1), .in(1'b0), .clk(or_1_out), .out(_1), .load(start), .clr(or_2_out),
    .d0(multiplexer_1_out[31]), .q0(shift_register_1_q31[31]), .d1(multiplexer_1_out[30]),
    .q1(shift_register_1_q31[30]), .d2(multiplexer_1_out[29]), .q2(shift_register_1_q31[29]),
    .d3(multiplexer_1_out[28]), .q3(shift_register_1_q31[28]), .d4(multiplexer_1_out[27]),
    .q4(shift_register_1_q31[27]), .d5(multiplexer_1_out[26]), .q5(shift_register_1_q31[26]),
    .d6(multiplexer_1_out[25]), .q6(shift_register_1_q31[25]), .d7(multiplexer_1_out[24]),
    .q7(shift_register_1_q31[24]), .d8(multiplexer_1_out[23]), .q8(shift_register_1_q31[23]),
    .d9(multiplexer_1_out[22]), .q9(shift_register_1_q31[22]), .d10(multiplexer_1_out[21]),
    .q10(shift_register_1_q31[21]), .d11(multiplexer_1_out[20]), .q11(shift_register_1_q31[20]),
    .d12(multiplexer_1_out[19]), .q12(shift_register_1_q31[19]), .d13(multiplexer_1_out[18]),
    .q13(shift_register_1_q31[18]), .d14(multiplexer_1_out[17]), .q14(shift_register_1_q31[17]),
    .d15(multiplexer_1_out[16]), .q15(shift_register_1_q31[16]), .d16(multiplexer_1_out[15]),
    .q16(shift_register_1_q31[15]), .d17(multiplexer_1_out[14]), .q17(shift_register_1_q31[14]),
    .d18(multiplexer_1_out[13]), .q18(shift_register_1_q31[13]), .d19(multiplexer_1_out[12]),
    .q19(shift_register_1_q31[12]), .d20(multiplexer_1_out[11]), .q20(shift_register_1_q31[11]),
    .d21(multiplexer_1_out[10]), .q21(shift_register_1_q31[10]), .d22(multiplexer_1_out[9]),
    .q22(shift_register_1_q31[9]), .d23(multiplexer_1_out[8]), .q23(shift_register_1_q31[8]),
    .d24(multiplexer_1_out[7]), .q24(shift_register_1_q31[7]), .d25(multiplexer_1_out[6]),
    .q25(shift_register_1_q31[6]), .d26(multiplexer_1_out[5]), .q26(shift_register_1_q31[5]),
    .d27(multiplexer_1_out[4]), .q27(shift_register_1_q31[4]), .d28(multiplexer_1_out[3]),
    .q28(shift_register_1_q31[3]), .d29(multiplexer_1_out[2]), .q29(shift_register_1_q31[2]),
    .d30(multiplexer_1_out[1]), .q30(shift_register_1_q31[1]), .d31(multiplexer_1_out[0]),
    .q31(shift_register_1_q31[0]));
  or or_2 (or_2_out, _0, _1);
  or or_3 (or_3_out, _0, _1);
  Adder #(.width(32)) adder_1 (.a(in_4), .b(shift_register_1_q31), .out(adder_1_out));  // open: cin, cout
  Adder #(.width(32)) adder_2 (.a(in_6), .b(shift_register_1_q31), .out(adder_2_out));  // open: cin, cout
  Adder #(.width(32)) adder_3 (.a(in_7), .b(shift_register_1_q31), .out(adder_3_out));  // open: cin, cout
  Adder #(.width(32)) adder_4 (.a(in_8), .b(shift_register_1_q31), .out(adder_4_out));  // open: cin, cout
  Adder #(.width(32)) adder_5 (.a(in_10), .b(shift_register_1_q31), .out(adder_5_out));  // open: cin, cout
  Adder #(.width(32)) adder_6 (.a(in_11), .b(shift_register_1_q31), .out(adder_6_out));  // open: cin, cout
  Adder #(.width(32)) adder_7 (.a(in_12), .b(shift_register_1_q31), .out(adder_7_out));  // open: cin, cout
  Adder #(.width(32)) adder_8 (.a(in_13), .b(shift_register_1_q31), .out(adder_8_out));  // open: cin, cout
  Adder #(.width(32)) adder_9 (.a(in_14), .b(shift_register_1_q31), .out(adder_9_out));  // open: cin, cout
  Adder #(.width(32)) adder_10 (.a(in_15), .b(shift_register_1_q31), .out(adder_10_out));  // open: cin, cout
  Adder #(.width(32)) adder_11 (.a(in_16), .b(shift_register_1_q31), .out(adder_11_out));  // open: cin, cout
  Adder #(.width(32)) adder_12 (.a(in_17), .b(shift_register_1_q31), .out(adder_12_out));  // open: cin, cout
  Adder #(.width(32)) adder_13 (.a(in_18), .b(shift_register_1_q31), .out(adder_13_out));  // open: cin, cout
  Adder #(.width(32)) adder_14 (.a(in_19), .b(shift_register_1_q31), .out(adder_14_out));  // open: cin, cout
  Adder #(.width(32)) adder_15 (.a(in_20), .b(shift_register_1_q31), .out(adder_15_out));  // open: cin, cout
  Adder #(.width(32)) adder_16 (.a(in_21), .b(shift_register_1_q31), .out(adder_16_out));  // open: cin, cout
  Adder #(.width(32)) adder_17 (.a(in_22), .b(shift_register_1_q31), .out(adder_17_out));  // open: cin, cout
  Adder #(.width(32)) adder_18 (.a(in_23), .b(shift_register_1_q31), .out(adder_18_out));  // open: cin, cout
  Adder #(.width(32)) adder_19 (.a(in_24), .b(shift_register_1_q31), .out(adder_19_out));  // open: cin, cout
  Adder #(.width(32)) adder_20 (.a(in_25), .b(shift_register_1_q31), .out(adder_20_out));  // open: cin, cout
  Adder #(.width(32)) adder_21 (.a(in_26), .b(shift_register_1_q31), .out(adder_21_out));  // open: cin, cout
  Adder #(.width(32)) adder_22 (.a(in_27), .b(shift_register_1_q31), .out(adder_22_out));  // open: cin, cout
  Adder #(.width(32)) adder_23 (.a(in_28), .b(shift_register_1_q31), .out(adder_23_out));  // open: cin, cout
  Adder #(.width(32)) adder_24 (.a(in_29), .b(shift_register_1_q31), .out(adder_24_out));  // open: cin, cout
  Adder #(.width(32)) adder_25 (.a(in_30), .b(shift_register_1_q31), .out(adder_25_out));  // open: cin, cout
  Adder #(.width(32)) adder_26 (.a(in_31), .b(shift_register_1_q31), .out(adder_26_out));  // open: cin, cout
  Adder #(.width(32)) adder_27 (.a(in_32), .b(shift_register_1_q31), .out(adder_27_out));  // open: cin, cout
  and and_1 (sos, register_1_q, clock_1_out);
  Register #(.width(1)) register_1 (.D(start), .Q(register_1_q), .clk(start), .clr(or_3_out));  // open: en
  Clock clock_1 (.out(clock_1_out));
  Register #(.width(1)) register_2 (.D(_1), .Q(out_33), .clk(_1), .clr(or_4_out));  // open: en
  or or_4 (or_4_out, _0, in_3, start);
  DotMatrix #(.matrixcols(3), .matrixrows(32)) dotmatrix_1 (.col1(out_34));  // open: col0, col2
  Multiplexer #(.width(32), .enable("false")) multiplexer_2 (
    .in0(in_4), .in1(adder_1_out), .out(out_34), .sel(decoder_1_out0));
  Multiplexer #(.width(32), .enable("false")) multiplexer_3 (
    .in0(in_6), .in1(adder_2_out), .out(out_35), .sel(decoder_1_out1));
  Multiplexer #(.width(32), .enable("false")) multiplexer_4 (
    .in0(in_7), .in1(adder_3_out), .out(out_36), .sel(decoder_1_out2));
  Multiplexer #(.width(32), .enable("false")) multiplexer_5 (
    .in0(in_8), .in1(adder_4_out), .out(out_37), .sel(decoder_1_out3));
  Multiplexer #(.width(32), .enable("false")) multiplexer_6 (
    .in0(in_10), .in1(adder_5_out), .out(out_39), .sel(decoder_1_out4));
  Multiplexer #(.width(32), .enable("false")) multiplexer_7 (
    .in0(in_11), .in1(adder_6_out), .out(out_40), .sel(decoder_1_out5));
  Multiplexer #(.width(32), .enable("false")) multiplexer_8 (
    .in0(in_12), .in1(adder_7_out), .out(out_41), .sel(decoder_1_out6));
  Multiplexer #(.width(32), .enable("false")) multiplexer_9 (
    .in0(in_13), .in1(adder_8_out), .out(out_42), .sel(decoder_1_out7));
  Multiplexer #(.width(32), .enable("false")) multiplexer_10 (
    .in0(in_14), .in1(adder_9_out), .out(out_43), .sel(decoder_1_out8));
  Multiplexer #(.width(32), .enable("false")) multiplexer_11 (
    .in0(in_15), .in1(adder_10_out), .out(out_44), .sel(decoder_1_out9));
  Multiplexer #(.width(32), .enable("false")) multiplexer_12 (
    .in0(in_16), .in1(adder_11_out), .out(out_45), .sel(decoder_1_out10));
  Multiplexer #(.width(32), .enable("false")) multiplexer_13 (
    .in0(in_17), .in1(adder_12_out), .out(out_46), .sel(decoder_1_out11));
  Multiplexer #(.width(32), .enable("false")) multiplexer_14 (
    .in0(in_18), .in1(adder_13_out), .out(out_47), .sel(decoder_1_out12));
  Multiplexer #(.width(32), .enable("false")) multiplexer_15 (
    .in0(in_19), .in1(adder_14_out), .out(out_48), .sel(decoder_1_out13));
  Multiplexer #(.width(32), .enable("false")) multiplexer_16 (
    .in0(in_20), .in1(adder_15_out), .out(out_49), .sel(decoder_1_out14));
  Multiplexer #(.width(32), .enable("false")) multiplexer_17 (
    .in0(in_21), .in1(adder_16_out), .out(out_50), .sel(decoder_1_out15));
  Multiplexer #(.width(32), .enable("false")) multiplexer_18 (
    .in0(in_22), .in1(adder_17_out), .out(out_51), .sel(decoder_1_out16));
  Multiplexer #(.width(32), .enable("false")) multiplexer_19 (
    .in0(in_23), .in1(adder_18_out), .out(out_52), .sel(decoder_1_out17));
  Multiplexer #(.width(32), .enable("false")) multiplexer_20 (
    .in0(in_24), .in1(adder_19_out), .out(out_53), .sel(decoder_1_out18));
  Multiplexer #(.width(32), .enable("false")) multiplexer_21 (
    .in0(in_25), .in1(adder_20_out), .out(out_54), .sel(decoder_1_out19));
  Multiplexer #(.width(32), .enable("false")) multiplexer_22 (
    .in0(in_26), .in1(adder_21_out), .out(out_55), .sel(decoder_1_out20));
  Multiplexer #(.width(32), .enable("false")) multiplexer_23 (
    .in0(in_27), .in1(adder_22_out), .out(out_56), .sel(decoder_1_out21));
  Multiplexer #(.width(32), .enable("false")) multiplexer_24 (
    .in0(in_28), .in1(adder_23_out), .out(out_57), .sel(decoder_1_out22));
  Multiplexer #(.width(32), .enable("false")) multiplexer_25 (
    .in0(in_29), .in1(adder_24_out), .out(out_58), .sel(decoder_1_out23));
  Multiplexer #(.width(32), .enable("false")) multiplexer_26 (
    .in0(in_30), .in1(adder_25_out), .out(out_59), .sel(decoder_1_out24));
  Multiplexer #(.width(32), .enable("false")) multiplexer_27 (
    .in0(in_31), .in1(adder_26_out), .out(out_60), .sel(decoder_1_out25));
  Multiplexer #(.width(32), .enable("false")) multiplexer_28 (
    .in0(in_32), .in1(adder_27_out), .out(out_61), .sel(decoder_1_out26));
  Register register_3 (.D(in_9), .Q(out_38), .clk(start), .clr(_0));  // open: en
  Bit_Extender #(.out_width(5)) bit_extender_2 (.in(out_38), .out(bit_extender_2_out));
  Decoder #(.select(5), .enable("false")) decoder_1 (
    .out0(decoder_1_out0), .out1(decoder_1_out1), .out2(decoder_1_out2), .out3(decoder_1_out3),
    .out4(decoder_1_out4), .out5(decoder_1_out5), .out6(decoder_1_out6), .out7(decoder_1_out7),
    .out8(decoder_1_out8), .out9(decoder_1_out9), .out10(decoder_1_out10), .out11(decoder_1_out11),
    .out12(decoder_1_out12), .out13(decoder_1_out13), .out14(decoder_1_out14), .out15(decoder_1_out15),
    .out16(decoder_1_out16), .out17(decoder_1_out17), .out18(decoder_1_out18), .out19(decoder_1_out19),
    .out20(decoder_1_out20), .out21(decoder_1_out21), .out22(decoder_1_out22), .out23(decoder_1_out23),
    .out24(decoder_1_out24), .out25(decoder_1_out25), .out26(decoder_1_out26), .sel(bit_extender_2_out));  // open: out27, out28, out29, out30, out31

  // Other names for the same wires on the sheet: s = start
endmodule

module _1 (
  input  in_1,
  input  in_2,
  input  [1:0] in_3,
  input  [1:0] in_4,
  output [7:0] out_5,
  output [7:0] out_6,
  output [31:0] out_7,
  output [31:0] out_8,
  output [31:0] out_9,
  output [31:0] out_10,
  output [31:0] out_11,
  output [31:0] out_12,
  output [31:0] out_13,
  output [31:0] out_14,
  output [31:0] out_15,
  output [31:0] out_16,
  output [31:0] out_17,
  output [31:0] out_18,
  output [31:0] out_19,
  output [31:0] out_20,
  output [31:0] out_21,
  output [31:0] out_22,
  output [31:0] out_23,
  output [31:0] out_24,
  output [31:0] out_25,
  output [31:0] out_26,
  output [31:0] out_27,
  output [31:0] out_28,
  output [31:0] out_29,
  output [31:0] out_30,
  output [31:0] out_31,
  output [31:0] out_32,
  output [31:0] out_33,
  output [31:0] out_34,
  output [31:0] out_35,
  output [31:0] out_36,
  output [31:0] out_37
);

  wire and_1_out, and_2_out, and_3_out, and_4_out, and_5_out, and_6_out, and_7_out, and_8_out,
       comparator_1_eq, comparator_2_lt, comparator_3_eq, comparator_4_lt, d, m, not_1_out, not_2_out,
       not_3_out, not_4_out, or_1_out, or_2_out, or_3_out, or_4_out, or_5_out, or_6_out, or_7_out, or_8_out,
       or_9_out, or_10_out, register_1_q, tunnel, tunnel_t;
  wire [31:0] n2_1_out_6, n2_2_out_6, n2_3_out_6, n2_4_out_6, n2_5_out_6, n3_1_out_10, n3_1_out_11,
       n3_1_out_12, n3_1_out_13, n3_1_out_14, n3_1_out_15, n3_1_out_16, n3_1_out_17, n3_1_out_18,
       n3_1_out_19, n3_1_out_20, n3_1_out_21, n3_1_out_22, n3_1_out_23, n3_1_out_24, n3_1_out_25,
       n3_1_out_26, n3_1_out_27, n3_1_out_28, n3_1_out_29, n3_1_out_30, n3_1_out_31, n3_1_out_32,
       n3_1_out_33, n3_1_out_34, n3_1_out_35, n3_1_out_36, n3_1_out_37, n3_1_out_38, n3_1_out_39, n3_1_out_40;

  Register #(.width(1)) register_1 (.D(in_2), .Q(register_1_q), .clk(in_2), .clr(in_1));  // open: en
  j j_1 (.out_3(tunnel_t), .in_2(in_3), .out_4(tunnel), .in_1(in_4), .out_5(m), .out_6(d));
  or or_1 (or_1_out, tunnel_t, tunnel);
  _2 u_2_1 (.in_1(32'hc), .in_2(tunnel_t), .out_6(n2_1_out_6), .in_4(or_1_out), .in_3(in_2), .in_5(in_1));
  _2 u_2_2 (.in_1(32'he), .in_2(tunnel_t), .out_6(n2_2_out_6), .in_4(or_1_out), .in_3(in_2), .in_5(in_1));
  _2 u_2_3 (.in_1(32'hf), .in_2(tunnel_t), .out_6(n2_3_out_6), .in_4(or_1_out), .in_3(in_2), .in_5(in_1));
  _2 u_2_4 (.in_1(32'he), .in_2(tunnel_t), .out_6(n2_4_out_6), .in_4(or_1_out), .in_3(in_2), .in_5(in_1));
  _2 u_2_5 (.in_1(32'hc), .in_2(tunnel_t), .out_6(n2_5_out_6), .in_4(or_1_out), .in_3(in_2), .in_5(in_1));
  _3 u_3_1 (
    .in_2(n2_1_out_6), .in_6(n2_2_out_6), .in_7(n2_3_out_6), .in_8(n2_4_out_6), .in_9(n2_5_out_6), .in_4(m),
    .out_10(n3_1_out_10), .out_11(n3_1_out_11), .out_12(n3_1_out_12), .out_13(n3_1_out_13),
    .out_14(n3_1_out_14), .out_15(n3_1_out_15), .out_16(n3_1_out_16), .out_17(n3_1_out_17),
    .out_18(n3_1_out_18), .out_19(n3_1_out_19), .out_20(n3_1_out_20), .out_21(n3_1_out_21),
    .out_22(n3_1_out_22), .out_23(n3_1_out_23), .out_24(n3_1_out_24), .in_3(or_2_out), .in_5(in_2),
    .in_1(in_1), .out_25(n3_1_out_25), .out_26(n3_1_out_26), .out_27(n3_1_out_27), .out_28(n3_1_out_28),
    .out_29(n3_1_out_29), .out_30(n3_1_out_30), .out_31(n3_1_out_31), .out_32(n3_1_out_32),
    .out_33(n3_1_out_33), .out_34(n3_1_out_34), .out_35(n3_1_out_35), .out_36(n3_1_out_36),
    .out_37(n3_1_out_37), .out_38(n3_1_out_38), .out_39(n3_1_out_39), .out_40(n3_1_out_40));
  or or_2 (or_2_out, m, d);
  Multiplexer #(.width(32), .enable("false")) multiplexer_1 (
    .in0(n3_1_out_10), .in1({32{1'b0}}), .out(out_35), .sel(register_1_q));
  Multiplexer #(.width(32), .enable("false")) multiplexer_2 (
    .in0(n3_1_out_11), .in1({32{1'b0}}), .out(out_33), .sel(register_1_q));
  Multiplexer #(.width(32), .enable("false")) multiplexer_3 (
    .in0(n3_1_out_12), .in1({32{1'b0}}), .out(out_31), .sel(register_1_q));
  Multiplexer #(.width(32), .enable("false")) multiplexer_4 (
    .in0(n3_1_out_13), .in1({32{1'b0}}), .out(out_29), .sel(register_1_q));
  Multiplexer #(.width(32), .enable("false")) multiplexer_5 (
    .in0(n3_1_out_14), .in1({32{1'b0}}), .out(out_27), .sel(register_1_q));
  Multiplexer #(.width(32), .enable("false")) multiplexer_6 (
    .in0(n3_1_out_15), .in1({32{1'b0}}), .out(out_25), .sel(register_1_q));
  Multiplexer #(.width(32), .enable("false")) multiplexer_7 (
    .in0(n3_1_out_16), .in1({32{1'b0}}), .out(out_23), .sel(register_1_q));
  Multiplexer #(.width(32), .enable("false")) multiplexer_8 (
    .in0(n3_1_out_17), .in1({32{1'b0}}), .out(out_21), .sel(register_1_q));
  Multiplexer #(.width(32), .enable("false")) multiplexer_9 (
    .in0(n3_1_out_18), .in1({32{1'b0}}), .out(out_19), .sel(register_1_q));
  Multiplexer #(.width(32), .enable("false")) multiplexer_10 (
    .in0(n3_1_out_19), .in1({32{1'b0}}), .out(out_17), .sel(register_1_q));
  Multiplexer #(.width(32), .enable("false")) multiplexer_11 (
    .in0(n3_1_out_20), .in1({32{1'b0}}), .out(out_15), .sel(register_1_q));
  Multiplexer #(.width(32), .enable("false")) multiplexer_12 (
    .in0(n3_1_out_21), .in1({32{1'b0}}), .out(out_13), .sel(register_1_q));
  Multiplexer #(.width(32), .enable("false")) multiplexer_13 (
    .in0(n3_1_out_22), .in1({32{1'b0}}), .out(out_11), .sel(register_1_q));
  Multiplexer #(.width(32), .enable("false")) multiplexer_14 (
    .in0(n3_1_out_23), .in1({32{1'b0}}), .out(out_9), .sel(register_1_q));
  Multiplexer #(.width(32), .enable("false")) multiplexer_15 (
    .in0(n3_1_out_24), .in1({32{1'b0}}), .out(out_7), .sel(register_1_q));
  Multiplexer #(.width(32), .enable("false")) multiplexer_16 (
    .in0(n3_1_out_25), .in1({32{1'b0}}), .out(out_37), .sel(register_1_q));
  Multiplexer #(.width(32), .enable("false")) multiplexer_17 (
    .in0(n3_1_out_26), .in1({32{1'b0}}), .out(out_36), .sel(register_1_q));
  Multiplexer #(.width(32), .enable("false")) multiplexer_18 (
    .in0(n3_1_out_27), .in1({32{1'b0}}), .out(out_34), .sel(register_1_q));
  Multiplexer #(.width(32), .enable("false")) multiplexer_19 (
    .in0(n3_1_out_28), .in1({32{1'b0}}), .out(out_32), .sel(register_1_q));
  Multiplexer #(.width(32), .enable("false")) multiplexer_20 (
    .in0(n3_1_out_29), .in1({32{1'b0}}), .out(out_30), .sel(register_1_q));
  Multiplexer #(.width(32), .enable("false")) multiplexer_21 (
    .in0(n3_1_out_30), .in1({32{1'b0}}), .out(out_28), .sel(register_1_q));
  Multiplexer #(.width(32), .enable("false")) multiplexer_22 (
    .in0(n3_1_out_31), .in1({32{1'b0}}), .out(out_26), .sel(register_1_q));
  Multiplexer #(.width(32), .enable("false")) multiplexer_23 (
    .in0(n3_1_out_32), .in1({32{1'b0}}), .out(out_24), .sel(register_1_q));
  Multiplexer #(.width(32), .enable("false")) multiplexer_24 (
    .in0(n3_1_out_33), .in1({32{1'b0}}), .out(out_22), .sel(register_1_q));
  Multiplexer #(.width(32), .enable("false")) multiplexer_25 (
    .in0(n3_1_out_34), .in1({32{1'b0}}), .out(out_20), .sel(register_1_q));
  Multiplexer #(.width(32), .enable("false")) multiplexer_26 (
    .in0(n3_1_out_35), .in1({32{1'b0}}), .out(out_18), .sel(register_1_q));
  Multiplexer #(.width(32), .enable("false")) multiplexer_27 (
    .in0(n3_1_out_36), .in1({32{1'b0}}), .out(out_16), .sel(register_1_q));
  Multiplexer #(.width(32), .enable("false")) multiplexer_28 (
    .in0(n3_1_out_37), .in1({32{1'b0}}), .out(out_14), .sel(register_1_q));
  Multiplexer #(.width(32), .enable("false")) multiplexer_29 (
    .in0(n3_1_out_38), .in1({32{1'b0}}), .out(out_12), .sel(register_1_q));
  Multiplexer #(.width(32), .enable("false")) multiplexer_30 (
    .in0(n3_1_out_39), .in1({32{1'b0}}), .out(out_10), .sel(register_1_q));
  Multiplexer #(.width(32), .enable("false")) multiplexer_31 (
    .in0(n3_1_out_40), .in1({32{1'b0}}), .out(out_8), .sel(register_1_q));
  or or_3 (or_3_out, in_1, tunnel_t);
  not not_1 (not_1_out, in_1);
  or or_4 (or_4_out, in_1, and_7_out);
  or or_5 (or_5_out, in_1, m);
  not not_2 (not_2_out, in_1);
  or or_6 (or_6_out, in_1, and_8_out);
  Counter counter_1 (
    .load(or_3_out), .D(8'he), .count(not_1_out), .Q(out_5), .clk(or_4_out), .clr(in_2));  // open: carry
  Counter counter_2 (
    .load(or_5_out), .D(8'hd), .count(not_2_out), .Q(out_6), .clk(or_6_out), .clr(in_2));  // open: carry
  Comparator comparator_1 (.a(out_5), .b(8'h3), .eq(comparator_1_eq));  // open: gt, lt
  Comparator comparator_2 (.a(out_5), .b(8'h13), .lt(comparator_2_lt));  // open: gt, eq
  Comparator comparator_3 (.a(out_6), .b({8{1'b1}}), .eq(comparator_3_eq));  // open: gt, lt
  Comparator comparator_4 (.a(out_6), .b(8'h1a), .lt(comparator_4_lt));  // open: gt, eq
  or or_7 (or_7_out, m, d);
  or or_8 (or_8_out, tunnel, tunnel_t);
  and and_1 (and_1_out, or_8_out, comparator_2_lt);
  and and_2 (and_2_out, tunnel_t, or_8_out);
  and and_3 (and_3_out, m, or_7_out);
  and and_4 (and_4_out, or_7_out, comparator_4_lt);
  and and_5 (and_5_out, comparator_1_eq, tunnel_t);
  not not_3 (not_3_out, and_5_out);
  and and_6 (and_6_out, comparator_3_eq, m);
  not not_4 (not_4_out, and_6_out);
  or or_9 (or_9_out, and_4_out, and_3_out);
  and and_7 (and_7_out, not_3_out, or_10_out);
  or or_10 (or_10_out, and_1_out, and_2_out);
  and and_8 (and_8_out, not_4_out, or_9_out);

  // Other names for the same wires on the sheet: _1[1:0] = in_3; _2[1:0] = in_4; rest = in_2; start = in_1
endmodule

module j (
  input  [1:0] in_1,
  input  [1:0] in_2,
  output out_3,
  output out_4,
  output out_5,
  output out_6
);

  wire not_1_out, not_2_out;

  and and_1 (out_3, in_1[0], not_1_out);
  not not_1 (not_1_out, in_1[1]);
  and and_2 (out_5, not_2_out, in_2[0]);
  not not_2 (not_2_out, in_2[1]);
  and and_3 (out_6, in_2[1], in_2[0]);
  and and_4 (out_4, in_1[0], in_1[1]);
endmodule

module _2 (
  input  [31:0] in_1,
  input  in_2,
  input  in_3,
  input  in_4,
  input  in_5,
  output [31:0] out_6
);

  wire and_1_out, and_2_out, and_3_out, and_4_out, ckolk, comparator_1_eq, comparator_2_lt, not_1_out,
       not_2_out, or_1_out, or_2_out;
  wire [3:0] bit_extender_1_out;
  wire [4:0] counter_1_q;
  wire [31:0] multiplier_1_out, multiplier_2_out, multiplier_3_out, multiplier_4_out, multiplier_5_out,
       multiplier_6_out, multiplier_7_out, multiplier_8_out, multiplier_9_out, multiplier_10_out,
       multiplier_11_out, multiplier_12_out, multiplier_13_out, multiplier_14_out, multiplier_15_out,
       multiplier_16_out;

  Multiplier #(.width(32)) multiplier_1 (.a(in_1), .b(32'h10000000), .out(multiplier_1_out));  // open: cin, cout
  Multiplier #(.width(32)) multiplier_2 (.a(in_1), .b(32'h8000000), .out(multiplier_2_out));  // open: cin, cout
  Multiplier #(.width(32)) multiplier_3 (.a(in_1), .b(32'h4000000), .out(multiplier_3_out));  // open: cin, cout
  Multiplier #(.width(32)) multiplier_4 (.a(in_1), .b(32'h2000000), .out(multiplier_4_out));  // open: cin, cout
  Multiplier #(.width(32)) multiplier_5 (.a(in_1), .b(32'h1000000), .out(multiplier_5_out));  // open: cin, cout
  Multiplier #(.width(32)) multiplier_6 (.a(in_1), .b(32'h800000), .out(multiplier_6_out));  // open: cin, cout
  Multiplier #(.width(32)) multiplier_7 (.a(in_1), .b(32'h400000), .out(multiplier_7_out));  // open: cin, cout
  Multiplier #(.width(32)) multiplier_8 (.a(in_1), .b(32'h200000), .out(multiplier_8_out));  // open: cin, cout
  Multiplier #(.width(32)) multiplier_9 (.a(in_1), .b(32'h100000), .out(multiplier_9_out));  // open: cin, cout
  Multiplier #(.width(32)) multiplier_10 (.a(in_1), .b(32'h80000), .out(multiplier_10_out));  // open: cin, cout
  Multiplier #(.width(32)) multiplier_11 (.a(in_1), .b(32'h40000), .out(multiplier_11_out));  // open: cin, cout
  Multiplier #(.width(32)) multiplier_12 (.a(in_1), .b(32'h20000), .out(multiplier_12_out));  // open: cin, cout
  Multiplier #(.width(32)) multiplier_13 (.a(in_1), .b(32'h10000), .out(multiplier_13_out));  // open: cin, cout
  Multiplier #(.width(32)) multiplier_14 (.a(in_1), .b(32'h8000), .out(multiplier_14_out));  // open: cin, cout
  Multiplier #(.width(32)) multiplier_15 (.a(in_1), .b(32'h4000), .out(multiplier_15_out));  // open: cin, cout
  Multiplier #(.width(32)) multiplier_16 (.a(in_1), .b(32'h2000), .out(multiplier_16_out));  // open: cin, cout
  or or_1 (or_1_out, in_5, in_2);
  Counter #(.width(5), .max('h1f)) counter_1 (
    .load(or_1_out), .D(5'b01010), .count(not_1_out), .Q(counter_1_q), .clk(ckolk), .clr(in_3));  // open: carry
  not not_1 (not_1_out, in_5);
  Multiplexer #(.select(4), .width(32), .enable("false")) multiplexer_1 (
    .in0(multiplier_1_out), .in1(multiplier_2_out), .in2(multiplier_3_out), .in3(multiplier_4_out),
    .in4(multiplier_5_out), .in5(multiplier_6_out), .in6(multiplier_7_out), .in7(multiplier_8_out),
    .in8(multiplier_9_out), .in9(multiplier_10_out), .in10(multiplier_11_out), .in11(multiplier_12_out),
    .in12(multiplier_13_out), .in13(multiplier_14_out), .in14(multiplier_15_out), .in15(multiplier_16_out),
    .out(out_6), .sel(bit_extender_1_out));
  Bit_Extender #(.in_width(5), .out_width(4)) bit_extender_1 (.in(counter_1_q), .out(bit_extender_1_out));
  Comparator #(.width(5)) comparator_1 (.a(counter_1_q), .b({5{1'b0}}), .eq(comparator_1_eq));  // open: gt, lt
  Comparator #(.width(5)) comparator_2 (.a(counter_1_q), .b(5'b01111), .lt(comparator_2_lt));  // open: gt, eq
  and and_1 (and_1_out, in_4, comparator_2_lt);
  and and_2 (and_2_out, or_1_out, in_4);
  and and_3 (and_3_out, comparator_1_eq, or_1_out);
  not not_2 (not_2_out, and_3_out);
  or or_2 (or_2_out, and_1_out, and_2_out);
  and and_4 (and_4_out, not_2_out, or_2_out);
  or or_3 (ckolk, and_4_out, in_5);

  // Other names for the same wires on the sheet: start = in_5
endmodule
module _3 (
  input  in_1,
  input  [31:0] in_2,
  input  in_3,
  input  in_4,
  input  in_5,
  input  [31:0] in_6,
  input  [31:0] in_7,
  input  [31:0] in_8,
  input  [31:0] in_9,
  output [31:0] out_10,
  output [31:0] out_11,
  output [31:0] out_12,
  output [31:0] out_13,
  output [31:0] out_14,
  output [31:0] out_15,
  output [31:0] out_16,
  output [31:0] out_17,
  output [31:0] out_18,
  output [31:0] out_19,
  output [31:0] out_20,
  output [31:0] out_21,
  output [31:0] out_22,
  output [31:0] out_23,
  output [31:0] out_24,
  output [31:0] out_25,
  output [31:0] out_26,
  output [31:0] out_27,
  output [31:0] out_28,
  output [31:0] out_29,
  output [31:0] out_30,
  output [31:0] out_31,
  output [31:0] out_32,
  output [31:0] out_33,
  output [31:0] out_34,
  output [31:0] out_35,
  output [31:0] out_36,
  output [31:0] out_37,
  output [31:0] out_38,
  output [31:0] out_39,
  output [31:0] out_40
);

  wire and_1_out, and_2_out, and_3_out, and_4_out, comparator_1_eq, comparator_2_lt, not_1_out, not_2_out,
       or_1_out, or_2_out, or_3_out;
  wire [4:0] bas1;
  wire [5:0] bit_extender_1_out, bit_extender_2_out;

  Multiplexer #(.select(5), .width(32), .enable("false")) multiplexer_1 (
    .in0(in_2), .in1({32{1'b0}}), .in2({32{1'b0}}), .in3({32{1'b0}}), .in4({32{1'b0}}), .in5({32{1'b0}}),
    .in6({32{1'b0}}), .in7({32{1'b0}}), .in8({32{1'b0}}), .in9({32{1'b0}}), .in10({32{1'b0}}),
    .in11({32{1'b0}}), .in12({32{1'b0}}), .in13({32{1'b0}}), .in14({32{1'b0}}), .in15({32{1'b0}}),
    .in16({32{1'b0}}), .in17({32{1'b0}}), .in18({32{1'b0}}), .in19({32{1'b0}}), .in20({32{1'b0}}),
    .in21({32{1'b0}}), .in22({32{1'b0}}), .in23({32{1'b0}}), .in24({32{1'b0}}), .in25({32{1'b0}}),
    .in26({32{1'b0}}), .in27({32{1'b0}}), .in28({32{1'b0}}), .in29({32{1'b0}}), .in30({32{1'b0}}),
    .in31({32{1'b0}}), .out(out_10), .sel(bas1));
  Multiplexer #(.select(5), .width(32), .enable("false")) multiplexer_2 (
    .in0(in_6), .in1(in_2), .in2({32{1'b0}}), .in3({32{1'b0}}), .in4({32{1'b0}}), .in5({32{1'b0}}),
    .in6({32{1'b0}}), .in7({32{1'b0}}), .in8({32{1'b0}}), .in9({32{1'b0}}), .in10({32{1'b0}}),
    .in11({32{1'b0}}), .in12({32{1'b0}}), .in13({32{1'b0}}), .in14({32{1'b0}}), .in15({32{1'b0}}),
    .in16({32{1'b0}}), .in17({32{1'b0}}), .in18({32{1'b0}}), .in19({32{1'b0}}), .in20({32{1'b0}}),
    .in21({32{1'b0}}), .in22({32{1'b0}}), .in23({32{1'b0}}), .in24({32{1'b0}}), .in25({32{1'b0}}),
    .in26({32{1'b0}}), .in27({32{1'b0}}), .in28({32{1'b0}}), .in29({32{1'b0}}), .in30({32{1'b0}}),
    .in31({32{1'b0}}), .out(out_11), .sel(bas1));
  Multiplexer #(.select(5), .width(32), .enable("false")) multiplexer_3 (
    .in0(in_7), .in1(in_6), .in2(in_2), .in3({32{1'b0}}), .in4({32{1'b0}}), .in5({32{1'b0}}),
    .in6({32{1'b0}}), .in7({32{1'b0}}), .in8({32{1'b0}}), .in9({32{1'b0}}), .in10({32{1'b0}}),
    .in11({32{1'b0}}), .in12({32{1'b0}}), .in13({32{1'b0}}), .in14({32{1'b0}}), .in15({32{1'b0}}),
    .in16({32{1'b0}}), .in17({32{1'b0}}), .in18({32{1'b0}}), .in19({32{1'b0}}), .in20({32{1'b0}}),
    .in21({32{1'b0}}), .in22({32{1'b0}}), .in23({32{1'b0}}), .in24({32{1'b0}}), .in25({32{1'b0}}),
    .in26({32{1'b0}}), .in27({32{1'b0}}), .in28({32{1'b0}}), .in29({32{1'b0}}), .in30({32{1'b0}}),
    .in31({32{1'b0}}), .out(out_12), .sel(bas1));
  Multiplexer #(.select(5), .width(32), .enable("false")) multiplexer_4 (
    .in0(in_8), .in1(in_7), .in2(in_6), .in3(in_2), .in4({32{1'b0}}), .in5({32{1'b0}}), .in6({32{1'b0}}),
    .in7({32{1'b0}}), .in8({32{1'b0}}), .in9({32{1'b0}}), .in10({32{1'b0}}), .in11({32{1'b0}}),
    .in12({32{1'b0}}), .in13({32{1'b0}}), .in14({32{1'b0}}), .in15({32{1'b0}}), .in16({32{1'b0}}),
    .in17({32{1'b0}}), .in18({32{1'b0}}), .in19({32{1'b0}}), .in20({32{1'b0}}), .in21({32{1'b0}}),
    .in22({32{1'b0}}), .in23({32{1'b0}}), .in24({32{1'b0}}), .in25({32{1'b0}}), .in26({32{1'b0}}),
    .in27({32{1'b0}}), .in28({32{1'b0}}), .in29({32{1'b0}}), .in30({32{1'b0}}), .in31({32{1'b0}}),
    .out(out_13), .sel(bas1));
  Multiplexer #(.select(5), .width(32), .enable("false")) multiplexer_5 (
    .in0(in_9), .in1(in_8), .in2(in_7), .in3(in_6), .in4(in_2), .in5({32{1'b0}}), .in6({32{1'b0}}),
    .in7({32{1'b0}}), .in8({32{1'b0}}), .in9({32{1'b0}}), .in10({32{1'b0}}), .in11({32{1'b0}}),
    .in12({32{1'b0}}), .in13({32{1'b0}}), .in14({32{1'b0}}), .in15({32{1'b0}}), .in16({32{1'b0}}),
    .in17({32{1'b0}}), .in18({32{1'b0}}), .in19({32{1'b0}}), .in20({32{1'b0}}), .in21({32{1'b0}}),
    .in22({32{1'b0}}), .in23({32{1'b0}}), .in24({32{1'b0}}), .in25({32{1'b0}}), .in26({32{1'b0}}),
    .in27({32{1'b0}}), .in28({32{1'b0}}), .in29({32{1'b0}}), .in30({32{1'b0}}), .in31({32{1'b0}}),
    .out(out_14), .sel(bas1));
  Multiplexer #(.select(5), .width(32), .enable("false")) multiplexer_6 (
    .in0({32{1'b0}}), .in1(in_9), .in2(in_8), .in3(in_7), .in4(in_6), .in5(in_2), .in6({32{1'b0}}),
    .in7({32{1'b0}}), .in8({32{1'b0}}), .in9({32{1'b0}}), .in10({32{1'b0}}), .in11({32{1'b0}}),
    .in12({32{1'b0}}), .in13({32{1'b0}}), .in14({32{1'b0}}), .in15({32{1'b0}}), .in16({32{1'b0}}),
    .in17({32{1'b0}}), .in18({32{1'b0}}), .in19({32{1'b0}}), .in20({32{1'b0}}), .in21({32{1'b0}}),
    .in22({32{1'b0}}), .in23({32{1'b0}}), .in24({32{1'b0}}), .in25({32{1'b0}}), .in26({32{1'b0}}),
    .in27({32{1'b0}}), .in28({32{1'b0}}), .in29({32{1'b0}}), .in30({32{1'b0}}), .in31({32{1'b0}}),
    .out(out_15), .sel(bas1));
  Multiplexer #(.select(5), .width(32), .enable("false")) multiplexer_7 (
    .in0({32{1'b0}}), .in1({32{1'b0}}), .in2(in_9), .in3(in_8), .in4(in_7), .in5(in_6), .in6(in_2),
    .in7({32{1'b0}}), .in8({32{1'b0}}), .in9({32{1'b0}}), .in10({32{1'b0}}), .in11({32{1'b0}}),
    .in12({32{1'b0}}), .in13({32{1'b0}}), .in14({32{1'b0}}), .in15({32{1'b0}}), .in16({32{1'b0}}),
    .in17({32{1'b0}}), .in18({32{1'b0}}), .in19({32{1'b0}}), .in20({32{1'b0}}), .in21({32{1'b0}}),
    .in22({32{1'b0}}), .in23({32{1'b0}}), .in24({32{1'b0}}), .in25({32{1'b0}}), .in26({32{1'b0}}),
    .in27({32{1'b0}}), .in28({32{1'b0}}), .in29({32{1'b0}}), .in30({32{1'b0}}), .in31({32{1'b0}}),
    .out(out_16), .sel(bas1));
  Multiplexer #(.select(5), .width(32), .enable("false")) multiplexer_8 (
    .in0({32{1'b0}}), .in1({32{1'b0}}), .in2({32{1'b0}}), .in3(in_9), .in4(in_8), .in5(in_7), .in6(in_6),
    .in7(in_2), .in8({32{1'b0}}), .in9({32{1'b0}}), .in10({32{1'b0}}), .in11({32{1'b0}}), .in12({32{1'b0}}),
    .in13({32{1'b0}}), .in14({32{1'b0}}), .in15({32{1'b0}}), .in16({32{1'b0}}), .in17({32{1'b0}}),
    .in18({32{1'b0}}), .in19({32{1'b0}}), .in20({32{1'b0}}), .in21({32{1'b0}}), .in22({32{1'b0}}),
    .in23({32{1'b0}}), .in24({32{1'b0}}), .in25({32{1'b0}}), .in26({32{1'b0}}), .in27({32{1'b0}}),
    .in28({32{1'b0}}), .in29({32{1'b0}}), .in30({32{1'b0}}), .in31({32{1'b0}}), .out(out_17), .sel(bas1));
  Multiplexer #(.select(5), .width(32), .enable("false")) multiplexer_9 (
    .in0({32{1'b0}}), .in1({32{1'b0}}), .in2({32{1'b0}}), .in3({32{1'b0}}), .in4(in_9), .in5(in_8),
    .in6(in_7), .in7(in_6), .in8(in_2), .in9({32{1'b0}}), .in10({32{1'b0}}), .in11({32{1'b0}}),
    .in12({32{1'b0}}), .in13({32{1'b0}}), .in14({32{1'b0}}), .in15({32{1'b0}}), .in16({32{1'b0}}),
    .in17({32{1'b0}}), .in18({32{1'b0}}), .in19({32{1'b0}}), .in20({32{1'b0}}), .in21({32{1'b0}}),
    .in22({32{1'b0}}), .in23({32{1'b0}}), .in24({32{1'b0}}), .in25({32{1'b0}}), .in26({32{1'b0}}),
    .in27({32{1'b0}}), .in28({32{1'b0}}), .in29({32{1'b0}}), .in30({32{1'b0}}), .in31({32{1'b0}}),
    .out(out_18), .sel(bas1));
  Multiplexer #(.select(5), .width(32), .enable("false")) multiplexer_10 (
    .in0({32{1'b0}}), .in1({32{1'b0}}), .in2({32{1'b0}}), .in3({32{1'b0}}), .in4({32{1'b0}}), .in5(in_9),
    .in6(in_8), .in7(in_7), .in8(in_6), .in9(in_2), .in10({32{1'b0}}), .in11({32{1'b0}}), .in12({32{1'b0}}),
    .in13({32{1'b0}}), .in14({32{1'b0}}), .in15({32{1'b0}}), .in16({32{1'b0}}), .in17({32{1'b0}}),
    .in18({32{1'b0}}), .in19({32{1'b0}}), .in20({32{1'b0}}), .in21({32{1'b0}}), .in22({32{1'b0}}),
    .in23({32{1'b0}}), .in24({32{1'b0}}), .in25({32{1'b0}}), .in26({32{1'b0}}), .in27({32{1'b0}}),
    .in28({32{1'b0}}), .in29({32{1'b0}}), .in30({32{1'b0}}), .in31({32{1'b0}}), .out(out_19), .sel(bas1));
  Multiplexer #(.select(5), .width(32), .enable("false")) multiplexer_11 (
    .in0({32{1'b0}}), .in1({32{1'b0}}), .in2({32{1'b0}}), .in3({32{1'b0}}), .in4({32{1'b0}}),
    .in5({32{1'b0}}), .in6(in_9), .in7(in_8), .in8(in_7), .in9(in_6), .in10(in_2), .in11({32{1'b0}}),
    .in12({32{1'b0}}), .in13({32{1'b0}}), .in14({32{1'b0}}), .in15({32{1'b0}}), .in16({32{1'b0}}),
    .in17({32{1'b0}}), .in18({32{1'b0}}), .in19({32{1'b0}}), .in20({32{1'b0}}), .in21({32{1'b0}}),
    .in22({32{1'b0}}), .in23({32{1'b0}}), .in24({32{1'b0}}), .in25({32{1'b0}}), .in26({32{1'b0}}),
    .in27({32{1'b0}}), .in28({32{1'b0}}), .in29({32{1'b0}}), .in30({32{1'b0}}), .in31({32{1'b0}}),
    .out(out_20), .sel(bas1));
  Multiplexer #(.select(5), .width(32), .enable("false")) multiplexer_12 (
    .in0({32{1'b0}}), .in1({32{1'b0}}), .in2({32{1'b0}}), .in3({32{1'b0}}), .in4({32{1'b0}}),
    .in5({32{1'b0}}), .in6({32{1'b0}}), .in7(in_9), .in8(in_8), .in9(in_7), .in10(in_6), .in11(in_2),
    .in12({32{1'b0}}), .in13({32{1'b0}}), .in14({32{1'b0}}), .in15({32{1'b0}}), .in16({32{1'b0}}),
    .in17({32{1'b0}}), .in18({32{1'b0}}), .in19({32{1'b0}}), .in20({32{1'b0}}), .in21({32{1'b0}}),
    .in22({32{1'b0}}), .in23({32{1'b0}}), .in24({32{1'b0}}), .in25({32{1'b0}}), .in26({32{1'b0}}),
    .in27({32{1'b0}}), .in28({32{1'b0}}), .in29({32{1'b0}}), .in30({32{1'b0}}), .in31({32{1'b0}}),
    .out(out_21), .sel(bas1));
  Multiplexer #(.select(5), .width(32), .enable("false")) multiplexer_13 (
    .in0({32{1'b0}}), .in1({32{1'b0}}), .in2({32{1'b0}}), .in3({32{1'b0}}), .in4({32{1'b0}}),
    .in5({32{1'b0}}), .in6({32{1'b0}}), .in7({32{1'b0}}), .in8(in_9), .in9(in_8), .in10(in_7), .in11(in_6),
    .in12(in_2), .in13({32{1'b0}}), .in14({32{1'b0}}), .in15({32{1'b0}}), .in16({32{1'b0}}),
    .in17({32{1'b0}}), .in18({32{1'b0}}), .in19({32{1'b0}}), .in20({32{1'b0}}), .in21({32{1'b0}}),
    .in22({32{1'b0}}), .in23({32{1'b0}}), .in24({32{1'b0}}), .in25({32{1'b0}}), .in26({32{1'b0}}),
    .in27({32{1'b0}}), .in28({32{1'b0}}), .in29({32{1'b0}}), .in30({32{1'b0}}), .in31({32{1'b0}}),
    .out(out_22), .sel(bas1));
  Multiplexer #(.select(5), .width(32), .enable("false")) multiplexer_14 (
    .in0({32{1'b0}}), .in1({32{1'b0}}), .in2({32{1'b0}}), .in3({32{1'b0}}), .in4({32{1'b0}}),
    .in5({32{1'b0}}), .in6({32{1'b0}}), .in7({32{1'b0}}), .in8({32{1'b0}}), .in9(in_9), .in10(in_8),
    .in11(in_7), .in12(in_6), .in13(in_2), .in14({32{1'b0}}), .in15({32{1'b0}}), .in16({32{1'b0}}),
    .in17({32{1'b0}}), .in18({32{1'b0}}), .in19({32{1'b0}}), .in20({32{1'b0}}), .in21({32{1'b0}}),
    .in22({32{1'b0}}), .in23({32{1'b0}}), .in24({32{1'b0}}), .in25({32{1'b0}}), .in26({32{1'b0}}),
    .in27({32{1'b0}}), .in28({32{1'b0}}), .in29({32{1'b0}}), .in30({32{1'b0}}), .in31({32{1'b0}}),
    .out(out_23), .sel(bas1));
  Multiplexer #(.select(5), .width(32), .enable("false")) multiplexer_15 (
    .in0({32{1'b0}}), .in1({32{1'b0}}), .in2({32{1'b0}}), .in3({32{1'b0}}), .in4({32{1'b0}}),
    .in5({32{1'b0}}), .in6({32{1'b0}}), .in7({32{1'b0}}), .in8({32{1'b0}}), .in9({32{1'b0}}), .in10(in_9),
    .in11(in_8), .in12(in_7), .in13(in_6), .in14(in_2), .in15({32{1'b0}}), .in16({32{1'b0}}),
    .in17({32{1'b0}}), .in18({32{1'b0}}), .in19({32{1'b0}}), .in20({32{1'b0}}), .in21({32{1'b0}}),
    .in22({32{1'b0}}), .in23({32{1'b0}}), .in24({32{1'b0}}), .in25({32{1'b0}}), .in26({32{1'b0}}),
    .in27({32{1'b0}}), .in28({32{1'b0}}), .in29({32{1'b0}}), .in30({32{1'b0}}), .in31({32{1'b0}}),
    .out(out_24), .sel(bas1));
  Multiplexer #(.select(5), .width(32), .enable("false")) multiplexer_16 (
    .in0({32{1'b0}}), .in1({32{1'b0}}), .in2({32{1'b0}}), .in3({32{1'b0}}), .in4({32{1'b0}}),
    .in5({32{1'b0}}), .in6({32{1'b0}}), .in7({32{1'b0}}), .in8({32{1'b0}}), .in9({32{1'b0}}),
    .in10({32{1'b0}}), .in11(in_2), .in12(in_6), .in13(in_7), .in14(in_8), .in15(in_9), .in16({32{1'b0}}),
    .in17({32{1'b0}}), .in18({32{1'b0}}), .in19({32{1'b0}}), .in20({32{1'b0}}), .in21({32{1'b0}}),
    .in22({32{1'b0}}), .in23({32{1'b0}}), .in24({32{1'b0}}), .in25({32{1'b0}}), .in26({32{1'b0}}),
    .in27({32{1'b0}}), .in28({32{1'b0}}), .in29({32{1'b0}}), .in30({32{1'b0}}), .in31({32{1'b0}}),
    .out(out_25), .sel(bas1));
  Multiplexer #(.select(5), .width(32), .enable("false")) multiplexer_17 (
    .in0({32{1'b0}}), .in1({32{1'b0}}), .in2({32{1'b0}}), .in3({32{1'b0}}), .in4({32{1'b0}}),
    .in5({32{1'b0}}), .in6({32{1'b0}}), .in7({32{1'b0}}), .in8({32{1'b0}}), .in9({32{1'b0}}),
    .in10({32{1'b0}}), .in11({32{1'b0}}), .in12(in_2), .in13(in_6), .in14(in_7), .in15(in_8), .in16(in_9),
    .in17({32{1'b0}}), .in18({32{1'b0}}), .in19({32{1'b0}}), .in20({32{1'b0}}), .in21({32{1'b0}}),
    .in22({32{1'b0}}), .in23({32{1'b0}}), .in24({32{1'b0}}), .in25({32{1'b0}}), .in26({32{1'b0}}),
    .in27({32{1'b0}}), .in28({32{1'b0}}), .in29({32{1'b0}}), .in30({32{1'b0}}), .in31({32{1'b0}}),
    .out(out_26), .sel(bas1));
  Multiplexer #(.select(5), .width(32), .enable("false")) multiplexer_18 (
    .in0({32{1'b0}}), .in1({32{1'b0}}), .in2({32{1'b0}}), .in3({32{1'b0}}), .in4({32{1'b0}}),
    .in5({32{1'b0}}), .in6({32{1'b0}}), .in7({32{1'b0}}), .in8({32{1'b0}}), .in9({32{1'b0}}),
    .in10({32{1'b0}}), .in11({32{1'b0}}), .in12({32{1'b0}}), .in13(in_2), .in14(in_6), .in15(in_7),
    .in16(in_8), .in17(in_9), .in18({32{1'b0}}), .in19({32{1'b0}}), .in20({32{1'b0}}), .in21({32{1'b0}}),
    .in22({32{1'b0}}), .in23({32{1'b0}}), .in24({32{1'b0}}), .in25({32{1'b0}}), .in26({32{1'b0}}),
    .in27({32{1'b0}}), .in28({32{1'b0}}), .in29({32{1'b0}}), .in30({32{1'b0}}), .in31({32{1'b0}}),
    .out(out_27), .sel(bas1));
  Multiplexer #(.select(5), .width(32), .enable("false")) multiplexer_19 (
    .in0({32{1'b0}}), .in1({32{1'b0}}), .in2({32{1'b0}}), .in3({32{1'b0}}), .in4({32{1'b0}}),
    .in5({32{1'b0}}), .in6({32{1'b0}}), .in7({32{1'b0}}), .in8({32{1'b0}}), .in9({32{1'b0}}),
    .in10({32{1'b0}}), .in11({32{1'b0}}), .in12({32{1'b0}}), .in13({32{1'b0}}), .in14(in_2), .in15(in_6),
    .in16(in_7), .in17(in_8), .in18(in_9), .in19({32{1'b0}}), .in20({32{1'b0}}), .in21({32{1'b0}}),
    .in22({32{1'b0}}), .in23({32{1'b0}}), .in24({32{1'b0}}), .in25({32{1'b0}}), .in26({32{1'b0}}),
    .in27({32{1'b0}}), .in28({32{1'b0}}), .in29({32{1'b0}}), .in30({32{1'b0}}), .in31({32{1'b0}}),
    .out(out_28), .sel(bas1));
  Multiplexer #(.select(5), .width(32), .enable("false")) multiplexer_20 (
    .in0({32{1'b0}}), .in1({32{1'b0}}), .in2({32{1'b0}}), .in3({32{1'b0}}), .in4({32{1'b0}}),
    .in5({32{1'b0}}), .in6({32{1'b0}}), .in7({32{1'b0}}), .in8({32{1'b0}}), .in9({32{1'b0}}),
    .in10({32{1'b0}}), .in11({32{1'b0}}), .in12({32{1'b0}}), .in13({32{1'b0}}), .in14({32{1'b0}}),
    .in15(in_2), .in16(in_6), .in17(in_7), .in18(in_8), .in19(in_9), .in20({32{1'b0}}), .in21({32{1'b0}}),
    .in22({32{1'b0}}), .in23({32{1'b0}}), .in24({32{1'b0}}), .in25({32{1'b0}}), .in26({32{1'b0}}),
    .in27({32{1'b0}}), .in28({32{1'b0}}), .in29({32{1'b0}}), .in30({32{1'b0}}), .in31({32{1'b0}}),
    .out(out_29), .sel(bas1));
  Multiplexer #(.select(5), .width(32), .enable("false")) multiplexer_21 (
    .in0({32{1'b0}}), .in1({32{1'b0}}), .in2({32{1'b0}}), .in3({32{1'b0}}), .in4({32{1'b0}}),
    .in5({32{1'b0}}), .in6({32{1'b0}}), .in7({32{1'b0}}), .in8({32{1'b0}}), .in9({32{1'b0}}),
    .in10({32{1'b0}}), .in11({32{1'b0}}), .in12({32{1'b0}}), .in13({32{1'b0}}), .in14({32{1'b0}}),
    .in15({32{1'b0}}), .in16(in_2), .in17(in_6), .in18(in_7), .in19(in_8), .in20(in_9), .in21({32{1'b0}}),
    .in22({32{1'b0}}), .in23({32{1'b0}}), .in24({32{1'b0}}), .in25({32{1'b0}}), .in26({32{1'b0}}),
    .in27({32{1'b0}}), .in28({32{1'b0}}), .in29({32{1'b0}}), .in30({32{1'b0}}), .in31({32{1'b0}}),
    .out(out_30), .sel(bas1));
  Multiplexer #(.select(5), .width(32), .enable("false")) multiplexer_22 (
    .in0({32{1'b0}}), .in1({32{1'b0}}), .in2({32{1'b0}}), .in3({32{1'b0}}), .in4({32{1'b0}}),
    .in5({32{1'b0}}), .in6({32{1'b0}}), .in7({32{1'b0}}), .in8({32{1'b0}}), .in9({32{1'b0}}),
    .in10({32{1'b0}}), .in11({32{1'b0}}), .in12({32{1'b0}}), .in13({32{1'b0}}), .in14({32{1'b0}}),
    .in15({32{1'b0}}), .in16({32{1'b0}}), .in17(in_2), .in18(in_6), .in19(in_7), .in20(in_8), .in21(in_9),
    .in22({32{1'b0}}), .in23({32{1'b0}}), .in24({32{1'b0}}), .in25({32{1'b0}}), .in26({32{1'b0}}),
    .in27({32{1'b0}}), .in28({32{1'b0}}), .in29({32{1'b0}}), .in30({32{1'b0}}), .in31({32{1'b0}}),
    .out(out_31), .sel(bas1));
  Multiplexer #(.select(5), .width(32), .enable("false")) multiplexer_23 (
    .in0({32{1'b0}}), .in1({32{1'b0}}), .in2({32{1'b0}}), .in3({32{1'b0}}), .in4({32{1'b0}}),
    .in5({32{1'b0}}), .in6({32{1'b0}}), .in7({32{1'b0}}), .in8({32{1'b0}}), .in9({32{1'b0}}),
    .in10({32{1'b0}}), .in11({32{1'b0}}), .in12({32{1'b0}}), .in13({32{1'b0}}), .in14({32{1'b0}}),
    .in15({32{1'b0}}), .in16({32{1'b0}}), .in17({32{1'b0}}), .in18(in_2), .in19(in_6), .in20(in_7),
    .in21(in_8), .in22(in_9), .in23({32{1'b0}}), .in24({32{1'b0}}), .in25({32{1'b0}}), .in26({32{1'b0}}),
    .in27({32{1'b0}}), .in28({32{1'b0}}), .in29({32{1'b0}}), .in30({32{1'b0}}), .in31({32{1'b0}}),
    .out(out_32), .sel(bas1));
  Multiplexer #(.select(5), .width(32), .enable("false")) multiplexer_24 (
    .in0({32{1'b0}}), .in1({32{1'b0}}), .in2({32{1'b0}}), .in3({32{1'b0}}), .in4({32{1'b0}}),
    .in5({32{1'b0}}), .in6({32{1'b0}}), .in7({32{1'b0}}), .in8({32{1'b0}}), .in9({32{1'b0}}),
    .in10({32{1'b0}}), .in11({32{1'b0}}), .in12({32{1'b0}}), .in13({32{1'b0}}), .in14({32{1'b0}}),
    .in15({32{1'b0}}), .in16({32{1'b0}}), .in17({32{1'b0}}), .in18({32{1'b0}}), .in19(in_2), .in20(in_6),
    .in21(in_7), .in22(in_8), .in23(in_9), .in24({32{1'b0}}), .in25({32{1'b0}}), .in26({32{1'b0}}),
    .in27({32{1'b0}}), .in28({32{1'b0}}), .in29({32{1'b0}}), .in30({32{1'b0}}), .in31({32{1'b0}}),
    .out(out_33), .sel(bas1));
  Multiplexer #(.select(5), .width(32), .enable("false")) multiplexer_25 (
    .in0({32{1'b0}}), .in1({32{1'b0}}), .in2({32{1'b0}}), .in3({32{1'b0}}), .in4({32{1'b0}}),
    .in5({32{1'b0}}), .in6({32{1'b0}}), .in7({32{1'b0}}), .in8({32{1'b0}}), .in9({32{1'b0}}),
    .in10({32{1'b0}}), .in11({32{1'b0}}), .in12({32{1'b0}}), .in13({32{1'b0}}), .in14({32{1'b0}}),
    .in15({32{1'b0}}), .in16({32{1'b0}}), .in17({32{1'b0}}), .in18({32{1'b0}}), .in19({32{1'b0}}),
    .in20(in_2), .in21(in_6), .in22(in_7), .in23(in_8), .in24(in_9), .in25({32{1'b0}}), .in26({32{1'b0}}),
    .in27({32{1'b0}}), .in28({32{1'b0}}), .in29({32{1'b0}}), .in30({32{1'b0}}), .in31({32{1'b0}}),
    .out(out_34), .sel(bas1));
  Multiplexer #(.select(5), .width(32), .enable("false")) multiplexer_26 (
    .in0({32{1'b0}}), .in1({32{1'b0}}), .in2({32{1'b0}}), .in3({32{1'b0}}), .in4({32{1'b0}}),
    .in5({32{1'b0}}), .in6({32{1'b0}}), .in7({32{1'b0}}), .in8({32{1'b0}}), .in9({32{1'b0}}),
    .in10({32{1'b0}}), .in11({32{1'b0}}), .in12({32{1'b0}}), .in13({32{1'b0}}), .in14({32{1'b0}}),
    .in15({32{1'b0}}), .in16({32{1'b0}}), .in17({32{1'b0}}), .in18({32{1'b0}}), .in19({32{1'b0}}),
    .in20({32{1'b0}}), .in21(in_2), .in22(in_6), .in23(in_7), .in24(in_8), .in25(in_9), .in26({32{1'b0}}),
    .in27({32{1'b0}}), .in28({32{1'b0}}), .in29({32{1'b0}}), .in30({32{1'b0}}), .in31({32{1'b0}}),
    .out(out_35), .sel(bas1));
  Multiplexer #(.select(5), .width(32), .enable("false")) multiplexer_27 (
    .in0({32{1'b0}}), .in1({32{1'b0}}), .in2({32{1'b0}}), .in3({32{1'b0}}), .in4({32{1'b0}}),
    .in5({32{1'b0}}), .in6({32{1'b0}}), .in7({32{1'b0}}), .in8({32{1'b0}}), .in9({32{1'b0}}),
    .in10({32{1'b0}}), .in11({32{1'b0}}), .in12({32{1'b0}}), .in13({32{1'b0}}), .in14({32{1'b0}}),
    .in15({32{1'b0}}), .in16({32{1'b0}}), .in17({32{1'b0}}), .in18({32{1'b0}}), .in19({32{1'b0}}),
    .in20({32{1'b0}}), .in21({32{1'b0}}), .in22(in_2), .in23(in_6), .in24(in_7), .in25(in_8), .in26(in_9),
    .in27({32{1'b0}}), .in28({32{1'b0}}), .in29({32{1'b0}}), .in30({32{1'b0}}), .in31({32{1'b0}}),
    .out(out_36), .sel(bas1));
  Multiplexer #(.select(5), .width(32), .enable("false")) multiplexer_28 (
    .in0({32{1'b0}}), .in1({32{1'b0}}), .in2({32{1'b0}}), .in3({32{1'b0}}), .in4({32{1'b0}}),
    .in5({32{1'b0}}), .in6({32{1'b0}}), .in7({32{1'b0}}), .in8({32{1'b0}}), .in9({32{1'b0}}),
    .in10({32{1'b0}}), .in11({32{1'b0}}), .in12({32{1'b0}}), .in13({32{1'b0}}), .in14({32{1'b0}}),
    .in15({32{1'b0}}), .in16({32{1'b0}}), .in17({32{1'b0}}), .in18({32{1'b0}}), .in19({32{1'b0}}),
    .in20({32{1'b0}}), .in21({32{1'b0}}), .in22({32{1'b0}}), .in23(in_2), .in24(in_6), .in25(in_7),
    .in26(in_8), .in27(in_9), .in28({32{1'b0}}), .in29({32{1'b0}}), .in30({32{1'b0}}), .in31({32{1'b0}}),
    .out(out_37), .sel(bas1));
  Multiplexer #(.select(5), .width(32), .enable("false")) multiplexer_29 (
    .in0({32{1'b0}}), .in1({32{1'b0}}), .in2({32{1'b0}}), .in3({32{1'b0}}), .in4({32{1'b0}}),
    .in5({32{1'b0}}), .in6({32{1'b0}}), .in7({32{1'b0}}), .in8({32{1'b0}}), .in9({32{1'b0}}),
    .in10({32{1'b0}}), .in11({32{1'b0}}), .in12({32{1'b0}}), .in13({32{1'b0}}), .in14({32{1'b0}}),
    .in15({32{1'b0}}), .in16({32{1'b0}}), .in17({32{1'b0}}), .in18({32{1'b0}}), .in19({32{1'b0}}),
    .in20({32{1'b0}}), .in21({32{1'b0}}), .in22({32{1'b0}}), .in23({32{1'b0}}), .in24(in_2), .in25(in_6),
    .in26(in_7), .in27(in_8), .in28(in_9), .in29({32{1'b0}}), .in30({32{1'b0}}), .in31({32{1'b0}}),
    .out(out_38), .sel(bas1));
  Multiplexer #(.select(5), .width(32), .enable("false")) multiplexer_30 (
    .in0({32{1'b0}}), .in1({32{1'b0}}), .in2({32{1'b0}}), .in3({32{1'b0}}), .in4({32{1'b0}}),
    .in5({32{1'b0}}), .in6({32{1'b0}}), .in7({32{1'b0}}), .in8({32{1'b0}}), .in9({32{1'b0}}),
    .in10({32{1'b0}}), .in11({32{1'b0}}), .in12({32{1'b0}}), .in13({32{1'b0}}), .in14({32{1'b0}}),
    .in15({32{1'b0}}), .in16({32{1'b0}}), .in17({32{1'b0}}), .in18({32{1'b0}}), .in19({32{1'b0}}),
    .in20({32{1'b0}}), .in21({32{1'b0}}), .in22({32{1'b0}}), .in23({32{1'b0}}), .in24({32{1'b0}}),
    .in25(in_2), .in26(in_6), .in27(in_7), .in28(in_8), .in29(in_9), .in30({32{1'b0}}), .in31({32{1'b0}}),
    .out(out_39), .sel(bas1));
  Multiplexer #(.select(5), .width(32), .enable("false")) multiplexer_31 (
    .in0({32{1'b0}}), .in1({32{1'b0}}), .in2({32{1'b0}}), .in3({32{1'b0}}), .in4({32{1'b0}}),
    .in5({32{1'b0}}), .in6({32{1'b0}}), .in7({32{1'b0}}), .in8({32{1'b0}}), .in9({32{1'b0}}),
    .in10({32{1'b0}}), .in11({32{1'b0}}), .in12({32{1'b0}}), .in13({32{1'b0}}), .in14({32{1'b0}}),
    .in15({32{1'b0}}), .in16({32{1'b0}}), .in17({32{1'b0}}), .in18({32{1'b0}}), .in19({32{1'b0}}),
    .in20({32{1'b0}}), .in21({32{1'b0}}), .in22({32{1'b0}}), .in23({32{1'b0}}), .in24({32{1'b0}}),
    .in25({32{1'b0}}), .in26(in_2), .in27(in_6), .in28(in_7), .in29(in_8), .in30(in_9), .in31({32{1'b0}}),
    .out(out_40), .sel(bas1));
  or or_1 (or_1_out, in_1, in_4);
  not not_1 (not_1_out, in_1);
  or or_2 (or_2_out, and_1_out, in_1);
  and and_1 (and_1_out, not_2_out, or_3_out);
  Counter #(.width(5), .max('h1f)) counter_1 (
    .load(or_1_out), .D(5'b01101), .count(not_1_out), .Q(bas1), .clk(or_2_out), .clr(in_5));  // open: carry
  or or_3 (or_3_out, and_4_out, and_3_out);
  assign bit_extender_1_out = {{1{1'b0}}, bas1};  // Bit_Extender bit_extender_1
  Comparator #(.width(6)) comparator_1 (.a(bit_extender_1_out), .b({6{1'b0}}), .eq(comparator_1_eq));  // open: gt, lt
  assign bit_extender_2_out = {{1{1'b0}}, bas1};  // Bit_Extender bit_extender_2
  Comparator #(.width(6)) comparator_2 (.a(bit_extender_2_out), .b(6'b011010), .lt(comparator_2_lt));  // open: gt, eq
  and and_2 (and_2_out, comparator_1_eq, or_1_out);
  and and_3 (and_3_out, comparator_2_lt, in_3);
  and and_4 (and_4_out, in_3, or_1_out);
  not not_2 (not_2_out, and_2_out);

  // Other names for the same wires on the sheet: _1[31:0] = in_2; _2[31:0] = in_6; _3[31:0] = in_7; _4[31:0] = in_8;
  //   _5[31:0] = in_9; _12 = in_3; r = in_4; rest = in_5; start = in_1
endmodule

module bot_sxedio (
  output [31:0] out_1,
  output [31:0] out_2,
  output [31:0] out_3,
  output [31:0] out_4,
  output [31:0] out_5,
  output [31:0] out_6,
  output [31:0] out_7,
  output [31:0] out_8,
  output [31:0] out_9,
  output [31:0] out_10,
  output [31:0] out_11,
  output [31:0] out_12,
  output [31:0] out_13,
  output [31:0] out_14,
  output [31:0] out_15
);


  assign out_1 = {32{1'b0}};
  assign out_2 = {32{1'b0}};
  assign out_3 = {32{1'b0}};
  assign out_4 = 32'hff;
  assign out_5 = 32'h1fb;
  assign out_6 = 32'h1dd;
  assign out_7 = 32'h1fb;
  assign out_8 = 32'h1ed;
  assign out_9 = 32'h1fb;
  assign out_10 = 32'h1dd;
  assign out_11 = 32'h1fb;
  assign out_12 = 32'hff;
  assign out_13 = {32{1'b0}};
  assign out_14 = {32{1'b0}};
  assign out_15 = {32{1'b0}};
endmodule

module fortosh_bol (
  input  in_1,
  input  in_2,
  input  in_3,
  input  in_4,
  output out_5
);

  wire not_1_out, or_1_out, register_1_q;

  Register #(.width(1)) register_1 (.D(in_1), .Q(register_1_q), .clk(in_1), .clr(or_1_out));  // open: en
  or or_1 (or_1_out, in_3, in_4);
  not not_1 (not_1_out, register_1_q);
  and and_1 (out_5, in_1, not_1_out, in_2);
endmodule

module h (
  input  [31:0] in_1,
  input  [31:0] in_2,
  input  [31:0] in_3,
  input  [31:0] in_4,
  input  [31:0] in_5,
  input  [31:0] in_6,
  input  [31:0] in_7,
  input  [31:0] in_8,
  input  [31:0] in_9,
  input  [31:0] in_10,
  input  [31:0] in_11,
  input  [31:0] in_12,
  input  [31:0] in_13,
  input  [31:0] in_14,
  input  [31:0] in_15,
  input  [31:0] in_16,
  input  [31:0] in_17,
  input  [31:0] in_18,
  input  [31:0] in_19,
  input  [31:0] in_20,
  input  [31:0] in_21,
  input  [31:0] in_22,
  input  [31:0] in_23,
  input  [31:0] in_24,
  input  [31:0] in_25,
  input  [31:0] in_26,
  input  [31:0] in_27,
  input  [31:0] in_28,
  input  [31:0] in_29,
  input  [31:0] in_30,
  input  [31:0] in_31,
  input  [31:0] in_32,
  input  [31:0] in_33,
  input  [31:0] in_34,
  input  [31:0] in_35,
  input  [31:0] in_36,
  input  [31:0] in_37,
  input  [31:0] in_38,
  input  [31:0] in_39,
  input  [31:0] in_40,
  input  [31:0] in_41,
  input  [31:0] in_42,
  input  [31:0] in_43,
  input  [31:0] in_44,
  input  [31:0] in_45,
  input  [31:0] in_46,
  input  [31:0] in_47,
  input  [31:0] in_48,
  input  [31:0] in_49,
  input  [31:0] in_50,
  input  [31:0] in_51,
  input  [31:0] in_52,
  input  [31:0] in_53,
  input  [31:0] in_54,
  output [31:0] out_55,
  output [31:0] out_56,
  output [31:0] out_57,
  output [31:0] out_58,
  output [31:0] out_59,
  output [31:0] out_60,
  output [31:0] out_61,
  output [31:0] out_62,
  output [31:0] out_63,
  output [31:0] out_64,
  output [31:0] out_65,
  output [31:0] out_66,
  output [31:0] out_67,
  output [31:0] out_68,
  output [31:0] out_69,
  output [31:0] out_70,
  output [31:0] out_71,
  output [31:0] out_72,
  output [31:0] out_73,
  output [31:0] out_74,
  output [31:0] out_75,
  output [31:0] out_76,
  output [31:0] out_77,
  output [31:0] out_78,
  output [31:0] out_79,
  output [31:0] out_80,
  output [31:0] out_81
);

  assign out_81 = in_1 | in_54;  // OR_Gate or_1, 32 bits wide
  assign out_80 = in_2 | in_53;  // OR_Gate or_2, 32 bits wide
  assign out_79 = in_3 | in_52;  // OR_Gate or_3, 32 bits wide
  assign out_78 = in_4 | in_51;  // OR_Gate or_4, 32 bits wide
  assign out_77 = in_5 | in_50;  // OR_Gate or_5, 32 bits wide
  assign out_76 = in_6 | in_49;  // OR_Gate or_6, 32 bits wide
  assign out_75 = in_7 | in_48;  // OR_Gate or_7, 32 bits wide
  assign out_74 = in_8 | in_47;  // OR_Gate or_8, 32 bits wide
  assign out_73 = in_9 | in_46;  // OR_Gate or_9, 32 bits wide
  assign out_72 = in_10 | in_45;  // OR_Gate or_10, 32 bits wide
  assign out_71 = in_11 | in_44;  // OR_Gate or_11, 32 bits wide
  assign out_70 = in_12 | in_43;  // OR_Gate or_12, 32 bits wide
  assign out_69 = in_13 | in_42;  // OR_Gate or_13, 32 bits wide
  assign out_68 = in_14 | in_41;  // OR_Gate or_14, 32 bits wide
  assign out_67 = in_15 | in_40;  // OR_Gate or_15, 32 bits wide
  assign out_66 = in_16 | in_39;  // OR_Gate or_16, 32 bits wide
  assign out_65 = in_17 | in_38;  // OR_Gate or_17, 32 bits wide
  assign out_64 = in_18 | in_37;  // OR_Gate or_18, 32 bits wide
  assign out_63 = in_19 | in_36;  // OR_Gate or_19, 32 bits wide
  assign out_62 = in_20 | in_35;  // OR_Gate or_20, 32 bits wide
  assign out_61 = in_21 | in_34;  // OR_Gate or_21, 32 bits wide
  assign out_60 = in_22 | in_33;  // OR_Gate or_22, 32 bits wide
  assign out_59 = in_23 | in_32;  // OR_Gate or_23, 32 bits wide
  assign out_58 = in_24 | in_31;  // OR_Gate or_24, 32 bits wide
  assign out_57 = in_25 | in_30;  // OR_Gate or_25, 32 bits wide
  assign out_56 = in_26 | in_29;  // OR_Gate or_26, 32 bits wide
  assign out_55 = in_27 | in_28;  // OR_Gate or_27, 32 bits wide
endmodule

module roloh (
  input  in_1,
  input  star,
  input  in_3,
  output [3:0] out_4,
  output [3:0] out_5,
  output [3:0] out_6,
  output [3:0] out_7,
  output out_8
);

  wire and_1_out, and_2_out, and_3_out, and_4_out, and_5_out, and_6_out, and_7_out, and_8_out, and_9_out,
       and_10_out, and_11_out, and_12_out, clock_1_out, counter_1_carry, counter_2_carry, counter_3_carry,
       not_1_out, not_2_out, not_3_out, not_4_out, not_5_out, not_6_out, not_7_out, not_8_out, not_9_out,
       not_10_out, not_11_out, not_12_out, not_13_out, not_14_out, not_15_out, not_16_out, not_17_out,
       not_18_out, not_19_out, not_20_out, not_21_out, not_22_out, not_23_out, not_24_out, not_25_out,
       not_26_out, not_27_out, or_1_out, or_2_out, or_3_out, or_4_out, or_5_out, or_6_out, or_7_out,
       or_8_out, or_9_out, or_10_out, register_1_q, register_2_q, register_3_q, register_4_q;
  wire [3:0] bit_extender_1_out, bit_extender_2_out, bit_extender_3_out;

  or or_1 (or_1_out, star, and_6_out);
  or or_2 (or_2_out, star, and_7_out);
  or or_3 (or_3_out, counter_2_carry, in_1);
  Register #(.width(1)) register_1 (.D(or_4_out), .Q(register_1_q), .clk(or_4_out), .clr(or_5_out));  // open: en
  or or_4 (or_4_out, star, and_5_out);
  or or_5 (or_5_out, counter_3_carry, in_1);
  Register #(.width(1)) register_2 (.D(or_1_out), .Q(register_2_q), .clk(or_1_out), .clr(or_6_out));  // open: en
  or or_6 (or_6_out, counter_1_carry, in_1);
  Clock clock_1 (.out(clock_1_out));
  Bit_Extender #(.in_width(5), .out_width(4)) bit_extender_1 (.in(5'b01001), .out(bit_extender_1_out));
  Register #(.width(1)) register_3 (.D(or_2_out), .Q(register_3_q), .clk(or_2_out), .clr(or_3_out));  // open: en
  Bit_Extender #(.in_width(5), .out_width(4)) bit_extender_2 (.in(5'b01001), .out(bit_extender_2_out));
  or or_7 (or_7_out, star, counter_3_carry, and_1_out);
  and and_1 (and_1_out, out_7[3], not_1_out, not_5_out, out_7[0]);
  not not_1 (not_1_out, out_7[2]);
  Counter #(.width(4), .max('hf)) counter_1 (
    .load(1'b1), .D(bit_extender_3_out), .count(register_2_q), .Q(out_7), .carry(counter_1_carry),
    .clk(or_8_out), .clr(in_1));
  Bit_Extender #(.in_width(5), .out_width(4)) bit_extender_3 (.in(5'b01001), .out(bit_extender_3_out));
  or or_8 (or_8_out, star, counter_1_carry, and_3_out);
  and and_2 (and_2_out, clock_1_out, register_4_q);
  and and_3 (and_3_out, and_2_out, not_27_out);
  Register #(.width(1)) register_4 (.D(star), .Q(register_4_q), .clk(star), .clr(or_9_out));  // open: en
  or or_9 (or_9_out, and_12_out, in_1);
  Counter #(.width(4), .max('hf)) counter_2 (
    .load(1'b1), .D(bit_extender_1_out), .count(register_3_q), .Q(out_5), .carry(counter_2_carry),
    .clk(or_10_out), .clr(in_1));
  or or_10 (or_10_out, star, counter_2_carry, and_4_out);
  and and_4 (and_4_out, out_6[3], not_3_out, not_2_out, out_6[0]);
  not not_2 (not_2_out, out_6[1]);
  not not_3 (not_3_out, out_6[2]);
  Counter #(.width(4), .max('hf)) counter_3 (
    .load(1'b1), .D(bit_extender_2_out), .count(register_1_q), .Q(out_6), .carry(counter_3_carry),
    .clk(or_7_out), .clr(in_1));
  not not_4 (not_4_out, out_6[2]);
  and and_5 (and_5_out, out_6[3], not_4_out, not_10_out, out_6[0]);
  not not_5 (not_5_out, out_7[1]);
  not not_6 (not_6_out, out_7[1]);
  not not_7 (not_7_out, out_7[2]);
  and and_6 (and_6_out, out_7[3], not_7_out, not_6_out, out_7[0]);
  not not_8 (not_8_out, out_5[2]);
  not not_9 (not_9_out, out_5[1]);
  and and_7 (and_7_out, out_5[3], not_8_out, not_9_out, out_5[0]);
  not not_10 (not_10_out, out_6[1]);
  not not_11 (not_11_out, 1'b0);
  not not_12 (not_12_out, 1'b0);
  not not_13 (not_13_out, 1'b0);
  not not_14 (not_14_out, 1'b0);
  not not_15 (not_15_out, out_5[0]);
  not not_16 (not_16_out, out_5[1]);
  not not_17 (not_17_out, out_5[2]);
  not not_18 (not_18_out, out_5[3]);
  not not_19 (not_19_out, out_6[0]);
  not not_20 (not_20_out, out_6[1]);
  not not_21 (not_21_out, out_6[2]);
  not not_22 (not_22_out, out_6[3]);
  not not_23 (not_23_out, out_7[0]);
  not not_24 (not_24_out, out_7[1]);
  not not_25 (not_25_out, out_7[2]);
  not not_26 (not_26_out, out_7[3]);
  and and_8 (and_8_out, not_11_out, not_12_out, not_13_out, not_14_out);
  and and_9 (and_9_out, not_15_out, not_16_out, not_17_out, not_18_out);
  and and_10 (and_10_out, not_19_out, not_20_out, not_21_out, not_22_out);
  and and_11 (and_11_out, not_23_out, not_24_out, not_25_out, not_26_out);
  and and_12 (and_12_out, and_8_out, and_9_out, and_10_out, and_11_out);
  not not_27 (not_27_out, in_3);
  or or_11 (out_8, in_3, and_12_out);

  assign out_4 = 4'b0000;

  // Other names for the same wires on the sheet: rest = in_1; s = star
endmodule

module le (
  input  in_1,
  output [7:0] out_2,
  output [7:0] out_3,
  output [7:0] out_4,
  output [7:0] out_5,
  output [7:0] out_6,
  output [7:0] out_7,
  output [7:0] out_8,
  output [7:0] out_9,
  output [7:0] out_10,
  output [7:0] out_11,
  output [7:0] out_12,
  output [7:0] out_13,
  output [7:0] out_14,
  output [7:0] out_15,
  output [7:0] out_16,
  output [7:0] out_17,
  output [7:0] out_18,
  output [7:0] out_19,
  output [7:0] out_20,
  output [1:0] out_21,
  output [7:0] out_22,
  output [1:0] out_23,
  output [7:0] out_24,
  output [1:0] out_25,
  output [7:0] out_26,
  output [1:0] out_27,
  output [7:0] out_28,
  output [7:0] out_29,
  output [7:0] out_30,
  output [7:0] out_31,
  output [7:0] out_32
);

  wire [1:1] undriven, undriven_2, undriven_3, undriven_4, undriven_5, undriven_6, undriven_7, undriven_8,
       undriven_9, undriven_10, undriven_11, undriven_12, undriven_13, undriven_14, undriven_15;

  Multiplexer #(.width(8), .enable("false")) multiplexer_1 (
    .in0({8{1'b0}}), .in1({{6{1'b0}}, undriven[1], 1'b0}), .out(out_2), .sel(in_1));
  Multiplexer #(.width(8), .enable("false")) multiplexer_2 (
    .in0({8{1'b0}}), .in1({6'b010101, undriven_2[1], 1'b0}), .out(out_7), .sel(in_1));
  Multiplexer #(.width(8), .enable("false")) multiplexer_3 (
    .in0({8{1'b0}}), .in1({6'b010101, undriven_3[1], 1'b0}), .out(out_5), .sel(in_1));
  Multiplexer #(.width(8), .enable("false")) multiplexer_4 (
    .in0({8{1'b0}}), .in1({6'b011111, undriven_4[1], 1'b0}), .out(out_3), .sel(in_1));
  Multiplexer #(.width(8), .enable("false")) multiplexer_5 (
    .in0({8{1'b0}}), .in1({{6{1'b0}}, undriven_5[1], 1'b0}), .out(out_12), .sel(in_1));
  Multiplexer #(.width(8), .enable("false")) multiplexer_6 (
    .in0({8{1'b0}}), .in1({{6{1'b0}}, undriven_6[1], 1'b0}), .out(out_10), .sel(in_1));
  Multiplexer #(.width(8), .enable("false")) multiplexer_7 (
    .in0({8{1'b0}}), .in1({6'b000001, undriven_7[1], 1'b0}), .out(out_8), .sel(in_1));
  Multiplexer #(.width(8), .enable("false")) multiplexer_8 (
    .in0({8{1'b0}}), .in1({6'b000001, undriven_8[1], 1'b0}), .out(out_6), .sel(in_1));
  Multiplexer #(.width(8), .enable("false")) multiplexer_9 (
    .in0({8{1'b0}}), .in1({6'b011111, undriven_9[1], 1'b0}), .out(out_4), .sel(in_1));
  Multiplexer #(.width(2), .enable("false")) multiplexer_10 (
    .in0(2'b00), .in1({undriven_10[1], 1'b0}), .out(out_21), .sel(in_1));
  Multiplexer #(.width(8), .enable("false")) multiplexer_11 (
    .in0({8{1'b0}}), .in1({6'b011111, undriven_11[1], 1'b0}), .out(out_24), .sel(in_1));
  Multiplexer #(.width(8), .enable("false")) multiplexer_12 (
    .in0({8{1'b0}}), .in1({6'b010101, undriven_12[1], 1'b0}), .out(out_26), .sel(in_1));
  Multiplexer #(.width(8), .enable("false")) multiplexer_13 (
    .in0({8{1'b0}}), .in1({6'b010101, undriven_13[1], 1'b0}), .out(out_28), .sel(in_1));
  Multiplexer #(.width(8), .enable("false")) multiplexer_14 (
    .in0({8{1'b0}}), .in1({6'b011101, undriven_14[1], 1'b0}), .out(out_29), .sel(in_1));
  Multiplexer #(.width(8), .enable("false")) multiplexer_15 (
    .in0({8{1'b0}}), .in1({6'b000111, undriven_15[1], 1'b0}), .out(out_30), .sel(in_1));

  assign out_9 = out_2;
  assign out_11 = out_2;
  assign out_13 = out_4;
  assign out_14 = out_3;
  assign out_15 = out_6;
  assign out_16 = out_5;
  assign out_17 = out_8;
  assign out_18 = out_7;
  assign out_19 = out_2;
  assign out_20 = out_2;
  assign out_22 = out_2;
  assign out_23 = out_21;
  assign out_25 = out_21;
  assign out_27 = out_21;
  assign out_31 = out_2;
  assign out_32 = out_2;
endmodule

module nikh_h_hta (
  input  in_1,
  input  in_2,
  output [7:0] out_3,
  output [7:0] out_4,
  output [7:0] out_5,
  output [7:0] out_6,
  output [7:0] out_7,
  output [7:0] out_8,
  output [7:0] out_9,
  output [7:0] out_10,
  output [7:0] out_11,
  output [7:0] out_12,
  output [7:0] out_13,
  output [7:0] out_14,
  output [7:0] out_15,
  output [7:0] out_16,
  output [7:0] out_17,
  output [7:0] out_18,
  output [7:0] out_19,
  output [7:0] out_20,
  output [7:0] out_21,
  output [7:0] out_22,
  output [7:0] out_23,
  output [7:0] out_24,
  output [7:0] out_25,
  output [7:0] out_26,
  output [7:0] out_27,
  output [7:0] out_28,
  output [7:0] out_29,
  output [7:0] out_30,
  output [7:0] out_31,
  output [7:0] out_32,
  output [7:0] out_33,
  output [7:0] out_34,
  output [7:0] out_35,
  output [7:0] out_36,
  output [7:0] out_37,
  output [7:0] out_38,
  output [7:0] out_39,
  output [7:0] out_40,
  output [7:0] out_41,
  output [7:0] out_42,
  output [7:0] out_43,
  output [7:0] out_44,
  output [7:0] out_45,
  output [7:0] out_46,
  output [7:0] out_47
);

  wire decoder_1_out5, decoder_1_out7, not_1_out, not_2_out, not_3_out, not_4_out, shma;
  wire [7:0] controlled_buffer_1_out, controlled_buffer_3_out, controlled_buffer_5_out,
       controlled_buffer_7_out, l_1_p6, l_1_p7, l_1_p8, l_1_p9, l_1_p10, multiplexer_1_out,
       multiplexer_2_out, multiplexer_3_out, multiplexer_4_out, multiplexer_5_out, multiplexer_6_out,
       multiplexer_7_out, multiplexer_8_out, multiplexer_9_out, multiplexer_10_out, multiplexer_11_out,
       multiplexer_12_out, multiplexer_13_out, multiplexer_14_out, multiplexer_15_out, multiplexer_16_out,
       multiplexer_17_out, multiplexer_18_out, multiplexer_19_out, multiplexer_20_out, multiplexer_21_out,
       multiplexer_22_out, multiplexer_23_out, multiplexer_24_out, multiplexer_25_out, multiplexer_26_out,
       multiplexer_27_out, multiplexer_28_out, multiplexer_29_out, multiplexer_30_out, multiplexer_31_out,
       multiplexer_32_out, multiplexer_33_out, multiplexer_34_out, multiplexer_35_out, multiplexer_36_out,
       multiplexer_37_out, multiplexer_38_out, multiplexer_39_out, multiplexer_40_out, multiplexer_41_out,
       multiplexer_42_out, multiplexer_43_out, multiplexer_44_out, multiplexer_45_out, n_1_p3, n_1_p4,
       n_1_p5, n_1_p6, n_1_p7, o_1_p3, o_1_p4, o_1_p5, o_1_p6, o_1_p7, o_2_p2, o_2_p3, o_2_p4, o_2_p5,
       o_2_p6, o_3_p3, o_3_p4, o_3_p5, o_3_p6, o_3_p7, o_4_p4, o_4_p5, o_4_p6, o_4_p7, o_4_p8, ok_1_out_2,
       ok_1_out_3, ok_1_out_4, ok_1_out_5, ok_1_out_6, ok_1_out_7, ok_1_out_8, ok_1_out_9, ok_1_out_10,
       ok_1_out_11, ok_1_out_12, ok_1_out_13, ok_1_out_14, ok_1_out_15, ok_1_out_16, ok_1_out_17,
       ok_1_out_18, ok_1_out_19, ok_1_out_20, ok_1_out_21, ok_1_out_22, ok_1_out_23, ok_1_out_24,
       ok_1_out_25, ok_1_out_26, ok_1_out_27, ok_1_out_28, ok_1_out_29, ok_1_out_30, ok_1_out_31,
       ok_1_out_32, ok_1_out_33, ok_1_out_34, ok_1_out_35, ok_1_out_36, ok_1_out_37, ok_1_out_38,
       ok_1_out_39, ok_1_out_40, ok_1_out_41, ok_1_out_42, ok_1_out_43, ok_1_out_44, ok_1_out_45,
       ok_1_out_46, s_1_p3, s_1_p4, s_1_p5, s_1_p6, s_1_p7, t_1_p3, t_1_p4, t_1_p5, t_1_p6, t_1_p7, u_1_p3,
       u_1_p4, u_1_p5, u_1_p6, u_1_p7, u_2_p3, u_2_p4, u_2_p5, u_2_p6, u_2_p7, y_1_p3, y_1_p4, y_1_p5,
       y_1_p6, y_1_p7, y_2_p3, y_2_p4, y_2_p5, y_2_p6, y_2_p7;

  Decoder #(.select(3), .enable("false")) decoder_1 (
    .out1(shma), .out5(decoder_1_out5), .out7(decoder_1_out7), .sel({in_1, in_2, 1'b1}));  // open: out0, out2, out3, out4, out6
  // Y y_1: pin names not known; wires that end beside it: {8{1'b0}}, decoder_1_out5, y_1_p3, y_1_p4, y_1_p5, y_1_p6, y_1_p7, {8{1'b0}}
  // O o_1: pin names not known; wires that end beside it: {8{1'b0}}, decoder_1_out5, o_1_p3, o_1_p4, o_1_p5, o_1_p6, o_1_p7, {8{1'b0}}
  // U u_1: pin names not known; wires that end beside it: {8{1'b0}}, decoder_1_out5, u_1_p3, u_1_p4, u_1_p5, u_1_p6, u_1_p7, {8{1'b0}}, {8{1'b0}}, {8{1'b0}}
  // L l_1: pin names not known; wires that end beside it: {8{1'b0}}, {8{1'b0}}, {8{1'b0}}, {8{1'b0}}, decoder_1_out5, l_1_p6, l_1_p7, l_1_p8, l_1_p9, l_1_p10
  // S s_1: pin names not known; wires that end beside it: {8{1'b0}}, decoder_1_out5, s_1_p3, s_1_p4, s_1_p5, s_1_p6, s_1_p7, {8{1'b0}}
  // O o_2: pin names not known; wires that end beside it: decoder_1_out5, o_2_p2, o_2_p3, o_2_p4, o_2_p5, o_2_p6, {8{1'b0}}
  // T t_1: pin names not known; wires that end beside it: {8{1'b0}}, decoder_1_out5, t_1_p3, t_1_p4, t_1_p5, t_1_p6, t_1_p7, {8{1'b0}}
  // Y y_2: pin names not known; wires that end beside it: {8{1'b0}}, decoder_1_out7, y_2_p3, y_2_p4, y_2_p5, y_2_p6, y_2_p7, {8{1'b0}}
  // O o_3: pin names not known; wires that end beside it: {8{1'b0}}, decoder_1_out7, o_3_p3, o_3_p4, o_3_p5, o_3_p6, o_3_p7, {8{1'b0}}
  // U u_2: pin names not known; wires that end beside it: {8{1'b0}}, decoder_1_out7, u_2_p3, u_2_p4, u_2_p5, u_2_p6, u_2_p7, {8{1'b0}}, {8{1'b0}}, {8{1'b0}}
  assign controlled_buffer_1_out = not_1_out ? {8{1'b0}} : 8'bz;  // Controlled_Buffer controlled_buffer_1
  // O o_4: pin names not known; wires that end beside it: {8{1'b0}}, {8{1'b0}}, decoder_1_out7, o_4_p4, o_4_p5, o_4_p6, o_4_p7, o_4_p8, {8{1'b0}}
  assign controlled_buffer_1_out = decoder_1_out7 ? 8'h60 : 8'bz;  // Controlled_Buffer controlled_buffer_2
  assign controlled_buffer_3_out = not_2_out ? {8{1'b0}} : 8'bz;  // Controlled_Buffer controlled_buffer_3
  not not_1 (not_1_out, decoder_1_out7);
  not not_2 (not_2_out, decoder_1_out7);
  // N n_1: pin names not known; wires that end beside it: {8{1'b0}}, decoder_1_out7, n_1_p3, n_1_p4, n_1_p5, n_1_p6, n_1_p7, {8{1'b0}}
  assign controlled_buffer_3_out = decoder_1_out7 ? 8'h7c : 8'bz;  // Controlled_Buffer controlled_buffer_4
  assign controlled_buffer_5_out = not_3_out ? {8{1'b0}} : 8'bz;  // Controlled_Buffer controlled_buffer_5
  not not_3 (not_3_out, decoder_1_out7);
  Multiplexer #(.width(8), .enable("false")) multiplexer_1 (
    .in0({8{1'b0}}), .in1({8{1'b0}}), .out(multiplexer_1_out), .sel(in_2));
  Multiplexer #(.width(8), .enable("false")) multiplexer_2 (
    .in0(y_1_p3), .in1(y_2_p3), .out(multiplexer_2_out), .sel(in_2));
  Multiplexer #(.width(8), .enable("false")) multiplexer_3 (
    .in0(y_1_p4), .in1(y_2_p4), .out(multiplexer_3_out), .sel(in_2));
  Multiplexer #(.width(8), .enable("false")) multiplexer_4 (
    .in0(y_1_p5), .in1(y_2_p5), .out(multiplexer_4_out), .sel(in_2));
  Multiplexer #(.width(8), .enable("false")) multiplexer_5 (
    .in0(y_1_p6), .in1(y_2_p6), .out(multiplexer_5_out), .sel(in_2));
  Multiplexer #(.width(8), .enable("false")) multiplexer_6 (
    .in0(y_1_p7), .in1(y_2_p7), .out(multiplexer_6_out), .sel(in_2));
  Multiplexer #(.width(8), .enable("false")) multiplexer_7 (
    .in0({8{1'b0}}), .in1({8{1'b0}}), .out(multiplexer_7_out), .sel(in_2));
  Multiplexer #(.width(8), .enable("false")) multiplexer_8 (
    .in0(o_1_p3), .in1(o_3_p3), .out(multiplexer_8_out), .sel(in_2));
  Multiplexer #(.width(8), .enable("false")) multiplexer_9 (
    .in0(o_1_p4), .in1(o_3_p4), .out(multiplexer_9_out), .sel(in_2));
  Multiplexer #(.width(8), .enable("false")) multiplexer_10 (
    .in0(o_1_p5), .in1(o_3_p5), .out(multiplexer_10_out), .sel(in_2));
  Multiplexer #(.width(8), .enable("false")) multiplexer_11 (
    .in0(o_1_p6), .in1(o_3_p6), .out(multiplexer_11_out), .sel(in_2));
  Multiplexer #(.width(8), .enable("false")) multiplexer_12 (
    .in0(o_1_p7), .in1(o_3_p7), .out(multiplexer_12_out), .sel(in_2));
  Multiplexer #(.width(8), .enable("false")) multiplexer_13 (
    .in0({8{1'b0}}), .in1({8{1'b0}}), .out(multiplexer_13_out), .sel(in_2));
  Multiplexer #(.width(8), .enable("false")) multiplexer_14 (
    .in0(u_1_p3), .in1(u_2_p3), .out(multiplexer_14_out), .sel(in_2));
  Multiplexer #(.width(8), .enable("false")) multiplexer_15 (
    .in0(u_1_p4), .in1(u_2_p4), .out(multiplexer_15_out), .sel(in_2));
  Multiplexer #(.width(8), .enable("false")) multiplexer_16 (
    .in0(u_1_p5), .in1(u_2_p5), .out(multiplexer_16_out), .sel(in_2));
  Multiplexer #(.width(8), .enable("false")) multiplexer_17 (
    .in0(u_1_p6), .in1(u_2_p6), .out(multiplexer_17_out), .sel(in_2));
  Multiplexer #(.width(8), .enable("false")) multiplexer_18 (
    .in0(u_1_p7), .in1(u_2_p7), .out(multiplexer_18_out), .sel(in_2));
  Multiplexer #(.width(8), .enable("false")) multiplexer_19 (
    .in0({8{1'b0}}), .in1({8{1'b0}}), .out(multiplexer_19_out), .sel(in_2));
  Multiplexer #(.width(8), .enable("false")) multiplexer_20 (
    .in0({8{1'b0}}), .in1({8{1'b0}}), .out(multiplexer_20_out), .sel(in_2));
  Multiplexer #(.width(8), .enable("false")) multiplexer_21 (
    .in0({8{1'b0}}), .in1({8{1'b0}}), .out(multiplexer_21_out), .sel(in_2));
  Multiplexer #(.width(8), .enable("false")) multiplexer_22 (
    .in0({8{1'b0}}), .in1({8{1'b0}}), .out(multiplexer_22_out), .sel(in_2));
  Multiplexer #(.width(8), .enable("false")) multiplexer_23 (
    .in0(l_1_p6), .in1({8{1'b0}}), .out(multiplexer_23_out), .sel(in_2));
  Multiplexer #(.width(8), .enable("false")) multiplexer_24 (
    .in0(l_1_p7), .in1({8{1'b0}}), .out(multiplexer_24_out), .sel(in_2));
  Multiplexer #(.width(8), .enable("false")) multiplexer_25 (
    .in0(l_1_p8), .in1(controlled_buffer_3_out), .out(multiplexer_25_out), .sel(in_2));
  Multiplexer #(.width(8), .enable("false")) multiplexer_26 (
    .in0(l_1_p9), .in1(controlled_buffer_5_out), .out(multiplexer_26_out), .sel(in_2));
  Multiplexer #(.width(8), .enable("false")) multiplexer_27 (
    .in0(l_1_p10), .in1(controlled_buffer_7_out), .out(multiplexer_27_out), .sel(in_2));
  Multiplexer #(.width(8), .enable("false")) multiplexer_28 (
    .in0(o_2_p2), .in1(controlled_buffer_1_out), .out(multiplexer_28_out), .sel(in_2));
  Multiplexer #(.width(8), .enable("false")) multiplexer_29 (
    .in0(o_2_p3), .in1(controlled_buffer_7_out), .out(multiplexer_29_out), .sel(in_2));
  Multiplexer #(.width(8), .enable("false")) multiplexer_30 (
    .in0(o_2_p4), .in1(controlled_buffer_5_out), .out(multiplexer_30_out), .sel(in_2));
  Multiplexer #(.width(8), .enable("false")) multiplexer_31 (
    .in0(o_2_p5), .in1(controlled_buffer_3_out), .out(multiplexer_31_out), .sel(in_2));
  Multiplexer #(.width(8), .enable("false")) multiplexer_32 (
    .in0(o_2_p6), .in1({8{1'b0}}), .out(multiplexer_32_out), .sel(in_2));
  Multiplexer #(.width(8), .enable("false")) multiplexer_33 (
    .in0({8{1'b0}}), .in1({8{1'b0}}), .out(multiplexer_33_out), .sel(in_2));
  Multiplexer #(.width(8), .enable("false")) multiplexer_34 (
    .in0(s_1_p3), .in1(o_4_p4), .out(multiplexer_34_out), .sel(in_2));
  Multiplexer #(.width(8), .enable("false")) multiplexer_35 (
    .in0(s_1_p4), .in1(o_4_p5), .out(multiplexer_35_out), .sel(in_2));
  Multiplexer #(.width(8), .enable("false")) multiplexer_36 (
    .in0(s_1_p5), .in1(o_4_p6), .out(multiplexer_36_out), .sel(in_2));
  Multiplexer #(.width(8), .enable("false")) multiplexer_37 (
    .in0(s_1_p6), .in1(o_4_p7), .out(multiplexer_37_out), .sel(in_2));
  Multiplexer #(.width(8), .enable("false")) multiplexer_38 (
    .in0(s_1_p7), .in1(o_4_p8), .out(multiplexer_38_out), .sel(in_2));
  Multiplexer #(.width(8), .enable("false")) multiplexer_39 (
    .in0({8{1'b0}}), .in1({8{1'b0}}), .out(multiplexer_39_out), .sel(in_2));
  Multiplexer #(.width(8), .enable("false")) multiplexer_40 (
    .in0(t_1_p3), .in1(n_1_p3), .out(multiplexer_40_out), .sel(in_2));
  Multiplexer #(.width(8), .enable("false")) multiplexer_41 (
    .in0(t_1_p4), .in1(n_1_p4), .out(multiplexer_41_out), .sel(in_2));
  Multiplexer #(.width(8), .enable("false")) multiplexer_42 (
    .in0(t_1_p5), .in1(n_1_p5), .out(multiplexer_42_out), .sel(in_2));
  Multiplexer #(.width(8), .enable("false")) multiplexer_43 (
    .in0(t_1_p6), .in1(n_1_p6), .out(multiplexer_43_out), .sel(in_2));
  Multiplexer #(.width(8), .enable("false")) multiplexer_44 (
    .in0(t_1_p7), .in1(n_1_p7), .out(multiplexer_44_out), .sel(in_2));
  Multiplexer #(.width(8), .enable("false")) multiplexer_45 (
    .in0({8{1'b0}}), .in1({8{1'b0}}), .out(multiplexer_45_out), .sel(in_2));
  assign controlled_buffer_5_out = decoder_1_out7 ? 8'h6 : 8'bz;  // Controlled_Buffer controlled_buffer_6
  assign controlled_buffer_7_out = not_4_out ? {8{1'b0}} : 8'bz;  // Controlled_Buffer controlled_buffer_7
  not not_4 (not_4_out, decoder_1_out7);
  assign controlled_buffer_7_out = decoder_1_out7 ? 8'h3c : 8'bz;  // Controlled_Buffer controlled_buffer_8
  ok ok_1 (
    .in_1(shma), .out_46(ok_1_out_46), .out_45(ok_1_out_45), .out_44(ok_1_out_44), .out_43(ok_1_out_43),
    .out_42(ok_1_out_42), .out_41(ok_1_out_41), .out_40(ok_1_out_40), .out_39(ok_1_out_39),
    .out_38(ok_1_out_38), .out_37(ok_1_out_37), .out_36(ok_1_out_36), .out_35(ok_1_out_35),
    .out_34(ok_1_out_34), .out_33(ok_1_out_33), .out_32(ok_1_out_32), .out_31(ok_1_out_31),
    .out_30(ok_1_out_30), .out_29(ok_1_out_29), .out_28(ok_1_out_28), .out_27(ok_1_out_27),
    .out_26(ok_1_out_26), .out_25(ok_1_out_25), .out_24(ok_1_out_24), .out_23(ok_1_out_23),
    .out_22(ok_1_out_22), .out_21(ok_1_out_21), .out_20(ok_1_out_20), .out_19(ok_1_out_19),
    .out_18(ok_1_out_18), .out_17(ok_1_out_17), .out_16(ok_1_out_16), .out_15(ok_1_out_15),
    .out_14(ok_1_out_14), .out_13(ok_1_out_13), .out_12(ok_1_out_12), .out_11(ok_1_out_11),
    .out_10(ok_1_out_10), .out_9(ok_1_out_9), .out_8(ok_1_out_8), .out_7(ok_1_out_7), .out_6(ok_1_out_6),
    .out_5(ok_1_out_5), .out_4(ok_1_out_4), .out_3(ok_1_out_3), .out_2(ok_1_out_2));
  Multiplexer #(.width(8), .enable("false")) multiplexer_46 (
    .in0(ok_1_out_46), .in1(multiplexer_1_out), .out(out_47), .sel(in_1));
  Multiplexer #(.width(8), .enable("false")) multiplexer_47 (
    .in0(ok_1_out_45), .in1(multiplexer_2_out), .out(out_46), .sel(in_1));
  Multiplexer #(.width(8), .enable("false")) multiplexer_48 (
    .in0(ok_1_out_44), .in1(multiplexer_3_out), .out(out_45), .sel(in_1));
  Multiplexer #(.width(8), .enable("false")) multiplexer_49 (
    .in0(ok_1_out_43), .in1(multiplexer_4_out), .out(out_44), .sel(in_1));
  Multiplexer #(.width(8), .enable("false")) multiplexer_50 (
    .in0(ok_1_out_42), .in1(multiplexer_5_out), .out(out_43), .sel(in_1));
  Multiplexer #(.width(8), .enable("false")) multiplexer_51 (
    .in0(ok_1_out_41), .in1(multiplexer_6_out), .out(out_42), .sel(in_1));
  Multiplexer #(.width(8), .enable("false")) multiplexer_52 (
    .in0(ok_1_out_40), .in1(multiplexer_7_out), .out(out_41), .sel(in_1));
  Multiplexer #(.width(8), .enable("false")) multiplexer_53 (
    .in0(ok_1_out_39), .in1(multiplexer_8_out), .out(out_40), .sel(in_1));
  Multiplexer #(.width(8), .enable("false")) multiplexer_54 (
    .in0(ok_1_out_38), .in1(multiplexer_9_out), .out(out_39), .sel(in_1));
  Multiplexer #(.width(8), .enable("false")) multiplexer_55 (
    .in0(ok_1_out_37), .in1(multiplexer_10_out), .out(out_38), .sel(in_1));
  Multiplexer #(.width(8), .enable("false")) multiplexer_56 (
    .in0(ok_1_out_36), .in1(multiplexer_11_out), .out(out_37), .sel(in_1));
  Multiplexer #(.width(8), .enable("false")) multiplexer_57 (
    .in0(ok_1_out_35), .in1(multiplexer_12_out), .out(out_36), .sel(in_1));
  Multiplexer #(.width(8), .enable("false")) multiplexer_58 (
    .in0(ok_1_out_34), .in1(multiplexer_13_out), .out(out_35), .sel(in_1));
  Multiplexer #(.width(8), .enable("false")) multiplexer_59 (
    .in0(ok_1_out_33), .in1(multiplexer_14_out), .out(out_34), .sel(in_1));
  Multiplexer #(.width(8), .enable("false")) multiplexer_60 (
    .in0(ok_1_out_32), .in1(multiplexer_15_out), .out(out_33), .sel(in_1));
  Multiplexer #(.width(8), .enable("false")) multiplexer_61 (
    .in0(ok_1_out_31), .in1(multiplexer_16_out), .out(out_32), .sel(in_1));
  Multiplexer #(.width(8), .enable("false")) multiplexer_62 (
    .in0(ok_1_out_30), .in1(multiplexer_17_out), .out(out_31), .sel(in_1));
  Multiplexer #(.width(8), .enable("false")) multiplexer_63 (
    .in0(ok_1_out_29), .in1(multiplexer_18_out), .out(out_30), .sel(in_1));
  Multiplexer #(.width(8), .enable("false")) multiplexer_64 (
    .in0(ok_1_out_28), .in1(multiplexer_19_out), .out(out_29), .sel(in_1));
  Multiplexer #(.width(8), .enable("false")) multiplexer_65 (
    .in0(ok_1_out_27), .in1(multiplexer_20_out), .out(out_28), .sel(in_1));
  Multiplexer #(.width(8), .enable("false")) multiplexer_66 (
    .in0(ok_1_out_26), .in1(multiplexer_21_out), .out(out_27), .sel(in_1));
  Multiplexer #(.width(8), .enable("false")) multiplexer_67 (
    .in0(ok_1_out_25), .in1(multiplexer_22_out), .out(out_26), .sel(in_1));
  Multiplexer #(.width(8), .enable("false")) multiplexer_68 (
    .in0(ok_1_out_24), .in1(multiplexer_23_out), .out(out_25), .sel(in_1));
  Multiplexer #(.width(8), .enable("false")) multiplexer_69 (
    .in0(ok_1_out_23), .in1(multiplexer_24_out), .out(out_24), .sel(in_1));
  Multiplexer #(.width(8), .enable("false")) multiplexer_70 (
    .in0(ok_1_out_22), .in1(multiplexer_25_out), .out(out_23), .sel(in_1));
  Multiplexer #(.width(8), .enable("false")) multiplexer_71 (
    .in0(ok_1_out_21), .in1(multiplexer_26_out), .out(out_22), .sel(in_1));
  Multiplexer #(.width(8), .enable("false")) multiplexer_72 (
    .in0(ok_1_out_20), .in1(multiplexer_27_out), .out(out_21), .sel(in_1));
  Multiplexer #(.width(8), .enable("false")) multiplexer_73 (
    .in0(ok_1_out_19), .in1(multiplexer_28_out), .out(out_20), .sel(in_1));
  Multiplexer #(.width(8), .enable("false")) multiplexer_74 (
    .in0(ok_1_out_18), .in1(multiplexer_29_out), .out(out_19), .sel(in_1));
  Multiplexer #(.width(8), .enable("false")) multiplexer_75 (
    .in0(ok_1_out_17), .in1(multiplexer_30_out), .out(out_18), .sel(in_1));
  Multiplexer #(.width(8), .enable("false")) multiplexer_76 (
    .in0(ok_1_out_16), .in1(multiplexer_31_out), .out(out_17), .sel(in_1));
  Multiplexer #(.width(8), .enable("false")) multiplexer_77 (
    .in0(ok_1_out_15), .in1(multiplexer_32_out), .out(out_16), .sel(in_1));
  Multiplexer #(.width(8), .enable("false")) multiplexer_78 (
    .in0(ok_1_out_14), .in1(multiplexer_33_out), .out(out_15), .sel(in_1));
  Multiplexer #(.width(8), .enable("false")) multiplexer_79 (
    .in0(ok_1_out_13), .in1(multiplexer_34_out), .out(out_14), .sel(in_1));
  Multiplexer #(.width(8), .enable("false")) multiplexer_80 (
    .in0(ok_1_out_12), .in1(multiplexer_35_out), .out(out_13), .sel(in_1));
  Multiplexer #(.width(8), .enable("false")) multiplexer_81 (
    .in0(ok_1_out_11), .in1(multiplexer_36_out), .out(out_12), .sel(in_1));
  Multiplexer #(.width(8), .enable("false")) multiplexer_82 (
    .in0(ok_1_out_10), .in1(multiplexer_37_out), .out(out_11), .sel(in_1));
  Multiplexer #(.width(8), .enable("false")) multiplexer_83 (
    .in0(ok_1_out_9), .in1(multiplexer_38_out), .out(out_10), .sel(in_1));
  Multiplexer #(.width(8), .enable("false")) multiplexer_84 (
    .in0(ok_1_out_8), .in1(multiplexer_39_out), .out(out_9), .sel(in_1));
  Multiplexer #(.width(8), .enable("false")) multiplexer_85 (
    .in0(ok_1_out_7), .in1(multiplexer_40_out), .out(out_8), .sel(in_1));
  Multiplexer #(.width(8), .enable("false")) multiplexer_86 (
    .in0(ok_1_out_6), .in1(multiplexer_41_out), .out(out_7), .sel(in_1));
  Multiplexer #(.width(8), .enable("false")) multiplexer_87 (
    .in0(ok_1_out_5), .in1(multiplexer_42_out), .out(out_6), .sel(in_1));
  Multiplexer #(.width(8), .enable("false")) multiplexer_88 (
    .in0(ok_1_out_4), .in1(multiplexer_43_out), .out(out_5), .sel(in_1));
  Multiplexer #(.width(8), .enable("false")) multiplexer_89 (
    .in0(ok_1_out_3), .in1(multiplexer_44_out), .out(out_4), .sel(in_1));
  Multiplexer #(.width(8), .enable("false")) multiplexer_90 (
    .in0(ok_1_out_2), .in1(multiplexer_45_out), .out(out_3), .sel(in_1));

  // Other names for the same wires on the sheet: s = in_2; m = in_1
endmodule

module sos_sos (
  input  in_1,
  input  [31:0] in_2,
  input  [31:0] in_3,
  input  [31:0] in_4,
  input  [31:0] in_5,
  input  [31:0] in_6,
  input  [31:0] in_7,
  input  [31:0] in_8,
  input  [31:0] in_9,
  input  [31:0] in_10,
  input  [31:0] in_11,
  input  [31:0] in_12,
  input  [31:0] in_13,
  input  [31:0] in_14,
  input  [31:0] in_15,
  input  [31:0] in_16,
  input  [31:0] in_17,
  input  [31:0] in_18,
  input  [31:0] in_19,
  input  [31:0] in_20,
  input  [31:0] in_21,
  input  [31:0] in_22,
  input  [31:0] in_23,
  input  [31:0] in_24,
  input  [31:0] in_25,
  input  [31:0] in_26,
  input  [31:0] in_27,
  input  [31:0] in_28,
  input  [31:0] in_29,
  input  [31:0] in_30,
  input  [31:0] in_31,
  input  [31:0] in_32,
  output [31:0] out_33,
  output [31:0] out_34,
  output [31:0] out_35,
  output [31:0] out_36,
  output [31:0] out_37,
  output [31:0] out_38,
  output [31:0] out_39,
  output [31:0] out_40,
  output [31:0] out_41,
  output [31:0] out_42,
  output [31:0] out_43,
  output [31:0] out_44,
  output [31:0] out_45,
  output [31:0] out_46,
  output [31:0] out_47,
  output [31:0] out_48,
  output [31:0] out_49,
  output [31:0] out_50,
  output [31:0] out_51,
  output [31:0] out_52,
  output [31:0] out_53,
  output [31:0] out_54,
  output [31:0] out_55,
  output [31:0] out_56,
  output [31:0] out_57,
  output [31:0] out_58,
  output [31:0] out_59,
  output [31:0] out_60,
  output [31:0] out_61,
  output [31:0] out_62,
  output [31:0] out_63
);

  Multiplexer #(.width(32), .enable("false")) multiplexer_1 (.in0({32{1'b0}}), .in1(in_2), .out(out_33), .sel(in_1));
  Multiplexer #(.width(32), .enable("false")) multiplexer_2 (.in0({32{1'b0}}), .in1(in_3), .out(out_34), .sel(in_1));
  Multiplexer #(.width(32), .enable("false")) multiplexer_3 (.in0({32{1'b0}}), .in1(in_4), .out(out_35), .sel(in_1));
  Multiplexer #(.width(32), .enable("false")) multiplexer_4 (.in0({32{1'b0}}), .in1(in_5), .out(out_36), .sel(in_1));
  Multiplexer #(.width(32), .enable("false")) multiplexer_5 (.in0({32{1'b0}}), .in1(in_6), .out(out_37), .sel(in_1));
  Multiplexer #(.width(32), .enable("false")) multiplexer_6 (.in0({32{1'b0}}), .in1(in_7), .out(out_38), .sel(in_1));
  Multiplexer #(.width(32), .enable("false")) multiplexer_7 (.in0({32{1'b0}}), .in1(in_8), .out(out_39), .sel(in_1));
  Multiplexer #(.width(32), .enable("false")) multiplexer_8 (.in0({32{1'b0}}), .in1(in_9), .out(out_40), .sel(in_1));
  Multiplexer #(.width(32), .enable("false")) multiplexer_9 (.in0({32{1'b0}}), .in1(in_10), .out(out_41), .sel(in_1));
  Multiplexer #(.width(32), .enable("false")) multiplexer_10 (.in0({32{1'b0}}), .in1(in_11), .out(out_42), .sel(in_1));
  Multiplexer #(.width(32), .enable("false")) multiplexer_11 (.in0({32{1'b0}}), .in1(in_12), .out(out_43), .sel(in_1));
  Multiplexer #(.width(32), .enable("false")) multiplexer_12 (.in0({32{1'b0}}), .in1(in_13), .out(out_44), .sel(in_1));
  Multiplexer #(.width(32), .enable("false")) multiplexer_13 (.in0({32{1'b0}}), .in1(in_14), .out(out_45), .sel(in_1));
  Multiplexer #(.width(32), .enable("false")) multiplexer_14 (.in0({32{1'b0}}), .in1(in_15), .out(out_46), .sel(in_1));
  Multiplexer #(.width(32), .enable("false")) multiplexer_15 (.in0({32{1'b0}}), .in1(in_16), .out(out_47), .sel(in_1));
  Multiplexer #(.width(32), .enable("false")) multiplexer_16 (.in0({32{1'b0}}), .in1(in_17), .out(out_48), .sel(in_1));
  Multiplexer #(.width(32), .enable("false")) multiplexer_17 (.in0({32{1'b0}}), .in1(in_18), .out(out_49), .sel(in_1));
  Multiplexer #(.width(32), .enable("false")) multiplexer_18 (.in0({32{1'b0}}), .in1(in_19), .out(out_50), .sel(in_1));
  Multiplexer #(.width(32), .enable("false")) multiplexer_19 (.in0({32{1'b0}}), .in1(in_20), .out(out_51), .sel(in_1));
  Multiplexer #(.width(32), .enable("false")) multiplexer_20 (.in0({32{1'b0}}), .in1(in_21), .out(out_52), .sel(in_1));
  Multiplexer #(.width(32), .enable("false")) multiplexer_21 (.in0({32{1'b0}}), .in1(in_22), .out(out_53), .sel(in_1));
  Multiplexer #(.width(32), .enable("false")) multiplexer_22 (.in0({32{1'b0}}), .in1(in_23), .out(out_54), .sel(in_1));
  Multiplexer #(.width(32), .enable("false")) multiplexer_23 (.in0({32{1'b0}}), .in1(in_24), .out(out_55), .sel(in_1));
  Multiplexer #(.width(32), .enable("false")) multiplexer_24 (.in0({32{1'b0}}), .in1(in_25), .out(out_56), .sel(in_1));
  Multiplexer #(.width(32), .enable("false")) multiplexer_25 (.in0({32{1'b0}}), .in1(in_26), .out(out_57), .sel(in_1));
  Multiplexer #(.width(32), .enable("false")) multiplexer_26 (.in0({32{1'b0}}), .in1(in_27), .out(out_58), .sel(in_1));
  Multiplexer #(.width(32), .enable("false")) multiplexer_27 (.in0({32{1'b0}}), .in1(in_28), .out(out_59), .sel(in_1));
  Multiplexer #(.width(32), .enable("false")) multiplexer_28 (.in0({32{1'b0}}), .in1(in_29), .out(out_60), .sel(in_1));
  Multiplexer #(.width(32), .enable("false")) multiplexer_29 (.in0({32{1'b0}}), .in1(in_30), .out(out_61), .sel(in_1));
  Multiplexer #(.width(32), .enable("false")) multiplexer_30 (.in0({32{1'b0}}), .in1(in_31), .out(out_62), .sel(in_1));
  Multiplexer #(.width(32), .enable("false")) multiplexer_31 (.in0({32{1'b0}}), .in1(in_32), .out(out_63), .sel(in_1));
endmodule

module dejia_aristera (
  input  in_1,
  input  in_2,
  input  in_3,
  input  [31:0] in_4,
  input  [31:0] in_5,
  input  [31:0] in_6,
  input  [31:0] in_7,
  input  [31:0] in_8,
  input  [31:0] in_9,
  input  [31:0] in_10,
  input  [31:0] in_11,
  input  [31:0] in_12,
  output [31:0] out_13,
  output [31:0] out_14,
  output [31:0] out_15,
  output [31:0] out_16,
  output [31:0] out_17,
  output [31:0] out_18,
  output [31:0] out_19,
  output [31:0] out_20,
  output [31:0] out_21,
  output [31:0] out_22,
  output [31:0] out_23,
  output [31:0] out_24,
  output [31:0] out_25,
  output [31:0] out_26,
  output [31:0] out_27,
  output [31:0] out_28,
  output [31:0] out_29,
  output [31:0] out_30,
  output [31:0] out_31,
  output [31:0] out_32,
  output [31:0] out_33,
  output [31:0] out_34,
  output [31:0] out_35,
  output [31:0] out_36,
  output [31:0] out_37,
  output [31:0] out_38,
  output [31:0] out_39,
  output [4:0] out_40
);

  wire and_1_out, and_2_out, comparator_1_eq, comparator_1_gt, comparator_2_eq, comparator_3_eq,
       comparator_3_lt, comparator_4_eq, not_1_out, not_2_out, not_3_out, or_1_out, or_2_out, or_3_out,
       or_4_out, or_5_out;
  wire [5:0] bit_extender_1_out, bit_extender_2_out, bit_extender_3_out, bit_extender_4_out;

  Multiplexer #(.select(5), .width(32), .enable("false")) multiplexer_1 (
    .in0(in_12), .in1({32{1'b0}}), .in2({32{1'b0}}), .in3({32{1'b0}}), .in4({32{1'b0}}), .in5({32{1'b0}}),
    .in6({32{1'b0}}), .in7({32{1'b0}}), .in8({32{1'b0}}), .in9({32{1'b0}}), .in10({32{1'b0}}),
    .in11({32{1'b0}}), .in12({32{1'b0}}), .in13({32{1'b0}}), .in14({32{1'b0}}), .in15({32{1'b0}}),
    .in16({32{1'b0}}), .in17({32{1'b0}}), .in18({32{1'b0}}), .in19({32{1'b0}}), .in20({32{1'b0}}),
    .in21({32{1'b0}}), .in22({32{1'b0}}), .in23({32{1'b0}}), .in24({32{1'b0}}), .in25({32{1'b0}}),
    .in26({32{1'b0}}), .in27({32{1'b0}}), .in28({32{1'b0}}), .in29({32{1'b0}}), .in30({32{1'b0}}),
    .in31({32{1'b0}}), .out(out_13), .sel(out_40));
  Multiplexer #(.select(5), .width(32), .enable("false")) multiplexer_2 (
    .in0(in_11), .in1(in_12), .in2({32{1'b0}}), .in3({32{1'b0}}), .in4({32{1'b0}}), .in5({32{1'b0}}),
    .in6({32{1'b0}}), .in7({32{1'b0}}), .in8({32{1'b0}}), .in9({32{1'b0}}), .in10({32{1'b0}}),
    .in11({32{1'b0}}), .in12({32{1'b0}}), .in13({32{1'b0}}), .in14({32{1'b0}}), .in15({32{1'b0}}),
    .in16({32{1'b0}}), .in17({32{1'b0}}), .in18({32{1'b0}}), .in19({32{1'b0}}), .in20({32{1'b0}}),
    .in21({32{1'b0}}), .in22({32{1'b0}}), .in23({32{1'b0}}), .in24({32{1'b0}}), .in25({32{1'b0}}),
    .in26({32{1'b0}}), .in27({32{1'b0}}), .in28({32{1'b0}}), .in29({32{1'b0}}), .in30({32{1'b0}}),
    .in31({32{1'b0}}), .out(out_14), .sel(out_40));
  Multiplexer #(.select(5), .width(32), .enable("false")) multiplexer_3 (
    .in0(in_10), .in1(in_11), .in2(in_12), .in3({32{1'b0}}), .in4({32{1'b0}}), .in5({32{1'b0}}),
    .in6({32{1'b0}}), .in7({32{1'b0}}), .in8({32{1'b0}}), .in9({32{1'b0}}), .in10({32{1'b0}}),
    .in11({32{1'b0}}), .in12({32{1'b0}}), .in13({32{1'b0}}), .in14({32{1'b0}}), .in15({32{1'b0}}),
    .in16({32{1'b0}}), .in17({32{1'b0}}), .in18({32{1'b0}}), .in19({32{1'b0}}), .in20({32{1'b0}}),
    .in21({32{1'b0}}), .in22({32{1'b0}}), .in23({32{1'b0}}), .in24({32{1'b0}}), .in25({32{1'b0}}),
    .in26({32{1'b0}}), .out(out_15), .sel(out_40));  // open: in27, in28, in29, in30, in31
  Multiplexer #(.select(5), .width(32), .enable("false")) multiplexer_4 (
    .in0(in_9), .in1(in_10), .in2(in_11), .in3(in_12), .in4({32{1'b0}}), .in5({32{1'b0}}), .in6({32{1'b0}}),
    .in7({32{1'b0}}), .in8({32{1'b0}}), .in9({32{1'b0}}), .in10({32{1'b0}}), .in11({32{1'b0}}),
    .in12({32{1'b0}}), .in13({32{1'b0}}), .in14({32{1'b0}}), .in15({32{1'b0}}), .in16({32{1'b0}}),
    .in17({32{1'b0}}), .in18({32{1'b0}}), .in19({32{1'b0}}), .in20({32{1'b0}}), .in21({32{1'b0}}),
    .in22({32{1'b0}}), .in23({32{1'b0}}), .in24({32{1'b0}}), .in25({32{1'b0}}), .in26({32{1'b0}}),
    .out(out_16), .sel(out_40));  // open: in27, in28, in29, in30, in31
  Multiplexer #(.select(5), .width(32), .enable("false")) multiplexer_5 (
    .in0(in_8), .in1(in_9), .in2(in_10), .in3(in_11), .in4(in_12), .in5({32{1'b0}}), .in6({32{1'b0}}),
    .in7({32{1'b0}}), .in8({32{1'b0}}), .in9({32{1'b0}}), .in10({32{1'b0}}), .in11({32{1'b0}}),
    .in12({32{1'b0}}), .in13({32{1'b0}}), .in14({32{1'b0}}), .in15({32{1'b0}}), .in16({32{1'b0}}),
    .in17({32{1'b0}}), .in18({32{1'b0}}), .in19({32{1'b0}}), .in20({32{1'b0}}), .in21({32{1'b0}}),
    .in22({32{1'b0}}), .in23({32{1'b0}}), .in24({32{1'b0}}), .in25({32{1'b0}}), .in26({32{1'b0}}),
    .in27({32{1'b0}}), .in28({32{1'b0}}), .in29({32{1'b0}}), .in30({32{1'b0}}), .in31({32{1'b0}}),
    .out(out_17), .sel(out_40));
  Multiplexer #(.select(5), .width(32), .enable("false")) multiplexer_6 (
    .in0(in_7), .in1(in_8), .in2(in_9), .in3(in_10), .in4(in_11), .in5(in_12), .in6({32{1'b0}}),
    .in7({32{1'b0}}), .in8({32{1'b0}}), .in9({32{1'b0}}), .in10({32{1'b0}}), .in11({32{1'b0}}),
    .in12({32{1'b0}}), .in13({32{1'b0}}), .in14({32{1'b0}}), .in15({32{1'b0}}), .in16({32{1'b0}}),
    .in17({32{1'b0}}), .in18({32{1'b0}}), .in19({32{1'b0}}), .in20({32{1'b0}}), .in21({32{1'b0}}),
    .in22({32{1'b0}}), .in23({32{1'b0}}), .in24({32{1'b0}}), .in25({32{1'b0}}), .in26({32{1'b0}}),
    .in27({32{1'b0}}), .in28({32{1'b0}}), .in29({32{1'b0}}), .in30({32{1'b0}}), .in31({32{1'b0}}),
    .out(out_18), .sel(out_40));
  Multiplexer #(.select(5), .width(32), .enable("false")) multiplexer_7 (
    .in0(in_6), .in1(in_7), .in2(in_8), .in3(in_9), .in4(in_10), .in5(in_11), .in6(in_12), .in7({32{1'b0}}),
    .in8({32{1'b0}}), .in9({32{1'b0}}), .in10({32{1'b0}}), .in11({32{1'b0}}), .in12({32{1'b0}}),
    .in13({32{1'b0}}), .in14({32{1'b0}}), .in15({32{1'b0}}), .in16({32{1'b0}}), .in17({32{1'b0}}),
    .in18({32{1'b0}}), .in19({32{1'b0}}), .in20({32{1'b0}}), .in21({32{1'b0}}), .in22({32{1'b0}}),
    .in23({32{1'b0}}), .in24({32{1'b0}}), .in25({32{1'b0}}), .in26({32{1'b0}}), .in27({32{1'b0}}),
    .in28({32{1'b0}}), .in29({32{1'b0}}), .in30({32{1'b0}}), .in31({32{1'b0}}), .out(out_19), .sel(out_40));
  Multiplexer #(.select(5), .width(32), .enable("false")) multiplexer_8 (
    .in0(in_5), .in1(in_6), .in2(in_7), .in3(in_8), .in4(in_9), .in5(in_10), .in6(in_11), .in7(in_12),
    .in8({32{1'b0}}), .in9({32{1'b0}}), .in10({32{1'b0}}), .in11({32{1'b0}}), .in12({32{1'b0}}),
    .in13({32{1'b0}}), .in14({32{1'b0}}), .in15({32{1'b0}}), .in16({32{1'b0}}), .in17({32{1'b0}}),
    .in18({32{1'b0}}), .in19({32{1'b0}}), .in20({32{1'b0}}), .in21({32{1'b0}}), .in22({32{1'b0}}),
    .in23({32{1'b0}}), .in24({32{1'b0}}), .in25({32{1'b0}}), .in26({32{1'b0}}), .in27({32{1'b0}}),
    .in28({32{1'b0}}), .in29({32{1'b0}}), .in30({32{1'b0}}), .in31({32{1'b0}}), .out(out_20), .sel(out_40));
  Multiplexer #(.select(5), .width(32), .enable("false")) multiplexer_9 (
    .in0(in_4), .in1(in_5), .in2(in_6), .in3(in_7), .in4(in_8), .in5(in_9), .in6(in_10), .in7(in_11),
    .in8(in_12), .in9({32{1'b0}}), .in10({32{1'b0}}), .in11({32{1'b0}}), .in12({32{1'b0}}),
    .in13({32{1'b0}}), .in14({32{1'b0}}), .in15({32{1'b0}}), .in16({32{1'b0}}), .in17({32{1'b0}}),
    .in18({32{1'b0}}), .in19({32{1'b0}}), .in20({32{1'b0}}), .in21({32{1'b0}}), .in22({32{1'b0}}),
    .in23({32{1'b0}}), .in24({32{1'b0}}), .in25({32{1'b0}}), .in26({32{1'b0}}), .in27({32{1'b0}}),
    .in28({32{1'b0}}), .in29({32{1'b0}}), .in30({32{1'b0}}), .in31({32{1'b0}}), .out(out_21), .sel(out_40));
  Multiplexer #(.select(5), .width(32), .enable("false")) multiplexer_10 (
    .in0({32{1'b0}}), .in1(in_4), .in2(in_5), .in3(in_6), .in4(in_7), .in5(in_8), .in6(in_9), .in7(in_10),
    .in8(in_11), .in9(in_12), .in10({32{1'b0}}), .in11({32{1'b0}}), .in12({32{1'b0}}), .in13({32{1'b0}}),
    .in14({32{1'b0}}), .in15({32{1'b0}}), .in16({32{1'b0}}), .in17({32{1'b0}}), .in18({32{1'b0}}),
    .in19({32{1'b0}}), .in20({32{1'b0}}), .in21({32{1'b0}}), .in22({32{1'b0}}), .in23({32{1'b0}}),
    .in24({32{1'b0}}), .in25({32{1'b0}}), .in26({32{1'b0}}), .in27({32{1'b0}}), .in28({32{1'b0}}),
    .in29({32{1'b0}}), .in30({32{1'b0}}), .in31({32{1'b0}}), .out(out_22), .sel(out_40));
  Multiplexer #(.select(5), .width(32), .enable("false")) multiplexer_11 (
    .in0({32{1'b0}}), .in1({32{1'b0}}), .in2(in_4), .in3(in_5), .in4(in_6), .in5(in_7), .in6(in_8),
    .in7(in_9), .in8(in_10), .in9(in_11), .in10(in_12), .in11({32{1'b0}}), .in12({32{1'b0}}),
    .in13({32{1'b0}}), .in14({32{1'b0}}), .in15({32{1'b0}}), .in16({32{1'b0}}), .in17({32{1'b0}}),
    .in18({32{1'b0}}), .in19({32{1'b0}}), .in20({32{1'b0}}), .in21({32{1'b0}}), .in22({32{1'b0}}),
    .in23({32{1'b0}}), .in24({32{1'b0}}), .in25({32{1'b0}}), .in26({32{1'b0}}), .in27({32{1'b0}}),
    .in28({32{1'b0}}), .in29({32{1'b0}}), .in30({32{1'b0}}), .in31({32{1'b0}}), .out(out_23), .sel(out_40));
  Multiplexer #(.select(5), .width(32), .enable("false")) multiplexer_12 (
    .in0({32{1'b0}}), .in1({32{1'b0}}), .in2({32{1'b0}}), .in3(in_4), .in4(in_5), .in5(in_6), .in6(in_7),
    .in7(in_8), .in8(in_9), .in9(in_10), .in10(in_11), .in11(in_12), .in12({32{1'b0}}), .in13({32{1'b0}}),
    .in14({32{1'b0}}), .in15({32{1'b0}}), .in16({32{1'b0}}), .in17({32{1'b0}}), .in18({32{1'b0}}),
    .in19({32{1'b0}}), .in20({32{1'b0}}), .in21({32{1'b0}}), .in22({32{1'b0}}), .in23({32{1'b0}}),
    .in24({32{1'b0}}), .in25({32{1'b0}}), .in26({32{1'b0}}), .in27({32{1'b0}}), .in28({32{1'b0}}),
    .in29({32{1'b0}}), .in30({32{1'b0}}), .in31({32{1'b0}}), .out(out_24), .sel(out_40));
  Multiplexer #(.select(5), .width(32), .enable("false")) multiplexer_13 (
    .in0({32{1'b0}}), .in1({32{1'b0}}), .in2({32{1'b0}}), .in3({32{1'b0}}), .in4(in_4), .in5(in_5),
    .in6(in_6), .in7(in_7), .in8(in_8), .in9(in_9), .in10(in_10), .in11(in_11), .in12(in_12),
    .in13({32{1'b0}}), .in14({32{1'b0}}), .in15({32{1'b0}}), .in16({32{1'b0}}), .in17({32{1'b0}}),
    .in18({32{1'b0}}), .in19({32{1'b0}}), .in20({32{1'b0}}), .in21({32{1'b0}}), .in22({32{1'b0}}),
    .in23({32{1'b0}}), .in24({32{1'b0}}), .in25({32{1'b0}}), .in26({32{1'b0}}), .in27({32{1'b0}}),
    .in28({32{1'b0}}), .in29({32{1'b0}}), .in30({32{1'b0}}), .in31({32{1'b0}}), .out(out_25), .sel(out_40));
  Multiplexer #(.select(5), .width(32), .enable("false")) multiplexer_14 (
    .in0({32{1'b0}}), .in1({32{1'b0}}), .in2({32{1'b0}}), .in3({32{1'b0}}), .in4({32{1'b0}}), .in5(in_4),
    .in6(in_5), .in7(in_6), .in8(in_7), .in9(in_8), .in10(in_9), .in11(in_10), .in12(in_11), .in13(in_12),
    .in14({32{1'b0}}), .in15({32{1'b0}}), .in16({32{1'b0}}), .in17({32{1'b0}}), .in18({32{1'b0}}),
    .in19({32{1'b0}}), .in20({32{1'b0}}), .in21({32{1'b0}}), .in22({32{1'b0}}), .in23({32{1'b0}}),
    .in24({32{1'b0}}), .in25({32{1'b0}}), .in26({32{1'b0}}), .in27({32{1'b0}}), .in28({32{1'b0}}),
    .in29({32{1'b0}}), .in30({32{1'b0}}), .in31({32{1'b0}}), .out(out_26), .sel(out_40));
  Multiplexer #(.select(5), .width(32), .enable("false")) multiplexer_15 (
    .in0({32{1'b0}}), .in1({32{1'b0}}), .in2({32{1'b0}}), .in3({32{1'b0}}), .in4({32{1'b0}}),
    .in5({32{1'b0}}), .in6(in_4), .in7(in_5), .in8(in_6), .in9(in_7), .in10(in_8), .in11(in_9), .in12(in_10),
    .in13(in_11), .in14(in_12), .in15({32{1'b0}}), .in16({32{1'b0}}), .in17({32{1'b0}}), .in18({32{1'b0}}),
    .in19({32{1'b0}}), .in20({32{1'b0}}), .in21({32{1'b0}}), .in22({32{1'b0}}), .in23({32{1'b0}}),
    .in24({32{1'b0}}), .in25({32{1'b0}}), .in26({32{1'b0}}), .in27({32{1'b0}}), .in28({32{1'b0}}),
    .in29({32{1'b0}}), .in30({32{1'b0}}), .in31({32{1'b0}}), .out(out_27), .sel(out_40));
  Multiplexer #(.select(5), .width(32), .enable("false")) multiplexer_16 (
    .in0({32{1'b0}}), .in1({32{1'b0}}), .in2({32{1'b0}}), .in3({32{1'b0}}), .in4({32{1'b0}}),
    .in5({32{1'b0}}), .in6({32{1'b0}}), .in7(in_4), .in8(in_5), .in9(in_6), .in10(in_7), .in11(in_8),
    .in12(in_9), .in13(in_10), .in14(in_11), .in15(in_12), .in16({32{1'b0}}), .in17({32{1'b0}}),
    .in18({32{1'b0}}), .in19({32{1'b0}}), .in20({32{1'b0}}), .in21({32{1'b0}}), .in22({32{1'b0}}),
    .in23({32{1'b0}}), .in24({32{1'b0}}), .in25({32{1'b0}}), .in26({32{1'b0}}), .in27({32{1'b0}}),
    .in28({32{1'b0}}), .in29({32{1'b0}}), .in30({32{1'b0}}), .in31({32{1'b0}}), .out(out_28), .sel(out_40));
  Multiplexer #(.select(5), .width(32), .enable("false")) multiplexer_17 (
    .in0({32{1'b0}}), .in1({32{1'b0}}), .in2({32{1'b0}}), .in3({32{1'b0}}), .in4({32{1'b0}}),
    .in5({32{1'b0}}), .in6({32{1'b0}}), .in7({32{1'b0}}), .in8(in_4), .in9(in_5), .in10(in_6), .in11(in_7),
    .in12(in_8), .in13(in_9), .in14(in_10), .in15(in_11), .in16(in_12), .in17({32{1'b0}}), .in18({32{1'b0}}),
    .in19({32{1'b0}}), .in20({32{1'b0}}), .in21({32{1'b0}}), .in22({32{1'b0}}), .in23({32{1'b0}}),
    .in24({32{1'b0}}), .in25({32{1'b0}}), .in26({32{1'b0}}), .in27({32{1'b0}}), .in28({32{1'b0}}),
    .in29({32{1'b0}}), .in30({32{1'b0}}), .in31({32{1'b0}}), .out(out_29), .sel(out_40));
  Multiplexer #(.select(5), .width(32), .enable("false")) multiplexer_18 (
    .in0({32{1'b0}}), .in1({32{1'b0}}), .in2({32{1'b0}}), .in3({32{1'b0}}), .in4({32{1'b0}}),
    .in5({32{1'b0}}), .in6({32{1'b0}}), .in7({32{1'b0}}), .in8({32{1'b0}}), .in9(in_4), .in10(in_5),
    .in11(in_6), .in12(in_7), .in13(in_8), .in14(in_9), .in15(in_10), .in16(in_11), .in17(in_12),
    .in18({32{1'b0}}), .in19({32{1'b0}}), .in20({32{1'b0}}), .in21({32{1'b0}}), .in22({32{1'b0}}),
    .in23({32{1'b0}}), .in24({32{1'b0}}), .in25({32{1'b0}}), .in26({32{1'b0}}), .in27({32{1'b0}}),
    .in28({32{1'b0}}), .in29({32{1'b0}}), .in30({32{1'b0}}), .in31({32{1'b0}}), .out(out_30), .sel(out_40));
  Multiplexer #(.select(5), .width(32), .enable("false")) multiplexer_19 (
    .in0({32{1'b0}}), .in1({32{1'b0}}), .in2({32{1'b0}}), .in3({32{1'b0}}), .in4({32{1'b0}}),
    .in5({32{1'b0}}), .in6({32{1'b0}}), .in7({32{1'b0}}), .in8({32{1'b0}}), .in9({32{1'b0}}), .in10(in_4),
    .in11(in_5), .in12(in_6), .in13(in_7), .in14(in_8), .in15(in_9), .in16(in_10), .in17(in_11),
    .in18(in_12), .in19({32{1'b0}}), .in20({32{1'b0}}), .in21({32{1'b0}}), .in22({32{1'b0}}),
    .in23({32{1'b0}}), .in24({32{1'b0}}), .in25({32{1'b0}}), .in26({32{1'b0}}), .in27({32{1'b0}}),
    .in28({32{1'b0}}), .in29({32{1'b0}}), .in30({32{1'b0}}), .in31({32{1'b0}}), .out(out_31), .sel(out_40));
  Multiplexer #(.select(5), .width(32), .enable("false")) multiplexer_20 (
    .in0({32{1'b0}}), .in1({32{1'b0}}), .in2({32{1'b0}}), .in3({32{1'b0}}), .in4({32{1'b0}}),
    .in5({32{1'b0}}), .in6({32{1'b0}}), .in7({32{1'b0}}), .in8({32{1'b0}}), .in9({32{1'b0}}),
    .in10({32{1'b0}}), .in11(in_4), .in12(in_5), .in13(in_6), .in14(in_7), .in15(in_8), .in16(in_9),
    .in17(in_10), .in18(in_11), .in19(in_12), .in20({32{1'b0}}), .in21({32{1'b0}}), .in22({32{1'b0}}),
    .in23({32{1'b0}}), .in24({32{1'b0}}), .in25({32{1'b0}}), .in26({32{1'b0}}), .in27({32{1'b0}}),
    .in28({32{1'b0}}), .in29({32{1'b0}}), .in30({32{1'b0}}), .in31({32{1'b0}}), .out(out_32), .sel(out_40));
  Multiplexer #(.select(5), .width(32), .enable("false")) multiplexer_21 (
    .in0({32{1'b0}}), .in1({32{1'b0}}), .in2({32{1'b0}}), .in3({32{1'b0}}), .in4({32{1'b0}}),
    .in5({32{1'b0}}), .in6({32{1'b0}}), .in7({32{1'b0}}), .in8({32{1'b0}}), .in9({32{1'b0}}),
    .in10({32{1'b0}}), .in11({32{1'b0}}), .in12(in_4), .in13(in_5), .in14(in_6), .in15(in_7), .in16(in_8),
    .in17(in_9), .in18(in_10), .in19(in_11), .in20(in_12), .in21({32{1'b0}}), .in22({32{1'b0}}),
    .in23({32{1'b0}}), .in24({32{1'b0}}), .in25({32{1'b0}}), .in26({32{1'b0}}), .in27({32{1'b0}}),
    .in28({32{1'b0}}), .in29({32{1'b0}}), .in30({32{1'b0}}), .in31({32{1'b0}}), .out(out_33), .sel(out_40));
  Multiplexer #(.select(5), .width(32), .enable("false")) multiplexer_22 (
    .in0({32{1'b0}}), .in1({32{1'b0}}), .in2({32{1'b0}}), .in3({32{1'b0}}), .in4({32{1'b0}}),
    .in5({32{1'b0}}), .in6({32{1'b0}}), .in7({32{1'b0}}), .in8({32{1'b0}}), .in9({32{1'b0}}),
    .in10({32{1'b0}}), .in11({32{1'b0}}), .in12({32{1'b0}}), .in13(in_4), .in14(in_5), .in15(in_6),
    .in16(in_7), .in17(in_8), .in18(in_9), .in19(in_10), .in20(in_11), .in21(in_12), .in22({32{1'b0}}),
    .in23({32{1'b0}}), .in24({32{1'b0}}), .in25({32{1'b0}}), .in26({32{1'b0}}), .in27({32{1'b0}}),
    .in28({32{1'b0}}), .in29({32{1'b0}}), .in30({32{1'b0}}), .in31({32{1'b0}}), .out(out_34), .sel(out_40));
  Multiplexer #(.select(5), .width(32), .enable("false")) multiplexer_23 (
    .in0({32{1'b0}}), .in1({32{1'b0}}), .in2({32{1'b0}}), .in3({32{1'b0}}), .in4({32{1'b0}}),
    .in5({32{1'b0}}), .in6({32{1'b0}}), .in7({32{1'b0}}), .in8({32{1'b0}}), .in9({32{1'b0}}),
    .in10({32{1'b0}}), .in11({32{1'b0}}), .in12({32{1'b0}}), .in13({32{1'b0}}), .in14(in_4), .in15(in_5),
    .in16(in_6), .in17(in_7), .in18(in_8), .in19(in_9), .in20(in_10), .in21(in_11), .in22(in_12),
    .in23({32{1'b0}}), .in24({32{1'b0}}), .in25({32{1'b0}}), .in26({32{1'b0}}), .in27({32{1'b0}}),
    .in28({32{1'b0}}), .in29({32{1'b0}}), .in30({32{1'b0}}), .in31({32{1'b0}}), .out(out_35), .sel(out_40));
  Multiplexer #(.select(5), .width(32), .enable("false")) multiplexer_24 (
    .in0({32{1'b0}}), .in1({32{1'b0}}), .in2({32{1'b0}}), .in3({32{1'b0}}), .in4({32{1'b0}}),
    .in5({32{1'b0}}), .in6({32{1'b0}}), .in7({32{1'b0}}), .in8({32{1'b0}}), .in9({32{1'b0}}),
    .in10({32{1'b0}}), .in11({32{1'b0}}), .in12({32{1'b0}}), .in13({32{1'b0}}), .in14({32{1'b0}}),
    .in15(in_4), .in16(in_5), .in17(in_6), .in18(in_7), .in19(in_8), .in20(in_9), .in21(in_10), .in22(in_11),
    .in23(in_12), .in24({32{1'b0}}), .in25({32{1'b0}}), .in26({32{1'b0}}), .in27({32{1'b0}}),
    .in28({32{1'b0}}), .in29({32{1'b0}}), .in30({32{1'b0}}), .in31({32{1'b0}}), .out(out_36), .sel(out_40));
  Multiplexer #(.select(5), .width(32), .enable("false")) multiplexer_25 (
    .in0({32{1'b0}}), .in1({32{1'b0}}), .in2({32{1'b0}}), .in3({32{1'b0}}), .in4({32{1'b0}}),
    .in5({32{1'b0}}), .in6({32{1'b0}}), .in7({32{1'b0}}), .in8({32{1'b0}}), .in9({32{1'b0}}),
    .in10({32{1'b0}}), .in11({32{1'b0}}), .in12({32{1'b0}}), .in13({32{1'b0}}), .in14({32{1'b0}}),
    .in15({32{1'b0}}), .in16(in_4), .in17(in_5), .in18(in_6), .in19(in_7), .in20(in_8), .in21(in_9),
    .in22(in_10), .in23(in_11), .in24(in_12), .in25({32{1'b0}}), .in26({32{1'b0}}), .in27({32{1'b0}}),
    .in28({32{1'b0}}), .in29({32{1'b0}}), .in30({32{1'b0}}), .in31({32{1'b0}}), .out(out_37), .sel(out_40));
  Multiplexer #(.select(5), .width(32), .enable("false")) multiplexer_26 (
    .in0({32{1'b0}}), .in1({32{1'b0}}), .in2({32{1'b0}}), .in3({32{1'b0}}), .in4({32{1'b0}}),
    .in5({32{1'b0}}), .in6({32{1'b0}}), .in7({32{1'b0}}), .in8({32{1'b0}}), .in9({32{1'b0}}),
    .in10({32{1'b0}}), .in11({32{1'b0}}), .in12({32{1'b0}}), .in13({32{1'b0}}), .in14({32{1'b0}}),
    .in15({32{1'b0}}), .in16({32{1'b0}}), .in17(in_4), .in18(in_5), .in19(in_6), .in20(in_7), .in21(in_8),
    .in22(in_9), .in23(in_10), .in24(in_11), .in25(in_12), .in26({32{1'b0}}), .in27({32{1'b0}}),
    .in28({32{1'b0}}), .in29({32{1'b0}}), .in30({32{1'b0}}), .in31({32{1'b0}}), .out(out_38), .sel(out_40));
  Multiplexer #(.select(5), .width(32), .enable("false")) multiplexer_27 (
    .in0({32{1'b0}}), .in1({32{1'b0}}), .in2({32{1'b0}}), .in3({32{1'b0}}), .in4({32{1'b0}}),
    .in5({32{1'b0}}), .in6({32{1'b0}}), .in7({32{1'b0}}), .in8({32{1'b0}}), .in9({32{1'b0}}),
    .in10({32{1'b0}}), .in11({32{1'b0}}), .in12({32{1'b0}}), .in13({32{1'b0}}), .in14({32{1'b0}}),
    .in15({32{1'b0}}), .in16({32{1'b0}}), .in17({32{1'b0}}), .in18(in_4), .in19(in_5), .in20(in_6),
    .in21(in_7), .in22(in_8), .in23(in_9), .in24(in_10), .in25(in_11), .in26(in_12), .in27({32{1'b0}}),
    .in28({32{1'b0}}), .in29({32{1'b0}}), .in30({32{1'b0}}), .in31({32{1'b0}}), .out(out_39), .sel(out_40));
  DotMatrix #(.matrixcols(31), .matrixrows(32)) dotmatrix_1 (
    .col1(out_13), .col2(out_14), .col3(out_15), .col4(out_16), .col5(out_17), .col6(out_18), .col7(out_19),
    .col8(out_20), .col9(out_21), .col10(out_22), .col11(out_23), .col12(out_24), .col13(out_25),
    .col14(out_26), .col15(out_27), .col16(out_28), .col17(out_29), .col18(out_30), .col19(out_31),
    .col20(out_32), .col21(out_33), .col22(out_34), .col23(out_35), .col24(out_36), .col25(out_37),
    .col26(out_38), .col27(out_39));  // open: col0, col28, col29, col30
  assign bit_extender_1_out = {{1{1'b0}}, out_40};  // Bit_Extender bit_extender_1
  assign bit_extender_2_out = {{1{1'b0}}, out_40};  // Bit_Extender bit_extender_2
  and and_1 (and_1_out, or_1_out, not_1_out, in_3);
  or or_1 (or_1_out, comparator_1_gt, comparator_1_eq);
  not not_1 (not_1_out, comparator_2_eq);
  Comparator #(.width(6)) comparator_1 (
    .a(bit_extender_1_out), .b({6{1'b0}}), .gt(comparator_1_gt), .eq(comparator_1_eq));  // open: lt
  Comparator #(.width(6)) comparator_2 (.a(bit_extender_2_out), .b(6'b010010), .eq(comparator_2_eq));  // open: gt, lt
  or or_2 (or_2_out, in_1, in_2);
  not not_2 (not_2_out, in_1);
  Counter #(.width(5), .max('h1f)) counter_1 (
    .load(or_2_out), .D(5'b01001), .count(not_2_out), .Q(out_40), .clk(or_3_out));  // open: carry, clr
  or or_3 (or_3_out, or_4_out, in_1);
  or or_4 (or_4_out, and_1_out, and_2_out);
  or or_5 (or_5_out, comparator_3_eq, comparator_3_lt);
  assign bit_extender_3_out = {{1{1'b0}}, out_40};  // Bit_Extender bit_extender_3
  Comparator #(.width(6)) comparator_3 (
    .a(bit_extender_3_out), .b(6'b010010), .eq(comparator_3_eq), .lt(comparator_3_lt));  // open: gt
  assign bit_extender_4_out = {{1{1'b0}}, out_40};  // Bit_Extender bit_extender_4
  Comparator #(.width(6)) comparator_4 (.a(bit_extender_4_out), .b({6{1'b0}}), .eq(comparator_4_eq));  // open: gt, lt
  and and_2 (and_2_out, or_5_out, not_3_out, in_2);
  not not_3 (not_3_out, comparator_4_eq);

  // Other names for the same wires on the sheet: _1[31:0] = in_4; _2[31:0] = in_5; _3[31:0] = in_6; _4[31:0] = in_7;
  //   _5[31:0] = in_8; _6[31:0] = in_9; _7[31:0] = in_10; _8[31:0] = in_11; _9[31:0] = in_12; bas1[4:0] = out_40;
  //   start = in_1; tunnel = in_3; tunnel_t = in_2
endmodule

module thxh (
  input  in_1,
  input  in_2,
  output out_3
);

  wire clock_1_out, register_1_q;
  wire [7:0] random_1_out, register_2_q, register_3_q;

  Clock clock_1 (.out(clock_1_out));
  Random random_1 (.clk(clock_1_out), .next(register_1_q), .out(random_1_out));  // open: clr
  Register #(.width(1)) register_1 (.D(in_1), .Q(register_1_q), .clk(in_1), .clr(in_2));  // open: en
  Register register_2 (.D(random_1_out), .Q(register_2_q), .clk(clock_1_out), .clr(in_2));  // open: en
  Register register_3 (.D(register_2_q), .Q(register_3_q), .clk(clock_1_out), .clr(in_2));  // open: en
  Comparator #(.width(9)) comparator_1 (
    .a({1'b0, register_2_q}), .b({register_3_q, 1'b0}), .gt(out_3));  // open: eq, lt
endmodule
