// Logisim project niiio2.circ as structural Verilog: 6 circuits, main circuit main
module main (
);

  wire rest, start;
  wire [1:0] _1, _2;
  wire [3:0] n1_1_out_21, n1_1_out_21_2;
  wire [7:0] n1_1_out_20;
  wire [31:0] n1_1_out_5, n1_1_out_6, n1_1_out_7, n1_1_out_8, n1_1_out_9, n1_1_out_10, n1_1_out_11,
       n1_1_out_12, n1_1_out_13, n1_1_out_14, n1_1_out_15, n1_1_out_16, n1_1_out_17, n1_1_out_18,
       n1_1_out_19, undriven, undriven_2, undriven_3, undriven_4;

  Button button_1 ();  // open: out
  Joystick #(.bits(2)) joystick_1 (.x(_1), .y(_2));
  Button button_2 (.out(start));
  Button button_3 (.out(rest));
  DotMatrix #(.matrixcols(15), .matrixrows(32)) dotmatrix_1 (
    .col0(n1_1_out_19), .col1(n1_1_out_18), .col2(n1_1_out_17), .col3(n1_1_out_16), .col4(n1_1_out_15),
    .col5(n1_1_out_14), .col6(n1_1_out_13), .col7(n1_1_out_12), .col8(n1_1_out_11), .col9(undriven),
    .col10(undriven_2), .col11(undriven_3), .col12(undriven_4), .col13(n1_1_out_6), .col14(n1_1_out_5));
  _1 u_1_1 (
    .in_3(_1), .in_4(_2), .in_1(start), .in_2(rest), .out_19(n1_1_out_19), .out_18(n1_1_out_18),
    .out_17(n1_1_out_17), .out_16(n1_1_out_16), .out_15(n1_1_out_15), .out_14(n1_1_out_14),
    .out_13(n1_1_out_13), .out_12(n1_1_out_12), .out_11(n1_1_out_11), .out_10(n1_1_out_10),
    .out_9(n1_1_out_9), .out_8(n1_1_out_8), .out_7(n1_1_out_7), .out_6(n1_1_out_6), .out_5(n1_1_out_5),
    .out_21({n1_1_out_21_2, n1_1_out_21}), .out_20(n1_1_out_20));
  Hex_Digit_Display hex_digit_display_1 (.value(n1_1_out_20[3:0]));  // open: dp
  Hex_Digit_Display hex_digit_display_2 (.value(n1_1_out_20[7:4]));  // open: dp
  Hex_Digit_Display hex_digit_display_3 (.value(n1_1_out_21));  // open: dp
  Hex_Digit_Display hex_digit_display_4 (.value(n1_1_out_21_2));  // open: dp
endmodule

module bol (
  input  start,
  input  _0,
  input  [31:0] in_3,
  input  in_4,
  input  [31:0] in_5,
  input  [7:0] in_6,
  input  [31:0] in_7,
  input  [31:0] in_8,
  input  [31:0] in_9,
  input  [4:0] in_10,
  input  [31:0] in_11,
  input  [31:0] in_12,
  input  [31:0] in_13,
  input  [31:0] in_14,
  input  [31:0] in_15,
  input  [31:0] in_16,
  output [31:0] out_17,
  output [31:0] out_18,
  output [31:0] out_19,
  output [31:0] out_20,
  output [31:0] out_21,
  output [31:0] out_22,
  output [31:0] out_23,
  output [31:0] out_24,
  output [31:0] out_25,
  output [31:0] out_26,
  output [31:0] out_27
);

  wire and_1_out, and_2_out, and_3_out, clock_1_out, comparator_1_eq, decoder_1_out0, decoder_1_out1,
       decoder_1_out2, decoder_1_out3, decoder_1_out4, decoder_1_out5, decoder_1_out6, decoder_1_out7,
       decoder_1_out8, decoder_1_out9, decoder_1_out10, not_1_out, or_1_out, register_1_q, undriven_16;
  wire [3:0] bit_extender_1_out;
  wire [31:0] multiplexer_1_out, shift_register_1_q0, undriven, undriven_2, undriven_3, undriven_4,
       undriven_5, undriven_6, undriven_7, undriven_8, undriven_9, undriven_10, undriven_11, undriven_12,
       undriven_13, undriven_14, undriven_15, undriven_17, undriven_18, undriven_19, undriven_20,
       undriven_21, undriven_22, undriven_23, undriven_24, undriven_25, undriven_26, undriven_27;

  Multiplexer #(.select(5), .width(32), .enable("false")) multiplexer_1 (
    .in0(32'h10), .in1(32'h20), .in2(32'h40), .in3(32'h80), .in4(undriven), .in5(undriven_2),
    .in6(undriven_3), .in7(undriven_4), .in8(undriven_5), .in9(undriven_6), .in10(undriven_7),
    .in11(undriven_8), .in12(undriven_9), .in13(undriven_10), .in14(undriven_11), .in15(undriven_12),
    .in16(undriven_13), .in17(undriven_14), .in18(undriven_15), .out(multiplexer_1_out), .sel(in_10));  // open: in19, in20, in21, in22, in23, in24, in25, in26, in27, in28, in29, in30, in31
  Button button_1 ();  // open: out
  Register #(.width(1)) register_1 (.D(and_1_out), .Q(register_1_q), .clk(and_1_out), .clr(_0));  // open: en
  and and_1 (and_1_out, undriven_16, start);
  Shift_Register #(.length(32)) shift_register_1 (
    .shift(1'b1), .in(start), .clk(or_1_out), .clr(_0), .q0(shift_register_1_q0[0]),
    .q1(shift_register_1_q0[1]), .q2(shift_register_1_q0[2]), .q3(shift_register_1_q0[3]),
    .q4(shift_register_1_q0[4]), .q5(shift_register_1_q0[5]), .q6(shift_register_1_q0[6]),
    .q7(shift_register_1_q0[7]), .q8(shift_register_1_q0[8]), .q9(shift_register_1_q0[9]),
    .q10(shift_register_1_q0[10]), .q11(shift_register_1_q0[11]), .q12(shift_register_1_q0[12]),
    .q13(shift_register_1_q0[13]), .q14(shift_register_1_q0[14]), .q15(shift_register_1_q0[15]),
    .q16(shift_register_1_q0[16]), .q17(shift_register_1_q0[17]), .q18(shift_register_1_q0[18]),
    .q19(shift_register_1_q0[19]), .q20(shift_register_1_q0[20]), .q21(shift_register_1_q0[21]),
    .q22(shift_register_1_q0[22]), .q23(shift_register_1_q0[23]), .q24(shift_register_1_q0[24]),
    .q25(shift_register_1_q0[25]), .q26(shift_register_1_q0[26]), .q27(shift_register_1_q0[27]),
    .q28(shift_register_1_q0[28]), .q29(shift_register_1_q0[29]), .q30(shift_register_1_q0[30]),
    .q31(shift_register_1_q0[31]));  // open: out, load, d0, d1, d2, d3, d4, d5, d6, d7, d8, d9, d10, d11, d12, d13, d14, d15, d16, d17, d18, d19, d20, d21, d22, d23, d24, d25, d26, d27, d28, d29, d30, d31
  buf or_1 (or_1_out, in_4);  // OR_Gate
  and and_2 (and_2_out, and_3_out, not_1_out);
  and and_3 (and_3_out, register_1_q, clock_1_out);
  not not_1 (not_1_out, comparator_1_eq);
  Clock clock_1 (.out(clock_1_out));
  Comparator #(.width(32)) comparator_1 (.a(shift_register_1_q0), .eq(comparator_1_eq));  // open: b, gt, lt
  Multiplexer #(.width(32), .enable("false")) multiplexer_2 (
    .in0(in_3), .in1(undriven_22), .out(out_17), .sel(decoder_1_out0));
  Multiplexer #(.width(32), .enable("false")) multiplexer_3 (
    .in0(in_5), .in1(undriven_23), .out(out_18), .sel(decoder_1_out1));
  Multiplexer #(.width(32), .enable("false")) multiplexer_4 (
    .in0(in_7), .in1(undriven_17), .out(out_19), .sel(decoder_1_out2));
  Multiplexer #(.width(32), .enable("false")) multiplexer_5 (
    .in0(in_8), .in1(undriven_18), .out(out_20), .sel(decoder_1_out3));
  Multiplexer #(.width(32), .enable("false")) multiplexer_6 (
    .in0(in_9), .in1(undriven_24), .out(out_21), .sel(decoder_1_out4));
  Multiplexer #(.width(32), .enable("false")) multiplexer_7 (
    .in0(in_11), .in1(undriven_25), .out(out_22), .sel(decoder_1_out5));
  Multiplexer #(.width(32), .enable("false")) multiplexer_8 (
    .in0(in_12), .in1(undriven_19), .out(out_23), .sel(decoder_1_out6));
  Multiplexer #(.width(32), .enable("false")) multiplexer_9 (
    .in0(in_13), .in1(undriven_20), .out(out_24), .sel(decoder_1_out7));
  Multiplexer #(.width(32), .enable("false")) multiplexer_10 (
    .in0(in_14), .in1(undriven_26), .out(out_25), .sel(decoder_1_out8));
  Multiplexer #(.width(32), .enable("false")) multiplexer_11 (
    .in0(in_15), .in1(undriven_27), .out(out_26), .sel(decoder_1_out9));
  Multiplexer #(.width(32), .enable("false")) multiplexer_12 (
    .in0(in_16), .in1(undriven_21), .out(out_27), .sel(decoder_1_out10));
  Bit_Extender #(.out_width(4)) bit_extender_1 (.in(in_6), .out(bit_extender_1_out));
  Decoder #(.select(4), .enable("false")) decoder_1 (
    .out0(decoder_1_out0), .out1(decoder_1_out1), .out2(decoder_1_out2), .out3(decoder_1_out3),
    .out4(decoder_1_out4), .out5(decoder_1_out5), .out6(decoder_1_out6), .out7(decoder_1_out7),
    .out8(decoder_1_out8), .out9(decoder_1_out9), .out10(decoder_1_out10), .sel(bit_extender_1_out));  // open: out11, out12, out13, out14, out15

  // Other names for the same wires on the sheet: s = start
endmodule

module _1 (
  input  in_1,
  input  in_2,
  input  [1:0] in_3,
  input  [1:0] in_4,
  output [31:0] out_5,
  output [31:0] out_6,
  output [31:0] out_7,
  output [31:0] out_8,
  output [31:0] out_9,
  output [31:0] out_10,
  output [31:0] out_11,
  output [31:0] out_12,
  output [31:0] out_13,
  output [31:0] out_14,
  output [31:0] out_15,
  output [31:0] out_16,
  output [31:0] out_17,
  output [31:0] out_18,
  output [31:0] out_19,
  output [7:0] out_20,
  output [7:0] out_21
);

  wire and_1_out, and_2_out, and_3_out, and_4_out, and_5_out, and_6_out, and_7_out, and_8_out,
       comparator_1_eq, comparator_2_lt, comparator_3_eq, comparator_4_lt, d, m, not_1_out, not_2_out,
       not_3_out, not_4_out, or_1_out, or_2_out, or_3_out, or_4_out, or_5_out, or_6_out, or_7_out, or_8_out,
       or_9_out, or_10_out, register_1_q, tunnel, tunnel_t;
  wire [31:0] n2_1_out_6, n2_2_out_6, n2_3_out_6, n2_4_out_6, n2_5_out_6, n3_1_out_10, n3_1_out_11,
       n3_1_out_12, n3_1_out_13, n3_1_out_14, n3_1_out_15, n3_1_out_16, n3_1_out_17, n3_1_out_18,
       n3_1_out_19, n3_1_out_20, n3_1_out_21, n3_1_out_22, n3_1_out_23, n3_1_out_24;

  or or_1 (or_1_out, tunnel_t, tunnel);
  _2 u_2_1 (.in_1(32'hc), .in_2(tunnel_t), .out_6(n2_1_out_6), .in_4(or_1_out), .in_3(in_2), .in_5(in_1));
  _2 u_2_2 (.in_1(32'he), .in_2(tunnel_t), .out_6(n2_2_out_6), .in_4(or_1_out), .in_3(in_2), .in_5(in_1));
  _2 u_2_3 (.in_1(32'hf), .in_2(tunnel_t), .out_6(n2_3_out_6), .in_4(or_1_out), .in_3(in_2), .in_5(in_1));
  _2 u_2_4 (.in_1(32'he), .in_2(tunnel_t), .out_6(n2_4_out_6), .in_4(or_1_out), .in_3(in_2), .in_5(in_1));
  _2 u_2_5 (.in_1(32'hc), .in_2(tunnel_t), .out_6(n2_5_out_6), .in_4(or_1_out), .in_3(in_2), .in_5(in_1));
  j j_1 (.out_3(tunnel_t), .in_2(in_3), .out_4(tunnel), .in_1(in_4), .out_5(m), .out_6(d));
  Register #(.width(1)) register_1 (.D(in_2), .Q(register_1_q), .clk(in_2), .clr(in_1));  // open: en
  _3 u_3_1 (
    .in_1(n2_1_out_6), .in_2(n2_2_out_6), .in_3(n2_3_out_6), .in_4(n2_4_out_6), .in_5(n2_5_out_6), .in_6(m),
    .out_10(n3_1_out_10), .out_11(n3_1_out_11), .out_12(n3_1_out_12), .out_13(n3_1_out_13),
    .out_14(n3_1_out_14), .out_15(n3_1_out_15), .out_16(n3_1_out_16), .out_17(n3_1_out_17),
    .out_18(n3_1_out_18), .out_19(n3_1_out_19), .out_20(n3_1_out_20), .out_21(n3_1_out_21),
    .out_22(n3_1_out_22), .out_23(n3_1_out_23), .out_24(n3_1_out_24), .in_8(or_2_out), .in_7(in_2),
    .in_9(in_1));
  or or_2 (or_2_out, m, d);
  Multiplexer #(.width(32), .enable("false")) multiplexer_1 (
    .in0(n3_1_out_10), .in1({32{1'b0}}), .out(out_19), .sel(register_1_q));
  Multiplexer #(.width(32), .enable("false")) multiplexer_2 (
    .in0(n3_1_out_11), .in1({32{1'b0}}), .out(out_18), .sel(register_1_q));
  Multiplexer #(.width(32), .enable("false")) multiplexer_3 (
    .in0(n3_1_out_12), .in1({32{1'b0}}), .out(out_17), .sel(register_1_q));
  Multiplexer #(.width(32), .enable("false")) multiplexer_4 (
    .in0(n3_1_out_13), .in1({32{1'b0}}), .out(out_16), .sel(register_1_q));
  Multiplexer #(.width(32), .enable("false")) multiplexer_5 (
    .in0(n3_1_out_14), .in1({32{1'b0}}), .out(out_15), .sel(register_1_q));
  Multiplexer #(.width(32), .enable("false")) multiplexer_6 (
    .in0(n3_1_out_15), .in1({32{1'b0}}), .out(out_14), .sel(register_1_q));
  Multiplexer #(.width(32), .enable("false")) multiplexer_7 (
    .in0(n3_1_out_16), .in1({32{1'b0}}), .out(out_13), .sel(register_1_q));
  Multiplexer #(.width(32), .enable("false")) multiplexer_8 (
    .in0(n3_1_out_17), .in1({32{1'b0}}), .out(out_12), .sel(register_1_q));
  Multiplexer #(.width(32), .enable("false")) multiplexer_9 (
    .in0(n3_1_out_18), .in1({32{1'b0}}), .out(out_11), .sel(register_1_q));
  Multiplexer #(.width(32), .enable("false")) multiplexer_10 (
    .in0(n3_1_out_19), .in1({32{1'b0}}), .out(out_10), .sel(register_1_q));
  Multiplexer #(.width(32), .enable("false")) multiplexer_11 (
    .in0(n3_1_out_20), .in1({32{1'b0}}), .out(out_9), .sel(register_1_q));
  Multiplexer #(.width(32), .enable("false")) multiplexer_12 (
    .in0(n3_1_out_21), .in1({32{1'b0}}), .out(out_8), .sel(register_1_q));
  Multiplexer #(.width(32), .enable("false")) multiplexer_13 (
    .in0(n3_1_out_22), .in1({32{1'b0}}), .out(out_7), .sel(register_1_q));
  Multiplexer #(.width(32), .enable("false")) multiplexer_14 (
    .in0(n3_1_out_23), .in1({32{1'b0}}), .out(out_6), .sel(register_1_q));
  Multiplexer #(.width(32), .enable("false")) multiplexer_15 (
    .in0(n3_1_out_24), .in1({32{1'b0}}), .out(out_5), .sel(register_1_q));
  or or_3 (or_3_out, in_1, and_7_out);
  or or_4 (or_4_out, in_1, tunnel_t);
  Counter counter_1 (
    .load(or_4_out), .D(8'h9), .count(not_1_out), .Q(out_20), .clk(or_5_out), .clr(in_2));  // open: carry
  not not_1 (not_1_out, in_1);
  or or_5 (or_5_out, in_1, and_8_out);
  or or_6 (or_6_out, in_1, m);
  Counter counter_2 (
    .load(or_6_out), .D(8'h5), .count(not_2_out), .Q(out_21), .clk(or_3_out), .clr(in_2));  // open: carry
  not not_2 (not_2_out, in_1);
  Comparator comparator_1 (.a(out_20), .b(8'h3), .eq(comparator_1_eq));  // open: gt, lt
  Comparator comparator_2 (.a(out_20), .b(8'h13), .lt(comparator_2_lt));  // open: gt, eq
  or or_7 (or_7_out, tunnel, tunnel_t);
  and and_1 (and_1_out, tunnel_t, or_7_out);
  Comparator comparator_3 (.a(out_21), .b({8{1'b1}}), .eq(comparator_3_eq));  // open: gt, lt
  Comparator comparator_4 (.a(out_21), .b(8'ha), .lt(comparator_4_lt));  // open: gt, eq
  or or_8 (or_8_out, m, d);
  and and_2 (and_2_out, m, or_8_out);
  and and_3 (and_3_out, comparator_1_eq, tunnel_t);
  not not_3 (not_3_out, and_3_out);
  and and_4 (and_4_out, or_7_out, comparator_2_lt);
  and and_5 (and_5_out, comparator_3_eq, m);
  not not_4 (not_4_out, and_5_out);
  and and_6 (and_6_out, or_8_out, comparator_4_lt);
  or or_9 (or_9_out, and_4_out, and_1_out);
  and and_7 (and_7_out, not_4_out, or_10_out);
  or or_10 (or_10_out, and_6_out, and_2_out);
  and and_8 (and_8_out, not_3_out, or_9_out);

  // Other names for the same wires on the sheet: _1[1:0] = in_3; _2[1:0] = in_4; rest = in_2; start = in_1
endmodule

module j (
  input  [1:0] in_1,
  input  [1:0] in_2,
  output out_3,
  output out_4,
  output out_5,
  output out_6
);

  wire not_1_out, not_2_out;

  and and_1 (out_3, in_1[0], not_1_out);
  not not_1 (not_1_out, in_1[1]);
  and and_2 (out_5, not_2_out, in_2[0]);
  not not_2 (not_2_out, in_2[1]);
  and and_3 (out_6, in_2[1], in_2[0]);
  and and_4 (out_4, in_1[0], in_1[1]);
endmodule

module _2 (
  input  [31:0] in_1,
  input  in_2,
  input  in_3,
  input  in_4,
  input  in_5,
  output [31:0] out_6
);

  wire and_1_out, and_2_out, and_3_out, and_4_out, ckolk, comparator_1_eq, comparator_2_lt, not_1_out,
       not_2_out, or_1_out, or_2_out;
  wire [3:0] bit_extender_1_out;
  wire [4:0] counter_1_q;
  wire [31:0] multiplier_1_out, multiplier_2_out, multiplier_3_out, multiplier_4_out, multiplier_5_out,
       multiplier_6_out, multiplier_7_out, multiplier_8_out, multiplier_9_out, multiplier_10_out,
       multiplier_11_out, multiplier_12_out, multiplier_13_out, multiplier_14_out, multiplier_15_out,
       multiplier_16_out;

  Multiplier #(.width(32)) multiplier_1 (.a(in_1), .b(32'h10000000), .out(multiplier_1_out));  // open: cin, cout
  Multiplier #(.width(32)) multiplier_2 (.a(in_1), .b(32'h8000000), .out(multiplier_2_out));  // open: cin, cout
  Multiplier #(.width(32)) multiplier_3 (.a(in_1), .b(32'h4000000), .out(multiplier_3_out));  // open: cin, cout
  Multiplier #(.width(32)) multiplier_4 (.a(in_1), .b(32'h2000000), .out(multiplier_4_out));  // open: cin, cout
  Multiplier #(.width(32)) multiplier_5 (.a(in_1), .b(32'h1000000), .out(multiplier_5_out));  // open: cin, cout
  Multiplier #(.width(32)) multiplier_6 (.a(in_1), .b(32'h800000), .out(multiplier_6_out));  // open: cin, cout
  Multiplier #(.width(32)) multiplier_7 (.a(in_1), .b(32'h400000), .out(multiplier_7_out));  // open: cin, cout
  Multiplier #(.width(32)) multiplier_8 (.a(in_1), .b(32'h200000), .out(multiplier_8_out));  // open: cin, cout
  Multiplier #(.width(32)) multiplier_9 (.a(in_1), .b(32'h100000), .out(multiplier_9_out));  // open: cin, cout
  Multiplier #(.width(32)) multiplier_10 (.a(in_1), .b(32'h80000), .out(multiplier_10_out));  // open: cin, cout
  Multiplier #(.width(32)) multiplier_11 (.a(in_1), .b(32'h40000), .out(multiplier_11_out));  // open: cin, cout
  Multiplier #(.width(32)) multiplier_12 (.a(in_1), .b(32'h20000), .out(multiplier_12_out));  // open: cin, cout
  Multiplier #(.width(32)) multiplier_13 (.a(in_1), .b(32'h10000), .out(multiplier_13_out));  // open: cin, cout
  Multiplier #(.width(32)) multiplier_14 (.a(in_1), .b(32'h8000), .out(multiplier_14_out));  // open: cin, cout
  Multiplier #(.width(32)) multiplier_15 (.a(in_1), .b(32'h4000), .out(multiplier_15_out));  // open: cin, cout
  Multiplier #(.width(32)) multiplier_16 (.a(in_1), .b(32'h2000), .out(multiplier_16_out));  // open: cin, cout
  or or_1 (or_1_out, in_5, in_2);
  Counter #(.width(5), .max('h1f)) counter_1 (
    .load(or_1_out), .D(5'b00101), .count(not_1_out), .Q(counter_1_q), .clk(ckolk), .clr(in_3));  // open: carry
  not not_1 (not_1_out, in_5);
  Multiplexer #(.select(4), .width(32), .enable("false")) multiplexer_1 (
    .in0(multiplier_1_out), .in1(multiplier_2_out), .in2(multiplier_3_out), .in3(multiplier_4_out),
    .in4(multiplier_5_out), .in5(multiplier_6_out), .in6(multiplier_7_out), .in7(multiplier_8_out),
    .in8(multiplier_9_out), .in9(multiplier_10_out), .in10(multiplier_11_out), .in11(multiplier_12_out),
    .in12(multiplier_13_out), .in13(multiplier_14_out), .in14(multiplier_15_out), .in15(multiplier_16_out),
    .out(out_6), .sel(bit_extender_1_out));
  Bit_Extender #(.in_width(5), .out_width(4)) bit_extender_1 (.in(counter_1_q), .out(bit_extender_1_out));
  Comparator #(.width(5)) comparator_1 (.a(counter_1_q), .b({5{1'b0}}), .eq(comparator_1_eq));  // open: gt, lt
  Comparator #(.width(5)) comparator_2 (.a(counter_1_q), .b(5'b01111), .lt(comparator_2_lt));  // open: gt, eq
  and and_1 (and_1_out, in_4, comparator_2_lt);
  and and_2 (and_2_out, or_1_out, in_4);
  and and_3 (and_3_out, comparator_1_eq, or_1_out);
  not not_2 (not_2_out, and_3_out);
  or or_2 (or_2_out, and_1_out, and_2_out);
  and and_4 (and_4_out, not_2_out, or_2_out);
  or or_3 (ckolk, and_4_out, in_5);

  // Other names for the same wires on the sheet: start = in_5
endmodule

module _3 (
  input  [31:0] in_1,
  input  [31:0] in_2,
  input  [31:0] in_3,
  input  [31:0] in_4,
  input  [31:0] in_5,
  input  in_6,
  input  in_7,
  input  in_8,
  input  in_9,
  output [31:0] out_10,
  output [31:0] out_11,
  output [31:0] out_12,
  output [31:0] out_13,
  output [31:0] out_14,
  output [31:0] out_15,
  output [31:0] out_16,
  output [31:0] out_17,
  output [31:0] out_18,
  output [31:0] out_19,
  output [31:0] out_20,
  output [31:0] out_21,
  output [31:0] out_22,
  output [31:0] out_23,
  output [31:0] out_24
);

  wire and_1_out, and_2_out, and_3_out, and_4_out, comparator_1_eq, comparator_2_lt, not_1_out, not_2_out,
       or_1_out, or_2_out, or_3_out;
  wire [3:0] bit_extender_1_out;
  wire [4:0] counter_1_q;

  or or_1 (or_1_out, in_9, in_6);
  not not_1 (not_1_out, in_9);
  or or_2 (or_2_out, and_1_out, in_9);
  Counter #(.width(5), .max('h1f)) counter_1 (
    .load(or_1_out), .D(5'b00101), .count(not_1_out), .Q(counter_1_q), .clk(or_2_out), .clr(in_7));  // open: carry
  and and_1 (and_1_out, not_2_out, or_3_out);
  or or_3 (or_3_out, and_4_out, and_3_out);
  Comparator #(.width(5)) comparator_1 (.a(counter_1_q), .b({5{1'b0}}), .eq(comparator_1_eq));  // open: gt, lt
  Comparator #(.width(5)) comparator_2 (.a(counter_1_q), .b(5'b01010), .lt(comparator_2_lt));  // open: gt, eq
  Multiplexer #(.select(4), .width(32), .enable("false")) multiplexer_1 (
    .in0(in_1), .in1({32{1'b0}}), .in2({32{1'b0}}), .in3({32{1'b0}}), .in4({32{1'b0}}), .in5({32{1'b0}}),
    .in6({32{1'b0}}), .in7({32{1'b0}}), .in8({32{1'b0}}), .in9({32{1'b0}}), .in10({32{1'b0}}),
    .in11({32{1'b0}}), .in12({32{1'b0}}), .in13({32{1'b0}}), .in14({32{1'b0}}), .in15({32{1'b0}}),
    .out(out_10), .sel(bit_extender_1_out));
  Multiplexer #(.select(4), .width(32), .enable("false")) multiplexer_2 (
    .in0(in_2), .in1(in_1), .in2({32{1'b0}}), .in3({32{1'b0}}), .in4({32{1'b0}}), .in5({32{1'b0}}),
    .in6({32{1'b0}}), .in7({32{1'b0}}), .in8({32{1'b0}}), .in9({32{1'b0}}), .in10({32{1'b0}}),
    .in11({32{1'b0}}), .in12({32{1'b0}}), .in13({32{1'b0}}), .in14({32{1'b0}}), .in15({32{1'b0}}),
    .out(out_11), .sel(bit_extender_1_out));
  Multiplexer #(.select(4), .width(32), .enable("false")) multiplexer_3 (
    .in0(in_3), .in1(in_2), .in2(in_1), .in3({32{1'b0}}), .in4({32{1'b0}}), .in5({32{1'b0}}),
    .in6({32{1'b0}}), .in7({32{1'b0}}), .in8({32{1'b0}}), .in9({32{1'b0}}), .in10({32{1'b0}}),
    .in11({32{1'b0}}), .in12({32{1'b0}}), .in13({32{1'b0}}), .in14({32{1'b0}}), .in15({32{1'b0}}),
    .out(out_12), .sel(bit_extender_1_out));
  Multiplexer #(.select(4), .width(32), .enable("false")) multiplexer_4 (
    .in0(in_4), .in1(in_3), .in2(in_2), .in3(in_1), .in4({32{1'b0}}), .in5({32{1'b0}}), .in6({32{1'b0}}),
    .in7({32{1'b0}}), .in8({32{1'b0}}), .in9({32{1'b0}}), .in10({32{1'b0}}), .in11({32{1'b0}}),
    .in12({32{1'b0}}), .in13({32{1'b0}}), .in14({32{1'b0}}), .in15({32{1'b0}}), .out(out_13),
    .sel(bit_extender_1_out));
  Multiplexer #(.select(4), .width(32), .enable("false")) multiplexer_5 (
    .in0(in_5), .in1(in_4), .in2(in_3), .in3(in_2), .in4(in_1), .in5({32{1'b0}}), .in6({32{1'b0}}),
    .in7({32{1'b0}}), .in8({32{1'b0}}), .in9({32{1'b0}}), .in10({32{1'b0}}), .in11({32{1'b0}}),
    .in12({32{1'b0}}), .in13({32{1'b0}}), .in14({32{1'b0}}), .in15({32{1'b0}}), .out(out_14),
    .sel(bit_extender_1_out));
  Multiplexer #(.select(4), .width(32), .enable("false")) multiplexer_6 (
    .in0({32{1'b0}}), .in1(in_5), .in2(in_4), .in3(in_3), .in4(in_2), .in5(in_1), .in6({32{1'b0}}),
    .in7({32{1'b0}}), .in8({32{1'b0}}), .in9({32{1'b0}}), .in10({32{1'b0}}), .in11({32{1'b0}}),
    .in12({32{1'b0}}), .in13({32{1'b0}}), .in14({32{1'b0}}), .in15({32{1'b0}}), .out(out_15),
    .sel(bit_extender_1_out));
  Multiplexer #(.select(4), .width(32), .enable("false")) multiplexer_7 (
    .in0({32{1'b0}}), .in1({32{1'b0}}), .in2(in_5), .in3(in_4), .in4(in_3), .in5(in_2), .in6(in_1),
    .in7({32{1'b0}}), .in8({32{1'b0}}), .in9({32{1'b0}}), .in10({32{1'b0}}), .in11({32{1'b0}}),
    .in12({32{1'b0}}), .in13({32{1'b0}}), .in14({32{1'b0}}), .in15({32{1'b0}}), .out(out_16),
    .sel(bit_extender_1_out));
  Multiplexer #(.select(4), .width(32), .enable("false")) multiplexer_8 (
    .in0({32{1'b0}}), .in1({32{1'b0}}), .in2({32{1'b0}}), .in3(in_5), .in4(in_4), .in5(in_3), .in6(in_2),
    .in7(in_1), .in8({32{1'b0}}), .in9({32{1'b0}}), .in10({32{1'b0}}), .in11({32{1'b0}}), .in12({32{1'b0}}),
    .in13({32{1'b0}}), .in14({32{1'b0}}), .in15({32{1'b0}}), .out(out_17), .sel(bit_extender_1_out));
  Multiplexer #(.select(4), .width(32), .enable("false")) multiplexer_9 (
    .in0({32{1'b0}}), .in1({32{1'b0}}), .in2({32{1'b0}}), .in3({32{1'b0}}), .in4(in_5), .in5(in_4),
    .in6(in_3), .in7(in_2), .in8(in_1), .in9({32{1'b0}}), .in10({32{1'b0}}), .in11({32{1'b0}}),
    .in12({32{1'b0}}), .in13({32{1'b0}}), .in14({32{1'b0}}), .in15({32{1'b0}}), .out(out_18),
    .sel(bit_extender_1_out));
  Multiplexer #(.select(4), .width(32), .enable("false")) multiplexer_10 (
    .in0({32{1'b0}}), .in1({32{1'b0}}), .in2({32{1'b0}}), .in3({32{1'b0}}), .in4({32{1'b0}}), .in5(in_5),
    .in6(in_4), .in7(in_3), .in8(in_2), .in9(in_1), .in10({32{1'b0}}), .in11({32{1'b0}}), .in12({32{1'b0}}),
    .in13({32{1'b0}}), .in14({32{1'b0}}), .in15({32{1'b0}}), .out(out_19), .sel(bit_extender_1_out));
  Multiplexer #(.select(4), .width(32), .enable("false")) multiplexer_11 (
    .in0({32{1'b0}}), .in1({32{1'b0}}), .in2({32{1'b0}}), .in3({32{1'b0}}), .in4({32{1'b0}}),
    .in5({32{1'b0}}), .in6(in_5), .in7(in_4), .in8(in_3), .in9(in_2), .in10(in_1), .in11({32{1'b0}}),
    .in12({32{1'b0}}), .in13({32{1'b0}}), .in14({32{1'b0}}), .in15({32{1'b0}}), .out(out_20),
    .sel(bit_extender_1_out));
  Multiplexer #(.select(4), .width(32), .enable("false")) multiplexer_12 (
    .in0({32{1'b0}}), .in1({32{1'b0}}), .in2({32{1'b0}}), .in3({32{1'b0}}), .in4({32{1'b0}}),
    .in5({32{1'b0}}), .in6({32{1'b0}}), .in7(in_5), .in8(in_4), .in9(in_3), .in10(in_2), .in11(in_1),
    .in12({32{1'b0}}), .in13({32{1'b0}}), .in14({32{1'b0}}), .in15({32{1'b0}}), .out(out_21),
    .sel(bit_extender_1_out));
  Multiplexer #(.select(4), .width(32), .enable("false")) multiplexer_13 (
    .in0({32{1'b0}}), .in1({32{1'b0}}), .in2({32{1'b0}}), .in3({32{1'b0}}), .in4({32{1'b0}}),
    .in5({32{1'b0}}), .in6({32{1'b0}}), .in7({32{1'b0}}), .in8(in_5), .in9(in_4), .in10(in_3), .in11(in_2),
    .in12(in_1), .in13({32{1'b0}}), .in14({32{1'b0}}), .in15({32{1'b0}}), .out(out_22),
    .sel(bit_extender_1_out));
  Multiplexer #(.select(4), .width(32), .enable("false")) multiplexer_14 (
    .in0({32{1'b0}}), .in1({32{1'b0}}), .in2({32{1'b0}}), .in3({32{1'b0}}), .in4({32{1'b0}}),
    .in5({32{1'b0}}), .in6({32{1'b0}}), .in7({32{1'b0}}), .in8({32{1'b0}}), .in9(in_5), .in10(in_4),
    .in11(in_3), .in12(in_2), .in13(in_1), .in14({32{1'b0}}), .in15({32{1'b0}}), .out(out_23),
    .sel(bit_extender_1_out));
  Multiplexer #(.select(4), .width(32), .enable("false")) multiplexer_15 (
    .in0({32{1'b0}}), .in1({32{1'b0}}), .in2({32{1'b0}}), .in3({32{1'b0}}), .in4({32{1'b0}}),
    .in5({32{1'b0}}), .in6({32{1'b0}}), .in7({32{1'b0}}), .in8({32{1'b0}}), .in9({32{1'b0}}), .in10(in_5),
    .in11(in_4), .in12(in_3), .in13(in_2), .in14(in_1), .in15({32{1'b0}}), .out(out_24),
    .sel(bit_extender_1_out));
  Bit_Extender #(.in_width(5), .out_width(4)) bit_extender_1 (.in(counter_1_q), .out(bit_extender_1_out));
  and and_2 (and_2_out, comparator_1_eq, or_1_out);
  and and_3 (and_3_out, comparator_2_lt, in_8);
  and and_4 (and_4_out, in_8, or_1_out);
  not not_2 (not_2_out, and_2_out);

  // Other names for the same wires on the sheet: _1[31:0] = in_1; _2[31:0] = in_2; _3[31:0] = in_3; _4[31:0] = in_4;
  //   _5[31:0] = in_5; start = in_9
endmodule
