// Logisim project 1.circ as structural Verilog: 14 circuits, main circuit main
module fa (
  input  in_1
);

  wire clock_1_out, clock_2_out, clock_3_out, keyboard_1_avail;
  wire [6:0] keyboard_1_data, main_1_out_4, main_1_out_5;

  Clock clock_1 (.out(clock_1_out));
  Keyboard keyboard_1 (.clk(clock_1_out), .avail(keyboard_1_avail), .data(keyboard_1_data));  // open: re, clr
  main main_1 (
    .in_1(keyboard_1_data), .in_2(keyboard_1_avail), .out_4(main_1_out_4), .out_5(main_1_out_5), .in_3(in_1));
  TTY #(.rows(20)) tty_1 (.data(main_1_out_4), .clk(clock_2_out), .clr(in_1));  // open: we
  Clock clock_2 (.out(clock_2_out));
  Clock clock_3 (.out(clock_3_out));
  TTY #(.rows(48), .cols(38)) tty_2 (.data(main_1_out_5), .clk(clock_3_out), .clr(in_1));  // open: we
endmodule

module main (
  input  [6:0] in_1,
  input  in_2,
  input  in_3,
  output [6:0] out_4,
  output [6:0] out_5
);

  wire adder_1_out, and_1_out, and_2_out, and_3_out, and_4_out, and_5_out, clock_1_out, clock_2_out,
       clock_3_out, clock_4_out, clock_5_out, comparator_1_eq, comparator_2_eq, comparator_2_gt,
       comparator_2_lt, controlled_buffer_1_out, n2_1_out_5, n2_2_out_5, not_1_out, not_2_out, not_3_out,
       not_4_out, not_5_out, not_6_out, not_7_out, not_8_out, or_1_out, or_2_out, or_3_out, or_4_out,
       or_5_out, or_6_out, or_7_out, register_1_q, register_2_q, register_3_q, register_4_q, register_5_q,
       register_6_q, register_7_q, register_8_q, register_9_q, s_1_out_5, \μηνημα_λαθος_ψ_out ;
  wire [1:0] s_1_out_2, s_1_out_3;
  wire [2:0] n00_1_out_3, n6_1_out_3;
  wire [6:0] ent_1_out_1, multiplexer_1_out, n0_1_out_5, n0_2_out_5, n0_2_out_6, n2_1_out_4, n2_2_out_4,
       n30_1_out_2, n30_2_out_2, part_1_out_1, part_2_out_1, part_3_out_1, ram_1_data, ram_2_data,
       ram_3_data, ram_4_data, x_1_out_1, y_1_out_1;
  wire [9:0] bit_extender_1_out, multiplier_1_out, n0_3_out_3;

  s s_1 (
    .in_1(in_1), .out_6(s_1_out_2[1]), .out_4(s_1_out_3[1]), .out_5(s_1_out_5), .out_2(s_1_out_2[0]),
    .out_3(s_1_out_3[0]));
  or or_1 (or_1_out, s_1_out_2[1], s_1_out_2[0]);
  _2 u_2_1 (.out_4(n2_1_out_4), .out_5(n2_1_out_5), .in_2(s_1_out_2), .in_3(or_1_out), .in_1(in_3));
  Register #(.width(1)) register_1 (.D(s_1_out_5), .Q(register_1_q), .clk(s_1_out_5), .clr(in_3));  // open: en
  or or_2 (or_2_out, s_1_out_3[0], s_1_out_2[0], s_1_out_5, s_1_out_3[1], s_1_out_2[1]);
  or or_3 (or_3_out, s_1_out_3[1], s_1_out_3[0]);
  _2 u_2_2 (.out_4(n2_2_out_4), .out_5(n2_2_out_5), .in_2(s_1_out_3), .in_3(or_3_out), .in_1(in_3));
  not not_1 (not_1_out, or_2_out);
  and \u_μηνημα_λαθος_ψ  (\μηνημα_λαθος_ψ_out , in_2, not_1_out);
  or or_4 (or_4_out, n2_2_out_5, n2_1_out_5);
  _30 u_30_1 (.in_1(n2_2_out_4), .out_2(n30_1_out_2));
  _30 u_30_2 (.in_1(n2_1_out_4), .out_2(n30_2_out_2));
  and and_1 (and_1_out, 1'b1, 1'b1, 1'b1, n00_1_out_3[0], n00_1_out_3[1], n00_1_out_3[2]);
  or or_5 (or_5_out, in_2, and_1_out);
  _0 u_0_1 (.out_5(n0_1_out_5), .in_3(or_5_out), .in_2(or_6_out), .in_1(s_1_out_5), .in_4(in_3));  // open: out_6
  or or_6 (or_6_out, s_1_out_5, in_3);
  _0 u_0_2 (.out_5(n0_2_out_5), .in_3(or_5_out), .in_2(or_6_out), .in_1(s_1_out_5), .out_6(n0_2_out_6), .in_4(in_3));
  Clock clock_1 (.out(clock_1_out));
  not not_2 (not_2_out, register_1_q);
  RAM #(.addrWidth(7), .dataWidth(7), .bus("separate")) ram_1 (
    .addr(n0_1_out_5), .din(n30_1_out_2), .data(ram_1_data), .str(not_2_out), .sel(1'b1), .clk(clock_1_out),
    .ld(1'b1), .clr(in_3));
  RAM #(.addrWidth(7), .dataWidth(7), .bus("separate")) ram_2 (
    .addr(n0_2_out_5), .din(n30_2_out_2), .data(ram_2_data), .str(not_2_out), .sel(1'b1), .clk(clock_1_out),
    .ld(1'b1), .clr(in_3));
  X x_1 (.out_1(x_1_out_1));
  circuit part_1 (.out_1(part_1_out_1));
  circuit_2 part_2 (.out_1(part_2_out_1));
  Y y_1 (.out_1(y_1_out_1));
  circuit part_3 (.out_1(part_3_out_1));
  ent ent_1 (.out_1(ent_1_out_1));
  Register #(.width(1)) register_2 (.D(register_1_q), .Q(register_2_q), .clk(register_1_q), .clr(in_3));  // open: en
  Clock clock_2 (.out(clock_2_out));
  and and_2 (and_2_out, register_2_q, clock_2_out);
  assign controlled_buffer_1_out = in_3 ? in_3 : 1'bz;  // Controlled_Buffer controlled_buffer_1
  _00 u_00_1 (.in_1(and_2_out), .out_3(n00_1_out_3), .in_2(in_3));
  Multiplexer #(.select(3), .width(7), .enable("false")) multiplexer_1 (
    .in0(x_1_out_1), .in1(part_1_out_1), .in2(ram_1_data), .in3(part_2_out_1), .in4(y_1_out_1),
    .in5(part_3_out_1), .in6(ram_2_data), .in7(ent_1_out_1), .out(multiplexer_1_out), .sel(n00_1_out_3));
  assign bit_extender_1_out = {{3{1'b0}}, n0_2_out_6};  // Bit_Extender bit_extender_1
  _0_2 u_0_3 (.out_3(n0_3_out_3), .in_1(and_2_out), .in_2(controlled_buffer_1_out));
  assign controlled_buffer_1_out = comparator_2_gt ? comparator_2_gt : 1'bz;  // Controlled_Buffer controlled_buffer_2
  Multiplier #(.width(10)) multiplier_1 (.a(10'h8), .b(bit_extender_1_out), .out(multiplier_1_out));  // open: cin, cout
  Register #(.width(1)) register_3 (.D(register_1_q), .Q(register_3_q), .clk(comparator_2_eq), .clr(in_3));  // open: en
  Comparator #(.width(10)) comparator_1 (.a(multiplier_1_out), .b(n0_3_out_3), .eq(comparator_1_eq));  // open: gt, lt
  assign controlled_buffer_1_out = and_4_out ? and_4_out : 1'bz;  // Controlled_Buffer controlled_buffer_3
  Comparator #(.width(10)) comparator_2 (
    .a(n0_3_out_3), .b(multiplier_1_out), .gt(comparator_2_gt), .eq(comparator_2_eq), .lt(comparator_2_lt));
  Register #(.width(1)) register_4 (
    .D(comparator_2_lt), .Q(register_4_q), .clk(comparator_2_lt), .clr(or_7_out));  // open: en
  or or_7 (or_7_out, register_5_q, in_3);
  and and_3 (and_3_out, comparator_2_eq, register_3_q);
  Register #(.width(1)) register_5 (.D(and_3_out), .Q(register_5_q), .clk(and_3_out), .clr(in_3));  // open: en
  Clock clock_3 (.out(clock_3_out));
  RAM #(.addrWidth(10), .dataWidth(7), .bus("separate")) ram_3 (
    .addr(n0_3_out_3), .din(multiplexer_1_out), .data(ram_3_data), .str(register_4_q), .clk(clock_3_out),
    .ld(1'b1), .clr(in_3));  // open: sel
  Adder #(.width(1)) adder_1 (.a(register_6_q), .b(comparator_1_eq), .out(adder_1_out), .cin(1'b1));  // open: cout
  Multiplexer #(.width(7), .enable("false")) multiplexer_2 (
    .in0(ram_3_data), .in1({7{1'b0}}), .out(out_5), .sel(and_4_out));
  Register #(.width(1), .trigger("falling")) register_6 (
    .D(adder_1_out), .Q(register_6_q), .clk(comparator_1_eq), .clr(in_3));  // open: en
  and and_4 (and_4_out, adder_1_out, register_8_q);
  Register #(.width(1)) register_7 (.D(1'b1), .Q(register_7_q), .clk(adder_1_out), .clr(in_3));  // open: en
  Register #(.width(1)) register_8 (.D(register_7_q), .Q(register_8_q), .clk(adder_1_out), .clr(in_3));  // open: en
  _6 u_6_1 (.in_2(\μηνημα_λαθος_ψ_out ), .out_3(n6_1_out_3), .in_1(and_5_out));
  and and_5 (and_5_out, not_5_out, not_6_out, not_7_out, not_3_out, not_4_out, not_8_out, ram_4_data[0]);
  not not_3 (not_3_out, ram_4_data[3]);
  not not_4 (not_4_out, ram_4_data[2]);
  not not_5 (not_5_out, ram_4_data[6]);
  not not_6 (not_6_out, ram_4_data[5]);
  not not_7 (not_7_out, ram_4_data[4]);
  not not_8 (not_8_out, ram_4_data[1]);
  RAM #(.addrWidth(3), .dataWidth(7), .bus("separate")) ram_4 (
    .addr(n6_1_out_3), .data(ram_4_data));  // open: din, str, sel, clk, ld, clr
  Multiplexer #(.width(7), .enable("false")) multiplexer_3 (
    .in0(in_1), .in1(ram_4_data), .out(out_4), .sel(register_9_q));
  Register #(.width(1)) register_9 (.D(or_4_out), .Q(register_9_q), .clk(or_4_out), .clr(and_5_out));  // open: en
  TTY #(.rows(20)) tty_1 (.data(out_4), .clk(clock_4_out), .clr(in_3));  // open: we
  Clock clock_4 (.out(clock_4_out));
  Clock clock_5 (.out(clock_5_out));
  TTY #(.rows(48), .cols(38)) tty_2 (.data(out_5), .clk(clock_5_out), .clr(in_3));  // open: we
endmodule

module _2 (
  input  in_1,
  input  [1:0] in_2,
  input  in_3,
  output [6:0] out_4,
  output out_5
);

  wire and_1_out, comparator_1_eq, comparator_1_gt, comparator_1_lt, comparator_2_eq, comparator_2_gt,
       or_1_out;
  wire [6:0] adder_1_out, multiplexer_1_out, subtractor_1_out;

  Adder #(.width(7)) adder_1 (.a(out_4), .b({7{1'b0}}), .out(adder_1_out), .cin(1'b1));  // open: cout
  Subtractor #(.width(7)) subtractor_1 (.a(out_4), .b({7{1'b0}}), .out(subtractor_1_out), .bin(1'b1));  // open: bout
  Register #(.width(7), .trigger("falling")) register_1 (
    .D(multiplexer_1_out), .en(and_1_out), .Q(out_4), .clk(in_3), .clr(in_1));
  Multiplexer #(.select(2), .width(7), .enable("false")) multiplexer_1 (
    .in0({7{1'b0}}), .in1(adder_1_out), .in2(subtractor_1_out), .in3({7{1'b0}}), .out(multiplexer_1_out),
    .sel(in_2));
  and and_1 (and_1_out, comparator_2_gt, or_1_out);
  Comparator #(.width(7)) comparator_1 (
    .a({7{1'b0}}), .b(multiplexer_1_out), .gt(comparator_1_gt), .eq(comparator_1_eq), .lt(comparator_1_lt));
  Comparator #(.width(7)) comparator_2 (
    .a(7'b0001011), .b(multiplexer_1_out), .gt(comparator_2_gt), .eq(comparator_2_eq));  // open: lt
  or or_1 (or_1_out, comparator_1_eq, comparator_1_lt);
  or or_2 (out_5, comparator_1_gt, comparator_2_eq);
endmodule

module _6 (
  input  in_1,
  input  in_2,
  output [2:0] out_3
);

  wire and_1_out, clock_1_out, comparator_1_eq, multiplexer_1_out, not_1_out, register_1_q;
  wire [2:0] adder_1_out;

  Register #(.width(1)) register_1 (.D(in_2), .Q(register_1_q), .clk(in_2), .clr(in_1));  // open: en
  Adder #(.width(3)) adder_1 (.a(out_3), .b(3'b000), .out(adder_1_out), .cin(1'b1));  // open: cout
  Register #(.width(3)) register_2 (.D(adder_1_out), .Q(out_3), .clk(multiplexer_1_out), .clr(in_1));  // open: en
  Multiplexer #(.enable("false")) multiplexer_1 (
    .in0(1'b0), .in1(and_1_out), .out(multiplexer_1_out), .sel(register_1_q));
  and and_1 (and_1_out, clock_1_out, not_1_out);
  Clock clock_1 (.out(clock_1_out));
  Comparator #(.width(3)) comparator_1 (.a(out_3), .b(3'b111), .eq(comparator_1_eq));  // open: gt, lt
  not not_1 (not_1_out, comparator_1_eq);
endmodule

module s (
  input  [6:0] in_1,
  output out_2,
  output out_3,
  output out_4,
  output out_5,
  output out_6
);

  wire not_1_out, not_2_out, not_3_out, not_4_out, not_5_out, not_6_out, not_7_out, not_8_out, not_9_out,
       not_10_out, not_11_out, not_12_out, not_13_out, not_14_out;
  wire [6:0] demultiplexer_1_out1, demultiplexer_1_out3, demultiplexer_1_out4, demultiplexer_1_out7,
       demultiplexer_2_out0, demultiplexer_2_out1;

  Demultiplexer #(.select(3), .width(7), .enable("false")) demultiplexer_1 (
    .out1(demultiplexer_1_out1), .out3(demultiplexer_1_out3), .out4(demultiplexer_1_out4),
    .out7(demultiplexer_1_out7), .in(in_1), .sel(in_1[2:0]));  // open: out0, out2, out5, out6
  not not_1 (not_1_out, demultiplexer_1_out7[3]);
  and w (out_2, demultiplexer_1_out7[6], demultiplexer_1_out7[5], demultiplexer_1_out7[4], not_1_out, demultiplexer_1_out7[2], demultiplexer_1_out7[1], demultiplexer_1_out7[0]);
  not not_2 (not_2_out, demultiplexer_1_out4[3]);
  not not_3 (not_3_out, demultiplexer_1_out4[1]);
  not not_4 (not_4_out, demultiplexer_1_out4[4]);
  and d (out_3, demultiplexer_1_out4[6], demultiplexer_1_out4[5], not_4_out, not_2_out, demultiplexer_1_out4[2], not_3_out, not_6_out);
  not not_5 (not_5_out, demultiplexer_1_out3[2]);
  not not_6 (not_6_out, demultiplexer_1_out4[0]);
  not not_7 (not_7_out, demultiplexer_1_out3[3]);
  and s (out_4, demultiplexer_1_out3[6], demultiplexer_1_out3[5], demultiplexer_1_out3[4], not_7_out, not_5_out, demultiplexer_1_out3[1], demultiplexer_1_out3[0]);
  Demultiplexer #(.width(7), .enable("false")) demultiplexer_2 (
    .out0(demultiplexer_2_out0), .out1(demultiplexer_2_out1), .in(demultiplexer_1_out1), .sel(in_1[4]));
  not not_8 (not_8_out, demultiplexer_2_out1[2]);
  not not_9 (not_9_out, demultiplexer_2_out1[3]);
  and q (out_5, demultiplexer_2_out1[6], demultiplexer_2_out1[5], demultiplexer_2_out1[4], not_9_out, not_8_out, not_11_out, demultiplexer_2_out1[0]);
  not not_10 (not_10_out, demultiplexer_2_out0[3]);
  not not_11 (not_11_out, demultiplexer_2_out1[1]);
  not not_12 (not_12_out, demultiplexer_2_out0[2]);
  not not_13 (not_13_out, demultiplexer_2_out0[4]);
  and a (out_6, demultiplexer_2_out0[6], demultiplexer_2_out0[5], not_13_out, not_10_out, not_12_out, not_14_out, demultiplexer_2_out0[0]);
  not not_14 (not_14_out, demultiplexer_2_out0[1]);
endmodule

module _30 (
  input  [6:0] in_1,
  output [6:0] out_2
);

  Adder #(.width(7)) adder_1 (.a(7'b0110000), .b(in_1), .out(out_2));  // open: cin, cout
endmodule

module _0 (
  input  in_1,
  input  in_2,
  input  in_3,
  input  in_4,
  output [6:0] out_5,
  output [6:0] out_6
);

  wire or_1_out;
  wire [6:0] adder_1_out;

  Adder #(.width(7)) adder_1 (.a(out_5), .b({7{1'b0}}), .out(adder_1_out), .cin(1'b1));  // open: cout
  Register #(.width(7), .trigger("falling")) register_1 (
    .D(adder_1_out), .Q(out_5), .clk(in_3), .clr(or_1_out));  // open: en
  or or_1 (or_1_out, in_2, in_4);
  Register #(.width(7)) register_2 (.D(out_5), .Q(out_6), .clk(in_1), .clr(in_4));  // open: en
endmodule

module _00 (
  input  in_1,
  input  in_2,
  output [2:0] out_3
);

  wire and_1_out, clock_1_out, register_1_q;
  wire [2:0] adder_1_out;

  Register #(.width(1)) register_1 (.D(in_1), .Q(register_1_q), .clk(in_1), .clr(in_2));  // open: en
  Register #(.width(3)) register_2 (.D(adder_1_out), .Q(out_3), .clk(and_1_out), .clr(in_2));  // open: en
  Adder #(.width(3)) adder_1 (.a(out_3), .b(3'b000), .out(adder_1_out), .cin(1'b1));  // open: cout
  and and_1 (and_1_out, register_1_q, clock_1_out);
  Clock clock_1 (.out(clock_1_out));
endmodule

module _0_2 (
  input  in_1,
  input  in_2,
  output [9:0] out_3
);

  wire [9:0] adder_1_out;

  Adder #(.width(10)) adder_1 (.a(out_3), .b({10{1'b0}}), .out(adder_1_out), .cin(1'b1));  // open: cout
  Register #(.width(10), .trigger("falling")) register_1 (
    .D(adder_1_out), .Q(out_3), .clk(in_1), .clr(in_2));  // open: en
endmodule

module X (
  output [6:0] out_1
);


  assign out_1 = 7'b1011000;
endmodule

module circuit (
  output [6:0] out_1
);


  assign out_1 = 7'b0111101;
endmodule

module circuit_2 (
  output [6:0] out_1
);


  assign out_1 = 7'b0101100;
endmodule

module Y (
  output [6:0] out_1
);


  assign out_1 = 7'b1011001;
endmodule

module ent (
  output [6:0] out_1
);


  assign out_1 = 7'b0001010;
endmodule
