// Logisim project a.circ as structural Verilog: 1 circuit, main circuit main
module main (
);

  DotMatrix #(.matrixcols(32), .matrixrows(8)) dotmatrix_1 (
    .col1(8'h19), .col3(8'h18), .col5(8'h17), .col7(8'h15), .col9(8'h14), .col11(8'h13), .col13(8'h12),
    .col15(8'h11), .col17(8'h10), .col19(8'hf), .col21(8'he), .col23(8'hd), .col25(8'hc), .col27(8'hb),
    .col29(8'ha), .col31(8'h9));  // open: col0, col2, col4, col6, col8, col10, col12, col14, col16, col18, col20, col22, col24, col26, col28, col30
  DotMatrix #(.matrixcols(32), .matrixrows(8)) dotmatrix_2 (
    .col1(8'h8), .col3(8'hf), .col5(8'he), .col7(8'hd), .col9(8'hc), .col11(8'hb), .col13(8'ha),
    .col15(8'h9), .col17(8'h8), .col19(8'h7), .col21(8'h6), .col23(8'h5), .col25(8'h4), .col27(8'h3),
    .col29(8'h2), .col31(8'h1));  // open: col0, col2, col4, col6, col8, col10, col12, col14, col16, col18, col20, col22, col24, col26, col28, col30
  DotMatrix #(.matrixcols(8), .matrixrows(8)) dotmatrix_3 ();  // open: col0, col1, col2, col3, col4, col5, col6, col7
endmodule
