// Logisim project n.circ as structural Verilog: 6 circuits, main circuit `1234567890-=~!@#$%^&*()_+ backspace
module _1234567890________________backspace (
  input  [6:0] in_1,
  output out_2,
  output out_3,
  output out_4,
  output out_5,
  output out_6,
  output out_7,
  output out_8,
  output out_9,
  output out_10,
  output out_11,
  output out_12,
  output out_13,
  output out_14,
  output out_15,
  output out_16,
  output out_17,
  output out_18,
  output out_19,
  output out_20,
  output out_21,
  output out_22,
  output out_23,
  output out_24,
  output out_25,
  output out_26,
  output out_27,
  output out_28
);

  wire not_1_out, not_2_out, not_3_out, not_4_out, not_5_out, not_6_out, not_7_out, not_8_out, not_9_out,
       not_10_out, not_11_out, not_12_out, not_13_out, not_14_out, not_15_out, not_16_out, not_17_out,
       not_18_out, not_19_out, not_20_out, not_21_out, not_22_out, not_23_out, not_24_out, not_25_out,
       not_26_out, not_27_out, not_28_out, not_29_out, not_30_out, not_31_out, not_32_out, not_33_out,
       not_34_out, not_35_out, not_36_out, not_37_out, not_38_out, not_39_out, not_40_out, not_41_out,
       not_42_out, not_43_out, not_44_out, not_45_out, not_46_out, not_47_out, not_48_out, not_49_out,
       not_50_out, not_51_out, not_52_out, not_53_out, not_54_out, not_55_out, not_56_out, not_57_out,
       not_58_out, not_59_out, not_60_out, not_61_out, not_62_out, not_63_out, not_64_out, not_65_out,
       not_66_out, not_67_out, not_68_out, not_69_out, not_70_out, not_71_out, not_72_out, not_73_out,
       not_74_out, not_75_out, not_76_out, not_77_out, not_78_out, not_79_out, not_80_out, not_81_out,
       not_82_out, not_83_out, not_84_out, not_85_out, not_86_out, not_87_out, not_88_out, not_89_out,
       not_90_out, not_91_out, not_92_out, not_93_out, not_94_out, not_95_out, not_96_out, not_97_out,
       not_98_out, not_99_out;

  and \and  (out_2, in_1[6], in_1[5], in_1[4], in_1[3], in_1[2], in_1[1], not_10_out);
  not not_1 (not_1_out, in_1[1]);
  not not_2 (not_2_out, in_1[4]);
  not not_3 (not_3_out, in_1[2]);
  not not_4 (not_4_out, in_1[3]);
  and and_2 (out_16, in_1[6], in_1[5], not_2_out, not_4_out, not_3_out, not_1_out, not_13_out);
  not not_5 (not_5_out, in_1[1]);
  not not_6 (not_6_out, in_1[3]);
  not not_7 (not_7_out, in_1[6]);
  not not_8 (not_8_out, in_1[4]);
  not not_9 (not_9_out, in_1[2]);
  not not_10 (not_10_out, in_1[0]);
  and and_3 (out_3, not_7_out, in_1[5], not_8_out, not_6_out, not_9_out, not_5_out, in_1[0]);
  not not_11 (not_11_out, in_1[1]);
  not not_12 (not_12_out, in_1[3]);
  not not_13 (not_13_out, in_1[0]);
  not not_14 (not_14_out, in_1[6]);
  not not_15 (not_15_out, in_1[2]);
  and _1 (out_17, not_14_out, in_1[5], in_1[4], not_12_out, not_15_out, not_11_out, in_1[0]);
  not not_16 (not_16_out, in_1[5]);
  not not_17 (not_17_out, in_1[1]);
  not not_18 (not_18_out, in_1[2]);
  not not_19 (not_19_out, in_1[4]);
  not not_20 (not_20_out, in_1[3]);
  and and_4 (out_4, in_1[6], not_16_out, not_19_out, not_20_out, not_18_out, not_17_out, not_28_out);
  not not_21 (not_21_out, in_1[6]);
  not not_22 (not_22_out, in_1[3]);
  not not_23 (not_23_out, in_1[2]);
  and _2 (out_18, not_21_out, in_1[5], in_1[4], not_22_out, not_23_out, in_1[1], not_30_out);
  not not_24 (not_24_out, in_1[3]);
  not not_25 (not_25_out, in_1[4]);
  not not_26 (not_26_out, in_1[2]);
  not not_27 (not_27_out, in_1[6]);
  not not_28 (not_28_out, in_1[0]);
  and and_5 (out_5, not_27_out, in_1[5], not_25_out, not_24_out, not_26_out, in_1[1], in_1[0]);
  not not_29 (not_29_out, in_1[2]);
  not not_30 (not_30_out, in_1[0]);
  not not_31 (not_31_out, in_1[3]);
  not not_32 (not_32_out, in_1[6]);
  and _3 (out_19, not_32_out, in_1[5], in_1[4], not_31_out, not_29_out, in_1[1], in_1[0]);
  not not_33 (not_33_out, in_1[4]);
  not not_34 (not_34_out, in_1[1]);
  not not_35 (not_35_out, in_1[6]);
  not not_36 (not_36_out, in_1[3]);
  and and_6 (out_6, not_35_out, in_1[5], not_33_out, not_36_out, in_1[2], not_34_out, not_41_out);
  not not_37 (not_37_out, in_1[1]);
  not not_38 (not_38_out, in_1[3]);
  not not_39 (not_39_out, in_1[6]);
  and _4 (out_20, not_39_out, in_1[5], in_1[4], not_38_out, in_1[2], not_37_out, not_46_out);
  not not_40 (not_40_out, in_1[6]);
  not not_41 (not_41_out, in_1[0]);
  not not_42 (not_42_out, in_1[1]);
  not not_43 (not_43_out, in_1[4]);
  not not_44 (not_44_out, in_1[3]);
  and and_7 (out_7, not_40_out, in_1[5], not_43_out, not_44_out, in_1[2], not_42_out, in_1[0]);
  not not_45 (not_45_out, in_1[3]);
  not not_46 (not_46_out, in_1[0]);
  not not_47 (not_47_out, in_1[1]);
  not not_48 (not_48_out, in_1[6]);
  and _5 (out_21, not_48_out, in_1[5], in_1[4], not_45_out, in_1[2], not_47_out, in_1[0]);
  not not_49 (not_49_out, in_1[5]);
  and and_8 (out_8, in_1[6], not_49_out, in_1[4], in_1[3], in_1[2], in_1[1], not_52_out);
  not not_50 (not_50_out, in_1[6]);
  not not_51 (not_51_out, in_1[3]);
  and _6 (out_22, not_50_out, in_1[5], in_1[4], not_51_out, in_1[2], in_1[1], not_58_out);
  not not_52 (not_52_out, in_1[0]);
  not not_53 (not_53_out, in_1[4]);
  not not_54 (not_54_out, in_1[3]);
  not not_55 (not_55_out, in_1[6]);
  and and_9 (out_9, not_55_out, in_1[5], not_53_out, not_54_out, in_1[2], in_1[1], not_59_out);
  not not_56 (not_56_out, in_1[6]);
  not not_57 (not_57_out, in_1[3]);
  not not_58 (not_58_out, in_1[0]);
  and _7 (out_23, not_56_out, in_1[5], in_1[4], not_57_out, in_1[2], in_1[1], in_1[0]);
  not not_59 (not_59_out, in_1[0]);
  not not_60 (not_60_out, in_1[6]);
  not not_61 (not_61_out, in_1[2]);
  not not_62 (not_62_out, in_1[4]);
  and and_10 (out_10, not_60_out, in_1[5], not_62_out, in_1[3], not_61_out, in_1[1], not_69_out);
  not not_63 (not_63_out, in_1[1]);
  not not_64 (not_64_out, in_1[2]);
  not not_65 (not_65_out, in_1[6]);
  and _8 (out_24, not_65_out, in_1[5], in_1[4], in_1[3], not_64_out, not_63_out, not_73_out);
  not not_66 (not_66_out, in_1[4]);
  not not_67 (not_67_out, in_1[6]);
  not not_68 (not_68_out, in_1[2]);
  not not_69 (not_69_out, in_1[0]);
  not not_70 (not_70_out, in_1[1]);
  and and_11 (out_11, not_67_out, in_1[5], not_66_out, in_1[3], not_68_out, not_70_out, not_75_out);
  not not_71 (not_71_out, in_1[2]);
  not not_72 (not_72_out, in_1[1]);
  not not_73 (not_73_out, in_1[0]);
  not not_74 (not_74_out, in_1[6]);
  and _9 (out_25, not_74_out, in_1[5], in_1[4], in_1[3], not_71_out, not_72_out, in_1[0]);
  not not_75 (not_75_out, in_1[0]);
  not not_76 (not_76_out, in_1[6]);
  not not_77 (not_77_out, in_1[4]);
  not not_78 (not_78_out, in_1[1]);
  not not_79 (not_79_out, in_1[2]);
  and and_12 (out_12, not_76_out, in_1[5], not_77_out, in_1[3], not_79_out, not_78_out, in_1[0]);
  not not_80 (not_80_out, in_1[3]);
  not not_81 (not_81_out, in_1[2]);
  not not_82 (not_82_out, in_1[6]);
  not not_83 (not_83_out, in_1[1]);
  and _0 (out_26, not_82_out, in_1[5], in_1[4], not_80_out, not_81_out, not_83_out, not_86_out);
  not not_84 (not_84_out, in_1[5]);
  and and_13 (out_13, in_1[6], not_84_out, in_1[4], in_1[3], in_1[2], in_1[1], in_1[0]);
  not not_85 (not_85_out, in_1[4]);
  not not_86 (not_86_out, in_1[0]);
  not not_87 (not_87_out, in_1[6]);
  not not_88 (not_88_out, in_1[1]);
  and and_14 (out_27, not_87_out, in_1[5], not_85_out, in_1[3], in_1[2], not_88_out, in_1[0]);
  not not_89 (not_89_out, in_1[6]);
  not not_90 (not_90_out, in_1[4]);
  not not_91 (not_91_out, in_1[2]);
  and and_15 (out_14, not_89_out, in_1[5], not_90_out, in_1[3], not_91_out, in_1[1], in_1[0]);
  not not_92 (not_92_out, in_1[1]);
  not not_93 (not_93_out, in_1[6]);
  and and_16 (out_28, not_93_out, in_1[5], in_1[4], in_1[3], in_1[2], not_92_out, in_1[0]);
  not not_94 (not_94_out, in_1[5]);
  not not_95 (not_95_out, in_1[6]);
  not not_96 (not_96_out, in_1[4]);
  not not_97 (not_97_out, in_1[0]);
  not not_98 (not_98_out, in_1[2]);
  not not_99 (not_99_out, in_1[1]);
  and backpace (out_15, not_95_out, not_94_out, not_96_out, in_1[3], not_98_out, not_99_out, not_97_out);
endmodule

module qwertyuiop____QWERYUIOP (
  input  [6:0] in_1,
  output out_2,
  output out_3,
  output out_4,
  output out_5,
  output out_6,
  output out_7,
  output out_8,
  output out_9,
  output out_10,
  output out_11,
  output out_12,
  output out_13,
  output out_14,
  output out_15,
  output out_16,
  output out_17
);

  wire E_2_out, e_out, I_2_out, i_out, not_1_out, not_2_out, not_3_out, not_4_out, not_5_out, not_6_out,
       not_7_out, not_8_out, not_9_out, not_10_out, not_11_out, not_12_out, not_13_out, not_14_out,
       not_15_out, not_16_out, not_17_out, not_18_out, not_19_out, not_20_out, not_21_out, not_22_out,
       not_23_out, not_24_out, not_25_out, not_26_out, not_27_out, not_28_out, not_29_out, not_30_out,
       not_31_out, not_32_out, not_33_out, not_34_out, not_35_out, not_36_out, not_37_out, not_38_out,
       not_39_out, not_40_out, not_41_out, not_42_out, not_43_out, not_44_out, not_45_out, not_46_out,
       not_47_out, not_48_out, not_49_out, not_50_out, not_51_out, not_52_out, not_53_out, not_54_out,
       not_55_out, not_56_out, not_57_out, not_58_out, not_59_out, not_60_out, not_61_out, not_62_out,
       not_63_out, not_64_out, not_65_out, not_66_out, not_67_out, not_68_out, not_69_out, not_70_out,
       not_71_out, O_2_out, o_out, P_2_out, p_out, q_2_out, q_out, R_2_out, r_out, T_2_out, t_out, U_2_out,
       u_out, W_2_out, w_out, Y_2_out, y_out;

  not not_1 (not_1_out, in_1[2]);
  not not_2 (not_2_out, in_1[1]);
  not not_3 (not_3_out, in_1[3]);
  and q (q_out, in_1[6], in_1[5], in_1[4], not_3_out, not_1_out, not_2_out, in_1[0]);
  not not_4 (not_4_out, in_1[5]);
  not not_5 (not_5_out, in_1[3]);
  not not_6 (not_6_out, in_1[2]);
  not not_7 (not_7_out, in_1[1]);
  and q_2 (q_2_out, in_1[6], not_4_out, in_1[4], not_5_out, not_6_out, not_7_out, in_1[0]);
  or or_1 (out_5, q_out, q_2_out);
  not not_8 (not_8_out, in_1[3]);
  and w (w_out, in_1[6], in_1[5], in_1[4], not_8_out, in_1[2], in_1[1], in_1[0]);
  not not_9 (not_9_out, in_1[5]);
  not not_10 (not_10_out, in_1[3]);
  and W_2 (W_2_out, in_1[6], not_9_out, in_1[4], not_10_out, in_1[2], in_1[1], in_1[0]);
  or or_2 (out_6, w_out, W_2_out);
  not not_11 (not_11_out, in_1[3]);
  not not_12 (not_12_out, in_1[1]);
  not not_13 (not_13_out, in_1[4]);
  and e (e_out, in_1[6], in_1[5], not_13_out, not_11_out, in_1[2], not_12_out, in_1[0]);
  not not_14 (not_14_out, in_1[3]);
  not not_15 (not_15_out, in_1[5]);
  not not_16 (not_16_out, in_1[4]);
  not not_17 (not_17_out, in_1[1]);
  and E_2 (E_2_out, in_1[6], not_15_out, not_16_out, not_14_out, in_1[2], not_17_out, in_1[0]);
  or or_3 (out_7, e_out, E_2_out);
  not not_18 (not_18_out, in_1[2]);
  not not_19 (not_19_out, in_1[3]);
  not not_20 (not_20_out, in_1[0]);
  and r (r_out, in_1[6], in_1[5], in_1[4], not_19_out, not_18_out, in_1[1], not_20_out);
  not not_21 (not_21_out, in_1[3]);
  not not_22 (not_22_out, in_1[0]);
  not not_23 (not_23_out, in_1[2]);
  not not_24 (not_24_out, in_1[5]);
  and R_2 (R_2_out, in_1[6], not_24_out, in_1[4], not_21_out, not_23_out, in_1[1], not_22_out);
  or or_4 (out_8, r_out, R_2_out);
  not not_25 (not_25_out, in_1[1]);
  not not_26 (not_26_out, in_1[0]);
  not not_27 (not_27_out, in_1[3]);
  and t (t_out, in_1[6], in_1[5], in_1[4], not_27_out, in_1[2], not_25_out, not_26_out);
  not not_28 (not_28_out, in_1[3]);
  not not_29 (not_29_out, in_1[5]);
  not not_30 (not_30_out, in_1[1]);
  not not_31 (not_31_out, in_1[0]);
  and T_2 (T_2_out, in_1[6], not_29_out, in_1[4], not_28_out, in_1[2], not_30_out, not_31_out);
  or or_5 (out_9, t_out, T_2_out);
  not not_32 (not_32_out, in_1[2]);
  not not_33 (not_33_out, in_1[1]);
  and y (y_out, in_1[6], in_1[5], in_1[4], in_1[3], not_32_out, not_33_out, in_1[0]);
  not not_34 (not_34_out, in_1[2]);
  not not_35 (not_35_out, in_1[1]);
  not not_36 (not_36_out, in_1[5]);
  and Y_2 (Y_2_out, in_1[6], not_36_out, in_1[4], in_1[3], not_34_out, not_35_out, in_1[0]);
  or or_6 (out_10, y_out, Y_2_out);
  not not_37 (not_37_out, in_1[1]);
  not not_38 (not_38_out, in_1[3]);
  and u (u_out, in_1[6], in_1[5], in_1[4], not_38_out, in_1[2], not_37_out, in_1[0]);
  not not_39 (not_39_out, in_1[1]);
  not not_40 (not_40_out, in_1[5]);
  not not_41 (not_41_out, in_1[3]);
  and U_2 (U_2_out, in_1[6], not_40_out, in_1[4], not_41_out, in_1[2], not_39_out, in_1[0]);
  or or_7 (out_11, u_out, U_2_out);
  not not_42 (not_42_out, in_1[1]);
  not not_43 (not_43_out, in_1[4]);
  not not_44 (not_44_out, in_1[2]);
  and i (i_out, in_1[6], in_1[5], not_43_out, in_1[3], not_44_out, not_42_out, in_1[0]);
  not not_45 (not_45_out, in_1[5]);
  not not_46 (not_46_out, in_1[1]);
  not not_47 (not_47_out, in_1[4]);
  not not_48 (not_48_out, in_1[2]);
  and I_2 (I_2_out, in_1[6], not_45_out, not_47_out, in_1[3], not_48_out, not_46_out, in_1[0]);
  or or_8 (out_12, i_out, I_2_out);
  not not_49 (not_49_out, in_1[4]);
  and o (o_out, in_1[6], in_1[5], not_49_out, in_1[3], in_1[2], in_1[1], in_1[0]);
  not not_50 (not_50_out, in_1[4]);
  not not_51 (not_51_out, in_1[5]);
  and O_2 (O_2_out, in_1[6], not_51_out, not_50_out, in_1[3], in_1[2], in_1[1], in_1[0]);
  or or_9 (out_13, o_out, O_2_out);
  not not_52 (not_52_out, in_1[1]);
  not not_53 (not_53_out, in_1[3]);
  not not_54 (not_54_out, in_1[2]);
  not not_55 (not_55_out, in_1[0]);
  and p (p_out, in_1[6], in_1[5], in_1[4], not_53_out, not_54_out, not_52_out, not_55_out);
  not not_56 (not_56_out, in_1[0]);
  not not_57 (not_57_out, in_1[5]);
  not not_58 (not_58_out, in_1[2]);
  not not_59 (not_59_out, in_1[1]);
  not not_60 (not_60_out, in_1[3]);
  and P_2 (P_2_out, in_1[6], not_57_out, in_1[4], not_60_out, not_58_out, not_59_out, not_56_out);
  or or_10 (out_14, p_out, P_2_out);
  not not_61 (not_61_out, in_1[5]);
  and \and  (out_2, in_1[6], not_61_out, in_1[4], in_1[3], not_62_out, in_1[1], in_1[0]);
  and and_2 (out_15, in_1[6], in_1[5], in_1[4], in_1[3], not_64_out, in_1[1], in_1[0]);
  not not_62 (not_62_out, in_1[2]);
  not not_63 (not_63_out, in_1[5]);
  and and_3 (out_3, in_1[6], not_63_out, in_1[4], in_1[3], in_1[2], not_66_out, in_1[0]);
  not not_64 (not_64_out, in_1[2]);
  and and_4 (out_16, in_1[6], in_1[5], in_1[4], in_1[3], in_1[2], not_67_out, in_1[0]);
  not not_65 (not_65_out, in_1[5]);
  not not_66 (not_66_out, in_1[1]);
  and and_5 (out_4, in_1[6], not_65_out, in_1[4], in_1[3], in_1[2], not_68_out, not_69_out);
  not not_67 (not_67_out, in_1[1]);
  and and_6 (out_17, in_1[6], in_1[5], in_1[4], in_1[3], in_1[2], not_70_out, not_71_out);
  not not_68 (not_68_out, in_1[1]);
  not not_69 (not_69_out, in_1[0]);
  not not_70 (not_70_out, in_1[1]);
  not not_71 (not_71_out, in_1[0]);
endmodule

module asdfghjkl___ASDFGHJKL____CAPS_LOCK__ENTER (
  input  [6:0] in_1,
  output out_2,
  output out_3,
  output out_4,
  output out_5,
  output out_6,
  output out_7,
  output out_8,
  output out_9,
  output out_10,
  output out_11,
  output out_12,
  output out_13,
  output out_14,
  output out_15
);

  wire A_2_out, a_out, D_2_out, d_out, F_2_out, f_out, G_2_out, g_out, H_2_out, h_out, J_2_out, j_out,
       K_2_out, k_out, L_2_out, l_out, not_1_out, not_2_out, not_3_out, not_4_out, not_5_out, not_6_out,
       not_7_out, not_8_out, not_9_out, not_10_out, not_11_out, not_12_out, not_13_out, not_14_out,
       not_15_out, not_16_out, not_17_out, not_18_out, not_19_out, not_20_out, not_21_out, not_22_out,
       not_23_out, not_24_out, not_25_out, not_26_out, not_27_out, not_28_out, not_29_out, not_30_out,
       not_31_out, not_32_out, not_33_out, not_34_out, not_35_out, not_36_out, not_37_out, not_38_out,
       not_39_out, not_40_out, not_41_out, not_42_out, not_43_out, not_44_out, not_45_out, not_46_out,
       not_47_out, not_48_out, not_49_out, not_50_out, not_51_out, not_52_out, not_53_out, not_54_out,
       not_55_out, not_56_out, not_57_out, not_58_out, not_59_out, not_60_out, not_61_out, not_62_out,
       not_63_out, not_64_out, not_65_out, not_66_out, not_67_out, not_68_out, not_69_out, not_70_out,
       not_71_out, not_72_out, not_73_out, not_74_out, not_75_out, not_76_out, not_77_out, not_78_out,
       not_79_out, not_80_out, not_81_out, S_2_out, s_out;

  not not_1 (not_1_out, in_1[4]);
  not not_2 (not_2_out, in_1[3]);
  not not_3 (not_3_out, in_1[1]);
  not not_4 (not_4_out, in_1[2]);
  and a (a_out, in_1[6], in_1[5], not_1_out, not_2_out, not_4_out, not_3_out, in_1[0]);
  not not_5 (not_5_out, in_1[3]);
  not not_6 (not_6_out, in_1[1]);
  not not_7 (not_7_out, in_1[2]);
  not not_8 (not_8_out, in_1[4]);
  not not_9 (not_9_out, in_1[5]);
  and A_2 (A_2_out, in_1[6], not_9_out, not_8_out, not_5_out, not_7_out, not_6_out, in_1[0]);
  or or_1 (out_7, a_out, A_2_out);
  not not_10 (not_10_out, in_1[3]);
  not not_11 (not_11_out, in_1[2]);
  and s (s_out, in_1[6], in_1[5], in_1[4], not_10_out, not_11_out, in_1[1], in_1[0]);
  not not_12 (not_12_out, in_1[5]);
  not not_13 (not_13_out, in_1[2]);
  not not_14 (not_14_out, in_1[3]);
  and S_2 (S_2_out, in_1[6], not_12_out, in_1[4], not_14_out, not_13_out, in_1[1], in_1[0]);
  or or_2 (out_8, s_out, S_2_out);
  not not_15 (not_15_out, in_1[1]);
  not not_16 (not_16_out, in_1[4]);
  not not_17 (not_17_out, in_1[0]);
  not not_18 (not_18_out, in_1[3]);
  and d (d_out, in_1[6], in_1[5], not_16_out, not_18_out, in_1[2], not_15_out, not_17_out);
  not not_19 (not_19_out, in_1[5]);
  not not_20 (not_20_out, in_1[1]);
  not not_21 (not_21_out, in_1[4]);
  not not_22 (not_22_out, in_1[0]);
  not not_23 (not_23_out, in_1[3]);
  and D_2 (D_2_out, in_1[6], not_19_out, not_21_out, not_23_out, in_1[2], not_20_out, not_22_out);
  or or_3 (out_9, d_out, D_2_out);
  not not_24 (not_24_out, in_1[0]);
  not not_25 (not_25_out, in_1[4]);
  not not_26 (not_26_out, in_1[3]);
  and f (f_out, in_1[6], in_1[5], not_25_out, not_26_out, in_1[2], in_1[1], not_24_out);
  not not_27 (not_27_out, in_1[5]);
  not not_28 (not_28_out, in_1[0]);
  not not_29 (not_29_out, in_1[4]);
  not not_30 (not_30_out, in_1[3]);
  and F_2 (F_2_out, in_1[6], not_27_out, not_29_out, not_30_out, in_1[2], in_1[1], not_28_out);
  or or_4 (out_10, f_out, F_2_out);
  not not_31 (not_31_out, in_1[3]);
  not not_32 (not_32_out, in_1[4]);
  and g (g_out, in_1[6], in_1[5], not_32_out, not_31_out, in_1[2], in_1[1], in_1[0]);
  not not_33 (not_33_out, in_1[3]);
  not not_34 (not_34_out, in_1[4]);
  not not_35 (not_35_out, in_1[5]);
  and G_2 (G_2_out, in_1[6], not_35_out, not_34_out, not_33_out, in_1[2], in_1[1], in_1[0]);
  or or_5 (out_11, g_out, G_2_out);
  not not_36 (not_36_out, in_1[0]);
  not not_37 (not_37_out, in_1[4]);
  not not_38 (not_38_out, in_1[2]);
  not not_39 (not_39_out, in_1[1]);
  and h (h_out, in_1[6], in_1[5], not_37_out, in_1[3], not_38_out, not_39_out, not_36_out);
  not not_40 (not_40_out, in_1[5]);
  not not_41 (not_41_out, in_1[4]);
  not not_42 (not_42_out, in_1[0]);
  not not_43 (not_43_out, in_1[1]);
  not not_44 (not_44_out, in_1[2]);
  and H_2 (H_2_out, in_1[6], not_40_out, not_41_out, in_1[3], not_44_out, not_43_out, not_42_out);
  or or_6 (out_12, h_out, H_2_out);
  not not_45 (not_45_out, in_1[2]);
  not not_46 (not_46_out, in_1[0]);
  not not_47 (not_47_out, in_1[4]);
  and j (j_out, in_1[6], in_1[5], not_47_out, in_1[3], not_45_out, in_1[1], not_46_out);
  not not_48 (not_48_out, in_1[0]);
  not not_49 (not_49_out, in_1[4]);
  not not_50 (not_50_out, in_1[5]);
  not not_51 (not_51_out, in_1[2]);
  and J_2 (J_2_out, in_1[6], not_50_out, not_49_out, in_1[3], not_51_out, in_1[1], not_48_out);
  or or_7 (out_13, j_out, J_2_out);
  not not_52 (not_52_out, in_1[4]);
  not not_53 (not_53_out, in_1[2]);
  and k (k_out, in_1[6], in_1[5], not_52_out, in_1[3], not_53_out, in_1[1], in_1[0]);
  not not_54 (not_54_out, in_1[5]);
  not not_55 (not_55_out, in_1[4]);
  not not_56 (not_56_out, in_1[2]);
  and K_2 (K_2_out, in_1[6], not_54_out, not_55_out, in_1[3], not_56_out, in_1[1], in_1[0]);
  or or_8 (out_14, k_out, K_2_out);
  not not_57 (not_57_out, in_1[1]);
  not not_58 (not_58_out, in_1[4]);
  not not_59 (not_59_out, in_1[0]);
  and l (l_out, in_1[6], in_1[5], not_58_out, in_1[3], in_1[2], not_57_out, not_59_out);
  not not_60 (not_60_out, in_1[4]);
  not not_61 (not_61_out, in_1[5]);
  not not_62 (not_62_out, in_1[1]);
  not not_63 (not_63_out, in_1[0]);
  and L_2 (L_2_out, in_1[6], not_61_out, not_60_out, in_1[3], in_1[2], not_62_out, not_63_out);
  or or_9 (out_15, l_out, L_2_out);
  not not_64 (not_64_out, in_1[2]);
  not not_65 (not_65_out, in_1[4]);
  not not_66 (not_66_out, in_1[6]);
  not not_67 (not_67_out, in_1[5]);
  and enter (out_2, not_66_out, not_67_out, not_65_out, in_1[3], not_64_out, in_1[1], not_68_out);
  not not_68 (not_68_out, in_1[0]);
  not not_69 (not_69_out, in_1[6]);
  not not_70 (not_70_out, in_1[2]);
  and \and  (out_3, not_69_out, in_1[5], in_1[4], in_1[3], not_70_out, in_1[1], in_1[0]);
  not not_71 (not_71_out, in_1[2]);
  not not_72 (not_72_out, in_1[6]);
  and and_2 (out_4, not_72_out, in_1[5], in_1[4], in_1[3], not_71_out, in_1[1], not_74_out);
  not not_73 (not_73_out, in_1[6]);
  not not_74 (not_74_out, in_1[0]);
  not not_75 (not_75_out, in_1[4]);
  not not_76 (not_76_out, in_1[3]);
  and and_3 (out_5, not_73_out, in_1[5], not_75_out, not_76_out, in_1[2], in_1[1], in_1[0]);
  not not_77 (not_77_out, in_1[2]);
  not not_78 (not_78_out, in_1[3]);
  not not_79 (not_79_out, in_1[4]);
  not not_80 (not_80_out, in_1[6]);
  and and_4 (out_6, not_80_out, in_1[5], not_79_out, not_78_out, not_77_out, in_1[1], not_81_out);
  not not_81 (not_81_out, in_1[0]);
endmodule

module zxcvbnm___ZXCVBNM____shift (
  input  [6:0] in_1,
  output out_2,
  output out_3,
  output out_4,
  output out_5,
  output out_6,
  output out_7,
  output out_8,
  output out_9,
  output out_10,
  output out_11,
  output out_12,
  output out_13,
  output out_14
);

  wire B_2_out, b_out, C_2_out, c_out, M_2_out, m_out, N_2_out, n_out, not_1_out, not_2_out, not_3_out,
       not_4_out, not_5_out, not_6_out, not_7_out, not_8_out, not_9_out, not_10_out, not_11_out, not_12_out,
       not_13_out, not_14_out, not_15_out, not_16_out, not_17_out, not_18_out, not_19_out, not_20_out,
       not_21_out, not_22_out, not_23_out, not_24_out, not_25_out, not_26_out, not_27_out, not_28_out,
       not_29_out, not_30_out, not_31_out, not_32_out, not_33_out, not_34_out, not_35_out, not_36_out,
       not_37_out, not_38_out, not_39_out, not_40_out, not_41_out, not_42_out, not_43_out, not_44_out,
       not_45_out, not_46_out, not_47_out, not_48_out, not_49_out, not_50_out, not_51_out, not_52_out,
       not_53_out, not_54_out, not_55_out, not_56_out, not_57_out, not_58_out, V_2_out, v_out, X_2_out,
       x_out, Z_2_out, z_out;

  not not_1 (not_1_out, in_1[2]);
  not not_2 (not_2_out, in_1[0]);
  and z (z_out, in_1[6], in_1[5], in_1[4], in_1[3], not_1_out, in_1[1], not_2_out);
  not not_3 (not_3_out, in_1[0]);
  not not_4 (not_4_out, in_1[5]);
  not not_5 (not_5_out, in_1[2]);
  and Z_2 (Z_2_out, in_1[6], not_4_out, in_1[4], in_1[3], not_5_out, in_1[1], not_3_out);
  or or_1 (out_8, z_out, Z_2_out);
  not not_6 (not_6_out, in_1[1]);
  not not_7 (not_7_out, in_1[2]);
  not not_8 (not_8_out, in_1[0]);
  and x (x_out, in_1[6], in_1[5], in_1[4], in_1[3], not_7_out, not_6_out, not_8_out);
  not not_9 (not_9_out, in_1[1]);
  not not_10 (not_10_out, in_1[2]);
  not not_11 (not_11_out, in_1[5]);
  not not_12 (not_12_out, in_1[0]);
  and X_2 (X_2_out, in_1[6], not_11_out, in_1[4], in_1[3], not_10_out, not_9_out, not_12_out);
  or or_2 (out_9, x_out, X_2_out);
  not not_13 (not_13_out, in_1[4]);
  not not_14 (not_14_out, in_1[3]);
  not not_15 (not_15_out, in_1[2]);
  and c (c_out, in_1[6], in_1[5], not_13_out, not_14_out, not_15_out, in_1[1], in_1[0]);
  not not_16 (not_16_out, in_1[5]);
  not not_17 (not_17_out, in_1[4]);
  not not_18 (not_18_out, in_1[3]);
  not not_19 (not_19_out, in_1[2]);
  and C_2 (C_2_out, in_1[6], not_16_out, not_17_out, not_18_out, not_19_out, in_1[1], in_1[0]);
  or or_3 (out_10, c_out, C_2_out);
  not not_20 (not_20_out, in_1[0]);
  not not_21 (not_21_out, in_1[3]);
  and v (v_out, in_1[6], in_1[5], in_1[4], not_21_out, in_1[2], in_1[1], not_20_out);
  not not_22 (not_22_out, in_1[0]);
  not not_23 (not_23_out, in_1[3]);
  not not_24 (not_24_out, in_1[5]);
  and V_2 (V_2_out, in_1[6], not_24_out, in_1[4], not_23_out, in_1[2], in_1[1], not_22_out);
  or or_4 (out_11, v_out, V_2_out);
  not not_25 (not_25_out, in_1[0]);
  not not_26 (not_26_out, in_1[2]);
  not not_27 (not_27_out, in_1[3]);
  not not_28 (not_28_out, in_1[4]);
  and b (b_out, in_1[6], in_1[5], not_28_out, not_27_out, not_26_out, in_1[1], not_25_out);
  not not_29 (not_29_out, in_1[2]);
  not not_30 (not_30_out, in_1[0]);
  not not_31 (not_31_out, in_1[3]);
  not not_32 (not_32_out, in_1[5]);
  not not_33 (not_33_out, in_1[4]);
  and B_2 (B_2_out, in_1[6], not_32_out, not_33_out, not_31_out, not_29_out, in_1[1], not_30_out);
  or or_5 (out_12, b_out, B_2_out);
  not not_34 (not_34_out, in_1[0]);
  not not_35 (not_35_out, in_1[4]);
  and n (n_out, in_1[6], in_1[5], not_35_out, in_1[3], in_1[2], in_1[1], not_34_out);
  not not_36 (not_36_out, in_1[0]);
  not not_37 (not_37_out, in_1[5]);
  not not_38 (not_38_out, in_1[4]);
  and N_2 (N_2_out, in_1[6], not_37_out, not_38_out, in_1[3], in_1[2], in_1[1], not_36_out);
  or or_6 (out_13, n_out, N_2_out);
  not not_39 (not_39_out, in_1[1]);
  not not_40 (not_40_out, in_1[4]);
  and m (m_out, in_1[6], in_1[5], not_40_out, in_1[3], in_1[2], not_39_out, in_1[0]);
  not not_41 (not_41_out, in_1[1]);
  not not_42 (not_42_out, in_1[4]);
  not not_43 (not_43_out, in_1[5]);
  and M_2 (M_2_out, in_1[6], not_43_out, not_42_out, in_1[3], in_1[2], not_41_out, in_1[0]);
  or or_7 (out_14, m_out, M_2_out);
  not not_44 (not_44_out, in_1[4]);
  not not_45 (not_45_out, in_1[1]);
  not not_46 (not_46_out, in_1[6]);
  not not_47 (not_47_out, in_1[0]);
  and \and  (out_2, not_46_out, in_1[5], not_44_out, in_1[3], in_1[2], not_45_out, not_47_out);
  not not_48 (not_48_out, in_1[6]);
  not not_49 (not_49_out, in_1[1]);
  not not_50 (not_50_out, in_1[0]);
  and and_2 (out_7, not_48_out, in_1[5], in_1[4], in_1[3], in_1[2], not_49_out, not_50_out);
  not not_51 (not_51_out, in_1[6]);
  not not_52 (not_52_out, in_1[4]);
  not not_53 (not_53_out, in_1[0]);
  and and_3 (out_3, not_51_out, in_1[5], not_52_out, in_1[3], in_1[2], in_1[1], not_53_out);
  not not_54 (not_54_out, in_1[0]);
  not not_55 (not_55_out, in_1[6]);
  and and_4 (out_6, not_55_out, in_1[5], in_1[4], in_1[3], in_1[2], in_1[1], not_54_out);
  not not_56 (not_56_out, in_1[6]);
  not not_57 (not_57_out, in_1[4]);
  and and_5 (out_4, not_56_out, in_1[5], not_57_out, in_1[3], in_1[2], in_1[1], in_1[0]);
  not not_58 (not_58_out, in_1[6]);
  and and_6 (out_5, not_58_out, in_1[5], in_1[4], in_1[3], in_1[2], in_1[1], in_1[0]);
endmodule

module spais (
  input  [6:0] in_1,
  output out_2
);

  wire not_1_out, not_2_out, not_3_out, not_4_out, not_5_out, not_6_out;

  not not_1 (not_1_out, in_1[3]);
  not not_2 (not_2_out, in_1[1]);
  not not_3 (not_3_out, in_1[4]);
  not not_4 (not_4_out, in_1[6]);
  not not_5 (not_5_out, in_1[2]);
  and \and  (out_2, not_4_out, in_1[5], not_3_out, not_1_out, not_5_out, not_2_out, not_6_out);
  not not_6 (not_6_out, in_1[0]);
endmodule

module _1 (
);

  wire asdfghjkl_asdfghjkl_caps_lock_enter_1_out_2, asdfghjkl_asdfghjkl_caps_lock_enter_1_out_3,
       asdfghjkl_asdfghjkl_caps_lock_enter_1_out_4, asdfghjkl_asdfghjkl_caps_lock_enter_1_out_5,
       asdfghjkl_asdfghjkl_caps_lock_enter_1_out_6, asdfghjkl_asdfghjkl_caps_lock_enter_1_out_7,
       asdfghjkl_asdfghjkl_caps_lock_enter_1_out_8, asdfghjkl_asdfghjkl_caps_lock_enter_1_out_9,
       asdfghjkl_asdfghjkl_caps_lock_enter_1_out_10, asdfghjkl_asdfghjkl_caps_lock_enter_1_out_11,
       asdfghjkl_asdfghjkl_caps_lock_enter_1_out_12, asdfghjkl_asdfghjkl_caps_lock_enter_1_out_13,
       asdfghjkl_asdfghjkl_caps_lock_enter_1_out_14, asdfghjkl_asdfghjkl_caps_lock_enter_1_out_15,
       clock_1_out, clock_2_out, n1234567890___backspace_1_out_2, n1234567890___backspace_1_out_3,
       n1234567890___backspace_1_out_4, n1234567890___backspace_1_out_5, n1234567890___backspace_1_out_6,
       n1234567890___backspace_1_out_7, n1234567890___backspace_1_out_8, n1234567890___backspace_1_out_9,
       n1234567890___backspace_1_out_10, n1234567890___backspace_1_out_11, n1234567890___backspace_1_out_12,
       n1234567890___backspace_1_out_13, n1234567890___backspace_1_out_14, n1234567890___backspace_1_out_15,
       n1234567890___backspace_1_out_16, n1234567890___backspace_1_out_17, n1234567890___backspace_1_out_18,
       n1234567890___backspace_1_out_19, n1234567890___backspace_1_out_20, n1234567890___backspace_1_out_21,
       n1234567890___backspace_1_out_22, n1234567890___backspace_1_out_23, n1234567890___backspace_1_out_24,
       n1234567890___backspace_1_out_25, n1234567890___backspace_1_out_26, n1234567890___backspace_1_out_27,
       n1234567890___backspace_1_out_28, qwertyuiop_qweryuiop_1_out_2, qwertyuiop_qweryuiop_1_out_3,
       qwertyuiop_qweryuiop_1_out_4, qwertyuiop_qweryuiop_1_out_5, qwertyuiop_qweryuiop_1_out_6,
       qwertyuiop_qweryuiop_1_out_7, qwertyuiop_qweryuiop_1_out_8, qwertyuiop_qweryuiop_1_out_9,
       qwertyuiop_qweryuiop_1_out_10, qwertyuiop_qweryuiop_1_out_11, qwertyuiop_qweryuiop_1_out_12,
       qwertyuiop_qweryuiop_1_out_13, qwertyuiop_qweryuiop_1_out_14, qwertyuiop_qweryuiop_1_out_15,
       qwertyuiop_qweryuiop_1_out_16, qwertyuiop_qweryuiop_1_out_17, spais_1_out_2,
       zxcvbnm_zxcvbnm_shift_1_out_2, zxcvbnm_zxcvbnm_shift_1_out_3, zxcvbnm_zxcvbnm_shift_1_out_4,
       zxcvbnm_zxcvbnm_shift_1_out_5, zxcvbnm_zxcvbnm_shift_1_out_6, zxcvbnm_zxcvbnm_shift_1_out_7,
       zxcvbnm_zxcvbnm_shift_1_out_8, zxcvbnm_zxcvbnm_shift_1_out_9, zxcvbnm_zxcvbnm_shift_1_out_10,
       zxcvbnm_zxcvbnm_shift_1_out_11, zxcvbnm_zxcvbnm_shift_1_out_12, zxcvbnm_zxcvbnm_shift_1_out_13,
       zxcvbnm_zxcvbnm_shift_1_out_14;
  wire [6:0] keyboard_1_data;

  LED led (.in(n1234567890___backspace_1_out_2));
  LED led_2 (.in(n1234567890___backspace_1_out_16));
  LED led_3 (.in(n1234567890___backspace_1_out_3));
  LED led_4 (.in(n1234567890___backspace_1_out_6));
  LED led_5 (.in(n1234567890___backspace_1_out_4));
  LED led_6 (.in(n1234567890___backspace_1_out_5));
  LED _3 (.in(n1234567890___backspace_1_out_19));
  LED _2 (.in(n1234567890___backspace_1_out_18));
  LED _4 (.in(n1234567890___backspace_1_out_20));
  LED _1 (.in(n1234567890___backspace_1_out_17));
  LED W (.in(qwertyuiop_qweryuiop_1_out_6));
  LED Q (.in(qwertyuiop_qweryuiop_1_out_5));
  LED E (.in(qwertyuiop_qweryuiop_1_out_7));
  LED D (.in(asdfghjkl_asdfghjkl_caps_lock_enter_1_out_9));
  LED A (.in(asdfghjkl_asdfghjkl_caps_lock_enter_1_out_7));
  LED S (.in(asdfghjkl_asdfghjkl_caps_lock_enter_1_out_8));
  LED Z (.in(zxcvbnm_zxcvbnm_shift_1_out_8));
  LED C (.in(zxcvbnm_zxcvbnm_shift_1_out_10));
  LED X (.in(zxcvbnm_zxcvbnm_shift_1_out_9));
  Keyboard #(.buflen(64)) keyboard_1 (.clk(clock_1_out), .data(keyboard_1_data));  // open: re, clr, avail
  Clock clock_1 (.out(clock_1_out));
  LED led_7 (.in(n1234567890___backspace_1_out_8));
  LED led_8 (.in(n1234567890___backspace_1_out_9));
  LED led_9 (.in(n1234567890___backspace_1_out_10));
  LED led_10 (.in(n1234567890___backspace_1_out_7));
  LED _6 (.in(n1234567890___backspace_1_out_22));
  LED _7 (.in(n1234567890___backspace_1_out_23));
  LED _8 (.in(n1234567890___backspace_1_out_24));
  LED _5 (.in(n1234567890___backspace_1_out_21));
  LED Y (.in(qwertyuiop_qweryuiop_1_out_10));
  LED R (.in(qwertyuiop_qweryuiop_1_out_8));
  LED U (.in(qwertyuiop_qweryuiop_1_out_11));
  LED T (.in(qwertyuiop_qweryuiop_1_out_9));
  LED F (.in(asdfghjkl_asdfghjkl_caps_lock_enter_1_out_10));
  LED H (.in(asdfghjkl_asdfghjkl_caps_lock_enter_1_out_12));
  LED J (.in(asdfghjkl_asdfghjkl_caps_lock_enter_1_out_13));
  LED G (.in(asdfghjkl_asdfghjkl_caps_lock_enter_1_out_11));
  LED N (.in(zxcvbnm_zxcvbnm_shift_1_out_13));
  LED B (.in(zxcvbnm_zxcvbnm_shift_1_out_12));
  LED M (.in(zxcvbnm_zxcvbnm_shift_1_out_14));
  LED V (.in(zxcvbnm_zxcvbnm_shift_1_out_11));
  LED led_11 (.in(spais_1_out_2));
  LED led_12 (.in(n1234567890___backspace_1_out_13));
  LED led_13 (.in(n1234567890___backspace_1_out_11));
  LED led_14 (.in(n1234567890___backspace_1_out_12));
  LED led_15 (.in(n1234567890___backspace_1_out_14));
  LED _0 (.in(n1234567890___backspace_1_out_26));
  LED led_16 (.in(n1234567890___backspace_1_out_27));
  LED _9 (.in(n1234567890___backspace_1_out_25));
  LED led_17 (.in(n1234567890___backspace_1_out_28));
  LED led_18 (.in(qwertyuiop_qweryuiop_1_out_2));
  LED O (.in(qwertyuiop_qweryuiop_1_out_13));
  LED I (.in(qwertyuiop_qweryuiop_1_out_12));
  LED P (.in(qwertyuiop_qweryuiop_1_out_14));
  LED led_19 (.in(qwertyuiop_qweryuiop_1_out_15));
  LED led_20 (.in(asdfghjkl_asdfghjkl_caps_lock_enter_1_out_4));
  LED K (.in(asdfghjkl_asdfghjkl_caps_lock_enter_1_out_14));
  LED led_21 (.in(asdfghjkl_asdfghjkl_caps_lock_enter_1_out_6));
  LED L (.in(asdfghjkl_asdfghjkl_caps_lock_enter_1_out_15));
  LED led_22 (.in(asdfghjkl_asdfghjkl_caps_lock_enter_1_out_5));
  LED led_23 (.in(asdfghjkl_asdfghjkl_caps_lock_enter_1_out_3));
  LED led_24 (.in(zxcvbnm_zxcvbnm_shift_1_out_7));
  LED led_25 (.in(zxcvbnm_zxcvbnm_shift_1_out_5));
  LED led_26 (.in(zxcvbnm_zxcvbnm_shift_1_out_6));
  LED led_27 (.in(zxcvbnm_zxcvbnm_shift_1_out_3));
  LED led_28 (.in(zxcvbnm_zxcvbnm_shift_1_out_4));
  LED led_29 (.in(zxcvbnm_zxcvbnm_shift_1_out_2));
  _1234567890________________backspace u_1234567890___backspace_1 (
    .in_1(keyboard_1_data), .out_2(n1234567890___backspace_1_out_2),
    .out_16(n1234567890___backspace_1_out_16), .out_17(n1234567890___backspace_1_out_17),
    .out_3(n1234567890___backspace_1_out_3), .out_18(n1234567890___backspace_1_out_18),
    .out_4(n1234567890___backspace_1_out_4), .out_19(n1234567890___backspace_1_out_19),
    .out_5(n1234567890___backspace_1_out_5), .out_20(n1234567890___backspace_1_out_20),
    .out_6(n1234567890___backspace_1_out_6), .out_21(n1234567890___backspace_1_out_21),
    .out_7(n1234567890___backspace_1_out_7), .out_22(n1234567890___backspace_1_out_22),
    .out_8(n1234567890___backspace_1_out_8), .out_23(n1234567890___backspace_1_out_23),
    .out_9(n1234567890___backspace_1_out_9), .out_24(n1234567890___backspace_1_out_24),
    .out_10(n1234567890___backspace_1_out_10), .out_25(n1234567890___backspace_1_out_25),
    .out_11(n1234567890___backspace_1_out_11), .out_26(n1234567890___backspace_1_out_26),
    .out_12(n1234567890___backspace_1_out_12), .out_27(n1234567890___backspace_1_out_27),
    .out_13(n1234567890___backspace_1_out_13), .out_28(n1234567890___backspace_1_out_28),
    .out_14(n1234567890___backspace_1_out_14), .out_15(n1234567890___backspace_1_out_15));
  LED led_30 (.in(n1234567890___backspace_1_out_15));
  LED led_31 (.in(qwertyuiop_qweryuiop_1_out_3));
  qwertyuiop____QWERYUIOP qwertyuiop_qweryuiop_1 (
    .out_15(qwertyuiop_qweryuiop_1_out_15), .out_16(qwertyuiop_qweryuiop_1_out_16), .in_1(keyboard_1_data),
    .out_5(qwertyuiop_qweryuiop_1_out_5), .out_6(qwertyuiop_qweryuiop_1_out_6),
    .out_7(qwertyuiop_qweryuiop_1_out_7), .out_8(qwertyuiop_qweryuiop_1_out_8),
    .out_9(qwertyuiop_qweryuiop_1_out_9), .out_10(qwertyuiop_qweryuiop_1_out_10),
    .out_11(qwertyuiop_qweryuiop_1_out_11), .out_12(qwertyuiop_qweryuiop_1_out_12),
    .out_13(qwertyuiop_qweryuiop_1_out_13), .out_14(qwertyuiop_qweryuiop_1_out_14),
    .out_2(qwertyuiop_qweryuiop_1_out_2), .out_3(qwertyuiop_qweryuiop_1_out_3),
    .out_17(qwertyuiop_qweryuiop_1_out_17), .out_4(qwertyuiop_qweryuiop_1_out_4));
  LED led_32 (.in(qwertyuiop_qweryuiop_1_out_4));
  asdfghjkl___ASDFGHJKL____CAPS_LOCK__ENTER asdfghjkl_asdfghjkl_caps_lock_enter_1 (
    .in_1(keyboard_1_data), .out_7(asdfghjkl_asdfghjkl_caps_lock_enter_1_out_7),
    .out_8(asdfghjkl_asdfghjkl_caps_lock_enter_1_out_8), .out_9(asdfghjkl_asdfghjkl_caps_lock_enter_1_out_9),
    .out_10(asdfghjkl_asdfghjkl_caps_lock_enter_1_out_10),
    .out_11(asdfghjkl_asdfghjkl_caps_lock_enter_1_out_11),
    .out_12(asdfghjkl_asdfghjkl_caps_lock_enter_1_out_12),
    .out_13(asdfghjkl_asdfghjkl_caps_lock_enter_1_out_13),
    .out_14(asdfghjkl_asdfghjkl_caps_lock_enter_1_out_14),
    .out_15(asdfghjkl_asdfghjkl_caps_lock_enter_1_out_15),
    .out_2(asdfghjkl_asdfghjkl_caps_lock_enter_1_out_2), .out_3(asdfghjkl_asdfghjkl_caps_lock_enter_1_out_3),
    .out_4(asdfghjkl_asdfghjkl_caps_lock_enter_1_out_4), .out_5(asdfghjkl_asdfghjkl_caps_lock_enter_1_out_5),
    .out_6(asdfghjkl_asdfghjkl_caps_lock_enter_1_out_6));
  LED led_33 (.in(qwertyuiop_qweryuiop_1_out_16));
  LED led_34 (.in(qwertyuiop_qweryuiop_1_out_17));
  LED Enter (.in(asdfghjkl_asdfghjkl_caps_lock_enter_1_out_2));
  zxcvbnm___ZXCVBNM____shift zxcvbnm_zxcvbnm_shift_1 (
    .out_8(zxcvbnm_zxcvbnm_shift_1_out_8), .out_9(zxcvbnm_zxcvbnm_shift_1_out_9),
    .out_10(zxcvbnm_zxcvbnm_shift_1_out_10), .out_11(zxcvbnm_zxcvbnm_shift_1_out_11),
    .out_12(zxcvbnm_zxcvbnm_shift_1_out_12), .out_13(zxcvbnm_zxcvbnm_shift_1_out_13),
    .out_14(zxcvbnm_zxcvbnm_shift_1_out_14), .in_1(keyboard_1_data), .out_2(zxcvbnm_zxcvbnm_shift_1_out_2),
    .out_7(zxcvbnm_zxcvbnm_shift_1_out_7), .out_3(zxcvbnm_zxcvbnm_shift_1_out_3),
    .out_6(zxcvbnm_zxcvbnm_shift_1_out_6), .out_4(zxcvbnm_zxcvbnm_shift_1_out_4),
    .out_5(zxcvbnm_zxcvbnm_shift_1_out_5));
  spais spais_1 (.in_1(keyboard_1_data), .out_2(spais_1_out_2));
  TTY tty_1 (.data(keyboard_1_data), .clk(clock_2_out));  // open: we, clr
  Clock clock_2 (.out(clock_2_out));
endmodule
