// Logisim project x.circ as structural Verilog: 109 circuits, main circuit 1
module main (
  input  reset,
  input  \αρχικοποιηση ,
  input  \_0_για_μνημη_1_για_πληκρολογιο ,
  input  in_4,
  input  in_5
);

  wire _0_out, _1_out, _2_out, _3_num_out, _4_out, _5_out, _6_out, _7_out, _8_star_out, _9_out, A_out, B_out,
       Ba_out, button_2_out, button_3_out, button_4_out, button_5_out, button_6_out, button_7_out,
       button_8_out, button_9_out, button_10_out, button_11_out, button_12_out, button_out, C_out,
       clock_1_out, D_out, E_out, En_out, F_out, G_out, H_out, I_out, J_out, K_out, L_out, M_out, minus__out,
       multiplexer_2_out, N_out, O_out, P_out, Q_out, R_out, S_out, T_out, U_out, V_out, W_out, X_out, Y_out,
       Z_out;
  wire [6:0] adder_1_out, multiplexer_1_out, ram_1_data, register_1_q, \πληκτολογιο_1_out_54 ;

  Adder #(.width(7)) adder_1 (.a(register_1_q), .b(7'b0000001), .out(adder_1_out));  // open: cin, cout
  Register #(.width(7)) register_1 (.D(adder_1_out), .Q(register_1_q), .clk(clock_1_out));  // open: en, clr
  Clock clock_1 (.out(clock_1_out));
  Multiplexer #(.width(7), .enable("false")) multiplexer_1 (
    .in0(register_1_q), .in1(\πληκτολογιο_1_out_54 ), .out(multiplexer_1_out),
    .sel(\_0_για_μνημη_1_για_πληκρολογιο ));
  RAM #(.addrWidth(7), .dataWidth(7), .bus("separate")) ram_1 (
    .addr(multiplexer_1_out), .din(register_1_q), .data(ram_1_data), .str(multiplexer_2_out),
    .clk(clock_1_out));  // open: sel, ld, clr
  TTY #(.rows(32), .cols(100)) tty_1 (.data(ram_1_data), .clk(clock_1_out), .clr(reset));  // open: we
  Multiplexer #(.enable("false")) multiplexer_2 (.in0(1'b1), .in1(1'b0), .out(multiplexer_2_out), .sel(\αρχικοποιηση ));
  Button _1 (.out(_1_out));
  Button button (.out(button_out));
  Button _3_num (.out(_3_num_out));
  Button _2 (.out(_2_out));
  Button W (.out(W_out));
  Button E (.out(E_out));
  Button Q (.out(Q_out));
  Button A (.out(A_out));
  Button S (.out(S_out));
  Button button_2 (.out(button_2_out));
  Button Z (.out(Z_out));
  \πληκτολογιο  \u_πληκτολογιο_1  (
    .out_54(\πληκτολογιο_1_out_54 ), .in_1(button_out), .in_2(_1_out), .in_3(_2_out), .in_4(_3_num_out),
    .in_5(_4_out), .in_6(_5_out), .in_7(_6_out), .in_8(_7_out), .in_9(_8_star_out), .in_10(_9_out),
    .in_11(_0_out), .in_12(minus__out), .in_13(button_8_out), .in_14(Ba_out), .in_16(Q_out), .in_15(W_out),
    .in_17(E_out), .in_18(R_out), .in_19(T_out), .in_20(Y_out), .in_21(U_out), .in_22(I_out), .in_23(O_out),
    .in_24(P_out), .in_25(button_4_out), .in_26(button_10_out), .in_27(button_9_out), .in_28(button_2_out),
    .in_29(A_out), .in_30(S_out), .in_31(D_out), .in_32(F_out), .in_33(G_out), .in_34(H_out), .in_35(J_out),
    .in_36(K_out), .in_37(L_out), .in_38(button_5_out), .in_39(button_11_out), .in_40(En_out), .in_41(in_4),
    .in_42(Z_out), .in_43(X_out), .in_44(C_out), .in_45(V_out), .in_46(B_out), .in_47(N_out), .in_48(M_out),
    .in_49(button_6_out), .in_50(button_7_out), .in_51(button_12_out), .in_52(in_5), .in_53(button_3_out));
  Button _6 (.out(_6_out));
  Button _5 (.out(_5_out));
  Button _4 (.out(_4_out));
  Button _7 (.out(_7_out));
  Button Y (.out(Y_out));
  Button R (.out(R_out));
  Button U (.out(U_out));
  Button T (.out(T_out));
  Button F (.out(F_out));
  Button D (.out(D_out));
  Button H (.out(H_out));
  Button G (.out(G_out));
  Button C (.out(C_out));
  Button X (.out(X_out));
  Button B (.out(B_out));
  Button V (.out(V_out));
  Button button_3 (.out(button_3_out));
  Button _9 (.out(_9_out));
  Button _8_star (.out(_8_star_out));
  Button _0 (.out(_0_out));
  Button minus_ (.out(minus__out));
  Button P (.out(P_out));
  Button O (.out(O_out));
  Button button_4 (.out(button_4_out));
  Button I (.out(I_out));
  Button J (.out(J_out));
  Button K (.out(K_out));
  Button L (.out(L_out));
  Button button_5 (.out(button_5_out));
  Button N (.out(N_out));
  Button button_6 (.out(button_6_out));
  Button M (.out(M_out));
  Button button_7 (.out(button_7_out));
  Button Ba (.out(Ba_out));
  Button button_8 (.out(button_8_out));
  Button button_9 (.out(button_9_out));
  Button button_10 (.out(button_10_out));
  Button button_11 (.out(button_11_out));
  Button En (.out(En_out));
  Button button_12 (.out(button_12_out));
endmodule

module \πληκτολογιο  (
  input  in_1,
  input  in_2,
  input  in_3,
  input  in_4,
  input  in_5,
  input  in_6,
  input  in_7,
  input  in_8,
  input  in_9,
  input  in_10,
  input  in_11,
  input  in_12,
  input  in_13,
  input  in_14,
  input  in_15,
  input  in_16,
  input  in_17,
  input  in_18,
  input  in_19,
  input  in_20,
  input  in_21,
  input  in_22,
  input  in_23,
  input  in_24,
  input  in_25,
  input  in_26,
  input  in_27,
  input  in_28,
  input  in_29,
  input  in_30,
  input  in_31,
  input  in_32,
  input  in_33,
  input  in_34,
  input  in_35,
  input  in_36,
  input  in_37,
  input  in_38,
  input  in_39,
  input  in_40,
  input  in_41,
  input  in_42,
  input  in_43,
  input  in_44,
  input  in_45,
  input  in_46,
  input  in_47,
  input  in_48,
  input  in_49,
  input  in_50,
  input  in_51,
  input  in_52,
  input  in_53,
  output [6:0] out_54
);

  wire button_1_out, not_1_out, not_2_out, or_4_out, register_1_q;
  wire [6:0] ariumi_0_9_1_out_11, backspace_08_1_out_2, multiplexer_1_out, multiplexer_2_out,
       multiplexer_3_out, multiplexer_4_out, n2b_1_out_2, n2d_1_out_2, n3d_1_out_2, n5f_1_out_2, n7e_1_out_2,
       n60_1_out_2, n61_1_out_11, or_1_out, or_3_out, spahs_1_out_2, \δετερι_1_out_16 , \τεραρτη_1_out_13 ,
       \τριτη_1_out_15 ;

  Multiplexer #(.width(7), .enable("false")) multiplexer_1 (
    .in0(n61_1_out_11), .in1(ariumi_0_9_1_out_11), .out(multiplexer_1_out), .sel(not_1_out));
  assign or_1_out = multiplexer_1_out | or_3_out;  // OR_Gate or_1, 7 bits wide
  _61 u_61_1 (
    .in_1(in_11), .in_2(in_10), .in_3(in_9), .in_4(in_8), .in_5(in_7), .in_6(in_6), .in_7(in_5), .in_8(in_4),
    .in_9(in_3), .in_10(in_2), .out_11(n61_1_out_11));
  not not_1 (not_1_out, or_4_out);
  assign out_54 = or_1_out | \δετερι_1_out_16  | \τριτη_1_out_15  | \τεραρτη_1_out_13  | spahs_1_out_2;  // OR_Gate or_2, 7 bits wide
  ariumi_0_9 ariumi_0_9_1 (
    .in_1(in_2), .in_2(in_3), .in_3(in_4), .in_4(in_5), .in_5(in_6), .in_6(in_7), .in_7(in_8), .in_8(in_9),
    .in_9(in_10), .in_10(in_11), .out_11(ariumi_0_9_1_out_11));
  Hex_Digit_Display hex_digit_display_1 (.value({1'b0, out_54[6:4]}));  // open: dp
  Hex_Digit_Display hex_digit_display_2 (.value(out_54[3:0]));  // open: dp
  _60 u_60_1 (.in_1(in_1), .out_2(n60_1_out_2));
  Multiplexer #(.width(7), .enable("false")) multiplexer_2 (
    .in0(n60_1_out_2), .in1(n7e_1_out_2), .out(multiplexer_2_out), .sel(or_4_out));
  _5f u_5f_1 (.in_1(in_12), .out_2(n5f_1_out_2));
  _7e u_7e_1 (.in_1(in_1), .out_2(n7e_1_out_2));
  _2d u_2d_1 (.in_1(in_12), .out_2(n2d_1_out_2));
  Multiplexer #(.width(7), .enable("false")) multiplexer_3 (
    .in0(n2d_1_out_2), .in1(n5f_1_out_2), .out(multiplexer_3_out), .sel(or_4_out));
  Button button_1 (.out(button_1_out));
  _3d u_3d_1 (.in_1(in_13), .out_2(n3d_1_out_2));
  Multiplexer #(.width(7), .enable("false")) multiplexer_4 (
    .in0(n3d_1_out_2), .in1(n2b_1_out_2), .out(multiplexer_4_out), .sel(or_4_out));
  assign or_3_out = multiplexer_2_out | multiplexer_3_out | multiplexer_4_out | backspace_08_1_out_2;  // OR_Gate or_3, 7 bits wide
  TTY tty_1 (.data(out_54), .clk(button_1_out));  // open: we, clr
  _2b u_2b_1 (.in_1(in_13), .out_2(n2b_1_out_2));
  Backspace_08 backspace_08_1 (.in_1(in_14), .out_2(backspace_08_1_out_2));
  \δετερι  \u_δετερι_1  (
    .in_14(register_1_q), .in_15(or_4_out), .in_1(in_15), .in_2(in_16), .in_3(in_17), .in_4(in_18),
    .in_5(in_19), .in_6(in_20), .in_7(in_21), .in_8(in_22), .in_9(in_23), .in_10(in_24), .in_11(in_25),
    .in_12(in_26), .in_13(in_27), .out_16(\δετερι_1_out_16 ));
  not not_2 (not_2_out, register_1_q);
  Register #(.width(1)) register_1 (.D(not_2_out), .Q(register_1_q), .clk(in_28));  // open: en, clr
  \τριτη  \u_τριτη_1  (
    .in_13(register_1_q), .in_14(or_4_out), .in_1(in_29), .in_2(in_30), .in_3(in_31), .in_4(in_32),
    .in_5(in_33), .in_6(in_34), .in_7(in_35), .in_8(in_36), .in_9(in_37), .in_10(in_38), .in_11(in_39),
    .in_12(in_40), .out_15(\τριτη_1_out_15 ));
  or or_4 (or_4_out, in_41, in_52);
  \τεραρτη  \u_τεραρτη_1  (
    .in_11(register_1_q), .in_12(or_4_out), .in_1(in_42), .in_2(in_43), .in_3(in_44), .in_4(in_45),
    .in_5(in_46), .in_6(in_47), .in_7(in_48), .in_8(in_49), .in_9(in_50), .in_10(in_51),
    .out_13(\τεραρτη_1_out_13 ));
  spahs spahs_1 (.in_1(in_53), .out_2(spahs_1_out_2));
endmodule

module \δετερι  (
  input  in_1,
  input  in_2,
  input  in_3,
  input  in_4,
  input  in_5,
  input  in_6,
  input  in_7,
  input  in_8,
  input  in_9,
  input  in_10,
  input  in_11,
  input  in_12,
  input  in_13,
  input  in_14,
  input  in_15,
  output [6:0] out_16
);

  wire or_2_out;
  wire [6:0] e_45_1_out_2, e_65_1_out_2, f_46_1_out_2, i_49_1_out_2, i_69_1_out_2, multiplexer_1_out,
       multiplexer_2_out, multiplexer_3_out, multiplexer_4_out, multiplexer_5_out, multiplexer_6_out,
       multiplexer_7_out, multiplexer_8_out, multiplexer_9_out, multiplexer_10_out, multiplexer_11_out,
       multiplexer_12_out, multiplexer_13_out, n5b_1_out_2, n5c_1_out_2, n5d_1_out_2, n7b_1_out_2,
       n7c_1_out_2, n7d_1_out_2, o_4f_1_out_2, p_50_1_out_2, p_70_1_out_2, q_51_1_out_2, q_71_1_out_2,
       r_52_1_out_2, r_72_1_out_2, t_54_1_out_2, t_74_1_out_2, u_55_1_out_2, u_75_1_out_2, w_57_1_out_2,
       w_77_1_out_2, y_59_1_out_2, y_79_1_out_2;

  w_77 w_77_1 (.in_1(in_2), .out_2(w_77_1_out_2));
  q_71 q_71_1 (.in_1(in_1), .out_2(q_71_1_out_2));
  Q_51 q_51_1 (.in_1(in_1), .out_2(q_51_1_out_2));
  Multiplexer #(.width(7), .enable("false")) multiplexer_1 (
    .in0(w_77_1_out_2), .in1(w_57_1_out_2), .out(multiplexer_1_out), .sel(or_2_out));
  Multiplexer #(.width(7), .enable("false")) multiplexer_2 (
    .in0(q_71_1_out_2), .in1(q_51_1_out_2), .out(multiplexer_2_out), .sel(or_2_out));
  e_65 e_65_1 (.in_1(in_3), .out_2(e_65_1_out_2));
  E_45 e_45_1 (.in_1(in_3), .out_2(e_45_1_out_2));
  W_57 w_57_1 (.in_1(in_2), .out_2(w_57_1_out_2));
  Multiplexer #(.width(7), .enable("false")) multiplexer_3 (
    .in0(e_65_1_out_2), .in1(e_45_1_out_2), .out(multiplexer_3_out), .sel(or_2_out));
  r_72 r_72_1 (.in_1(in_4), .out_2(r_72_1_out_2));
  t_74 t_74_1 (.in_1(in_5), .out_2(t_74_1_out_2));
  T_54 t_54_1 (.in_1(in_5), .out_2(t_54_1_out_2));
  R_52 r_52_1 (.in_1(in_4), .out_2(r_52_1_out_2));
  Multiplexer #(.width(7), .enable("false")) multiplexer_4 (
    .in0(r_72_1_out_2), .in1(r_52_1_out_2), .out(multiplexer_4_out), .sel(or_2_out));
  Multiplexer #(.width(7), .enable("false")) multiplexer_5 (
    .in0(t_74_1_out_2), .in1(t_54_1_out_2), .out(multiplexer_5_out), .sel(or_2_out));
  u_75 u_75_1 (.in_1(in_7), .out_2(u_75_1_out_2));
  y_79 y_79_1 (.in_1(in_6), .out_2(y_79_1_out_2));
  Y_59 y_59_1 (.in_1(in_6), .out_2(y_59_1_out_2));
  Multiplexer #(.width(7), .enable("false")) multiplexer_6 (
    .in0(y_79_1_out_2), .in1(y_59_1_out_2), .out(multiplexer_6_out), .sel(or_2_out));
  i_69 i_69_1 (.in_1(in_8), .out_2(i_69_1_out_2));
  U_55 u_55_1 (.in_1(in_7), .out_2(u_55_1_out_2));
  I_49 i_49_1 (.in_1(in_8), .out_2(i_49_1_out_2));
  Multiplexer #(.width(7), .enable("false")) multiplexer_7 (
    .in0(i_69_1_out_2), .in1(i_49_1_out_2), .out(multiplexer_7_out), .sel(or_2_out));
  Multiplexer #(.width(7), .enable("false")) multiplexer_8 (
    .in0(u_75_1_out_2), .in1(u_55_1_out_2), .out(multiplexer_8_out), .sel(or_2_out));
  assign out_16 = multiplexer_2_out | multiplexer_1_out | multiplexer_3_out | multiplexer_4_out | multiplexer_5_out | multiplexer_6_out | multiplexer_8_out | multiplexer_7_out | multiplexer_10_out | multiplexer_9_out | multiplexer_11_out | multiplexer_12_out | multiplexer_13_out;  // OR_Gate or_1, 7 bits wide
  O_4f o_4f_1 (.in_1(in_9), .out_2(o_4f_1_out_2));
  p_70 p_70_1 (.in_1(in_10), .out_2(p_70_1_out_2));
  F_46 f_46_1 (.in_1(in_9), .out_2(f_46_1_out_2));
  Multiplexer #(.width(7), .enable("false")) multiplexer_9 (
    .in0(p_70_1_out_2), .in1(p_50_1_out_2), .out(multiplexer_9_out), .sel(or_2_out));
  Multiplexer #(.width(7), .enable("false")) multiplexer_10 (
    .in0(o_4f_1_out_2), .in1(f_46_1_out_2), .out(multiplexer_10_out), .sel(or_2_out));
  _5b u_5b_1 (.in_1(in_11), .out_2(n5b_1_out_2));
  P_50 p_50_1 (.in_1(in_10), .out_2(p_50_1_out_2));
  _7b u_7b_1 (.in_1(in_11), .out_2(n7b_1_out_2));
  Multiplexer #(.width(7), .enable("false")) multiplexer_11 (
    .in0(n5b_1_out_2), .in1(n7b_1_out_2), .out(multiplexer_11_out), .sel(in_15));
  _5c u_5c_1 (.in_1(in_13), .out_2(n5c_1_out_2));
  _5d u_5d_1 (.in_1(in_12), .out_2(n5d_1_out_2));
  _7d u_7d_1 (.in_1(in_12), .out_2(n7d_1_out_2));
  _7c u_7c_1 (.in_1(in_13), .out_2(n7c_1_out_2));
  Multiplexer #(.width(7), .enable("false")) multiplexer_12 (
    .in0(n5d_1_out_2), .in1(n7d_1_out_2), .out(multiplexer_12_out), .sel(in_15));
  Multiplexer #(.width(7), .enable("false")) multiplexer_13 (
    .in0(n5c_1_out_2), .in1(n7c_1_out_2), .out(multiplexer_13_out), .sel(in_15));
  or or_2 (or_2_out, in_14, in_15);
endmodule

module \τριτη  (
  input  in_1,
  input  in_2,
  input  in_3,
  input  in_4,
  input  in_5,
  input  in_6,
  input  in_7,
  input  in_8,
  input  in_9,
  input  in_10,
  input  in_11,
  input  in_12,
  input  in_13,
  input  in_14,
  output [6:0] out_15
);

  wire or_2_out;
  wire [6:0] a_41_1_out_2, a_61_1_out_2, d_44_1_out_2, d_64_1_out_2, enter_1_out_2, f_46_1_out_2,
       f_66_1_out_2, g_47_1_out_2, g_67_1_out_2, h_48_1_out_2, h_68_1_out_2, j_4a_1_out_2, j_6a_1_out_2,
       k_4b_1_out_2, k_6b_1_out_2, l_4c_1_out_2, l_6c_1_out_2, multiplexer_1_out, multiplexer_2_out,
       multiplexer_3_out, multiplexer_4_out, multiplexer_5_out, multiplexer_6_out, multiplexer_7_out,
       multiplexer_8_out, multiplexer_9_out, multiplexer_10_out, multiplexer_11_out, n3a_1_out_2,
       n3b_1_out_2, n27_1_out_2, part_1_out_2, s_53_1_out_2, s_73_1_out_2;

  a_61 a_61_1 (.in_1(in_1), .out_2(a_61_1_out_2));
  s_73 s_73_1 (.in_1(in_2), .out_2(s_73_1_out_2));
  A_41 a_41_1 (.in_1(in_1), .out_2(a_41_1_out_2));
  Multiplexer #(.width(7), .enable("false")) multiplexer_1 (
    .in0(a_61_1_out_2), .in1(a_41_1_out_2), .out(multiplexer_1_out), .sel(or_2_out));
  Multiplexer #(.width(7), .enable("false")) multiplexer_2 (
    .in0(s_73_1_out_2), .in1(s_53_1_out_2), .out(multiplexer_2_out), .sel(or_2_out));
  d_64 d_64_1 (.in_1(in_3), .out_2(d_64_1_out_2));
  S_53 s_53_1 (.in_1(in_2), .out_2(s_53_1_out_2));
  D_44 d_44_1 (.in_1(in_3), .out_2(d_44_1_out_2));
  Multiplexer #(.width(7), .enable("false")) multiplexer_3 (
    .in0(d_64_1_out_2), .in1(d_44_1_out_2), .out(multiplexer_3_out), .sel(or_2_out));
  f_66 f_66_1 (.in_1(in_4), .out_2(f_66_1_out_2));
  g_67 g_67_1 (.in_1(in_5), .out_2(g_67_1_out_2));
  F_46 f_46_1 (.in_1(in_4), .out_2(f_46_1_out_2));
  G_47 g_47_1 (.in_1(in_5), .out_2(g_47_1_out_2));
  Multiplexer #(.width(7), .enable("false")) multiplexer_4 (
    .in0(f_66_1_out_2), .in1(f_46_1_out_2), .out(multiplexer_4_out), .sel(or_2_out));
  Multiplexer #(.width(7), .enable("false")) multiplexer_5 (
    .in0(g_67_1_out_2), .in1(g_47_1_out_2), .out(multiplexer_5_out), .sel(or_2_out));
  h_68 h_68_1 (.in_1(in_6), .out_2(h_68_1_out_2));
  H_48 h_48_1 (.in_1(in_6), .out_2(h_48_1_out_2));
  Multiplexer #(.width(7), .enable("false")) multiplexer_6 (
    .in0(h_68_1_out_2), .in1(h_48_1_out_2), .out(multiplexer_6_out), .sel(or_2_out));
  assign out_15 = multiplexer_1_out | multiplexer_2_out | multiplexer_3_out | multiplexer_4_out | multiplexer_5_out | multiplexer_6_out | multiplexer_8_out | multiplexer_7_out | multiplexer_9_out | multiplexer_11_out | multiplexer_10_out | enter_1_out_2;  // OR_Gate or_1, 7 bits wide
  j_6a j_6a_1 (.in_1(in_7), .out_2(j_6a_1_out_2));
  k_6b k_6b_1 (.in_1(in_8), .out_2(k_6b_1_out_2));
  K_4b k_4b_1 (.in_1(in_8), .out_2(k_4b_1_out_2));
  J_4a j_4a_1 (.in_1(in_7), .out_2(j_4a_1_out_2));
  Multiplexer #(.width(7), .enable("false")) multiplexer_7 (
    .in0(k_6b_1_out_2), .in1(k_4b_1_out_2), .out(multiplexer_7_out), .sel(or_2_out));
  Multiplexer #(.width(7), .enable("false")) multiplexer_8 (
    .in0(j_6a_1_out_2), .in1(j_4a_1_out_2), .out(multiplexer_8_out), .sel(or_2_out));
  _3b u_3b_1 (.in_1(in_10), .out_2(n3b_1_out_2));
  l_6c l_6c_1 (.in_1(in_9), .out_2(l_6c_1_out_2));
  L_4c l_4c_1 (.in_1(in_9), .out_2(l_4c_1_out_2));
  Multiplexer #(.width(7), .enable("false")) multiplexer_9 (
    .in0(l_6c_1_out_2), .in1(l_4c_1_out_2), .out(multiplexer_9_out), .sel(or_2_out));
  _27 u_27_1 (.in_1(in_11), .out_2(n27_1_out_2));
  _3a u_3a_1 (.in_1(in_10), .out_2(n3a_1_out_2));
  circuit part_1 (.in_1(in_11), .out_2(part_1_out_2));
  Multiplexer #(.width(7), .enable("false")) multiplexer_10 (
    .in0(n27_1_out_2), .in1(part_1_out_2), .out(multiplexer_10_out), .sel(in_14));
  Multiplexer #(.width(7), .enable("false")) multiplexer_11 (
    .in0(n3b_1_out_2), .in1(n3a_1_out_2), .out(multiplexer_11_out), .sel(in_14));
  enter enter_1 (.in_1(in_12), .out_2(enter_1_out_2));
  or or_2 (or_2_out, in_13, in_14);
endmodule

module \τεραρτη  (
  input  in_1,
  input  in_2,
  input  in_3,
  input  in_4,
  input  in_5,
  input  in_6,
  input  in_7,
  input  in_8,
  input  in_9,
  input  in_10,
  input  in_11,
  input  in_12,
  output [6:0] out_13
);

  wire or_2_out;
  wire [6:0] b_42_1_out_2, b_62_1_out_2, c_43_1_out_2, c_63_1_out_2, m_4d_1_out_2, m_6d_1_out_2,
       multiplexer_1_out, multiplexer_2_out, multiplexer_3_out, multiplexer_4_out, multiplexer_5_out,
       multiplexer_6_out, multiplexer_7_out, multiplexer_8_out, multiplexer_9_out, multiplexer_10_out,
       n2c_1_out_2, n2e_1_out_2, n2f_1_out_2, n3c_1_out_2, n3e_1_out_2, n3f_1_out_2, n_4e_1_out_2,
       n_6e_1_out_2, v_56_1_out_2, v_76_1_out_2, x_58_1_out_2, x_78_1_out_2, z_5a_1_out_2, z_7a_1_out_2;

  x_78 x_78_1 (.in_1(in_2), .out_2(x_78_1_out_2));
  z_7a z_7a_1 (.in_1(in_1), .out_2(z_7a_1_out_2));
  Z_5a z_5a_1 (.in_1(in_1), .out_2(z_5a_1_out_2));
  Multiplexer #(.width(7), .enable("false")) multiplexer_1 (
    .in0(z_7a_1_out_2), .in1(z_5a_1_out_2), .out(multiplexer_1_out), .sel(or_2_out));
  Multiplexer #(.width(7), .enable("false")) multiplexer_2 (
    .in0(x_78_1_out_2), .in1(x_58_1_out_2), .out(multiplexer_2_out), .sel(or_2_out));
  c_63 c_63_1 (.in_1(in_3), .out_2(c_63_1_out_2));
  C_43 c_43_1 (.in_1(in_3), .out_2(c_43_1_out_2));
  X_58 x_58_1 (.in_1(in_2), .out_2(x_58_1_out_2));
  Multiplexer #(.width(7), .enable("false")) multiplexer_3 (
    .in0(c_63_1_out_2), .in1(c_43_1_out_2), .out(multiplexer_3_out), .sel(or_2_out));
  v_76 v_76_1 (.in_1(in_4), .out_2(v_76_1_out_2));
  b_62 b_62_1 (.in_1(in_5), .out_2(b_62_1_out_2));
  B_42 b_42_1 (.in_1(in_5), .out_2(b_42_1_out_2));
  V_56 v_56_1 (.in_1(in_4), .out_2(v_56_1_out_2));
  Multiplexer #(.width(7), .enable("false")) multiplexer_4 (
    .in0(v_76_1_out_2), .in1(v_56_1_out_2), .out(multiplexer_4_out), .sel(or_2_out));
  Multiplexer #(.width(7), .enable("false")) multiplexer_5 (
    .in0(b_62_1_out_2), .in1(b_42_1_out_2), .out(multiplexer_5_out), .sel(or_2_out));
  n_6e n_6e_1 (.in_1(in_6), .out_2(n_6e_1_out_2));
  N_4e n_4e_1 (.in_1(in_6), .out_2(n_4e_1_out_2));
  Multiplexer #(.width(7), .enable("false")) multiplexer_6 (
    .in0(n_6e_1_out_2), .in1(n_4e_1_out_2), .out(multiplexer_6_out), .sel(or_2_out));
  assign out_13 = multiplexer_1_out | multiplexer_2_out | multiplexer_3_out | multiplexer_4_out | multiplexer_5_out | multiplexer_6_out | multiplexer_8_out | multiplexer_7_out | multiplexer_9_out | multiplexer_10_out;  // OR_Gate or_1, 7 bits wide
  _2c u_2c_1 (.in_1(in_8), .out_2(n2c_1_out_2));
  m_6d m_6d_1 (.in_1(in_7), .out_2(m_6d_1_out_2));
  M_4d m_4d_1 (.in_1(in_7), .out_2(m_4d_1_out_2));
  Multiplexer #(.width(7), .enable("false")) multiplexer_7 (
    .in0(n2c_1_out_2), .in1(n3c_1_out_2), .out(multiplexer_7_out), .sel(in_12));
  Multiplexer #(.width(7), .enable("false")) multiplexer_8 (
    .in0(m_6d_1_out_2), .in1(m_4d_1_out_2), .out(multiplexer_8_out), .sel(or_2_out));
  _2e u_2e_1 (.in_1(in_9), .out_2(n2e_1_out_2));
  _3c u_3c_1 (.in_1(in_8), .out_2(n3c_1_out_2));
  _3e u_3e_1 (.in_1(in_9), .out_2(n3e_1_out_2));
  Multiplexer #(.width(7), .enable("false")) multiplexer_9 (
    .in0(n2e_1_out_2), .in1(n3e_1_out_2), .out(multiplexer_9_out), .sel(in_12));
  _2f u_2f_1 (.in_1(in_10), .out_2(n2f_1_out_2));
  _3f u_3f_1 (.in_1(in_10), .out_2(n3f_1_out_2));
  Multiplexer #(.width(7), .enable("false")) multiplexer_10 (
    .in0(n2f_1_out_2), .in1(n3f_1_out_2), .out(multiplexer_10_out), .sel(in_12));
  or or_2 (or_2_out, in_11, in_12);
endmodule

module _61 (
  input  in_1,
  input  in_2,
  input  in_3,
  input  in_4,
  input  in_5,
  input  in_6,
  input  in_7,
  input  in_8,
  input  in_9,
  input  in_10,
  output [6:0] out_11
);

  wire [6:0] n2a_1_out_2, n5e_1_out_2, n21_1_out_2, n26_1_out_2, n28_1_out_2, n29_1_out_2, n40_1_out_2,
       part_1_out_2, part_2_out_2, part_3_out_2;

  _29 u_29_1 (.in_1(in_1), .out_2(n29_1_out_2));
  _28 u_28_1 (.in_1(in_2), .out_2(n28_1_out_2));
  _2a u_2a_1 (.in_1(in_3), .out_2(n2a_1_out_2));
  _26 u_26_1 (.in_1(in_4), .out_2(n26_1_out_2));
  _5e u_5e_1 (.in_1(in_5), .out_2(n5e_1_out_2));
  circuit_2_2_2 part_1 (.in_1(in_6), .out_2(part_1_out_2));
  circuit_2_2 part_2 (.in_1(in_7), .out_2(part_2_out_2));
  circuit_2 part_3 (.in_1(in_8), .out_2(part_3_out_2));
  _40 u_40_1 (.in_1(in_9), .out_2(n40_1_out_2));
  _21 u_21_1 (.in_1(in_10), .out_2(n21_1_out_2));
  assign out_11 = n29_1_out_2 | n28_1_out_2 | n2a_1_out_2 | n26_1_out_2 | n5e_1_out_2 | part_1_out_2 | part_2_out_2 | part_3_out_2 | n40_1_out_2 | n21_1_out_2;  // OR_Gate or_1, 7 bits wide
endmodule

module _1 (
  input  in_1,
  output [6:0] out_2
);


  assign out_2 = {1'b0, {2{in_1}}, 3'b000, in_1};
endmodule

module _2 (
  input  in_1,
  output [6:0] out_2
);


  assign out_2 = {1'b0, {2{in_1}}, 2'b00, in_1, 1'b0};
endmodule

module _3 (
  input  in_1,
  output [6:0] out_2
);


  assign out_2 = {1'b0, {2{in_1}}, 2'b00, {2{in_1}}};
endmodule

module _4 (
  input  in_1,
  output [6:0] out_2
);


  assign out_2 = {1'b0, {2{in_1}}, 1'b0, in_1, 2'b00};
endmodule

module _5 (
  input  in_1,
  output [6:0] out_2
);


  assign out_2 = {1'b0, {2{in_1}}, 1'b0, in_1, 1'b0, in_1};
endmodule

module _6 (
  input  in_1,
  output [6:0] out_2
);


  assign out_2 = {1'b0, {2{in_1}}, 1'b0, {2{in_1}}, 1'b0};
endmodule

module _7 (
  input  in_1,
  output [6:0] out_2
);


  assign out_2 = {1'b0, {2{in_1}}, 1'b0, {3{in_1}}};
endmodule

module _8 (
  input  in_1,
  output [6:0] out_2
);


  assign out_2 = {1'b0, {3{in_1}}, 3'b000};
endmodule

module _9 (
  input  in_1,
  output [6:0] out_2
);


  assign out_2 = {1'b0, {3{in_1}}, 2'b00, in_1};
endmodule

module _0 (
  input  in_1,
  output [6:0] out_2
);


  assign out_2 = {1'b0, {2{in_1}}, 4'b0000};
endmodule

module ariumi_0_9 (
  input  in_1,
  input  in_2,
  input  in_3,
  input  in_4,
  input  in_5,
  input  in_6,
  input  in_7,
  input  in_8,
  input  in_9,
  input  in_10,
  output [6:0] out_11
);

  wire [6:0] n0_1_out_2, n1_1_out_2, n2_1_out_2, n3_1_out_2, n4_1_out_2, n5_1_out_2, n6_1_out_2, n7_1_out_2,
       n8_1_out_2, n9_1_out_2;

  _1 u_1_1 (.in_1(in_1), .out_2(n1_1_out_2));
  _2 u_2_1 (.in_1(in_2), .out_2(n2_1_out_2));
  _3 u_3_1 (.in_1(in_3), .out_2(n3_1_out_2));
  _4 u_4_1 (.in_1(in_4), .out_2(n4_1_out_2));
  _5 u_5_1 (.in_1(in_5), .out_2(n5_1_out_2));
  _6 u_6_1 (.in_1(in_6), .out_2(n6_1_out_2));
  _7 u_7_1 (.in_1(in_7), .out_2(n7_1_out_2));
  _8 u_8_1 (.in_1(in_8), .out_2(n8_1_out_2));
  _9 u_9_1 (.in_1(in_9), .out_2(n9_1_out_2));
  _0 u_0_1 (.in_1(in_10), .out_2(n0_1_out_2));
  assign out_11 = n1_1_out_2 | n2_1_out_2 | n3_1_out_2 | n4_1_out_2 | n5_1_out_2 | n6_1_out_2 | n7_1_out_2 | n8_1_out_2 | n9_1_out_2 | n0_1_out_2;  // OR_Gate or_1, 7 bits wide
endmodule

module enter (
  input  in_1,
  output [6:0] out_2
);


  assign out_2 = {3'b000, {2{in_1}}, 1'b0, in_1};
endmodule

module _21 (
  input  in_1,
  output [6:0] out_2
);


  assign out_2 = {1'b0, in_1, 4'b0000, in_1};
endmodule

module circuit (
  input  in_1,
  output [6:0] out_2
);


  assign out_2 = {1'b0, in_1, 3'b000, in_1, 1'b0};
endmodule

module circuit_2 (
  input  in_1,
  output [6:0] out_2
);


  assign out_2 = {1'b0, in_1, 3'b000, {2{in_1}}};
endmodule

module circuit_2_2 (
  input  in_1,
  output [6:0] out_2
);

  wire [6:0] register_1_q;

  Register #(.width(7)) register_1 (.Q(register_1_q));  // open: D, en, clk, clr

  assign out_2 = {1'b0, in_1, 2'b00, in_1, 2'b00};
endmodule

module circuit_2_2_2 (
  input  in_1,
  output [6:0] out_2
);


  assign out_2 = {1'b0, in_1, 2'b00, in_1, 1'b0, in_1};
endmodule

module _26 (
  input  in_1,
  output [6:0] out_2
);

  wire [6:0] register_1_q;

  Register #(.width(7)) register_1 (.Q(register_1_q));  // open: D, en, clk, clr

  assign out_2 = {1'b0, in_1, 2'b00, {2{in_1}}, 1'b0};
endmodule

module _27 (
  input  in_1,
  output [6:0] out_2
);

  wire [6:0] register_1_q;

  Register #(.width(7)) register_1 (.Q(register_1_q));  // open: D, en, clk, clr

  assign out_2 = {1'b0, in_1, 2'b00, {3{in_1}}};
endmodule

module _28 (
  input  in_1,
  output [6:0] out_2
);

  wire [6:0] register_1_q;

  Register #(.width(7)) register_1 (.Q(register_1_q));  // open: D, en, clk, clr

  assign out_2 = {1'b0, in_1, 1'b0, in_1, 3'b000};
endmodule

module _29 (
  input  in_1,
  output [6:0] out_2
);

  wire [6:0] register_1_q;

  Register #(.width(7)) register_1 (.Q(register_1_q));  // open: D, en, clk, clr

  assign out_2 = {1'b0, in_1, 1'b0, in_1, 2'b00, in_1};
endmodule

module _2a (
  input  in_1,
  output [6:0] out_2
);

  wire [6:0] register_1_q;

  Register #(.width(7)) register_1 (.Q(register_1_q));  // open: D, en, clk, clr

  assign out_2 = {1'b0, in_1, 1'b0, in_1, 1'b0, in_1, 1'b0};
endmodule

module _2b (
  input  in_1,
  output [6:0] out_2
);

  wire [6:0] register_1_q;

  Register #(.width(7)) register_1 (.Q(register_1_q));  // open: D, en, clk, clr

  assign out_2 = {1'b0, in_1, 1'b0, in_1, 1'b0, {2{in_1}}};
endmodule

module _2c (
  input  in_1,
  output [6:0] out_2
);

  wire [6:0] register_1_q;

  Register #(.width(7)) register_1 (.Q(register_1_q));  // open: D, en, clk, clr

  assign out_2 = {1'b0, in_1, 1'b0, {2{in_1}}, 2'b00};
endmodule

module _2d (
  input  in_1,
  output [6:0] out_2
);

  wire [6:0] register_1_q;

  Register #(.width(7)) register_1 (.Q(register_1_q));  // open: D, en, clk, clr

  assign out_2 = {1'b0, in_1, 1'b0, {2{in_1}}, 1'b0, in_1};
endmodule

module _2e (
  input  in_1,
  output [6:0] out_2
);

  wire [6:0] register_1_q;

  Register #(.width(7)) register_1 (.Q(register_1_q));  // open: D, en, clk, clr

  assign out_2 = {1'b0, in_1, 1'b0, {3{in_1}}, 1'b0};
endmodule

module _2f (
  input  in_1,
  output [6:0] out_2
);

  wire [6:0] register_1_q;

  Register #(.width(7)) register_1 (.Q(register_1_q));  // open: D, en, clk, clr

  assign out_2 = {1'b0, in_1, 1'b0, {4{in_1}}};
endmodule

module _3a (
  input  in_1,
  output [6:0] out_2
);

  wire [6:0] register_1_q;

  Register #(.width(7)) register_1 (.Q(register_1_q));  // open: D, en, clk, clr

  assign out_2 = {1'b0, {3{in_1}}, 1'b0, in_1, 1'b0};
endmodule

module _3b (
  input  in_1,
  output [6:0] out_2
);

  wire [6:0] register_1_q;

  Register #(.width(7)) register_1 (.Q(register_1_q));  // open: D, en, clk, clr

  assign out_2 = {1'b0, {3{in_1}}, 1'b0, {2{in_1}}};
endmodule

module _3c (
  input  in_1,
  output [6:0] out_2
);

  wire [6:0] register_1_q;

  Register #(.width(7)) register_1 (.Q(register_1_q));  // open: D, en, clk, clr

  assign out_2 = {1'b0, {4{in_1}}, 2'b00};
endmodule

module _3d (
  input  in_1,
  output [6:0] out_2
);

  wire [6:0] register_1_q;

  Register #(.width(7)) register_1 (.Q(register_1_q));  // open: D, en, clk, clr

  assign out_2 = {1'b0, {4{in_1}}, 1'b0, in_1};
endmodule

module _3e (
  input  in_1,
  output [6:0] out_2
);

  wire [6:0] register_1_q;

  Register #(.width(7)) register_1 (.Q(register_1_q));  // open: D, en, clk, clr

  assign out_2 = {1'b0, {5{in_1}}, 1'b0};
endmodule

module _3f (
  input  in_1,
  output [6:0] out_2
);

  wire [6:0] register_1_q;

  Register #(.width(7)) register_1 (.Q(register_1_q));  // open: D, en, clk, clr

  assign out_2 = {1'b0, {6{in_1}}};
endmodule

module _40 (
  input  in_1,
  output [6:0] out_2
);

  wire [6:0] register_1_q;

  Register #(.width(7)) register_1 (.Q(register_1_q));  // open: D, en, clk, clr

  assign out_2 = {in_1, {6{1'b0}}};
endmodule

module A_41 (
  input  in_1,
  output [6:0] out_2
);

  wire [6:0] register_1_q;

  Register #(.width(7)) register_1 (.Q(register_1_q));  // open: D, en, clk, clr

  assign out_2 = {in_1, {5{1'b0}}, in_1};
endmodule

module B_42 (
  input  in_1,
  output [6:0] out_2
);

  wire [6:0] register_1_q;

  Register #(.width(7)) register_1 (.Q(register_1_q));  // open: D, en, clk, clr

  assign out_2 = {in_1, 4'b0000, in_1, 1'b0};
endmodule

module C_43 (
  input  in_1,
  output [6:0] out_2
);

  wire [6:0] register_1_q;

  Register #(.width(7)) register_1 (.Q(register_1_q));  // open: D, en, clk, clr

  assign out_2 = {in_1, 4'b0000, {2{in_1}}};
endmodule

module D_44 (
  input  in_1,
  output [6:0] out_2
);

  wire [6:0] register_1_q;

  Register #(.width(7)) register_1 (.Q(register_1_q));  // open: D, en, clk, clr

  assign out_2 = {in_1, 3'b000, in_1, 2'b00};
endmodule

module E_45 (
  input  in_1,
  output [6:0] out_2
);

  wire [6:0] register_1_q;

  Register #(.width(7)) register_1 (.Q(register_1_q));  // open: D, en, clk, clr

  assign out_2 = {in_1, 3'b000, in_1, 1'b0, in_1};
endmodule

module F_46 (
  input  in_1,
  output [6:0] out_2
);

  wire [6:0] register_1_q;

  Register #(.width(7)) register_1 (.Q(register_1_q));  // open: D, en, clk, clr

  assign out_2 = {in_1, 3'b000, {2{in_1}}, 1'b0};
endmodule

module G_47 (
  input  in_1,
  output [6:0] out_2
);

  wire [6:0] register_1_q;

  Register #(.width(7)) register_1 (.Q(register_1_q));  // open: D, en, clk, clr

  assign out_2 = {in_1, 3'b000, {3{in_1}}};
endmodule

module H_48 (
  input  in_1,
  output [6:0] out_2
);

  wire [6:0] register_1_q;

  Register #(.width(7)) register_1 (.Q(register_1_q));  // open: D, en, clk, clr

  assign out_2 = {in_1, 2'b00, in_1, 3'b000};
endmodule

module I_49 (
  input  in_1,
  output [6:0] out_2
);

  wire [6:0] register_1_q;

  Register #(.width(7)) register_1 (.Q(register_1_q));  // open: D, en, clk, clr

  assign out_2 = {in_1, 2'b00, in_1, 2'b00, in_1};
endmodule

module J_4a (
  input  in_1,
  output [6:0] out_2
);

  wire [6:0] register_1_q;

  Register #(.width(7)) register_1 (.Q(register_1_q));  // open: D, en, clk, clr

  assign out_2 = {in_1, 2'b00, in_1, 1'b0, in_1, 1'b0};
endmodule

module K_4b (
  input  in_1,
  output [6:0] out_2
);

  wire [6:0] register_1_q;

  Register #(.width(7)) register_1 (.Q(register_1_q));  // open: D, en, clk, clr

  assign out_2 = {in_1, 2'b00, in_1, 1'b0, {2{in_1}}};
endmodule

module L_4c (
  input  in_1,
  output [6:0] out_2
);

  wire [6:0] register_1_q;

  Register #(.width(7)) register_1 (.Q(register_1_q));  // open: D, en, clk, clr

  assign out_2 = {in_1, 2'b00, {2{in_1}}, 2'b00};
endmodule

module M_4d (
  input  in_1,
  output [6:0] out_2
);

  wire [6:0] register_1_q;

  Register #(.width(7)) register_1 (.Q(register_1_q));  // open: D, en, clk, clr

  assign out_2 = {in_1, 2'b00, {2{in_1}}, 1'b0, in_1};
endmodule

module N_4e (
  input  in_1,
  output [6:0] out_2
);

  wire [6:0] register_1_q;

  Register #(.width(7)) register_1 (.Q(register_1_q));  // open: D, en, clk, clr

  assign out_2 = {in_1, 2'b00, {3{in_1}}, 1'b0};
endmodule

module O_4f (
  input  in_1,
  output [6:0] out_2
);

  wire [6:0] register_1_q;

  Register #(.width(7)) register_1 (.Q(register_1_q));  // open: D, en, clk, clr

  assign out_2 = {in_1, 2'b00, {4{in_1}}};
endmodule

module P_50 (
  input  in_1,
  output [6:0] out_2
);

  wire [6:0] register_1_q;

  Register #(.width(7)) register_1 (.Q(register_1_q));  // open: D, en, clk, clr

  assign out_2 = {in_1, 1'b0, in_1, 4'b0000};
endmodule

module Q_51 (
  input  in_1,
  output [6:0] out_2
);

  wire [6:0] register_1_q;

  Register #(.width(7)) register_1 (.Q(register_1_q));  // open: D, en, clk, clr

  assign out_2 = {in_1, 1'b0, in_1, 3'b000, in_1};
endmodule

module R_52 (
  input  in_1,
  output [6:0] out_2
);

  wire [6:0] register_1_q;

  Register #(.width(7)) register_1 (.Q(register_1_q));  // open: D, en, clk, clr

  assign out_2 = {in_1, 1'b0, in_1, 2'b00, in_1, 1'b0};
endmodule

module S_53 (
  input  in_1,
  output [6:0] out_2
);

  wire [6:0] register_1_q;

  Register #(.width(7)) register_1 (.Q(register_1_q));  // open: D, en, clk, clr

  assign out_2 = {in_1, 1'b0, in_1, 2'b00, {2{in_1}}};
endmodule

module T_54 (
  input  in_1,
  output [6:0] out_2
);

  wire [6:0] register_1_q;

  Register #(.width(7)) register_1 (.Q(register_1_q));  // open: D, en, clk, clr

  assign out_2 = {in_1, 1'b0, in_1, 1'b0, in_1, 2'b00};
endmodule

module U_55 (
  input  in_1,
  output [6:0] out_2
);

  wire [6:0] register_1_q;

  Register #(.width(7)) register_1 (.Q(register_1_q));  // open: D, en, clk, clr

  assign out_2 = {in_1, 1'b0, in_1, 1'b0, in_1, 1'b0, in_1};
endmodule

module V_56 (
  input  in_1,
  output [6:0] out_2
);

  wire [6:0] register_1_q;

  Register #(.width(7)) register_1 (.Q(register_1_q));  // open: D, en, clk, clr

  assign out_2 = {in_1, 1'b0, in_1, 1'b0, {2{in_1}}, 1'b0};
endmodule

module W_57 (
  input  in_1,
  output [6:0] out_2
);

  wire [6:0] register_1_q;

  Register #(.width(7)) register_1 (.Q(register_1_q));  // open: D, en, clk, clr

  assign out_2 = {in_1, 1'b0, in_1, 1'b0, {3{in_1}}};
endmodule

module X_58 (
  input  in_1,
  output [6:0] out_2
);

  wire [6:0] register_1_q;

  Register #(.width(7)) register_1 (.Q(register_1_q));  // open: D, en, clk, clr

  assign out_2 = {in_1, 1'b0, {2{in_1}}, 3'b000};
endmodule

module Y_59 (
  input  in_1,
  output [6:0] out_2
);

  wire [6:0] register_1_q;

  Register #(.width(7)) register_1 (.Q(register_1_q));  // open: D, en, clk, clr

  assign out_2 = {in_1, 1'b0, {2{in_1}}, 2'b00, in_1};
endmodule

module Z_5a (
  input  in_1,
  output [6:0] out_2
);

  wire [6:0] register_1_q;

  Register #(.width(7)) register_1 (.Q(register_1_q));  // open: D, en, clk, clr

  assign out_2 = {in_1, 1'b0, {2{in_1}}, 1'b0, in_1, 1'b0};
endmodule

module _5b (
  input  in_1,
  output [6:0] out_2
);

  wire [6:0] register_1_q;

  Register #(.width(7)) register_1 (.Q(register_1_q));  // open: D, en, clk, clr

  assign out_2 = {in_1, 1'b0, {2{in_1}}, 1'b0, {2{in_1}}};
endmodule

module _5c (
  input  in_1,
  output [6:0] out_2
);

  wire [6:0] register_1_q;

  Register #(.width(7)) register_1 (.Q(register_1_q));  // open: D, en, clk, clr

  assign out_2 = {in_1, 1'b0, {3{in_1}}, 2'b00};
endmodule

module _5d (
  input  in_1,
  output [6:0] out_2
);

  wire [6:0] register_1_q;

  Register #(.width(7)) register_1 (.Q(register_1_q));  // open: D, en, clk, clr

  assign out_2 = {in_1, 1'b0, {3{in_1}}, 1'b0, in_1};
endmodule

module _5e (
  input  in_1,
  output [6:0] out_2
);

  wire [6:0] register_1_q;

  Register #(.width(7)) register_1 (.Q(register_1_q));  // open: D, en, clk, clr

  assign out_2 = {in_1, 1'b0, {4{in_1}}, 1'b0};
endmodule

module _5f (
  input  in_1,
  output [6:0] out_2
);

  wire [6:0] register_1_q;

  Register #(.width(7)) register_1 (.Q(register_1_q));  // open: D, en, clk, clr

  assign out_2 = {in_1, 1'b0, {5{in_1}}};
endmodule

module _60 (
  input  in_1,
  output [6:0] out_2
);

  wire [6:0] register_1_q;

  Register #(.width(7)) register_1 (.Q(register_1_q));  // open: D, en, clk, clr

  assign out_2 = {{2{in_1}}, {5{1'b0}}};
endmodule

module a_61 (
  input  in_1,
  output [6:0] out_2
);

  wire [6:0] register_1_q;

  Register #(.width(7)) register_1 (.Q(register_1_q));  // open: D, en, clk, clr

  assign out_2 = {{2{in_1}}, 4'b0000, in_1};
endmodule

module b_62 (
  input  in_1,
  output [6:0] out_2
);

  wire [6:0] register_1_q;

  Register #(.width(7)) register_1 (.Q(register_1_q));  // open: D, en, clk, clr

  assign out_2 = {{2{in_1}}, 3'b000, in_1, 1'b0};
endmodule

module c_63 (
  input  in_1,
  output [6:0] out_2
);

  wire [6:0] register_1_q;

  Register #(.width(7)) register_1 (.Q(register_1_q));  // open: D, en, clk, clr

  assign out_2 = {{2{in_1}}, 3'b000, {2{in_1}}};
endmodule

module d_64 (
  input  in_1,
  output [6:0] out_2
);

  wire [6:0] register_1_q;

  Register #(.width(7)) register_1 (.Q(register_1_q));  // open: D, en, clk, clr

  assign out_2 = {{2{in_1}}, 2'b00, in_1, 2'b00};
endmodule

module e_65 (
  input  in_1,
  output [6:0] out_2
);

  wire [6:0] register_1_q;

  Register #(.width(7)) register_1 (.Q(register_1_q));  // open: D, en, clk, clr

  assign out_2 = {{2{in_1}}, 2'b00, in_1, 1'b0, in_1};
endmodule

module f_66 (
  input  in_1,
  output [6:0] out_2
);

  wire [6:0] register_1_q;

  Register #(.width(7)) register_1 (.Q(register_1_q));  // open: D, en, clk, clr

  assign out_2 = {{2{in_1}}, 2'b00, {2{in_1}}, 1'b0};
endmodule

module g_67 (
  input  in_1,
  output [6:0] out_2
);

  wire [6:0] register_1_q;

  Register #(.width(7)) register_1 (.Q(register_1_q));  // open: D, en, clk, clr

  assign out_2 = {{2{in_1}}, 2'b00, {3{in_1}}};
endmodule

module h_68 (
  input  in_1,
  output [6:0] out_2
);

  wire [6:0] register_1_q;

  Register #(.width(7)) register_1 (.Q(register_1_q));  // open: D, en, clk, clr

  assign out_2 = {{2{in_1}}, 1'b0, in_1, 3'b000};
endmodule

module i_69 (
  input  in_1,
  output [6:0] out_2
);

  wire [6:0] register_1_q;

  Register #(.width(7)) register_1 (.Q(register_1_q));  // open: D, en, clk, clr

  assign out_2 = {{2{in_1}}, 1'b0, in_1, 2'b00, in_1};
endmodule

module j_6a (
  input  in_1,
  output [6:0] out_2
);

  wire [6:0] register_1_q;

  Register #(.width(7)) register_1 (.Q(register_1_q));  // open: D, en, clk, clr

  assign out_2 = {{2{in_1}}, 1'b0, in_1, 1'b0, in_1, 1'b0};
endmodule

module k_6b (
  input  in_1,
  output [6:0] out_2
);

  wire [6:0] register_1_q;

  Register #(.width(7)) register_1 (.Q(register_1_q));  // open: D, en, clk, clr

  assign out_2 = {{2{in_1}}, 1'b0, in_1, 1'b0, {2{in_1}}};
endmodule

module l_6c (
  input  in_1,
  output [6:0] out_2
);

  wire [6:0] register_1_q;

  Register #(.width(7)) register_1 (.Q(register_1_q));  // open: D, en, clk, clr

  assign out_2 = {{2{in_1}}, 1'b0, {2{in_1}}, 2'b00};
endmodule

module m_6d (
  input  in_1,
  output [6:0] out_2
);

  wire [6:0] register_1_q;

  Register #(.width(7)) register_1 (.Q(register_1_q));  // open: D, en, clk, clr

  assign out_2 = {{2{in_1}}, 1'b0, {2{in_1}}, 1'b0, in_1};
endmodule

module n_6e (
  input  in_1,
  output [6:0] out_2
);

  wire [6:0] register_1_q;

  Register #(.width(7)) register_1 (.Q(register_1_q));  // open: D, en, clk, clr

  assign out_2 = {{2{in_1}}, 1'b0, {3{in_1}}, 1'b0};
endmodule

module o_6f (
  input  in_1,
  output [6:0] out_2
);

  wire [6:0] register_1_q;

  Register #(.width(7)) register_1 (.Q(register_1_q));  // open: D, en, clk, clr

  assign out_2 = {{2{in_1}}, 1'b0, {4{in_1}}};
endmodule

module p_70 (
  input  in_1,
  output [6:0] out_2
);

  wire [6:0] register_1_q;

  Register #(.width(7)) register_1 (.Q(register_1_q));  // open: D, en, clk, clr

  assign out_2 = {{3{in_1}}, 4'b0000};
endmodule

module q_71 (
  input  in_1,
  output [6:0] out_2
);

  wire [6:0] register_1_q;

  Register #(.width(7)) register_1 (.Q(register_1_q));  // open: D, en, clk, clr

  assign out_2 = {{3{in_1}}, 3'b000, in_1};
endmodule

module r_72 (
  input  in_1,
  output [6:0] out_2
);

  wire [6:0] register_1_q;

  Register #(.width(7)) register_1 (.Q(register_1_q));  // open: D, en, clk, clr

  assign out_2 = {{3{in_1}}, 2'b00, in_1, 1'b0};
endmodule

module s_73 (
  input  in_1,
  output [6:0] out_2
);

  wire [6:0] register_1_q;

  Register #(.width(7)) register_1 (.Q(register_1_q));  // open: D, en, clk, clr

  assign out_2 = {{3{in_1}}, 2'b00, {2{in_1}}};
endmodule

module t_74 (
  input  in_1,
  output [6:0] out_2
);

  wire [6:0] register_1_q;

  Register #(.width(7)) register_1 (.Q(register_1_q));  // open: D, en, clk, clr

  assign out_2 = {{3{in_1}}, 1'b0, in_1, 2'b00};
endmodule

module u_75 (
  input  in_1,
  output [6:0] out_2
);

  wire [6:0] register_1_q;

  Register #(.width(7)) register_1 (.Q(register_1_q));  // open: D, en, clk, clr

  assign out_2 = {{3{in_1}}, 1'b0, in_1, 1'b0, in_1};
endmodule

module v_76 (
  input  in_1,
  output [6:0] out_2
);

  wire [6:0] register_1_q;

  Register #(.width(7)) register_1 (.Q(register_1_q));  // open: D, en, clk, clr

  assign out_2 = {{3{in_1}}, 1'b0, {2{in_1}}, 1'b0};
endmodule

module w_77 (
  input  in_1,
  output [6:0] out_2
);

  wire [6:0] register_1_q;

  Register #(.width(7)) register_1 (.Q(register_1_q));  // open: D, en, clk, clr

  assign out_2 = {{3{in_1}}, 1'b0, {3{in_1}}};
endmodule

module x_78 (
  input  in_1,
  output [6:0] out_2
);

  wire [6:0] register_1_q;

  Register #(.width(7)) register_1 (.Q(register_1_q));  // open: D, en, clk, clr

  assign out_2 = {{4{in_1}}, 3'b000};
endmodule

module y_79 (
  input  in_1,
  output [6:0] out_2
);

  wire [6:0] register_1_q;

  Register #(.width(7)) register_1 (.Q(register_1_q));  // open: D, en, clk, clr

  assign out_2 = {{4{in_1}}, 2'b00, in_1};
endmodule

module z_7a (
  input  in_1,
  output [6:0] out_2
);

  wire [6:0] register_1_q;

  Register #(.width(7)) register_1 (.Q(register_1_q));  // open: D, en, clk, clr

  assign out_2 = {{4{in_1}}, 1'b0, in_1, 1'b0};
endmodule

module _7b (
  input  in_1,
  output [6:0] out_2
);

  wire [6:0] register_1_q;

  Register #(.width(7)) register_1 (.Q(register_1_q));  // open: D, en, clk, clr

  assign out_2 = {{4{in_1}}, 1'b0, {2{in_1}}};
endmodule

module _7c (
  input  in_1,
  output [6:0] out_2
);

  wire [6:0] register_1_q;

  Register #(.width(7)) register_1 (.Q(register_1_q));  // open: D, en, clk, clr

  assign out_2 = {{5{in_1}}, 2'b00};
endmodule

module _7d (
  input  in_1,
  output [6:0] out_2
);

  wire [6:0] register_1_q;

  Register #(.width(7)) register_1 (.Q(register_1_q));  // open: D, en, clk, clr

  assign out_2 = {{5{in_1}}, 1'b0, in_1};
endmodule

module _7e (
  input  in_1,
  output [6:0] out_2
);

  wire [6:0] register_1_q;

  Register #(.width(7)) register_1 (.Q(register_1_q));  // open: D, en, clk, clr

  assign out_2 = {{6{in_1}}, 1'b0};
endmodule

module Backspace_08 (
  input  in_1,
  output [6:0] out_2
);

  wire [6:0] register_1_q;

  Register #(.width(7)) register_1 (.Q(register_1_q));  // open: D, en, clk, clr

  assign out_2 = {3'b000, in_1, 3'b000};
endmodule

module diagrah_sel_0c (
  input  in_1,
  output [6:0] out_2
);

  wire [6:0] register_1_q;

  Register #(.width(7)) register_1 (.Q(register_1_q));  // open: D, en, clk, clr

  assign out_2 = {3'b000, {2{in_1}}, 2'b00};
endmodule

module spahs (
  input  in_1,
  output [6:0] out_2
);


  assign out_2 = {1'b0, in_1, {5{1'b0}}};
endmodule

module HY_120 (
  input  in_1,
  input  in_2,
  input  in_3,
  input  in_4,
  input  in_5,
  input  in_6,
  input  in_7,
  input  in_8,
  input  in_9,
  input  in_10,
  input  in_11,
  input  in_12,
  input  in_13,
  input  in_14,
  input  in_15,
  input  in_16,
  input  in_17,
  input  in_18,
  input  in_19,
  input  in_20,
  input  in_21,
  input  in_22,
  input  in_23,
  input  in_24,
  input  in_25,
  input  in_26,
  input  [7:0] in_27,
  input  [7:0] in_28,
  output out_29,
  output out_30,
  output out_31,
  output out_32,
  output out_33,
  output out_34,
  output out_35,
  output out_36,
  output out_37,
  output out_38,
  output out_39,
  output out_40,
  output [7:0] out_41
);

  wire button_1_out, not_1_out;
  wire [3:0] multiplexer_1_out, multiplexer_1_out_2, multiplexer_2_out, multiplexer_2_out_2, register_3_q,
       register_3_q_2, rom_1_data, \αθηζη_και_αφερη_1_out_4 , \αθηζη_και_αφερη_1_out_4_2 ;
  wire [7:0] adder_1_out, adder_2_out, controlled_buffer_3_out, controlled_buffer_7_out, kataxoriths_1_out_3,
       ram_1_data, register_1_q, register_2_q, register_4_q;
  wire [7:4] rom_1_data_2;

  Register register_1 (.D(adder_1_out), .Q(register_1_q), .clk(button_1_out));  // open: en, clr
  Adder adder_1 (.a(register_1_q), .b(8'h1), .out(adder_1_out));  // open: cin, cout
  assign in_15 = in_1 ? in_1 : 1'bz;  // Controlled_Buffer controlled_buffer_1
  Multiplexer #(.width(8), .enable("false")) multiplexer_1 (
    .in0(register_1_q), .in1(controlled_buffer_3_out), .out({multiplexer_1_out_2, multiplexer_1_out}),
    .sel(in_15));
  Hex_Digit_Display hex_digit_display_1 (.value(multiplexer_1_out));  // open: dp
  Hex_Digit_Display hex_digit_display_2 (.value(multiplexer_1_out_2));  // open: dp
  assign in_14 = in_2 ? in_2 : 1'bz;  // Controlled_Buffer controlled_buffer_2
  Hex_Digit_Display hex_digit_display_3 (.value(register_2_q[7:4]));  // open: dp
  Register #(.trigger("low")) register_2 (
    .D({multiplexer_1_out_2, multiplexer_1_out}), .Q(register_2_q), .clk(in_14));  // open: en, clr
  Hex_Digit_Display hex_digit_display_4 (.value(register_2_q[3:0]));  // open: dp
  Hex_Digit_Display hex_digit_display_5 (.value(rom_1_data_2));  // open: dp
  ROM rom_1 (.addr(register_2_q), .data({rom_1_data_2, rom_1_data}));  // open: sel
  DotMatrix #(.matrixcols(4), .matrixrows(1), .dotshape("circle")) dotmatrix_1 (
    .col0(rom_1_data[3]), .col1(rom_1_data[2]), .col2(rom_1_data[1]), .col3(rom_1_data[0]));
  Hex_Digit_Display hex_digit_display_6 (.value(controlled_buffer_3_out[3:0]));  // open: dp
  Hex_Digit_Display hex_digit_display_7 (.value(controlled_buffer_3_out[7:4]));  // open: dp
  Hex_Digit_Display hex_digit_display_8 (.value(rom_1_data));  // open: dp
  assign controlled_buffer_3_out = in_16 ? {rom_1_data_2, rom_1_data} : 8'bz;  // Controlled_Buffer controlled_buffer_3
  assign in_16 = in_3 ? in_3 : 1'bz;  // Controlled_Buffer controlled_buffer_4
  kataxoriths kataxoriths_1 (.in_1(controlled_buffer_3_out), .in_2(in_16), .out_3(kataxoriths_1_out_3));
  assign in_17 = in_4 ? in_4 : 1'bz;  // Controlled_Buffer controlled_buffer_5
  Hex_Digit_Display hex_digit_display_9 (.value(multiplexer_2_out_2));  // open: dp
  Multiplexer #(.width(8), .enable("false")) multiplexer_2 (
    .in0({rom_1_data_2, rom_1_data}), .in1(kataxoriths_1_out_3),
    .out({multiplexer_2_out_2, multiplexer_2_out}), .sel(in_17));
  Hex_Digit_Display hex_digit_display_10 (.value(kataxoriths_1_out_3[3:0]));  // open: dp
  Hex_Digit_Display hex_digit_display_11 (.value(kataxoriths_1_out_3[7:4]));  // open: dp
  Button button_1 (.out(button_1_out));
  assign in_19 = in_8 ? in_8 : 1'bz;  // Controlled_Buffer controlled_buffer_6
  Hex_Digit_Display hex_digit_display_12 (.value(multiplexer_2_out));  // open: dp
  assign controlled_buffer_7_out = in_19 ? {multiplexer_2_out_2, multiplexer_2_out} : 8'bz;  // Controlled_Buffer controlled_buffer_7
  assign controlled_buffer_7_out = not_1_out ? controlled_buffer_3_out : 8'bz;  // Controlled_Buffer controlled_buffer_8
  not not_1 (not_1_out, in_19);
  Adder adder_2 (.a({register_3_q_2, register_3_q}), .b(8'h1), .out(adder_2_out));  // open: cin, cout
  Hex_Digit_Display hex_digit_display_13 (.value(register_3_q_2));  // open: dp
  Hex_Digit_Display hex_digit_display_14 (.value(register_3_q));  // open: dp
  Register register_3 (
    .D(adder_2_out), .Q({register_3_q_2, register_3_q}), .clk(button_1_out), .clr(in_13));  // open: en
  assign in_18 = in_9 ? in_9 : 1'bz;  // Controlled_Buffer controlled_buffer_9
  RAM ram_1 (.addr(controlled_buffer_7_out), .data(ram_1_data));  // open: sel, clk, ld, clr
  assign controlled_buffer_3_out = in_18 ? ram_1_data : 8'bz;  // Controlled_Buffer controlled_buffer_10
  assign in_22 = in_10 ? in_10 : 1'bz;  // Controlled_Buffer controlled_buffer_11
  \αθηζη_και_αφερη  \u_αθηζη_και_αφερη_1  (
    .in_2({in_22, in_21, in_20}), .in_1(register_4_q), .in_3(controlled_buffer_3_out),
    .out_4({\αθηζη_και_αφερη_1_out_4_2 , \αθηζη_και_αφερη_1_out_4 }));
  assign in_20 = in_12 ? in_12 : 1'bz;  // Controlled_Buffer controlled_buffer_12
  assign in_21 = in_11 ? in_11 : 1'bz;  // Controlled_Buffer controlled_buffer_13
  Hex_Digit_Display hex_digit_display_15 (.value(\αθηζη_και_αφερη_1_out_4_2 ));  // open: dp
  assign in_23 = in_5 ? in_5 : 1'bz;  // Controlled_Buffer controlled_buffer_14
  Hex_Digit_Display hex_digit_display_16 (.value(\αθηζη_και_αφερη_1_out_4 ));  // open: dp
  Hex_Digit_Display hex_digit_display_17 (.value(register_4_q[7:4]));  // open: dp
  Register register_4 (
    .D({\αθηζη_και_αφερη_1_out_4_2 , \αθηζη_και_αφερη_1_out_4 }), .Q(register_4_q), .clr(in_23));  // open: en, clk
  Hex_Digit_Display hex_digit_display_18 (.value(register_4_q[3:0]));  // open: dp
  assign out_41 = ~(register_4_q | register_4_q);  // NOR_Gate nor_1, 8 bits wide
  assign in_24 = in_6 ? in_6 : 1'bz;  // Controlled_Buffer controlled_buffer_15
  assign controlled_buffer_3_out = in_24 ? register_4_q : 8'bz;  // Controlled_Buffer controlled_buffer_16
  assign in_25 = in_7 ? in_7 : 1'bz;  // Controlled_Buffer controlled_buffer_17
  assign controlled_buffer_3_out = in_25 ? in_27 : 8'bz;  // Controlled_Buffer controlled_buffer_18

  assign out_29 = in_14;
  assign out_30 = in_15;
  assign out_31 = in_16;
  assign out_32 = in_17;
  assign out_33 = in_18;
  assign out_34 = in_19;
  assign out_35 = in_20;
  assign out_36 = in_21;
  assign out_37 = in_22;
  assign out_38 = in_23;
  assign out_39 = in_24;
  assign out_40 = in_25;

  // Other names for the same wires on the sheet: aluMd_0 = in_20; aluMd_1 = in_21; aluMd_2 = in_22; acc2bus = in_24;
  //   accLd = in_23; addrMd = in_17; dmRd = in_18; dmWr = in_19; ext2bus = in_25; im2dus = in_16; pc_Ld = in_14;
  //   pc_Md = in_15

  // Notes on the sheet:
  //   contents of rom_1 (hex, n*v repeats v):
  //   0 1 2 3 4 5 6 7 8 9 a b c d e f 10 11 12 13 14 15 16 17 18 19 1a 1b 1c 1d 1e 1f 20 21 22 23 24 25 26
  //   27 28 29 2a 2b 2c 2d 2e 2f 30 31 32 33 34 35 36 37 38 39 3a 3b 3c 3d 3e 3f 40 41 42 43 44 45 46 47
  //   48 49 4a 4b 4c 4d 3e 4f 50 51 52 53 54 55 56 57 58 59 5a 5b 5c 5d 5e 5f 60 61 62 63 64 65 66 67 68
  //   69 6a 6b 6c 6d 6e 6f 70 71 72 73 74 75 76 77 78 79 7a 7b 7c 7d 7e 7f
endmodule

module kataxoriths (
  input  [7:0] in_1,
  input  in_2,
  output [7:0] out_3
);

  Register register_1 (.D(in_1), .Q(out_3), .clk(in_2));  // open: en, clr
endmodule

module \αθηζη_και_αφερη  (
  input  [7:0] in_1,
  input  [2:0] in_2,
  input  [7:0] in_3,
  output [7:0] out_4
);

  wire decoder_1_out0, decoder_1_out2, decoder_1_out3, decoder_1_out5, decoder_1_out7;
  wire [7:0] adder_1_out, negator_1_out, negator_2_out, subtractor_1_out, subtractor_2_out, subtractor_3_out,
       subtractor_4_out;

  Adder adder_1 (.a(in_1), .b(in_3), .out(adder_1_out));  // open: cin, cout
  Subtractor subtractor_1 (.a(in_1), .b(in_3), .out(subtractor_1_out));  // open: bin, bout
  Subtractor subtractor_2 (.a(in_3), .b(in_1), .out(subtractor_2_out));  // open: bin, bout
  Negator negator_1 (.in(in_1), .out(negator_1_out));
  Negator negator_2 (.in(in_3), .out(negator_2_out));
  Subtractor subtractor_3 (.a(negator_1_out), .b(in_3), .out(subtractor_3_out));  // open: bin, bout
  Subtractor subtractor_4 (.a(in_1), .b(negator_2_out), .out(subtractor_4_out));  // open: bin, bout
  Decoder #(.select(3), .enable("false")) decoder_1 (
    .out0(decoder_1_out0), .out2(decoder_1_out2), .out3(decoder_1_out3), .out5(decoder_1_out5),
    .out7(decoder_1_out7), .sel(in_2));  // open: out1, out4, out6
  assign out_4 = decoder_1_out0 ? adder_1_out : 8'bz;  // Controlled_Buffer controlled_buffer_1
  assign out_4 = decoder_1_out2 ? subtractor_1_out : 8'bz;  // Controlled_Buffer controlled_buffer_2
  assign out_4 = decoder_1_out3 ? subtractor_2_out : 8'bz;  // Controlled_Buffer controlled_buffer_3
  assign out_4 = decoder_1_out5 ? subtractor_3_out : 8'bz;  // Controlled_Buffer controlled_buffer_4
  assign out_4 = decoder_1_out7 ? subtractor_4_out : 8'bz;  // Controlled_Buffer controlled_buffer_5
endmodule

module circuit_2_2_2_2 (
  input  [4:0] in_1,
  input  [4:0] in_2,
  input  [4:0] in_3,
  input  [4:0] in_4
);

  TTY tty_1 ();  // open: data, clk, we, clr
  DotMatrix #(.matrixcols(10), .matrixrows(5)) dotmatrix_1 (
    .col0(in_1), .col1(in_2), .col2(in_3), .col3(in_4), .col4({5{1'b0}}), .col5({5{1'b0}}), .col6({5{1'b0}}),
    .col7({5{1'b0}}), .col8({5{1'b0}}), .col9({5{1'b0}}));
endmodule
