// Logisim project πληκρολογιο NEO.circ as structural Verilog: 1 circuit, main circuit πληκρολογιο
module \πληκρολογιο  (
  input  [13:0] in_1,
  input  [11:0] in_2,
  input  [12:0] in_3,
  input  [12:0] in_4,
  input  in_5,
  output [6:0] out_6
);

  wire button_1_out, not_1_out, not_2_out, or_2_out, register_1_q;
  wire [6:0] ariumi_0_9_1_out_11, backspace_08_1_out_2, multiplexer_1_out, multiplexer_2_out,
       multiplexer_3_out, multiplexer_4_out, n2b_1_out_2, n2d_1_out_2, n3d_1_out_2, n5f_1_out_2, n7e_1_out_2,
       n60_1_out_2, n61_1_out_11, spahs_1_out_2, xor_1_out, xor_2_out, \δετερι_1_out_16 , \τεραρτη_1_out_13 ,
       \τριτη_1_out_15 ;

  Multiplexer #(.width(7), .enable("false")) multiplexer_1 (
    .in0(n61_1_out_11), .in1(ariumi_0_9_1_out_11), .out(multiplexer_1_out), .sel(not_1_out));
  assign xor_1_out = multiplexer_1_out ^ xor_2_out;  // XOR_Gate xor_1, 7 bits wide
  _61 u_61_1 (
    .in_1(in_1[3]), .in_2(in_1[4]), .in_3(in_1[5]), .in_4(in_1[6]), .in_5(in_1[7]), .in_6(in_1[8]),
    .in_7(in_1[9]), .in_8(in_1[10]), .in_9(in_1[11]), .in_10(in_1[12]), .out_11(n61_1_out_11));
  not not_1 (not_1_out, or_2_out);
  assign out_6 = xor_1_out | \δετερι_1_out_16  | \τριτη_1_out_15  | \τεραρτη_1_out_13  | spahs_1_out_2;  // OR_Gate or_1, 7 bits wide
  ariumi_0_9 ariumi_0_9_1 (
    .in_1(in_1[12]), .in_2(in_1[11]), .in_3(in_1[10]), .in_4(in_1[9]), .in_5(in_1[8]), .in_6(in_1[7]),
    .in_7(in_1[6]), .in_8(in_1[5]), .in_9(in_1[4]), .in_10(in_1[3]), .out_11(ariumi_0_9_1_out_11));
  Hex_Digit_Display hex_digit_display_1 (.value(out_6[3:0]));  // open: dp
  Hex_Digit_Display hex_digit_display_2 (.value({1'b0, out_6[6:4]}));  // open: dp
  _60 u_60_1 (.in_1(in_1[13]), .out_2(n60_1_out_2));
  Multiplexer #(.width(7), .enable("false")) multiplexer_2 (
    .in0(n60_1_out_2), .in1(n7e_1_out_2), .out(multiplexer_2_out), .sel(or_2_out));
  _2d u_2d_1 (.in_1(in_1[2]), .out_2(n2d_1_out_2));
  _5f u_5f_1 (.in_1(in_1[2]), .out_2(n5f_1_out_2));
  _7e u_7e_1 (.in_1(in_1[13]), .out_2(n7e_1_out_2));
  Multiplexer #(.width(7), .enable("false")) multiplexer_3 (
    .in0(n2d_1_out_2), .in1(n5f_1_out_2), .out(multiplexer_3_out), .sel(or_2_out));
  Button button_1 (.out(button_1_out));
  _3d u_3d_1 (.in_1(in_1[1]), .out_2(n3d_1_out_2));
  Multiplexer #(.width(7), .enable("false")) multiplexer_4 (
    .in0(n3d_1_out_2), .in1(n2b_1_out_2), .out(multiplexer_4_out), .sel(or_2_out));
  ExactlyOne xor_2[6:0] (
    .out(xor_2_out), .in0(multiplexer_2_out), .in1(multiplexer_3_out), .in2(multiplexer_4_out),
    .in3(backspace_08_1_out_2));
  TTY tty_1 (.data(out_6), .clk(button_1_out));  // open: we, clr
  _2b u_2b_1 (.in_1(in_1[1]), .out_2(n2b_1_out_2));
  Backspace_08 backspace_08_1 (.in_1(in_1[0]), .out_2(backspace_08_1_out_2));
  \δετερι  \u_δετερι_1  (
    .in_14(register_1_q), .in_15(or_2_out), .in_1(in_4[12]), .in_2(in_4[11]), .in_3(in_4[10]),
    .in_4(in_4[9]), .in_5(in_4[8]), .in_6(in_4[7]), .in_7(in_4[6]), .in_8(in_4[5]), .in_9(in_4[4]),
    .in_10(in_4[3]), .in_11(in_4[2]), .in_12(in_4[1]), .in_13(in_4[0]), .out_16(\δετερι_1_out_16 ));
  not not_2 (not_2_out, register_1_q);
  Register #(.width(1)) register_1 (.D(not_2_out), .Q(register_1_q), .clk(in_3[12]));  // open: en, clr
  \τριτη  \u_τριτη_1  (
    .in_13(register_1_q), .in_14(or_2_out), .in_1(in_3[11]), .in_2(in_3[10]), .in_3(in_3[9]), .in_4(in_3[8]),
    .in_5(in_3[7]), .in_6(in_3[6]), .in_7(in_3[5]), .in_8(in_3[4]), .in_9(in_3[3]), .in_10(in_3[2]),
    .in_11(in_3[1]), .in_12(in_3[0]), .out_15(\τριτη_1_out_15 ));
  or or_2 (or_2_out, in_2[11], in_2[0]);
  \τεραρτη  \u_τεραρτη_1  (
    .in_11(register_1_q), .in_12(or_2_out), .in_1(in_2[10]), .in_2(in_2[9]), .in_3(in_2[8]), .in_4(in_2[7]),
    .in_5(in_2[6]), .in_6(in_2[5]), .in_7(in_2[4]), .in_8(in_2[3]), .in_9(in_2[2]), .in_10(in_2[1]),
    .out_13(\τεραρτη_1_out_13 ));
  spahs spahs_1 (.in_1(in_5), .out_2(spahs_1_out_2));
endmodule
