// Logisim project πληκρολογιο.circ as structural Verilog: 1 circuit, main circuit πληκρολογιο
module \πληκρολογιο  (
  input  in_1,
  input  in_2,
  input  in_3,
  input  in_4,
  input  in_5,
  input  in_6,
  input  in_7,
  input  in_8,
  input  in_9,
  input  in_10,
  input  in_11,
  input  in_12,
  input  in_13,
  input  in_14,
  input  in_15,
  input  in_16,
  input  in_17,
  input  in_18,
  input  in_19,
  input  in_20,
  input  in_21,
  input  in_22,
  input  in_23,
  input  in_24,
  input  in_25,
  input  in_26,
  input  in_27,
  input  in_28,
  input  in_29,
  input  in_30,
  input  in_31,
  input  in_32,
  input  in_33,
  input  in_34,
  input  in_35,
  input  in_36,
  input  in_37,
  input  in_38,
  input  in_39,
  input  in_40,
  input  in_41,
  input  in_42,
  input  in_43,
  input  in_44,
  input  in_45,
  input  in_46,
  input  in_47,
  input  in_48,
  input  in_49,
  input  in_50,
  input  in_51,
  input  in_52,
  input  in_53,
  output [6:0] out_54
);

  wire button_1_out, not_1_out, not_2_out, or_4_out, register_1_q;
  wire [6:0] ariumi_0_9_1_out_11, backspace_08_1_out_2, multiplexer_1_out, multiplexer_2_out,
       multiplexer_3_out, multiplexer_4_out, n2b_1_out_2, n2d_1_out_2, n3d_1_out_2, n5f_1_out_2, n7e_1_out_2,
       n60_1_out_2, n61_1_out_11, or_1_out, or_3_out, spahs_1_out_2, \δετερι_1_out_16 , \τεραρτη_1_out_13 ,
       \τριτη_1_out_15 ;

  Multiplexer #(.width(7), .enable("false")) multiplexer_1 (
    .in0(n61_1_out_11), .in1(ariumi_0_9_1_out_11), .out(multiplexer_1_out), .sel(not_1_out));
  assign or_1_out = multiplexer_1_out | or_3_out;  // OR_Gate or_1, 7 bits wide
  _61 u_61_1 (
    .in_1(in_11), .in_2(in_10), .in_3(in_9), .in_4(in_8), .in_5(in_7), .in_6(in_6), .in_7(in_5), .in_8(in_4),
    .in_9(in_3), .in_10(in_2), .out_11(n61_1_out_11));
  not not_1 (not_1_out, or_4_out);
  assign out_54 = or_1_out | \δετερι_1_out_16  | \τριτη_1_out_15  | \τεραρτη_1_out_13  | spahs_1_out_2;  // OR_Gate or_2, 7 bits wide
  ariumi_0_9 ariumi_0_9_1 (
    .in_1(in_2), .in_2(in_3), .in_3(in_4), .in_4(in_5), .in_5(in_6), .in_6(in_7), .in_7(in_8), .in_8(in_9),
    .in_9(in_10), .in_10(in_11), .out_11(ariumi_0_9_1_out_11));
  Hex_Digit_Display hex_digit_display_1 (.value({1'b0, out_54[6:4]}));  // open: dp
  Hex_Digit_Display hex_digit_display_2 (.value(out_54[3:0]));  // open: dp
  _60 u_60_1 (.in_1(in_1), .out_2(n60_1_out_2));
  Multiplexer #(.width(7), .enable("false")) multiplexer_2 (
    .in0(n60_1_out_2), .in1(n7e_1_out_2), .out(multiplexer_2_out), .sel(or_4_out));
  _5f u_5f_1 (.in_1(in_12), .out_2(n5f_1_out_2));
  _7e u_7e_1 (.in_1(in_1), .out_2(n7e_1_out_2));
  _2d u_2d_1 (.in_1(in_12), .out_2(n2d_1_out_2));
  Multiplexer #(.width(7), .enable("false")) multiplexer_3 (
    .in0(n2d_1_out_2), .in1(n5f_1_out_2), .out(multiplexer_3_out), .sel(or_4_out));
  Button button_1 (.out(button_1_out));
  _3d u_3d_1 (.in_1(in_13), .out_2(n3d_1_out_2));
  Multiplexer #(.width(7), .enable("false")) multiplexer_4 (
    .in0(n3d_1_out_2), .in1(n2b_1_out_2), .out(multiplexer_4_out), .sel(or_4_out));
  assign or_3_out = multiplexer_2_out | multiplexer_3_out | multiplexer_4_out | backspace_08_1_out_2;  // OR_Gate or_3, 7 bits wide
  TTY tty_1 (.data(out_54), .clk(button_1_out));  // open: we, clr
  _2b u_2b_1 (.in_1(in_13), .out_2(n2b_1_out_2));
  Backspace_08 backspace_08_1 (.in_1(in_14), .out_2(backspace_08_1_out_2));
  \δετερι  \u_δετερι_1  (
    .in_14(register_1_q), .in_15(or_4_out), .in_1(in_15), .in_2(in_16), .in_3(in_17), .in_4(in_18),
    .in_5(in_19), .in_6(in_20), .in_7(in_21), .in_8(in_22), .in_9(in_23), .in_10(in_24), .in_11(in_25),
    .in_12(in_26), .in_13(in_27), .out_16(\δετερι_1_out_16 ));
  not not_2 (not_2_out, register_1_q);
  Register #(.width(1)) register_1 (.D(not_2_out), .Q(register_1_q), .clk(in_28));  // open: en, clr
  \τριτη  \u_τριτη_1  (
    .in_13(register_1_q), .in_14(or_4_out), .in_1(in_29), .in_2(in_30), .in_3(in_31), .in_4(in_32),
    .in_5(in_33), .in_6(in_34), .in_7(in_35), .in_8(in_36), .in_9(in_37), .in_10(in_38), .in_11(in_39),
    .in_12(in_40), .out_15(\τριτη_1_out_15 ));
  or or_4 (or_4_out, in_41, in_52);
  \τεραρτη  \u_τεραρτη_1  (
    .in_11(register_1_q), .in_12(or_4_out), .in_1(in_42), .in_2(in_43), .in_3(in_44), .in_4(in_45),
    .in_5(in_46), .in_6(in_47), .in_7(in_48), .in_8(in_49), .in_9(in_50), .in_10(in_51),
    .out_13(\τεραρτη_1_out_13 ));
  spahs spahs_1 (.in_1(in_53), .out_2(spahs_1_out_2));
endmodule
