// Logisim project χ2.circ as structural Verilog: 103 circuits, main circuit 1
module \δετερι  (
  input  in_1,
  input  in_2,
  input  in_3,
  input  in_4,
  input  in_5,
  input  in_6,
  input  in_7,
  input  in_8,
  input  in_9,
  input  in_10,
  input  in_11,
  input  in_12,
  input  in_13,
  input  in_14,
  input  in_15,
  output [6:0] out_16
);

  wire or_2_out;
  wire [6:0] e_45_1_out_2, e_65_1_out_2, i_49_1_out_2, i_69_1_out_2, multiplexer_1_out, multiplexer_2_out,
       multiplexer_3_out, multiplexer_4_out, multiplexer_5_out, multiplexer_6_out, multiplexer_7_out,
       multiplexer_8_out, multiplexer_9_out, multiplexer_10_out, multiplexer_11_out, multiplexer_12_out,
       multiplexer_13_out, n5b_1_out_2, n5c_1_out_2, n5d_1_out_2, n7b_1_out_2, n7c_1_out_2, n7d_1_out_2,
       o_4f_1_out_2, o_6f_1_out_2, p_50_1_out_2, p_70_1_out_2, q_51_1_out_2, q_71_1_out_2, r_52_1_out_2,
       r_72_1_out_2, t_54_1_out_2, t_74_1_out_2, u_55_1_out_2, u_75_1_out_2, w_57_1_out_2, w_77_1_out_2,
       y_59_1_out_2, y_79_1_out_2;

  q_71 q_71_1 (.in_1(in_1), .out_2(q_71_1_out_2));
  w_77 w_77_1 (.in_1(in_2), .out_2(w_77_1_out_2));
  Q_51 q_51_1 (.in_1(in_1), .out_2(q_51_1_out_2));
  Multiplexer #(.width(7), .enable("false")) multiplexer_1 (
    .in0(w_77_1_out_2), .in1(w_57_1_out_2), .out(multiplexer_1_out), .sel(or_2_out));
  Multiplexer #(.width(7), .enable("false")) multiplexer_2 (
    .in0(q_71_1_out_2), .in1(q_51_1_out_2), .out(multiplexer_2_out), .sel(or_2_out));
  e_65 e_65_1 (.in_1(in_3), .out_2(e_65_1_out_2));
  W_57 w_57_1 (.in_1(in_2), .out_2(w_57_1_out_2));
  E_45 e_45_1 (.in_1(in_3), .out_2(e_45_1_out_2));
  Multiplexer #(.width(7), .enable("false")) multiplexer_3 (
    .in0(e_65_1_out_2), .in1(e_45_1_out_2), .out(multiplexer_3_out), .sel(or_2_out));
  r_72 r_72_1 (.in_1(in_4), .out_2(r_72_1_out_2));
  t_74 t_74_1 (.in_1(in_5), .out_2(t_74_1_out_2));
  T_54 t_54_1 (.in_1(in_5), .out_2(t_54_1_out_2));
  R_52 r_52_1 (.in_1(in_4), .out_2(r_52_1_out_2));
  Multiplexer #(.width(7), .enable("false")) multiplexer_4 (
    .in0(t_74_1_out_2), .in1(t_54_1_out_2), .out(multiplexer_4_out), .sel(or_2_out));
  Multiplexer #(.width(7), .enable("false")) multiplexer_5 (
    .in0(r_72_1_out_2), .in1(r_52_1_out_2), .out(multiplexer_5_out), .sel(or_2_out));
  y_79 y_79_1 (.in_1(in_6), .out_2(y_79_1_out_2));
  u_75 u_75_1 (.in_1(in_7), .out_2(u_75_1_out_2));
  Y_59 y_59_1 (.in_1(in_6), .out_2(y_59_1_out_2));
  Multiplexer #(.width(7), .enable("false")) multiplexer_6 (
    .in0(y_79_1_out_2), .in1(y_59_1_out_2), .out(multiplexer_6_out), .sel(or_2_out));
  i_69 i_69_1 (.in_1(in_8), .out_2(i_69_1_out_2));
  I_49 i_49_1 (.in_1(in_8), .out_2(i_49_1_out_2));
  U_55 u_55_1 (.in_1(in_7), .out_2(u_55_1_out_2));
  Multiplexer #(.width(7), .enable("false")) multiplexer_7 (
    .in0(u_75_1_out_2), .in1(u_55_1_out_2), .out(multiplexer_7_out), .sel(or_2_out));
  Multiplexer #(.width(7), .enable("false")) multiplexer_8 (
    .in0(i_69_1_out_2), .in1(i_49_1_out_2), .out(multiplexer_8_out), .sel(or_2_out));
  assign out_16 = multiplexer_2_out | multiplexer_1_out | multiplexer_3_out | multiplexer_5_out | multiplexer_4_out | multiplexer_6_out | multiplexer_7_out | multiplexer_8_out | multiplexer_10_out | multiplexer_9_out | multiplexer_11_out | multiplexer_13_out | multiplexer_12_out;  // OR_Gate or_1, 7 bits wide
  p_70 p_70_1 (.in_1(in_10), .out_2(p_70_1_out_2));
  o_6f o_6f_1 (.in_1(in_9), .out_2(o_6f_1_out_2));
  O_4f o_4f_1 (.in_1(in_9), .out_2(o_4f_1_out_2));
  Multiplexer #(.width(7), .enable("false")) multiplexer_9 (
    .in0(p_70_1_out_2), .in1(p_50_1_out_2), .out(multiplexer_9_out), .sel(or_2_out));
  Multiplexer #(.width(7), .enable("false")) multiplexer_10 (
    .in0(o_6f_1_out_2), .in1(o_4f_1_out_2), .out(multiplexer_10_out), .sel(or_2_out));
  _5b u_5b_1 (.in_1(in_11), .out_2(n5b_1_out_2));
  _7b u_7b_1 (.in_1(in_11), .out_2(n7b_1_out_2));
  P_50 p_50_1 (.in_1(in_10), .out_2(p_50_1_out_2));
  Multiplexer #(.width(7), .enable("false")) multiplexer_11 (
    .in0(n5b_1_out_2), .in1(n7b_1_out_2), .out(multiplexer_11_out), .sel(in_15));
  _5c u_5c_1 (.in_1(in_13), .out_2(n5c_1_out_2));
  _5d u_5d_1 (.in_1(in_12), .out_2(n5d_1_out_2));
  _7c u_7c_1 (.in_1(in_13), .out_2(n7c_1_out_2));
  _7d u_7d_1 (.in_1(in_12), .out_2(n7d_1_out_2));
  Multiplexer #(.width(7), .enable("false")) multiplexer_12 (
    .in0(n5c_1_out_2), .in1(n7c_1_out_2), .out(multiplexer_12_out), .sel(in_15));
  Multiplexer #(.width(7), .enable("false")) multiplexer_13 (
    .in0(n5d_1_out_2), .in1(n7d_1_out_2), .out(multiplexer_13_out), .sel(in_15));
  or or_2 (or_2_out, in_14, in_15);
endmodule

module \τριτη  (
  input  in_1,
  input  in_2,
  input  in_3,
  input  in_4,
  input  in_5,
  input  in_6,
  input  in_7,
  input  in_8,
  input  in_9,
  input  in_10,
  input  in_11,
  input  in_12,
  input  in_13,
  input  in_14,
  output [6:0] out_15
);

  wire or_2_out;
  wire [6:0] a_41_1_out_2, a_61_1_out_2, d_44_1_out_2, d_64_1_out_2, enter_1_out_2, f_46_1_out_2,
       f_66_1_out_2, g_47_1_out_2, g_67_1_out_2, h_48_1_out_2, h_68_1_out_2, j_4a_1_out_2, j_6a_1_out_2,
       k_4b_1_out_2, k_6b_1_out_2, l_4c_1_out_2, l_6c_1_out_2, multiplexer_1_out, multiplexer_2_out,
       multiplexer_3_out, multiplexer_4_out, multiplexer_5_out, multiplexer_6_out, multiplexer_7_out,
       multiplexer_8_out, multiplexer_9_out, multiplexer_10_out, multiplexer_11_out, n3a_1_out_2,
       n3b_1_out_2, n27_1_out_2, part_1_out_2, s_53_1_out_2, s_73_1_out_2;

  s_73 s_73_1 (.in_1(in_2), .out_2(s_73_1_out_2));
  a_61 a_61_1 (.in_1(in_1), .out_2(a_61_1_out_2));
  A_41 a_41_1 (.in_1(in_1), .out_2(a_41_1_out_2));
  Multiplexer #(.width(7), .enable("false")) multiplexer_1 (
    .in0(a_61_1_out_2), .in1(a_41_1_out_2), .out(multiplexer_1_out), .sel(or_2_out));
  Multiplexer #(.width(7), .enable("false")) multiplexer_2 (
    .in0(s_73_1_out_2), .in1(s_53_1_out_2), .out(multiplexer_2_out), .sel(or_2_out));
  d_64 d_64_1 (.in_1(in_3), .out_2(d_64_1_out_2));
  D_44 d_44_1 (.in_1(in_3), .out_2(d_44_1_out_2));
  S_53 s_53_1 (.in_1(in_2), .out_2(s_53_1_out_2));
  Multiplexer #(.width(7), .enable("false")) multiplexer_3 (
    .in0(d_64_1_out_2), .in1(d_44_1_out_2), .out(multiplexer_3_out), .sel(or_2_out));
  g_67 g_67_1 (.in_1(in_5), .out_2(g_67_1_out_2));
  f_66 f_66_1 (.in_1(in_4), .out_2(f_66_1_out_2));
  F_46 f_46_1 (.in_1(in_4), .out_2(f_46_1_out_2));
  G_47 g_47_1 (.in_1(in_5), .out_2(g_47_1_out_2));
  Multiplexer #(.width(7), .enable("false")) multiplexer_4 (
    .in0(f_66_1_out_2), .in1(f_46_1_out_2), .out(multiplexer_4_out), .sel(or_2_out));
  Multiplexer #(.width(7), .enable("false")) multiplexer_5 (
    .in0(g_67_1_out_2), .in1(g_47_1_out_2), .out(multiplexer_5_out), .sel(or_2_out));
  h_68 h_68_1 (.in_1(in_6), .out_2(h_68_1_out_2));
  H_48 h_48_1 (.in_1(in_6), .out_2(h_48_1_out_2));
  Multiplexer #(.width(7), .enable("false")) multiplexer_6 (
    .in0(h_68_1_out_2), .in1(h_48_1_out_2), .out(multiplexer_6_out), .sel(or_2_out));
  assign out_15 = multiplexer_1_out | multiplexer_2_out | multiplexer_3_out | multiplexer_4_out | multiplexer_5_out | multiplexer_6_out | multiplexer_7_out | multiplexer_8_out | multiplexer_9_out | multiplexer_10_out | multiplexer_11_out | enter_1_out_2;  // OR_Gate or_1, 7 bits wide
  k_6b k_6b_1 (.in_1(in_8), .out_2(k_6b_1_out_2));
  j_6a j_6a_1 (.in_1(in_7), .out_2(j_6a_1_out_2));
  J_4a j_4a_1 (.in_1(in_7), .out_2(j_4a_1_out_2));
  K_4b k_4b_1 (.in_1(in_8), .out_2(k_4b_1_out_2));
  Multiplexer #(.width(7), .enable("false")) multiplexer_7 (
    .in0(j_6a_1_out_2), .in1(j_4a_1_out_2), .out(multiplexer_7_out), .sel(or_2_out));
  Multiplexer #(.width(7), .enable("false")) multiplexer_8 (
    .in0(k_6b_1_out_2), .in1(k_4b_1_out_2), .out(multiplexer_8_out), .sel(or_2_out));
  l_6c l_6c_1 (.in_1(in_9), .out_2(l_6c_1_out_2));
  _3b u_3b_1 (.in_1(in_10), .out_2(n3b_1_out_2));
  L_4c l_4c_1 (.in_1(in_9), .out_2(l_4c_1_out_2));
  Multiplexer #(.width(7), .enable("false")) multiplexer_9 (
    .in0(l_6c_1_out_2), .in1(l_4c_1_out_2), .out(multiplexer_9_out), .sel(or_2_out));
  _27 u_27_1 (.in_1(in_11), .out_2(n27_1_out_2));
  _3a u_3a_1 (.in_1(in_10), .out_2(n3a_1_out_2));
  circuit part_1 (.in_1(in_11), .out_2(part_1_out_2));
  Multiplexer #(.width(7), .enable("false")) multiplexer_10 (
    .in0(n3b_1_out_2), .in1(n3a_1_out_2), .out(multiplexer_10_out), .sel(in_14));
  Multiplexer #(.width(7), .enable("false")) multiplexer_11 (
    .in0(n27_1_out_2), .in1(part_1_out_2), .out(multiplexer_11_out), .sel(in_14));
  enter enter_1 (.in_1(in_12), .out_2(enter_1_out_2));
  or or_2 (or_2_out, in_13, in_14);

  // Notes on the sheet:
  //   ;':"
endmodule

module \τεραρτη  (
  input  in_1,
  input  in_2,
  input  in_3,
  input  in_4,
  input  in_5,
  input  in_6,
  input  in_7,
  input  in_8,
  input  in_9,
  input  in_10,
  input  in_11,
  input  in_12,
  output [6:0] out_13
);

  wire or_2_out;
  wire [6:0] b_42_1_out_2, b_62_1_out_2, c_43_1_out_2, c_63_1_out_2, m_4d_1_out_2, m_6d_1_out_2,
       multiplexer_1_out, multiplexer_2_out, multiplexer_3_out, multiplexer_4_out, multiplexer_5_out,
       multiplexer_6_out, multiplexer_7_out, multiplexer_8_out, multiplexer_9_out, multiplexer_10_out,
       n2c_1_out_2, n2e_1_out_2, n2f_1_out_2, n3c_1_out_2, n3e_1_out_2, n3f_1_out_2, n_4e_1_out_2,
       n_6e_1_out_2, v_56_1_out_2, v_76_1_out_2, x_58_1_out_2, x_78_1_out_2, z_5a_1_out_2, z_7a_1_out_2;

  z_7a z_7a_1 (.in_1(in_1), .out_2(z_7a_1_out_2));
  x_78 x_78_1 (.in_1(in_2), .out_2(x_78_1_out_2));
  Z_5a z_5a_1 (.in_1(in_1), .out_2(z_5a_1_out_2));
  Multiplexer #(.width(7), .enable("false")) multiplexer_1 (
    .in0(z_7a_1_out_2), .in1(z_5a_1_out_2), .out(multiplexer_1_out), .sel(or_2_out));
  Multiplexer #(.width(7), .enable("false")) multiplexer_2 (
    .in0(x_78_1_out_2), .in1(x_58_1_out_2), .out(multiplexer_2_out), .sel(or_2_out));
  c_63 c_63_1 (.in_1(in_3), .out_2(c_63_1_out_2));
  C_43 c_43_1 (.in_1(in_3), .out_2(c_43_1_out_2));
  X_58 x_58_1 (.in_1(in_2), .out_2(x_58_1_out_2));
  Multiplexer #(.width(7), .enable("false")) multiplexer_3 (
    .in0(c_63_1_out_2), .in1(c_43_1_out_2), .out(multiplexer_3_out), .sel(or_2_out));
  b_62 b_62_1 (.in_1(in_5), .out_2(b_62_1_out_2));
  v_76 v_76_1 (.in_1(in_4), .out_2(v_76_1_out_2));
  B_42 b_42_1 (.in_1(in_5), .out_2(b_42_1_out_2));
  V_56 v_56_1 (.in_1(in_4), .out_2(v_56_1_out_2));
  Multiplexer #(.width(7), .enable("false")) multiplexer_4 (
    .in0(b_62_1_out_2), .in1(b_42_1_out_2), .out(multiplexer_4_out), .sel(or_2_out));
  Multiplexer #(.width(7), .enable("false")) multiplexer_5 (
    .in0(v_76_1_out_2), .in1(v_56_1_out_2), .out(multiplexer_5_out), .sel(or_2_out));
  n_6e n_6e_1 (.in_1(in_6), .out_2(n_6e_1_out_2));
  N_4e n_4e_1 (.in_1(in_6), .out_2(n_4e_1_out_2));
  Multiplexer #(.width(7), .enable("false")) multiplexer_6 (
    .in0(n_6e_1_out_2), .in1(n_4e_1_out_2), .out(multiplexer_6_out), .sel(or_2_out));
  assign out_13 = multiplexer_1_out | multiplexer_2_out | multiplexer_3_out | multiplexer_5_out | multiplexer_4_out | multiplexer_6_out | multiplexer_8_out | multiplexer_7_out | multiplexer_9_out | multiplexer_10_out;  // OR_Gate or_1, 7 bits wide
  _2c u_2c_1 (.in_1(in_8), .out_2(n2c_1_out_2));
  m_6d m_6d_1 (.in_1(in_7), .out_2(m_6d_1_out_2));
  M_4d m_4d_1 (.in_1(in_7), .out_2(m_4d_1_out_2));
  Multiplexer #(.width(7), .enable("false")) multiplexer_7 (
    .in0(n2c_1_out_2), .in1(n3c_1_out_2), .out(multiplexer_7_out), .sel(in_12));
  Multiplexer #(.width(7), .enable("false")) multiplexer_8 (
    .in0(m_6d_1_out_2), .in1(m_4d_1_out_2), .out(multiplexer_8_out), .sel(or_2_out));
  _2e u_2e_1 (.in_1(in_9), .out_2(n2e_1_out_2));
  _3c u_3c_1 (.in_1(in_8), .out_2(n3c_1_out_2));
  _3e u_3e_1 (.in_1(in_9), .out_2(n3e_1_out_2));
  Multiplexer #(.width(7), .enable("false")) multiplexer_9 (
    .in0(n2e_1_out_2), .in1(n3e_1_out_2), .out(multiplexer_9_out), .sel(in_12));
  _2f u_2f_1 (.in_1(in_10), .out_2(n2f_1_out_2));
  _3f u_3f_1 (.in_1(in_10), .out_2(n3f_1_out_2));
  Multiplexer #(.width(7), .enable("false")) multiplexer_10 (
    .in0(n2f_1_out_2), .in1(n3f_1_out_2), .out(multiplexer_10_out), .sel(in_12));
  or or_2 (or_2_out, in_11, in_12);
endmodule

module _61 (
  input  in_1,
  input  in_2,
  input  in_3,
  input  in_4,
  input  in_5,
  input  in_6,
  input  in_7,
  input  in_8,
  input  in_9,
  input  in_10,
  output [6:0] out_11
);

  wire [6:0] n2a_1_out_2, n5e_1_out_2, n21_1_out_2, n26_1_out_2, n28_1_out_2, n29_1_out_2, n40_1_out_2,
       part_1_out_2, part_2_out_2, part_3_out_2;

  _29 u_29_1 (.in_1(in_1), .out_2(n29_1_out_2));
  _28 u_28_1 (.in_1(in_2), .out_2(n28_1_out_2));
  _2a u_2a_1 (.in_1(in_3), .out_2(n2a_1_out_2));
  _26 u_26_1 (.in_1(in_4), .out_2(n26_1_out_2));
  _5e u_5e_1 (.in_1(in_5), .out_2(n5e_1_out_2));
  circuit_2_2_2 part_1 (.in_1(in_6), .out_2(part_1_out_2));
  circuit_2_2 part_2 (.in_1(in_7), .out_2(part_2_out_2));
  circuit_2 part_3 (.in_1(in_8), .out_2(part_3_out_2));
  _40 u_40_1 (.in_1(in_9), .out_2(n40_1_out_2));
  _21 u_21_1 (.in_1(in_10), .out_2(n21_1_out_2));
  assign out_11 = n29_1_out_2 | n28_1_out_2 | n2a_1_out_2 | n26_1_out_2 | n5e_1_out_2 | part_1_out_2 | part_2_out_2 | part_3_out_2 | n40_1_out_2 | n21_1_out_2;  // OR_Gate or_1, 7 bits wide
endmodule

module _1 (
  input  in_1,
  output [6:0] out_2
);


  assign out_2 = {1'b0, {2{in_1}}, 3'b000, in_1};
endmodule

module _2 (
  input  in_1,
  output [6:0] out_2
);


  assign out_2 = {1'b0, {2{in_1}}, 2'b00, in_1, 1'b0};
endmodule

module _3 (
  input  in_1,
  output [6:0] out_2
);


  assign out_2 = {1'b0, {2{in_1}}, 2'b00, {2{in_1}}};
endmodule

module _4 (
  input  in_1,
  output [6:0] out_2
);


  assign out_2 = {1'b0, {2{in_1}}, 1'b0, in_1, 2'b00};
endmodule

module _5 (
  input  in_1,
  output [6:0] out_2
);


  assign out_2 = {1'b0, {2{in_1}}, 1'b0, in_1, 1'b0, in_1};
endmodule

module _6 (
  input  in_1,
  output [6:0] out_2
);


  assign out_2 = {1'b0, {2{in_1}}, 1'b0, {2{in_1}}, 1'b0};
endmodule

module _7 (
  input  in_1,
  output [6:0] out_2
);


  assign out_2 = {1'b0, {2{in_1}}, 1'b0, {3{in_1}}};
endmodule

module _8 (
  input  in_1,
  output [6:0] out_2
);


  assign out_2 = {1'b0, {3{in_1}}, 3'b000};
endmodule

module _9 (
  input  in_1,
  output [6:0] out_2
);


  assign out_2 = {1'b0, {3{in_1}}, 2'b00, in_1};
endmodule

module _0 (
  input  in_1,
  output [6:0] out_2
);


  assign out_2 = {1'b0, {2{in_1}}, 4'b0000};
endmodule

module ariumi_0_9 (
  input  in_1,
  input  in_2,
  input  in_3,
  input  in_4,
  input  in_5,
  input  in_6,
  input  in_7,
  input  in_8,
  input  in_9,
  input  in_10,
  output [6:0] out_11
);

  wire [6:0] n0_1_out_2, n1_1_out_2, n2_1_out_2, n3_1_out_2, n4_1_out_2, n5_1_out_2, n6_1_out_2, n7_1_out_2,
       n8_1_out_2, n9_1_out_2;

  _1 u_1_1 (.in_1(in_1), .out_2(n1_1_out_2));
  _2 u_2_1 (.in_1(in_2), .out_2(n2_1_out_2));
  _3 u_3_1 (.in_1(in_3), .out_2(n3_1_out_2));
  _4 u_4_1 (.in_1(in_4), .out_2(n4_1_out_2));
  _5 u_5_1 (.in_1(in_5), .out_2(n5_1_out_2));
  _6 u_6_1 (.in_1(in_6), .out_2(n6_1_out_2));
  _7 u_7_1 (.in_1(in_7), .out_2(n7_1_out_2));
  _8 u_8_1 (.in_1(in_8), .out_2(n8_1_out_2));
  _9 u_9_1 (.in_1(in_9), .out_2(n9_1_out_2));
  _0 u_0_1 (.in_1(in_10), .out_2(n0_1_out_2));
  assign out_11 = n1_1_out_2 | n2_1_out_2 | n3_1_out_2 | n4_1_out_2 | n5_1_out_2 | n6_1_out_2 | n7_1_out_2 | n8_1_out_2 | n9_1_out_2 | n0_1_out_2;  // OR_Gate or_1, 7 bits wide
endmodule

module enter (
  input  in_1,
  output [6:0] out_2
);


  assign out_2 = {3'b000, {2{in_1}}, 1'b0, in_1};
endmodule

module _21 (
  input  in_1,
  output [6:0] out_2
);


  assign out_2 = {1'b0, in_1, 4'b0000, in_1};
endmodule

module circuit (
  input  in_1,
  output [6:0] out_2
);


  assign out_2 = {1'b0, in_1, 3'b000, in_1, 1'b0};
endmodule

module circuit_2 (
  input  in_1,
  output [6:0] out_2
);


  assign out_2 = {1'b0, in_1, 3'b000, {2{in_1}}};
endmodule

module circuit_2_2 (
  input  in_1,
  output [6:0] out_2
);

  wire [6:0] register_1_q;

  Register #(.width(7)) register_1 (.Q(register_1_q));  // open: D, en, clk, clr

  assign out_2 = {1'b0, in_1, 2'b00, in_1, 2'b00};
endmodule

module circuit_2_2_2 (
  input  in_1,
  output [6:0] out_2
);


  assign out_2 = {1'b0, in_1, 2'b00, in_1, 1'b0, in_1};
endmodule

module _26 (
  input  in_1,
  output [6:0] out_2
);

  wire [6:0] register_1_q;

  Register #(.width(7)) register_1 (.Q(register_1_q));  // open: D, en, clk, clr

  assign out_2 = {1'b0, in_1, 2'b00, {2{in_1}}, 1'b0};
endmodule

module _27 (
  input  in_1,
  output [6:0] out_2
);

  wire [6:0] register_1_q;

  Register #(.width(7)) register_1 (.Q(register_1_q));  // open: D, en, clk, clr

  assign out_2 = {1'b0, in_1, 2'b00, {3{in_1}}};
endmodule

module _28 (
  input  in_1,
  output [6:0] out_2
);

  wire [6:0] register_1_q;

  Register #(.width(7)) register_1 (.Q(register_1_q));  // open: D, en, clk, clr

  assign out_2 = {1'b0, in_1, 1'b0, in_1, 3'b000};
endmodule

module _29 (
  input  in_1,
  output [6:0] out_2
);

  wire [6:0] register_1_q;

  Register #(.width(7)) register_1 (.Q(register_1_q));  // open: D, en, clk, clr

  assign out_2 = {1'b0, in_1, 1'b0, in_1, 2'b00, in_1};
endmodule

module _2a (
  input  in_1,
  output [6:0] out_2
);

  wire [6:0] register_1_q;

  Register #(.width(7)) register_1 (.Q(register_1_q));  // open: D, en, clk, clr

  assign out_2 = {1'b0, in_1, 1'b0, in_1, 1'b0, in_1, 1'b0};
endmodule

module _2b (
  input  in_1,
  output [6:0] out_2
);

  wire [6:0] register_1_q;

  Register #(.width(7)) register_1 (.Q(register_1_q));  // open: D, en, clk, clr

  assign out_2 = {1'b0, in_1, 1'b0, in_1, 1'b0, {2{in_1}}};
endmodule

module _2c (
  input  in_1,
  output [6:0] out_2
);

  wire [6:0] register_1_q;

  Register #(.width(7)) register_1 (.Q(register_1_q));  // open: D, en, clk, clr

  assign out_2 = {1'b0, in_1, 1'b0, {2{in_1}}, 2'b00};
endmodule

module _2d (
  input  in_1,
  output [6:0] out_2
);

  wire [6:0] register_1_q;

  Register #(.width(7)) register_1 (.Q(register_1_q));  // open: D, en, clk, clr

  assign out_2 = {1'b0, in_1, 1'b0, {2{in_1}}, 1'b0, in_1};
endmodule

module _2e (
  input  in_1,
  output [6:0] out_2
);

  wire [6:0] register_1_q;

  Register #(.width(7)) register_1 (.Q(register_1_q));  // open: D, en, clk, clr

  assign out_2 = {1'b0, in_1, 1'b0, {3{in_1}}, 1'b0};
endmodule

module _2f (
  input  in_1,
  output [6:0] out_2
);

  wire [6:0] register_1_q;

  Register #(.width(7)) register_1 (.Q(register_1_q));  // open: D, en, clk, clr

  assign out_2 = {1'b0, in_1, 1'b0, {4{in_1}}};
endmodule

module _3a (
  input  in_1,
  output [6:0] out_2
);

  wire [6:0] register_1_q;

  Register #(.width(7)) register_1 (.Q(register_1_q));  // open: D, en, clk, clr

  assign out_2 = {1'b0, {3{in_1}}, 1'b0, in_1, 1'b0};
endmodule

module _3b (
  input  in_1,
  output [6:0] out_2
);

  wire [6:0] register_1_q;

  Register #(.width(7)) register_1 (.Q(register_1_q));  // open: D, en, clk, clr

  assign out_2 = {1'b0, {3{in_1}}, 1'b0, {2{in_1}}};
endmodule

module _3c (
  input  in_1,
  output [6:0] out_2
);

  wire [6:0] register_1_q;

  Register #(.width(7)) register_1 (.Q(register_1_q));  // open: D, en, clk, clr

  assign out_2 = {1'b0, {4{in_1}}, 2'b00};
endmodule

module _3d (
  input  in_1,
  output [6:0] out_2
);

  wire [6:0] register_1_q;

  Register #(.width(7)) register_1 (.Q(register_1_q));  // open: D, en, clk, clr

  assign out_2 = {1'b0, {4{in_1}}, 1'b0, in_1};
endmodule

module _3e (
  input  in_1,
  output [6:0] out_2
);

  wire [6:0] register_1_q;

  Register #(.width(7)) register_1 (.Q(register_1_q));  // open: D, en, clk, clr

  assign out_2 = {1'b0, {5{in_1}}, 1'b0};
endmodule

module _3f (
  input  in_1,
  output [6:0] out_2
);

  wire [6:0] register_1_q;

  Register #(.width(7)) register_1 (.Q(register_1_q));  // open: D, en, clk, clr

  assign out_2 = {1'b0, {6{in_1}}};
endmodule

module _40 (
  input  in_1,
  output [6:0] out_2
);

  wire [6:0] register_1_q;

  Register #(.width(7)) register_1 (.Q(register_1_q));  // open: D, en, clk, clr

  assign out_2 = {in_1, {6{1'b0}}};
endmodule

module A_41 (
  input  in_1,
  output [6:0] out_2
);

  wire [6:0] register_1_q;

  Register #(.width(7)) register_1 (.Q(register_1_q));  // open: D, en, clk, clr

  assign out_2 = {in_1, {5{1'b0}}, in_1};
endmodule

module B_42 (
  input  in_1,
  output [6:0] out_2
);

  wire [6:0] register_1_q;

  Register #(.width(7)) register_1 (.Q(register_1_q));  // open: D, en, clk, clr

  assign out_2 = {in_1, 4'b0000, in_1, 1'b0};
endmodule

module C_43 (
  input  in_1,
  output [6:0] out_2
);

  wire [6:0] register_1_q;

  Register #(.width(7)) register_1 (.Q(register_1_q));  // open: D, en, clk, clr

  assign out_2 = {in_1, 4'b0000, {2{in_1}}};
endmodule

module D_44 (
  input  in_1,
  output [6:0] out_2
);

  wire [6:0] register_1_q;

  Register #(.width(7)) register_1 (.Q(register_1_q));  // open: D, en, clk, clr

  assign out_2 = {in_1, 3'b000, in_1, 2'b00};
endmodule

module E_45 (
  input  in_1,
  output [6:0] out_2
);

  wire [6:0] register_1_q;

  Register #(.width(7)) register_1 (.Q(register_1_q));  // open: D, en, clk, clr

  assign out_2 = {in_1, 3'b000, in_1, 1'b0, in_1};
endmodule

module F_46 (
  input  in_1,
  output [6:0] out_2
);

  wire [6:0] register_1_q;

  Register #(.width(7)) register_1 (.Q(register_1_q));  // open: D, en, clk, clr

  assign out_2 = {in_1, 3'b000, {2{in_1}}, 1'b0};
endmodule

module G_47 (
  input  in_1,
  output [6:0] out_2
);

  wire [6:0] register_1_q;

  Register #(.width(7)) register_1 (.Q(register_1_q));  // open: D, en, clk, clr

  assign out_2 = {in_1, 3'b000, {3{in_1}}};
endmodule

module H_48 (
  input  in_1,
  output [6:0] out_2
);

  wire [6:0] register_1_q;

  Register #(.width(7)) register_1 (.Q(register_1_q));  // open: D, en, clk, clr

  assign out_2 = {in_1, 2'b00, in_1, 3'b000};
endmodule

module I_49 (
  input  in_1,
  output [6:0] out_2
);

  wire [6:0] register_1_q;

  Register #(.width(7)) register_1 (.Q(register_1_q));  // open: D, en, clk, clr

  assign out_2 = {in_1, 2'b00, in_1, 2'b00, in_1};
endmodule

module J_4a (
  input  in_1,
  output [6:0] out_2
);

  wire [6:0] register_1_q;

  Register #(.width(7)) register_1 (.Q(register_1_q));  // open: D, en, clk, clr

  assign out_2 = {in_1, 2'b00, in_1, 1'b0, in_1, 1'b0};
endmodule

module K_4b (
  input  in_1,
  output [6:0] out_2
);

  wire [6:0] register_1_q;

  Register #(.width(7)) register_1 (.Q(register_1_q));  // open: D, en, clk, clr

  assign out_2 = {in_1, 2'b00, in_1, 1'b0, {2{in_1}}};
endmodule

module L_4c (
  input  in_1,
  output [6:0] out_2
);

  wire [6:0] register_1_q;

  Register #(.width(7)) register_1 (.Q(register_1_q));  // open: D, en, clk, clr

  assign out_2 = {in_1, 2'b00, {2{in_1}}, 2'b00};
endmodule

module M_4d (
  input  in_1,
  output [6:0] out_2
);

  wire [6:0] register_1_q;

  Register #(.width(7)) register_1 (.Q(register_1_q));  // open: D, en, clk, clr

  assign out_2 = {in_1, 2'b00, {2{in_1}}, 1'b0, in_1};
endmodule

module N_4e (
  input  in_1,
  output [6:0] out_2
);

  wire [6:0] register_1_q;

  Register #(.width(7)) register_1 (.Q(register_1_q));  // open: D, en, clk, clr

  assign out_2 = {in_1, 2'b00, {3{in_1}}, 1'b0};
endmodule

module O_4f (
  input  in_1,
  output [6:0] out_2
);

  wire [6:0] register_1_q;

  Register #(.width(7)) register_1 (.Q(register_1_q));  // open: D, en, clk, clr

  assign out_2 = {in_1, 2'b00, {4{in_1}}};
endmodule

module P_50 (
  input  in_1,
  output [6:0] out_2
);

  wire [6:0] register_1_q;

  Register #(.width(7)) register_1 (.Q(register_1_q));  // open: D, en, clk, clr

  assign out_2 = {in_1, 1'b0, in_1, 4'b0000};
endmodule

module Q_51 (
  input  in_1,
  output [6:0] out_2
);

  wire [6:0] register_1_q;

  Register #(.width(7)) register_1 (.Q(register_1_q));  // open: D, en, clk, clr

  assign out_2 = {in_1, 1'b0, in_1, 3'b000, in_1};
endmodule

module R_52 (
  input  in_1,
  output [6:0] out_2
);

  wire [6:0] register_1_q;

  Register #(.width(7)) register_1 (.Q(register_1_q));  // open: D, en, clk, clr

  assign out_2 = {in_1, 1'b0, in_1, 2'b00, in_1, 1'b0};
endmodule

module S_53 (
  input  in_1,
  output [6:0] out_2
);

  wire [6:0] register_1_q;

  Register #(.width(7)) register_1 (.Q(register_1_q));  // open: D, en, clk, clr

  assign out_2 = {in_1, 1'b0, in_1, 2'b00, {2{in_1}}};
endmodule

module T_54 (
  input  in_1,
  output [6:0] out_2
);

  wire [6:0] register_1_q;

  Register #(.width(7)) register_1 (.Q(register_1_q));  // open: D, en, clk, clr

  assign out_2 = {in_1, 1'b0, in_1, 1'b0, in_1, 2'b00};
endmodule

module U_55 (
  input  in_1,
  output [6:0] out_2
);

  wire [6:0] register_1_q;

  Register #(.width(7)) register_1 (.Q(register_1_q));  // open: D, en, clk, clr

  assign out_2 = {in_1, 1'b0, in_1, 1'b0, in_1, 1'b0, in_1};
endmodule

module V_56 (
  input  in_1,
  output [6:0] out_2
);

  wire [6:0] register_1_q;

  Register #(.width(7)) register_1 (.Q(register_1_q));  // open: D, en, clk, clr

  assign out_2 = {in_1, 1'b0, in_1, 1'b0, {2{in_1}}, 1'b0};
endmodule

module W_57 (
  input  in_1,
  output [6:0] out_2
);

  wire [6:0] register_1_q;

  Register #(.width(7)) register_1 (.Q(register_1_q));  // open: D, en, clk, clr

  assign out_2 = {in_1, 1'b0, in_1, 1'b0, {3{in_1}}};
endmodule

module X_58 (
  input  in_1,
  output [6:0] out_2
);

  wire [6:0] register_1_q;

  Register #(.width(7)) register_1 (.Q(register_1_q));  // open: D, en, clk, clr

  assign out_2 = {in_1, 1'b0, {2{in_1}}, 3'b000};
endmodule

module Y_59 (
  input  in_1,
  output [6:0] out_2
);

  wire [6:0] register_1_q;

  Register #(.width(7)) register_1 (.Q(register_1_q));  // open: D, en, clk, clr

  assign out_2 = {in_1, 1'b0, {2{in_1}}, 2'b00, in_1};
endmodule

module Z_5a (
  input  in_1,
  output [6:0] out_2
);

  wire [6:0] register_1_q;

  Register #(.width(7)) register_1 (.Q(register_1_q));  // open: D, en, clk, clr

  assign out_2 = {in_1, 1'b0, {2{in_1}}, 1'b0, in_1, 1'b0};
endmodule

module _5b (
  input  in_1,
  output [6:0] out_2
);

  wire [6:0] register_1_q;

  Register #(.width(7)) register_1 (.Q(register_1_q));  // open: D, en, clk, clr

  assign out_2 = {in_1, 1'b0, {2{in_1}}, 1'b0, {2{in_1}}};
endmodule

module _5c (
  input  in_1,
  output [6:0] out_2
);

  wire [6:0] register_1_q;

  Register #(.width(7)) register_1 (.Q(register_1_q));  // open: D, en, clk, clr

  assign out_2 = {in_1, 1'b0, {3{in_1}}, 2'b00};
endmodule

module _5d (
  input  in_1,
  output [6:0] out_2
);

  wire [6:0] register_1_q;

  Register #(.width(7)) register_1 (.Q(register_1_q));  // open: D, en, clk, clr

  assign out_2 = {in_1, 1'b0, {3{in_1}}, 1'b0, in_1};
endmodule

module _5e (
  input  in_1,
  output [6:0] out_2
);

  wire [6:0] register_1_q;

  Register #(.width(7)) register_1 (.Q(register_1_q));  // open: D, en, clk, clr

  assign out_2 = {in_1, 1'b0, {4{in_1}}, 1'b0};
endmodule

module _5f (
  input  in_1,
  output [6:0] out_2
);

  wire [6:0] register_1_q;

  Register #(.width(7)) register_1 (.Q(register_1_q));  // open: D, en, clk, clr

  assign out_2 = {in_1, 1'b0, {5{in_1}}};
endmodule

module _60 (
  input  in_1,
  output [6:0] out_2
);

  wire [6:0] register_1_q;

  Register #(.width(7)) register_1 (.Q(register_1_q));  // open: D, en, clk, clr

  assign out_2 = {{2{in_1}}, {5{1'b0}}};
endmodule

module a_61 (
  input  in_1,
  output [6:0] out_2
);

  wire [6:0] register_1_q;

  Register #(.width(7)) register_1 (.Q(register_1_q));  // open: D, en, clk, clr

  assign out_2 = {{2{in_1}}, 4'b0000, in_1};
endmodule

module b_62 (
  input  in_1,
  output [6:0] out_2
);

  wire [6:0] register_1_q;

  Register #(.width(7)) register_1 (.Q(register_1_q));  // open: D, en, clk, clr

  assign out_2 = {{2{in_1}}, 3'b000, in_1, 1'b0};
endmodule

module c_63 (
  input  in_1,
  output [6:0] out_2
);

  wire [6:0] register_1_q;

  Register #(.width(7)) register_1 (.Q(register_1_q));  // open: D, en, clk, clr

  assign out_2 = {{2{in_1}}, 3'b000, {2{in_1}}};
endmodule

module d_64 (
  input  in_1,
  output [6:0] out_2
);

  wire [6:0] register_1_q;

  Register #(.width(7)) register_1 (.Q(register_1_q));  // open: D, en, clk, clr

  assign out_2 = {{2{in_1}}, 2'b00, in_1, 2'b00};
endmodule

module e_65 (
  input  in_1,
  output [6:0] out_2
);

  wire [6:0] register_1_q;

  Register #(.width(7)) register_1 (.Q(register_1_q));  // open: D, en, clk, clr

  assign out_2 = {{2{in_1}}, 2'b00, in_1, 1'b0, in_1};
endmodule

module f_66 (
  input  in_1,
  output [6:0] out_2
);

  wire [6:0] register_1_q;

  Register #(.width(7)) register_1 (.Q(register_1_q));  // open: D, en, clk, clr

  assign out_2 = {{2{in_1}}, 2'b00, {2{in_1}}, 1'b0};
endmodule

module g_67 (
  input  in_1,
  output [6:0] out_2
);

  wire [6:0] register_1_q;

  Register #(.width(7)) register_1 (.Q(register_1_q));  // open: D, en, clk, clr

  assign out_2 = {{2{in_1}}, 2'b00, {3{in_1}}};
endmodule

module h_68 (
  input  in_1,
  output [6:0] out_2
);

  wire [6:0] register_1_q;

  Register #(.width(7)) register_1 (.Q(register_1_q));  // open: D, en, clk, clr

  assign out_2 = {{2{in_1}}, 1'b0, in_1, 3'b000};
endmodule

module i_69 (
  input  in_1,
  output [6:0] out_2
);

  wire [6:0] register_1_q;

  Register #(.width(7)) register_1 (.Q(register_1_q));  // open: D, en, clk, clr

  assign out_2 = {{2{in_1}}, 1'b0, in_1, 2'b00, in_1};
endmodule

module j_6a (
  input  in_1,
  output [6:0] out_2
);

  wire [6:0] register_1_q;

  Register #(.width(7)) register_1 (.Q(register_1_q));  // open: D, en, clk, clr

  assign out_2 = {{2{in_1}}, 1'b0, in_1, 1'b0, in_1, 1'b0};
endmodule

module k_6b (
  input  in_1,
  output [6:0] out_2
);

  wire [6:0] register_1_q;

  Register #(.width(7)) register_1 (.Q(register_1_q));  // open: D, en, clk, clr

  assign out_2 = {{2{in_1}}, 1'b0, in_1, 1'b0, {2{in_1}}};
endmodule

module l_6c (
  input  in_1,
  output [6:0] out_2
);

  wire [6:0] register_1_q;

  Register #(.width(7)) register_1 (.Q(register_1_q));  // open: D, en, clk, clr

  assign out_2 = {{2{in_1}}, 1'b0, {2{in_1}}, 2'b00};
endmodule

module m_6d (
  input  in_1,
  output [6:0] out_2
);

  wire [6:0] register_1_q;

  Register #(.width(7)) register_1 (.Q(register_1_q));  // open: D, en, clk, clr

  assign out_2 = {{2{in_1}}, 1'b0, {2{in_1}}, 1'b0, in_1};
endmodule

module n_6e (
  input  in_1,
  output [6:0] out_2
);

  wire [6:0] register_1_q;

  Register #(.width(7)) register_1 (.Q(register_1_q));  // open: D, en, clk, clr

  assign out_2 = {{2{in_1}}, 1'b0, {3{in_1}}, 1'b0};
endmodule

module o_6f (
  input  in_1,
  output [6:0] out_2
);

  wire [6:0] register_1_q;

  Register #(.width(7)) register_1 (.Q(register_1_q));  // open: D, en, clk, clr

  assign out_2 = {{2{in_1}}, 1'b0, {4{in_1}}};
endmodule

module p_70 (
  input  in_1,
  output [6:0] out_2
);

  wire [6:0] register_1_q;

  Register #(.width(7)) register_1 (.Q(register_1_q));  // open: D, en, clk, clr

  assign out_2 = {{3{in_1}}, 4'b0000};
endmodule

module q_71 (
  input  in_1,
  output [6:0] out_2
);

  wire [6:0] register_1_q;

  Register #(.width(7)) register_1 (.Q(register_1_q));  // open: D, en, clk, clr

  assign out_2 = {{3{in_1}}, 3'b000, in_1};
endmodule

module r_72 (
  input  in_1,
  output [6:0] out_2
);

  wire [6:0] register_1_q;

  Register #(.width(7)) register_1 (.Q(register_1_q));  // open: D, en, clk, clr

  assign out_2 = {{3{in_1}}, 2'b00, in_1, 1'b0};
endmodule

module s_73 (
  input  in_1,
  output [6:0] out_2
);

  wire [6:0] register_1_q;

  Register #(.width(7)) register_1 (.Q(register_1_q));  // open: D, en, clk, clr

  assign out_2 = {{3{in_1}}, 2'b00, {2{in_1}}};
endmodule

module t_74 (
  input  in_1,
  output [6:0] out_2
);

  wire [6:0] register_1_q;

  Register #(.width(7)) register_1 (.Q(register_1_q));  // open: D, en, clk, clr

  assign out_2 = {{3{in_1}}, 1'b0, in_1, 2'b00};
endmodule

module u_75 (
  input  in_1,
  output [6:0] out_2
);

  wire [6:0] register_1_q;

  Register #(.width(7)) register_1 (.Q(register_1_q));  // open: D, en, clk, clr

  assign out_2 = {{3{in_1}}, 1'b0, in_1, 1'b0, in_1};
endmodule

module v_76 (
  input  in_1,
  output [6:0] out_2
);

  wire [6:0] register_1_q;

  Register #(.width(7)) register_1 (.Q(register_1_q));  // open: D, en, clk, clr

  assign out_2 = {{3{in_1}}, 1'b0, {2{in_1}}, 1'b0};
endmodule

module w_77 (
  input  in_1,
  output [6:0] out_2
);

  wire [6:0] register_1_q;

  Register #(.width(7)) register_1 (.Q(register_1_q));  // open: D, en, clk, clr

  assign out_2 = {{3{in_1}}, 1'b0, {3{in_1}}};
endmodule

module x_78 (
  input  in_1,
  output [6:0] out_2
);

  wire [6:0] register_1_q;

  Register #(.width(7)) register_1 (.Q(register_1_q));  // open: D, en, clk, clr

  assign out_2 = {{4{in_1}}, 3'b000};
endmodule

module y_79 (
  input  in_1,
  output [6:0] out_2
);

  wire [6:0] register_1_q;

  Register #(.width(7)) register_1 (.Q(register_1_q));  // open: D, en, clk, clr

  assign out_2 = {{4{in_1}}, 2'b00, in_1};
endmodule

module z_7a (
  input  in_1,
  output [6:0] out_2
);

  wire [6:0] register_1_q;

  Register #(.width(7)) register_1 (.Q(register_1_q));  // open: D, en, clk, clr

  assign out_2 = {{4{in_1}}, 1'b0, in_1, 1'b0};
endmodule

module _7b (
  input  in_1,
  output [6:0] out_2
);

  wire [6:0] register_1_q;

  Register #(.width(7)) register_1 (.Q(register_1_q));  // open: D, en, clk, clr

  assign out_2 = {{4{in_1}}, 1'b0, {2{in_1}}};
endmodule

module _7c (
  input  in_1,
  output [6:0] out_2
);

  wire [6:0] register_1_q;

  Register #(.width(7)) register_1 (.Q(register_1_q));  // open: D, en, clk, clr

  assign out_2 = {{5{in_1}}, 2'b00};
endmodule

module _7d (
  input  in_1,
  output [6:0] out_2
);

  wire [6:0] register_1_q;

  Register #(.width(7)) register_1 (.Q(register_1_q));  // open: D, en, clk, clr

  assign out_2 = {{5{in_1}}, 1'b0, in_1};
endmodule

module _7e (
  input  in_1,
  output [6:0] out_2
);

  wire [6:0] register_1_q;

  Register #(.width(7)) register_1 (.Q(register_1_q));  // open: D, en, clk, clr

  assign out_2 = {{6{in_1}}, 1'b0};
endmodule

module Backspace_08 (
  input  in_1,
  output [6:0] out_2
);

  wire [6:0] register_1_q;

  Register #(.width(7)) register_1 (.Q(register_1_q));  // open: D, en, clk, clr

  assign out_2 = {3'b000, in_1, 3'b000};
endmodule

module diagrah_sel_0c (
  input  in_1,
  output [6:0] out_2
);

  wire [6:0] register_1_q;

  Register #(.width(7)) register_1 (.Q(register_1_q));  // open: D, en, clk, clr

  assign out_2 = {3'b000, {2{in_1}}, 2'b00};
endmodule

module spahs (
  input  in_1,
  output [6:0] out_2
);


  assign out_2 = {1'b0, in_1, {5{1'b0}}};
endmodule
