// Logisim project χα.circ as structural Verilog
module circuit (
  input  in_1,
  input  in_2,
  input  in_3,
  input  in_4,
  input  in_5,
  input  in_6,
  input  in_7,
  input  in_8,
  input  in_9,
  input  in_10,
  output out_11,
  output out_12,
  output out_13,
  output out_14
);

  wire and_1_out, and_2_out, and_3_out, and_4_out, and_5_out, not_1_out;

  not not_1 (not_1_out, in_2);
  and and_1 (and_1_out, in_1, not_1_out);
  and and_2 (and_2_out, in_3, in_4);
  and and_3 (and_3_out, in_5, in_6);
  and and_4 (and_4_out, in_7, in_8);
  and and_5 (and_5_out, in_9, in_10);
  and and_6 (out_11, and_1_out, and_2_out);
  and and_7 (out_12, and_1_out, and_3_out);
  and and_8 (out_13, and_1_out, and_4_out);
  and and_9 (out_14, and_1_out, and_5_out);
endmodule

module _7434 (
  input  in_1,
  input  in_2,
  input  in_3,
  input  in_4,
  input  in_5,
  input  in_6,
  input  in_7,
  input  in_8,
  input  in_9,
  input  in_10,
  output out_11,
  output out_12,
  output out_13,
  output out_14
);

  wire and_1_out, not_1_out, or_1_out, or_2_out, or_3_out, or_4_out;

  not not_1 (not_1_out, in_2);
  and and_1 (and_1_out, in_1, not_1_out);
  or or_1 (or_1_out, in_3, in_4);
  or or_2 (or_2_out, in_5, in_6);
  or or_3 (or_3_out, in_7, in_8);
  or or_4 (or_4_out, in_9, in_10);
  and and_2 (out_11, and_1_out, or_1_out);
  and and_3 (out_12, and_1_out, or_2_out);
  and and_4 (out_13, and_1_out, or_3_out);
  and and_5 (out_14, and_1_out, or_4_out);
endmodule
