// Logisim project χχ arxiko.circ as structural Verilog: 4 circuits, main circuit πληκρολογιο
module \πληκρολογιο  (
  input  in_1,
  input  in_2,
  output [6:0] out_3
);

  wire _0_out, _1_out, _2_out, _3_num_out, _4_out, _5_out, _6_out, _7_out, _8_star_out, _9_out, A_out, B_out,
       Ba_out, button_2_out, button_3_out, button_4_out, button_5_out, button_6_out, button_7_out,
       button_8_out, button_9_out, button_10_out, button_11_out, button_12_out, button_out, C_out,
       clock_1_out, D_out, E_out, En_out, F_out, G_out, H_out, I_out, J_out, K_out, L_out, M_out, minus__out,
       N_out, O_out, P_out, Q_out, R_out, S_out, T_out, U_out, V_out, W_out, X_out, Y_out, Z_out;
  wire [11:0] n3_1_out_13;
  wire [12:0] n2_1_out_14, n2_2_out_14;
  wire [13:0] n1_1_out_15;

  \πληκρολογιο_NEO_πληκρολογιο  \u_πληκρολογιο_1  (
    .out_6(out_3), .in_1(n1_1_out_15), .in_5(button_3_out), .in_4(n2_1_out_14), .in_3(n2_2_out_14),
    .in_2(n3_1_out_13));
  _1 u_1_1 (
    .out_15(n1_1_out_15), .in_1(button_out), .in_2(_1_out), .in_3(_2_out), .in_4(_3_num_out), .in_5(_4_out),
    .in_6(_5_out), .in_7(_6_out), .in_8(_7_out), .in_9(_8_star_out), .in_10(_9_out), .in_11(_0_out),
    .in_12(minus__out), .in_13(button_9_out), .in_14(Ba_out));
  Button button (.out(button_out));
  _2 u_2_1 (
    .in_1(Q_out), .in_2(W_out), .in_3(E_out), .in_4(R_out), .in_5(T_out), .in_6(Y_out), .in_7(U_out),
    .in_8(I_out), .in_9(O_out), .in_10(P_out), .in_11(button_4_out), .in_12(button_11_out),
    .in_13(button_10_out), .out_14(n2_1_out_14));
  Button Q (.out(Q_out));
  Button button_2 (.out(button_2_out));
  _2 u_2_2 (
    .in_1(button_2_out), .in_2(A_out), .in_3(S_out), .in_4(D_out), .in_5(F_out), .in_6(G_out), .in_7(H_out),
    .in_8(J_out), .in_9(K_out), .in_10(L_out), .in_11(button_5_out), .in_12(button_12_out), .in_13(En_out),
    .out_14(n2_2_out_14));
  Clock clock_1 (.out(clock_1_out));
  TTY #(.rows(20), .cols(43)) tty_1 (.data(out_3), .clk(clock_1_out));  // open: we, clr
  Button _1 (.out(_1_out));
  Button _2 (.out(_2_out));
  Button _3_num (.out(_3_num_out));
  Button E (.out(E_out));
  Button W (.out(W_out));
  Button S (.out(S_out));
  Button A (.out(A_out));
  Button Z (.out(Z_out));
  Button X (.out(X_out));
  _3 u_3_1 (
    .in_1(in_1), .in_2(Z_out), .in_3(X_out), .in_4(C_out), .in_5(V_out), .in_6(B_out), .in_7(N_out),
    .in_8(M_out), .in_9(button_7_out), .in_10(button_8_out), .in_11(button_6_out), .in_12(in_2),
    .out_13(n3_1_out_13));
  Button _4 (.out(_4_out));
  Button _5 (.out(_5_out));
  Button T (.out(T_out));
  Button R (.out(R_out));
  Button Y (.out(Y_out));
  Button D (.out(D_out));
  Button G (.out(G_out));
  Button F (.out(F_out));
  Button B (.out(B_out));
  Button V (.out(V_out));
  Button C (.out(C_out));
  Button _8_star (.out(_8_star_out));
  Button _6 (.out(_6_out));
  Button _7 (.out(_7_out));
  Button I (.out(I_out));
  Button O (.out(O_out));
  Button U (.out(U_out));
  Button H (.out(H_out));
  Button J (.out(J_out));
  Button K (.out(K_out));
  Button N (.out(N_out));
  Button M (.out(M_out));
  Button button_3 (.out(button_3_out));
  Button _9 (.out(_9_out));
  Button _0 (.out(_0_out));
  Button minus_ (.out(minus__out));
  Button button_4 (.out(button_4_out));
  Button P (.out(P_out));
  Button button_5 (.out(button_5_out));
  Button L (.out(L_out));
  Button button_6 (.out(button_6_out));
  Button button_7 (.out(button_7_out));
  Button button_8 (.out(button_8_out));
  Button Ba (.out(Ba_out));
  Button button_9 (.out(button_9_out));
  Button button_10 (.out(button_10_out));
  Button button_11 (.out(button_11_out));
  Button button_12 (.out(button_12_out));
  Button En (.out(En_out));
endmodule

module _1 (
  input  in_1,
  input  in_2,
  input  in_3,
  input  in_4,
  input  in_5,
  input  in_6,
  input  in_7,
  input  in_8,
  input  in_9,
  input  in_10,
  input  in_11,
  input  in_12,
  input  in_13,
  input  in_14,
  output [13:0] out_15
);


  assign out_15 = {in_1, in_2, in_3, in_4, in_5, in_6, in_7, in_8, in_9, in_10, in_11, in_12, in_13, in_14};
endmodule

module _2 (
  input  in_1,
  input  in_2,
  input  in_3,
  input  in_4,
  input  in_5,
  input  in_6,
  input  in_7,
  input  in_8,
  input  in_9,
  input  in_10,
  input  in_11,
  input  in_12,
  input  in_13,
  output [12:0] out_14
);


  assign out_14 = {in_1, in_2, in_3, in_4, in_5, in_6, in_7, in_8, in_9, in_10, in_11, in_12, in_13};
endmodule

module _3 (
  input  in_1,
  input  in_2,
  input  in_3,
  input  in_4,
  input  in_5,
  input  in_6,
  input  in_7,
  input  in_8,
  input  in_9,
  input  in_10,
  input  in_11,
  input  in_12,
  output [11:0] out_13
);


  assign out_13 = {in_1, in_2, in_3, in_4, in_5, in_6, in_7, in_8, in_9, in_10, in_11, in_12};
endmodule
