// Logisim project b.circ as structural Verilog
module _1 (
  output [7:0] out_1,
  output [7:0] out_2,
  output [7:0] out_3,
  output [7:0] out_4,
  output [7:0] out_5,
  output [7:0] out_6,
  output [7:0] out_7,
  output [7:0] out_8,
  output [7:0] out_9,
  output [7:0] out_10,
  output [7:0] out_11
);

  DotMatrix #(.matrixcols(11), .matrixrows(8)) dotmatrix_1 (
    .col0({8{1'b0}}), .col1({8{1'b0}}), .col2({8{1'b0}}), .col3({8{1'b0}}), .col4(8'h22), .col5(8'h7e),
    .col6(8'h2), .col7({8{1'b0}}), .col8({8{1'b0}}), .col9({8{1'b0}}), .col10({8{1'b0}}));

  assign out_1 = {8{1'b0}};
  assign out_2 = {8{1'b0}};
  assign out_3 = {8{1'b0}};
  assign out_4 = {8{1'b0}};
  assign out_5 = {8{1'b0}};
  assign out_6 = 8'h2;
  assign out_7 = 8'h7e;
  assign out_8 = 8'h22;
  assign out_9 = {8{1'b0}};
  assign out_10 = {8{1'b0}};
  assign out_11 = {8{1'b0}};
endmodule

module _2 (
  output [7:0] out_1,
  output [7:0] out_2,
  output [7:0] out_3,
  output [7:0] out_4,
  output [7:0] out_5,
  output [7:0] out_6,
  output [7:0] out_7,
  output [7:0] out_8,
  output [7:0] out_9,
  output [7:0] out_10,
  output [7:0] out_11
);

  DotMatrix #(.matrixcols(11), .matrixrows(8)) dotmatrix_1 (
    .col0({8{1'b0}}), .col1({8{1'b0}}), .col2({8{1'b0}}), .col3(8'h66), .col4(8'h8e), .col5(8'h9a),
    .col6(8'h92), .col7(8'h72), .col8({8{1'b0}}), .col9({8{1'b0}}), .col10({8{1'b0}}));

  assign out_1 = {8{1'b0}};
  assign out_2 = {8{1'b0}};
  assign out_3 = {8{1'b0}};
  assign out_4 = 8'h72;
  assign out_5 = 8'h92;
  assign out_6 = 8'h9a;
  assign out_7 = 8'h8e;
  assign out_8 = 8'h66;
  assign out_9 = {8{1'b0}};
  assign out_10 = {8{1'b0}};
  assign out_11 = {8{1'b0}};
endmodule

module bot_1 (
  output [7:0] out_1,
  output [7:0] out_2,
  output [7:0] out_3,
  output [7:0] out_4,
  output [7:0] out_5,
  output [7:0] out_6,
  output [7:0] out_7,
  output [7:0] out_8,
  output [7:0] out_9,
  output [7:0] out_10,
  output [7:0] out_11,
  output [7:0] out_12,
  output [7:0] out_13,
  output [7:0] out_14,
  output [7:0] out_15,
  output [7:0] out_16,
  output [7:0] out_17,
  output [7:0] out_18,
  output [7:0] out_19,
  output [7:0] out_20,
  output [7:0] out_21,
  output [7:0] out_22,
  output [7:0] out_23,
  output [7:0] out_24,
  output [7:0] out_25,
  output [7:0] out_26,
  output [7:0] out_27,
  output [7:0] out_28,
  output [7:0] out_29,
  output [7:0] out_30,
  output [7:0] out_31,
  output [7:0] out_32
);


  assign out_1 = {8{1'b0}};
  assign out_2 = 8'h2;
  assign out_3 = 8'h7e;
  assign out_4 = 8'h22;
  assign out_5 = {8{1'b0}};
  assign out_6 = {8{1'b0}};
  assign out_7 = {8{1'b0}};
  assign out_8 = 8'h40;
  assign out_9 = 8'h40;
  assign out_10 = 8'h7e;
  assign out_11 = 8'h40;
  assign out_12 = 8'h40;
  assign out_13 = {8{1'b0}};
  assign out_14 = {8{1'b0}};
  assign out_15 = {8{1'b0}};
  assign out_16 = {8{1'b0}};
  assign out_17 = 8'h3c;
  assign out_18 = 8'h42;
  assign out_19 = 8'h42;
  assign out_20 = 8'h42;
  assign out_21 = 8'h3c;
  assign out_22 = {8{1'b0}};
  assign out_23 = {8{1'b0}};
  assign out_24 = {8{1'b0}};
  assign out_25 = {8{1'b0}};
  assign out_26 = 8'h2c;
  assign out_27 = 8'h52;
  assign out_28 = 8'h52;
  assign out_29 = 8'h52;
  assign out_30 = 8'h7e;
  assign out_31 = {8{1'b0}};
  assign out_32 = {8{1'b0}};
endmodule

module vs (
  output [7:0] out_1,
  output [7:0] out_2,
  output [7:0] out_3,
  output [7:0] out_4,
  output [7:0] out_5,
  output [7:0] out_6,
  output [7:0] out_7,
  output [7:0] out_8,
  output [7:0] out_9,
  output [7:0] out_10,
  output [7:0] out_11,
  output [7:0] out_12,
  output [7:0] out_13,
  output [7:0] out_14,
  output [7:0] out_15,
  output [7:0] out_16,
  output [7:0] out_17,
  output [7:0] out_18,
  output [7:0] out_19,
  output [7:0] out_20,
  output [7:0] out_21,
  output [7:0] out_22,
  output [7:0] out_23,
  output [7:0] out_24,
  output [7:0] out_25,
  output [7:0] out_26,
  output [7:0] out_27,
  output [7:0] out_28,
  output [7:0] out_29,
  output [7:0] out_30,
  output [7:0] out_31,
  output [7:0] out_32
);

  DotMatrix #(.matrixcols(32), .matrixrows(8)) dotmatrix_1 (
    .col0(out_1), .col1(out_1), .col2(out_1), .col3(out_1), .col4(out_1), .col5(out_1), .col6(out_1),
    .col7(out_1), .col8(out_1), .col9(8'h78), .col10(8'hc), .col11(8'h6), .col12(8'h3), .col13(8'h6),
    .col14(8'hc), .col15(8'h78), .col16(out_1), .col17(out_1), .col18(8'h66), .col19(8'h72), .col20(8'h5a),
    .col21(8'h4e), .col22(8'h66), .col23(out_1), .col24(out_1), .col25(out_1), .col26(out_1), .col27(out_1),
    .col28(out_1), .col29(out_1), .col30(out_1), .col31(out_1));
  Pull_Resistor pull_resistor_1 (.node(out_1));

  assign out_2 = out_1;
  assign out_3 = out_1;
  assign out_4 = out_1;
  assign out_5 = out_1;
  assign out_6 = out_1;
  assign out_7 = out_1;
  assign out_8 = out_1;
  assign out_9 = out_1;
  assign out_10 = 8'h66;
  assign out_11 = 8'h4e;
  assign out_12 = 8'h5a;
  assign out_13 = 8'h72;
  assign out_14 = 8'h66;
  assign out_15 = out_1;
  assign out_16 = out_1;
  assign out_17 = 8'h78;
  assign out_18 = 8'hc;
  assign out_19 = 8'h6;
  assign out_20 = 8'h3;
  assign out_21 = 8'h6;
  assign out_22 = 8'hc;
  assign out_23 = 8'h78;
  assign out_24 = out_1;
  assign out_25 = out_1;
  assign out_26 = out_1;
  assign out_27 = out_1;
  assign out_28 = out_1;
  assign out_29 = out_1;
  assign out_30 = out_1;
  assign out_31 = out_1;
  assign out_32 = out_1;
endmodule
