// Logisim project bolh.circ as structural Verilog: 2 circuits, main circuit main
module main (
  input  in_1,
  input  in_2,
  input  in_3,
  input  in_4,
  input  in_5,
  input  in_6,
  input  reset,
  input  [31:0] in_8,
  input  [31:0] in_9,
  input  [31:0] in_10,
  input  [31:0] in_11,
  input  [31:0] in_12,
  input  [31:0] in_13,
  input  [31:0] in_14,
  input  [31:0] in_15,
  input  [31:0] in_16,
  input  [31:0] in_17,
  input  [31:0] in_18,
  input  [31:0] in_19,
  input  [31:0] in_20,
  input  [31:0] in_21,
  input  [31:0] in_22,
  input  [31:0] in_23,
  input  [31:0] in_24,
  input  [31:0] in_25,
  input  [31:0] in_26,
  input  [31:0] in_27,
  input  [31:0] in_28,
  input  [31:0] in_29,
  input  [31:0] in_30,
  input  [31:0] in_31,
  input  [31:0] in_32,
  input  [31:0] in_33,
  input  [31:0] in_34,
  input  [31:0] in_35,
  input  [31:0] in_36,
  input  [31:0] in_37,
  input  [31:0] in_38,
  input  [31:0] in_39,
  input  [31:0] in_40,
  input  [31:0] in_41,
  input  [31:0] in_42,
  input  [31:0] in_43,
  input  [31:0] in_44,
  input  [31:0] in_45,
  input  [31:0] in_46,
  input  [31:0] in_47,
  input  [31:0] in_48,
  input  [31:0] in_49,
  input  [31:0] in_50,
  input  [31:0] in_51,
  input  [31:0] in_52,
  input  [31:0] in_53,
  input  [31:0] in_54,
  input  [31:0] in_55,
  input  [31:0] in_56,
  output [31:0] out_57,
  output [31:0] out_58,
  output [31:0] out_59,
  output [31:0] out_60,
  output [31:0] out_61,
  output [31:0] out_62,
  output [31:0] out_63,
  output [31:0] out_64,
  output [31:0] out_65,
  output [31:0] out_66,
  output [31:0] out_67,
  output [31:0] out_68,
  output [31:0] out_69,
  output [31:0] out_70,
  output [31:0] out_71,
  output [31:0] out_72,
  output [31:0] out_73,
  output [31:0] out_74,
  output [31:0] out_75,
  output [31:0] out_76,
  output [31:0] out_77,
  output [31:0] out_78,
  output [31:0] out_79,
  output [31:0] out_80,
  output [31:0] out_81,
  output [31:0] out_82,
  output [31:0] out_83,
  output [31:0] out_84,
  output [31:0] out_85,
  output [31:0] out_86,
  output [31:0] out_87,
  output [31:0] out_88,
  output [31:0] out_89,
  output [31:0] out_90,
  output [31:0] out_91,
  output [31:0] out_92,
  output [31:0] out_93,
  output [31:0] out_94,
  output [31:0] out_95,
  output [31:0] out_96,
  output [31:0] out_97,
  output [31:0] out_98,
  output [31:0] out_99,
  output [31:0] out_100,
  output [31:0] out_101,
  output [31:0] out_102,
  output [31:0] out_103,
  output [31:0] out_104,
  output [31:0] out_105
);

  wire clock_1_out, clock_2_out, comparator_1_eq, comparator_1_gt, comparator_2_eq, comparator_2_gt, klok,
       klok1, niiio, or_1_out, or_2_out, register_1_q, register_2_q, shift_register_1_out,
       shift_register_1_q0, shift_register_1_q1, shift_register_1_q2, shift_register_1_q3,
       shift_register_1_q4, shift_register_1_q5, shift_register_1_q6, shift_register_1_q7,
       shift_register_1_q8, shift_register_1_q9, shift_register_1_q10, shift_register_1_q11,
       shift_register_1_q12, shift_register_1_q13, shift_register_1_q14, shift_register_1_q15,
       shift_register_1_q16, shift_register_1_q17, shift_register_1_q18, shift_register_1_q19,
       shift_register_1_q20, shift_register_1_q21, shift_register_1_q22, shift_register_1_q23,
       shift_register_1_q24, shift_register_1_q25, shift_register_1_q26, shift_register_1_q27,
       shift_register_1_q28, shift_register_1_q29, shift_register_1_q30, shift_register_1_q31,
       shift_register_2_q0, shift_register_2_q1, shift_register_2_q2, shift_register_2_q3,
       shift_register_2_q4, shift_register_2_q5, shift_register_2_q6, shift_register_2_q7,
       shift_register_2_q8, shift_register_2_q9, shift_register_2_q10, shift_register_2_q11,
       shift_register_2_q12, shift_register_2_q13, shift_register_2_q14, shift_register_2_q15,
       shift_register_2_q16, shift_register_2_q17, shift_register_2_q18, shift_register_2_q19,
       shift_register_2_q20, shift_register_2_q21, shift_register_2_q22, shift_register_3_out,
       shift_register_3_q0, shift_register_3_q1, shift_register_3_q2, shift_register_3_q3,
       shift_register_3_q4, shift_register_3_q5, shift_register_3_q6, shift_register_3_q7,
       shift_register_3_q8, shift_register_3_q9, shift_register_3_q10, shift_register_3_q11,
       shift_register_3_q12, shift_register_3_q13, shift_register_3_q14, shift_register_3_q15,
       shift_register_3_q16, shift_register_3_q17, shift_register_3_q18, shift_register_3_q19,
       shift_register_3_q20, shift_register_3_q21, shift_register_3_q22, shift_register_3_q23,
       shift_register_3_q24, shift_register_3_q25, shift_register_3_q26, shift_register_3_q27,
       shift_register_3_q28, shift_register_3_q29, shift_register_3_q30, shift_register_3_q31,
       shift_register_4_q0, shift_register_4_q1, shift_register_4_q2, shift_register_4_q3,
       shift_register_4_q4, shift_register_4_q5, shift_register_4_q6, shift_register_4_q7,
       shift_register_4_q8, shift_register_4_q9, shift_register_4_q10, shift_register_4_q11,
       shift_register_4_q12, shift_register_4_q13, shift_register_4_q14, shift_register_4_q15,
       shift_register_4_q16, sos, sos1, xor_1_out, xor_2_out, xor_3_out, xor_4_out, xor_5_out, xor_6_out,
       xor_7_out, xor_8_out, xor_9_out, xor_10_out, xor_11_out, xor_12_out, xor_13_out, xor_15_out,
       xor_16_out, xor_17_out, xor_18_out, xor_19_out, xor_20_out, xor_21_out, xor_22_out, xor_23_out,
       xor_24_out, xor_25_out, xor_26_out, xor_27_out, xor_28_out, xor_29_out, xor_30_out, xor_31_out,
       xor_32_out, xor_33_out, xor_34_out, xor_35_out, xor_36_out, xor_37_out, xor_38_out, xor_39_out,
       xor_40_out, xor_41_out, xor_42_out, xor_43_out, xor_44_out, xor_45_out, xor_46_out, xor_48_out,
       xor_49_out, xor_50_out, xor_51_out, xor_52_out, xor_53_out, xor_54_out, xor_55_out, xor_56_out,
       xor_57_out, xor_58_out, xor_59_out, xor_60_out, xor_61_out, xor_62_out, xor_63_out, xor_64_out,
       xor_65_out, xor_66_out;
  wire [7:0] n1_1_out_7, n1_1_out_8;
  wire [31:0] bit_extender_1_out, bit_extender_2_out, counter_1_q, counter_2_q, subtractor_1_out,
       subtractor_2_out;

  _1 u_1_1 (
    .set(in_5), .out_7(n1_1_out_7), .out_8(n1_1_out_8), .in_1(in_3), .in_2(in_1), .in_3(in_4), .in_4(in_2),
    .reset(in_6));
  // Probe on n1_1_out_7
  // Probe on n1_1_out_8
  assign bit_extender_1_out = {{24{1'b0}}, n1_1_out_8};  // Bit_Extender bit_extender_1
  Subtractor #(.width(32)) subtractor_1 (.a(bit_extender_1_out), .b(32'h7), .out(subtractor_1_out));  // open: bin, bout
  Shift_Register #(.length(32)) shift_register_1 (
    .shift(1'b1), .in(1'b1), .clk(klok), .out(shift_register_1_out), .clr(reset), .q0(shift_register_1_q0),
    .q1(shift_register_1_q1), .q2(shift_register_1_q2), .q3(shift_register_1_q3), .q4(shift_register_1_q4),
    .q5(shift_register_1_q5), .q6(shift_register_1_q6), .q7(shift_register_1_q7), .q8(shift_register_1_q8),
    .q9(shift_register_1_q9), .q10(shift_register_1_q10), .q11(shift_register_1_q11),
    .q12(shift_register_1_q12), .q13(shift_register_1_q13), .q14(shift_register_1_q14),
    .q15(shift_register_1_q15), .q16(shift_register_1_q16), .q17(shift_register_1_q17),
    .q18(shift_register_1_q18), .q19(shift_register_1_q19), .q20(shift_register_1_q20),
    .q21(shift_register_1_q21), .q22(shift_register_1_q22), .q23(shift_register_1_q23),
    .q24(shift_register_1_q24), .q25(shift_register_1_q25), .q26(shift_register_1_q26),
    .q27(shift_register_1_q27), .q28(shift_register_1_q28), .q29(shift_register_1_q29),
    .q30(shift_register_1_q30), .q31(shift_register_1_q31));  // open: load, d0, d1, d2, d3, d4, d5, d6, d7, d8, d9, d10, d11, d12, d13, d14, d15, d16, d17, d18, d19, d20, d21, d22, d23, d24, d25, d26, d27, d28, d29, d30, d31
  xor xor_1 (xor_1_out, shift_register_1_q0, shift_register_1_q1);
  Counter #(.width(32), .max('hffffffff)) counter_1 (
    .Q(counter_1_q), .clk(klok), .clr(reset));  // open: load, D, count, carry
  xor xor_2 (xor_2_out, shift_register_1_q1, shift_register_1_q2);
  xor xor_3 (xor_3_out, shift_register_1_q2, shift_register_1_q3);
  and and_1 (klok, or_1_out, clock_1_out);
  Clock clock_1 (.out(clock_1_out));
  or or_1 (or_1_out, comparator_1_gt, comparator_1_eq);
  Comparator #(.width(32)) comparator_1 (
    .a(subtractor_1_out), .b(counter_1_q), .gt(comparator_1_gt), .eq(comparator_1_eq));  // open: lt
  xor xor_4 (xor_4_out, shift_register_1_q3, shift_register_1_q4);
  xor xor_5 (xor_5_out, shift_register_1_q4, shift_register_1_q5);
  xor xor_6 (xor_6_out, shift_register_1_q5, shift_register_1_q6);
  xor xor_7 (xor_7_out, shift_register_1_q6, shift_register_1_q7);
  assign bit_extender_2_out = {{24{1'b0}}, n1_1_out_7};  // Bit_Extender bit_extender_2
  xor xor_8 (xor_8_out, shift_register_1_q8, shift_register_1_q9);
  xor xor_9 (xor_9_out, shift_register_1_q7, shift_register_1_q8);
  Shift_Register #(.length(24)) shift_register_2 (
    .shift(1'b1), .in(sos), .clk(klok), .clr(reset), .q0(shift_register_2_q0), .q1(shift_register_2_q1),
    .q2(shift_register_2_q2), .q3(shift_register_2_q3), .q4(shift_register_2_q4), .q5(shift_register_2_q5),
    .q6(shift_register_2_q6), .q7(shift_register_2_q7), .q8(shift_register_2_q8), .q9(shift_register_2_q9),
    .q10(shift_register_2_q10), .q11(shift_register_2_q11), .q12(shift_register_2_q12),
    .q13(shift_register_2_q13), .q14(shift_register_2_q14), .q15(shift_register_2_q15),
    .q16(shift_register_2_q16), .q17(shift_register_2_q17), .q18(shift_register_2_q18),
    .q19(shift_register_2_q19), .q20(shift_register_2_q20), .q21(shift_register_2_q21),
    .q22(shift_register_2_q22));  // open: out, load, d0, d1, d2, d3, d4, d5, d6, d7, d8, d9, d10, d11, d12, d13, d14, d15, d16, d17, d18, d19, d20, d21, d22, d23, q23
  xor xor_10 (xor_10_out, shift_register_1_q9, shift_register_1_q10);
  xor xor_11 (xor_11_out, shift_register_1_q10, shift_register_1_q11);
  Subtractor #(.width(32)) subtractor_2 (.a(bit_extender_2_out), .b(32'hc), .out(subtractor_2_out));  // open: bin, bout
  Register #(.width(1)) register_1 (
    .D(shift_register_2_q0), .Q(register_1_q), .clk(shift_register_2_q0), .clr(reset));  // open: en
  xor xor_12 (xor_12_out, shift_register_1_q11, shift_register_1_q12);
  xor xor_13 (xor_13_out, shift_register_1_q12, shift_register_1_q13);
  or or_2 (or_2_out, comparator_2_gt, comparator_2_eq);
  Comparator #(.width(32)) comparator_2 (
    .a(subtractor_2_out), .b(counter_2_q), .gt(comparator_2_gt), .eq(comparator_2_eq));  // open: lt
  Counter #(.width(32), .max('hffffffff)) counter_2 (
    .Q(counter_2_q), .clk(klok1), .clr(reset));  // open: load, D, count, carry
  xor xor_14 (sos, register_1_q, shift_register_1_out);
  xor xor_15 (xor_15_out, shift_register_1_q13, shift_register_1_q14);
  xor xor_16 (xor_16_out, shift_register_1_q14, shift_register_1_q15);
  and and_2 (klok1, or_2_out, clock_2_out);
  Clock clock_2 (.out(clock_2_out));
  xor xor_17 (xor_17_out, shift_register_1_q16, shift_register_1_q17);
  xor xor_18 (xor_18_out, shift_register_1_q15, shift_register_1_q16);
  xor xor_19 (xor_19_out, shift_register_1_q17, shift_register_1_q18);
  xor xor_20 (xor_20_out, shift_register_1_q18, shift_register_1_q19);
  xor xor_21 (xor_21_out, shift_register_1_q20, shift_register_1_q21);
  xor xor_22 (xor_22_out, shift_register_1_q19, shift_register_1_q20);
  xor xor_23 (xor_23_out, shift_register_1_q22, shift_register_1_q23);
  xor xor_24 (xor_24_out, shift_register_1_q21, shift_register_1_q22);
  xor xor_25 (xor_25_out, shift_register_1_q23, shift_register_1_q24);
  xor xor_26 (xor_26_out, shift_register_1_q24, shift_register_1_q25);
  xor xor_27 (xor_27_out, shift_register_1_q26, shift_register_1_q27);
  xor xor_28 (xor_28_out, shift_register_1_q25, shift_register_1_q26);
  xor xor_29 (xor_29_out, shift_register_1_q28, shift_register_1_q29);
  xor xor_30 (xor_30_out, shift_register_1_q27, shift_register_1_q28);
  xor xor_31 (xor_31_out, shift_register_1_q29, shift_register_1_q30);
  xor xor_32 (xor_32_out, shift_register_1_q30, shift_register_1_q31);
  xor xor_33 (xor_33_out, shift_register_1_q31, shift_register_1_out);
  or or_3 (niiio, shift_register_2_q22, shift_register_2_q21, shift_register_2_q20, shift_register_2_q19, shift_register_2_q18, shift_register_2_q17, shift_register_2_q16, shift_register_2_q15, shift_register_2_q14, shift_register_2_q13, shift_register_2_q12, shift_register_2_q11, shift_register_2_q10, shift_register_2_q9, shift_register_2_q8, shift_register_2_q7, shift_register_2_q6, shift_register_2_q5, shift_register_2_q4, shift_register_2_q3, shift_register_2_q2, shift_register_2_q1, shift_register_2_q0);
  Shift_Register #(.length(32)) shift_register_3 (
    .shift(1'b1), .in(1'b1), .clk(klok1), .out(shift_register_3_out), .clr(reset), .q0(shift_register_3_q0),
    .q1(shift_register_3_q1), .q2(shift_register_3_q2), .q3(shift_register_3_q3), .q4(shift_register_3_q4),
    .q5(shift_register_3_q5), .q6(shift_register_3_q6), .q7(shift_register_3_q7), .q8(shift_register_3_q8),
    .q9(shift_register_3_q9), .q10(shift_register_3_q10), .q11(shift_register_3_q11),
    .q12(shift_register_3_q12), .q13(shift_register_3_q13), .q14(shift_register_3_q14),
    .q15(shift_register_3_q15), .q16(shift_register_3_q16), .q17(shift_register_3_q17),
    .q18(shift_register_3_q18), .q19(shift_register_3_q19), .q20(shift_register_3_q20),
    .q21(shift_register_3_q21), .q22(shift_register_3_q22), .q23(shift_register_3_q23),
    .q24(shift_register_3_q24), .q25(shift_register_3_q25), .q26(shift_register_3_q26),
    .q27(shift_register_3_q27), .q28(shift_register_3_q28), .q29(shift_register_3_q29),
    .q30(shift_register_3_q30), .q31(shift_register_3_q31));  // open: load, d0, d1, d2, d3, d4, d5, d6, d7, d8, d9, d10, d11, d12, d13, d14, d15, d16, d17, d18, d19, d20, d21, d22, d23, d24, d25, d26, d27, d28, d29, d30, d31
  xor xor_34 (xor_34_out, shift_register_3_q0, shift_register_3_q1);
  xor xor_35 (xor_35_out, shift_register_3_q2, shift_register_3_q3);
  xor xor_36 (xor_36_out, shift_register_3_q1, shift_register_3_q2);
  xor xor_37 (xor_37_out, shift_register_3_q3, shift_register_3_q4);
  xor xor_38 (xor_38_out, shift_register_3_q4, shift_register_3_q5);
  xor xor_39 (xor_39_out, shift_register_3_q6, shift_register_3_q7);
  xor xor_40 (xor_40_out, shift_register_3_q5, shift_register_3_q6);
  xor xor_41 (xor_41_out, shift_register_3_q8, shift_register_3_q9);
  xor xor_42 (xor_42_out, shift_register_3_q7, shift_register_3_q8);
  Shift_Register #(.length(18)) shift_register_4 (
    .shift(1'b1), .in(sos1), .clk(klok1), .clr(reset), .q0(shift_register_4_q0), .q1(shift_register_4_q1),
    .q2(shift_register_4_q2), .q3(shift_register_4_q3), .q4(shift_register_4_q4), .q5(shift_register_4_q5),
    .q6(shift_register_4_q6), .q7(shift_register_4_q7), .q8(shift_register_4_q8), .q9(shift_register_4_q9),
    .q10(shift_register_4_q10), .q11(shift_register_4_q11), .q12(shift_register_4_q12),
    .q13(shift_register_4_q13), .q14(shift_register_4_q14), .q15(shift_register_4_q15),
    .q16(shift_register_4_q16));  // open: out, load, d0, d1, d2, d3, d4, d5, d6, d7, d8, d9, d10, d11, d12, d13, d14, d15, d16, d17, q17
  xor xor_43 (xor_43_out, shift_register_3_q10, shift_register_3_q11);
  xor xor_44 (xor_44_out, shift_register_3_q9, shift_register_3_q10);
  Register #(.width(1)) register_2 (
    .D(shift_register_4_q0), .Q(register_2_q), .clk(shift_register_4_q0), .clr(reset));  // open: en
  xor xor_45 (xor_45_out, shift_register_3_q12, shift_register_3_q13);
  xor xor_46 (xor_46_out, shift_register_3_q11, shift_register_3_q12);
  xor xor_47 (sos1, register_2_q, shift_register_3_out);
  xor xor_48 (xor_48_out, shift_register_3_q13, shift_register_3_q14);
  xor xor_49 (xor_49_out, shift_register_3_q14, shift_register_3_q15);
  xor xor_50 (xor_50_out, shift_register_3_q15, shift_register_3_q16);
  xor xor_51 (xor_51_out, shift_register_3_q16, shift_register_3_q17);
  xor xor_52 (xor_52_out, shift_register_3_q17, shift_register_3_q18);
  xor xor_53 (xor_53_out, shift_register_3_q18, shift_register_3_q19);
  xor xor_54 (xor_54_out, shift_register_3_q20, shift_register_3_q21);
  xor xor_55 (xor_55_out, shift_register_3_q19, shift_register_3_q20);
  xor xor_56 (xor_56_out, shift_register_3_q21, shift_register_3_q22);
  xor xor_57 (xor_57_out, shift_register_3_q22, shift_register_3_q23);
  xor xor_58 (xor_58_out, shift_register_3_q23, shift_register_3_q24);
  xor xor_59 (xor_59_out, shift_register_3_q24, shift_register_3_q25);
  xor xor_60 (xor_60_out, shift_register_3_q25, shift_register_3_q26);
  xor xor_61 (xor_61_out, shift_register_3_q26, shift_register_3_q27);
  xor xor_62 (xor_62_out, shift_register_3_q27, shift_register_3_q28);
  xor xor_63 (xor_63_out, shift_register_3_q28, shift_register_3_q29);
  xor xor_64 (xor_64_out, shift_register_3_q30, shift_register_3_q31);
  xor xor_65 (xor_65_out, shift_register_3_q29, shift_register_3_q30);
  xor xor_66 (xor_66_out, shift_register_3_q31, shift_register_3_out);
  Multiplexer #(.width(32), .enable("false")) multiplexer_1 (
    .in0(in_8), .out(out_57), .sel(shift_register_4_q16));  // open: in1
  Multiplexer #(.width(32), .enable("false")) multiplexer_2 (
    .in0(in_9), .out(out_58), .sel(shift_register_4_q15));  // open: in1
  Multiplexer #(.width(32), .enable("false")) multiplexer_3 (
    .in0(in_10), .out(out_59), .sel(shift_register_4_q14));  // open: in1
  Multiplexer #(.width(32), .enable("false")) multiplexer_4 (
    .in0(in_11), .out(out_60), .sel(shift_register_4_q13));  // open: in1
  Multiplexer #(.width(32), .enable("false")) multiplexer_5 (
    .in0(in_12), .out(out_61), .sel(shift_register_4_q12));  // open: in1
  Multiplexer #(.width(32), .enable("false")) multiplexer_6 (
    .in0(in_13), .out(out_62), .sel(shift_register_4_q11));  // open: in1
  Multiplexer #(.width(32), .enable("false")) multiplexer_7 (
    .in0(in_14), .out(out_63), .sel(shift_register_4_q10));  // open: in1
  Multiplexer #(.width(32), .enable("false")) multiplexer_8 (
    .in0(in_15), .out(out_64), .sel(shift_register_4_q9));  // open: in1
  Multiplexer #(.width(32), .enable("false")) multiplexer_9 (
    .in0(in_16), .out(out_65), .sel(shift_register_4_q8));  // open: in1
  Multiplexer #(.width(32), .enable("false")) multiplexer_10 (
    .in0(in_17), .out(out_66), .sel(shift_register_4_q7));  // open: in1
  Multiplexer #(.width(32), .enable("false")) multiplexer_11 (
    .in0(in_18), .out(out_67), .sel(shift_register_4_q6));  // open: in1
  Multiplexer #(.width(32), .enable("false")) multiplexer_12 (
    .in0(in_19), .out(out_68), .sel(shift_register_4_q5));  // open: in1
  Multiplexer #(.width(32), .enable("false")) multiplexer_13 (
    .in0(in_20), .out(out_69), .sel(shift_register_4_q4));  // open: in1
  Multiplexer #(.width(32), .enable("false")) multiplexer_14 (
    .in0(in_21), .out(out_70), .sel(shift_register_4_q3));  // open: in1
  Multiplexer #(.width(32), .enable("false")) multiplexer_15 (
    .in0(in_22), .out(out_71), .sel(shift_register_4_q2));  // open: in1
  Multiplexer #(.width(32), .enable("false")) multiplexer_16 (
    .in0(in_23), .out(out_72), .sel(shift_register_4_q1));  // open: in1
  Multiplexer #(.width(32), .enable("false")) multiplexer_17 (
    .in0(in_24), .out(out_73), .sel(shift_register_4_q0));  // open: in1
  Multiplexer #(.width(32), .enable("false")) multiplexer_18 (
    .in0(in_25), .out(out_74), .sel(xor_66_out));  // open: in1
  Multiplexer #(.width(32), .enable("false")) multiplexer_19 (
    .in0(in_26), .out(out_75), .sel(xor_64_out));  // open: in1
  Multiplexer #(.width(32), .enable("false")) multiplexer_20 (
    .in0(in_27), .out(out_76), .sel(xor_65_out));  // open: in1
  Multiplexer #(.width(32), .enable("false")) multiplexer_21 (
    .in0(in_28), .out(out_77), .sel(xor_63_out));  // open: in1
  Multiplexer #(.width(32), .enable("false")) multiplexer_22 (
    .in0(in_29), .out(out_78), .sel(xor_62_out));  // open: in1
  Multiplexer #(.width(32), .enable("false")) multiplexer_23 (
    .in0(in_30), .out(out_79), .sel(xor_61_out));  // open: in1
  Multiplexer #(.width(32), .enable("false")) multiplexer_24 (
    .in0(in_31), .out(out_80), .sel(xor_60_out));  // open: in1
  Multiplexer #(.width(32), .enable("false")) multiplexer_25 (
    .in0(in_32), .out(out_81), .sel(xor_59_out));  // open: in1
  Multiplexer #(.width(32), .enable("false")) multiplexer_26 (
    .in0(in_33), .out(out_82), .sel(xor_58_out));  // open: in1
  Multiplexer #(.width(32), .enable("false")) multiplexer_27 (
    .in0(in_34), .out(out_83), .sel(xor_57_out));  // open: in1
  Multiplexer #(.width(32), .enable("false")) multiplexer_28 (
    .in0(in_35), .out(out_84), .sel(xor_56_out));  // open: in1
  Multiplexer #(.width(32), .enable("false")) multiplexer_29 (
    .in0(in_36), .out(out_85), .sel(xor_54_out));  // open: in1
  Multiplexer #(.width(32), .enable("false")) multiplexer_30 (
    .in0(in_37), .out(out_86), .sel(xor_55_out));  // open: in1
  Multiplexer #(.width(32), .enable("false")) multiplexer_31 (
    .in0(in_38), .out(out_87), .sel(xor_53_out));  // open: in1
  Multiplexer #(.width(32), .enable("false")) multiplexer_32 (
    .in0(in_39), .out(out_88), .sel(xor_52_out));  // open: in1
  Multiplexer #(.width(32), .enable("false")) multiplexer_33 (
    .in0(in_40), .out(out_89), .sel(xor_51_out));  // open: in1
  Multiplexer #(.width(32), .enable("false")) multiplexer_34 (
    .in0(in_41), .out(out_90), .sel(xor_50_out));  // open: in1
  Multiplexer #(.width(32), .enable("false")) multiplexer_35 (
    .in0(in_42), .out(out_91), .sel(xor_49_out));  // open: in1
  Multiplexer #(.width(32), .enable("false")) multiplexer_36 (
    .in0(in_43), .out(out_92), .sel(xor_48_out));  // open: in1
  Multiplexer #(.width(32), .enable("false")) multiplexer_37 (
    .in0(in_44), .out(out_93), .sel(xor_45_out));  // open: in1
  Multiplexer #(.width(32), .enable("false")) multiplexer_38 (
    .in0(in_45), .out(out_94), .sel(xor_46_out));  // open: in1
  Multiplexer #(.width(32), .enable("false")) multiplexer_39 (
    .in0(in_46), .out(out_95), .sel(xor_43_out));  // open: in1
  Multiplexer #(.width(32), .enable("false")) multiplexer_40 (
    .in0(in_47), .out(out_96), .sel(xor_44_out));  // open: in1
  Multiplexer #(.width(32), .enable("false")) multiplexer_41 (
    .in0(in_48), .out(out_97), .sel(xor_41_out));  // open: in1
  Multiplexer #(.width(32), .enable("false")) multiplexer_42 (
    .in0(in_49), .out(out_98), .sel(xor_42_out));  // open: in1
  Multiplexer #(.width(32), .enable("false")) multiplexer_43 (
    .in0(in_50), .out(out_99), .sel(xor_39_out));  // open: in1
  Multiplexer #(.width(32), .enable("false")) multiplexer_44 (
    .in0(in_51), .out(out_100), .sel(xor_40_out));  // open: in1
  Multiplexer #(.width(32), .enable("false")) multiplexer_45 (
    .in0(in_52), .out(out_101), .sel(xor_38_out));  // open: in1
  Multiplexer #(.width(32), .enable("false")) multiplexer_46 (
    .in0(in_53), .out(out_102), .sel(xor_37_out));  // open: in1
  Multiplexer #(.width(32), .enable("false")) multiplexer_47 (
    .in0(in_54), .out(out_103), .sel(xor_35_out));  // open: in1
  Multiplexer #(.width(32), .enable("false")) multiplexer_48 (
    .in0(in_55), .out(out_104), .sel(xor_36_out));  // open: in1
  Multiplexer #(.width(32), .enable("false")) multiplexer_49 (
    .in0(in_56), .out(out_105), .sel(xor_34_out));  // open: in1

  // Other names for the same wires on the sheet: m = klok; m1 = klok1

  // Notes on the sheet:
  //   12
endmodule

module _1 (
  input  in_1,
  input  in_2,
  input  in_3,
  input  in_4,
  input  reset,
  input  set,
  output [7:0] out_7,
  output [7:0] out_8
);

  wire and_1_out, and_3_out, comparator_1_eq, comparator_2_eq, comparator_3_eq, comparator_4_eq,
       multiplexer_1_out, or_3_out, or_4_out, or_5_out, or_6_out, register_1_q, \sos_Χ , \sos_Χ1 , \sos_Ψ ,
       \sos_Ψ1 , \Χ_minus , \Χ_plus , \Ψ_minus , \Ψ_plus ;

  and and_1 (and_1_out, in_1, \sos_Χ1 );
  and and_2 (\Χ_minus , in_2, \sos_Χ );
  or or_1 (\Χ_plus , and_1_out, \Χ_minus );
  Register #(.width(1)) register_1 (.D(set), .Q(register_1_q), .clk(set), .clr(reset));  // open: en
  and and_3 (and_3_out, in_3, \sos_Ψ1 );
  Multiplexer #(.enable("false")) multiplexer_1 (.in0(1'b0), .in1(1'b1), .out(multiplexer_1_out), .sel(register_1_q));
  and and_4 (\Ψ_minus , in_4, \sos_Ψ );
  or or_2 (\Ψ_plus , and_3_out, \Ψ_minus );
  or or_3 (or_3_out, \Χ_minus , set);
  Counter counter_1 (
    .load(or_3_out), .D(8'hc), .count(multiplexer_1_out), .Q(out_7), .clk(or_4_out), .clr(reset));  // open: carry
  or or_4 (or_4_out, set, \Χ_plus );
  or or_5 (or_5_out, \Ψ_minus , set);
  Counter counter_2 (
    .load(or_5_out), .D(8'h7), .count(multiplexer_1_out), .Q(out_8), .clk(or_6_out), .clr(reset));  // open: carry
  or or_6 (or_6_out, set, \Ψ_plus );
  not not_1 (\sos_Χ , comparator_1_eq);
  Comparator comparator_1 (.a(out_7), .b(8'hc), .eq(comparator_1_eq));  // open: gt, lt
  not not_2 (\sos_Ψ , comparator_2_eq);
  Comparator comparator_2 (.a(out_8), .b(8'h7), .eq(comparator_2_eq));  // open: gt, lt
  Comparator comparator_3 (.a(out_8), .b(8'h3d), .eq(comparator_3_eq));  // open: gt, lt
  not not_3 (\sos_Χ1 , comparator_4_eq);
  Comparator comparator_4 (.a(out_7), .b(8'h3c), .eq(comparator_4_eq));  // open: gt, lt
  not not_4 (\sos_Ψ1 , comparator_3_eq);
endmodule
