// Logisim project sos.circ as structural Verilog
module main (
  input  [31:0] in_1,
  output out_2,
  output [31:0] out_3
);

  wire comparator_1_eq, comparator_2_eq, comparator_3_eq, comparator_4_eq, comparator_5_eq, comparator_6_eq,
       comparator_7_eq, comparator_8_eq, comparator_9_eq, comparator_10_eq, comparator_11_eq,
       comparator_12_eq, comparator_13_eq, comparator_14_eq, comparator_15_eq, comparator_16_eq,
       comparator_17_eq, comparator_18_eq, comparator_19_eq, comparator_20_eq, comparator_21_eq,
       comparator_22_eq, comparator_23_eq, comparator_24_eq, comparator_25_eq;
  wire [4:0] controlled_buffer_1_out;
  wire [31:0] _1, _2, _3, _4, _5, _6, _7, _8, _9, _10, _11, _12, _13, _14, _15, _16, _17, _18, _19, _20, _21,
       _22, _23, _24, multiplexer_1_out, n2_1_out_2, n2_1_out_3, n2_1_out_4, n2_1_out_5, n2_1_out_6,
       n2_1_out_7, n2_1_out_8, n2_1_out_9, n2_1_out_10, n2_1_out_11, n2_1_out_12, n2_1_out_13, n2_1_out_14,
       n2_1_out_15, n2_1_out_16, n2_1_out_17, n2_1_out_18, n2_1_out_19, n2_1_out_20, n2_1_out_21,
       n2_1_out_22, n2_1_out_23, n2_1_out_24, n2_1_out_25;

  Comparator #(.width(32)) comparator_1 (.a(in_1), .b(32'ha0), .eq(comparator_1_eq));  // open: gt, lt
  Comparator #(.width(32)) comparator_2 (.a(in_1), .b(_1), .eq(comparator_2_eq));  // open: gt, lt
  Comparator #(.width(32)) comparator_3 (.a(in_1), .b(_2), .eq(comparator_3_eq));  // open: gt, lt
  Comparator #(.width(32)) comparator_4 (.a(in_1), .b(_3), .eq(comparator_4_eq));  // open: gt, lt
  Comparator #(.width(32)) comparator_5 (.a(in_1), .b(_4), .eq(comparator_5_eq));  // open: gt, lt
  Comparator #(.width(32)) comparator_6 (.a(in_1), .b(_5), .eq(comparator_6_eq));  // open: gt, lt
  Comparator #(.width(32)) comparator_7 (.a(in_1), .b(_6), .eq(comparator_7_eq));  // open: gt, lt
  Comparator #(.width(32)) comparator_8 (.a(in_1), .b(_7), .eq(comparator_8_eq));  // open: gt, lt
  Comparator #(.width(32)) comparator_9 (.a(in_1), .b(_8), .eq(comparator_9_eq));  // open: gt, lt
  Comparator #(.width(32)) comparator_10 (.a(in_1), .b(_9), .eq(comparator_10_eq));  // open: gt, lt
  Comparator #(.width(32)) comparator_11 (.a(in_1), .b(_10), .eq(comparator_11_eq));  // open: gt, lt
  Comparator #(.width(32)) comparator_12 (.a(in_1), .b(_11), .eq(comparator_12_eq));  // open: gt, lt
  Comparator #(.width(32)) comparator_13 (.a(in_1), .b(_12), .eq(comparator_13_eq));  // open: gt, lt
  Comparator #(.width(32)) comparator_14 (.a(in_1), .b(_13), .eq(comparator_14_eq));  // open: gt, lt
  Comparator #(.width(32)) comparator_15 (.a(in_1), .b(_14), .eq(comparator_15_eq));  // open: gt, lt
  Comparator #(.width(32)) comparator_16 (.a(in_1), .b(_15), .eq(comparator_16_eq));  // open: gt, lt
  Comparator #(.width(32)) comparator_17 (.a(in_1), .b(_16), .eq(comparator_17_eq));  // open: gt, lt
  Comparator #(.width(32)) comparator_18 (.a(in_1), .b(_17), .eq(comparator_18_eq));  // open: gt, lt
  Comparator #(.width(32)) comparator_19 (.a(in_1), .b(_18), .eq(comparator_19_eq));  // open: gt, lt
  Comparator #(.width(32)) comparator_20 (.a(in_1), .b(_19), .eq(comparator_20_eq));  // open: gt, lt
  Comparator #(.width(32)) comparator_21 (.a(in_1), .b(_20), .eq(comparator_21_eq));  // open: gt, lt
  Comparator #(.width(32)) comparator_22 (.a(in_1), .b(_21), .eq(comparator_22_eq));  // open: gt, lt
  Comparator #(.width(32)) comparator_23 (.a(in_1), .b(_22), .eq(comparator_23_eq));  // open: gt, lt
  Comparator #(.width(32)) comparator_24 (.a(in_1), .b(_23), .eq(comparator_24_eq));  // open: gt, lt
  Comparator #(.width(32)) comparator_25 (.a(in_1), .b(_24), .eq(comparator_25_eq));  // open: gt, lt
  _2 u_2_1 (
    .out_2(n2_1_out_2), .out_3(n2_1_out_3), .out_4(n2_1_out_4), .out_5(n2_1_out_5), .out_6(n2_1_out_6),
    .out_7(n2_1_out_7), .out_8(n2_1_out_8), .out_9(n2_1_out_9), .out_10(n2_1_out_10), .out_11(n2_1_out_11),
    .out_12(n2_1_out_12), .out_13(n2_1_out_13), .out_14(n2_1_out_14), .out_15(n2_1_out_15),
    .out_16(n2_1_out_16), .out_17(n2_1_out_17), .out_18(n2_1_out_18), .out_19(n2_1_out_19),
    .out_20(n2_1_out_20), .out_21(n2_1_out_21), .out_22(n2_1_out_22), .out_23(n2_1_out_23),
    .out_24(n2_1_out_24), .out_25(n2_1_out_25), .in_1(32'h80));
  Multiplexer #(.select(5), .width(32), .enable("false")) multiplexer_1 (
    .in0(32'h80), .in1(n2_1_out_2), .in2(n2_1_out_3), .in3(n2_1_out_4), .in4(n2_1_out_5), .in5(n2_1_out_6),
    .in6(n2_1_out_7), .in7(n2_1_out_8), .in8(n2_1_out_9), .in9(n2_1_out_10), .in10(n2_1_out_11),
    .in11(n2_1_out_12), .in12(n2_1_out_13), .in13(n2_1_out_14), .in14(n2_1_out_15), .in15(n2_1_out_16),
    .in16(n2_1_out_17), .in17(n2_1_out_18), .in18(n2_1_out_19), .in19(n2_1_out_20), .in20(n2_1_out_21),
    .in21(n2_1_out_22), .in22(n2_1_out_23), .in23(n2_1_out_24), .in24(n2_1_out_25), .out(multiplexer_1_out),
    .sel(controlled_buffer_1_out));  // open: in25, in26, in27, in28, in29, in30, in31
  Multiplexer #(.width(32), .enable("false")) multiplexer_2 (
    .in0({32{1'b0}}), .in1(multiplexer_1_out), .out(out_3), .sel(out_2));
  assign controlled_buffer_1_out = comparator_25_eq ? {5{1'b0}} : 5'bz;  // Controlled_Buffer controlled_buffer_1
  assign controlled_buffer_1_out = comparator_24_eq ? 5'b00001 : 5'bz;  // Controlled_Buffer controlled_buffer_2
  assign controlled_buffer_1_out = comparator_23_eq ? 5'b00010 : 5'bz;  // Controlled_Buffer controlled_buffer_3
  assign controlled_buffer_1_out = comparator_22_eq ? 5'b00011 : 5'bz;  // Controlled_Buffer controlled_buffer_4
  assign controlled_buffer_1_out = comparator_21_eq ? 5'b00100 : 5'bz;  // Controlled_Buffer controlled_buffer_5
  assign controlled_buffer_1_out = comparator_20_eq ? 5'b00101 : 5'bz;  // Controlled_Buffer controlled_buffer_6
  assign controlled_buffer_1_out = comparator_19_eq ? 5'b00110 : 5'bz;  // Controlled_Buffer controlled_buffer_7
  assign controlled_buffer_1_out = comparator_18_eq ? 5'b00111 : 5'bz;  // Controlled_Buffer controlled_buffer_8
  assign controlled_buffer_1_out = comparator_17_eq ? 5'b01000 : 5'bz;  // Controlled_Buffer controlled_buffer_9
  assign controlled_buffer_1_out = comparator_16_eq ? 5'b01001 : 5'bz;  // Controlled_Buffer controlled_buffer_10
  assign controlled_buffer_1_out = comparator_15_eq ? 5'b01010 : 5'bz;  // Controlled_Buffer controlled_buffer_11
  assign controlled_buffer_1_out = comparator_14_eq ? 5'b01011 : 5'bz;  // Controlled_Buffer controlled_buffer_12
  assign controlled_buffer_1_out = comparator_13_eq ? 5'b01100 : 5'bz;  // Controlled_Buffer controlled_buffer_13
  assign controlled_buffer_1_out = comparator_12_eq ? 5'b01101 : 5'bz;  // Controlled_Buffer controlled_buffer_14
  assign controlled_buffer_1_out = comparator_11_eq ? 5'b01110 : 5'bz;  // Controlled_Buffer controlled_buffer_15
  assign controlled_buffer_1_out = comparator_10_eq ? 5'b01111 : 5'bz;  // Controlled_Buffer controlled_buffer_16
  assign controlled_buffer_1_out = comparator_9_eq ? 5'b10000 : 5'bz;  // Controlled_Buffer controlled_buffer_17
  assign controlled_buffer_1_out = comparator_8_eq ? 5'b10001 : 5'bz;  // Controlled_Buffer controlled_buffer_18
  assign controlled_buffer_1_out = comparator_7_eq ? 5'b10010 : 5'bz;  // Controlled_Buffer controlled_buffer_19
  assign controlled_buffer_1_out = comparator_6_eq ? 5'b10011 : 5'bz;  // Controlled_Buffer controlled_buffer_20
  assign controlled_buffer_1_out = comparator_5_eq ? 5'b10100 : 5'bz;  // Controlled_Buffer controlled_buffer_21
  assign controlled_buffer_1_out = comparator_4_eq ? 5'b10101 : 5'bz;  // Controlled_Buffer controlled_buffer_22
  assign controlled_buffer_1_out = comparator_3_eq ? 5'b10110 : 5'bz;  // Controlled_Buffer controlled_buffer_23
  assign controlled_buffer_1_out = comparator_2_eq ? 5'b10111 : 5'bz;  // Controlled_Buffer controlled_buffer_24
  assign controlled_buffer_1_out = comparator_1_eq ? 5'b11000 : 5'bz;  // Controlled_Buffer controlled_buffer_25
  or or_1 (out_2, comparator_1_eq, comparator_2_eq, comparator_3_eq, comparator_4_eq, comparator_5_eq, comparator_6_eq, comparator_7_eq, comparator_8_eq, comparator_9_eq, comparator_10_eq, comparator_11_eq, comparator_12_eq, comparator_13_eq, comparator_14_eq, comparator_15_eq, comparator_16_eq, comparator_17_eq, comparator_18_eq, comparator_19_eq, comparator_20_eq, comparator_21_eq, comparator_22_eq, comparator_23_eq, comparator_24_eq, comparator_25_eq);
  _2 u__11 (
    .out_2(_1), .out_3(_2), .out_4(_3), .out_5(_4), .out_6(_5), .out_7(_6), .out_8(_7), .out_9(_8),
    .out_10(_9), .out_11(_10), .out_12(_11), .out_13(_12), .out_14(_13), .out_15(_14), .out_16(_15),
    .out_17(_16), .out_18(_17), .out_19(_18), .out_20(_19), .out_21(_20), .out_22(_21), .out_23(_22),
    .out_24(_23), .out_25(_24), .in_1(32'ha0));

  // Other names for the same wires on the sheet: s = out_2
endmodule

module _2 (
  input  [31:0] in_1,
  output [31:0] out_2,
  output [31:0] out_3,
  output [31:0] out_4,
  output [31:0] out_5,
  output [31:0] out_6,
  output [31:0] out_7,
  output [31:0] out_8,
  output [31:0] out_9,
  output [31:0] out_10,
  output [31:0] out_11,
  output [31:0] out_12,
  output [31:0] out_13,
  output [31:0] out_14,
  output [31:0] out_15,
  output [31:0] out_16,
  output [31:0] out_17,
  output [31:0] out_18,
  output [31:0] out_19,
  output [31:0] out_20,
  output [31:0] out_21,
  output [31:0] out_22,
  output [31:0] out_23,
  output [31:0] out_24,
  output [31:0] out_25
);

  Multiplier #(.width(32)) multiplier_1 (.a(in_1), .b(32'h2), .out(out_2));  // open: cin, cout
  Multiplier #(.width(32)) multiplier_2 (.a(out_2), .b(32'h2), .out(out_3));  // open: cin, cout
  Multiplier #(.width(32)) multiplier_3 (.a(out_3), .b(32'h2), .out(out_4));  // open: cin, cout
  Multiplier #(.width(32)) multiplier_4 (.a(out_4), .b(32'h2), .out(out_5));  // open: cin, cout
  Multiplier #(.width(32)) multiplier_5 (.a(out_5), .b(32'h2), .out(out_6));  // open: cin, cout
  Multiplier #(.width(32)) multiplier_6 (.a(out_6), .b(32'h2), .out(out_7));  // open: cin, cout
  Multiplier #(.width(32)) multiplier_7 (.a(out_7), .b(32'h2), .out(out_8));  // open: cin, cout
  Multiplier #(.width(32)) multiplier_8 (.a(out_8), .b(32'h2), .out(out_9));  // open: cin, cout
  Multiplier #(.width(32)) multiplier_9 (.a(out_9), .b(32'h2), .out(out_10));  // open: cin, cout
  Multiplier #(.width(32)) multiplier_10 (.a(out_10), .b(32'h2), .out(out_11));  // open: cin, cout
  Multiplier #(.width(32)) multiplier_11 (.a(out_11), .b(32'h2), .out(out_12));  // open: cin, cout
  Multiplier #(.width(32)) multiplier_12 (.a(out_12), .b(32'h2), .out(out_13));  // open: cin, cout
  Multiplier #(.width(32)) multiplier_13 (.a(out_13), .b(32'h2), .out(out_14));  // open: cin, cout
  Multiplier #(.width(32)) multiplier_14 (.a(out_14), .b(32'h2), .out(out_15));  // open: cin, cout
  Multiplier #(.width(32)) multiplier_15 (.a(out_15), .b(32'h2), .out(out_16));  // open: cin, cout
  Multiplier #(.width(32)) multiplier_16 (.a(out_16), .b(32'h2), .out(out_17));  // open: cin, cout
  Multiplier #(.width(32)) multiplier_17 (.a(out_17), .b(32'h2), .out(out_18));  // open: cin, cout
  Multiplier #(.width(32)) multiplier_18 (.a(out_18), .b(32'h2), .out(out_19));  // open: cin, cout
  Multiplier #(.width(32)) multiplier_19 (.a(out_19), .b(32'h2), .out(out_20));  // open: cin, cout
  Multiplier #(.width(32)) multiplier_20 (.a(out_20), .b(32'h2), .out(out_21));  // open: cin, cout
  Multiplier #(.width(32)) multiplier_21 (.a(out_21), .b(32'h2), .out(out_22));  // open: cin, cout
  Multiplier #(.width(32)) multiplier_22 (.a(out_22), .b(32'h2), .out(out_23));  // open: cin, cout
  Multiplier #(.width(32)) multiplier_23 (.a(out_23), .b(32'h2), .out(out_24));  // open: cin, cout
  Multiplier #(.width(32)) multiplier_24 (.a(out_24), .b(32'h2), .out(out_25));  // open: cin, cout
endmodule

module _3 (
  input  [31:0] in_1,
  input  [31:0] in_2,
  input  [31:0] in_3,
  input  [31:0] in_4,
  input  [31:0] in_5,
  input  [31:0] in_6,
  input  [31:0] in_7,
  input  [31:0] in_8,
  input  [31:0] in_9,
  input  [31:0] in_10,
  input  [31:0] in_11,
  input  [31:0] in_12,
  input  [31:0] in_13,
  input  [31:0] in_14,
  input  [31:0] in_15,
  input  [31:0] in_16,
  input  [31:0] in_17,
  input  [31:0] in_18,
  input  [31:0] in_19,
  input  [31:0] in_20,
  input  [31:0] in_21,
  input  [31:0] in_22,
  input  [31:0] in_23,
  input  [31:0] in_24,
  input  [31:0] in_25,
  input  [31:0] in_26,
  input  [31:0] in_27,
  input  [31:0] in_28,
  input  [31:0] in_29,
  input  [31:0] in_30,
  input  [31:0] in_31,
  input  [31:0] in_32,
  input  [31:0] in_33,
  input  [31:0] in_34,
  input  [31:0] in_35,
  input  [31:0] in_36,
  input  [31:0] in_37,
  input  [31:0] in_38,
  input  [31:0] in_39,
  input  [31:0] in_40,
  input  [31:0] in_41,
  input  [31:0] in_42,
  input  [31:0] in_43,
  input  [31:0] in_44,
  input  [31:0] in_45,
  input  [31:0] in_46,
  input  [31:0] in_47,
  input  [31:0] in_48,
  input  [31:0] in_49,
  output [31:0] out_50
);

  wire [31:0] main_1_out_3, main_2_out_3, main_3_out_3, main_4_out_3, main_5_out_3, main_6_out_3,
       main_7_out_3, main_8_out_3, main_9_out_3, main_10_out_3, main_11_out_3, main_12_out_3, main_13_out_3,
       main_14_out_3, main_15_out_3, main_16_out_3, main_17_out_3, main_18_out_3, main_19_out_3,
       main_20_out_3, main_21_out_3, main_22_out_3, main_23_out_3, main_24_out_3, main_25_out_3,
       main_26_out_3, main_27_out_3, main_29_out_3, main_30_out_3, main_31_out_3, main_32_out_3,
       main_33_out_3, main_34_out_3, main_35_out_3, main_36_out_3, main_37_out_3, main_38_out_3,
       main_39_out_3, main_40_out_3, main_41_out_3, main_42_out_3, main_43_out_3, main_44_out_3,
       main_45_out_3, main_46_out_3, main_47_out_3, main_48_out_3, main_49_out_3, or_1_out, or_3_out;

  assign or_1_out = main_1_out_3 | main_2_out_3 | main_3_out_3 | main_4_out_3 | main_5_out_3 | main_6_out_3 | main_7_out_3 | main_8_out_3 | main_9_out_3 | main_10_out_3 | main_11_out_3 | main_12_out_3 | main_13_out_3 | main_14_out_3 | main_15_out_3 | main_16_out_3 | main_17_out_3 | main_18_out_3 | main_19_out_3 | main_20_out_3 | main_21_out_3 | main_22_out_3 | main_23_out_3 | main_24_out_3 | main_25_out_3 | main_26_out_3 | main_27_out_3 | main_29_out_3 | main_30_out_3 | main_31_out_3 | main_32_out_3;  // OR_Gate or_1, 32 bits wide
  assign out_50 = or_1_out | or_3_out;  // OR_Gate or_2, 32 bits wide
  assign or_3_out = main_33_out_3 | main_34_out_3 | main_35_out_3 | main_36_out_3 | main_37_out_3 | main_38_out_3 | main_39_out_3 | main_40_out_3 | main_41_out_3 | main_42_out_3 | main_43_out_3 | main_44_out_3 | main_45_out_3 | main_46_out_3 | main_47_out_3 | main_48_out_3 | main_49_out_3;  // OR_Gate or_3, 32 bits wide
  main main_1 (.out_3(main_1_out_3), .in_1(in_1));  // open: out_2
  main main_2 (.out_3(main_2_out_3), .in_1(in_2));  // open: out_2
  main main_3 (.out_3(main_3_out_3), .in_1(in_3));  // open: out_2
  main main_4 (.out_3(main_4_out_3), .in_1(in_4));  // open: out_2
  main main_5 (.out_3(main_5_out_3), .in_1(in_5));  // open: out_2
  main main_6 (.out_3(main_6_out_3), .in_1(in_6));  // open: out_2
  main main_7 (.out_3(main_7_out_3), .in_1(in_7));  // open: out_2
  main main_8 (.out_3(main_8_out_3), .in_1(in_8));  // open: out_2
  main main_9 (.out_3(main_9_out_3), .in_1(in_9));  // open: out_2
  main main_10 (.out_3(main_10_out_3), .in_1(in_10));  // open: out_2
  main main_11 (.out_3(main_11_out_3), .in_1(in_11));  // open: out_2
  main main_12 (.out_3(main_12_out_3), .in_1(in_12));  // open: out_2
  main main_13 (.out_3(main_13_out_3), .in_1(in_13));  // open: out_2
  main main_14 (.out_3(main_14_out_3), .in_1(in_14));  // open: out_2
  main main_15 (.out_3(main_15_out_3), .in_1(in_15));  // open: out_2
  main main_16 (.out_3(main_16_out_3), .in_1(in_16));  // open: out_2
  main main_17 (.out_3(main_17_out_3), .in_1(in_17));  // open: out_2
  main main_18 (.out_3(main_18_out_3), .in_1(in_18));  // open: out_2
  main main_19 (.out_3(main_19_out_3), .in_1(in_19));  // open: out_2
  main main_20 (.out_3(main_20_out_3), .in_1(in_20));  // open: out_2
  main main_21 (.out_3(main_21_out_3), .in_1(in_21));  // open: out_2
  main main_22 (.out_3(main_22_out_3), .in_1(in_22));  // open: out_2
  main main_23 (.out_3(main_23_out_3), .in_1(in_23));  // open: out_2
  main main_24 (.out_3(main_24_out_3), .in_1(in_24));  // open: out_2
  main main_25 (.out_3(main_25_out_3), .in_1(in_25));  // open: out_2
  main main_26 (.out_3(main_26_out_3), .in_1(in_26));  // open: out_2
  main main_27 (.out_3(main_27_out_3), .in_1(in_27));  // open: out_2
  main main_28 (.in_1(in_28));  // open: out_2, out_3
  main main_29 (.out_3(main_29_out_3), .in_1(in_29));  // open: out_2
  main main_30 (.out_3(main_30_out_3), .in_1(in_30));  // open: out_2
  main main_31 (.out_3(main_31_out_3), .in_1(in_31));  // open: out_2
  main main_32 (.out_3(main_32_out_3), .in_1(in_32));  // open: out_2
  main main_33 (.out_3(main_33_out_3), .in_1(in_33));  // open: out_2
  main main_34 (.out_3(main_34_out_3), .in_1(in_34));  // open: out_2
  main main_35 (.out_3(main_35_out_3), .in_1(in_35));  // open: out_2
  main main_36 (.out_3(main_36_out_3), .in_1(in_36));  // open: out_2
  main main_37 (.out_3(main_37_out_3), .in_1(in_37));  // open: out_2
  main main_38 (.out_3(main_38_out_3), .in_1(in_38));  // open: out_2
  main main_39 (.out_3(main_39_out_3), .in_1(in_39));  // open: out_2
  main main_40 (.out_3(main_40_out_3), .in_1(in_40));  // open: out_2
  main main_41 (.out_3(main_41_out_3), .in_1(in_41));  // open: out_2
  main main_42 (.out_3(main_42_out_3), .in_1(in_42));  // open: out_2
  main main_43 (.out_3(main_43_out_3), .in_1(in_43));  // open: out_2
  main main_44 (.out_3(main_44_out_3), .in_1(in_44));  // open: out_2
  main main_45 (.out_3(main_45_out_3), .in_1(in_45));  // open: out_2
  main main_46 (.out_3(main_46_out_3), .in_1(in_46));  // open: out_2
  main main_47 (.out_3(main_47_out_3), .in_1(in_47));  // open: out_2
  main main_48 (.out_3(main_48_out_3), .in_1(in_48));  // open: out_2
  main main_49 (.out_3(main_49_out_3), .in_1(in_49));  // open: out_2
endmodule

module _4 (
  input  in_1
);

  wire _1, _2, _3, _4, clock_1_out, keyboard_1_avail, klok, or_3_out, or_4_out, or_5_out, or_6_out,
       plus_or_minus, s1, s2, s3, s4;
  wire [1:0] joystick_1_x, joystick_1_y;
  wire [6:0] keyboard_1_data;
  wire [31:0] neo_1_out_94, neo_1_out_95, neo_1_out_96, neo_1_out_97, neo_1_out_98, neo_1_out_99,
       neo_1_out_100, neo_1_out_101, neo_1_out_102, neo_1_out_103, neo_1_out_104, neo_1_out_105,
       neo_1_out_106, neo_1_out_107, neo_1_out_108, neo_1_out_109, neo_1_out_110, neo_1_out_111,
       neo_1_out_112, neo_1_out_113, neo_1_out_114, neo_1_out_115, neo_1_out_116, neo_1_out_117,
       neo_1_out_118, neo_1_out_119, neo_1_out_120, neo_1_out_121, neo_1_out_122, neo_1_out_123,
       neo_1_out_124, neo_1_out_125, neo_1_out_126, neo_1_out_127, neo_1_out_128, neo_1_out_129,
       neo_1_out_130, neo_1_out_131, neo_1_out_132, neo_1_out_133, neo_1_out_134, neo_1_out_135,
       neo_1_out_136, neo_1_out_137, neo_1_out_138, neo_1_out_139, neo_1_out_140, neo_1_out_141,
       neo_1_out_142, neo_1_out_143, neo_1_out_144, neo_1_out_145, neo_1_out_146, neo_1_out_147,
       neo_1_out_148, neo_1_out_149, neo_1_out_150, neo_1_out_151, neo_1_out_152, neo_1_out_153,
       neo_1_out_154, neo_1_out_155, neo_1_out_156, neo_1_out_157, neo_2_out_98, neo_2_out_99, neo_2_out_100,
       neo_2_out_101, neo_2_out_102, neo_2_out_103, neo_2_out_104, neo_2_out_105, neo_2_out_106,
       neo_2_out_107, neo_2_out_108, neo_2_out_109, neo_2_out_110, neo_2_out_111, neo_2_out_112,
       neo_2_out_113, neo_2_out_114, neo_2_out_115, neo_2_out_116, neo_2_out_117, neo_2_out_118,
       neo_2_out_119, neo_2_out_120, neo_2_out_121, neo_2_out_122, neo_2_out_123, neo_2_out_124,
       neo_2_out_125, neo_2_out_126, neo_2_out_127, neo_2_out_128, neo_2_out_129, neo_2_out_130,
       neo_2_out_131, neo_2_out_132, neo_2_out_133, neo_2_out_134, neo_2_out_135, neo_2_out_136,
       neo_2_out_137, neo_2_out_138, neo_2_out_139, neo_2_out_140, neo_2_out_141, neo_2_out_142,
       neo_2_out_143, neo_2_out_144, neo_2_out_145, neo_2_out_146, telos_1_out_4, telos_1_out_5,
       telos_1_out_6, telos_1_out_7, telos_1_out_8, telos_1_out_9, telos_1_out_10, telos_1_out_11,
       telos_1_out_12, telos_1_out_13, telos_1_out_14, telos_1_out_15, telos_1_out_16, telos_1_out_17,
       telos_1_out_18, telos_1_out_19, telos_1_out_20, telos_1_out_21, telos_1_out_22, telos_1_out_23,
       telos_1_out_24, telos_1_out_25, telos_1_out_26, telos_1_out_27, telos_1_out_28, telos_1_out_29,
       telos_2_out_4, telos_2_out_5, telos_2_out_6, telos_2_out_7, telos_2_out_8, telos_2_out_9,
       telos_2_out_10, telos_2_out_11, telos_2_out_12, telos_2_out_13, telos_2_out_14, telos_2_out_15,
       telos_2_out_16, telos_2_out_17, telos_2_out_18, telos_2_out_19, telos_2_out_20, telos_2_out_21,
       telos_2_out_22, telos_2_out_23, telos_2_out_24, telos_2_out_25, telos_2_out_26, telos_2_out_27,
       telos_2_out_28, telos_2_out_29;

  or or_1 (klok, s3, _4);
  or or_2 (plus_or_minus, s4, _3);
  Clock clock_1 (.out(clock_1_out));
  Keyboard keyboard_1 (.clk(clock_1_out), .avail(keyboard_1_avail), .data(keyboard_1_data));  // open: re, clr
  Joystick #(.bits(2)) joystick_1 (.x(joystick_1_x), .y(joystick_1_y));
  ss ss_1 (.in_1(keyboard_1_avail), .in_2(keyboard_1_data), .out_5(_2), .out_3(_1), .out_6(_3), .out_4(_4));
  mox mox_1 (.out_3(s1), .out_4(s2), .in_1(joystick_1_x), .in_2(joystick_1_y), .out_5(s4), .out_6(s3));
  telos telos_1 (
    .in_1(plus_or_minus), .in_3(in_1), .in_2(klok), .out_4(telos_1_out_4), .out_5(telos_1_out_5),
    .out_6(telos_1_out_6), .out_7(telos_1_out_7), .out_8(telos_1_out_8), .out_9(telos_1_out_9),
    .out_10(telos_1_out_10), .out_11(telos_1_out_11), .out_12(telos_1_out_12), .out_13(telos_1_out_13),
    .out_14(telos_1_out_14), .out_15(telos_1_out_15), .out_16(telos_1_out_16), .out_17(telos_1_out_17),
    .out_18(telos_1_out_18), .out_19(telos_1_out_19), .out_20(telos_1_out_20), .out_21(telos_1_out_21),
    .out_22(telos_1_out_22), .out_23(telos_1_out_23), .out_24(telos_1_out_24), .out_25(telos_1_out_25),
    .out_26(telos_1_out_26), .out_27(telos_1_out_27), .out_28(telos_1_out_28), .out_29(telos_1_out_29));
  DotMatrix #(.matrixcols(32), .matrixrows(32)) dotmatrix_1 (
    .col0(neo_1_out_157), .col1(neo_1_out_156), .col2(neo_1_out_155), .col3(neo_1_out_154),
    .col4(neo_1_out_153), .col5(neo_1_out_152), .col6(neo_1_out_151), .col7(neo_1_out_150),
    .col8(neo_1_out_149), .col9(neo_1_out_148), .col10(neo_1_out_147), .col11(neo_1_out_146),
    .col12(neo_1_out_145), .col13(neo_1_out_144), .col14(neo_1_out_143), .col15(neo_1_out_142),
    .col16(neo_1_out_141), .col17(neo_1_out_140), .col18(neo_1_out_139), .col19(neo_1_out_138),
    .col20(neo_1_out_137), .col21(neo_1_out_136), .col22(neo_1_out_135), .col23(neo_1_out_134),
    .col24(neo_1_out_133), .col25(neo_1_out_132), .col26(neo_1_out_131), .col27(neo_1_out_130),
    .col28(neo_1_out_129), .col29(neo_1_out_128), .col30(neo_1_out_127), .col31(neo_1_out_126));
  neo neo_1 (
    .in_17(telos_1_out_4), .in_18(telos_1_out_5), .in_1(or_3_out), .in_2(or_4_out), .in_3(in_1),
    .in_19(telos_1_out_6), .in_20(telos_1_out_7), .in_21(telos_1_out_8), .in_22(telos_1_out_9),
    .in_23(telos_1_out_10), .in_24(telos_1_out_11), .in_25(telos_1_out_12), .in_26(telos_1_out_13),
    .in_27(telos_1_out_14), .in_28(telos_1_out_15), .in_29(telos_1_out_16), .in_4(telos_1_out_17),
    .in_5(telos_1_out_18), .in_6(telos_1_out_19), .in_7(telos_1_out_20), .in_8(telos_1_out_21),
    .in_9(telos_1_out_22), .in_10(telos_1_out_23), .in_11(telos_1_out_24), .in_12(telos_1_out_25),
    .in_13(telos_1_out_26), .in_14(telos_1_out_27), .in_15(telos_1_out_28), .in_16(telos_1_out_29),
    .out_94(neo_1_out_94), .out_95(neo_1_out_95), .out_96(neo_1_out_96), .out_97(neo_1_out_97),
    .out_98(neo_1_out_98), .out_99(neo_1_out_99), .out_100(neo_1_out_100), .out_101(neo_1_out_101),
    .out_102(neo_1_out_102), .out_103(neo_1_out_103), .out_104(neo_1_out_104), .out_105(neo_1_out_105),
    .out_106(neo_1_out_106), .out_107(neo_1_out_107), .out_108(neo_1_out_108), .out_109(neo_1_out_109),
    .out_110(neo_1_out_110), .out_111(neo_1_out_111), .out_112(neo_1_out_112), .out_113(neo_1_out_113),
    .out_114(neo_1_out_114), .out_115(neo_1_out_115), .out_116(neo_1_out_116), .out_117(neo_1_out_117),
    .out_118(neo_1_out_118), .out_119(neo_1_out_119), .out_120(neo_1_out_120), .out_121(neo_1_out_121),
    .out_122(neo_1_out_122), .out_123(neo_1_out_123), .out_124(neo_1_out_124), .out_125(neo_1_out_125),
    .out_126(neo_1_out_126), .out_127(neo_1_out_127), .out_128(neo_1_out_128), .out_129(neo_1_out_129),
    .out_130(neo_1_out_130), .out_131(neo_1_out_131), .out_132(neo_1_out_132), .out_133(neo_1_out_133),
    .out_134(neo_1_out_134), .out_135(neo_1_out_135), .out_136(neo_1_out_136), .out_137(neo_1_out_137),
    .out_138(neo_1_out_138), .out_139(neo_1_out_139), .out_140(neo_1_out_140), .out_141(neo_1_out_141),
    .out_142(neo_1_out_142), .out_143(neo_1_out_143), .out_144(neo_1_out_144), .out_145(neo_1_out_145),
    .out_146(neo_1_out_146), .out_147(neo_1_out_147), .out_148(neo_1_out_148), .out_149(neo_1_out_149),
    .out_150(neo_1_out_150), .out_151(neo_1_out_151), .out_152(neo_1_out_152), .out_153(neo_1_out_153),
    .out_154(neo_1_out_154), .out_155(neo_1_out_155), .out_156(neo_1_out_156), .out_157(neo_1_out_157));  // open: out_30, out_31, out_32, out_33, out_34, out_35, out_36, out_37, out_38, out_39, out_40, out_41, out_42, out_43, out_44, out_45, out_46, out_47, out_48, out_49, out_50, out_51, out_52, out_53, out_54, out_55, out_56, out_57, out_58, out_59, out_60, out_61, out_62, out_63, out_64, out_65, out_66, out_67, out_68, out_69, out_70, out_71, out_72, out_73, out_74, out_75, out_76, out_77, out_78, out_79, out_80, out_81, out_82, out_83, out_84, out_85, out_86, out_87, out_88, out_89, out_90, out_91, out_92, out_93
  or or_3 (or_3_out, _2, s2);
  or or_4 (or_4_out, s1, _1);
  DotMatrix #(.matrixcols(32), .matrixrows(32)) dotmatrix_2 (
    .col0(neo_1_out_125), .col1(neo_1_out_124), .col2(neo_1_out_123), .col3(neo_1_out_122),
    .col4(neo_1_out_121), .col5(neo_1_out_120), .col6(neo_1_out_119), .col7(neo_1_out_118),
    .col8(neo_1_out_117), .col9(neo_1_out_116), .col10(neo_1_out_115), .col11(neo_1_out_114),
    .col12(neo_1_out_113), .col13(neo_1_out_112), .col14(neo_1_out_111), .col15(neo_1_out_110),
    .col16(neo_1_out_109), .col17(neo_1_out_108), .col18(neo_1_out_107), .col19(neo_1_out_106),
    .col20(neo_1_out_105), .col21(neo_1_out_104), .col22(neo_1_out_103), .col23(neo_1_out_102),
    .col24(neo_1_out_101), .col25(neo_1_out_100), .col26(neo_1_out_99), .col27(neo_1_out_98),
    .col28(neo_1_out_97), .col29(neo_1_out_96), .col30(neo_1_out_95), .col31(neo_1_out_94));
  neo neo_2 (
    .in_17(telos_2_out_4), .in_18(telos_2_out_5), .in_1(or_5_out), .in_2(or_6_out), .in_3(in_1),
    .in_19(telos_2_out_6), .in_20(telos_2_out_7), .in_21(telos_2_out_8), .in_22(telos_2_out_9),
    .in_23(telos_2_out_10), .in_24(telos_2_out_11), .in_25(telos_2_out_12), .in_26(telos_2_out_13),
    .in_27(telos_2_out_14), .in_28(telos_2_out_15), .in_29(telos_2_out_16), .in_4(telos_2_out_17),
    .in_5(telos_2_out_18), .in_6(telos_2_out_19), .in_7(telos_2_out_20), .in_8(telos_2_out_21),
    .in_9(telos_2_out_22), .in_10(telos_2_out_23), .in_11(telos_2_out_24), .in_12(telos_2_out_25),
    .in_13(telos_2_out_26), .in_14(telos_2_out_27), .in_15(telos_2_out_28), .in_16(telos_2_out_29),
    .out_98(neo_2_out_98), .out_99(neo_2_out_99), .out_100(neo_2_out_100), .out_101(neo_2_out_101),
    .out_102(neo_2_out_102), .out_103(neo_2_out_103), .out_104(neo_2_out_104), .out_105(neo_2_out_105),
    .out_106(neo_2_out_106), .out_107(neo_2_out_107), .out_108(neo_2_out_108), .out_109(neo_2_out_109),
    .out_110(neo_2_out_110), .out_111(neo_2_out_111), .out_112(neo_2_out_112), .out_113(neo_2_out_113),
    .out_114(neo_2_out_114), .out_115(neo_2_out_115), .out_116(neo_2_out_116), .out_117(neo_2_out_117),
    .out_118(neo_2_out_118), .out_119(neo_2_out_119), .out_120(neo_2_out_120), .out_121(neo_2_out_121),
    .out_122(neo_2_out_122), .out_123(neo_2_out_123), .out_124(neo_2_out_124), .out_125(neo_2_out_125),
    .out_126(neo_2_out_126), .out_127(neo_2_out_127), .out_128(neo_2_out_128), .out_129(neo_2_out_129),
    .out_130(neo_2_out_130), .out_131(neo_2_out_131), .out_132(neo_2_out_132), .out_133(neo_2_out_133),
    .out_134(neo_2_out_134), .out_135(neo_2_out_135), .out_136(neo_2_out_136), .out_137(neo_2_out_137),
    .out_138(neo_2_out_138), .out_139(neo_2_out_139), .out_140(neo_2_out_140), .out_141(neo_2_out_141),
    .out_142(neo_2_out_142), .out_143(neo_2_out_143), .out_144(neo_2_out_144), .out_145(neo_2_out_145),
    .out_146(neo_2_out_146));  // open: out_94, out_95, out_96, out_97, out_147, out_148, out_149, out_150, out_151, out_152, out_153, out_154, out_155, out_156, out_157, out_30, out_31, out_32, out_33, out_34, out_35, out_36, out_37, out_38, out_39, out_40, out_41, out_42, out_43, out_44, out_45, out_46, out_47, out_48, out_49, out_50, out_51, out_52, out_53, out_54, out_55, out_56, out_57, out_58, out_59, out_60, out_61, out_62, out_63, out_64, out_65, out_66, out_67, out_68, out_69, out_70, out_71, out_72, out_73, out_74, out_75, out_76, out_77, out_78, out_79, out_80, out_81, out_82, out_83, out_84, out_85, out_86, out_87, out_88, out_89, out_90, out_91, out_92, out_93
  telos telos_2 (
    .in_1(plus_or_minus), .in_3(in_1), .in_2(klok), .out_4(telos_2_out_4), .out_5(telos_2_out_5),
    .out_6(telos_2_out_6), .out_7(telos_2_out_7), .out_8(telos_2_out_8), .out_9(telos_2_out_9),
    .out_10(telos_2_out_10), .out_11(telos_2_out_11), .out_12(telos_2_out_12), .out_13(telos_2_out_13),
    .out_14(telos_2_out_14), .out_15(telos_2_out_15), .out_16(telos_2_out_16), .out_17(telos_2_out_17),
    .out_18(telos_2_out_18), .out_19(telos_2_out_19), .out_20(telos_2_out_20), .out_21(telos_2_out_21),
    .out_22(telos_2_out_22), .out_23(telos_2_out_23), .out_24(telos_2_out_24), .out_25(telos_2_out_25),
    .out_26(telos_2_out_26), .out_27(telos_2_out_27), .out_28(telos_2_out_28), .out_29(telos_2_out_29));
  or or_5 (or_5_out, _2, s2);
  or or_6 (or_6_out, s1, _1);

  // Other names for the same wires on the sheet: res = in_1
endmodule
