// Logisim project βολη.circ as structural Verilog: 1 circuit, main circuit main
module main (
  input  in_1
);

  wire klok, plus_or_minus, s1, s2;
  wire [1:0] joystick_1_x, joystick_1_y;
  wire [31:0] neo_1_out_30, neo_1_out_31, neo_1_out_32, neo_1_out_33, neo_1_out_34, neo_1_out_35,
       neo_1_out_36, neo_1_out_37, neo_1_out_38, neo_1_out_39, neo_1_out_40, neo_1_out_41, neo_1_out_42,
       neo_1_out_43, neo_1_out_44, neo_1_out_45, neo_1_out_46, neo_1_out_47, neo_1_out_48, neo_1_out_49,
       neo_1_out_50, neo_1_out_51, neo_1_out_52, neo_1_out_53, neo_1_out_54, neo_1_out_55, neo_1_out_56,
       neo_1_out_57, neo_1_out_58, neo_1_out_59, neo_1_out_60, neo_1_out_61, neo_1_out_62, neo_1_out_63,
       neo_1_out_64, neo_1_out_65, neo_1_out_66, neo_1_out_67, neo_1_out_68, neo_1_out_69, neo_1_out_70,
       neo_1_out_71, neo_1_out_72, neo_1_out_73, neo_1_out_74, neo_1_out_75, neo_1_out_76, neo_1_out_77,
       neo_1_out_78, neo_1_out_79, neo_1_out_80, neo_1_out_81, neo_1_out_82, neo_1_out_83, neo_1_out_84,
       neo_1_out_85, neo_1_out_86, neo_1_out_87, neo_1_out_88, neo_1_out_89, neo_1_out_90, neo_1_out_91,
       neo_1_out_92, neo_1_out_93, neo_1_out_94, neo_1_out_95, neo_1_out_96, neo_1_out_97, neo_1_out_98,
       neo_1_out_99, neo_1_out_100, neo_1_out_101, neo_1_out_102, neo_1_out_103, neo_1_out_104,
       neo_1_out_105, neo_1_out_106, neo_1_out_107, neo_1_out_108, neo_1_out_109, neo_1_out_110,
       neo_1_out_111, neo_1_out_112, neo_1_out_113, neo_1_out_114, neo_1_out_115, neo_1_out_116,
       neo_1_out_117, neo_1_out_118, neo_1_out_119, neo_1_out_120, neo_1_out_121, neo_1_out_122,
       neo_1_out_123, neo_1_out_124, neo_1_out_125, neo_1_out_126, neo_1_out_127, neo_1_out_128,
       neo_1_out_129, neo_1_out_130, neo_1_out_131, neo_1_out_132, neo_1_out_133, neo_1_out_134,
       neo_1_out_135, neo_1_out_136, neo_1_out_137, neo_1_out_138, neo_1_out_139, neo_1_out_140,
       neo_1_out_141, neo_1_out_142, neo_1_out_143, neo_1_out_144, neo_1_out_145, neo_1_out_146,
       neo_1_out_147, neo_1_out_148, neo_1_out_149, neo_1_out_150, neo_1_out_151, neo_1_out_152,
       neo_1_out_153, neo_1_out_154, neo_1_out_155, neo_1_out_156, neo_1_out_157, telos_1_out_4,
       telos_1_out_5, telos_1_out_6, telos_1_out_7, telos_1_out_8, telos_1_out_9, telos_1_out_10,
       telos_1_out_11, telos_1_out_12, telos_1_out_13, telos_1_out_14, telos_1_out_15, telos_1_out_16,
       telos_1_out_17, telos_1_out_18, telos_1_out_19, telos_1_out_20, telos_1_out_21, telos_1_out_22,
       telos_1_out_23, telos_1_out_24, telos_1_out_25, telos_1_out_26, telos_1_out_27, telos_1_out_28,
       telos_1_out_29;

  DotMatrix #(.matrixcols(32), .matrixrows(32)) dotmatrix_1 (
    .col0(neo_1_out_93), .col1(neo_1_out_92), .col2(neo_1_out_91), .col3(neo_1_out_90), .col4(neo_1_out_89),
    .col5(neo_1_out_88), .col6(neo_1_out_87), .col7(neo_1_out_86), .col8(neo_1_out_85), .col9(neo_1_out_84),
    .col10(neo_1_out_83), .col11(neo_1_out_82), .col12(neo_1_out_81), .col13(neo_1_out_80),
    .col14(neo_1_out_79), .col15(neo_1_out_78), .col16(neo_1_out_77), .col17(neo_1_out_76),
    .col18(neo_1_out_75), .col19(neo_1_out_74), .col20(neo_1_out_73), .col21(neo_1_out_72),
    .col22(neo_1_out_71), .col23(neo_1_out_70), .col24(neo_1_out_69), .col25(neo_1_out_68),
    .col26(neo_1_out_67), .col27(neo_1_out_66), .col28(neo_1_out_65), .col29(neo_1_out_64),
    .col30(neo_1_out_63), .col31(neo_1_out_62));
  DotMatrix #(.matrixcols(32), .matrixrows(32)) dotmatrix_2 (
    .col0(neo_1_out_157), .col1(neo_1_out_156), .col2(neo_1_out_155), .col3(neo_1_out_154),
    .col4(neo_1_out_153), .col5(neo_1_out_152), .col6(neo_1_out_151), .col7(neo_1_out_150),
    .col8(neo_1_out_149), .col9(neo_1_out_148), .col10(neo_1_out_147), .col11(neo_1_out_146),
    .col12(neo_1_out_145), .col13(neo_1_out_144), .col14(neo_1_out_143), .col15(neo_1_out_142),
    .col16(neo_1_out_141), .col17(neo_1_out_140), .col18(neo_1_out_139), .col19(neo_1_out_138),
    .col20(neo_1_out_137), .col21(neo_1_out_136), .col22(neo_1_out_135), .col23(neo_1_out_134),
    .col24(neo_1_out_133), .col25(neo_1_out_132), .col26(neo_1_out_131), .col27(neo_1_out_130),
    .col28(neo_1_out_129), .col29(neo_1_out_128), .col30(neo_1_out_127), .col31(neo_1_out_126));
  telos telos_1 (
    .in_1(plus_or_minus), .in_3(in_1), .in_2(klok), .out_4(telos_1_out_4), .out_5(telos_1_out_5),
    .out_6(telos_1_out_6), .out_7(telos_1_out_7), .out_8(telos_1_out_8), .out_9(telos_1_out_9),
    .out_10(telos_1_out_10), .out_11(telos_1_out_11), .out_12(telos_1_out_12), .out_13(telos_1_out_13),
    .out_14(telos_1_out_14), .out_15(telos_1_out_15), .out_16(telos_1_out_16), .out_17(telos_1_out_17),
    .out_18(telos_1_out_18), .out_19(telos_1_out_19), .out_20(telos_1_out_20), .out_21(telos_1_out_21),
    .out_22(telos_1_out_22), .out_23(telos_1_out_23), .out_24(telos_1_out_24), .out_25(telos_1_out_25),
    .out_26(telos_1_out_26), .out_27(telos_1_out_27), .out_28(telos_1_out_28), .out_29(telos_1_out_29));
  neo neo_1 (
    .in_17(telos_1_out_4), .in_18(telos_1_out_5), .in_1(s2), .in_2(s1), .in_3(in_1), .in_19(telos_1_out_6),
    .in_20(telos_1_out_7), .in_21(telos_1_out_8), .in_22(telos_1_out_9), .in_23(telos_1_out_10),
    .in_24(telos_1_out_11), .in_25(telos_1_out_12), .in_26(telos_1_out_13), .in_27(telos_1_out_14),
    .in_28(telos_1_out_15), .in_29(telos_1_out_16), .in_4(telos_1_out_17), .in_5(telos_1_out_18),
    .in_6(telos_1_out_19), .in_7(telos_1_out_20), .in_8(telos_1_out_21), .in_9(telos_1_out_22),
    .in_10(telos_1_out_23), .in_11(telos_1_out_24), .in_12(telos_1_out_25), .in_13(telos_1_out_26),
    .in_14(telos_1_out_27), .in_15(telos_1_out_28), .in_16(telos_1_out_29), .out_94(neo_1_out_94),
    .out_95(neo_1_out_95), .out_96(neo_1_out_96), .out_97(neo_1_out_97), .out_98(neo_1_out_98),
    .out_99(neo_1_out_99), .out_100(neo_1_out_100), .out_101(neo_1_out_101), .out_102(neo_1_out_102),
    .out_103(neo_1_out_103), .out_104(neo_1_out_104), .out_105(neo_1_out_105), .out_106(neo_1_out_106),
    .out_107(neo_1_out_107), .out_108(neo_1_out_108), .out_109(neo_1_out_109), .out_110(neo_1_out_110),
    .out_111(neo_1_out_111), .out_112(neo_1_out_112), .out_113(neo_1_out_113), .out_114(neo_1_out_114),
    .out_115(neo_1_out_115), .out_116(neo_1_out_116), .out_117(neo_1_out_117), .out_118(neo_1_out_118),
    .out_119(neo_1_out_119), .out_120(neo_1_out_120), .out_121(neo_1_out_121), .out_122(neo_1_out_122),
    .out_123(neo_1_out_123), .out_124(neo_1_out_124), .out_125(neo_1_out_125), .out_126(neo_1_out_126),
    .out_127(neo_1_out_127), .out_128(neo_1_out_128), .out_129(neo_1_out_129), .out_130(neo_1_out_130),
    .out_131(neo_1_out_131), .out_132(neo_1_out_132), .out_133(neo_1_out_133), .out_134(neo_1_out_134),
    .out_135(neo_1_out_135), .out_136(neo_1_out_136), .out_137(neo_1_out_137), .out_138(neo_1_out_138),
    .out_139(neo_1_out_139), .out_140(neo_1_out_140), .out_141(neo_1_out_141), .out_142(neo_1_out_142),
    .out_143(neo_1_out_143), .out_144(neo_1_out_144), .out_145(neo_1_out_145), .out_146(neo_1_out_146),
    .out_147(neo_1_out_147), .out_148(neo_1_out_148), .out_149(neo_1_out_149), .out_150(neo_1_out_150),
    .out_151(neo_1_out_151), .out_152(neo_1_out_152), .out_153(neo_1_out_153), .out_154(neo_1_out_154),
    .out_155(neo_1_out_155), .out_156(neo_1_out_156), .out_157(neo_1_out_157), .out_30(neo_1_out_30),
    .out_31(neo_1_out_31), .out_32(neo_1_out_32), .out_33(neo_1_out_33), .out_34(neo_1_out_34),
    .out_35(neo_1_out_35), .out_36(neo_1_out_36), .out_37(neo_1_out_37), .out_38(neo_1_out_38),
    .out_39(neo_1_out_39), .out_40(neo_1_out_40), .out_41(neo_1_out_41), .out_42(neo_1_out_42),
    .out_43(neo_1_out_43), .out_44(neo_1_out_44), .out_45(neo_1_out_45), .out_46(neo_1_out_46),
    .out_47(neo_1_out_47), .out_48(neo_1_out_48), .out_49(neo_1_out_49), .out_50(neo_1_out_50),
    .out_51(neo_1_out_51), .out_52(neo_1_out_52), .out_53(neo_1_out_53), .out_54(neo_1_out_54),
    .out_55(neo_1_out_55), .out_56(neo_1_out_56), .out_57(neo_1_out_57), .out_58(neo_1_out_58),
    .out_59(neo_1_out_59), .out_60(neo_1_out_60), .out_61(neo_1_out_61), .out_62(neo_1_out_62),
    .out_63(neo_1_out_63), .out_64(neo_1_out_64), .out_65(neo_1_out_65), .out_66(neo_1_out_66),
    .out_67(neo_1_out_67), .out_68(neo_1_out_68), .out_69(neo_1_out_69), .out_70(neo_1_out_70),
    .out_71(neo_1_out_71), .out_72(neo_1_out_72), .out_73(neo_1_out_73), .out_74(neo_1_out_74),
    .out_75(neo_1_out_75), .out_76(neo_1_out_76), .out_77(neo_1_out_77), .out_78(neo_1_out_78),
    .out_79(neo_1_out_79), .out_80(neo_1_out_80), .out_81(neo_1_out_81), .out_82(neo_1_out_82),
    .out_83(neo_1_out_83), .out_84(neo_1_out_84), .out_85(neo_1_out_85), .out_86(neo_1_out_86),
    .out_87(neo_1_out_87), .out_88(neo_1_out_88), .out_89(neo_1_out_89), .out_90(neo_1_out_90),
    .out_91(neo_1_out_91), .out_92(neo_1_out_92), .out_93(neo_1_out_93));
  DotMatrix #(.matrixcols(32), .matrixrows(32)) dotmatrix_3 (
    .col0(neo_1_out_61), .col1(neo_1_out_60), .col2(neo_1_out_59), .col3(neo_1_out_58), .col4(neo_1_out_57),
    .col5(neo_1_out_56), .col6(neo_1_out_55), .col7(neo_1_out_54), .col8(neo_1_out_53), .col9(neo_1_out_52),
    .col10(neo_1_out_51), .col11(neo_1_out_50), .col12(neo_1_out_49), .col13(neo_1_out_48),
    .col14(neo_1_out_47), .col15(neo_1_out_46), .col16(neo_1_out_45), .col17(neo_1_out_44),
    .col18(neo_1_out_43), .col19(neo_1_out_42), .col20(neo_1_out_41), .col21(neo_1_out_40),
    .col22(neo_1_out_39), .col23(neo_1_out_38), .col24(neo_1_out_37), .col25(neo_1_out_36),
    .col26(neo_1_out_35), .col27(neo_1_out_34), .col28(neo_1_out_33), .col29(neo_1_out_32),
    .col30(neo_1_out_31), .col31(neo_1_out_30));
  DotMatrix #(.matrixcols(32), .matrixrows(32)) dotmatrix_4 (
    .col0(neo_1_out_125), .col1(neo_1_out_124), .col2(neo_1_out_123), .col3(neo_1_out_122),
    .col4(neo_1_out_121), .col5(neo_1_out_120), .col6(neo_1_out_119), .col7(neo_1_out_118),
    .col8(neo_1_out_117), .col9(neo_1_out_116), .col10(neo_1_out_115), .col11(neo_1_out_114),
    .col12(neo_1_out_113), .col13(neo_1_out_112), .col14(neo_1_out_111), .col15(neo_1_out_110),
    .col16(neo_1_out_109), .col17(neo_1_out_108), .col18(neo_1_out_107), .col19(neo_1_out_106),
    .col20(neo_1_out_105), .col21(neo_1_out_104), .col22(neo_1_out_103), .col23(neo_1_out_102),
    .col24(neo_1_out_101), .col25(neo_1_out_100), .col26(neo_1_out_99), .col27(neo_1_out_98),
    .col28(neo_1_out_97), .col29(neo_1_out_96), .col30(neo_1_out_95), .col31(neo_1_out_94));
  mox mox_1 (.out_3(s1), .out_4(s2), .in_1(joystick_1_x), .in_2(joystick_1_y), .out_5(plus_or_minus), .out_6(klok));
  Joystick #(.bits(2)) joystick_1 (.x(joystick_1_x), .y(joystick_1_y));

  // Other names for the same wires on the sheet: res = in_1; s3 = klok; s4 = plus_or_minus
endmodule
