// Logisim project κηνηση πανο κατο.circ as structural Verilog: 15 circuits, main circuit ε
module \ε  (
  input  in_1,
  input  in_2,
  input  in_3,
  output [7:0] out_4,
  output [31:0] out_5,
  output [31:0] out_6,
  output [31:0] out_7,
  output [31:0] out_8,
  output [31:0] out_9,
  output [31:0] out_10,
  output [31:0] out_11,
  output [31:0] out_12,
  output [31:0] out_13,
  output [31:0] out_14,
  output [31:0] out_15,
  output [31:0] out_16,
  output [31:0] out_17
);

  wire and_1_out, comparator_1_lt, comparator_2_lt, not_1_out, or_1_out;
  wire [4:0] bit_extender_1_out;
  wire [31:0] multiplexer_1_out, multiplexer_2_out, multiplexer_3_out, multiplexer_4_out, multiplexer_5_out,
       multiplexer_6_out, multiplexer_7_out, multiplexer_8_out, multiplexer_9_out, multiplexer_10_out,
       multiplexer_11_out, multiplexer_12_out, multiplexer_13_out, \σοσ_1_out_2 , \σοσ_1_out_3 ,
       \σοσ_1_out_4 , \σοσ_1_out_5 , \σοσ_1_out_6 , \σοσ_1_out_7 , \σοσ_1_out_8 , \σοσ_1_out_9 ,
       \σοσ_1_out_10 , \σοσ_1_out_11 , \σοσ_1_out_12 , \σοσ_1_out_13 , \σοσ_1_out_14 , \σοσ_1_out_15 ,
       \σοσ_1_out_16 , \σοσ_1_out_17 , \σοσ_1_out_18 , \σοσ_1_out_19 , \σοσ_1_out_20 , \σοσ_1_out_21 ,
       \σοσ_1_out_22 , \σοσ_1_out_23 , \σοσ_1_out_24 , \σοσ_1_out_25 , \σοσ_1_out_26 , \σοσ_1_out_27 ,
       \σοσ_1_out_28 , \σοσ_1_out_29 , \σοσ_1_out_30 , \σοσ_1_out_31 , \σοσ_1_out_32 , \σοσ_1_out_33 ,
       \σοσ_2_out_2 , \σοσ_2_out_3 , \σοσ_2_out_4 , \σοσ_2_out_5 , \σοσ_2_out_6 , \σοσ_2_out_7 ,
       \σοσ_2_out_8 , \σοσ_2_out_9 , \σοσ_2_out_10 , \σοσ_2_out_11 , \σοσ_2_out_12 , \σοσ_2_out_13 ,
       \σοσ_2_out_14 , \σοσ_2_out_15 , \σοσ_2_out_16 , \σοσ_2_out_17 , \σοσ_2_out_18 , \σοσ_2_out_19 ,
       \σοσ_2_out_20 , \σοσ_2_out_21 , \σοσ_2_out_22 , \σοσ_2_out_23 , \σοσ_2_out_24 , \σοσ_2_out_25 ,
       \σοσ_2_out_26 , \σοσ_2_out_27 , \σοσ_2_out_28 , \σοσ_2_out_29 , \σοσ_2_out_30 , \σοσ_2_out_31 ,
       \σοσ_2_out_32 , \σοσ_2_out_33 , \σοσ_3_out_2 , \σοσ_3_out_3 , \σοσ_3_out_4 , \σοσ_3_out_5 ,
       \σοσ_3_out_6 , \σοσ_3_out_7 , \σοσ_3_out_8 , \σοσ_3_out_9 , \σοσ_3_out_10 , \σοσ_3_out_11 ,
       \σοσ_3_out_12 , \σοσ_3_out_13 , \σοσ_3_out_14 , \σοσ_3_out_15 , \σοσ_3_out_16 , \σοσ_3_out_17 ,
       \σοσ_3_out_18 , \σοσ_3_out_19 , \σοσ_3_out_20 , \σοσ_3_out_21 , \σοσ_3_out_22 , \σοσ_3_out_23 ,
       \σοσ_3_out_24 , \σοσ_3_out_25 , \σοσ_3_out_26 , \σοσ_3_out_27 , \σοσ_3_out_28 , \σοσ_3_out_29 ,
       \σοσ_3_out_30 , \σοσ_3_out_31 , \σοσ_3_out_32 , \σοσ_3_out_33 , \σοσ_4_out_2 , \σοσ_4_out_3 ,
       \σοσ_4_out_4 , \σοσ_4_out_5 , \σοσ_4_out_6 , \σοσ_4_out_7 , \σοσ_4_out_8 , \σοσ_4_out_9 ,
       \σοσ_4_out_10 , \σοσ_4_out_11 , \σοσ_4_out_12 , \σοσ_4_out_13 , \σοσ_4_out_14 , \σοσ_4_out_15 ,
       \σοσ_4_out_16 , \σοσ_4_out_17 , \σοσ_4_out_18 , \σοσ_4_out_19 , \σοσ_4_out_20 , \σοσ_4_out_21 ,
       \σοσ_4_out_22 , \σοσ_4_out_23 , \σοσ_4_out_24 , \σοσ_4_out_25 , \σοσ_4_out_26 , \σοσ_4_out_27 ,
       \σοσ_4_out_28 , \σοσ_4_out_29 , \σοσ_4_out_30 , \σοσ_4_out_31 , \σοσ_4_out_32 , \σοσ_4_out_33 ,
       \σοσ_5_out_2 , \σοσ_5_out_3 , \σοσ_5_out_4 , \σοσ_5_out_5 , \σοσ_5_out_6 , \σοσ_5_out_7 ,
       \σοσ_5_out_8 , \σοσ_5_out_9 , \σοσ_5_out_10 , \σοσ_5_out_11 , \σοσ_5_out_12 , \σοσ_5_out_13 ,
       \σοσ_5_out_14 , \σοσ_5_out_15 , \σοσ_5_out_16 , \σοσ_5_out_17 , \σοσ_5_out_18 , \σοσ_5_out_19 ,
       \σοσ_5_out_20 , \σοσ_5_out_21 , \σοσ_5_out_22 , \σοσ_5_out_23 , \σοσ_5_out_24 , \σοσ_5_out_25 ,
       \σοσ_5_out_26 , \σοσ_5_out_27 , \σοσ_5_out_28 , \σοσ_5_out_29 , \σοσ_5_out_30 , \σοσ_5_out_31 ,
       \σοσ_5_out_32 , \σοσ_5_out_33 , \σοσ_6_out_2 , \σοσ_6_out_3 , \σοσ_6_out_4 , \σοσ_6_out_5 ,
       \σοσ_6_out_6 , \σοσ_6_out_7 , \σοσ_6_out_8 , \σοσ_6_out_9 , \σοσ_6_out_10 , \σοσ_6_out_11 ,
       \σοσ_6_out_12 , \σοσ_6_out_13 , \σοσ_6_out_14 , \σοσ_6_out_15 , \σοσ_6_out_16 , \σοσ_6_out_17 ,
       \σοσ_6_out_18 , \σοσ_6_out_19 , \σοσ_6_out_20 , \σοσ_6_out_21 , \σοσ_6_out_22 , \σοσ_6_out_23 ,
       \σοσ_6_out_24 , \σοσ_6_out_25 , \σοσ_6_out_26 , \σοσ_6_out_27 , \σοσ_6_out_28 , \σοσ_6_out_29 ,
       \σοσ_6_out_30 , \σοσ_6_out_31 , \σοσ_6_out_32 , \σοσ_6_out_33 , \σοσ_7_out_2 , \σοσ_7_out_3 ,
       \σοσ_7_out_4 , \σοσ_7_out_5 , \σοσ_7_out_6 , \σοσ_7_out_7 , \σοσ_7_out_8 , \σοσ_7_out_9 ,
       \σοσ_7_out_10 , \σοσ_7_out_11 , \σοσ_7_out_12 , \σοσ_7_out_13 , \σοσ_7_out_14 , \σοσ_7_out_15 ,
       \σοσ_7_out_16 , \σοσ_7_out_17 , \σοσ_7_out_18 , \σοσ_7_out_19 , \σοσ_7_out_20 , \σοσ_7_out_21 ,
       \σοσ_7_out_22 , \σοσ_7_out_23 , \σοσ_7_out_24 , \σοσ_7_out_25 , \σοσ_7_out_26 , \σοσ_7_out_27 ,
       \σοσ_7_out_28 , \σοσ_7_out_29 , \σοσ_7_out_30 , \σοσ_7_out_31 , \σοσ_7_out_32 , \σοσ_7_out_33 ,
       \σοσ_8_out_2 , \σοσ_8_out_3 , \σοσ_8_out_4 , \σοσ_8_out_5 , \σοσ_8_out_6 , \σοσ_8_out_7 ,
       \σοσ_8_out_8 , \σοσ_8_out_9 , \σοσ_8_out_10 , \σοσ_8_out_11 , \σοσ_8_out_12 , \σοσ_8_out_13 ,
       \σοσ_8_out_14 , \σοσ_8_out_15 , \σοσ_8_out_16 , \σοσ_8_out_17 , \σοσ_8_out_18 , \σοσ_8_out_19 ,
       \σοσ_8_out_20 , \σοσ_8_out_21 , \σοσ_8_out_22 , \σοσ_8_out_23 , \σοσ_8_out_24 , \σοσ_8_out_25 ,
       \σοσ_8_out_26 , \σοσ_8_out_27 , \σοσ_8_out_28 , \σοσ_8_out_29 , \σοσ_8_out_30 , \σοσ_8_out_31 ,
       \σοσ_8_out_32 , \σοσ_8_out_33 , \σοσ_9_out_2 , \σοσ_9_out_3 , \σοσ_9_out_4 , \σοσ_9_out_5 ,
       \σοσ_9_out_6 , \σοσ_9_out_7 , \σοσ_9_out_8 , \σοσ_9_out_9 , \σοσ_9_out_10 , \σοσ_9_out_11 ,
       \σοσ_9_out_12 , \σοσ_9_out_13 , \σοσ_9_out_14 , \σοσ_9_out_15 , \σοσ_9_out_16 , \σοσ_9_out_17 ,
       \σοσ_9_out_18 , \σοσ_9_out_19 , \σοσ_9_out_20 , \σοσ_9_out_21 , \σοσ_9_out_22 , \σοσ_9_out_23 ,
       \σοσ_9_out_24 , \σοσ_9_out_25 , \σοσ_9_out_26 , \σοσ_9_out_27 , \σοσ_9_out_28 , \σοσ_9_out_29 ,
       \σοσ_9_out_30 , \σοσ_9_out_31 , \σοσ_9_out_32 , \σοσ_9_out_33 , \σοσ_10_out_2 , \σοσ_10_out_3 ,
       \σοσ_10_out_4 , \σοσ_10_out_5 , \σοσ_10_out_6 , \σοσ_10_out_7 , \σοσ_10_out_8 , \σοσ_10_out_9 ,
       \σοσ_10_out_10 , \σοσ_10_out_11 , \σοσ_10_out_12 , \σοσ_10_out_13 , \σοσ_10_out_14 , \σοσ_10_out_15 ,
       \σοσ_10_out_16 , \σοσ_10_out_17 , \σοσ_10_out_18 , \σοσ_10_out_19 , \σοσ_10_out_20 , \σοσ_10_out_21 ,
       \σοσ_10_out_22 , \σοσ_10_out_23 , \σοσ_10_out_24 , \σοσ_10_out_25 , \σοσ_10_out_26 , \σοσ_10_out_27 ,
       \σοσ_10_out_28 , \σοσ_10_out_29 , \σοσ_10_out_30 , \σοσ_10_out_31 , \σοσ_10_out_32 , \σοσ_10_out_33 ,
       \σοσ_11_out_2 , \σοσ_11_out_3 , \σοσ_11_out_4 , \σοσ_11_out_5 , \σοσ_11_out_6 , \σοσ_11_out_7 ,
       \σοσ_11_out_8 , \σοσ_11_out_9 , \σοσ_11_out_10 , \σοσ_11_out_11 , \σοσ_11_out_12 , \σοσ_11_out_13 ,
       \σοσ_11_out_14 , \σοσ_11_out_15 , \σοσ_11_out_16 , \σοσ_11_out_17 , \σοσ_11_out_18 , \σοσ_11_out_19 ,
       \σοσ_11_out_20 , \σοσ_11_out_21 , \σοσ_11_out_22 , \σοσ_11_out_23 , \σοσ_11_out_24 , \σοσ_11_out_25 ,
       \σοσ_11_out_26 , \σοσ_11_out_27 , \σοσ_11_out_28 , \σοσ_11_out_29 , \σοσ_11_out_30 , \σοσ_11_out_31 ,
       \σοσ_11_out_32 , \σοσ_11_out_33 , \σοσ_12_out_2 , \σοσ_12_out_3 , \σοσ_12_out_4 , \σοσ_12_out_5 ,
       \σοσ_12_out_6 , \σοσ_12_out_7 , \σοσ_12_out_8 , \σοσ_12_out_9 , \σοσ_12_out_10 , \σοσ_12_out_11 ,
       \σοσ_12_out_12 , \σοσ_12_out_13 , \σοσ_12_out_14 , \σοσ_12_out_15 , \σοσ_12_out_16 , \σοσ_12_out_17 ,
       \σοσ_12_out_18 , \σοσ_12_out_19 , \σοσ_12_out_20 , \σοσ_12_out_21 , \σοσ_12_out_22 , \σοσ_12_out_23 ,
       \σοσ_12_out_24 , \σοσ_12_out_25 , \σοσ_12_out_26 , \σοσ_12_out_27 , \σοσ_12_out_28 , \σοσ_12_out_29 ,
       \σοσ_12_out_30 , \σοσ_12_out_31 , \σοσ_12_out_32 , \σοσ_12_out_33 , \σοσ_13_out_2 , \σοσ_13_out_3 ,
       \σοσ_13_out_4 , \σοσ_13_out_5 , \σοσ_13_out_6 , \σοσ_13_out_7 , \σοσ_13_out_8 , \σοσ_13_out_9 ,
       \σοσ_13_out_10 , \σοσ_13_out_11 , \σοσ_13_out_12 , \σοσ_13_out_13 , \σοσ_13_out_14 , \σοσ_13_out_15 ,
       \σοσ_13_out_16 , \σοσ_13_out_17 , \σοσ_13_out_18 , \σοσ_13_out_19 , \σοσ_13_out_20 , \σοσ_13_out_21 ,
       \σοσ_13_out_22 , \σοσ_13_out_23 , \σοσ_13_out_24 , \σοσ_13_out_25 , \σοσ_13_out_26 , \σοσ_13_out_27 ,
       \σοσ_13_out_28 , \σοσ_13_out_29 , \σοσ_13_out_30 , \σοσ_13_out_31 , \σοσ_13_out_32 , \σοσ_13_out_33 ;

  or or_1 (or_1_out, in_1, comparator_1_lt);
  and and_1 (and_1_out, or_1_out, in_2);
  Comparator comparator_1 (.a(out_4), .b(8'h40), .lt(comparator_1_lt));  // open: gt, eq
  Comparator comparator_2 (.a(out_4), .b(8'h20), .lt(comparator_2_lt));  // open: gt, eq
  Counter counter_1 (.load(in_1), .Q(out_4), .clk(and_1_out), .clr(in_3));  // open: D, count, carry
  Bit_Extender #(.out_width(5)) bit_extender_1 (.in(out_4), .out(bit_extender_1_out));
  \σοσ  \u_σοσ_1  (
    .in_1(32'h1f), .out_2(\σοσ_1_out_2 ), .out_3(\σοσ_1_out_3 ), .out_4(\σοσ_1_out_4 ),
    .out_5(\σοσ_1_out_5 ), .out_6(\σοσ_1_out_6 ), .out_7(\σοσ_1_out_7 ), .out_8(\σοσ_1_out_8 ),
    .out_9(\σοσ_1_out_9 ), .out_10(\σοσ_1_out_10 ), .out_11(\σοσ_1_out_11 ), .out_12(\σοσ_1_out_12 ),
    .out_13(\σοσ_1_out_13 ), .out_14(\σοσ_1_out_14 ), .out_15(\σοσ_1_out_15 ), .out_16(\σοσ_1_out_16 ),
    .out_17(\σοσ_1_out_17 ), .out_18(\σοσ_1_out_18 ), .out_19(\σοσ_1_out_19 ), .out_20(\σοσ_1_out_20 ),
    .out_21(\σοσ_1_out_21 ), .out_22(\σοσ_1_out_22 ), .out_23(\σοσ_1_out_23 ), .out_24(\σοσ_1_out_24 ),
    .out_25(\σοσ_1_out_25 ), .out_26(\σοσ_1_out_26 ), .out_27(\σοσ_1_out_27 ), .out_28(\σοσ_1_out_28 ),
    .out_29(\σοσ_1_out_29 ), .out_30(\σοσ_1_out_30 ), .out_31(\σοσ_1_out_31 ), .out_32(\σοσ_1_out_32 ),
    .out_33(\σοσ_1_out_33 ));
  \σοσ  \u_σοσ_2  (
    .in_1(32'h1f1), .out_2(\σοσ_2_out_2 ), .out_3(\σοσ_2_out_3 ), .out_4(\σοσ_2_out_4 ),
    .out_5(\σοσ_2_out_5 ), .out_6(\σοσ_2_out_6 ), .out_7(\σοσ_2_out_7 ), .out_8(\σοσ_2_out_8 ),
    .out_9(\σοσ_2_out_9 ), .out_10(\σοσ_2_out_10 ), .out_11(\σοσ_2_out_11 ), .out_12(\σοσ_2_out_12 ),
    .out_13(\σοσ_2_out_13 ), .out_14(\σοσ_2_out_14 ), .out_15(\σοσ_2_out_15 ), .out_16(\σοσ_2_out_16 ),
    .out_17(\σοσ_2_out_17 ), .out_18(\σοσ_2_out_18 ), .out_19(\σοσ_2_out_19 ), .out_20(\σοσ_2_out_20 ),
    .out_21(\σοσ_2_out_21 ), .out_22(\σοσ_2_out_22 ), .out_23(\σοσ_2_out_23 ), .out_24(\σοσ_2_out_24 ),
    .out_25(\σοσ_2_out_25 ), .out_26(\σοσ_2_out_26 ), .out_27(\σοσ_2_out_27 ), .out_28(\σοσ_2_out_28 ),
    .out_29(\σοσ_2_out_29 ), .out_30(\σοσ_2_out_30 ), .out_31(\σοσ_2_out_31 ), .out_32(\σοσ_2_out_32 ),
    .out_33(\σοσ_2_out_33 ));
  \σοσ  \u_σοσ_3  (
    .in_1(32'h115), .out_2(\σοσ_3_out_2 ), .out_3(\σοσ_3_out_3 ), .out_4(\σοσ_3_out_4 ),
    .out_5(\σοσ_3_out_5 ), .out_6(\σοσ_3_out_6 ), .out_7(\σοσ_3_out_7 ), .out_8(\σοσ_3_out_8 ),
    .out_9(\σοσ_3_out_9 ), .out_10(\σοσ_3_out_10 ), .out_11(\σοσ_3_out_11 ), .out_12(\σοσ_3_out_12 ),
    .out_13(\σοσ_3_out_13 ), .out_14(\σοσ_3_out_14 ), .out_15(\σοσ_3_out_15 ), .out_16(\σοσ_3_out_16 ),
    .out_17(\σοσ_3_out_17 ), .out_18(\σοσ_3_out_18 ), .out_19(\σοσ_3_out_19 ), .out_20(\σοσ_3_out_20 ),
    .out_21(\σοσ_3_out_21 ), .out_22(\σοσ_3_out_22 ), .out_23(\σοσ_3_out_23 ), .out_24(\σοσ_3_out_24 ),
    .out_25(\σοσ_3_out_25 ), .out_26(\σοσ_3_out_26 ), .out_27(\σοσ_3_out_27 ), .out_28(\σοσ_3_out_28 ),
    .out_29(\σοσ_3_out_29 ), .out_30(\σοσ_3_out_30 ), .out_31(\σοσ_3_out_31 ), .out_32(\σοσ_3_out_32 ),
    .out_33(\σοσ_3_out_33 ));
  \σοσ  \u_σοσ_4  (
    .in_1(32'h311), .out_2(\σοσ_4_out_2 ), .out_3(\σοσ_4_out_3 ), .out_4(\σοσ_4_out_4 ),
    .out_5(\σοσ_4_out_5 ), .out_6(\σοσ_4_out_6 ), .out_7(\σοσ_4_out_7 ), .out_8(\σοσ_4_out_8 ),
    .out_9(\σοσ_4_out_9 ), .out_10(\σοσ_4_out_10 ), .out_11(\σοσ_4_out_11 ), .out_12(\σοσ_4_out_12 ),
    .out_13(\σοσ_4_out_13 ), .out_14(\σοσ_4_out_14 ), .out_15(\σοσ_4_out_15 ), .out_16(\σοσ_4_out_16 ),
    .out_17(\σοσ_4_out_17 ), .out_18(\σοσ_4_out_18 ), .out_19(\σοσ_4_out_19 ), .out_20(\σοσ_4_out_20 ),
    .out_21(\σοσ_4_out_21 ), .out_22(\σοσ_4_out_22 ), .out_23(\σοσ_4_out_23 ), .out_24(\σοσ_4_out_24 ),
    .out_25(\σοσ_4_out_25 ), .out_26(\σοσ_4_out_26 ), .out_27(\σοσ_4_out_27 ), .out_28(\σοσ_4_out_28 ),
    .out_29(\σοσ_4_out_29 ), .out_30(\σοσ_4_out_30 ), .out_31(\σοσ_4_out_31 ), .out_32(\σοσ_4_out_32 ),
    .out_33(\σοσ_4_out_33 ));
  \σοσ  \u_σοσ_5  (
    .in_1(32'h355), .out_2(\σοσ_5_out_2 ), .out_3(\σοσ_5_out_3 ), .out_4(\σοσ_5_out_4 ),
    .out_5(\σοσ_5_out_5 ), .out_6(\σοσ_5_out_6 ), .out_7(\σοσ_5_out_7 ), .out_8(\σοσ_5_out_8 ),
    .out_9(\σοσ_5_out_9 ), .out_10(\σοσ_5_out_10 ), .out_11(\σοσ_5_out_11 ), .out_12(\σοσ_5_out_12 ),
    .out_13(\σοσ_5_out_13 ), .out_14(\σοσ_5_out_14 ), .out_15(\σοσ_5_out_15 ), .out_16(\σοσ_5_out_16 ),
    .out_17(\σοσ_5_out_17 ), .out_18(\σοσ_5_out_18 ), .out_19(\σοσ_5_out_19 ), .out_20(\σοσ_5_out_20 ),
    .out_21(\σοσ_5_out_21 ), .out_22(\σοσ_5_out_22 ), .out_23(\σοσ_5_out_23 ), .out_24(\σοσ_5_out_24 ),
    .out_25(\σοσ_5_out_25 ), .out_26(\σοσ_5_out_26 ), .out_27(\σοσ_5_out_27 ), .out_28(\σοσ_5_out_28 ),
    .out_29(\σοσ_5_out_29 ), .out_30(\σοσ_5_out_30 ), .out_31(\σοσ_5_out_31 ), .out_32(\σοσ_5_out_32 ),
    .out_33(\σοσ_5_out_33 ));
  \σοσ  \u_σοσ_6  (
    .in_1(32'h351), .out_2(\σοσ_6_out_2 ), .out_3(\σοσ_6_out_3 ), .out_4(\σοσ_6_out_4 ),
    .out_5(\σοσ_6_out_5 ), .out_6(\σοσ_6_out_6 ), .out_7(\σοσ_6_out_7 ), .out_8(\σοσ_6_out_8 ),
    .out_9(\σοσ_6_out_9 ), .out_10(\σοσ_6_out_10 ), .out_11(\σοσ_6_out_11 ), .out_12(\σοσ_6_out_12 ),
    .out_13(\σοσ_6_out_13 ), .out_14(\σοσ_6_out_14 ), .out_15(\σοσ_6_out_15 ), .out_16(\σοσ_6_out_16 ),
    .out_17(\σοσ_6_out_17 ), .out_18(\σοσ_6_out_18 ), .out_19(\σοσ_6_out_19 ), .out_20(\σοσ_6_out_20 ),
    .out_21(\σοσ_6_out_21 ), .out_22(\σοσ_6_out_22 ), .out_23(\σοσ_6_out_23 ), .out_24(\σοσ_6_out_24 ),
    .out_25(\σοσ_6_out_25 ), .out_26(\σοσ_6_out_26 ), .out_27(\σοσ_6_out_27 ), .out_28(\σοσ_6_out_28 ),
    .out_29(\σοσ_6_out_29 ), .out_30(\σοσ_6_out_30 ), .out_31(\σοσ_6_out_31 ), .out_32(\σοσ_6_out_32 ),
    .out_33(\σοσ_6_out_33 ));
  \σοσ  \u_σοσ_7  (
    .in_1(32'h155), .out_2(\σοσ_7_out_2 ), .out_3(\σοσ_7_out_3 ), .out_4(\σοσ_7_out_4 ),
    .out_5(\σοσ_7_out_5 ), .out_6(\σοσ_7_out_6 ), .out_7(\σοσ_7_out_7 ), .out_8(\σοσ_7_out_8 ),
    .out_9(\σοσ_7_out_9 ), .out_10(\σοσ_7_out_10 ), .out_11(\σοσ_7_out_11 ), .out_12(\σοσ_7_out_12 ),
    .out_13(\σοσ_7_out_13 ), .out_14(\σοσ_7_out_14 ), .out_15(\σοσ_7_out_15 ), .out_16(\σοσ_7_out_16 ),
    .out_17(\σοσ_7_out_17 ), .out_18(\σοσ_7_out_18 ), .out_19(\σοσ_7_out_19 ), .out_20(\σοσ_7_out_20 ),
    .out_21(\σοσ_7_out_21 ), .out_22(\σοσ_7_out_22 ), .out_23(\σοσ_7_out_23 ), .out_24(\σοσ_7_out_24 ),
    .out_25(\σοσ_7_out_25 ), .out_26(\σοσ_7_out_26 ), .out_27(\σοσ_7_out_27 ), .out_28(\σοσ_7_out_28 ),
    .out_29(\σοσ_7_out_29 ), .out_30(\σοσ_7_out_30 ), .out_31(\σοσ_7_out_31 ), .out_32(\σοσ_7_out_32 ),
    .out_33(\σοσ_7_out_33 ));
  \σοσ  \u_σοσ_8  (
    .in_1(32'h1f1), .out_2(\σοσ_8_out_2 ), .out_3(\σοσ_8_out_3 ), .out_4(\σοσ_8_out_4 ),
    .out_5(\σοσ_8_out_5 ), .out_6(\σοσ_8_out_6 ), .out_7(\σοσ_8_out_7 ), .out_8(\σοσ_8_out_8 ),
    .out_9(\σοσ_8_out_9 ), .out_10(\σοσ_8_out_10 ), .out_11(\σοσ_8_out_11 ), .out_12(\σοσ_8_out_12 ),
    .out_13(\σοσ_8_out_13 ), .out_14(\σοσ_8_out_14 ), .out_15(\σοσ_8_out_15 ), .out_16(\σοσ_8_out_16 ),
    .out_17(\σοσ_8_out_17 ), .out_18(\σοσ_8_out_18 ), .out_19(\σοσ_8_out_19 ), .out_20(\σοσ_8_out_20 ),
    .out_21(\σοσ_8_out_21 ), .out_22(\σοσ_8_out_22 ), .out_23(\σοσ_8_out_23 ), .out_24(\σοσ_8_out_24 ),
    .out_25(\σοσ_8_out_25 ), .out_26(\σοσ_8_out_26 ), .out_27(\σοσ_8_out_27 ), .out_28(\σοσ_8_out_28 ),
    .out_29(\σοσ_8_out_29 ), .out_30(\σοσ_8_out_30 ), .out_31(\σοσ_8_out_31 ), .out_32(\σοσ_8_out_32 ),
    .out_33(\σοσ_8_out_33 ));
  \σοσ  \u_σοσ_9  (
    .in_1(32'h5f), .out_2(\σοσ_9_out_2 ), .out_3(\σοσ_9_out_3 ), .out_4(\σοσ_9_out_4 ),
    .out_5(\σοσ_9_out_5 ), .out_6(\σοσ_9_out_6 ), .out_7(\σοσ_9_out_7 ), .out_8(\σοσ_9_out_8 ),
    .out_9(\σοσ_9_out_9 ), .out_10(\σοσ_9_out_10 ), .out_11(\σοσ_9_out_11 ), .out_12(\σοσ_9_out_12 ),
    .out_13(\σοσ_9_out_13 ), .out_14(\σοσ_9_out_14 ), .out_15(\σοσ_9_out_15 ), .out_16(\σοσ_9_out_16 ),
    .out_17(\σοσ_9_out_17 ), .out_18(\σοσ_9_out_18 ), .out_19(\σοσ_9_out_19 ), .out_20(\σοσ_9_out_20 ),
    .out_21(\σοσ_9_out_21 ), .out_22(\σοσ_9_out_22 ), .out_23(\σοσ_9_out_23 ), .out_24(\σοσ_9_out_24 ),
    .out_25(\σοσ_9_out_25 ), .out_26(\σοσ_9_out_26 ), .out_27(\σοσ_9_out_27 ), .out_28(\σοσ_9_out_28 ),
    .out_29(\σοσ_9_out_29 ), .out_30(\σοσ_9_out_30 ), .out_31(\σοσ_9_out_31 ), .out_32(\σοσ_9_out_32 ),
    .out_33(\σοσ_9_out_33 ));
  \σοσ  \u_σοσ_10  (
    .in_1(32'h40), .out_2(\σοσ_10_out_2 ), .out_3(\σοσ_10_out_3 ), .out_4(\σοσ_10_out_4 ),
    .out_5(\σοσ_10_out_5 ), .out_6(\σοσ_10_out_6 ), .out_7(\σοσ_10_out_7 ), .out_8(\σοσ_10_out_8 ),
    .out_9(\σοσ_10_out_9 ), .out_10(\σοσ_10_out_10 ), .out_11(\σοσ_10_out_11 ), .out_12(\σοσ_10_out_12 ),
    .out_13(\σοσ_10_out_13 ), .out_14(\σοσ_10_out_14 ), .out_15(\σοσ_10_out_15 ), .out_16(\σοσ_10_out_16 ),
    .out_17(\σοσ_10_out_17 ), .out_18(\σοσ_10_out_18 ), .out_19(\σοσ_10_out_19 ), .out_20(\σοσ_10_out_20 ),
    .out_21(\σοσ_10_out_21 ), .out_22(\σοσ_10_out_22 ), .out_23(\σοσ_10_out_23 ), .out_24(\σοσ_10_out_24 ),
    .out_25(\σοσ_10_out_25 ), .out_26(\σοσ_10_out_26 ), .out_27(\σοσ_10_out_27 ), .out_28(\σοσ_10_out_28 ),
    .out_29(\σοσ_10_out_29 ), .out_30(\σοσ_10_out_30 ), .out_31(\σοσ_10_out_31 ), .out_32(\σοσ_10_out_32 ),
    .out_33(\σοσ_10_out_33 ));
  \σοσ  \u_σοσ_11  (
    .in_1(32'he0), .out_2(\σοσ_11_out_2 ), .out_3(\σοσ_11_out_3 ), .out_4(\σοσ_11_out_4 ),
    .out_5(\σοσ_11_out_5 ), .out_6(\σοσ_11_out_6 ), .out_7(\σοσ_11_out_7 ), .out_8(\σοσ_11_out_8 ),
    .out_9(\σοσ_11_out_9 ), .out_10(\σοσ_11_out_10 ), .out_11(\σοσ_11_out_11 ), .out_12(\σοσ_11_out_12 ),
    .out_13(\σοσ_11_out_13 ), .out_14(\σοσ_11_out_14 ), .out_15(\σοσ_11_out_15 ), .out_16(\σοσ_11_out_16 ),
    .out_17(\σοσ_11_out_17 ), .out_18(\σοσ_11_out_18 ), .out_19(\σοσ_11_out_19 ), .out_20(\σοσ_11_out_20 ),
    .out_21(\σοσ_11_out_21 ), .out_22(\σοσ_11_out_22 ), .out_23(\σοσ_11_out_23 ), .out_24(\σοσ_11_out_24 ),
    .out_25(\σοσ_11_out_25 ), .out_26(\σοσ_11_out_26 ), .out_27(\σοσ_11_out_27 ), .out_28(\σοσ_11_out_28 ),
    .out_29(\σοσ_11_out_29 ), .out_30(\σοσ_11_out_30 ), .out_31(\σοσ_11_out_31 ), .out_32(\σοσ_11_out_32 ),
    .out_33(\σοσ_11_out_33 ));
  \σοσ  \u_σοσ_12  (
    .in_1(32'ha0), .out_2(\σοσ_12_out_2 ), .out_3(\σοσ_12_out_3 ), .out_4(\σοσ_12_out_4 ),
    .out_5(\σοσ_12_out_5 ), .out_6(\σοσ_12_out_6 ), .out_7(\σοσ_12_out_7 ), .out_8(\σοσ_12_out_8 ),
    .out_9(\σοσ_12_out_9 ), .out_10(\σοσ_12_out_10 ), .out_11(\σοσ_12_out_11 ), .out_12(\σοσ_12_out_12 ),
    .out_13(\σοσ_12_out_13 ), .out_14(\σοσ_12_out_14 ), .out_15(\σοσ_12_out_15 ), .out_16(\σοσ_12_out_16 ),
    .out_17(\σοσ_12_out_17 ), .out_18(\σοσ_12_out_18 ), .out_19(\σοσ_12_out_19 ), .out_20(\σοσ_12_out_20 ),
    .out_21(\σοσ_12_out_21 ), .out_22(\σοσ_12_out_22 ), .out_23(\σοσ_12_out_23 ), .out_24(\σοσ_12_out_24 ),
    .out_25(\σοσ_12_out_25 ), .out_26(\σοσ_12_out_26 ), .out_27(\σοσ_12_out_27 ), .out_28(\σοσ_12_out_28 ),
    .out_29(\σοσ_12_out_29 ), .out_30(\σοσ_12_out_30 ), .out_31(\σοσ_12_out_31 ), .out_32(\σοσ_12_out_32 ),
    .out_33(\σοσ_12_out_33 ));
  \σοσ  \u_σοσ_13  (
    .in_1(32'he0), .out_2(\σοσ_13_out_2 ), .out_3(\σοσ_13_out_3 ), .out_4(\σοσ_13_out_4 ),
    .out_5(\σοσ_13_out_5 ), .out_6(\σοσ_13_out_6 ), .out_7(\σοσ_13_out_7 ), .out_8(\σοσ_13_out_8 ),
    .out_9(\σοσ_13_out_9 ), .out_10(\σοσ_13_out_10 ), .out_11(\σοσ_13_out_11 ), .out_12(\σοσ_13_out_12 ),
    .out_13(\σοσ_13_out_13 ), .out_14(\σοσ_13_out_14 ), .out_15(\σοσ_13_out_15 ), .out_16(\σοσ_13_out_16 ),
    .out_17(\σοσ_13_out_17 ), .out_18(\σοσ_13_out_18 ), .out_19(\σοσ_13_out_19 ), .out_20(\σοσ_13_out_20 ),
    .out_21(\σοσ_13_out_21 ), .out_22(\σοσ_13_out_22 ), .out_23(\σοσ_13_out_23 ), .out_24(\σοσ_13_out_24 ),
    .out_25(\σοσ_13_out_25 ), .out_26(\σοσ_13_out_26 ), .out_27(\σοσ_13_out_27 ), .out_28(\σοσ_13_out_28 ),
    .out_29(\σοσ_13_out_29 ), .out_30(\σοσ_13_out_30 ), .out_31(\σοσ_13_out_31 ), .out_32(\σοσ_13_out_32 ),
    .out_33(\σοσ_13_out_33 ));
  not not_1 (not_1_out, comparator_2_lt);
  Multiplexer #(.select(5), .width(32), .enable("false")) multiplexer_1 (
    .in0(\σοσ_1_out_2 ), .in1(\σοσ_1_out_3 ), .in2(\σοσ_1_out_4 ), .in3(\σοσ_1_out_5 ), .in4(\σοσ_1_out_6 ),
    .in5(\σοσ_1_out_7 ), .in6(\σοσ_1_out_8 ), .in7(\σοσ_1_out_9 ), .in8(\σοσ_1_out_10 ),
    .in9(\σοσ_1_out_11 ), .in10(\σοσ_1_out_12 ), .in11(\σοσ_1_out_13 ), .in12(\σοσ_1_out_14 ),
    .in13(\σοσ_1_out_15 ), .in14(\σοσ_1_out_16 ), .in15(\σοσ_1_out_17 ), .in16(\σοσ_1_out_18 ),
    .in17(\σοσ_1_out_19 ), .in18(\σοσ_1_out_20 ), .in19(\σοσ_1_out_21 ), .in20(\σοσ_1_out_22 ),
    .in21(\σοσ_1_out_23 ), .in22(\σοσ_1_out_24 ), .in23(\σοσ_1_out_25 ), .in24(\σοσ_1_out_26 ),
    .in25(\σοσ_1_out_27 ), .in26(\σοσ_1_out_28 ), .in27(\σοσ_1_out_29 ), .in28(\σοσ_1_out_30 ),
    .in29(\σοσ_1_out_31 ), .in30(\σοσ_1_out_32 ), .in31(\σοσ_1_out_33 ), .out(multiplexer_1_out),
    .sel(bit_extender_1_out));
  Multiplexer #(.select(5), .width(32), .enable("false")) multiplexer_2 (
    .in0(\σοσ_2_out_2 ), .in1(\σοσ_2_out_3 ), .in2(\σοσ_2_out_4 ), .in3(\σοσ_2_out_5 ), .in4(\σοσ_2_out_6 ),
    .in5(\σοσ_2_out_7 ), .in6(\σοσ_2_out_8 ), .in7(\σοσ_2_out_9 ), .in8(\σοσ_2_out_10 ),
    .in9(\σοσ_2_out_11 ), .in10(\σοσ_2_out_12 ), .in11(\σοσ_2_out_13 ), .in12(\σοσ_2_out_14 ),
    .in13(\σοσ_2_out_15 ), .in14(\σοσ_2_out_16 ), .in15(\σοσ_2_out_17 ), .in16(\σοσ_2_out_18 ),
    .in17(\σοσ_2_out_19 ), .in18(\σοσ_2_out_20 ), .in19(\σοσ_2_out_21 ), .in20(\σοσ_2_out_22 ),
    .in21(\σοσ_2_out_23 ), .in22(\σοσ_2_out_24 ), .in23(\σοσ_2_out_25 ), .in24(\σοσ_2_out_26 ),
    .in25(\σοσ_2_out_27 ), .in26(\σοσ_2_out_28 ), .in27(\σοσ_2_out_29 ), .in28(\σοσ_2_out_30 ),
    .in29(\σοσ_2_out_31 ), .in30(\σοσ_2_out_32 ), .in31(\σοσ_2_out_33 ), .out(multiplexer_2_out),
    .sel(bit_extender_1_out));
  Multiplexer #(.select(5), .width(32), .enable("false")) multiplexer_3 (
    .in0(\σοσ_3_out_2 ), .in1(\σοσ_3_out_3 ), .in2(\σοσ_3_out_4 ), .in3(\σοσ_3_out_5 ), .in4(\σοσ_3_out_6 ),
    .in5(\σοσ_3_out_7 ), .in6(\σοσ_3_out_8 ), .in7(\σοσ_3_out_9 ), .in8(\σοσ_3_out_10 ),
    .in9(\σοσ_3_out_11 ), .in10(\σοσ_3_out_12 ), .in11(\σοσ_3_out_13 ), .in12(\σοσ_3_out_14 ),
    .in13(\σοσ_3_out_15 ), .in14(\σοσ_3_out_16 ), .in15(\σοσ_3_out_17 ), .in16(\σοσ_3_out_18 ),
    .in17(\σοσ_3_out_19 ), .in18(\σοσ_3_out_20 ), .in19(\σοσ_3_out_21 ), .in20(\σοσ_3_out_22 ),
    .in21(\σοσ_3_out_23 ), .in22(\σοσ_3_out_24 ), .in23(\σοσ_3_out_25 ), .in24(\σοσ_3_out_26 ),
    .in25(\σοσ_3_out_27 ), .in26(\σοσ_3_out_28 ), .in27(\σοσ_3_out_29 ), .in28(\σοσ_3_out_30 ),
    .in29(\σοσ_3_out_31 ), .in30(\σοσ_3_out_32 ), .in31(\σοσ_3_out_33 ), .out(multiplexer_3_out),
    .sel(bit_extender_1_out));
  Multiplexer #(.select(5), .width(32), .enable("false")) multiplexer_4 (
    .in0(\σοσ_4_out_2 ), .in1(\σοσ_4_out_3 ), .in2(\σοσ_4_out_4 ), .in3(\σοσ_4_out_5 ), .in4(\σοσ_4_out_6 ),
    .in5(\σοσ_4_out_7 ), .in6(\σοσ_4_out_8 ), .in7(\σοσ_4_out_9 ), .in8(\σοσ_4_out_10 ),
    .in9(\σοσ_4_out_11 ), .in10(\σοσ_4_out_12 ), .in11(\σοσ_4_out_13 ), .in12(\σοσ_4_out_14 ),
    .in13(\σοσ_4_out_15 ), .in14(\σοσ_4_out_16 ), .in15(\σοσ_4_out_17 ), .in16(\σοσ_4_out_18 ),
    .in17(\σοσ_4_out_19 ), .in18(\σοσ_4_out_20 ), .in19(\σοσ_4_out_21 ), .in20(\σοσ_4_out_22 ),
    .in21(\σοσ_4_out_23 ), .in22(\σοσ_4_out_24 ), .in23(\σοσ_4_out_25 ), .in24(\σοσ_4_out_26 ),
    .in25(\σοσ_4_out_27 ), .in26(\σοσ_4_out_28 ), .in27(\σοσ_4_out_29 ), .in28(\σοσ_4_out_30 ),
    .in29(\σοσ_4_out_31 ), .in30(\σοσ_4_out_32 ), .in31(\σοσ_4_out_33 ), .out(multiplexer_4_out),
    .sel(bit_extender_1_out));
  Multiplexer #(.select(5), .width(32), .enable("false")) multiplexer_5 (
    .in0(\σοσ_5_out_2 ), .in1(\σοσ_5_out_3 ), .in2(\σοσ_5_out_4 ), .in3(\σοσ_5_out_5 ), .in4(\σοσ_5_out_6 ),
    .in5(\σοσ_5_out_7 ), .in6(\σοσ_5_out_8 ), .in7(\σοσ_5_out_9 ), .in8(\σοσ_5_out_10 ),
    .in9(\σοσ_5_out_11 ), .in10(\σοσ_5_out_12 ), .in11(\σοσ_5_out_13 ), .in12(\σοσ_5_out_14 ),
    .in13(\σοσ_5_out_15 ), .in14(\σοσ_5_out_16 ), .in15(\σοσ_5_out_17 ), .in16(\σοσ_5_out_18 ),
    .in17(\σοσ_5_out_19 ), .in18(\σοσ_5_out_20 ), .in19(\σοσ_5_out_21 ), .in20(\σοσ_5_out_22 ),
    .in21(\σοσ_5_out_23 ), .in22(\σοσ_5_out_24 ), .in23(\σοσ_5_out_25 ), .in24(\σοσ_5_out_26 ),
    .in25(\σοσ_5_out_27 ), .in26(\σοσ_5_out_28 ), .in27(\σοσ_5_out_29 ), .in28(\σοσ_5_out_30 ),
    .in29(\σοσ_5_out_31 ), .in30(\σοσ_5_out_32 ), .in31(\σοσ_5_out_33 ), .out(multiplexer_5_out),
    .sel(bit_extender_1_out));
  Multiplexer #(.select(5), .width(32), .enable("false")) multiplexer_6 (
    .in0(\σοσ_6_out_2 ), .in1(\σοσ_6_out_3 ), .in2(\σοσ_6_out_4 ), .in3(\σοσ_6_out_5 ), .in4(\σοσ_6_out_6 ),
    .in5(\σοσ_6_out_7 ), .in6(\σοσ_6_out_8 ), .in7(\σοσ_6_out_9 ), .in8(\σοσ_6_out_10 ),
    .in9(\σοσ_6_out_11 ), .in10(\σοσ_6_out_12 ), .in11(\σοσ_6_out_13 ), .in12(\σοσ_6_out_14 ),
    .in13(\σοσ_6_out_15 ), .in14(\σοσ_6_out_16 ), .in15(\σοσ_6_out_17 ), .in16(\σοσ_6_out_18 ),
    .in17(\σοσ_6_out_19 ), .in18(\σοσ_6_out_20 ), .in19(\σοσ_6_out_21 ), .in20(\σοσ_6_out_22 ),
    .in21(\σοσ_6_out_23 ), .in22(\σοσ_6_out_24 ), .in23(\σοσ_6_out_25 ), .in24(\σοσ_6_out_26 ),
    .in25(\σοσ_6_out_27 ), .in26(\σοσ_6_out_28 ), .in27(\σοσ_6_out_29 ), .in28(\σοσ_6_out_30 ),
    .in29(\σοσ_6_out_31 ), .in30(\σοσ_6_out_32 ), .in31(\σοσ_6_out_33 ), .out(multiplexer_6_out),
    .sel(bit_extender_1_out));
  Multiplexer #(.select(5), .width(32), .enable("false")) multiplexer_7 (
    .in0(\σοσ_7_out_2 ), .in1(\σοσ_7_out_3 ), .in2(\σοσ_7_out_4 ), .in3(\σοσ_7_out_5 ), .in4(\σοσ_7_out_6 ),
    .in5(\σοσ_7_out_7 ), .in6(\σοσ_7_out_8 ), .in7(\σοσ_7_out_9 ), .in8(\σοσ_7_out_10 ),
    .in9(\σοσ_7_out_11 ), .in10(\σοσ_7_out_12 ), .in11(\σοσ_7_out_13 ), .in12(\σοσ_7_out_14 ),
    .in13(\σοσ_7_out_15 ), .in14(\σοσ_7_out_16 ), .in15(\σοσ_7_out_17 ), .in16(\σοσ_7_out_18 ),
    .in17(\σοσ_7_out_19 ), .in18(\σοσ_7_out_20 ), .in19(\σοσ_7_out_21 ), .in20(\σοσ_7_out_22 ),
    .in21(\σοσ_7_out_23 ), .in22(\σοσ_7_out_24 ), .in23(\σοσ_7_out_25 ), .in24(\σοσ_7_out_26 ),
    .in25(\σοσ_7_out_27 ), .in26(\σοσ_7_out_28 ), .in27(\σοσ_7_out_29 ), .in28(\σοσ_7_out_30 ),
    .in29(\σοσ_7_out_31 ), .in30(\σοσ_7_out_32 ), .in31(\σοσ_7_out_33 ), .out(multiplexer_7_out),
    .sel(bit_extender_1_out));
  Multiplexer #(.select(5), .width(32), .enable("false")) multiplexer_8 (
    .in0(\σοσ_8_out_2 ), .in1(\σοσ_8_out_3 ), .in2(\σοσ_8_out_4 ), .in3(\σοσ_8_out_5 ), .in4(\σοσ_8_out_6 ),
    .in5(\σοσ_8_out_7 ), .in6(\σοσ_8_out_8 ), .in7(\σοσ_8_out_9 ), .in8(\σοσ_8_out_10 ),
    .in9(\σοσ_8_out_11 ), .in10(\σοσ_8_out_12 ), .in11(\σοσ_8_out_13 ), .in12(\σοσ_8_out_14 ),
    .in13(\σοσ_8_out_15 ), .in14(\σοσ_8_out_16 ), .in15(\σοσ_8_out_17 ), .in16(\σοσ_8_out_18 ),
    .in17(\σοσ_8_out_19 ), .in18(\σοσ_8_out_20 ), .in19(\σοσ_8_out_21 ), .in20(\σοσ_8_out_22 ),
    .in21(\σοσ_8_out_23 ), .in22(\σοσ_8_out_24 ), .in23(\σοσ_8_out_25 ), .in24(\σοσ_8_out_26 ),
    .in25(\σοσ_8_out_27 ), .in26(\σοσ_8_out_28 ), .in27(\σοσ_8_out_29 ), .in28(\σοσ_8_out_30 ),
    .in29(\σοσ_8_out_31 ), .in30(\σοσ_8_out_32 ), .in31(\σοσ_8_out_33 ), .out(multiplexer_8_out),
    .sel(bit_extender_1_out));
  Multiplexer #(.select(5), .width(32), .enable("false")) multiplexer_9 (
    .in0(\σοσ_9_out_2 ), .in1(\σοσ_9_out_3 ), .in2(\σοσ_9_out_4 ), .in3(\σοσ_9_out_5 ), .in4(\σοσ_9_out_6 ),
    .in5(\σοσ_9_out_7 ), .in6(\σοσ_9_out_8 ), .in7(\σοσ_9_out_9 ), .in8(\σοσ_9_out_10 ),
    .in9(\σοσ_9_out_11 ), .in10(\σοσ_9_out_12 ), .in11(\σοσ_9_out_13 ), .in12(\σοσ_9_out_14 ),
    .in13(\σοσ_9_out_15 ), .in14(\σοσ_9_out_16 ), .in15(\σοσ_9_out_17 ), .in16(\σοσ_9_out_18 ),
    .in17(\σοσ_9_out_19 ), .in18(\σοσ_9_out_20 ), .in19(\σοσ_9_out_21 ), .in20(\σοσ_9_out_22 ),
    .in21(\σοσ_9_out_23 ), .in22(\σοσ_9_out_24 ), .in23(\σοσ_9_out_25 ), .in24(\σοσ_9_out_26 ),
    .in25(\σοσ_9_out_27 ), .in26(\σοσ_9_out_28 ), .in27(\σοσ_9_out_29 ), .in28(\σοσ_9_out_30 ),
    .in29(\σοσ_9_out_31 ), .in30(\σοσ_9_out_32 ), .in31(\σοσ_9_out_33 ), .out(multiplexer_9_out),
    .sel(bit_extender_1_out));
  Multiplexer #(.select(5), .width(32), .enable("false")) multiplexer_10 (
    .in0(\σοσ_10_out_2 ), .in1(\σοσ_10_out_3 ), .in2(\σοσ_10_out_4 ), .in3(\σοσ_10_out_5 ),
    .in4(\σοσ_10_out_6 ), .in5(\σοσ_10_out_7 ), .in6(\σοσ_10_out_8 ), .in7(\σοσ_10_out_9 ),
    .in8(\σοσ_10_out_10 ), .in9(\σοσ_10_out_11 ), .in10(\σοσ_10_out_12 ), .in11(\σοσ_10_out_13 ),
    .in12(\σοσ_10_out_14 ), .in13(\σοσ_10_out_15 ), .in14(\σοσ_10_out_16 ), .in15(\σοσ_10_out_17 ),
    .in16(\σοσ_10_out_18 ), .in17(\σοσ_10_out_19 ), .in18(\σοσ_10_out_20 ), .in19(\σοσ_10_out_21 ),
    .in20(\σοσ_10_out_22 ), .in21(\σοσ_10_out_23 ), .in22(\σοσ_10_out_24 ), .in23(\σοσ_10_out_25 ),
    .in24(\σοσ_10_out_26 ), .in25(\σοσ_10_out_27 ), .in26(\σοσ_10_out_28 ), .in27(\σοσ_10_out_29 ),
    .in28(\σοσ_10_out_30 ), .in29(\σοσ_10_out_31 ), .in30(\σοσ_10_out_32 ), .in31(\σοσ_10_out_33 ),
    .out(multiplexer_10_out), .sel(bit_extender_1_out));
  Multiplexer #(.select(5), .width(32), .enable("false")) multiplexer_11 (
    .in0(\σοσ_11_out_2 ), .in1(\σοσ_11_out_3 ), .in2(\σοσ_11_out_4 ), .in3(\σοσ_11_out_5 ),
    .in4(\σοσ_11_out_6 ), .in5(\σοσ_11_out_7 ), .in6(\σοσ_11_out_8 ), .in7(\σοσ_11_out_9 ),
    .in8(\σοσ_11_out_10 ), .in9(\σοσ_11_out_11 ), .in10(\σοσ_11_out_12 ), .in11(\σοσ_11_out_13 ),
    .in12(\σοσ_11_out_14 ), .in13(\σοσ_11_out_15 ), .in14(\σοσ_11_out_16 ), .in15(\σοσ_11_out_17 ),
    .in16(\σοσ_11_out_18 ), .in17(\σοσ_11_out_19 ), .in18(\σοσ_11_out_20 ), .in19(\σοσ_11_out_21 ),
    .in20(\σοσ_11_out_22 ), .in21(\σοσ_11_out_23 ), .in22(\σοσ_11_out_24 ), .in23(\σοσ_11_out_25 ),
    .in24(\σοσ_11_out_26 ), .in25(\σοσ_11_out_27 ), .in26(\σοσ_11_out_28 ), .in27(\σοσ_11_out_29 ),
    .in28(\σοσ_11_out_30 ), .in29(\σοσ_11_out_31 ), .in30(\σοσ_11_out_32 ), .in31(\σοσ_11_out_33 ),
    .out(multiplexer_11_out), .sel(bit_extender_1_out));
  Multiplexer #(.select(5), .width(32), .enable("false")) multiplexer_12 (
    .in0(\σοσ_12_out_2 ), .in1(\σοσ_12_out_3 ), .in2(\σοσ_12_out_4 ), .in3(\σοσ_12_out_5 ),
    .in4(\σοσ_12_out_6 ), .in5(\σοσ_12_out_7 ), .in6(\σοσ_12_out_8 ), .in7(\σοσ_12_out_9 ),
    .in8(\σοσ_12_out_10 ), .in9(\σοσ_12_out_11 ), .in10(\σοσ_12_out_12 ), .in11(\σοσ_12_out_13 ),
    .in12(\σοσ_12_out_14 ), .in13(\σοσ_12_out_15 ), .in14(\σοσ_12_out_16 ), .in15(\σοσ_12_out_17 ),
    .in16(\σοσ_12_out_18 ), .in17(\σοσ_12_out_19 ), .in18(\σοσ_12_out_20 ), .in19(\σοσ_12_out_21 ),
    .in20(\σοσ_12_out_22 ), .in21(\σοσ_12_out_23 ), .in22(\σοσ_12_out_24 ), .in23(\σοσ_12_out_25 ),
    .in24(\σοσ_12_out_26 ), .in25(\σοσ_12_out_27 ), .in26(\σοσ_12_out_28 ), .in27(\σοσ_12_out_29 ),
    .in28(\σοσ_12_out_30 ), .in29(\σοσ_12_out_31 ), .in30(\σοσ_12_out_32 ), .in31(\σοσ_12_out_33 ),
    .out(multiplexer_12_out), .sel(bit_extender_1_out));
  Multiplexer #(.select(5), .width(32), .enable("false")) multiplexer_13 (
    .in0(\σοσ_13_out_2 ), .in1(\σοσ_13_out_3 ), .in2(\σοσ_13_out_4 ), .in3(\σοσ_13_out_5 ),
    .in4(\σοσ_13_out_6 ), .in5(\σοσ_13_out_7 ), .in6(\σοσ_13_out_8 ), .in7(\σοσ_13_out_9 ),
    .in8(\σοσ_13_out_10 ), .in9(\σοσ_13_out_11 ), .in10(\σοσ_13_out_12 ), .in11(\σοσ_13_out_13 ),
    .in12(\σοσ_13_out_14 ), .in13(\σοσ_13_out_15 ), .in14(\σοσ_13_out_16 ), .in15(\σοσ_13_out_17 ),
    .in16(\σοσ_13_out_18 ), .in17(\σοσ_13_out_19 ), .in18(\σοσ_13_out_20 ), .in19(\σοσ_13_out_21 ),
    .in20(\σοσ_13_out_22 ), .in21(\σοσ_13_out_23 ), .in22(\σοσ_13_out_24 ), .in23(\σοσ_13_out_25 ),
    .in24(\σοσ_13_out_26 ), .in25(\σοσ_13_out_27 ), .in26(\σοσ_13_out_28 ), .in27(\σοσ_13_out_29 ),
    .in28(\σοσ_13_out_30 ), .in29(\σοσ_13_out_31 ), .in30(\σοσ_13_out_32 ), .in31(\σοσ_13_out_33 ),
    .out(multiplexer_13_out), .sel(bit_extender_1_out));
  Multiplexer #(.width(32), .enable("false")) multiplexer_14 (
    .in0(multiplexer_1_out), .in1({32{1'b0}}), .out(out_5), .sel(not_1_out));
  Multiplexer #(.width(32), .enable("false")) multiplexer_15 (
    .in0(multiplexer_2_out), .in1({32{1'b0}}), .out(out_6), .sel(not_1_out));
  Multiplexer #(.width(32), .enable("false")) multiplexer_16 (
    .in0(multiplexer_3_out), .in1({32{1'b0}}), .out(out_7), .sel(not_1_out));
  Multiplexer #(.width(32), .enable("false")) multiplexer_17 (
    .in0(multiplexer_4_out), .in1({32{1'b0}}), .out(out_8), .sel(not_1_out));
  Multiplexer #(.width(32), .enable("false")) multiplexer_18 (
    .in0(multiplexer_5_out), .in1({32{1'b0}}), .out(out_9), .sel(not_1_out));
  Multiplexer #(.width(32), .enable("false")) multiplexer_19 (
    .in0(multiplexer_6_out), .in1({32{1'b0}}), .out(out_10), .sel(not_1_out));
  Multiplexer #(.width(32), .enable("false")) multiplexer_20 (
    .in0(multiplexer_7_out), .in1({32{1'b0}}), .out(out_11), .sel(not_1_out));
  Multiplexer #(.width(32), .enable("false")) multiplexer_21 (
    .in0(multiplexer_8_out), .in1({32{1'b0}}), .out(out_12), .sel(not_1_out));
  Multiplexer #(.width(32), .enable("false")) multiplexer_22 (
    .in0(multiplexer_9_out), .in1({32{1'b0}}), .out(out_13), .sel(not_1_out));
  Multiplexer #(.width(32), .enable("false")) multiplexer_23 (
    .in0(multiplexer_10_out), .in1({32{1'b0}}), .out(out_14), .sel(not_1_out));
  Multiplexer #(.width(32), .enable("false")) multiplexer_24 (
    .in0(multiplexer_11_out), .in1({32{1'b0}}), .out(out_15), .sel(not_1_out));
  Multiplexer #(.width(32), .enable("false")) multiplexer_25 (
    .in0(multiplexer_12_out), .in1({32{1'b0}}), .out(out_16), .sel(not_1_out));
  Multiplexer #(.width(32), .enable("false")) multiplexer_26 (
    .in0(multiplexer_13_out), .in1({32{1'b0}}), .out(out_17), .sel(not_1_out));
  DotMatrix #(.matrixcols(32), .matrixrows(32)) dotmatrix_1 (
    .col0(out_5), .col1(out_6), .col2(out_7), .col3(out_8), .col4(out_9), .col5(out_10), .col6(out_11),
    .col7(out_12), .col8(out_13), .col9(out_14), .col10(out_15), .col11(out_16), .col12(out_17),
    .col13({32{1'b0}}), .col14({32{1'b0}}), .col15({32{1'b0}}), .col16({32{1'b0}}), .col17({32{1'b0}}),
    .col18({32{1'b0}}), .col19({32{1'b0}}), .col20({32{1'b0}}), .col21({32{1'b0}}), .col22({32{1'b0}}),
    .col23({32{1'b0}}), .col24({32{1'b0}}), .col25({32{1'b0}}), .col26({32{1'b0}}), .col27({32{1'b0}}),
    .col28({32{1'b0}}), .col29({32{1'b0}}), .col30({32{1'b0}}), .col31({32{1'b0}}));
  DotMatrix #(.matrixcols(32), .matrixrows(32)) dotmatrix_2 (
    .col0({32{1'b0}}), .col1({32{1'b0}}), .col2({32{1'b0}}), .col3({32{1'b0}}), .col4({32{1'b0}}),
    .col5({32{1'b0}}), .col6({32{1'b0}}), .col7({32{1'b0}}), .col8({32{1'b0}}), .col9({32{1'b0}}),
    .col10({32{1'b0}}), .col11({32{1'b0}}), .col12({32{1'b0}}), .col13({32{1'b0}}), .col14({32{1'b0}}),
    .col15({32{1'b0}}), .col16({32{1'b0}}), .col17({32{1'b0}}), .col18({32{1'b0}}), .col19({32{1'b0}}),
    .col20({32{1'b0}}), .col21({32{1'b0}}), .col22({32{1'b0}}), .col23({32{1'b0}}), .col24({32{1'b0}}),
    .col25({32{1'b0}}), .col26({32{1'b0}}), .col27({32{1'b0}}), .col28({32{1'b0}}), .col29({32{1'b0}}),
    .col30({32{1'b0}}), .col31({32{1'b0}}));
endmodule

module \σοσ  (
  input  [31:0] in_1,
  output [31:0] out_2,
  output [31:0] out_3,
  output [31:0] out_4,
  output [31:0] out_5,
  output [31:0] out_6,
  output [31:0] out_7,
  output [31:0] out_8,
  output [31:0] out_9,
  output [31:0] out_10,
  output [31:0] out_11,
  output [31:0] out_12,
  output [31:0] out_13,
  output [31:0] out_14,
  output [31:0] out_15,
  output [31:0] out_16,
  output [31:0] out_17,
  output [31:0] out_18,
  output [31:0] out_19,
  output [31:0] out_20,
  output [31:0] out_21,
  output [31:0] out_22,
  output [31:0] out_23,
  output [31:0] out_24,
  output [31:0] out_25,
  output [31:0] out_26,
  output [31:0] out_27,
  output [31:0] out_28,
  output [31:0] out_29,
  output [31:0] out_30,
  output [31:0] out_31,
  output [31:0] out_32,
  output [31:0] out_33
);

  Multiplier #(.width(32)) multiplier_1 (.a(in_1), .b(32'h2), .out(out_3));  // open: cin, cout
  Multiplier #(.width(32)) multiplier_2 (.a(out_3), .b(32'h2), .out(out_4));  // open: cin, cout
  Multiplier #(.width(32)) multiplier_3 (.a(out_4), .b(32'h2), .out(out_5));  // open: cin, cout
  Multiplier #(.width(32)) multiplier_4 (.a(out_5), .b(32'h2), .out(out_6));  // open: cin, cout
  Multiplier #(.width(32)) multiplier_5 (.a(out_6), .b(32'h2), .out(out_7));  // open: cin, cout
  Multiplier #(.width(32)) multiplier_6 (.a(out_7), .b(32'h2), .out(out_8));  // open: cin, cout
  Multiplier #(.width(32)) multiplier_7 (.a(out_8), .b(32'h2), .out(out_9));  // open: cin, cout
  Multiplier #(.width(32)) multiplier_8 (.a(out_9), .b(32'h2), .out(out_10));  // open: cin, cout
  Multiplier #(.width(32)) multiplier_9 (.a(out_10), .b(32'h2), .out(out_11));  // open: cin, cout
  Multiplier #(.width(32)) multiplier_10 (.a(out_11), .b(32'h2), .out(out_12));  // open: cin, cout
  Multiplier #(.width(32)) multiplier_11 (.a(out_12), .b(32'h2), .out(out_13));  // open: cin, cout
  Multiplier #(.width(32)) multiplier_12 (.a(out_13), .b(32'h2), .out(out_14));  // open: cin, cout
  Multiplier #(.width(32)) multiplier_13 (.a(out_14), .b(32'h2), .out(out_15));  // open: cin, cout
  Multiplier #(.width(32)) multiplier_14 (.a(out_15), .b(32'h2), .out(out_16));  // open: cin, cout
  Multiplier #(.width(32)) multiplier_15 (.a(out_16), .b(32'h2), .out(out_17));  // open: cin, cout
  Multiplier #(.width(32)) multiplier_16 (.a(out_17), .b(32'h2), .out(out_18));  // open: cin, cout
  Multiplier #(.width(32)) multiplier_17 (.a(out_18), .b(32'h2), .out(out_19));  // open: cin, cout
  Multiplier #(.width(32)) multiplier_18 (.a(out_19), .b(32'h2), .out(out_20));  // open: cin, cout
  Multiplier #(.width(32)) multiplier_19 (.a(out_20), .b(32'h2), .out(out_21));  // open: cin, cout
  Multiplier #(.width(32)) multiplier_20 (.a(out_21), .b(32'h2), .out(out_22));  // open: cin, cout
  Multiplier #(.width(32)) multiplier_21 (.a(out_22), .b(32'h2), .out(out_23));  // open: cin, cout
  Multiplier #(.width(32)) multiplier_22 (.a(out_23), .b(32'h2), .out(out_24));  // open: cin, cout
  Multiplier #(.width(32)) multiplier_23 (.a(out_24), .b(32'h2), .out(out_25));  // open: cin, cout
  Multiplier #(.width(32)) multiplier_24 (.a(out_25), .b(32'h2), .out(out_26));  // open: cin, cout
  Multiplier #(.width(32)) multiplier_25 (.a(out_26), .b(32'h2), .out(out_27));  // open: cin, cout
  Multiplier #(.width(32)) multiplier_26 (.a(out_27), .b(32'h2), .out(out_28));  // open: cin, cout
  Multiplier #(.width(32)) multiplier_27 (.a(out_28), .b(32'h2), .out(out_29));  // open: cin, cout
  Multiplier #(.width(32)) multiplier_28 (.a(out_29), .b(32'h2), .out(out_30));  // open: cin, cout
  Multiplier #(.width(32)) multiplier_29 (.a(out_30), .b(32'h2), .out(out_31));  // open: cin, cout
  Multiplier #(.width(32)) multiplier_30 (.a(out_31), .b(32'h2), .out(out_32));  // open: cin, cout
  Multiplier #(.width(32)) multiplier_31 (.a(out_32), .b(32'h2), .out(out_33));  // open: cin, cout

  assign out_2 = in_1;
endmodule

module \_2_οθ  (
  input  in_1,
  input  in_2,
  input  in_3,
  input  in_4
);

  wire [31:0] \ε_1_out_5 , \ε_1_out_6 , \ε_1_out_7 , \ε_1_out_8 , \ε_1_out_9 , \ε_1_out_10 , \ε_1_out_11 ,
       \ε_1_out_12 , \ε_1_out_13 , \ε_1_out_14 , \ε_1_out_15 , \ε_1_out_16 , \ε_1_out_17 ;

  DotMatrix #(.matrixcols(32), .matrixrows(32)) dotmatrix_1 ();  // open: col0, col1, col2, col3, col4, col5, col6, col7, col8, col9, col10, col11, col12, col13, col14, col15, col16, col17, col18, col19, col20, col21, col22, col23, col24, col25, col26, col27, col28, col29, col30, col31
  DotMatrix #(.matrixcols(32), .matrixrows(32)) dotmatrix_2 (
    .col0(\ε_1_out_5 ), .col1(\ε_1_out_6 ), .col2(\ε_1_out_7 ), .col3(\ε_1_out_8 ), .col4(\ε_1_out_9 ),
    .col5(\ε_1_out_10 ), .col6(\ε_1_out_11 ), .col7(\ε_1_out_12 ), .col8(\ε_1_out_13 ), .col9(\ε_1_out_14 ),
    .col10(\ε_1_out_15 ), .col11(\ε_1_out_16 ), .col12(\ε_1_out_17 ));  // open: col13, col14, col15, col16, col17, col18, col19, col20, col21, col22, col23, col24, col25, col26, col27, col28, col29, col30, col31
  \ε  \u_ε_1  (
    .in_1(in_3), .in_2(in_2), .out_5(\ε_1_out_5 ), .out_6(\ε_1_out_6 ), .in_3(in_4), .out_7(\ε_1_out_7 ),
    .out_8(\ε_1_out_8 ), .out_9(\ε_1_out_9 ), .out_10(\ε_1_out_10 ), .out_11(\ε_1_out_11 ),
    .out_12(\ε_1_out_12 ), .out_13(\ε_1_out_13 ), .out_14(\ε_1_out_14 ), .out_15(\ε_1_out_15 ),
    .out_16(\ε_1_out_16 ), .out_17(\ε_1_out_17 ));  // open: out_4

  // Other names for the same wires on the sheet: klok = in_2; plus_or_minus = in_3; res = in_4; set = in_1
endmodule

module ep (
  input  in_1,
  input  [31:0] in_2,
  input  [31:0] in_3,
  input  [31:0] in_4,
  input  [31:0] in_5,
  input  [31:0] in_6,
  input  [31:0] in_7,
  input  [31:0] in_8,
  input  [31:0] in_9,
  input  [31:0] in_10,
  input  [31:0] in_11,
  input  [31:0] in_12,
  input  [31:0] in_13,
  input  [31:0] in_14,
  output [31:0] out_15,
  output [31:0] out_16,
  output [31:0] out_17,
  output [31:0] out_18,
  output [31:0] out_19,
  output [31:0] out_20,
  output [31:0] out_21,
  output [31:0] out_22,
  output [31:0] out_23,
  output [31:0] out_24,
  output [31:0] out_25,
  output [31:0] out_26,
  output [31:0] out_27
);

  Multiplexer #(.width(32), .enable("false")) multiplexer_1 (.in0(in_2), .in1({32{1'b0}}), .out(out_15), .sel(in_1));
  Multiplexer #(.width(32), .enable("false")) multiplexer_2 (.in0(in_3), .in1({32{1'b0}}), .out(out_16), .sel(in_1));
  Multiplexer #(.width(32), .enable("false")) multiplexer_3 (.in0(in_4), .in1({32{1'b0}}), .out(out_17), .sel(in_1));
  Multiplexer #(.width(32), .enable("false")) multiplexer_4 (.in0(in_5), .in1({32{1'b0}}), .out(out_18), .sel(in_1));
  Multiplexer #(.width(32), .enable("false")) multiplexer_5 (.in0(in_6), .in1({32{1'b0}}), .out(out_19), .sel(in_1));
  Multiplexer #(.width(32), .enable("false")) multiplexer_6 (.in0(in_7), .in1({32{1'b0}}), .out(out_20), .sel(in_1));
  Multiplexer #(.width(32), .enable("false")) multiplexer_7 (.in0(in_8), .in1({32{1'b0}}), .out(out_21), .sel(in_1));
  Multiplexer #(.width(32), .enable("false")) multiplexer_8 (.in0(in_9), .in1({32{1'b0}}), .out(out_22), .sel(in_1));
  Multiplexer #(.width(32), .enable("false")) multiplexer_9 (.in0(in_10), .in1({32{1'b0}}), .out(out_23), .sel(in_1));
  Multiplexer #(.width(32), .enable("false")) multiplexer_10 (.in0(in_11), .in1({32{1'b0}}), .out(out_24), .sel(in_1));
  Multiplexer #(.width(32), .enable("false")) multiplexer_11 (.in0(in_12), .in1({32{1'b0}}), .out(out_25), .sel(in_1));
  Multiplexer #(.width(32), .enable("false")) multiplexer_12 (.in0(in_13), .in1({32{1'b0}}), .out(out_26), .sel(in_1));
  Multiplexer #(.width(32), .enable("false")) multiplexer_13 (.in0(in_14), .in1({32{1'b0}}), .out(out_27), .sel(in_1));
endmodule

module _1 (
  input  in_1,
  input  [31:0] in_2,
  input  [31:0] in_3,
  input  [31:0] in_4,
  input  [31:0] in_5,
  input  [31:0] in_6,
  input  [31:0] in_7,
  input  [31:0] in_8,
  input  [31:0] in_9,
  input  [31:0] in_10,
  input  [31:0] in_11,
  input  [31:0] in_12,
  input  [31:0] in_13,
  input  [31:0] in_14,
  output [31:0] out_15,
  output [31:0] out_16,
  output [31:0] out_17,
  output [31:0] out_18,
  output [31:0] out_19,
  output [31:0] out_20,
  output [31:0] out_21,
  output [31:0] out_22,
  output [31:0] out_23,
  output [31:0] out_24,
  output [31:0] out_25,
  output [31:0] out_26,
  output [31:0] out_27
);

  Multiplexer #(.width(32), .enable("false")) multiplexer_1 (.in0(in_2), .in1({32{1'b0}}), .out(out_15), .sel(in_1));
  Multiplexer #(.width(32), .enable("false")) multiplexer_2 (.in0(in_3), .in1({32{1'b0}}), .out(out_16), .sel(in_1));
  Multiplexer #(.width(32), .enable("false")) multiplexer_3 (.in0(in_4), .in1({32{1'b0}}), .out(out_17), .sel(in_1));
  Multiplexer #(.width(32), .enable("false")) multiplexer_4 (.in0(in_5), .in1(32'h1), .out(out_18), .sel(in_1));
  Multiplexer #(.width(32), .enable("false")) multiplexer_5 (.in0(in_6), .in1(32'h1), .out(out_19), .sel(in_1));
  Multiplexer #(.width(32), .enable("false")) multiplexer_6 (.in0(in_7), .in1(32'h1), .out(out_20), .sel(in_1));
  Multiplexer #(.width(32), .enable("false")) multiplexer_7 (.in0(in_8), .in1({32{1'b0}}), .out(out_21), .sel(in_1));
  Multiplexer #(.width(32), .enable("false")) multiplexer_8 (.in0(in_9), .in1({32{1'b0}}), .out(out_22), .sel(in_1));
  Multiplexer #(.width(32), .enable("false")) multiplexer_9 (.in0(in_10), .in1({32{1'b0}}), .out(out_23), .sel(in_1));
  Multiplexer #(.width(32), .enable("false")) multiplexer_10 (.in0(in_11), .in1({32{1'b0}}), .out(out_24), .sel(in_1));
  Multiplexer #(.width(32), .enable("false")) multiplexer_11 (.in0(in_12), .in1({32{1'b0}}), .out(out_25), .sel(in_1));
  Multiplexer #(.width(32), .enable("false")) multiplexer_12 (.in0(in_13), .in1({32{1'b0}}), .out(out_26), .sel(in_1));
  Multiplexer #(.width(32), .enable("false")) multiplexer_13 (.in0(in_14), .in1({32{1'b0}}), .out(out_27), .sel(in_1));
endmodule

module _2 (
  input  in_1,
  input  [31:0] in_2,
  input  [31:0] in_3,
  input  [31:0] in_4,
  input  [31:0] in_5,
  input  [31:0] in_6,
  input  [31:0] in_7,
  input  [31:0] in_8,
  input  [31:0] in_9,
  input  [31:0] in_10,
  input  [31:0] in_11,
  input  [31:0] in_12,
  input  [31:0] in_13,
  input  [31:0] in_14,
  output [31:0] out_15,
  output [31:0] out_16,
  output [31:0] out_17,
  output [31:0] out_18,
  output [31:0] out_19,
  output [31:0] out_20,
  output [31:0] out_21,
  output [31:0] out_22,
  output [31:0] out_23,
  output [31:0] out_24,
  output [31:0] out_25,
  output [31:0] out_26,
  output [31:0] out_27
);

  Multiplexer #(.width(32), .enable("false")) multiplexer_1 (.in0(in_2), .in1({32{1'b0}}), .out(out_15), .sel(in_1));
  Multiplexer #(.width(32), .enable("false")) multiplexer_2 (.in0(in_3), .in1(32'h1), .out(out_16), .sel(in_1));
  Multiplexer #(.width(32), .enable("false")) multiplexer_3 (.in0(in_4), .in1(32'h1), .out(out_17), .sel(in_1));
  Multiplexer #(.width(32), .enable("false")) multiplexer_4 (.in0(in_5), .in1(32'h3), .out(out_18), .sel(in_1));
  Multiplexer #(.width(32), .enable("false")) multiplexer_5 (.in0(in_6), .in1(32'h3), .out(out_19), .sel(in_1));
  Multiplexer #(.width(32), .enable("false")) multiplexer_6 (.in0(in_7), .in1(32'h3), .out(out_20), .sel(in_1));
  Multiplexer #(.width(32), .enable("false")) multiplexer_7 (.in0(in_8), .in1(32'h1), .out(out_21), .sel(in_1));
  Multiplexer #(.width(32), .enable("false")) multiplexer_8 (.in0(in_9), .in1(32'h1), .out(out_22), .sel(in_1));
  Multiplexer #(.width(32), .enable("false")) multiplexer_9 (.in0(in_10), .in1({32{1'b0}}), .out(out_23), .sel(in_1));
  Multiplexer #(.width(32), .enable("false")) multiplexer_10 (.in0(in_11), .in1({32{1'b0}}), .out(out_24), .sel(in_1));
  Multiplexer #(.width(32), .enable("false")) multiplexer_11 (.in0(in_12), .in1({32{1'b0}}), .out(out_25), .sel(in_1));
  Multiplexer #(.width(32), .enable("false")) multiplexer_12 (.in0(in_13), .in1({32{1'b0}}), .out(out_26), .sel(in_1));
  Multiplexer #(.width(32), .enable("false")) multiplexer_13 (.in0(in_14), .in1({32{1'b0}}), .out(out_27), .sel(in_1));
endmodule

module _3 (
  input  in_1,
  input  [31:0] in_2,
  input  [31:0] in_3,
  input  [31:0] in_4,
  input  [31:0] in_5,
  input  [31:0] in_6,
  input  [31:0] in_7,
  input  [31:0] in_8,
  input  [31:0] in_9,
  input  [31:0] in_10,
  input  [31:0] in_11,
  input  [31:0] in_12,
  input  [31:0] in_13,
  input  [31:0] in_14,
  output [31:0] out_15,
  output [31:0] out_16,
  output [31:0] out_17,
  output [31:0] out_18,
  output [31:0] out_19,
  output [31:0] out_20,
  output [31:0] out_21,
  output [31:0] out_22,
  output [31:0] out_23,
  output [31:0] out_24,
  output [31:0] out_25,
  output [31:0] out_26,
  output [31:0] out_27
);

  Multiplexer #(.width(32), .enable("false")) multiplexer_1 (.in0(in_2), .in1({32{1'b0}}), .out(out_15), .sel(in_1));
  Multiplexer #(.width(32), .enable("false")) multiplexer_2 (.in0(in_3), .in1(32'h3), .out(out_16), .sel(in_1));
  Multiplexer #(.width(32), .enable("false")) multiplexer_3 (.in0(in_4), .in1(32'h2), .out(out_17), .sel(in_1));
  Multiplexer #(.width(32), .enable("false")) multiplexer_4 (.in0(in_5), .in1(32'h6), .out(out_18), .sel(in_1));
  Multiplexer #(.width(32), .enable("false")) multiplexer_5 (.in0(in_6), .in1(32'h6), .out(out_19), .sel(in_1));
  Multiplexer #(.width(32), .enable("false")) multiplexer_6 (.in0(in_7), .in1(32'h6), .out(out_20), .sel(in_1));
  Multiplexer #(.width(32), .enable("false")) multiplexer_7 (.in0(in_8), .in1(32'h2), .out(out_21), .sel(in_1));
  Multiplexer #(.width(32), .enable("false")) multiplexer_8 (.in0(in_9), .in1(32'h3), .out(out_22), .sel(in_1));
  Multiplexer #(.width(32), .enable("false")) multiplexer_9 (.in0(in_10), .in1({32{1'b0}}), .out(out_23), .sel(in_1));
  Multiplexer #(.width(32), .enable("false")) multiplexer_10 (.in0(in_11), .in1({32{1'b0}}), .out(out_24), .sel(in_1));
  Multiplexer #(.width(32), .enable("false")) multiplexer_11 (.in0(in_12), .in1(32'h1), .out(out_25), .sel(in_1));
  Multiplexer #(.width(32), .enable("false")) multiplexer_12 (.in0(in_13), .in1(32'h1), .out(out_26), .sel(in_1));
  Multiplexer #(.width(32), .enable("false")) multiplexer_13 (.in0(in_14), .in1(32'h1), .out(out_27), .sel(in_1));
endmodule

module _4 (
  input  in_1,
  input  [31:0] in_2,
  input  [31:0] in_3,
  input  [31:0] in_4,
  input  [31:0] in_5,
  input  [31:0] in_6,
  input  [31:0] in_7,
  input  [31:0] in_8,
  input  [31:0] in_9,
  input  [31:0] in_10,
  input  [31:0] in_11,
  input  [31:0] in_12,
  input  [31:0] in_13,
  input  [31:0] in_14,
  output [31:0] out_15,
  output [31:0] out_16,
  output [31:0] out_17,
  output [31:0] out_18,
  output [31:0] out_19,
  output [31:0] out_20,
  output [31:0] out_21,
  output [31:0] out_22,
  output [31:0] out_23,
  output [31:0] out_24,
  output [31:0] out_25,
  output [31:0] out_26,
  output [31:0] out_27
);

  Multiplexer #(.width(32), .enable("false")) multiplexer_1 (.in0(in_2), .in1({32{1'b0}}), .out(out_15), .sel(in_1));
  Multiplexer #(.width(32), .enable("false")) multiplexer_2 (.in0(in_3), .in1(32'h7), .out(out_16), .sel(in_1));
  Multiplexer #(.width(32), .enable("false")) multiplexer_3 (.in0(in_4), .in1(32'h4), .out(out_17), .sel(in_1));
  Multiplexer #(.width(32), .enable("false")) multiplexer_4 (.in0(in_5), .in1(32'hc), .out(out_18), .sel(in_1));
  Multiplexer #(.width(32), .enable("false")) multiplexer_5 (.in0(in_6), .in1(32'hd), .out(out_19), .sel(in_1));
  Multiplexer #(.width(32), .enable("false")) multiplexer_6 (.in0(in_7), .in1(32'hd), .out(out_20), .sel(in_1));
  Multiplexer #(.width(32), .enable("false")) multiplexer_7 (.in0(in_8), .in1(32'h5), .out(out_21), .sel(in_1));
  Multiplexer #(.width(32), .enable("false")) multiplexer_8 (.in0(in_9), .in1(32'h7), .out(out_22), .sel(in_1));
  Multiplexer #(.width(32), .enable("false")) multiplexer_9 (.in0(in_10), .in1(32'h1), .out(out_23), .sel(in_1));
  Multiplexer #(.width(32), .enable("false")) multiplexer_10 (.in0(in_11), .in1(32'h1), .out(out_24), .sel(in_1));
  Multiplexer #(.width(32), .enable("false")) multiplexer_11 (.in0(in_12), .in1(32'h3), .out(out_25), .sel(in_1));
  Multiplexer #(.width(32), .enable("false")) multiplexer_12 (.in0(in_13), .in1(32'h2), .out(out_26), .sel(in_1));
  Multiplexer #(.width(32), .enable("false")) multiplexer_13 (.in0(in_14), .in1(32'h3), .out(out_27), .sel(in_1));
endmodule

module _5 (
  input  in_1,
  input  [31:0] in_2,
  input  [31:0] in_3,
  input  [31:0] in_4,
  input  [31:0] in_5,
  input  [31:0] in_6,
  input  [31:0] in_7,
  input  [31:0] in_8,
  input  [31:0] in_9,
  input  [31:0] in_10,
  input  [31:0] in_11,
  input  [31:0] in_12,
  input  [31:0] in_13,
  input  [31:0] in_14,
  output [31:0] out_15,
  output [31:0] out_16,
  output [31:0] out_17,
  output [31:0] out_18,
  output [31:0] out_19,
  output [31:0] out_20,
  output [31:0] out_21,
  output [31:0] out_22,
  output [31:0] out_23,
  output [31:0] out_24,
  output [31:0] out_25,
  output [31:0] out_26,
  output [31:0] out_27
);

  Multiplexer #(.width(32), .enable("false")) multiplexer_1 (.in0(in_2), .in1({32{1'b0}}), .out(out_15), .sel(in_1));
  Multiplexer #(.width(32), .enable("false")) multiplexer_2 (.in0(in_3), .in1(32'hf), .out(out_16), .sel(in_1));
  Multiplexer #(.width(32), .enable("false")) multiplexer_3 (.in0(in_4), .in1(32'h8), .out(out_17), .sel(in_1));
  Multiplexer #(.width(32), .enable("false")) multiplexer_4 (.in0(in_5), .in1(32'h18), .out(out_18), .sel(in_1));
  Multiplexer #(.width(32), .enable("false")) multiplexer_5 (.in0(in_6), .in1(32'h1a), .out(out_19), .sel(in_1));
  Multiplexer #(.width(32), .enable("false")) multiplexer_6 (.in0(in_7), .in1(32'h1a), .out(out_20), .sel(in_1));
  Multiplexer #(.width(32), .enable("false")) multiplexer_7 (.in0(in_8), .in1(32'ha), .out(out_21), .sel(in_1));
  Multiplexer #(.width(32), .enable("false")) multiplexer_8 (.in0(in_9), .in1(32'hf), .out(out_22), .sel(in_1));
  Multiplexer #(.width(32), .enable("false")) multiplexer_9 (.in0(in_10), .in1(32'h2), .out(out_23), .sel(in_1));
  Multiplexer #(.width(32), .enable("false")) multiplexer_10 (.in0(in_11), .in1(32'h2), .out(out_24), .sel(in_1));
  Multiplexer #(.width(32), .enable("false")) multiplexer_11 (.in0(in_12), .in1(32'h7), .out(out_25), .sel(in_1));
  Multiplexer #(.width(32), .enable("false")) multiplexer_12 (.in0(in_13), .in1(32'h5), .out(out_26), .sel(in_1));
  Multiplexer #(.width(32), .enable("false")) multiplexer_13 (.in0(in_14), .in1(32'h7), .out(out_27), .sel(in_1));
endmodule

module _6 (
  input  in_1,
  input  [31:0] in_2,
  input  [31:0] in_3,
  input  [31:0] in_4,
  input  [31:0] in_5,
  input  [31:0] in_6,
  input  [31:0] in_7,
  input  [31:0] in_8,
  input  [31:0] in_9,
  input  [31:0] in_10,
  input  [31:0] in_11,
  input  [31:0] in_12,
  input  [31:0] in_13,
  input  [31:0] in_14,
  output [31:0] out_15,
  output [31:0] out_16,
  output [31:0] out_17,
  output [31:0] out_18,
  output [31:0] out_19,
  output [31:0] out_20,
  output [31:0] out_21,
  output [31:0] out_22,
  output [31:0] out_23,
  output [31:0] out_24,
  output [31:0] out_25,
  output [31:0] out_26,
  output [31:0] out_27
);

  Multiplexer #(.width(32), .enable("false")) multiplexer_1 (.in0(in_2), .in1(32'h1), .out(out_15), .sel(in_1));
  Multiplexer #(.width(32), .enable("false")) multiplexer_2 (.in0(in_3), .in1(32'h1f), .out(out_16), .sel(in_1));
  Multiplexer #(.width(32), .enable("false")) multiplexer_3 (.in0(in_4), .in1(32'h11), .out(out_17), .sel(in_1));
  Multiplexer #(.width(32), .enable("false")) multiplexer_4 (.in0(in_5), .in1(32'h31), .out(out_18), .sel(in_1));
  Multiplexer #(.width(32), .enable("false")) multiplexer_5 (.in0(in_6), .in1(32'h35), .out(out_19), .sel(in_1));
  Multiplexer #(.width(32), .enable("false")) multiplexer_6 (.in0(in_7), .in1(32'h35), .out(out_20), .sel(in_1));
  Multiplexer #(.width(32), .enable("false")) multiplexer_7 (.in0(in_8), .in1(32'h15), .out(out_21), .sel(in_1));
  Multiplexer #(.width(32), .enable("false")) multiplexer_8 (.in0(in_9), .in1(32'h1f), .out(out_22), .sel(in_1));
  Multiplexer #(.width(32), .enable("false")) multiplexer_9 (.in0(in_10), .in1(32'h5), .out(out_23), .sel(in_1));
  Multiplexer #(.width(32), .enable("false")) multiplexer_10 (.in0(in_11), .in1(32'h4), .out(out_24), .sel(in_1));
  Multiplexer #(.width(32), .enable("false")) multiplexer_11 (.in0(in_12), .in1(32'he), .out(out_25), .sel(in_1));
  Multiplexer #(.width(32), .enable("false")) multiplexer_12 (.in0(in_13), .in1(32'ha), .out(out_26), .sel(in_1));
  Multiplexer #(.width(32), .enable("false")) multiplexer_13 (.in0(in_14), .in1(32'he), .out(out_27), .sel(in_1));
endmodule

module _7 (
  input  in_1,
  input  [31:0] in_2,
  input  [31:0] in_3,
  input  [31:0] in_4,
  input  [31:0] in_5,
  input  [31:0] in_6,
  input  [31:0] in_7,
  input  [31:0] in_8,
  input  [31:0] in_9,
  input  [31:0] in_10,
  input  [31:0] in_11,
  input  [31:0] in_12,
  input  [31:0] in_13,
  input  [31:0] in_14,
  output [31:0] out_15,
  output [31:0] out_16,
  output [31:0] out_17,
  output [31:0] out_18,
  output [31:0] out_19,
  output [31:0] out_20,
  output [31:0] out_21,
  output [31:0] out_22,
  output [31:0] out_23,
  output [31:0] out_24,
  output [31:0] out_25,
  output [31:0] out_26,
  output [31:0] out_27
);

  Multiplexer #(.width(32), .enable("false")) multiplexer_1 (.in0(in_2), .in1(32'h3), .out(out_15), .sel(in_1));
  Multiplexer #(.width(32), .enable("false")) multiplexer_2 (.in0(in_3), .in1(32'h3e), .out(out_16), .sel(in_1));
  Multiplexer #(.width(32), .enable("false")) multiplexer_3 (.in0(in_4), .in1(32'h22), .out(out_17), .sel(in_1));
  Multiplexer #(.width(32), .enable("false")) multiplexer_4 (.in0(in_5), .in1(32'h62), .out(out_18), .sel(in_1));
  Multiplexer #(.width(32), .enable("false")) multiplexer_5 (.in0(in_6), .in1(32'h6a), .out(out_19), .sel(in_1));
  Multiplexer #(.width(32), .enable("false")) multiplexer_6 (.in0(in_7), .in1(32'h6a), .out(out_20), .sel(in_1));
  Multiplexer #(.width(32), .enable("false")) multiplexer_7 (.in0(in_8), .in1(32'h2a), .out(out_21), .sel(in_1));
  Multiplexer #(.width(32), .enable("false")) multiplexer_8 (.in0(in_9), .in1(32'h3e), .out(out_22), .sel(in_1));
  Multiplexer #(.width(32), .enable("false")) multiplexer_9 (.in0(in_10), .in1(32'hb), .out(out_23), .sel(in_1));
  Multiplexer #(.width(32), .enable("false")) multiplexer_10 (.in0(in_11), .in1(32'h8), .out(out_24), .sel(in_1));
  Multiplexer #(.width(32), .enable("false")) multiplexer_11 (.in0(in_12), .in1(32'h1c), .out(out_25), .sel(in_1));
  Multiplexer #(.width(32), .enable("false")) multiplexer_12 (.in0(in_13), .in1(32'h14), .out(out_26), .sel(in_1));
  Multiplexer #(.width(32), .enable("false")) multiplexer_13 (.in0(in_14), .in1(32'h1c), .out(out_27), .sel(in_1));
endmodule

module _8 (
  input  in_1,
  input  [31:0] in_2,
  input  [31:0] in_3,
  input  [31:0] in_4,
  input  [31:0] in_5,
  input  [31:0] in_6,
  input  [31:0] in_7,
  input  [31:0] in_8,
  input  [31:0] in_9,
  input  [31:0] in_10,
  input  [31:0] in_11,
  input  [31:0] in_12,
  input  [31:0] in_13,
  input  [31:0] in_14,
  output [31:0] out_15,
  output [31:0] out_16,
  output [31:0] out_17,
  output [31:0] out_18,
  output [31:0] out_19,
  output [31:0] out_20,
  output [31:0] out_21,
  output [31:0] out_22,
  output [31:0] out_23,
  output [31:0] out_24,
  output [31:0] out_25,
  output [31:0] out_26,
  output [31:0] out_27
);

  wire [31:0] multiplier_1_out, multiplier_2_out, multiplier_3_out, multiplier_4_out, multiplier_5_out,
       multiplier_6_out, multiplier_7_out, multiplier_8_out, multiplier_9_out, multiplier_10_out,
       multiplier_11_out, multiplier_12_out, multiplier_13_out;

  Multiplier #(.width(32)) multiplier_1 (.a(32'h3), .b(32'h2), .out(multiplier_1_out), .cin(32'h1));  // open: cout
  Multiplier #(.width(32)) multiplier_2 (.a(32'h3e), .b(32'h2), .out(multiplier_2_out));  // open: cin, cout
  Multiplier #(.width(32)) multiplier_3 (.a(32'h22), .b(32'h2), .out(multiplier_3_out), .cin(32'h1));  // open: cout
  Multiplier #(.width(32)) multiplier_4 (.a(32'h62), .b(32'h2), .out(multiplier_4_out));  // open: cin, cout
  Multiplier #(.width(32)) multiplier_5 (.a(32'h6a), .b(32'h2), .out(multiplier_5_out), .cin(32'h1));  // open: cout
  Multiplier #(.width(32)) multiplier_6 (.a(32'h6a), .b(32'h2), .out(multiplier_6_out));  // open: cin, cout
  Multiplier #(.width(32)) multiplier_7 (.a(32'h2a), .b(32'h2), .out(multiplier_7_out), .cin(32'h1));  // open: cout
  Multiplier #(.width(32)) multiplier_8 (.a(32'h3e), .b(32'h2), .out(multiplier_8_out));  // open: cin, cout
  Multiplier #(.width(32)) multiplier_9 (.a(32'hb), .b(32'h2), .out(multiplier_9_out), .cin(32'h1));  // open: cout
  Multiplier #(.width(32)) multiplier_10 (.a(32'h8), .b(32'h2), .out(multiplier_10_out));  // open: cin, cout
  Multiplier #(.width(32)) multiplier_11 (.a(32'h1c), .b(32'h2), .out(multiplier_11_out));  // open: cin, cout
  Multiplier #(.width(32)) multiplier_12 (.a(32'h14), .b(32'h2), .out(multiplier_12_out));  // open: cin, cout
  Multiplier #(.width(32)) multiplier_13 (.a(32'h1c), .b(32'h2), .out(multiplier_13_out));  // open: cin, cout
  Multiplexer #(.width(32), .enable("false")) multiplexer_1 (
    .in0(in_2), .in1(multiplier_1_out), .out(out_15), .sel(in_1));
  Multiplexer #(.width(32), .enable("false")) multiplexer_2 (
    .in0(in_3), .in1(multiplier_2_out), .out(out_16), .sel(in_1));
  Multiplexer #(.width(32), .enable("false")) multiplexer_3 (
    .in0(in_4), .in1(multiplier_3_out), .out(out_17), .sel(in_1));
  Multiplexer #(.width(32), .enable("false")) multiplexer_4 (
    .in0(in_5), .in1(multiplier_4_out), .out(out_18), .sel(in_1));
  Multiplexer #(.width(32), .enable("false")) multiplexer_5 (
    .in0(in_6), .in1(multiplier_5_out), .out(out_19), .sel(in_1));
  Multiplexer #(.width(32), .enable("false")) multiplexer_6 (
    .in0(in_7), .in1(multiplier_6_out), .out(out_20), .sel(in_1));
  Multiplexer #(.width(32), .enable("false")) multiplexer_7 (
    .in0(in_8), .in1(multiplier_7_out), .out(out_21), .sel(in_1));
  Multiplexer #(.width(32), .enable("false")) multiplexer_8 (
    .in0(in_9), .in1(multiplier_8_out), .out(out_22), .sel(in_1));
  Multiplexer #(.width(32), .enable("false")) multiplexer_9 (
    .in0(in_10), .in1(multiplier_9_out), .out(out_23), .sel(in_1));
  Multiplexer #(.width(32), .enable("false")) multiplexer_10 (
    .in0(in_11), .in1(multiplier_10_out), .out(out_24), .sel(in_1));
  Multiplexer #(.width(32), .enable("false")) multiplexer_11 (
    .in0(in_12), .in1(multiplier_11_out), .out(out_25), .sel(in_1));
  Multiplexer #(.width(32), .enable("false")) multiplexer_12 (
    .in0(in_13), .in1(multiplier_12_out), .out(out_26), .sel(in_1));
  Multiplexer #(.width(32), .enable("false")) multiplexer_13 (
    .in0(in_14), .in1(multiplier_13_out), .out(out_27), .sel(in_1));
endmodule

module _9 (
  input  [31:0] in_1,
  input  [31:0] in_2,
  input  [31:0] in_3,
  input  [31:0] in_4,
  input  [31:0] in_5,
  input  [31:0] in_6,
  input  [31:0] in_7,
  input  [31:0] in_8,
  input  in_9,
  input  [31:0] in_10,
  input  [31:0] in_11,
  input  [31:0] in_12,
  input  [31:0] in_13,
  input  [31:0] in_14,
  output [31:0] out_15,
  output [31:0] out_16,
  output [31:0] out_17,
  output [31:0] out_18,
  output [31:0] out_19,
  output [31:0] out_20,
  output [31:0] out_21,
  output [31:0] out_22,
  output [31:0] out_23,
  output [31:0] out_24,
  output [31:0] out_25,
  output [31:0] out_26,
  output [31:0] out_27
);

  wire [31:0] multiplier_1_out, multiplier_2_out, multiplier_3_out, multiplier_4_out, multiplier_5_out,
       multiplier_6_out, multiplier_7_out, multiplier_8_out, multiplier_9_out, multiplier_10_out,
       multiplier_11_out, multiplier_12_out, multiplier_13_out, n8_1_out_15, n8_1_out_16, n8_1_out_17,
       n8_1_out_18, n8_1_out_19, n8_1_out_20, n8_1_out_21, n8_1_out_22, n8_1_out_23, n8_1_out_24,
       n8_1_out_25, n8_1_out_26, n8_1_out_27;

  _8 u_8_1 (
    .in_2(in_1), .in_3(in_2), .in_4(in_3), .in_5(in_4), .in_6(in_5), .in_7(in_6), .in_8(in_7), .in_9(in_8),
    .in_10(in_10), .in_11(in_11), .in_12(in_12), .in_13(in_13), .in_14(in_14), .out_15(n8_1_out_15),
    .out_16(n8_1_out_16), .out_17(n8_1_out_17), .out_18(n8_1_out_18), .out_19(n8_1_out_19),
    .out_20(n8_1_out_20), .out_21(n8_1_out_21), .out_22(n8_1_out_22), .out_23(n8_1_out_23),
    .out_24(n8_1_out_24), .out_25(n8_1_out_25), .out_26(n8_1_out_26), .out_27(n8_1_out_27), .in_1(in_9));
  Multiplier #(.width(32)) multiplier_1 (.a(n8_1_out_27), .b(32'h2), .out(multiplier_1_out));  // open: cin, cout
  Multiplier #(.width(32)) multiplier_2 (.a(n8_1_out_26), .b(32'h2), .out(multiplier_2_out));  // open: cin, cout
  Multiplier #(.width(32)) multiplier_3 (.a(n8_1_out_25), .b(32'h2), .out(multiplier_3_out));  // open: cin, cout
  Multiplier #(.width(32)) multiplier_4 (.a(n8_1_out_24), .b(32'h2), .out(multiplier_4_out));  // open: cin, cout
  Multiplier #(.width(32)) multiplier_5 (
    .a(n8_1_out_23), .b(32'h2), .out(multiplier_5_out), .cin(32'h1));  // open: cout
  Multiplier #(.width(32)) multiplier_6 (.a(n8_1_out_22), .b(32'h2), .out(multiplier_6_out));  // open: cin, cout
  Multiplier #(.width(32)) multiplier_7 (.a(n8_1_out_21), .b(32'h2), .out(multiplier_7_out));  // open: cin, cout
  Multiplier #(.width(32)) multiplier_8 (.a(n8_1_out_20), .b(32'h2), .out(multiplier_8_out));  // open: cin, cout
  Multiplier #(.width(32)) multiplier_9 (.a(n8_1_out_19), .b(32'h2), .out(multiplier_9_out));  // open: cin, cout
  Multiplier #(.width(32)) multiplier_10 (.a(n8_1_out_18), .b(32'h2), .out(multiplier_10_out));  // open: cin, cout
  Multiplier #(.width(32)) multiplier_11 (.a(n8_1_out_17), .b(32'h2), .out(multiplier_11_out));  // open: cin, cout
  Multiplier #(.width(32)) multiplier_12 (.a(n8_1_out_16), .b(32'h2), .out(multiplier_12_out));  // open: cin, cout
  Multiplier #(.width(32)) multiplier_13 (
    .a(n8_1_out_15), .b(32'h2), .out(multiplier_13_out), .cin(32'h1));  // open: cout
  Multiplexer #(.width(32), .enable("false")) multiplexer_1 (
    .in0(in_1), .in1(multiplier_13_out), .out(out_15), .sel(in_9));
  Multiplexer #(.width(32), .enable("false")) multiplexer_2 (
    .in0(in_2), .in1(multiplier_12_out), .out(out_16), .sel(in_9));
  Multiplexer #(.width(32), .enable("false")) multiplexer_3 (
    .in0(in_3), .in1(multiplier_11_out), .out(out_17), .sel(in_9));
  Multiplexer #(.width(32), .enable("false")) multiplexer_4 (
    .in0(in_4), .in1(multiplier_10_out), .out(out_18), .sel(in_9));
  Multiplexer #(.width(32), .enable("false")) multiplexer_5 (
    .in0(in_5), .in1(multiplier_9_out), .out(out_19), .sel(in_9));
  Multiplexer #(.width(32), .enable("false")) multiplexer_6 (
    .in0(in_6), .in1(multiplier_8_out), .out(out_20), .sel(in_9));
  Multiplexer #(.width(32), .enable("false")) multiplexer_7 (
    .in0(in_7), .in1(multiplier_7_out), .out(out_21), .sel(in_9));
  Multiplexer #(.width(32), .enable("false")) multiplexer_8 (
    .in0(in_8), .in1(multiplier_6_out), .out(out_22), .sel(in_9));
  Multiplexer #(.width(32), .enable("false")) multiplexer_9 (
    .in0(in_10), .in1(multiplier_5_out), .out(out_23), .sel(in_9));
  Multiplexer #(.width(32), .enable("false")) multiplexer_10 (
    .in0(in_11), .in1(multiplier_4_out), .out(out_24), .sel(in_9));
  Multiplexer #(.width(32), .enable("false")) multiplexer_11 (
    .in0(in_12), .in1(multiplier_3_out), .out(out_25), .sel(in_9));
  Multiplexer #(.width(32), .enable("false")) multiplexer_12 (
    .in0(in_13), .in1(multiplier_2_out), .out(out_26), .sel(in_9));
  Multiplexer #(.width(32), .enable("false")) multiplexer_13 (
    .in0(in_14), .in1(multiplier_1_out), .out(out_27), .sel(in_9));
endmodule

module _10 (
  input  in_1,
  input  [31:0] in_2,
  input  [31:0] in_3,
  input  [31:0] in_4,
  input  [31:0] in_5,
  input  [31:0] in_6,
  input  [31:0] in_7,
  input  [31:0] in_8,
  input  [31:0] in_9,
  input  [31:0] in_10,
  input  [31:0] in_11,
  input  [31:0] in_12,
  input  [31:0] in_13,
  input  [31:0] in_14,
  output [31:0] out_15,
  output [31:0] out_16,
  output [31:0] out_17,
  output [31:0] out_18,
  output [31:0] out_19,
  output [31:0] out_20,
  output [31:0] out_21,
  output [31:0] out_22,
  output [31:0] out_23,
  output [31:0] out_24,
  output [31:0] out_25,
  output [31:0] out_26,
  output [31:0] out_27
);

  Multiplexer #(.width(32), .enable("false")) multiplexer_1 (.in0(in_2), .in1(32'h1f), .out(out_15), .sel(in_1));
  Multiplexer #(.width(32), .enable("false")) multiplexer_2 (.in0(in_3), .in1(32'h1f1), .out(out_16), .sel(in_1));
  Multiplexer #(.width(32), .enable("false")) multiplexer_3 (.in0(in_4), .in1(32'h115), .out(out_17), .sel(in_1));
  Multiplexer #(.width(32), .enable("false")) multiplexer_4 (.in0(in_5), .in1(32'h311), .out(out_18), .sel(in_1));
  Multiplexer #(.width(32), .enable("false")) multiplexer_5 (.in0(in_6), .in1(32'h355), .out(out_19), .sel(in_1));
  Multiplexer #(.width(32), .enable("false")) multiplexer_6 (.in0(in_7), .in1(32'h351), .out(out_20), .sel(in_1));
  Multiplexer #(.width(32), .enable("false")) multiplexer_7 (.in0(in_8), .in1(32'h155), .out(out_21), .sel(in_1));
  Multiplexer #(.width(32), .enable("false")) multiplexer_8 (.in0(in_9), .in1(32'h1f1), .out(out_22), .sel(in_1));
  Multiplexer #(.width(32), .enable("false")) multiplexer_9 (.in0(in_10), .in1(32'h5f), .out(out_23), .sel(in_1));
  Multiplexer #(.width(32), .enable("false")) multiplexer_10 (.in0(in_11), .in1(32'h40), .out(out_24), .sel(in_1));
  Multiplexer #(.width(32), .enable("false")) multiplexer_11 (.in0(in_12), .in1(32'he0), .out(out_25), .sel(in_1));
  Multiplexer #(.width(32), .enable("false")) multiplexer_12 (.in0(in_13), .in1(32'ha0), .out(out_26), .sel(in_1));
  Multiplexer #(.width(32), .enable("false")) multiplexer_13 (.in0(in_14), .in1(32'he0), .out(out_27), .sel(in_1));
endmodule

module telos (
  input  in_1,
  input  in_2,
  input  in_3,
  output [31:0] out_4,
  output [31:0] out_5,
  output [31:0] out_6,
  output [31:0] out_7,
  output [31:0] out_8,
  output [31:0] out_9,
  output [31:0] out_10,
  output [31:0] out_11,
  output [31:0] out_12,
  output [31:0] out_13,
  output [31:0] out_14,
  output [31:0] out_15,
  output [31:0] out_16,
  output [31:0] out_17,
  output [31:0] out_18,
  output [31:0] out_19,
  output [31:0] out_20,
  output [31:0] out_21,
  output [31:0] out_22,
  output [31:0] out_23,
  output [31:0] out_24,
  output [31:0] out_25,
  output [31:0] out_26,
  output [31:0] out_27,
  output [31:0] out_28,
  output [31:0] out_29
);

  wire and_1_out, and_2_out, and_3_out, and_4_out, comparator_1_gt, comparator_2_eq, comparator_3_eq,
       comparator_3_gt, comparator_3_lt, comparator_4_eq, comparator_5_eq, comparator_6_eq, comparator_7_eq,
       comparator_8_eq, comparator_9_eq, comparator_10_eq, comparator_11_eq, comparator_12_eq, klok,
       not_1_out, or_1_out;
  wire [7:0] \ε_1_out_4 ;
  wire [31:0] ep_1_out_15, ep_1_out_16, ep_1_out_17, ep_1_out_18, ep_1_out_19, ep_1_out_20, ep_1_out_21,
       ep_1_out_22, ep_1_out_23, ep_1_out_24, ep_1_out_25, ep_1_out_26, ep_1_out_27, n2_1_out_15,
       n2_1_out_16, n2_1_out_17, n2_1_out_18, n2_1_out_19, n2_1_out_20, n2_1_out_21, n2_1_out_22,
       n2_1_out_23, n2_1_out_24, n2_1_out_25, n2_1_out_26, n2_1_out_27, n3_1_out_15, n3_1_out_16,
       n3_1_out_17, n3_1_out_18, n3_1_out_19, n3_1_out_20, n3_1_out_21, n3_1_out_22, n3_1_out_23,
       n3_1_out_24, n3_1_out_25, n3_1_out_26, n3_1_out_27, n4_1_out_15, n4_1_out_16, n4_1_out_17,
       n4_1_out_18, n4_1_out_19, n4_1_out_20, n4_1_out_21, n4_1_out_22, n4_1_out_23, n4_1_out_24,
       n4_1_out_25, n4_1_out_26, n4_1_out_27, n5_1_out_15, n5_1_out_16, n5_1_out_17, n5_1_out_18,
       n5_1_out_19, n5_1_out_20, n5_1_out_21, n5_1_out_22, n5_1_out_23, n5_1_out_24, n5_1_out_25,
       n5_1_out_26, n5_1_out_27, n6_1_out_15, n6_1_out_16, n6_1_out_17, n6_1_out_18, n6_1_out_19,
       n6_1_out_20, n6_1_out_21, n6_1_out_22, n6_1_out_23, n6_1_out_24, n6_1_out_25, n6_1_out_26,
       n6_1_out_27, n7_1_out_15, n7_1_out_16, n7_1_out_17, n7_1_out_18, n7_1_out_19, n7_1_out_20,
       n7_1_out_21, n7_1_out_22, n7_1_out_23, n7_1_out_24, n7_1_out_25, n7_1_out_26, n7_1_out_27,
       n8_1_out_15, n8_1_out_16, n8_1_out_17, n8_1_out_18, n8_1_out_19, n8_1_out_20, n8_1_out_21,
       n8_1_out_22, n8_1_out_23, n8_1_out_24, n8_1_out_25, n8_1_out_26, n8_1_out_27, n9_1_out_15,
       n9_1_out_16, n9_1_out_17, n9_1_out_18, n9_1_out_19, n9_1_out_20, n9_1_out_21, n9_1_out_22,
       n9_1_out_23, n9_1_out_24, n9_1_out_25, n9_1_out_26, n9_1_out_27, n10_1_out_15, n10_1_out_16,
       n10_1_out_17, n10_1_out_18, n10_1_out_19, n10_1_out_20, n10_1_out_21, n10_1_out_22, n10_1_out_23,
       n10_1_out_24, n10_1_out_25, n10_1_out_26, n10_1_out_27, \ε_2_out_5 , \ε_2_out_6 , \ε_2_out_7 ,
       \ε_2_out_8 , \ε_2_out_9 , \ε_2_out_10 , \ε_2_out_11 , \ε_2_out_12 , \ε_2_out_13 , \ε_2_out_14 ,
       \ε_2_out_15 , \ε_2_out_16 , \ε_2_out_17 ;

  Comparator comparator_1 (.a(8'h36), .b(\ε_1_out_4 ), .gt(comparator_1_gt));  // open: eq, lt
  Comparator comparator_2 (.a({8{1'b0}}), .b(\ε_1_out_4 ), .eq(comparator_2_eq));  // open: gt, lt
  and and_1 (and_1_out, klok, comparator_3_gt);
  \ε  \u_ε_1  (
    .in_1(in_1), .in_2(klok), .out_5(out_4), .out_6(out_5), .in_3(in_3), .out_7(out_6), .out_8(out_7),
    .out_9(out_8), .out_10(out_9), .out_11(out_10), .out_12(out_11), .out_13(out_12), .out_14(out_13),
    .out_15(out_14), .out_16(out_15), .out_17(out_16), .out_4(\ε_1_out_4 ));
  \ε  \u_ε_2  (
    .in_1(in_1), .in_2(and_1_out), .out_5(\ε_2_out_5 ), .out_6(\ε_2_out_6 ), .in_3(in_3),
    .out_7(\ε_2_out_7 ), .out_8(\ε_2_out_8 ), .out_9(\ε_2_out_9 ), .out_10(\ε_2_out_10 ),
    .out_11(\ε_2_out_11 ), .out_12(\ε_2_out_12 ), .out_13(\ε_2_out_13 ), .out_14(\ε_2_out_14 ),
    .out_15(\ε_2_out_15 ), .out_16(\ε_2_out_16 ), .out_17(\ε_2_out_17 ));  // open: out_4
  Comparator comparator_3 (
    .a(\ε_1_out_4 ), .b(8'h20), .gt(comparator_3_gt), .eq(comparator_3_eq), .lt(comparator_3_lt));
  Comparator comparator_4 (.a(\ε_1_out_4 ), .b(8'h1f), .eq(comparator_4_eq));  // open: gt, lt
  Comparator comparator_5 (.a(\ε_1_out_4 ), .b(8'h1e), .eq(comparator_5_eq));  // open: gt, lt
  Comparator comparator_6 (.a(\ε_1_out_4 ), .b(8'h1d), .eq(comparator_6_eq));  // open: gt, lt
  Comparator comparator_7 (.a(\ε_1_out_4 ), .b(8'h1c), .eq(comparator_7_eq));  // open: gt, lt
  Comparator comparator_8 (.a(\ε_1_out_4 ), .b(8'h1b), .eq(comparator_8_eq));  // open: gt, lt
  Comparator comparator_9 (.a(\ε_1_out_4 ), .b(8'h1a), .eq(comparator_9_eq));  // open: gt, lt
  Comparator comparator_10 (.a(\ε_1_out_4 ), .b(8'h19), .eq(comparator_10_eq));  // open: gt, lt
  Comparator comparator_11 (.a(\ε_1_out_4 ), .b(8'h18), .eq(comparator_11_eq));  // open: gt, lt
  Comparator comparator_12 (.a(\ε_1_out_4 ), .b(8'h17), .eq(comparator_12_eq));  // open: gt, lt
  and and_2 (and_2_out, in_1, in_2);
  or or_1 (or_1_out, and_2_out, and_3_out);
  and and_3 (and_3_out, in_2, comparator_1_gt);
  and and_4 (and_4_out, in_2, in_1, comparator_2_eq);
  not not_1 (not_1_out, and_4_out);
  and and_5 (klok, or_1_out, not_1_out);
  ep ep_1 (
    .in_2(\ε_2_out_5 ), .out_15(ep_1_out_15), .in_1(comparator_3_lt), .in_3(\ε_2_out_6 ),
    .out_16(ep_1_out_16), .in_4(\ε_2_out_7 ), .out_17(ep_1_out_17), .in_5(\ε_2_out_8 ), .out_18(ep_1_out_18),
    .in_6(\ε_2_out_9 ), .out_19(ep_1_out_19), .in_7(\ε_2_out_10 ), .out_20(ep_1_out_20), .in_8(\ε_2_out_11 ),
    .out_21(ep_1_out_21), .in_9(\ε_2_out_12 ), .out_22(ep_1_out_22), .in_10(\ε_2_out_13 ),
    .out_23(ep_1_out_23), .in_11(\ε_2_out_14 ), .out_24(ep_1_out_24), .in_12(\ε_2_out_15 ),
    .out_25(ep_1_out_25), .in_13(\ε_2_out_16 ), .out_26(ep_1_out_26), .in_14(\ε_2_out_17 ),
    .out_27(ep_1_out_27));
  _10 u_10_1 (
    .in_2(ep_1_out_15), .in_3(ep_1_out_16), .in_4(ep_1_out_17), .in_5(ep_1_out_18), .in_6(ep_1_out_19),
    .in_7(ep_1_out_20), .in_8(ep_1_out_21), .in_9(ep_1_out_22), .in_10(ep_1_out_23), .in_11(ep_1_out_24),
    .in_12(ep_1_out_25), .in_13(ep_1_out_26), .in_14(ep_1_out_27), .out_15(n10_1_out_15),
    .out_16(n10_1_out_16), .out_17(n10_1_out_17), .out_18(n10_1_out_18), .out_19(n10_1_out_19),
    .out_20(n10_1_out_20), .out_21(n10_1_out_21), .out_22(n10_1_out_22), .out_23(n10_1_out_23),
    .out_24(n10_1_out_24), .out_25(n10_1_out_25), .out_26(n10_1_out_26), .out_27(n10_1_out_27),
    .in_1(comparator_3_eq));
  _8 u_8_1 (
    .in_2(n9_1_out_15), .in_3(n9_1_out_16), .in_4(n9_1_out_17), .in_5(n9_1_out_18), .in_6(n9_1_out_19),
    .in_7(n9_1_out_20), .in_8(n9_1_out_21), .in_9(n9_1_out_22), .in_10(n9_1_out_23), .in_11(n9_1_out_24),
    .in_12(n9_1_out_25), .in_13(n9_1_out_26), .in_14(n9_1_out_27), .out_15(n8_1_out_15),
    .out_16(n8_1_out_16), .out_17(n8_1_out_17), .out_18(n8_1_out_18), .out_19(n8_1_out_19),
    .out_20(n8_1_out_20), .out_21(n8_1_out_21), .out_22(n8_1_out_22), .out_23(n8_1_out_23),
    .out_24(n8_1_out_24), .out_25(n8_1_out_25), .out_26(n8_1_out_26), .out_27(n8_1_out_27),
    .in_1(comparator_5_eq));
  _9 u_9_1 (
    .in_1(n10_1_out_15), .in_2(n10_1_out_16), .in_3(n10_1_out_17), .in_4(n10_1_out_18), .in_5(n10_1_out_19),
    .in_6(n10_1_out_20), .in_7(n10_1_out_21), .in_8(n10_1_out_22), .in_10(n10_1_out_23),
    .in_11(n10_1_out_24), .in_12(n10_1_out_25), .in_13(n10_1_out_26), .in_14(n10_1_out_27),
    .out_15(n9_1_out_15), .out_16(n9_1_out_16), .out_17(n9_1_out_17), .out_18(n9_1_out_18),
    .out_19(n9_1_out_19), .out_20(n9_1_out_20), .out_21(n9_1_out_21), .out_22(n9_1_out_22),
    .out_23(n9_1_out_23), .out_24(n9_1_out_24), .out_25(n9_1_out_25), .out_26(n9_1_out_26),
    .out_27(n9_1_out_27), .in_9(comparator_4_eq));
  DotMatrix #(.matrixcols(14), .matrixrows(32)) dotmatrix_1 (
    .col0(out_17), .col1(out_18), .col2(out_19), .col3(out_20), .col4(out_21), .col5(out_22), .col6(out_23),
    .col7(out_24), .col8(out_25), .col9(out_26), .col10(out_27), .col11(out_28), .col12(out_29),
    .col13({32{1'b0}}));
  DotMatrix #(.matrixcols(14), .matrixrows(32)) dotmatrix_2 (
    .col0(out_4), .col1(out_5), .col2(out_6), .col3(out_7), .col4(out_8), .col5(out_9), .col6(out_10),
    .col7(out_11), .col8(out_12), .col9(out_13), .col10(out_14), .col11(out_15), .col12(out_16),
    .col13({32{1'b0}}));
  _6 u_6_1 (
    .in_2(n7_1_out_15), .in_3(n7_1_out_16), .in_4(n7_1_out_17), .in_5(n7_1_out_18), .in_6(n7_1_out_19),
    .in_7(n7_1_out_20), .in_8(n7_1_out_21), .in_9(n7_1_out_22), .in_10(n7_1_out_23), .in_11(n7_1_out_24),
    .in_12(n7_1_out_25), .in_13(n7_1_out_26), .in_14(n7_1_out_27), .out_15(n6_1_out_15),
    .out_16(n6_1_out_16), .out_17(n6_1_out_17), .out_18(n6_1_out_18), .out_19(n6_1_out_19),
    .out_20(n6_1_out_20), .out_21(n6_1_out_21), .out_22(n6_1_out_22), .out_23(n6_1_out_23),
    .out_24(n6_1_out_24), .out_25(n6_1_out_25), .out_26(n6_1_out_26), .out_27(n6_1_out_27),
    .in_1(comparator_7_eq));
  _5 u_5_1 (
    .in_2(n6_1_out_15), .in_3(n6_1_out_16), .in_4(n6_1_out_17), .in_5(n6_1_out_18), .in_6(n6_1_out_19),
    .in_7(n6_1_out_20), .in_8(n6_1_out_21), .in_9(n6_1_out_22), .in_10(n6_1_out_23), .in_11(n6_1_out_24),
    .in_12(n6_1_out_25), .in_13(n6_1_out_26), .in_14(n6_1_out_27), .out_15(n5_1_out_15),
    .out_16(n5_1_out_16), .out_17(n5_1_out_17), .out_18(n5_1_out_18), .out_19(n5_1_out_19),
    .out_20(n5_1_out_20), .out_21(n5_1_out_21), .out_22(n5_1_out_22), .out_23(n5_1_out_23),
    .out_24(n5_1_out_24), .out_25(n5_1_out_25), .out_26(n5_1_out_26), .out_27(n5_1_out_27),
    .in_1(comparator_8_eq));
  _4 u_4_1 (
    .in_2(n5_1_out_15), .in_3(n5_1_out_16), .in_4(n5_1_out_17), .in_5(n5_1_out_18), .in_6(n5_1_out_19),
    .in_7(n5_1_out_20), .in_8(n5_1_out_21), .in_9(n5_1_out_22), .in_10(n5_1_out_23), .in_11(n5_1_out_24),
    .in_12(n5_1_out_25), .in_13(n5_1_out_26), .in_14(n5_1_out_27), .out_15(n4_1_out_15),
    .out_16(n4_1_out_16), .out_17(n4_1_out_17), .out_18(n4_1_out_18), .out_19(n4_1_out_19),
    .out_20(n4_1_out_20), .out_21(n4_1_out_21), .out_22(n4_1_out_22), .out_23(n4_1_out_23),
    .out_24(n4_1_out_24), .out_25(n4_1_out_25), .out_26(n4_1_out_26), .out_27(n4_1_out_27),
    .in_1(comparator_9_eq));
  _7 u_7_1 (
    .in_2(n8_1_out_15), .in_3(n8_1_out_16), .in_4(n8_1_out_17), .in_5(n8_1_out_18), .in_6(n8_1_out_19),
    .in_7(n8_1_out_20), .in_8(n8_1_out_21), .in_9(n8_1_out_22), .in_10(n8_1_out_23), .in_11(n8_1_out_24),
    .in_12(n8_1_out_25), .in_13(n8_1_out_26), .in_14(n8_1_out_27), .out_15(n7_1_out_15),
    .out_16(n7_1_out_16), .out_17(n7_1_out_17), .out_18(n7_1_out_18), .out_19(n7_1_out_19),
    .out_20(n7_1_out_20), .out_21(n7_1_out_21), .out_22(n7_1_out_22), .out_23(n7_1_out_23),
    .out_24(n7_1_out_24), .out_25(n7_1_out_25), .out_26(n7_1_out_26), .out_27(n7_1_out_27),
    .in_1(comparator_6_eq));
  _2 u_2_1 (
    .in_2(n3_1_out_15), .in_3(n3_1_out_16), .in_4(n3_1_out_17), .in_5(n3_1_out_18), .in_6(n3_1_out_19),
    .in_7(n3_1_out_20), .in_8(n3_1_out_21), .in_9(n3_1_out_22), .in_10(n3_1_out_23), .in_11(n3_1_out_24),
    .in_12(n3_1_out_25), .in_13(n3_1_out_26), .in_14(n3_1_out_27), .out_15(n2_1_out_15),
    .out_16(n2_1_out_16), .out_17(n2_1_out_17), .out_18(n2_1_out_18), .out_19(n2_1_out_19),
    .out_20(n2_1_out_20), .out_21(n2_1_out_21), .out_22(n2_1_out_22), .out_23(n2_1_out_23),
    .out_24(n2_1_out_24), .out_25(n2_1_out_25), .out_26(n2_1_out_26), .out_27(n2_1_out_27),
    .in_1(comparator_11_eq));
  _3 u_3_1 (
    .in_2(n4_1_out_15), .in_3(n4_1_out_16), .in_4(n4_1_out_17), .in_5(n4_1_out_18), .in_6(n4_1_out_19),
    .in_7(n4_1_out_20), .in_8(n4_1_out_21), .in_9(n4_1_out_22), .in_10(n4_1_out_23), .in_11(n4_1_out_24),
    .in_12(n4_1_out_25), .in_13(n4_1_out_26), .in_14(n4_1_out_27), .out_15(n3_1_out_15),
    .out_16(n3_1_out_16), .out_17(n3_1_out_17), .out_18(n3_1_out_18), .out_19(n3_1_out_19),
    .out_20(n3_1_out_20), .out_21(n3_1_out_21), .out_22(n3_1_out_22), .out_23(n3_1_out_23),
    .out_24(n3_1_out_24), .out_25(n3_1_out_25), .out_26(n3_1_out_26), .out_27(n3_1_out_27),
    .in_1(comparator_10_eq));
  _1 u_1_1 (
    .in_2(n2_1_out_15), .in_3(n2_1_out_16), .in_4(n2_1_out_17), .in_5(n2_1_out_18), .in_6(n2_1_out_19),
    .in_7(n2_1_out_20), .in_8(n2_1_out_21), .in_9(n2_1_out_22), .in_10(n2_1_out_23), .in_11(n2_1_out_24),
    .in_12(n2_1_out_25), .in_13(n2_1_out_26), .in_14(n2_1_out_27), .out_15(out_17), .out_16(out_18),
    .out_17(out_19), .out_18(out_20), .out_19(out_21), .out_20(out_22), .out_21(out_23), .out_22(out_24),
    .out_23(out_25), .out_24(out_26), .out_25(out_27), .out_26(out_28), .out_27(out_29),
    .in_1(comparator_12_eq));

  // Other names for the same wires on the sheet: plus_or_minus = in_1; rest = in_3
endmodule
