// Logisim project κηνηση.circ as structural Verilog: 6 circuits, main circuit δεξια αριστερα
module main (
  input  in_1,
  input  in_2,
  input  in_3
);

  wire _1, _2, _3, _4, clock_1_out, keyboard_1_avail, klok, or_3_out, or_4_out, or_5_out, or_6_out,
       plus_or_minus, s1, s2, s3, s4;
  wire [1:0] joystick_1_x, joystick_1_y;
  wire [6:0] keyboard_1_data;
  wire [7:0] bol_1_out_7, bol_1_out_8;
  wire [31:0] neo_1_out_30, neo_1_out_31, neo_1_out_32, neo_1_out_33, neo_1_out_34, neo_1_out_35,
       neo_1_out_36, neo_1_out_37, neo_1_out_38, neo_1_out_39, neo_1_out_40, neo_1_out_41, neo_1_out_42,
       neo_1_out_43, neo_1_out_44, neo_1_out_45, neo_1_out_46, neo_1_out_47, neo_1_out_48, neo_1_out_49,
       neo_1_out_50, neo_1_out_51, neo_1_out_52, neo_1_out_53, neo_1_out_54, neo_1_out_55, neo_1_out_56,
       neo_1_out_57, neo_1_out_58, neo_1_out_59, neo_1_out_60, neo_1_out_61, neo_1_out_62, neo_1_out_63,
       neo_1_out_64, neo_1_out_65, neo_1_out_66, neo_1_out_67, neo_1_out_68, neo_1_out_69, neo_1_out_70,
       neo_1_out_71, neo_1_out_72, neo_1_out_73, neo_1_out_74, neo_1_out_75, neo_1_out_76, neo_1_out_77,
       neo_1_out_78, neo_1_out_79, neo_1_out_80, neo_1_out_81, neo_1_out_82, neo_1_out_83, neo_1_out_84,
       neo_1_out_85, neo_1_out_86, neo_1_out_87, neo_1_out_88, neo_1_out_89, neo_1_out_90, neo_1_out_91,
       neo_1_out_92, neo_1_out_93, neo_1_out_94, neo_1_out_95, neo_1_out_96, neo_1_out_97, neo_1_out_98,
       neo_1_out_99, neo_1_out_100, neo_1_out_101, neo_1_out_102, neo_1_out_103, neo_1_out_104,
       neo_1_out_105, neo_1_out_106, neo_1_out_107, neo_1_out_108, neo_1_out_109, neo_1_out_110,
       neo_1_out_111, neo_1_out_112, neo_1_out_113, neo_1_out_114, neo_1_out_115, neo_1_out_116,
       neo_1_out_117, neo_1_out_118, neo_1_out_119, neo_1_out_120, neo_1_out_121, neo_1_out_122,
       neo_1_out_123, neo_1_out_124, neo_1_out_125, neo_1_out_126, neo_1_out_127, neo_1_out_128,
       neo_1_out_129, neo_1_out_130, neo_1_out_131, neo_1_out_132, neo_1_out_133, neo_1_out_134,
       neo_1_out_135, neo_1_out_136, neo_1_out_137, neo_1_out_138, neo_1_out_139, neo_1_out_140,
       neo_1_out_141, neo_1_out_142, neo_1_out_143, neo_1_out_144, neo_1_out_145, neo_1_out_146,
       neo_1_out_147, neo_1_out_148, neo_1_out_149, neo_1_out_150, neo_1_out_151, neo_1_out_152,
       neo_1_out_153, neo_1_out_154, neo_1_out_155, neo_1_out_156, neo_1_out_157, telos_1_out_4,
       telos_1_out_5, telos_1_out_6, telos_1_out_7, telos_1_out_8, telos_1_out_9, telos_1_out_10,
       telos_1_out_11, telos_1_out_12, telos_1_out_13, telos_1_out_14, telos_1_out_15, telos_1_out_16,
       telos_1_out_17, telos_1_out_18, telos_1_out_19, telos_1_out_20, telos_1_out_21, telos_1_out_22,
       telos_1_out_23, telos_1_out_24, telos_1_out_25, telos_1_out_26, telos_1_out_27, telos_1_out_28,
       telos_1_out_29;

  or or_1 (klok, s3, _4);
  or or_2 (plus_or_minus, s4, _3);
  Keyboard keyboard_1 (.clk(clock_1_out), .avail(keyboard_1_avail), .data(keyboard_1_data));  // open: re, clr
  Clock clock_1 (.out(clock_1_out));
  Joystick #(.bits(2)) joystick_1 (.x(joystick_1_x), .y(joystick_1_y));
  or or_3 (or_3_out, _1, s1);
  ss ss_1 (.in_1(keyboard_1_avail), .in_2(keyboard_1_data), .out_5(_2), .out_3(_1), .out_6(_3), .out_4(_4));
  mox mox_1 (.out_3(s1), .out_4(s2), .in_1(joystick_1_x), .in_2(joystick_1_y), .out_5(s4), .out_6(s3));
  or or_4 (or_4_out, s2, _2);
  bol bol_1 (
    .set(in_2), .out_7(bol_1_out_7), .out_8(bol_1_out_8), .in_1(or_3_out), .in_2(or_4_out), .in_3(klok),
    .in_4(plus_or_minus), .reset(in_3));
  // Probe on bol_1_out_7
  // Probe on bol_1_out_8
  DotMatrix #(.matrixcols(32), .matrixrows(32)) dotmatrix_1 (
    .col0(neo_1_out_93), .col1(neo_1_out_92), .col2(neo_1_out_91), .col3(neo_1_out_90), .col4(neo_1_out_89),
    .col5(neo_1_out_88), .col6(neo_1_out_87), .col7(neo_1_out_86), .col8(neo_1_out_85), .col9(neo_1_out_84),
    .col10(neo_1_out_83), .col11(neo_1_out_82), .col12(neo_1_out_81), .col13(neo_1_out_80),
    .col14(neo_1_out_79), .col15(neo_1_out_78), .col16(neo_1_out_77), .col17(neo_1_out_76),
    .col18(neo_1_out_75), .col19(neo_1_out_74), .col20(neo_1_out_73), .col21(neo_1_out_72),
    .col22(neo_1_out_71), .col23(neo_1_out_70), .col24(neo_1_out_69), .col25(neo_1_out_68),
    .col26(neo_1_out_67), .col27(neo_1_out_66), .col28(neo_1_out_65), .col29(neo_1_out_64),
    .col30(neo_1_out_63), .col31(neo_1_out_62));
  DotMatrix #(.matrixcols(32), .matrixrows(32)) dotmatrix_2 (
    .col0(neo_1_out_157), .col1(neo_1_out_156), .col2(neo_1_out_155), .col3(neo_1_out_154),
    .col4(neo_1_out_153), .col5(neo_1_out_152), .col6(neo_1_out_151), .col7(neo_1_out_150),
    .col8(neo_1_out_149), .col9(neo_1_out_148), .col10(neo_1_out_147), .col11(neo_1_out_146),
    .col12(neo_1_out_145), .col13(neo_1_out_144), .col14(neo_1_out_143), .col15(neo_1_out_142),
    .col16(neo_1_out_141), .col17(neo_1_out_140), .col18(neo_1_out_139), .col19(neo_1_out_138),
    .col20(neo_1_out_137), .col21(neo_1_out_136), .col22(neo_1_out_135), .col23(neo_1_out_134),
    .col24(neo_1_out_133), .col25(neo_1_out_132), .col26(neo_1_out_131), .col27(neo_1_out_130),
    .col28(neo_1_out_129), .col29(neo_1_out_128), .col30(neo_1_out_127), .col31(neo_1_out_126));
  telos telos_1 (
    .in_1(plus_or_minus), .in_3(in_1), .in_2(klok), .out_4(telos_1_out_4), .out_5(telos_1_out_5),
    .out_6(telos_1_out_6), .out_7(telos_1_out_7), .out_8(telos_1_out_8), .out_9(telos_1_out_9),
    .out_10(telos_1_out_10), .out_11(telos_1_out_11), .out_12(telos_1_out_12), .out_13(telos_1_out_13),
    .out_14(telos_1_out_14), .out_15(telos_1_out_15), .out_16(telos_1_out_16), .out_17(telos_1_out_17),
    .out_18(telos_1_out_18), .out_19(telos_1_out_19), .out_20(telos_1_out_20), .out_21(telos_1_out_21),
    .out_22(telos_1_out_22), .out_23(telos_1_out_23), .out_24(telos_1_out_24), .out_25(telos_1_out_25),
    .out_26(telos_1_out_26), .out_27(telos_1_out_27), .out_28(telos_1_out_28), .out_29(telos_1_out_29));
  neo neo_1 (
    .in_17(telos_1_out_4), .in_18(telos_1_out_5), .in_1(or_5_out), .in_2(or_6_out), .in_3(in_1),
    .in_19(telos_1_out_6), .in_20(telos_1_out_7), .in_21(telos_1_out_8), .in_22(telos_1_out_9),
    .in_23(telos_1_out_10), .in_24(telos_1_out_11), .in_25(telos_1_out_12), .in_26(telos_1_out_13),
    .in_27(telos_1_out_14), .in_28(telos_1_out_15), .in_29(telos_1_out_16), .in_4(telos_1_out_17),
    .in_5(telos_1_out_18), .in_6(telos_1_out_19), .in_7(telos_1_out_20), .in_8(telos_1_out_21),
    .in_9(telos_1_out_22), .in_10(telos_1_out_23), .in_11(telos_1_out_24), .in_12(telos_1_out_25),
    .in_13(telos_1_out_26), .in_14(telos_1_out_27), .in_15(telos_1_out_28), .in_16(telos_1_out_29),
    .out_94(neo_1_out_94), .out_95(neo_1_out_95), .out_96(neo_1_out_96), .out_97(neo_1_out_97),
    .out_98(neo_1_out_98), .out_99(neo_1_out_99), .out_100(neo_1_out_100), .out_101(neo_1_out_101),
    .out_102(neo_1_out_102), .out_103(neo_1_out_103), .out_104(neo_1_out_104), .out_105(neo_1_out_105),
    .out_106(neo_1_out_106), .out_107(neo_1_out_107), .out_108(neo_1_out_108), .out_109(neo_1_out_109),
    .out_110(neo_1_out_110), .out_111(neo_1_out_111), .out_112(neo_1_out_112), .out_113(neo_1_out_113),
    .out_114(neo_1_out_114), .out_115(neo_1_out_115), .out_116(neo_1_out_116), .out_117(neo_1_out_117),
    .out_118(neo_1_out_118), .out_119(neo_1_out_119), .out_120(neo_1_out_120), .out_121(neo_1_out_121),
    .out_122(neo_1_out_122), .out_123(neo_1_out_123), .out_124(neo_1_out_124), .out_125(neo_1_out_125),
    .out_126(neo_1_out_126), .out_127(neo_1_out_127), .out_128(neo_1_out_128), .out_129(neo_1_out_129),
    .out_130(neo_1_out_130), .out_131(neo_1_out_131), .out_132(neo_1_out_132), .out_133(neo_1_out_133),
    .out_134(neo_1_out_134), .out_135(neo_1_out_135), .out_136(neo_1_out_136), .out_137(neo_1_out_137),
    .out_138(neo_1_out_138), .out_139(neo_1_out_139), .out_140(neo_1_out_140), .out_141(neo_1_out_141),
    .out_142(neo_1_out_142), .out_143(neo_1_out_143), .out_144(neo_1_out_144), .out_145(neo_1_out_145),
    .out_146(neo_1_out_146), .out_147(neo_1_out_147), .out_148(neo_1_out_148), .out_149(neo_1_out_149),
    .out_150(neo_1_out_150), .out_151(neo_1_out_151), .out_152(neo_1_out_152), .out_153(neo_1_out_153),
    .out_154(neo_1_out_154), .out_155(neo_1_out_155), .out_156(neo_1_out_156), .out_157(neo_1_out_157),
    .out_30(neo_1_out_30), .out_31(neo_1_out_31), .out_32(neo_1_out_32), .out_33(neo_1_out_33),
    .out_34(neo_1_out_34), .out_35(neo_1_out_35), .out_36(neo_1_out_36), .out_37(neo_1_out_37),
    .out_38(neo_1_out_38), .out_39(neo_1_out_39), .out_40(neo_1_out_40), .out_41(neo_1_out_41),
    .out_42(neo_1_out_42), .out_43(neo_1_out_43), .out_44(neo_1_out_44), .out_45(neo_1_out_45),
    .out_46(neo_1_out_46), .out_47(neo_1_out_47), .out_48(neo_1_out_48), .out_49(neo_1_out_49),
    .out_50(neo_1_out_50), .out_51(neo_1_out_51), .out_52(neo_1_out_52), .out_53(neo_1_out_53),
    .out_54(neo_1_out_54), .out_55(neo_1_out_55), .out_56(neo_1_out_56), .out_57(neo_1_out_57),
    .out_58(neo_1_out_58), .out_59(neo_1_out_59), .out_60(neo_1_out_60), .out_61(neo_1_out_61),
    .out_62(neo_1_out_62), .out_63(neo_1_out_63), .out_64(neo_1_out_64), .out_65(neo_1_out_65),
    .out_66(neo_1_out_66), .out_67(neo_1_out_67), .out_68(neo_1_out_68), .out_69(neo_1_out_69),
    .out_70(neo_1_out_70), .out_71(neo_1_out_71), .out_72(neo_1_out_72), .out_73(neo_1_out_73),
    .out_74(neo_1_out_74), .out_75(neo_1_out_75), .out_76(neo_1_out_76), .out_77(neo_1_out_77),
    .out_78(neo_1_out_78), .out_79(neo_1_out_79), .out_80(neo_1_out_80), .out_81(neo_1_out_81),
    .out_82(neo_1_out_82), .out_83(neo_1_out_83), .out_84(neo_1_out_84), .out_85(neo_1_out_85),
    .out_86(neo_1_out_86), .out_87(neo_1_out_87), .out_88(neo_1_out_88), .out_89(neo_1_out_89),
    .out_90(neo_1_out_90), .out_91(neo_1_out_91), .out_92(neo_1_out_92), .out_93(neo_1_out_93));
  or or_5 (or_5_out, _2, s2);
  or or_6 (or_6_out, s1, _1);
  DotMatrix #(.matrixcols(32), .matrixrows(32)) dotmatrix_3 (
    .col0(neo_1_out_61), .col1(neo_1_out_60), .col2(neo_1_out_59), .col3(neo_1_out_58), .col4(neo_1_out_57),
    .col5(neo_1_out_56), .col6(neo_1_out_55), .col7(neo_1_out_54), .col8(neo_1_out_53), .col9(neo_1_out_52),
    .col10(neo_1_out_51), .col11(neo_1_out_50), .col12(neo_1_out_49), .col13(neo_1_out_48),
    .col14(neo_1_out_47), .col15(neo_1_out_46), .col16(neo_1_out_45), .col17(neo_1_out_44),
    .col18(neo_1_out_43), .col19(neo_1_out_42), .col20(neo_1_out_41), .col21(neo_1_out_40),
    .col22(neo_1_out_39), .col23(neo_1_out_38), .col24(neo_1_out_37), .col25(neo_1_out_36),
    .col26(neo_1_out_35), .col27(neo_1_out_34), .col28(neo_1_out_33), .col29(neo_1_out_32),
    .col30(neo_1_out_31), .col31(neo_1_out_30));
  DotMatrix #(.matrixcols(32), .matrixrows(32)) dotmatrix_4 (
    .col0(neo_1_out_125), .col1(neo_1_out_124), .col2(neo_1_out_123), .col3(neo_1_out_122),
    .col4(neo_1_out_121), .col5(neo_1_out_120), .col6(neo_1_out_119), .col7(neo_1_out_118),
    .col8(neo_1_out_117), .col9(neo_1_out_116), .col10(neo_1_out_115), .col11(neo_1_out_114),
    .col12(neo_1_out_113), .col13(neo_1_out_112), .col14(neo_1_out_111), .col15(neo_1_out_110),
    .col16(neo_1_out_109), .col17(neo_1_out_108), .col18(neo_1_out_107), .col19(neo_1_out_106),
    .col20(neo_1_out_105), .col21(neo_1_out_104), .col22(neo_1_out_103), .col23(neo_1_out_102),
    .col24(neo_1_out_101), .col25(neo_1_out_100), .col26(neo_1_out_99), .col27(neo_1_out_98),
    .col28(neo_1_out_97), .col29(neo_1_out_96), .col30(neo_1_out_95), .col31(neo_1_out_94));

  // Other names for the same wires on the sheet: res = in_1
endmodule

module \δεξια_αριστερα  (
  input  [31:0] in_1,
  input  [31:0] _2,
  input  in_3,
  input  [31:0] in_4,
  input  in_5,
  input  [31:0] _4,
  input  [31:0] _5,
  input  in_8,
  input  [31:0] in_9,
  input  [31:0] _7,
  input  [31:0] _8,
  input  [31:0] in_12,
  input  [31:0] _10,
  input  [31:0] _11,
  input  [31:0] _12,
  input  [31:0] in_16,
  output [31:0] out_17,
  output [31:0] out_18,
  output [31:0] out_19,
  output [31:0] out_20,
  output [31:0] out_21,
  output [31:0] out_22,
  output [31:0] out_23,
  output [31:0] out_24,
  output [31:0] out_25,
  output [31:0] out_26,
  output [31:0] out_27,
  output [31:0] out_28,
  output [31:0] out_29,
  output [31:0] out_30,
  output [31:0] out_31,
  output [31:0] out_32,
  output [31:0] out_33,
  output [31:0] out_34,
  output [31:0] out_35,
  output [31:0] out_36,
  output [31:0] out_37,
  output [31:0] out_38,
  output [31:0] out_39,
  output [31:0] out_40,
  output [31:0] out_41,
  output [31:0] out_42,
  output [31:0] out_43,
  output [31:0] out_44,
  output [31:0] out_45,
  output [31:0] out_46,
  output [31:0] out_47,
  output [31:0] out_48,
  output [31:0] out_49,
  output [31:0] out_50,
  output [31:0] out_51,
  output [31:0] out_52,
  output [31:0] out_53,
  output [31:0] out_54,
  output [31:0] out_55,
  output [31:0] out_56,
  output [31:0] out_57,
  output [31:0] out_58,
  output [31:0] out_59,
  output [31:0] out_60,
  output [31:0] out_61,
  output [31:0] out_62,
  output [31:0] out_63,
  output [31:0] out_64,
  output [31:0] out_65,
  output [31:0] out_66,
  output [31:0] out_67,
  output [31:0] out_68,
  output [31:0] out_69,
  output [31:0] out_70,
  output [31:0] out_71,
  output [31:0] out_72,
  output [31:0] out_73,
  output [31:0] out_74,
  output [31:0] out_75,
  output [31:0] out_76,
  output [31:0] out_77,
  output [31:0] out_78,
  output [31:0] out_79,
  output [31:0] out_80
);

  wire and_1_out, and_2_out, and_3_out, and_4_out, and_5_out, and_6_out, and_7_out, and_8_out, and_9_out,
       comparator_1_eq, comparator_1_gt, comparator_3_eq, comparator_5_eq, comparator_5_lt, comparator_6_eq,
       comparator_7_eq, klok, not_1_out, or_1_out, or_2_out, or_4_out, or_5_out, register_2_q, s, sos;
  wire [4:0] bit_extender_1_out, bit_extender_2_out;
  wire [5:0] counter_2_q;
  wire [6:0] counter_1_q, register_1_q;
  wire [31:0] multiplexer_32_out;

  Comparator #(.width(7)) comparator_1 (
    .a(counter_1_q), .b(register_1_q), .gt(comparator_1_gt), .eq(comparator_1_eq));  // open: lt
  Register #(.width(7)) register_1 (.D(7'b0000001), .Q(register_1_q), .clk(in_8), .clr(in_5));  // open: en
  not not_1 (not_1_out, in_3);
  or or_1 (or_1_out, comparator_1_eq, comparator_1_gt);
  and and_1 (and_1_out, in_3, comparator_1_gt);
  Bit_Extender #(.in_width(6), .out_width(5)) bit_extender_1 (.in(counter_2_q), .out(bit_extender_1_out));
  and and_2 (and_2_out, klok, or_2_out);
  or or_2 (or_2_out, in_3, sos);
  and and_3 (and_3_out, in_8, and_1_out);
  or or_3 (klok, and_3_out, and_4_out);
  and and_4 (and_4_out, in_8, not_1_out, or_1_out);
  and and_5 (and_5_out, and_2_out, register_2_q);
  and and_6 (and_6_out, or_4_out, and_2_out);
  Counter #(.width(7), .max('h7f)) counter_1 (
    .load(in_3), .Q(counter_1_q), .clk(and_6_out), .clr(in_5));  // open: D, count, carry
  Bit_Extender #(.in_width(7), .out_width(5)) bit_extender_2 (.in(counter_1_q), .out(bit_extender_2_out));
  Multiplexer #(.select(5), .width(32), .enable("false")) multiplexer_1 (
    .in0({32{1'b0}}), .in1(in_1), .in2({32{1'b0}}), .in3({32{1'b0}}), .in4({32{1'b0}}), .in5({32{1'b0}}),
    .in6({32{1'b0}}), .in7({32{1'b0}}), .in8({32{1'b0}}), .in9({32{1'b0}}), .in10({32{1'b0}}),
    .in11({32{1'b0}}), .in12({32{1'b0}}), .in13({32{1'b0}}), .in14({32{1'b0}}), .in15({32{1'b0}}),
    .in16({32{1'b0}}), .in17({32{1'b0}}), .in18({32{1'b0}}), .in19({32{1'b0}}), .in20({32{1'b0}}),
    .in21({32{1'b0}}), .in22({32{1'b0}}), .in23({32{1'b0}}), .in24({32{1'b0}}), .in25({32{1'b0}}),
    .in26({32{1'b0}}), .in27({32{1'b0}}), .in28({32{1'b0}}), .in29({32{1'b0}}), .in30({32{1'b0}}),
    .in31({32{1'b0}}), .out(out_17), .sel(bit_extender_2_out));
  Multiplexer #(.select(5), .width(32), .enable("false")) multiplexer_2 (
    .in0({32{1'b0}}), .in1(_2), .in2(in_1), .in3({32{1'b0}}), .in4({32{1'b0}}), .in5({32{1'b0}}),
    .in6({32{1'b0}}), .in7({32{1'b0}}), .in8({32{1'b0}}), .in9({32{1'b0}}), .in10({32{1'b0}}),
    .in11({32{1'b0}}), .in12({32{1'b0}}), .in13({32{1'b0}}), .in14({32{1'b0}}), .in15({32{1'b0}}),
    .in16({32{1'b0}}), .in17({32{1'b0}}), .in18({32{1'b0}}), .in19({32{1'b0}}), .in20({32{1'b0}}),
    .in21({32{1'b0}}), .in22({32{1'b0}}), .in23({32{1'b0}}), .in24({32{1'b0}}), .in25({32{1'b0}}),
    .in26({32{1'b0}}), .in27({32{1'b0}}), .in28({32{1'b0}}), .in29({32{1'b0}}), .in30({32{1'b0}}),
    .in31({32{1'b0}}), .out(out_18), .sel(bit_extender_2_out));
  Multiplexer #(.select(5), .width(32), .enable("false")) multiplexer_3 (
    .in0({32{1'b0}}), .in1(in_4), .in2(_2), .in3(in_1), .in4({32{1'b0}}), .in5({32{1'b0}}), .in6({32{1'b0}}),
    .in7({32{1'b0}}), .in8({32{1'b0}}), .in9({32{1'b0}}), .in10({32{1'b0}}), .in11({32{1'b0}}),
    .in12({32{1'b0}}), .in13({32{1'b0}}), .in14({32{1'b0}}), .in15({32{1'b0}}), .in16({32{1'b0}}),
    .in17({32{1'b0}}), .in18({32{1'b0}}), .in19({32{1'b0}}), .in20({32{1'b0}}), .in21({32{1'b0}}),
    .in22({32{1'b0}}), .in23({32{1'b0}}), .in24({32{1'b0}}), .in25({32{1'b0}}), .in26({32{1'b0}}),
    .in27({32{1'b0}}), .in28({32{1'b0}}), .in29({32{1'b0}}), .in30({32{1'b0}}), .in31({32{1'b0}}),
    .out(out_19), .sel(bit_extender_2_out));
  Multiplexer #(.select(5), .width(32), .enable("false")) multiplexer_4 (
    .in0({32{1'b0}}), .in1(_4), .in2(in_4), .in3(_2), .in4(in_1), .in5({32{1'b0}}), .in6({32{1'b0}}),
    .in7({32{1'b0}}), .in8({32{1'b0}}), .in9({32{1'b0}}), .in10({32{1'b0}}), .in11({32{1'b0}}),
    .in12({32{1'b0}}), .in13({32{1'b0}}), .in14({32{1'b0}}), .in15({32{1'b0}}), .in16({32{1'b0}}),
    .in17({32{1'b0}}), .in18({32{1'b0}}), .in19({32{1'b0}}), .in20({32{1'b0}}), .in21({32{1'b0}}),
    .in22({32{1'b0}}), .in23({32{1'b0}}), .in24({32{1'b0}}), .in25({32{1'b0}}), .in26({32{1'b0}}),
    .in27({32{1'b0}}), .in28({32{1'b0}}), .in29({32{1'b0}}), .in30({32{1'b0}}), .in31({32{1'b0}}),
    .out(out_20), .sel(bit_extender_2_out));
  Multiplexer #(.select(5), .width(32), .enable("false")) multiplexer_5 (
    .in0({32{1'b0}}), .in1(_5), .in2(_4), .in3(in_4), .in4(_2), .in5(in_1), .in6({32{1'b0}}),
    .in7({32{1'b0}}), .in8({32{1'b0}}), .in9({32{1'b0}}), .in10({32{1'b0}}), .in11({32{1'b0}}),
    .in12({32{1'b0}}), .in13({32{1'b0}}), .in14({32{1'b0}}), .in15({32{1'b0}}), .in16({32{1'b0}}),
    .in17({32{1'b0}}), .in18({32{1'b0}}), .in19({32{1'b0}}), .in20({32{1'b0}}), .in21({32{1'b0}}),
    .in22({32{1'b0}}), .in23({32{1'b0}}), .in24({32{1'b0}}), .in25({32{1'b0}}), .in26({32{1'b0}}),
    .in27({32{1'b0}}), .in28({32{1'b0}}), .in29({32{1'b0}}), .in30({32{1'b0}}), .in31({32{1'b0}}),
    .out(out_21), .sel(bit_extender_2_out));
  Multiplexer #(.select(5), .width(32), .enable("false")) multiplexer_6 (
    .in0({32{1'b0}}), .in1(in_9), .in2(_5), .in3(_4), .in4(in_4), .in5(_2), .in6(in_1), .in7({32{1'b0}}),
    .in8({32{1'b0}}), .in9({32{1'b0}}), .in10({32{1'b0}}), .in11({32{1'b0}}), .in12({32{1'b0}}),
    .in13({32{1'b0}}), .in14({32{1'b0}}), .in15({32{1'b0}}), .in16({32{1'b0}}), .in17({32{1'b0}}),
    .in18({32{1'b0}}), .in19({32{1'b0}}), .in20({32{1'b0}}), .in21({32{1'b0}}), .in22({32{1'b0}}),
    .in23({32{1'b0}}), .in24({32{1'b0}}), .in25({32{1'b0}}), .in26({32{1'b0}}), .in27({32{1'b0}}),
    .in28({32{1'b0}}), .in29({32{1'b0}}), .in30({32{1'b0}}), .in31({32{1'b0}}), .out(out_22),
    .sel(bit_extender_2_out));
  Multiplexer #(.select(5), .width(32), .enable("false")) multiplexer_7 (
    .in0({32{1'b0}}), .in1(_7), .in2(in_9), .in3(_5), .in4(_4), .in5(in_4), .in6(_2), .in7(in_1),
    .in8({32{1'b0}}), .in9({32{1'b0}}), .in10({32{1'b0}}), .in11({32{1'b0}}), .in12({32{1'b0}}),
    .in13({32{1'b0}}), .in14({32{1'b0}}), .in15({32{1'b0}}), .in16({32{1'b0}}), .in17({32{1'b0}}),
    .in18({32{1'b0}}), .in19({32{1'b0}}), .in20({32{1'b0}}), .in21({32{1'b0}}), .in22({32{1'b0}}),
    .in23({32{1'b0}}), .in24({32{1'b0}}), .in25({32{1'b0}}), .in26({32{1'b0}}), .in27({32{1'b0}}),
    .in28({32{1'b0}}), .in29({32{1'b0}}), .in30({32{1'b0}}), .in31({32{1'b0}}), .out(out_23),
    .sel(bit_extender_2_out));
  Multiplexer #(.select(5), .width(32), .enable("false")) multiplexer_8 (
    .in0({32{1'b0}}), .in1(_8), .in2(_7), .in3(in_9), .in4(_5), .in5(_4), .in6(in_4), .in7(_2), .in8(in_1),
    .in9({32{1'b0}}), .in10({32{1'b0}}), .in11({32{1'b0}}), .in12({32{1'b0}}), .in13({32{1'b0}}),
    .in14({32{1'b0}}), .in15({32{1'b0}}), .in16({32{1'b0}}), .in17({32{1'b0}}), .in18({32{1'b0}}),
    .in19({32{1'b0}}), .in20({32{1'b0}}), .in21({32{1'b0}}), .in22({32{1'b0}}), .in23({32{1'b0}}),
    .in24({32{1'b0}}), .in25({32{1'b0}}), .in26({32{1'b0}}), .in27({32{1'b0}}), .in28({32{1'b0}}),
    .in29({32{1'b0}}), .in30({32{1'b0}}), .in31({32{1'b0}}), .out(out_24), .sel(bit_extender_2_out));
  Multiplexer #(.select(5), .width(32), .enable("false")) multiplexer_9 (
    .in0({32{1'b0}}), .in1(in_12), .in2(_8), .in3(_7), .in4(in_9), .in5(_5), .in6(_4), .in7(in_4), .in8(_2),
    .in9(in_1), .in10({32{1'b0}}), .in11({32{1'b0}}), .in12({32{1'b0}}), .in13({32{1'b0}}),
    .in14({32{1'b0}}), .in15({32{1'b0}}), .in16({32{1'b0}}), .in17({32{1'b0}}), .in18({32{1'b0}}),
    .in19({32{1'b0}}), .in20({32{1'b0}}), .in21({32{1'b0}}), .in22({32{1'b0}}), .in23({32{1'b0}}),
    .in24({32{1'b0}}), .in25({32{1'b0}}), .in26({32{1'b0}}), .in27({32{1'b0}}), .in28({32{1'b0}}),
    .in29({32{1'b0}}), .in30({32{1'b0}}), .in31({32{1'b0}}), .out(out_25), .sel(bit_extender_2_out));
  Multiplexer #(.select(5), .width(32), .enable("false")) multiplexer_10 (
    .in0({32{1'b0}}), .in1(_10), .in2(in_12), .in3(_8), .in4(_7), .in5(in_9), .in6(_5), .in7(_4), .in8(in_4),
    .in9(_2), .in10(in_1), .in11({32{1'b0}}), .in12({32{1'b0}}), .in13({32{1'b0}}), .in14({32{1'b0}}),
    .in15({32{1'b0}}), .in16({32{1'b0}}), .in17({32{1'b0}}), .in18({32{1'b0}}), .in19({32{1'b0}}),
    .in20({32{1'b0}}), .in21({32{1'b0}}), .in22({32{1'b0}}), .in23({32{1'b0}}), .in24({32{1'b0}}),
    .in25({32{1'b0}}), .in26({32{1'b0}}), .in27({32{1'b0}}), .in28({32{1'b0}}), .in29({32{1'b0}}),
    .in30({32{1'b0}}), .in31({32{1'b0}}), .out(out_26), .sel(bit_extender_2_out));
  Multiplexer #(.select(5), .width(32), .enable("false")) multiplexer_11 (
    .in0({32{1'b0}}), .in1(_11), .in2(_10), .in3(in_12), .in4(_8), .in5(_7), .in6(in_9), .in7(_5), .in8(_4),
    .in9(in_4), .in10(_2), .in11(in_1), .in12({32{1'b0}}), .in13({32{1'b0}}), .in14({32{1'b0}}),
    .in15({32{1'b0}}), .in16({32{1'b0}}), .in17({32{1'b0}}), .in18({32{1'b0}}), .in19({32{1'b0}}),
    .in20({32{1'b0}}), .in21({32{1'b0}}), .in22({32{1'b0}}), .in23({32{1'b0}}), .in24({32{1'b0}}),
    .in25({32{1'b0}}), .in26({32{1'b0}}), .in27({32{1'b0}}), .in28({32{1'b0}}), .in29({32{1'b0}}),
    .in30({32{1'b0}}), .in31({32{1'b0}}), .out(out_27), .sel(bit_extender_2_out));
  Multiplexer #(.select(5), .width(32), .enable("false")) multiplexer_12 (
    .in0({32{1'b0}}), .in1(_12), .in2(_11), .in3(_10), .in4(in_12), .in5(_8), .in6(_7), .in7(in_9), .in8(_5),
    .in9(_4), .in10(in_4), .in11(_2), .in12(in_1), .in13({32{1'b0}}), .in14({32{1'b0}}), .in15({32{1'b0}}),
    .in16({32{1'b0}}), .in17({32{1'b0}}), .in18({32{1'b0}}), .in19({32{1'b0}}), .in20({32{1'b0}}),
    .in21({32{1'b0}}), .in22({32{1'b0}}), .in23({32{1'b0}}), .in24({32{1'b0}}), .in25({32{1'b0}}),
    .in26({32{1'b0}}), .in27({32{1'b0}}), .in28({32{1'b0}}), .in29({32{1'b0}}), .in30({32{1'b0}}),
    .in31({32{1'b0}}), .out(out_28), .sel(bit_extender_2_out));
  Multiplexer #(.select(5), .width(32), .enable("false")) multiplexer_13 (
    .in0({32{1'b0}}), .in1(in_16), .in2(_12), .in3(_11), .in4(_10), .in5(in_12), .in6(_8), .in7(_7),
    .in8(in_9), .in9(_5), .in10(_4), .in11(in_4), .in12(_2), .in13(in_1), .in14({32{1'b0}}),
    .in15({32{1'b0}}), .in16({32{1'b0}}), .in17({32{1'b0}}), .in18({32{1'b0}}), .in19({32{1'b0}}),
    .in20({32{1'b0}}), .in21({32{1'b0}}), .in22({32{1'b0}}), .in23({32{1'b0}}), .in24({32{1'b0}}),
    .in25({32{1'b0}}), .in26({32{1'b0}}), .in27({32{1'b0}}), .in28({32{1'b0}}), .in29({32{1'b0}}),
    .in30({32{1'b0}}), .in31({32{1'b0}}), .out(out_29), .sel(bit_extender_2_out));
  Multiplexer #(.select(5), .width(32), .enable("false")) multiplexer_14 (
    .in0({32{1'b0}}), .in1({32{1'b0}}), .in2(in_16), .in3(_12), .in4(_11), .in5(_10), .in6(in_12), .in7(_8),
    .in8(_7), .in9(in_9), .in10(_5), .in11(_4), .in12(in_4), .in13(_2), .in14(in_1), .in15({32{1'b0}}),
    .in16({32{1'b0}}), .in17({32{1'b0}}), .in18({32{1'b0}}), .in19({32{1'b0}}), .in20({32{1'b0}}),
    .in21({32{1'b0}}), .in22({32{1'b0}}), .in23({32{1'b0}}), .in24({32{1'b0}}), .in25({32{1'b0}}),
    .in26({32{1'b0}}), .in27({32{1'b0}}), .in28({32{1'b0}}), .in29({32{1'b0}}), .in30({32{1'b0}}),
    .in31({32{1'b0}}), .out(out_30), .sel(bit_extender_2_out));
  Multiplexer #(.select(5), .width(32), .enable("false")) multiplexer_15 (
    .in0({32{1'b0}}), .in1({32{1'b0}}), .in2({32{1'b0}}), .in3(in_16), .in4(_12), .in5(_11), .in6(_10),
    .in7(in_12), .in8(_8), .in9(_7), .in10(in_9), .in11(_5), .in12(_4), .in13(in_4), .in14(_2), .in15(in_1),
    .in16({32{1'b0}}), .in17({32{1'b0}}), .in18({32{1'b0}}), .in19({32{1'b0}}), .in20({32{1'b0}}),
    .in21({32{1'b0}}), .in22({32{1'b0}}), .in23({32{1'b0}}), .in24({32{1'b0}}), .in25({32{1'b0}}),
    .in26({32{1'b0}}), .in27({32{1'b0}}), .in28({32{1'b0}}), .in29({32{1'b0}}), .in30({32{1'b0}}),
    .in31({32{1'b0}}), .out(out_31), .sel(bit_extender_2_out));
  Multiplexer #(.select(5), .width(32), .enable("false")) multiplexer_16 (
    .in0({32{1'b0}}), .in1({32{1'b0}}), .in2({32{1'b0}}), .in3({32{1'b0}}), .in4(in_16), .in5(_12),
    .in6(_11), .in7(_10), .in8(in_12), .in9(_8), .in10(_7), .in11(in_9), .in12(_5), .in13(_4), .in14(in_4),
    .in15(_2), .in16(in_1), .in17({32{1'b0}}), .in18({32{1'b0}}), .in19({32{1'b0}}), .in20({32{1'b0}}),
    .in21({32{1'b0}}), .in22({32{1'b0}}), .in23({32{1'b0}}), .in24({32{1'b0}}), .in25({32{1'b0}}),
    .in26({32{1'b0}}), .in27({32{1'b0}}), .in28({32{1'b0}}), .in29({32{1'b0}}), .in30({32{1'b0}}),
    .in31({32{1'b0}}), .out(out_32), .sel(bit_extender_2_out));
  Multiplexer #(.select(5), .width(32), .enable("false")) multiplexer_17 (
    .in0({32{1'b0}}), .in1({32{1'b0}}), .in2({32{1'b0}}), .in3({32{1'b0}}), .in4({32{1'b0}}), .in5(in_16),
    .in6(_12), .in7(_11), .in8(_10), .in9(in_12), .in10(_8), .in11(_7), .in12(in_9), .in13(_5), .in14(_4),
    .in15(in_4), .in16(_2), .in17(in_1), .in18({32{1'b0}}), .in19({32{1'b0}}), .in20({32{1'b0}}),
    .in21({32{1'b0}}), .in22({32{1'b0}}), .in23({32{1'b0}}), .in24({32{1'b0}}), .in25({32{1'b0}}),
    .in26({32{1'b0}}), .in27({32{1'b0}}), .in28({32{1'b0}}), .in29({32{1'b0}}), .in30({32{1'b0}}),
    .in31({32{1'b0}}), .out(out_33), .sel(bit_extender_2_out));
  Multiplexer #(.select(5), .width(32), .enable("false")) multiplexer_18 (
    .in0({32{1'b0}}), .in1({32{1'b0}}), .in2({32{1'b0}}), .in3({32{1'b0}}), .in4({32{1'b0}}),
    .in5({32{1'b0}}), .in6(in_16), .in7(_12), .in8(_11), .in9(_10), .in10(in_12), .in11(_8), .in12(_7),
    .in13(in_9), .in14(_5), .in15(_4), .in16(in_4), .in17(_2), .in18(in_1), .in19({32{1'b0}}),
    .in20({32{1'b0}}), .in21({32{1'b0}}), .in22({32{1'b0}}), .in23({32{1'b0}}), .in24({32{1'b0}}),
    .in25({32{1'b0}}), .in26({32{1'b0}}), .in27({32{1'b0}}), .in28({32{1'b0}}), .in29({32{1'b0}}),
    .in30({32{1'b0}}), .in31({32{1'b0}}), .out(out_34), .sel(bit_extender_2_out));
  Multiplexer #(.select(5), .width(32), .enable("false")) multiplexer_19 (
    .in0({32{1'b0}}), .in1({32{1'b0}}), .in2({32{1'b0}}), .in3({32{1'b0}}), .in4({32{1'b0}}),
    .in5({32{1'b0}}), .in6({32{1'b0}}), .in7(in_16), .in8(_12), .in9(_11), .in10(_10), .in11(in_12),
    .in12(_8), .in13(_7), .in14(in_9), .in15(_5), .in16(_4), .in17(in_4), .in18(_2), .in19(in_1),
    .in20({32{1'b0}}), .in21({32{1'b0}}), .in22({32{1'b0}}), .in23({32{1'b0}}), .in24({32{1'b0}}),
    .in25({32{1'b0}}), .in26({32{1'b0}}), .in27({32{1'b0}}), .in28({32{1'b0}}), .in29({32{1'b0}}),
    .in30({32{1'b0}}), .in31({32{1'b0}}), .out(out_35), .sel(bit_extender_2_out));
  Multiplexer #(.select(5), .width(32), .enable("false")) multiplexer_20 (
    .in0({32{1'b0}}), .in1({32{1'b0}}), .in2({32{1'b0}}), .in3({32{1'b0}}), .in4({32{1'b0}}),
    .in5({32{1'b0}}), .in6({32{1'b0}}), .in7({32{1'b0}}), .in8(in_16), .in9(_12), .in10(_11), .in11(_10),
    .in12(in_12), .in13(_8), .in14(_7), .in15(in_9), .in16(_5), .in17(_4), .in18(in_4), .in19(_2),
    .in20(in_1), .in21({32{1'b0}}), .in22({32{1'b0}}), .in23({32{1'b0}}), .in24({32{1'b0}}),
    .in25({32{1'b0}}), .in26({32{1'b0}}), .in27({32{1'b0}}), .in28({32{1'b0}}), .in29({32{1'b0}}),
    .in30({32{1'b0}}), .in31({32{1'b0}}), .out(out_36), .sel(bit_extender_2_out));
  Multiplexer #(.select(5), .width(32), .enable("false")) multiplexer_21 (
    .in0({32{1'b0}}), .in1({32{1'b0}}), .in2({32{1'b0}}), .in3({32{1'b0}}), .in4({32{1'b0}}),
    .in5({32{1'b0}}), .in6({32{1'b0}}), .in7({32{1'b0}}), .in8({32{1'b0}}), .in9(in_16), .in10(_12),
    .in11(_11), .in12(_10), .in13(in_12), .in14(_8), .in15(_7), .in16(in_9), .in17(_5), .in18(_4),
    .in19(in_4), .in20(_2), .in21(in_1), .in22({32{1'b0}}), .in23({32{1'b0}}), .in24({32{1'b0}}),
    .in25({32{1'b0}}), .in26({32{1'b0}}), .in27({32{1'b0}}), .in28({32{1'b0}}), .in29({32{1'b0}}),
    .in30({32{1'b0}}), .in31({32{1'b0}}), .out(out_37), .sel(bit_extender_2_out));
  Multiplexer #(.select(5), .width(32), .enable("false")) multiplexer_22 (
    .in0({32{1'b0}}), .in1({32{1'b0}}), .in2({32{1'b0}}), .in3({32{1'b0}}), .in4({32{1'b0}}),
    .in5({32{1'b0}}), .in6({32{1'b0}}), .in7({32{1'b0}}), .in8({32{1'b0}}), .in9({32{1'b0}}), .in10(in_16),
    .in11(_12), .in12(_11), .in13(_10), .in14(in_12), .in15(_8), .in16(_7), .in17(in_9), .in18(_5),
    .in19(_4), .in20(in_4), .in21(_2), .in22(in_1), .in23({32{1'b0}}), .in24({32{1'b0}}), .in25({32{1'b0}}),
    .in26({32{1'b0}}), .in27({32{1'b0}}), .in28({32{1'b0}}), .in29({32{1'b0}}), .in30({32{1'b0}}),
    .in31({32{1'b0}}), .out(out_38), .sel(bit_extender_2_out));
  Multiplexer #(.select(5), .width(32), .enable("false")) multiplexer_23 (
    .in0({32{1'b0}}), .in1({32{1'b0}}), .in2({32{1'b0}}), .in3({32{1'b0}}), .in4({32{1'b0}}),
    .in5({32{1'b0}}), .in6({32{1'b0}}), .in7({32{1'b0}}), .in8({32{1'b0}}), .in9({32{1'b0}}),
    .in10({32{1'b0}}), .in11(in_16), .in12(_12), .in13(_11), .in14(_10), .in15(in_12), .in16(_8), .in17(_7),
    .in18(in_9), .in19(_5), .in20(_4), .in21(in_4), .in22(_2), .in23(in_1), .in24({32{1'b0}}),
    .in25({32{1'b0}}), .in26({32{1'b0}}), .in27({32{1'b0}}), .in28({32{1'b0}}), .in29({32{1'b0}}),
    .in30({32{1'b0}}), .in31({32{1'b0}}), .out(out_39), .sel(bit_extender_2_out));
  Multiplexer #(.select(5), .width(32), .enable("false")) multiplexer_24 (
    .in0({32{1'b0}}), .in1({32{1'b0}}), .in2({32{1'b0}}), .in3({32{1'b0}}), .in4({32{1'b0}}),
    .in5({32{1'b0}}), .in6({32{1'b0}}), .in7({32{1'b0}}), .in8({32{1'b0}}), .in9({32{1'b0}}),
    .in10({32{1'b0}}), .in11({32{1'b0}}), .in12(in_16), .in13(_12), .in14(_11), .in15(_10), .in16(in_12),
    .in17(_8), .in18(_7), .in19(in_9), .in20(_5), .in21(_4), .in22(in_4), .in23(_2), .in24(in_1),
    .in25({32{1'b0}}), .in26({32{1'b0}}), .in27({32{1'b0}}), .in28({32{1'b0}}), .in29({32{1'b0}}),
    .in30({32{1'b0}}), .in31({32{1'b0}}), .out(out_40), .sel(bit_extender_2_out));
  Multiplexer #(.select(5), .width(32), .enable("false")) multiplexer_25 (
    .in0({32{1'b0}}), .in1({32{1'b0}}), .in2({32{1'b0}}), .in3({32{1'b0}}), .in4({32{1'b0}}),
    .in5({32{1'b0}}), .in6({32{1'b0}}), .in7({32{1'b0}}), .in8({32{1'b0}}), .in9({32{1'b0}}),
    .in10({32{1'b0}}), .in11({32{1'b0}}), .in12({32{1'b0}}), .in13(in_16), .in14(_12), .in15(_11),
    .in16(_10), .in17(in_12), .in18(_8), .in19(_7), .in20(in_9), .in21(_5), .in22(_4), .in23(in_4),
    .in24(_2), .in25(in_1), .in26({32{1'b0}}), .in27({32{1'b0}}), .in28({32{1'b0}}), .in29({32{1'b0}}),
    .in30({32{1'b0}}), .in31({32{1'b0}}), .out(out_41), .sel(bit_extender_2_out));
  Multiplexer #(.select(5), .width(32), .enable("false")) multiplexer_26 (
    .in0({32{1'b0}}), .in1({32{1'b0}}), .in2({32{1'b0}}), .in3({32{1'b0}}), .in4({32{1'b0}}),
    .in5({32{1'b0}}), .in6({32{1'b0}}), .in7({32{1'b0}}), .in8({32{1'b0}}), .in9({32{1'b0}}),
    .in10({32{1'b0}}), .in11({32{1'b0}}), .in12({32{1'b0}}), .in13({32{1'b0}}), .in14(in_16), .in15(_12),
    .in16(_11), .in17(_10), .in18(in_12), .in19(_8), .in20(_7), .in21(in_9), .in22(_5), .in23(_4),
    .in24(in_4), .in25(_2), .in26(in_1), .in27({32{1'b0}}), .in28({32{1'b0}}), .in29({32{1'b0}}),
    .in30({32{1'b0}}), .in31({32{1'b0}}), .out(out_42), .sel(bit_extender_2_out));
  Multiplexer #(.select(5), .width(32), .enable("false")) multiplexer_27 (
    .in0({32{1'b0}}), .in1({32{1'b0}}), .in2({32{1'b0}}), .in3({32{1'b0}}), .in4({32{1'b0}}),
    .in5({32{1'b0}}), .in6({32{1'b0}}), .in7({32{1'b0}}), .in8({32{1'b0}}), .in9({32{1'b0}}),
    .in10({32{1'b0}}), .in11({32{1'b0}}), .in12({32{1'b0}}), .in13({32{1'b0}}), .in14({32{1'b0}}),
    .in15(in_16), .in16(_12), .in17(_11), .in18(_10), .in19(in_12), .in20(_8), .in21(_7), .in22(in_9),
    .in23(_5), .in24(_4), .in25(in_4), .in26(_2), .in27(in_1), .in28({32{1'b0}}), .in29({32{1'b0}}),
    .in30({32{1'b0}}), .in31({32{1'b0}}), .out(out_43), .sel(bit_extender_2_out));
  Multiplexer #(.select(5), .width(32), .enable("false")) multiplexer_28 (
    .in0({32{1'b0}}), .in1({32{1'b0}}), .in2({32{1'b0}}), .in3({32{1'b0}}), .in4({32{1'b0}}),
    .in5({32{1'b0}}), .in6({32{1'b0}}), .in7({32{1'b0}}), .in8({32{1'b0}}), .in9({32{1'b0}}),
    .in10({32{1'b0}}), .in11({32{1'b0}}), .in12({32{1'b0}}), .in13({32{1'b0}}), .in14({32{1'b0}}),
    .in15({32{1'b0}}), .in16(in_16), .in17(_12), .in18(_11), .in19(_10), .in20(in_12), .in21(_8), .in22(_7),
    .in23(in_9), .in24(_5), .in25(_4), .in26(in_4), .in27(_2), .in28(in_1), .in29({32{1'b0}}),
    .in30({32{1'b0}}), .in31({32{1'b0}}), .out(out_44), .sel(bit_extender_2_out));
  Multiplexer #(.select(5), .width(32), .enable("false")) multiplexer_29 (
    .in0({32{1'b0}}), .in1({32{1'b0}}), .in2({32{1'b0}}), .in3({32{1'b0}}), .in4({32{1'b0}}),
    .in5({32{1'b0}}), .in6({32{1'b0}}), .in7({32{1'b0}}), .in8({32{1'b0}}), .in9({32{1'b0}}),
    .in10({32{1'b0}}), .in11({32{1'b0}}), .in12({32{1'b0}}), .in13({32{1'b0}}), .in14({32{1'b0}}),
    .in15({32{1'b0}}), .in16({32{1'b0}}), .in17(in_16), .in18(_12), .in19(_11), .in20(_10), .in21(in_12),
    .in22(_8), .in23(_7), .in24(in_9), .in25(_5), .in26(_4), .in27(in_4), .in28(_2), .in29(in_1),
    .in30({32{1'b0}}), .in31({32{1'b0}}), .out(out_45), .sel(bit_extender_2_out));
  Multiplexer #(.select(5), .width(32), .enable("false")) multiplexer_30 (
    .in0({32{1'b0}}), .in1({32{1'b0}}), .in2({32{1'b0}}), .in3({32{1'b0}}), .in4({32{1'b0}}),
    .in5({32{1'b0}}), .in6({32{1'b0}}), .in7({32{1'b0}}), .in8({32{1'b0}}), .in9({32{1'b0}}),
    .in10({32{1'b0}}), .in11({32{1'b0}}), .in12({32{1'b0}}), .in13({32{1'b0}}), .in14({32{1'b0}}),
    .in15({32{1'b0}}), .in16({32{1'b0}}), .in17({32{1'b0}}), .in18(in_16), .in19(_12), .in20(_11),
    .in21(_10), .in22(in_12), .in23(_8), .in24(_7), .in25(in_9), .in26(_5), .in27(_4), .in28(in_4),
    .in29(_2), .in30(in_1), .in31({32{1'b0}}), .out(out_46), .sel(bit_extender_2_out));
  Multiplexer #(.select(5), .width(32), .enable("false")) multiplexer_31 (
    .in0({32{1'b0}}), .in1({32{1'b0}}), .in2({32{1'b0}}), .in3({32{1'b0}}), .in4({32{1'b0}}),
    .in5({32{1'b0}}), .in6({32{1'b0}}), .in7({32{1'b0}}), .in8({32{1'b0}}), .in9({32{1'b0}}),
    .in10({32{1'b0}}), .in11({32{1'b0}}), .in12({32{1'b0}}), .in13({32{1'b0}}), .in14({32{1'b0}}),
    .in15({32{1'b0}}), .in16({32{1'b0}}), .in17({32{1'b0}}), .in18({32{1'b0}}), .in19(in_16), .in20(_12),
    .in21(_11), .in22(_10), .in23(in_12), .in24(_8), .in25(_7), .in26(in_9), .in27(_5), .in28(_4),
    .in29(in_4), .in30(_2), .in31(in_1), .out(out_47), .sel(bit_extender_2_out));
  Multiplexer #(.select(5), .width(32), .enable("false")) multiplexer_32 (
    .in0({32{1'b0}}), .in1({32{1'b0}}), .in2({32{1'b0}}), .in3({32{1'b0}}), .in4({32{1'b0}}),
    .in5({32{1'b0}}), .in6({32{1'b0}}), .in7({32{1'b0}}), .in8({32{1'b0}}), .in9({32{1'b0}}),
    .in10({32{1'b0}}), .in11({32{1'b0}}), .in12({32{1'b0}}), .in13({32{1'b0}}), .in14({32{1'b0}}),
    .in15({32{1'b0}}), .in16({32{1'b0}}), .in17({32{1'b0}}), .in18({32{1'b0}}), .in19({32{1'b0}}),
    .in20(in_16), .in21(_12), .in22(_11), .in23(_10), .in24(in_12), .in25(_8), .in26(_7), .in27(in_9),
    .in28(_5), .in29(_4), .in30(in_4), .in31(_2), .out(multiplexer_32_out), .sel(bit_extender_2_out));
  Multiplexer #(.select(5), .width(32), .enable("false")) multiplexer_33 (
    .in0({32{1'b0}}), .in1({32{1'b0}}), .in2({32{1'b0}}), .in3(in_16), .in4(_12), .in5(_11), .in6(_10),
    .in7(in_12), .in8(_8), .in9(_7), .in10(in_9), .in11(_5), .in12(_4), .in13(in_4), .in14(_2), .in15(in_1),
    .in16({32{1'b0}}), .in17({32{1'b0}}), .in18({32{1'b0}}), .in19({32{1'b0}}), .in20({32{1'b0}}),
    .in21({32{1'b0}}), .in22({32{1'b0}}), .in23({32{1'b0}}), .in24({32{1'b0}}), .in25({32{1'b0}}),
    .in26({32{1'b0}}), .in27({32{1'b0}}), .in28({32{1'b0}}), .in29({32{1'b0}}), .in30({32{1'b0}}),
    .in31({32{1'b0}}), .out(out_49), .sel(bit_extender_1_out));
  Multiplexer #(.select(5), .width(32), .enable("false")) multiplexer_34 (
    .in0({32{1'b0}}), .in1({32{1'b0}}), .in2({32{1'b0}}), .in3({32{1'b0}}), .in4(in_16), .in5(_12),
    .in6(_11), .in7(_10), .in8(in_12), .in9(_8), .in10(_7), .in11(in_9), .in12(_5), .in13(_4), .in14(in_4),
    .in15(_2), .in16(in_1), .in17({32{1'b0}}), .in18({32{1'b0}}), .in19({32{1'b0}}), .in20({32{1'b0}}),
    .in21({32{1'b0}}), .in22({32{1'b0}}), .in23({32{1'b0}}), .in24({32{1'b0}}), .in25({32{1'b0}}),
    .in26({32{1'b0}}), .in27({32{1'b0}}), .in28({32{1'b0}}), .in29({32{1'b0}}), .in30({32{1'b0}}),
    .in31({32{1'b0}}), .out(out_50), .sel(bit_extender_1_out));
  Multiplexer #(.select(5), .width(32), .enable("false")) multiplexer_35 (
    .in0({32{1'b0}}), .in1({32{1'b0}}), .in2({32{1'b0}}), .in3({32{1'b0}}), .in4({32{1'b0}}), .in5(in_16),
    .in6(_12), .in7(_11), .in8(_10), .in9(in_12), .in10(_8), .in11(_7), .in12(in_9), .in13(_5), .in14(_4),
    .in15(in_4), .in16(_2), .in17(in_1), .in18({32{1'b0}}), .in19({32{1'b0}}), .in20({32{1'b0}}),
    .in21({32{1'b0}}), .in22({32{1'b0}}), .in23({32{1'b0}}), .in24({32{1'b0}}), .in25({32{1'b0}}),
    .in26({32{1'b0}}), .in27({32{1'b0}}), .in28({32{1'b0}}), .in29({32{1'b0}}), .in30({32{1'b0}}),
    .in31({32{1'b0}}), .out(out_51), .sel(bit_extender_1_out));
  Multiplexer #(.select(5), .width(32), .enable("false")) multiplexer_36 (
    .in0({32{1'b0}}), .in1({32{1'b0}}), .in2({32{1'b0}}), .in3({32{1'b0}}), .in4({32{1'b0}}),
    .in5({32{1'b0}}), .in6(in_16), .in7(_12), .in8(_11), .in9(_10), .in10(in_12), .in11(_8), .in12(_7),
    .in13(in_9), .in14(_5), .in15(_4), .in16(in_4), .in17(_2), .in18(in_1), .in19({32{1'b0}}),
    .in20({32{1'b0}}), .in21({32{1'b0}}), .in22({32{1'b0}}), .in23({32{1'b0}}), .in24({32{1'b0}}),
    .in25({32{1'b0}}), .in26({32{1'b0}}), .in27({32{1'b0}}), .in28({32{1'b0}}), .in29({32{1'b0}}),
    .in30({32{1'b0}}), .in31({32{1'b0}}), .out(out_52), .sel(bit_extender_1_out));
  Multiplexer #(.select(5), .width(32), .enable("false")) multiplexer_37 (
    .in0({32{1'b0}}), .in1({32{1'b0}}), .in2({32{1'b0}}), .in3({32{1'b0}}), .in4({32{1'b0}}),
    .in5({32{1'b0}}), .in6({32{1'b0}}), .in7(in_16), .in8(_12), .in9(_11), .in10(_10), .in11(in_12),
    .in12(_8), .in13(_7), .in14(in_9), .in15(_5), .in16(_4), .in17(in_4), .in18(_2), .in19(in_1),
    .in20({32{1'b0}}), .in21({32{1'b0}}), .in22({32{1'b0}}), .in23({32{1'b0}}), .in24({32{1'b0}}),
    .in25({32{1'b0}}), .in26({32{1'b0}}), .in27({32{1'b0}}), .in28({32{1'b0}}), .in29({32{1'b0}}),
    .in30({32{1'b0}}), .in31({32{1'b0}}), .out(out_53), .sel(bit_extender_1_out));
  Multiplexer #(.select(5), .width(32), .enable("false")) multiplexer_38 (
    .in0({32{1'b0}}), .in1({32{1'b0}}), .in2({32{1'b0}}), .in3({32{1'b0}}), .in4({32{1'b0}}),
    .in5({32{1'b0}}), .in6({32{1'b0}}), .in7({32{1'b0}}), .in8(in_16), .in9(_12), .in10(_11), .in11(_10),
    .in12(in_12), .in13(_8), .in14(_7), .in15(in_9), .in16(_5), .in17(_4), .in18(in_4), .in19(_2),
    .in20(in_1), .in21({32{1'b0}}), .in22({32{1'b0}}), .in23({32{1'b0}}), .in24({32{1'b0}}),
    .in25({32{1'b0}}), .in26({32{1'b0}}), .in27({32{1'b0}}), .in28({32{1'b0}}), .in29({32{1'b0}}),
    .in30({32{1'b0}}), .in31({32{1'b0}}), .out(out_54), .sel(bit_extender_1_out));
  Multiplexer #(.select(5), .width(32), .enable("false")) multiplexer_39 (
    .in0({32{1'b0}}), .in1({32{1'b0}}), .in2({32{1'b0}}), .in3({32{1'b0}}), .in4({32{1'b0}}),
    .in5({32{1'b0}}), .in6({32{1'b0}}), .in7({32{1'b0}}), .in8({32{1'b0}}), .in9(in_16), .in10(_12),
    .in11(_11), .in12(_10), .in13(in_12), .in14(_8), .in15(_7), .in16(in_9), .in17(_5), .in18(_4),
    .in19(in_4), .in20(_2), .in21(in_1), .in22({32{1'b0}}), .in23({32{1'b0}}), .in24({32{1'b0}}),
    .in25({32{1'b0}}), .in26({32{1'b0}}), .in27({32{1'b0}}), .in28({32{1'b0}}), .in29({32{1'b0}}),
    .in30({32{1'b0}}), .in31({32{1'b0}}), .out(out_55), .sel(bit_extender_1_out));
  Multiplexer #(.select(5), .width(32), .enable("false")) multiplexer_40 (
    .in0({32{1'b0}}), .in1({32{1'b0}}), .in2({32{1'b0}}), .in3({32{1'b0}}), .in4({32{1'b0}}),
    .in5({32{1'b0}}), .in6({32{1'b0}}), .in7({32{1'b0}}), .in8({32{1'b0}}), .in9({32{1'b0}}), .in10(in_16),
    .in11(_12), .in12(_11), .in13(_10), .in14(in_12), .in15(_8), .in16(_7), .in17(in_9), .in18(_5),
    .in19(_4), .in20(in_4), .in21(_2), .in22(in_1), .in23({32{1'b0}}), .in24({32{1'b0}}), .in25({32{1'b0}}),
    .in26({32{1'b0}}), .in27({32{1'b0}}), .in28({32{1'b0}}), .in29({32{1'b0}}), .in30({32{1'b0}}),
    .in31({32{1'b0}}), .out(out_56), .sel(bit_extender_1_out));
  Multiplexer #(.select(5), .width(32), .enable("false")) multiplexer_41 (
    .in0({32{1'b0}}), .in1({32{1'b0}}), .in2({32{1'b0}}), .in3({32{1'b0}}), .in4({32{1'b0}}),
    .in5({32{1'b0}}), .in6({32{1'b0}}), .in7({32{1'b0}}), .in8({32{1'b0}}), .in9({32{1'b0}}),
    .in10({32{1'b0}}), .in11(in_16), .in12(_12), .in13(_11), .in14(_10), .in15(in_12), .in16(_8), .in17(_7),
    .in18(in_9), .in19(_5), .in20(_4), .in21(in_4), .in22(_2), .in23(in_1), .in24({32{1'b0}}),
    .in25({32{1'b0}}), .in26({32{1'b0}}), .in27({32{1'b0}}), .in28({32{1'b0}}), .in29({32{1'b0}}),
    .in30({32{1'b0}}), .in31({32{1'b0}}), .out(out_57), .sel(bit_extender_1_out));
  Multiplexer #(.select(5), .width(32), .enable("false")) multiplexer_42 (
    .in0({32{1'b0}}), .in1({32{1'b0}}), .in2({32{1'b0}}), .in3({32{1'b0}}), .in4({32{1'b0}}),
    .in5({32{1'b0}}), .in6({32{1'b0}}), .in7({32{1'b0}}), .in8({32{1'b0}}), .in9({32{1'b0}}),
    .in10({32{1'b0}}), .in11({32{1'b0}}), .in12(in_16), .in13(_12), .in14(_11), .in15(_10), .in16(in_12),
    .in17(_8), .in18(_7), .in19(in_9), .in20(_5), .in21(_4), .in22(in_4), .in23(_2), .in24(in_1),
    .in25({32{1'b0}}), .in26({32{1'b0}}), .in27({32{1'b0}}), .in28({32{1'b0}}), .in29({32{1'b0}}),
    .in30({32{1'b0}}), .in31({32{1'b0}}), .out(out_58), .sel(bit_extender_1_out));
  Multiplexer #(.select(5), .width(32), .enable("false")) multiplexer_43 (
    .in0({32{1'b0}}), .in1({32{1'b0}}), .in2({32{1'b0}}), .in3({32{1'b0}}), .in4({32{1'b0}}),
    .in5({32{1'b0}}), .in6({32{1'b0}}), .in7({32{1'b0}}), .in8({32{1'b0}}), .in9({32{1'b0}}),
    .in10({32{1'b0}}), .in11({32{1'b0}}), .in12({32{1'b0}}), .in13(in_16), .in14(_12), .in15(_11),
    .in16(_10), .in17(in_12), .in18(_8), .in19(_7), .in20(in_9), .in21(_5), .in22(_4), .in23(in_4),
    .in24(_2), .in25(in_1), .in26({32{1'b0}}), .in27({32{1'b0}}), .in28({32{1'b0}}), .in29({32{1'b0}}),
    .in30({32{1'b0}}), .in31({32{1'b0}}), .out(out_59), .sel(bit_extender_1_out));
  Multiplexer #(.select(5), .width(32), .enable("false")) multiplexer_44 (
    .in0({32{1'b0}}), .in1({32{1'b0}}), .in2({32{1'b0}}), .in3({32{1'b0}}), .in4({32{1'b0}}),
    .in5({32{1'b0}}), .in6({32{1'b0}}), .in7({32{1'b0}}), .in8({32{1'b0}}), .in9({32{1'b0}}),
    .in10({32{1'b0}}), .in11({32{1'b0}}), .in12({32{1'b0}}), .in13({32{1'b0}}), .in14(in_16), .in15(_12),
    .in16(_11), .in17(_10), .in18(in_12), .in19(_8), .in20(_7), .in21(in_9), .in22(_5), .in23(_4),
    .in24(in_4), .in25(_2), .in26(in_1), .in27({32{1'b0}}), .in28({32{1'b0}}), .in29({32{1'b0}}),
    .in30({32{1'b0}}), .in31({32{1'b0}}), .out(out_60), .sel(bit_extender_1_out));
  Multiplexer #(.select(5), .width(32), .enable("false")) multiplexer_45 (
    .in0({32{1'b0}}), .in1({32{1'b0}}), .in2({32{1'b0}}), .in3({32{1'b0}}), .in4({32{1'b0}}),
    .in5({32{1'b0}}), .in6({32{1'b0}}), .in7({32{1'b0}}), .in8({32{1'b0}}), .in9({32{1'b0}}),
    .in10({32{1'b0}}), .in11({32{1'b0}}), .in12({32{1'b0}}), .in13({32{1'b0}}), .in14({32{1'b0}}),
    .in15(in_16), .in16(_12), .in17(_11), .in18(_10), .in19(in_12), .in20(_8), .in21(_7), .in22(in_9),
    .in23(_5), .in24(_4), .in25(in_4), .in26(_2), .in27(in_1), .in28({32{1'b0}}), .in29({32{1'b0}}),
    .in30({32{1'b0}}), .in31({32{1'b0}}), .out(out_61), .sel(bit_extender_1_out));
  Multiplexer #(.select(5), .width(32), .enable("false")) multiplexer_46 (
    .in0({32{1'b0}}), .in1({32{1'b0}}), .in2({32{1'b0}}), .in3({32{1'b0}}), .in4({32{1'b0}}),
    .in5({32{1'b0}}), .in6({32{1'b0}}), .in7({32{1'b0}}), .in8({32{1'b0}}), .in9({32{1'b0}}),
    .in10({32{1'b0}}), .in11({32{1'b0}}), .in12({32{1'b0}}), .in13({32{1'b0}}), .in14({32{1'b0}}),
    .in15({32{1'b0}}), .in16(in_16), .in17(_12), .in18(_11), .in19(_10), .in20(in_12), .in21(_8), .in22(_7),
    .in23(in_9), .in24(_5), .in25(_4), .in26(in_4), .in27(_2), .in28(in_1), .in29({32{1'b0}}),
    .in30({32{1'b0}}), .in31({32{1'b0}}), .out(out_62), .sel(bit_extender_1_out));
  Multiplexer #(.select(5), .width(32), .enable("false")) multiplexer_47 (
    .in0({32{1'b0}}), .in1({32{1'b0}}), .in2({32{1'b0}}), .in3({32{1'b0}}), .in4({32{1'b0}}),
    .in5({32{1'b0}}), .in6({32{1'b0}}), .in7({32{1'b0}}), .in8({32{1'b0}}), .in9({32{1'b0}}),
    .in10({32{1'b0}}), .in11({32{1'b0}}), .in12({32{1'b0}}), .in13({32{1'b0}}), .in14({32{1'b0}}),
    .in15({32{1'b0}}), .in16({32{1'b0}}), .in17(in_16), .in18(_12), .in19(_11), .in20(_10), .in21(in_12),
    .in22(_8), .in23(_7), .in24(in_9), .in25(_5), .in26(_4), .in27(in_4), .in28(_2), .in29(in_1),
    .in30({32{1'b0}}), .in31({32{1'b0}}), .out(out_63), .sel(bit_extender_1_out));
  Multiplexer #(.select(5), .width(32), .enable("false")) multiplexer_48 (
    .in0({32{1'b0}}), .in1({32{1'b0}}), .in2({32{1'b0}}), .in3({32{1'b0}}), .in4({32{1'b0}}),
    .in5({32{1'b0}}), .in6({32{1'b0}}), .in7({32{1'b0}}), .in8({32{1'b0}}), .in9({32{1'b0}}),
    .in10({32{1'b0}}), .in11({32{1'b0}}), .in12({32{1'b0}}), .in13({32{1'b0}}), .in14({32{1'b0}}),
    .in15({32{1'b0}}), .in16({32{1'b0}}), .in17({32{1'b0}}), .in18(in_16), .in19(_12), .in20(_11),
    .in21(_10), .in22(in_12), .in23(_8), .in24(_7), .in25(in_9), .in26(_5), .in27(_4), .in28(in_4),
    .in29(_2), .in30(in_1), .in31({32{1'b0}}), .out(out_64), .sel(bit_extender_1_out));
  Multiplexer #(.select(5), .width(32), .enable("false")) multiplexer_49 (
    .in0({32{1'b0}}), .in1({32{1'b0}}), .in2({32{1'b0}}), .in3({32{1'b0}}), .in4({32{1'b0}}),
    .in5({32{1'b0}}), .in6({32{1'b0}}), .in7({32{1'b0}}), .in8({32{1'b0}}), .in9({32{1'b0}}),
    .in10({32{1'b0}}), .in11({32{1'b0}}), .in12({32{1'b0}}), .in13({32{1'b0}}), .in14({32{1'b0}}),
    .in15({32{1'b0}}), .in16({32{1'b0}}), .in17({32{1'b0}}), .in18({32{1'b0}}), .in19(in_16), .in20(_12),
    .in21(_11), .in22(_10), .in23(in_12), .in24(_8), .in25(_7), .in26(in_9), .in27(_5), .in28(_4),
    .in29(in_4), .in30(_2), .in31(in_1), .out(out_65), .sel(bit_extender_1_out));
  Multiplexer #(.select(5), .width(32), .enable("false")) multiplexer_50 (
    .in0({32{1'b0}}), .in1({32{1'b0}}), .in2({32{1'b0}}), .in3({32{1'b0}}), .in4({32{1'b0}}),
    .in5({32{1'b0}}), .in6({32{1'b0}}), .in7({32{1'b0}}), .in8({32{1'b0}}), .in9({32{1'b0}}),
    .in10({32{1'b0}}), .in11({32{1'b0}}), .in12({32{1'b0}}), .in13({32{1'b0}}), .in14({32{1'b0}}),
    .in15({32{1'b0}}), .in16({32{1'b0}}), .in17({32{1'b0}}), .in18({32{1'b0}}), .in19({32{1'b0}}),
    .in20(in_16), .in21(_12), .in22(_11), .in23(_10), .in24(in_12), .in25(_8), .in26(_7), .in27(in_9),
    .in28(_5), .in29(_4), .in30(in_4), .in31(_2), .out(out_66), .sel(bit_extender_1_out));
  Multiplexer #(.select(5), .width(32), .enable("false")) multiplexer_51 (
    .in0({32{1'b0}}), .in1({32{1'b0}}), .in2({32{1'b0}}), .in3({32{1'b0}}), .in4({32{1'b0}}),
    .in5({32{1'b0}}), .in6({32{1'b0}}), .in7({32{1'b0}}), .in8({32{1'b0}}), .in9({32{1'b0}}),
    .in10({32{1'b0}}), .in11({32{1'b0}}), .in12({32{1'b0}}), .in13({32{1'b0}}), .in14({32{1'b0}}),
    .in15({32{1'b0}}), .in16({32{1'b0}}), .in17({32{1'b0}}), .in18({32{1'b0}}), .in19({32{1'b0}}),
    .in20({32{1'b0}}), .in21(in_16), .in22(_12), .in23(_11), .in24(_10), .in25(in_12), .in26(_8), .in27(_7),
    .in28(in_9), .in29(_5), .in30(_4), .in31(in_4), .out(out_67), .sel(bit_extender_1_out));
  Multiplexer #(.select(5), .width(32), .enable("false")) multiplexer_52 (
    .in0({32{1'b0}}), .in1({32{1'b0}}), .in2({32{1'b0}}), .in3({32{1'b0}}), .in4({32{1'b0}}),
    .in5({32{1'b0}}), .in6({32{1'b0}}), .in7({32{1'b0}}), .in8({32{1'b0}}), .in9({32{1'b0}}),
    .in10({32{1'b0}}), .in11({32{1'b0}}), .in12({32{1'b0}}), .in13({32{1'b0}}), .in14({32{1'b0}}),
    .in15({32{1'b0}}), .in16({32{1'b0}}), .in17({32{1'b0}}), .in18({32{1'b0}}), .in19({32{1'b0}}),
    .in20({32{1'b0}}), .in21({32{1'b0}}), .in22(in_16), .in23(_12), .in24(_11), .in25(_10), .in26(in_12),
    .in27(_8), .in28(_7), .in29(in_9), .in30(_5), .in31(_4), .out(out_68), .sel(bit_extender_1_out));
  Multiplexer #(.select(5), .width(32), .enable("false")) multiplexer_53 (
    .in0({32{1'b0}}), .in1({32{1'b0}}), .in2({32{1'b0}}), .in3({32{1'b0}}), .in4({32{1'b0}}),
    .in5({32{1'b0}}), .in6({32{1'b0}}), .in7({32{1'b0}}), .in8({32{1'b0}}), .in9({32{1'b0}}),
    .in10({32{1'b0}}), .in11({32{1'b0}}), .in12({32{1'b0}}), .in13({32{1'b0}}), .in14({32{1'b0}}),
    .in15({32{1'b0}}), .in16({32{1'b0}}), .in17({32{1'b0}}), .in18({32{1'b0}}), .in19({32{1'b0}}),
    .in20({32{1'b0}}), .in21({32{1'b0}}), .in22({32{1'b0}}), .in23(in_16), .in24(_12), .in25(_11),
    .in26(_10), .in27(in_12), .in28(_8), .in29(_7), .in30(in_9), .in31(_5), .out(out_69),
    .sel(bit_extender_1_out));
  Multiplexer #(.select(5), .width(32), .enable("false")) multiplexer_54 (
    .in0({32{1'b0}}), .in1({32{1'b0}}), .in2({32{1'b0}}), .in3({32{1'b0}}), .in4({32{1'b0}}),
    .in5({32{1'b0}}), .in6({32{1'b0}}), .in7({32{1'b0}}), .in8({32{1'b0}}), .in9({32{1'b0}}),
    .in10({32{1'b0}}), .in11({32{1'b0}}), .in12({32{1'b0}}), .in13({32{1'b0}}), .in14({32{1'b0}}),
    .in15({32{1'b0}}), .in16({32{1'b0}}), .in17({32{1'b0}}), .in18({32{1'b0}}), .in19({32{1'b0}}),
    .in20({32{1'b0}}), .in21({32{1'b0}}), .in22({32{1'b0}}), .in23({32{1'b0}}), .in24(in_16), .in25(_12),
    .in26(_11), .in27(_10), .in28(in_12), .in29(_8), .in30(_7), .in31(in_9), .out(out_70),
    .sel(bit_extender_1_out));
  Multiplexer #(.select(5), .width(32), .enable("false")) multiplexer_55 (
    .in0({32{1'b0}}), .in1({32{1'b0}}), .in2({32{1'b0}}), .in3({32{1'b0}}), .in4({32{1'b0}}),
    .in5({32{1'b0}}), .in6({32{1'b0}}), .in7({32{1'b0}}), .in8({32{1'b0}}), .in9({32{1'b0}}),
    .in10({32{1'b0}}), .in11({32{1'b0}}), .in12({32{1'b0}}), .in13({32{1'b0}}), .in14({32{1'b0}}),
    .in15({32{1'b0}}), .in16({32{1'b0}}), .in17({32{1'b0}}), .in18({32{1'b0}}), .in19({32{1'b0}}),
    .in20({32{1'b0}}), .in21({32{1'b0}}), .in22({32{1'b0}}), .in23({32{1'b0}}), .in24({32{1'b0}}),
    .in25(in_16), .in26(_12), .in27(_11), .in28(_10), .in29(in_12), .in30(_8), .in31(_7), .out(out_71),
    .sel(bit_extender_1_out));
  Multiplexer #(.select(5), .width(32), .enable("false")) multiplexer_56 (
    .in0({32{1'b0}}), .in1({32{1'b0}}), .in2({32{1'b0}}), .in3({32{1'b0}}), .in4({32{1'b0}}),
    .in5({32{1'b0}}), .in6({32{1'b0}}), .in7({32{1'b0}}), .in8({32{1'b0}}), .in9({32{1'b0}}),
    .in10({32{1'b0}}), .in11({32{1'b0}}), .in12({32{1'b0}}), .in13({32{1'b0}}), .in14({32{1'b0}}),
    .in15({32{1'b0}}), .in16({32{1'b0}}), .in17({32{1'b0}}), .in18({32{1'b0}}), .in19({32{1'b0}}),
    .in20({32{1'b0}}), .in21({32{1'b0}}), .in22({32{1'b0}}), .in23({32{1'b0}}), .in24({32{1'b0}}),
    .in25({32{1'b0}}), .in26(in_16), .in27(_12), .in28(_11), .in29(_10), .in30(in_12), .in31(_8),
    .out(out_72), .sel(bit_extender_1_out));
  Multiplexer #(.select(5), .width(32), .enable("false")) multiplexer_57 (
    .in0({32{1'b0}}), .in1({32{1'b0}}), .in2({32{1'b0}}), .in3({32{1'b0}}), .in4({32{1'b0}}),
    .in5({32{1'b0}}), .in6({32{1'b0}}), .in7({32{1'b0}}), .in8({32{1'b0}}), .in9({32{1'b0}}),
    .in10({32{1'b0}}), .in11({32{1'b0}}), .in12({32{1'b0}}), .in13({32{1'b0}}), .in14({32{1'b0}}),
    .in15({32{1'b0}}), .in16({32{1'b0}}), .in17({32{1'b0}}), .in18({32{1'b0}}), .in19({32{1'b0}}),
    .in20({32{1'b0}}), .in21({32{1'b0}}), .in22({32{1'b0}}), .in23({32{1'b0}}), .in24({32{1'b0}}),
    .in25({32{1'b0}}), .in26({32{1'b0}}), .in27(in_16), .in28(_12), .in29(_11), .in30(_10), .in31(in_12),
    .out(out_73), .sel(bit_extender_1_out));
  Multiplexer #(.select(5), .width(32), .enable("false")) multiplexer_58 (
    .in0({32{1'b0}}), .in1({32{1'b0}}), .in2({32{1'b0}}), .in3({32{1'b0}}), .in4({32{1'b0}}),
    .in5({32{1'b0}}), .in6({32{1'b0}}), .in7({32{1'b0}}), .in8({32{1'b0}}), .in9({32{1'b0}}),
    .in10({32{1'b0}}), .in11({32{1'b0}}), .in12({32{1'b0}}), .in13({32{1'b0}}), .in14({32{1'b0}}),
    .in15({32{1'b0}}), .in16({32{1'b0}}), .in17({32{1'b0}}), .in18({32{1'b0}}), .in19({32{1'b0}}),
    .in20({32{1'b0}}), .in21({32{1'b0}}), .in22({32{1'b0}}), .in23({32{1'b0}}), .in24({32{1'b0}}),
    .in25({32{1'b0}}), .in26({32{1'b0}}), .in27({32{1'b0}}), .in28(in_16), .in29(_12), .in30(_11),
    .in31(_10), .out(out_74), .sel(bit_extender_1_out));
  Multiplexer #(.select(5), .width(32), .enable("false")) multiplexer_59 (
    .in0({32{1'b0}}), .in1({32{1'b0}}), .in2({32{1'b0}}), .in3({32{1'b0}}), .in4({32{1'b0}}),
    .in5({32{1'b0}}), .in6({32{1'b0}}), .in7({32{1'b0}}), .in8({32{1'b0}}), .in9({32{1'b0}}),
    .in10({32{1'b0}}), .in11({32{1'b0}}), .in12({32{1'b0}}), .in13({32{1'b0}}), .in14({32{1'b0}}),
    .in15({32{1'b0}}), .in16({32{1'b0}}), .in17({32{1'b0}}), .in18({32{1'b0}}), .in19({32{1'b0}}),
    .in20({32{1'b0}}), .in21({32{1'b0}}), .in22({32{1'b0}}), .in23({32{1'b0}}), .in24({32{1'b0}}),
    .in25({32{1'b0}}), .in26({32{1'b0}}), .in27({32{1'b0}}), .in28({32{1'b0}}), .in29(in_16), .in30(_12),
    .in31(_11), .out(out_75), .sel(bit_extender_1_out));
  Multiplexer #(.select(5), .width(32), .enable("false")) multiplexer_60 (
    .in0({32{1'b0}}), .in1({32{1'b0}}), .in2({32{1'b0}}), .in3({32{1'b0}}), .in4({32{1'b0}}),
    .in5({32{1'b0}}), .in6({32{1'b0}}), .in7({32{1'b0}}), .in8({32{1'b0}}), .in9({32{1'b0}}),
    .in10({32{1'b0}}), .in11({32{1'b0}}), .in12({32{1'b0}}), .in13({32{1'b0}}), .in14({32{1'b0}}),
    .in15({32{1'b0}}), .in16({32{1'b0}}), .in17({32{1'b0}}), .in18({32{1'b0}}), .in19({32{1'b0}}),
    .in20({32{1'b0}}), .in21({32{1'b0}}), .in22({32{1'b0}}), .in23({32{1'b0}}), .in24({32{1'b0}}),
    .in25({32{1'b0}}), .in26({32{1'b0}}), .in27({32{1'b0}}), .in28({32{1'b0}}), .in29({32{1'b0}}),
    .in30(in_16), .in31(_12), .out(out_76), .sel(bit_extender_1_out));
  Multiplexer #(.select(5), .width(32), .enable("false")) multiplexer_61 (
    .in0({32{1'b0}}), .in1({32{1'b0}}), .in2({32{1'b0}}), .in3({32{1'b0}}), .in4({32{1'b0}}),
    .in5({32{1'b0}}), .in6({32{1'b0}}), .in7({32{1'b0}}), .in8({32{1'b0}}), .in9({32{1'b0}}),
    .in10({32{1'b0}}), .in11({32{1'b0}}), .in12({32{1'b0}}), .in13({32{1'b0}}), .in14({32{1'b0}}),
    .in15({32{1'b0}}), .in16({32{1'b0}}), .in17({32{1'b0}}), .in18({32{1'b0}}), .in19({32{1'b0}}),
    .in20({32{1'b0}}), .in21({32{1'b0}}), .in22({32{1'b0}}), .in23({32{1'b0}}), .in24({32{1'b0}}),
    .in25({32{1'b0}}), .in26({32{1'b0}}), .in27({32{1'b0}}), .in28({32{1'b0}}), .in29({32{1'b0}}),
    .in30({32{1'b0}}), .in31(in_16), .out(out_77), .sel(bit_extender_1_out));
  Multiplexer #(.select(5), .width(32), .enable("false")) multiplexer_62 (
    .in0({32{1'b0}}), .in1({32{1'b0}}), .in2({32{1'b0}}), .in3({32{1'b0}}), .in4({32{1'b0}}),
    .in5({32{1'b0}}), .in6({32{1'b0}}), .in7({32{1'b0}}), .in8({32{1'b0}}), .in9({32{1'b0}}),
    .in10({32{1'b0}}), .in11({32{1'b0}}), .in12({32{1'b0}}), .in13({32{1'b0}}), .in14({32{1'b0}}),
    .in15({32{1'b0}}), .in16({32{1'b0}}), .in17({32{1'b0}}), .in18({32{1'b0}}), .in19({32{1'b0}}),
    .in20({32{1'b0}}), .in21({32{1'b0}}), .in22({32{1'b0}}), .in23({32{1'b0}}), .in24({32{1'b0}}),
    .in25({32{1'b0}}), .in26({32{1'b0}}), .in27({32{1'b0}}), .in28({32{1'b0}}), .in29({32{1'b0}}),
    .in30({32{1'b0}}), .in31({32{1'b0}}), .out(out_78), .sel(bit_extender_1_out));
  Multiplexer #(.select(5), .width(32), .enable("false")) multiplexer_63 (
    .in0({32{1'b0}}), .in1({32{1'b0}}), .in2({32{1'b0}}), .in3({32{1'b0}}), .in4({32{1'b0}}),
    .in5({32{1'b0}}), .in6({32{1'b0}}), .in7({32{1'b0}}), .in8({32{1'b0}}), .in9({32{1'b0}}),
    .in10({32{1'b0}}), .in11({32{1'b0}}), .in12({32{1'b0}}), .in13({32{1'b0}}), .in14({32{1'b0}}),
    .in15({32{1'b0}}), .in16({32{1'b0}}), .in17({32{1'b0}}), .in18({32{1'b0}}), .in19({32{1'b0}}),
    .in20({32{1'b0}}), .in21({32{1'b0}}), .in22({32{1'b0}}), .in23({32{1'b0}}), .in24({32{1'b0}}),
    .in25({32{1'b0}}), .in26({32{1'b0}}), .in27({32{1'b0}}), .in28({32{1'b0}}), .in29({32{1'b0}}),
    .in30({32{1'b0}}), .in31({32{1'b0}}), .out(out_79), .sel(bit_extender_1_out));
  Multiplexer #(.select(5), .width(32), .enable("false")) multiplexer_64 (
    .in0({32{1'b0}}), .in1({32{1'b0}}), .in2({32{1'b0}}), .in3({32{1'b0}}), .in4({32{1'b0}}),
    .in5({32{1'b0}}), .in6({32{1'b0}}), .in7({32{1'b0}}), .in8({32{1'b0}}), .in9({32{1'b0}}),
    .in10({32{1'b0}}), .in11({32{1'b0}}), .in12({32{1'b0}}), .in13({32{1'b0}}), .in14({32{1'b0}}),
    .in15({32{1'b0}}), .in16({32{1'b0}}), .in17({32{1'b0}}), .in18({32{1'b0}}), .in19({32{1'b0}}),
    .in20({32{1'b0}}), .in21({32{1'b0}}), .in22({32{1'b0}}), .in23({32{1'b0}}), .in24({32{1'b0}}),
    .in25({32{1'b0}}), .in26({32{1'b0}}), .in27({32{1'b0}}), .in28({32{1'b0}}), .in29({32{1'b0}}),
    .in30({32{1'b0}}), .in31({32{1'b0}}), .out(out_80), .sel(bit_extender_1_out));
  Comparator #(.width(6)) comparator_2 (.a(6'b011111), .b(counter_2_q), .gt(sos));  // open: eq, lt
  Comparator #(.width(6)) comparator_3 (.a(counter_2_q), .b(6'b001101), .eq(comparator_3_eq));  // open: gt, lt
  Counter #(.width(6), .max('h3f)) counter_2 (
    .load(in_3), .Q(counter_2_q), .clk(and_5_out), .clr(in_5));  // open: D, count, carry
  Comparator #(.width(6)) comparator_4 (.a(counter_2_q), .b(6'b001110), .eq(s));  // open: gt, lt
  or or_4 (or_4_out, comparator_5_lt, and_7_out);
  and and_7 (and_7_out, in_3, and_8_out, comparator_5_eq);
  Comparator #(.width(7)) comparator_5 (
    .a(counter_1_q), .b(7'b0100000), .eq(comparator_5_eq), .lt(comparator_5_lt));  // open: gt
  Comparator #(.width(7)) comparator_6 (.a(counter_1_q), .b(7'b0010011), .eq(comparator_6_eq));  // open: gt, lt
  Comparator #(.width(7)) comparator_7 (.a(counter_1_q), .b(7'b0010010), .eq(comparator_7_eq));  // open: gt, lt
  and and_8 (and_8_out, comparator_3_eq, in_3);
  Register #(.width(1)) register_2 (
    .D(comparator_6_eq), .Q(register_2_q), .clk(comparator_6_eq), .clr(or_5_out));  // open: en
  or or_5 (or_5_out, and_9_out, in_5);
  and and_9 (and_9_out, comparator_7_eq, in_3);
  Multiplexer #(.width(32), .enable("false")) multiplexer_65 (
    .in0(multiplexer_32_out), .in1(in_1), .out(out_48), .sel(s));
  DotMatrix #(.matrixcols(32), .matrixrows(32)) dotmatrix_1 (
    .col0(out_17), .col1(out_18), .col2(out_19), .col3(out_20), .col4(out_21), .col5(out_22), .col6(out_23),
    .col7(out_24), .col8(out_25), .col9(out_26), .col10(out_27), .col11(out_28), .col12(out_29),
    .col13(out_30), .col14(out_31), .col15(out_32), .col16(out_33), .col17(out_34), .col18(out_35),
    .col19(out_36), .col20(out_37), .col21(out_38), .col22(out_39), .col23(out_40), .col24(out_41),
    .col25(out_42), .col26(out_43), .col27(out_44), .col28(out_45), .col29(out_46), .col30(out_47),
    .col31(out_48));
  DotMatrix #(.matrixcols(32), .matrixrows(32)) dotmatrix_2 (
    .col0(out_49), .col1(out_50), .col2(out_51), .col3(out_52), .col4(out_53), .col5(out_54), .col6(out_55),
    .col7(out_56), .col8(out_57), .col9(out_58), .col10(out_59), .col11(out_60), .col12(out_61),
    .col13(out_62), .col14(out_63), .col15(out_64), .col16(out_65), .col17(out_66), .col18(out_67),
    .col19(out_68), .col20(out_69), .col21(out_70), .col22(out_71), .col23(out_72), .col24(out_73),
    .col25(out_74), .col26(out_75), .col27(out_76), .col28(out_77), .col29(out_78), .col30(out_79),
    .col31(out_80));

  // Other names for the same wires on the sheet: a1[31:0] = in_1; a2[31:0] = _2; a3[31:0] = in_4; a4[31:0] = _4;
  //   a5[31:0] = _5; a6[31:0] = in_9; a7[31:0] = _7; a8[31:0] = _8; a9[31:0] = in_12; a10[31:0] = _10;
  //   a11[31:0] = _11; a12[31:0] = _12; a13[31:0] = in_16; niiio = in_3; r = in_5

  // Notes on the sheet:
  //   1
  //   3
  //   6
  //   9
  //   13
endmodule

module ss (
  input  in_1,
  input  [6:0] in_2,
  output out_3,
  output out_4,
  output out_5,
  output out_6
);

  wire and_2_out, and_3_out, and_4_out, and_6_out, and_7_out, and_8_out, not_1_out, not_2_out, not_3_out,
       not_4_out, not_5_out, not_6_out, not_7_out, not_8_out, not_9_out, not_10_out, not_11_out;

  or or_1 (out_3, out_5, and_3_out);
  and and_1 (out_5, and_2_out, in_1);
  and and_2 (and_2_out, in_2[6], in_2[5], not_1_out, not_3_out, not_2_out, not_4_out, in_2[0]);
  not not_1 (not_1_out, in_2[4]);
  not not_2 (not_2_out, in_2[2]);
  not not_3 (not_3_out, in_2[3]);
  not not_4 (not_4_out, in_2[1]);
  and and_3 (and_3_out, in_1, and_4_out);
  and and_4 (and_4_out, in_2[6], in_2[5], not_8_out, not_5_out, in_2[2], not_6_out, not_7_out);
  not not_5 (not_5_out, in_2[3]);
  not not_6 (not_6_out, in_2[1]);
  not not_7 (not_7_out, in_2[0]);
  not not_8 (not_8_out, in_2[4]);
  and and_5 (out_6, and_6_out, in_1);
  and and_6 (and_6_out, in_2[6], in_2[5], in_2[4], not_10_out, not_9_out, in_2[1], in_2[0]);
  not not_9 (not_9_out, in_2[2]);
  not not_10 (not_10_out, in_2[3]);
  or or_2 (out_4, out_6, and_7_out);
  and and_7 (and_7_out, in_1, and_8_out);
  and and_8 (and_8_out, in_2[6], in_2[5], in_2[4], not_11_out, in_2[2], in_2[1], in_2[0]);
  not not_11 (not_11_out, in_2[3]);

  // Other names for the same wires on the sheet: _1 = in_1; _7[6:0] = in_2
endmodule

module mox (
  input  [1:0] in_1,
  input  [1:0] in_2,
  output out_3,
  output out_4,
  output out_5,
  output out_6
);

  wire and_2_out, and_3_out, and_4_out, not_1_out, not_2_out;

  and and_1 (out_4, not_1_out, in_1[0]);
  not not_1 (not_1_out, in_1[1]);
  not not_2 (not_2_out, in_2[1]);
  and and_2 (and_2_out, in_2[0], in_2[1]);
  and and_3 (and_3_out, in_2[0], not_2_out);
  or or_1 (out_6, and_3_out, and_2_out);
  or or_2 (out_3, out_4, and_4_out);
  and and_4 (and_4_out, in_1[1], in_1[0]);
  and and_5 (out_5, in_2[1], in_2[0]);
endmodule

module neo (
  input  in_1,
  input  in_2,
  input  in_3,
  input  [31:0] in_4,
  input  [31:0] in_5,
  input  [31:0] in_6,
  input  [31:0] in_7,
  input  [31:0] in_8,
  input  [31:0] in_9,
  input  [31:0] in_10,
  input  [31:0] in_11,
  input  [31:0] in_12,
  input  [31:0] in_13,
  input  [31:0] in_14,
  input  [31:0] in_15,
  input  [31:0] in_16,
  input  [31:0] in_17,
  input  [31:0] in_18,
  input  [31:0] in_19,
  input  [31:0] in_20,
  input  [31:0] in_21,
  input  [31:0] in_22,
  input  [31:0] in_23,
  input  [31:0] in_24,
  input  [31:0] in_25,
  input  [31:0] in_26,
  input  [31:0] in_27,
  input  [31:0] in_28,
  input  [31:0] in_29,
  output [31:0] out_30,
  output [31:0] out_31,
  output [31:0] out_32,
  output [31:0] out_33,
  output [31:0] out_34,
  output [31:0] out_35,
  output [31:0] out_36,
  output [31:0] out_37,
  output [31:0] out_38,
  output [31:0] out_39,
  output [31:0] out_40,
  output [31:0] out_41,
  output [31:0] out_42,
  output [31:0] out_43,
  output [31:0] out_44,
  output [31:0] out_45,
  output [31:0] out_46,
  output [31:0] out_47,
  output [31:0] out_48,
  output [31:0] out_49,
  output [31:0] out_50,
  output [31:0] out_51,
  output [31:0] out_52,
  output [31:0] out_53,
  output [31:0] out_54,
  output [31:0] out_55,
  output [31:0] out_56,
  output [31:0] out_57,
  output [31:0] out_58,
  output [31:0] out_59,
  output [31:0] out_60,
  output [31:0] out_61,
  output [31:0] out_62,
  output [31:0] out_63,
  output [31:0] out_64,
  output [31:0] out_65,
  output [31:0] out_66,
  output [31:0] out_67,
  output [31:0] out_68,
  output [31:0] out_69,
  output [31:0] out_70,
  output [31:0] out_71,
  output [31:0] out_72,
  output [31:0] out_73,
  output [31:0] out_74,
  output [31:0] out_75,
  output [31:0] out_76,
  output [31:0] out_77,
  output [31:0] out_78,
  output [31:0] out_79,
  output [31:0] out_80,
  output [31:0] out_81,
  output [31:0] out_82,
  output [31:0] out_83,
  output [31:0] out_84,
  output [31:0] out_85,
  output [31:0] out_86,
  output [31:0] out_87,
  output [31:0] out_88,
  output [31:0] out_89,
  output [31:0] out_90,
  output [31:0] out_91,
  output [31:0] out_92,
  output [31:0] out_93,
  output [31:0] out_94,
  output [31:0] out_95,
  output [31:0] out_96,
  output [31:0] out_97,
  output [31:0] out_98,
  output [31:0] out_99,
  output [31:0] out_100,
  output [31:0] out_101,
  output [31:0] out_102,
  output [31:0] out_103,
  output [31:0] out_104,
  output [31:0] out_105,
  output [31:0] out_106,
  output [31:0] out_107,
  output [31:0] out_108,
  output [31:0] out_109,
  output [31:0] out_110,
  output [31:0] out_111,
  output [31:0] out_112,
  output [31:0] out_113,
  output [31:0] out_114,
  output [31:0] out_115,
  output [31:0] out_116,
  output [31:0] out_117,
  output [31:0] out_118,
  output [31:0] out_119,
  output [31:0] out_120,
  output [31:0] out_121,
  output [31:0] out_122,
  output [31:0] out_123,
  output [31:0] out_124,
  output [31:0] out_125,
  output [31:0] out_126,
  output [31:0] out_127,
  output [31:0] out_128,
  output [31:0] out_129,
  output [31:0] out_130,
  output [31:0] out_131,
  output [31:0] out_132,
  output [31:0] out_133,
  output [31:0] out_134,
  output [31:0] out_135,
  output [31:0] out_136,
  output [31:0] out_137,
  output [31:0] out_138,
  output [31:0] out_139,
  output [31:0] out_140,
  output [31:0] out_141,
  output [31:0] out_142,
  output [31:0] out_143,
  output [31:0] out_144,
  output [31:0] out_145,
  output [31:0] out_146,
  output [31:0] out_147,
  output [31:0] out_148,
  output [31:0] out_149,
  output [31:0] out_150,
  output [31:0] out_151,
  output [31:0] out_152,
  output [31:0] out_153,
  output [31:0] out_154,
  output [31:0] out_155,
  output [31:0] out_156,
  output [31:0] out_157
);

  \δεξια_αριστερα  \u_δεξια_αριστερα_1  (
    .in_3(in_1), .in_1(in_4), ._2(in_5), .in_4(in_6), ._4(in_7), ._5(in_8), .in_9(in_9), ._7(in_10),
    ._8(in_11), .in_12(in_12), ._10(in_13), ._11(in_14), ._12(in_15), .in_16(in_16), .out_17(out_93),
    .out_18(out_92), .out_19(out_91), .out_20(out_90), .out_21(out_89), .out_22(out_88), .out_23(out_87),
    .out_24(out_86), .out_25(out_85), .out_26(out_84), .out_27(out_83), .out_28(out_82), .out_29(out_81),
    .out_30(out_80), .out_31(out_79), .out_32(out_78), .out_33(out_77), .out_34(out_76), .out_35(out_75),
    .out_36(out_74), .out_37(out_73), .out_38(out_72), .out_39(out_71), .out_40(out_70), .out_41(out_69),
    .out_42(out_68), .out_43(out_67), .out_44(out_66), .out_45(out_65), .out_46(out_64), .out_47(out_63),
    .out_48(out_62), .in_8(in_2), .in_5(in_3), .out_49(out_61), .out_50(out_60), .out_51(out_59),
    .out_52(out_58), .out_53(out_57), .out_54(out_56), .out_55(out_55), .out_56(out_54), .out_57(out_53),
    .out_58(out_52), .out_59(out_51), .out_60(out_50), .out_61(out_49), .out_62(out_48), .out_63(out_47),
    .out_64(out_46), .out_65(out_45), .out_66(out_44), .out_67(out_43), .out_68(out_42), .out_69(out_41),
    .out_70(out_40), .out_71(out_39), .out_72(out_38), .out_73(out_37), .out_74(out_36), .out_75(out_35),
    .out_76(out_34), .out_77(out_33), .out_78(out_32), .out_79(out_31), .out_80(out_30));
  \δεξια_αριστερα  \u_δεξια_αριστερα_2  (
    .in_3(in_1), .in_1(in_17), ._2(in_18), .in_4(in_19), ._4(in_20), ._5(in_21), .in_9(in_22), ._7(in_23),
    ._8(in_24), .in_12(in_25), ._10(in_26), ._11(in_27), ._12(in_28), .in_16(in_29), .out_17(out_157),
    .out_18(out_156), .out_19(out_155), .out_20(out_154), .out_21(out_153), .out_22(out_152),
    .out_23(out_151), .out_24(out_150), .out_25(out_149), .out_26(out_148), .out_27(out_147),
    .out_28(out_146), .out_29(out_145), .out_30(out_144), .out_31(out_143), .out_32(out_142),
    .out_33(out_141), .out_34(out_140), .out_35(out_139), .out_36(out_138), .out_37(out_137),
    .out_38(out_136), .out_39(out_135), .out_40(out_134), .out_41(out_133), .out_42(out_132),
    .out_43(out_131), .out_44(out_130), .out_45(out_129), .out_46(out_128), .out_47(out_127),
    .out_48(out_126), .in_8(in_2), .in_5(in_3), .out_49(out_125), .out_50(out_124), .out_51(out_123),
    .out_52(out_122), .out_53(out_121), .out_54(out_120), .out_55(out_119), .out_56(out_118),
    .out_57(out_117), .out_58(out_116), .out_59(out_115), .out_60(out_114), .out_61(out_113),
    .out_62(out_112), .out_63(out_111), .out_64(out_110), .out_65(out_109), .out_66(out_108),
    .out_67(out_107), .out_68(out_106), .out_69(out_105), .out_70(out_104), .out_71(out_103),
    .out_72(out_102), .out_73(out_101), .out_74(out_100), .out_75(out_99), .out_76(out_98), .out_77(out_97),
    .out_78(out_96), .out_79(out_95), .out_80(out_94));

  // Other names for the same wires on the sheet: _1 = in_1; _2 = in_2; _3 = in_3
endmodule

module bol (
  input  in_1,
  input  in_2,
  input  in_3,
  input  in_4,
  input  reset,
  input  set,
  output [7:0] out_7,
  output [7:0] out_8
);

  wire and_1_out, and_3_out, comparator_1_eq, comparator_2_eq, comparator_3_eq, comparator_4_eq,
       multiplexer_1_out, or_3_out, or_4_out, or_5_out, or_6_out, register_1_q, \sos_Χ , \sos_Χ1 , \sos_Ψ ,
       \sos_Ψ1 , \Χ_minus , \Χ_plus , \Ψ_minus , \Ψ_plus ;

  and and_1 (and_1_out, in_1, \sos_Χ1 );
  and and_2 (\Χ_minus , in_2, \sos_Χ );
  or or_1 (\Χ_plus , and_1_out, \Χ_minus );
  Register #(.width(1)) register_1 (.D(set), .Q(register_1_q), .clk(set), .clr(reset));  // open: en
  and and_3 (and_3_out, in_3, \sos_Ψ1 );
  Multiplexer #(.enable("false")) multiplexer_1 (.in0(1'b0), .in1(1'b1), .out(multiplexer_1_out), .sel(register_1_q));
  and and_4 (\Ψ_minus , in_4, \sos_Ψ );
  or or_2 (\Ψ_plus , and_3_out, \Ψ_minus );
  or or_3 (or_3_out, \Χ_minus , set);
  Counter counter_1 (
    .load(or_3_out), .D(8'hc), .count(multiplexer_1_out), .Q(out_7), .clk(or_4_out), .clr(reset));  // open: carry
  or or_4 (or_4_out, set, \Χ_plus );
  or or_5 (or_5_out, \Ψ_minus , set);
  Counter counter_2 (
    .load(or_5_out), .D(8'h7), .count(multiplexer_1_out), .Q(out_8), .clk(or_6_out), .clr(reset));  // open: carry
  or or_6 (or_6_out, set, \Ψ_plus );
  Comparator comparator_1 (.a(out_7), .b(8'hc), .eq(comparator_1_eq));  // open: gt, lt
  not not_1 (\sos_Χ , comparator_1_eq);
  Comparator comparator_2 (.a(out_8), .b(8'h7), .eq(comparator_2_eq));  // open: gt, lt
  not not_2 (\sos_Ψ , comparator_2_eq);
  Comparator comparator_3 (.a(out_8), .b(8'h3d), .eq(comparator_3_eq));  // open: gt, lt
  Comparator comparator_4 (.a(out_7), .b(8'h3c), .eq(comparator_4_eq));  // open: gt, lt
  not not_3 (\sos_Χ1 , comparator_4_eq);
  not not_4 (\sos_Ψ1 , comparator_3_eq);
endmodule
