// Logisim project η.circ as structural Verilog: 1 circuit, main circuit main
module main (
);

  wire and_1_out, and_2_out, and_3_out, and_4_out, and_5_out, and_6_out, and_7_out, and_8_out, nor_1_out,
       nor_2_out, nor_3_out, nor_4_out, nor_5_out, nor_6_out, nor_7_out, nor_8_out, not_1_out, not_2_out,
       not_3_out, not_4_out, not_5_out, not_6_out, not_7_out, not_8_out, not_9_out, not_10_out, not_11_out,
       not_12_out, or_1_out, or_2_out, or_3_out, or_4_out, or_5_out, or_6_out, or_7_out, or_8_out, undriven,
       undriven_2, undriven_3, undriven_4, undriven_5, undriven_6, undriven_7, undriven_8, undriven_9,
       undriven_10, undriven_11, undriven_12, undriven_13, undriven_14, undriven_15, undriven_16,
       undriven_17, undriven_18, undriven_19, undriven_20, undriven_21, undriven_22, undriven_23,
       undriven_24, undriven_25, undriven_26, undriven_27, undriven_28, undriven_29, undriven_30,
       undriven_31, undriven_32, undriven_33, undriven_34, undriven_35, undriven_36, undriven_37,
       undriven_38, undriven_39, undriven_40, undriven_41, undriven_42, undriven_43, undriven_44,
       undriven_45, undriven_46, undriven_47, undriven_48, undriven_49, undriven_50, undriven_51,
       undriven_52, undriven_53, undriven_54, undriven_55, undriven_56, undriven_57, undriven_58,
       undriven_59, undriven_60, undriven_61, undriven_62, undriven_63, undriven_64, undriven_65,
       undriven_66, undriven_67, undriven_68, undriven_69, undriven_70, undriven_71, undriven_72,
       undriven_73, undriven_74, undriven_75, undriven_76, xor_1_out, xor_2_out, xor_3_out, xor_4_out,
       xor_5_out, xor_6_out, xor_7_out, xor_8_out;

  and and_1 (and_1_out, undriven_11, undriven_7);
  and and_2 (and_2_out, undriven, undriven_5);
  xor xor_1 (xor_1_out, undriven_10, undriven_8);
  xor xor_2 (xor_2_out, undriven_2, undriven_4);
  nor nor_1 (nor_1_out, undriven_12, undriven_9);
  nor nor_2 (nor_2_out, undriven_3, undriven_6);
  and and_3 (and_3_out, undriven_22, undriven_19);
  and and_4 (and_4_out, undriven_13, undriven_17);
  xor xor_3 (xor_3_out, undriven_24, undriven_20);
  xor xor_4 (xor_4_out, undriven_14, undriven_16);
  nor nor_3 (nor_3_out, undriven_23, undriven_21);
  nor nor_4 (nor_4_out, undriven_15, undriven_18);
  or or_1 (or_1_out, undriven_26, undriven_27);
  not not_1 (not_1_out, undriven_28);
  not not_2 (not_2_out, undriven_25);
  or or_2 (or_2_out, undriven_30, undriven_29);
  not not_3 (not_3_out, undriven_32);
  not not_4 (not_4_out, undriven_31);
  or or_3 (or_3_out, undriven_33, undriven_34);
  not not_5 (not_5_out, undriven_35);
  or or_4 (or_4_out, undriven_37, undriven_36);
  not not_6 (not_6_out, undriven_38);
  and and_5 (and_5_out, undriven_48, undriven_45);
  and and_6 (and_6_out, undriven_39, undriven_42);
  xor xor_5 (xor_5_out, undriven_49, undriven_46);
  xor xor_6 (xor_6_out, undriven_40, undriven_43);
  nor nor_5 (nor_5_out, undriven_50, undriven_47);
  nor nor_6 (nor_6_out, undriven_41, undriven_44);
  and and_7 (and_7_out, undriven_51, undriven_54);
  xor xor_7 (xor_7_out, undriven_52, undriven_55);
  nor nor_7 (nor_7_out, undriven_53, undriven_56);
  and and_8 (and_8_out, undriven_60, undriven_57);
  xor xor_8 (xor_8_out, undriven_61, undriven_58);
  nor nor_8 (nor_8_out, undriven_62, undriven_59);
  not not_7 (not_7_out, undriven_64);
  or or_5 (or_5_out, undriven_68, undriven_66);
  or or_6 (or_6_out, undriven_63, undriven_65);
  not not_8 (not_8_out, undriven_67);
  not not_9 (not_9_out, undriven_69);
  or or_7 (or_7_out, undriven_70, undriven_72);
  not not_10 (not_10_out, undriven_71);
  not not_11 (not_11_out, undriven_74);
  or or_8 (or_8_out, undriven_75, undriven_73);
  not not_12 (not_12_out, undriven_76);
endmodule
